// Logisim project lab-CCAB.circ as structural Verilog: 25 circuits, main circuit 分支预测
module \单周期RISC_V  (
  input  IR1,
  input  IR2,
  input  IR3,
  output RegWrite,
  output MemWrite,
  output [31:0] PC,
  output [31:0] IR,
  output [31:0] RDin,
  output [31:0] MDin,
  output [31:0] LedData
);

  wire ALUSrc, and_1_out, and_2_out, and_3_out, and_4_out, B, Beq, Blt, Bne, CLK, clock_1_out,
       comparator_1_eq, comparator_2_eq, comparator_2_lt, d_ff_1_q, ecall, eq, Go, halt, IR1_t, IR2_t, IR3_t,
       IRA, IRB, IRC, JAL, JALR, less, lui, MemToReg, nand_1_out, not_1_out, not_2_out, not_3_out, not_4_out,
       not_5_out, or_2_out, RST, sb, srl, uret, W1, W2, W3, \单周期硬布线控制器_1_s_type ;
  wire [3:0] ALUop;
  wire [4:0] bit_extender_5_out, multiplexer_5_out, multiplexer_7_out, shifter_3_out;
  wire [11:0] multiplexer_6_out;
  wire [12:0] CNT_num;
  wire [15:0] \分支成功数 , \总周期数 ;
  wire [31:0] adder_4_out, ALUresult, and_6_out, bit_extender_2_out, bit_extender_3_out, bit_extender_4_out,
       BJ, DJ, imm12, MDout, multiplexer_1_out, multiplexer_2_out, multiplexer_3_out, multiplexer_8_out,
       multiplexer_9_out, multiplexer_10_out, PC_4, R1, R2, shifter_1_out, shifter_2_out, shifter_4_out;

  Button u_rst (.out(RST));
  Button _1 (.out(IRA));
  Button _2 (.out(IRB));
  Button _3 (.out(IRC));
  Button \u_继续运行  (.out(Go));
  LED #(.active("true")) led_1 (.in(W1));
  LED #(.active("true")) led_2 (.in(W2));
  LED #(.active("true")) led_3 (.in(W3));
  // Probe on \分支成功数 
  Hex_Digit_Display hex_digit_display_1 (.value(LedData[31:28]));  // open: dp
  not not_1 (not_1_out, halt);
  and and_1 (and_1_out, Beq, eq);
  and and_2 (and_2_out, Bne, not_2_out);
  not not_2 (not_2_out, eq);
  and and_3 (and_3_out, less, Blt);
  Hex_Digit_Display hex_digit_display_2 (.value(LedData[27:24]));  // open: dp
  Hex_Digit_Display hex_digit_display_3 (.value(LedData[23:20]));  // open: dp
  Counter #(.width(16), .max('hffff), .ongoal("wrap"), .trigger("rising"), .behavior("new")) counter_1 (
    .count(not_1_out), .Q(\总周期数 ), .clk(CLK), .clr(RST));  // open: load, D, carry, preset, down
  Multiplexer #(.select(3), .width(32), .disabled("Z"), .enable("false")) multiplexer_1 (
    .in0(PC_4), .in1(BJ), .in2(ALUresult), .in3({32{1'b0}}), .in4(DJ), .in5({32{1'b0}}), .in6({32{1'b0}}),
    .in7({32{1'b0}}), .out(multiplexer_1_out), .sel({JAL, JALR, B}));
  not not_3 (not_3_out, halt);
  or or_1 (B, and_1_out, and_2_out, and_3_out);
  and and_4 (and_4_out, ecall, comparator_1_eq);
  Comparator #(.width(32), .mode("twosComplement")) comparator_1 (
    .a(R1), .b(32'h22), .eq(comparator_1_eq));  // open: gt, lt
  not not_4 (not_4_out, comparator_1_eq);
  not not_5 (not_5_out, Go);
  or or_2 (or_2_out, JALR, JAL);
  Multiplexer #(.select(1), .width(32), .disabled("Z"), .enable("false")) multiplexer_2 (
    .in0(ALUresult), .in1(MDout), .out(multiplexer_2_out), .sel(MemToReg));
  Multiplexer #(.select(1), .width(32), .disabled("Z"), .enable("false")) multiplexer_3 (
    .in0(multiplexer_2_out), .in1(PC_4), .out(multiplexer_3_out), .sel(or_2_out));
  Hex_Digit_Display hex_digit_display_4 (.value(LedData[19:16]));  // open: dp
  Hex_Digit_Display hex_digit_display_5 (.value(LedData[15:12]));  // open: dp
  Register #(.width(32), .trigger("rising"), .Select("low")) u_PC (
    .D(multiplexer_1_out), .en(not_3_out), .Q(PC), .clk(CLK), .clr(RST));
  Counter #(.width(16), .max('hffff), .ongoal("wrap"), .trigger("rising"), .behavior("new")) counter_2 (
    .count(B), .Q(\分支成功数 ), .clk(CLK), .clr(RST));  // open: load, D, carry, preset, down
  Register #(.width(32), .trigger("rising"), .Select("low")) register_1 (
    .D(R2), .en(and_4_out), .Q(LedData), .clk(CLK));  // open: clr
  and and_5 (halt, not_4_out, ecall, not_5_out);
  Multiplexer #(.select(1), .width(32), .disabled("Z"), .enable("false")) multiplexer_4 (
    .in0(multiplexer_3_out), .in1({IR[31:12], {12{1'b0}}}), .out(RDin), .sel(lui));
  Hex_Digit_Display hex_digit_display_6 (.value(LedData[11:8]));  // open: dp
  Hex_Digit_Display hex_digit_display_7 (.value(LedData[7:4]));  // open: dp
  // Probe on \总周期数 
  Adder #(.width(32)) adder_1 (.a(PC), .b(32'h4), .out(PC_4));  // open: cin, cout
  Hex_Digit_Display hex_digit_display_8 (.value(LedData[3:0]));  // open: dp
  // RiscV_Probe riscv_probe_1: pin names not known; wires that end beside it: IR, IR[21], IR[6:2]
  ROM #(.addrWidth(10), .dataWidth(32), .Select("high")) rom_1 (.addr(PC[11:2]), .data(IR));
  or or_3 (IR1_t, IR1, IRA);
  \单周期硬布线控制器  \u_单周期硬布线控制器_1  (
    .Funct({IR[30], IR[25], IR[14:12]}), .OP(IR[6:2]), .ALU_OP(ALUop), .MemToReg(MemToReg),
    .MemWrite(MemWrite), .ALU_SRC(ALUSrc), .RegWrite(RegWrite), .ecall(ecall), .S_type(\单周期硬布线控制器_1_s_type ),
    .Jalr(JALR), .Beq(Beq), .JAL(JAL), .Bne(Bne), .in_3(IR[21]), .uret(uret), .sb(sb), .lui(lui), .srl(srl),
    .blt(Blt));  // open: CSRRSI, CSRRCI
  Multiplexer #(.select(1), .width(5), .disabled("Z"), .enable("false")) multiplexer_5 (
    .in0(IR[24:20]), .in1(5'b01010), .out(multiplexer_5_out), .sel(ecall));
  Multiplexer #(.select(1), .width(12), .disabled("Z"), .enable("false")) multiplexer_6 (
    .in0(IR[31:20]), .in1({IR[31:25], IR[11:7]}), .out(multiplexer_6_out), .sel(\单周期硬布线控制器_1_s_type ));
  or or_4 (IR2_t, IR2, IRB);
  Multiplexer #(.select(1), .width(5), .disabled("Z"), .enable("false")) multiplexer_7 (
    .in0(IR[19:15]), .in1(5'b10001), .out(multiplexer_7_out), .sel(ecall));
  assign imm12 = {{20{multiplexer_6_out[11]}}, multiplexer_6_out};  // Bit_Extender bit_extender_1
  assign bit_extender_2_out = {{20{IR[31]}}, {IR[31], IR[7], IR[30:25], IR[11:8]}};  // Bit_Extender bit_extender_2
  assign bit_extender_3_out = {{12{IR[31]}}, {IR[31], IR[19:12], IR[20], IR[30:21]}};  // Bit_Extender bit_extender_3
  Shifter #(.width(32), .shift("ll")) shifter_1 (.in(bit_extender_2_out), .\dist (5'b00001), .out(shifter_1_out));
  Shifter #(.width(32), .shift("ll")) shifter_2 (.in(bit_extender_3_out), .\dist (5'b00001), .out(shifter_2_out));
  or or_5 (IR3_t, IR3, IRC);
  Regifile regifile_1 (
    .Din(RDin), .Clk(CLK), .R1(R1), .R2(R2), .WE(RegWrite), .W_num(IR[11:7]), .R1_num(multiplexer_7_out),
    .R2_num(multiplexer_5_out));
  Adder #(.width(32)) adder_2 (.a(shifter_1_out), .b(PC), .out(BJ));  // open: cin, cout
  Adder #(.width(32)) adder_3 (.a(shifter_2_out), .b(PC), .out(DJ));  // open: cin, cout
  Multiplexer #(.select(1), .width(32), .disabled("Z"), .enable("false")) multiplexer_8 (
    .in0(R2), .in1(imm12), .out(multiplexer_8_out), .sel(ALUSrc));
  assign bit_extender_4_out = {{27{R2[4]}}, R2[4:0]};  // Bit_Extender bit_extender_4
  assign bit_extender_5_out = {{3{1'b0}}, ALUresult[1:0]};  // Bit_Extender bit_extender_5
  Multiplexer #(.select(1), .width(32), .disabled("Z"), .enable("false")) multiplexer_9 (
    .in0(multiplexer_8_out), .in1(bit_extender_4_out), .out(multiplexer_9_out), .sel(srl));
  Multiplexer #(.select(2), .width(32), .disabled("Z"), .enable("false")) multiplexer_10 (
    .in0(32'hffffff00), .in1(32'hffff00ff), .in2(32'hff00ffff), .in3(32'hffffff), .out(multiplexer_10_out),
    .sel(ALUresult[1:0]));
  Shifter #(.width(5), .shift("ll")) shifter_3 (.in(bit_extender_5_out), .\dist (3'b011), .out(shifter_3_out));
  ALU alu_1 (
    .X(R1), .Y(multiplexer_9_out), .AluOP(ALUop), .Equal(eq), .Result(ALUresult), .out_6(less));  // open: Result_2, out_4
  assign and_6_out = multiplexer_10_out & MDout;  // AND_Gate and_6, 32 bits wide
  Shifter #(.width(32), .shift("ll")) shifter_4 (.in(R2), .\dist (shifter_3_out), .out(shifter_4_out));
  Adder #(.width(32)) adder_4 (.a(and_6_out), .b(shifter_4_out), .out(adder_4_out));  // open: cin, cout
  Multiplexer #(.select(1), .width(32), .disabled("Z"), .enable("false")) multiplexer_11 (
    .in0(R2), .in1(adder_4_out), .out(MDin), .sel(sb));
  D_Flip_Flop #(.trigger("high"), .Pre_Clr_Positions("LEGACY"), .NegatePresetClear("false"), .enable("true"), .NewFFLayout("false")) d_ff_1 (.Q(d_ff_1_q));  // open: clk, D, Qn, preset, en, reset
  // Probe on 13'hc
  RAM #(.addrWidth(10), .dataWidth(32), .bus("separate"), .Select("high")) ram_1 (
    .addr(ALUresult[11:2]), .din(MDin), .data(MDout), .str(MemWrite), .clk(CLK), .ld(1'b1), .clr(RST));  // open: sel
  Comparator #(.width(13), .mode("twosComplement")) comparator_2 (
    .a(CNT_num), .b(13'hc), .eq(comparator_2_eq), .lt(comparator_2_lt));  // open: gt
  Clock #(.highDuration(1), .lowDuration(1)) clock_1 (.out(clock_1_out));
  Counter #(.width(13), .max('h1fff), .ongoal("stay"), .trigger("rising"), .behavior("old")) counter_3 (
    .count(comparator_2_lt), .Q(CNT_num), .clk(clock_1_out));  // open: load, D, carry, clr, preset
  nand nand_1 (nand_1_out, d_ff_1_q, comparator_2_eq);
  assign CLK = nand_1_out ? clock_1_out : 1'bz;  // Controlled_Buffer controlled_buffer_1
  Pull_Resistor #(.pull(1)) pull_resistor_1 (.node(CLK));

  // Other names for the same wires on the sheet: byte_ad[1:0] = ALUresult[1:0]; lu[31:12] = IR[31:12]

  // Notes on the sheet:
  //   中断源
  //   中断等待指示
  //   数码管输出
  //   指令探针
  //   指令字
  //   contents of rom_1 (hex, n*v repeats v):
  //   100493 100006f 100493 200913 300993 100006f 100493 200913 300993 100006f 100493 200913 300993
  //   100006f 100493 200913 300993 3b8000ef 100413 100493 1f49493 900533 2200893 73 24d493 48463 fedff06f
  //   900533 2200893 73 100493 249493 900533 2200893 73 48463 fedff06f 100493 1f49493 900533 2200893 73
  //   4034d493 900533 2200893 73 4044d493 900533 2200893 73 4044d493 900533 2200893 73 4044d493 900533
  //   2200893 73 4044d493 900533 2200893 73 4044d493 900533 2200893 73 4044d493 900533 2200893 73 4044d493
  //   900533 2200893 73 100413 1f41993 41f9d993 433 c00913 300b13 140413 f47413 800293 100313 499993
  //   89e9b3 1300533 2200893 73 406282b3 fe0294e3 140413 f00f93 1f47433 1c41413 800293 100313 49d993
  //   89e9b3 1300533 2200893 73 406282b3 fe0294e3 1c45413 406b0b33 b0463 f95ff06f 2b3 fff2c293 829293
  //   ff2e293 500533 2200893 73 fff00413 493 84a023 140413 448493 84a023 140413 448493 84a023 140413
  //   448493 84a023 140413 448493 84a023 140413 448493 84a023 140413 448493 84a023 140413 448493 84a023
  //   140413 448493 84a023 140413 448493 84a023 140413 448493 84a023 140413 448493 84a023 140413 448493
  //   84a023 140413 448493 84a023 140413 448493 84a023 140413 448493 84a023 140413 448493 140413 433
  //   3c00493 42983 4aa03 149a2b3 28663 134a023 1442023 ffc48493 fe9412e3 800533 2200893 73 440413 3c00493
  //   fc9416e3 a00893 73 100293 300313 800493 849493 7648493 1449493 900533 2200893 73 800e13 54d4b3
  //   64d4b3 900533 2200893 73 fffe0e13 fe0e14e3 a00893 73 800e13 fedc04b7 fff00413 1045413 84e4b3 900533
  //   2200893 73 ba984b7 900533 73 76544b7 900533 73 32104b7 900533 73 fffe0e13 fa0e1ee3 a00893 73 313
  //   2000e13 493 100913 930023 900533 2200893 73 12484b3 130313 fffe0e13 fe0e12e3 800e13 313 32483 900533
  //   2200893 73 430313 fffe0e13 fe0e14e3 a00893 73 ff100493 900533 2200893 73 148493 fe04c8e3 a00893 73
  //   413 140413 800533 2200893 73 240413 800533 2200893 73 340413 800533 2200893 73 440413 800533 2200893
  //   73 540413 800533 2200893 73 640413 800533 2200893 73 740413 800533 2200893 73 840413 800533 2200893
  //   2200893 73 8067
  //   B_type
  //   U_type
  //   为方便自动评测，需要输出PC，IR，寄存器堆写如数据RDin
  //   RAM写使能MemWrite、RAM写入数据MDin等信号
  //   控制位
  //   暂停节拍，不能为0
  //   戳工具置1进入计数暂停模式，ctrl+k时钟自动运行到对应节拍暂停
  //   ctrl+k关闭时钟连续运行，将控制位置零，进入单步调试模式调试
  //   用这个时钟源需要去掉电路中的其他时钟源
  //   数码管输出应该用寄存器锁存，否则显示数据只能一闪而过
  //   可计数暂停的时钟源
endmodule

module \理想流水线  (
  output RegWrite,
  output MemWrite,
  output [31:0] IF_PC,
  output [31:0] ID_PC,
  output [31:0] EX_PC,
  output [31:0] M_PC,
  output [31:0] WB_PC,
  output [31:0] RDin,
  output [31:0] MDin,
  output [31:0] LedData
);

  wire and_1_out, and_2_out, and_3_out, and_4_out, and_5_out, B, Beq, blt, Bne, CLK, clock_1_out,
       comparator_1_eq, comparator_1_lt, comparator_2_eq, d_ff_1_q, ecall, en, eq, EX_ecall, EX_MEM_halt_2,
       EX_MEM_jal_2, EX_MEM_jalr_2, EX_MEM_memtoreg_2, EX_RegWrite, Go, halt, ID_EX_p26, ID_EX_p33,
       ID_EX_p34, ID_EX_p36, IR1, IR2, IR3, JAL, JALR, lui, MEM_RegWrite, MEM_WB_jal_2, MEM_WB_jalr_2,
       MEM_WB_memtoreg_2, nand_1_out, not_1_out, not_2_out, not_3_out, not_4_out, not_5_out, not_6_out,
       or_2_out, or_3_out, RST, srl, W1, W2, W3, \单周期硬布线控制器_1_alu_src , \单周期硬布线控制器_1_beq , \单周期硬布线控制器_1_blt ,
       \单周期硬布线控制器_1_bne , \单周期硬布线控制器_1_jal , \单周期硬布线控制器_1_jalr , \单周期硬布线控制器_1_lui , \单周期硬布线控制器_1_memtoreg ,
       \单周期硬布线控制器_1_memwrite , \单周期硬布线控制器_1_regwrite , \单周期硬布线控制器_1_s_type , \单周期硬布线控制器_1_sb ,
       \单周期硬布线控制器_1_srl , \单周期硬布线控制器_1_uret ;
  wire [3:0] ID_EX_p35, \单周期硬布线控制器_1_alu_op ;
  wire [4:0] EX_W_num, MEM_W_num, multiplexer_2_out, multiplexer_3_out, WB_W_num;
  wire [11:0] multiplexer_4_out;
  wire [12:0] CNT_num;
  wire [15:0] adder_4_out, \LoadUse次数 , \分支成功数 , \总周期数 , \插入气泡数 , \无条件分支数 , \条件分支成功数 ;
  wire [31:0] adder_5_out, ALUresult, bit_extender_1_out, bit_extender_2_out, bit_extender_3_out,
       bit_extender_4_out, BJ, DJ, EX_IR, EX_MEM_aluresult_2, EX_MEM_lu_2, EX_R1, EX_R2, ID_EX_p46,
       ID_EX_p49, ID_EX_p50, ID_EX_p51, ID_IR, ID_R1, ID_R2, IF_IR, MEM_IR, MEM_WB_aluresult_2, MEM_WB_lu_2,
       MEM_WB_readdata_2, multiplexer_1_out, multiplexer_5_out, multiplexer_6_out, multiplexer_7_out,
       multiplexer_8_out, PC_4, ram_1_data, shifter_1_out, shifter_2_out, WB_IR;

  Button \u_总复位  (.out(RST));
  Button _1 (.out(IR1));
  Button _2 (.out(IR2));
  Button _3 (.out(IR3));
  // Probe on \总周期数 
  // Probe on \总周期数 
  Button \u_继续运行  (.out(Go));
  LED #(.active("true")) led_1 (.in(W1));
  LED #(.active("true")) led_2 (.in(W2));
  LED #(.active("true")) led_3 (.in(W3));
  Hex_Digit_Display hex_digit_display_1 (.value(LedData[31:28]));  // open: dp
  // Probe on IF_PC[19:0]
  // RiscV_Probe riscv_probe_1: pin names not known; wires that end beside it: IF_IR
  Hex_Digit_Display hex_digit_display_2 (.value(LedData[27:24]));  // open: dp
  Hex_Digit_Display hex_digit_display_3 (.value(LedData[23:20]));  // open: dp
  // Probe on ID_PC[19:0]
  // RiscV_Probe riscv_probe_2: pin names not known; wires that end beside it: ID_IR
  Hex_Digit_Display hex_digit_display_4 (.value(LedData[19:16]));  // open: dp
  Hex_Digit_Display hex_digit_display_5 (.value(LedData[15:12]));  // open: dp
  Hex_Digit_Display hex_digit_display_6 (.value(LedData[11:8]));  // open: dp
  Hex_Digit_Display hex_digit_display_7 (.value(LedData[7:4]));  // open: dp
  // Probe on EX_PC[19:0]
  // RiscV_Probe riscv_probe_3: pin names not known; wires that end beside it: EX_IR
  Multiplexer #(.select(3), .width(32), .disabled("Z"), .enable("false")) multiplexer_1 (
    .in0(PC_4), .in1(BJ), .in2(ALUresult), .in3({32{1'b0}}), .in4(DJ), .in5({32{1'b0}}), .in6({32{1'b0}}),
    .in7({32{1'b0}}), .out(multiplexer_1_out), .sel({JAL, JALR, B}));
  Hex_Digit_Display hex_digit_display_8 (.value(LedData[3:0]));  // open: dp
  Register #(.width(32), .trigger("rising"), .Select("low")) PC (
    .D(multiplexer_1_out), .en(en), .Q(IF_PC), .clk(and_1_out), .clr(RST));
  and and_1 (and_1_out, not_1_out, CLK);
  not not_1 (not_1_out, halt);
  // Probe on \总周期数 
  // Probe on M_PC[19:0]
  // RiscV_Probe riscv_probe_4: pin names not known; wires that end beside it: MEM_IR
  // Probe on \总周期数 
  // Probe on \无条件分支数 
  // Probe on \条件分支成功数 
  // Probe on \插入气泡数 
  // Probe on \LoadUse次数 
  not not_2 (not_2_out, halt);
  Counter #(.width(16), .max('hffff), .ongoal("wrap"), .trigger("rising"), .behavior("new")) counter_1 (
    .count(not_2_out), .Q(\总周期数 ), .clk(CLK), .clr(RST));  // open: load, D, carry, preset, down
  // Probe on IF_PC[11:0]
  // Probe on WB_PC[19:0]
  // RiscV_Probe riscv_probe_5: pin names not known; wires that end beside it: WB_IR
  ROM #(.addrWidth(10), .dataWidth(32), .Select("high")) rom_1 (.addr(IF_PC[11:2]), .data(IF_IR));
  Adder #(.width(32)) adder_1 (.a(IF_PC), .b(32'h4), .out(PC_4));  // open: cin, cout
  // Probe on EX_PC[11:0]
  // Probe on ID_PC[11:0]
  // Probe on M_PC[11:0]
  D_Flip_Flop #(.trigger("high"), .Pre_Clr_Positions("LEGACY"), .NegatePresetClear("false"), .enable("true"), .NewFFLayout("false")) d_ff_1 (.Q(d_ff_1_q));  // open: clk, D, Qn, preset, en, reset
  // Probe on 13'hc
  IF_ID IF_ID (
    .en(en), .IR(IF_IR), .IR_2(ID_IR), .PC(IF_PC), .PC_2(ID_PC), .CLK(CLK), .RST(RST));  // open: PC_4, PC_4_2, PredictJump, PredictJump_2
  // Probe on WB_PC[11:0]
  Comparator #(.width(13), .mode("twosComplement")) comparator_1 (
    .a(CNT_num), .b(13'hc), .eq(comparator_1_eq), .lt(comparator_1_lt));  // open: gt
  Clock #(.highDuration(1), .lowDuration(1)) clock_1 (.out(clock_1_out));
  // RiscV_Probe riscv_probe_6: pin names not known; wires that end beside it: ID_IR, 5'b00001
  nand nand_1 (nand_1_out, d_ff_1_q, comparator_1_eq);
  Counter #(.width(13), .max('h1fff), .ongoal("stay"), .trigger("rising"), .behavior("old")) counter_2 (
    .count(comparator_1_lt), .Q(CNT_num), .clk(clock_1_out));  // open: load, D, carry, clr, preset
  assign CLK = nand_1_out ? clock_1_out : 1'bz;  // Controlled_Buffer controlled_buffer_1
  \单周期硬布线控制器  \u_单周期硬布线控制器_1  (
    .Funct({ID_IR[30], ID_IR[25], ID_IR[14:12]}), .OP(ID_IR[6:2]), .ALU_OP(\单周期硬布线控制器_1_alu_op ),
    .MemToReg(\单周期硬布线控制器_1_memtoreg ), .MemWrite(\单周期硬布线控制器_1_memwrite ), .ALU_SRC(\单周期硬布线控制器_1_alu_src ),
    .RegWrite(\单周期硬布线控制器_1_regwrite ), .ecall(ecall), .S_type(\单周期硬布线控制器_1_s_type ),
    .Jalr(\单周期硬布线控制器_1_jalr ), .Beq(\单周期硬布线控制器_1_beq ), .JAL(\单周期硬布线控制器_1_jal ), .Bne(\单周期硬布线控制器_1_bne ),
    .in_3(ID_IR[21]), .uret(\单周期硬布线控制器_1_uret ), .sb(\单周期硬布线控制器_1_sb ), .lui(\单周期硬布线控制器_1_lui ),
    .srl(\单周期硬布线控制器_1_srl ), .blt(\单周期硬布线控制器_1_blt ));  // open: CSRRSI, CSRRCI
  Multiplexer #(.select(1), .width(5), .disabled("Z"), .enable("false")) multiplexer_2 (
    .in0(ID_IR[19:15]), .in1(5'b10001), .out(multiplexer_2_out), .sel(ecall));
  Multiplexer #(.select(1), .width(5), .disabled("Z"), .enable("false")) multiplexer_3 (
    .in0(ID_IR[24:20]), .in1(5'b01010), .out(multiplexer_3_out), .sel(ecall));
  Multiplexer #(.select(1), .width(12), .disabled("Z"), .enable("false")) multiplexer_4 (
    .in0(ID_IR[31:20]), .in1({ID_IR[31:25], ID_IR[11:7]}), .out(multiplexer_4_out), .sel(\单周期硬布线控制器_1_s_type ));
  assign bit_extender_1_out = {{20{multiplexer_4_out[11]}}, multiplexer_4_out};  // Bit_Extender bit_extender_1
  assign bit_extender_2_out = {{20{ID_IR[31]}}, {ID_IR[31], ID_IR[7], ID_IR[30:25], ID_IR[11:8]}};  // Bit_Extender bit_extender_2
  assign bit_extender_3_out = {{12{ID_IR[31]}}, {ID_IR[31], ID_IR[19:12], ID_IR[20], ID_IR[30:21]}};  // Bit_Extender bit_extender_3
  Comparator #(.width(32), .mode("twosComplement")) comparator_2 (
    .a(ID_R1), .b(32'h22), .eq(comparator_2_eq));  // open: gt, lt
  Pull_Resistor #(.pull(1)) pull_resistor_1 (.node(CLK));
  Shifter #(.width(32), .shift("ll")) shifter_1 (.in(bit_extender_2_out), .\dist (5'b00001), .out(shifter_1_out));
  Shifter #(.width(32), .shift("ll")) shifter_2 (.in(bit_extender_3_out), .\dist (5'b00001), .out(shifter_2_out));
  and and_2 (and_2_out, EX_ecall, comparator_2_eq);
  not not_3 (not_3_out, comparator_2_eq);
  and and_3 (and_3_out, not_3_out, EX_ecall, not_4_out);
  not not_4 (not_4_out, Go);
  Register #(.width(32), .trigger("rising"), .Select("low")) register_1 (
    .D(ID_R2), .en(and_2_out), .Q(LedData), .clk(CLK));  // open: clr
  not not_5 (not_5_out, CLK);
  Regifile regifile_1 (
    .Din(RDin), .Clk(not_5_out), .R1(ID_R1), .R2(ID_R2), .WE(RegWrite), .W_num(WB_W_num),
    .R1_num(multiplexer_2_out), .R2_num(multiplexer_3_out));
  and and_4 (and_4_out, Beq, eq);
  and and_5 (and_5_out, Bne, not_6_out);
  not not_6 (not_6_out, eq);
  or or_1 (B, and_4_out, and_5_out, blt);
  // ID_EX ID_EX: pin names not known; wires that end beside it: en, \单周期硬布线控制器_1_beq , \单周期硬布线控制器_1_bne , \单周期硬布线控制器_1_blt , \单周期硬布线控制器_1_memtoreg , \单周期硬布线控制器_1_memwrite , \单周期硬布线控制器_1_alu_op , \单周期硬布线控制器_1_alu_src , \单周期硬布线控制器_1_regwrite , \单周期硬布线控制器_1_jal , \单周期硬布线控制器_1_jalr , \单周期硬布线控制器_1_lui , \单周期硬布线控制器_1_srl , \单周期硬布线控制器_1_sb , \单周期硬布线控制器_1_uret , ecall, ID_R1, ID_R2, ID_IR[11:7], bit_extender_1_out, ID_PC, ID_IR, shifter_1_out, shifter_2_out, {ID_IR[31:12], {12{1'b0}}}, ID_EX_p26, ID_EX_p26, CLK, RST, Beq, Bne, blt, ID_EX_p33, ID_EX_p34, ID_EX_p35, ID_EX_p36, EX_RegWrite, JAL, JALR, lui, srl, EX_ecall, EX_R1, EX_R2, EX_W_num, ID_EX_p46, EX_PC, EX_IR, ID_EX_p49, ID_EX_p50, ID_EX_p51
  Counter #(.width(16), .max('hffff), .ongoal("wrap"), .trigger("rising"), .behavior("new")) counter_3 (
    .count(B), .Q(\分支成功数 ), .clk(CLK), .clr(RST));  // open: load, D, carry, preset, down
  Multiplexer #(.select(1), .width(32), .disabled("Z"), .enable("false")) multiplexer_5 (
    .in0(EX_R2), .in1(ID_EX_p46), .out(multiplexer_5_out), .sel(ID_EX_p36));
  assign bit_extender_4_out = {{27{EX_R2[4]}}, EX_R2[4:0]};  // Bit_Extender bit_extender_4
  Adder #(.width(32)) adder_2 (.a(ID_EX_p49), .b(EX_PC), .out(BJ));  // open: cin, cout
  Multiplexer #(.select(1), .width(32), .disabled("Z"), .enable("false")) multiplexer_6 (
    .in0(multiplexer_5_out), .in1(bit_extender_4_out), .out(multiplexer_6_out), .sel(srl));
  Adder #(.width(32)) adder_3 (.a(ID_EX_p50), .b(EX_PC), .out(DJ));  // open: cin, cout
  or or_2 (or_2_out, JAL, JALR);
  Counter #(.width(16), .max('hffff), .ongoal("wrap"), .trigger("rising"), .behavior("new")) counter_4 (
    .count(or_2_out), .Q(\无条件分支数 ), .clk(CLK), .clr(RST));  // open: load, D, carry, preset, down
  EX_MEM EX_MEM (
    .RegWrite(EX_RegWrite), .MemToReg(ID_EX_p33), .MemWrite(ID_EX_p34), .AluResult(ALUresult),
    .WriteData(EX_R2), .WriteReg_num(EX_W_num), .PC(EX_PC), .IR(EX_IR), .JAL(JAL), .JALR(JALR),
    .RegWrite_2(MEM_RegWrite), .MemToReg_2(EX_MEM_memtoreg_2), .MemWrite_2(MemWrite),
    .AluResult_2(EX_MEM_aluresult_2), .WriteData_2(MDin), .WriteReg_num_2(MEM_W_num), .PC_2(M_PC),
    .IR_2(MEM_IR), .JAL_2(EX_MEM_jal_2), .JALR_2(EX_MEM_jalr_2), .CLK(CLK), .lu(ID_EX_p51),
    .lu_2(EX_MEM_lu_2), .RST(RST), .en(en), .halt(and_3_out), .halt_2(EX_MEM_halt_2));  // open: Bj, lui, sb, bj_2, lui_2, sb_2
  ALU alu_1 (
    .X(EX_R1), .Y(multiplexer_6_out), .AluOP(ID_EX_p35), .Equal(eq), .Result(ALUresult));  // open: Result_2, out_4, out_6
  RAM #(.addrWidth(10), .dataWidth(32), .bus("separate"), .Select("high")) ram_1 (
    .addr(EX_MEM_aluresult_2[11:2]), .din(MDin), .data(ram_1_data), .str(MemWrite), .clk(CLK), .ld(1'b1),
    .clr(RST));  // open: sel
  Adder #(.width(16)) adder_4 (.a(\无条件分支数 ), .b(\条件分支成功数 ), .out(adder_4_out));  // open: cin, cout
  MEM_WB MEM_WB (
    .RegWrite(MEM_RegWrite), .MemToReg(EX_MEM_memtoreg_2), .AluResult(EX_MEM_aluresult_2),
    .ReadData(ram_1_data), .WriteReg_num(MEM_W_num), .PC(M_PC), .IR(MEM_IR), .JAL(EX_MEM_jal_2),
    .JALR(EX_MEM_jalr_2), .RegWrite_2(RegWrite), .MemToReg_2(MEM_WB_memtoreg_2),
    .AluResult_2(MEM_WB_aluresult_2), .ReadData_2(MEM_WB_readdata_2), .WriteReg_num_2(WB_W_num),
    .PC_2(WB_PC), .IR_2(WB_IR), .JAL_2(MEM_WB_jal_2), .JALR_2(MEM_WB_jalr_2), .CLK(CLK), .RST(RST), .en(en),
    .halt(EX_MEM_halt_2), .halt_2(halt), .lu(EX_MEM_lu_2), .lu_2(MEM_WB_lu_2));  // open: lui, lui_2
  Shifter #(.width(16), .shift("ll")) shifter_3 (.in(adder_4_out), .\dist (4'b0001), .out(\插入气泡数 ));
  Multiplexer #(.select(1), .width(32), .disabled("Z"), .enable("false")) multiplexer_7 (
    .in0(MEM_WB_aluresult_2), .in1(MEM_WB_readdata_2), .out(multiplexer_7_out), .sel(MEM_WB_memtoreg_2));
  Adder #(.width(32)) adder_5 (.a(WB_PC), .b(32'h4), .out(adder_5_out));  // open: cin, cout
  not not_7 (en, halt);
  or or_3 (or_3_out, MEM_WB_jalr_2, MEM_WB_jal_2);
  Multiplexer #(.select(1), .width(32), .disabled("Z"), .enable("false")) multiplexer_8 (
    .in0(multiplexer_7_out), .in1(adder_5_out), .out(multiplexer_8_out), .sel(or_3_out));
  Multiplexer #(.select(1), .width(32), .disabled("Z"), .enable("false")) multiplexer_9 (
    .in0(multiplexer_8_out), .in1(MEM_WB_lu_2), .out(RDin), .sel(lui));

  // Other names for the same wires on the sheet: MEM_PC[31:0] = M_PC

  // Notes on the sheet:
  //   中断源
  //   中断等待指示
  //   数码管输出
  //   指令存储器
  //   contents of rom_1 (hex, n*v repeats v):
  //   413 493 913 993 46413 14e493 296913 39e993 842023 942223 1242423 1342623 a00893 493 913 993 73
  //   控制位
  //   流水调试日志用
  //   暂停节拍，不能为0
  //   指令探针
  //   可计数暂停的时钟源
  //   Beq
  //   Bne
  //   为方便自动评测，需要输出流水线各段保存的PC值，注意是PC不是PC+4，另外ID段寄存器写入信息，Mem段内存写入信息也要输出
  //   R2
  //   数据存储器
endmodule

module \气泡流水线  (
  output RegWrite,
  output MemWrite,
  output [31:0] IF_PC,
  output [31:0] ID_PC,
  output [31:0] EX_PC,
  output [31:0] M_PC,
  output [31:0] WB_PC,
  output [31:0] RDin,
  output [31:0] MDin,
  output [31:0] LedData
);

  wire and_1_out, and_2_out, and_3_out, and_4_out, and_5_out, and_6_out, B, Beq, blt, Bne, CLK, clock_1_out,
       comparator_1_eq, comparator_1_lt, comparator_2_eq, d_ff_1_q, ecall, en, eq, EX_ecall, EX_MEM_halt_2,
       EX_MEM_jal_2, EX_MEM_jalr_2, EX_MEM_lui_2, EX_MEM_memtoreg_2, EX_RegWrite, Go, halt, ID_EX_p26,
       ID_EX_p33, ID_EX_p34, ID_EX_p36, ID_EX_p40, ID_EX_p42, IR1, IR2, IR3, JAL, JALR, less, MEM_RegWrite,
       MEM_WB_halt_2, MEM_WB_jal_2, MEM_WB_jalr_2, MEM_WB_lui_2, MEM_WB_memtoreg_2, multiplexer_2_out,
       nand_1_out, not_1_out, not_2_out, not_3_out, not_4_out, not_5_out, not_6_out, not_7_out, not_8_out,
       not_9_out, or_1_out, or_3_out, or_4_out, or_5_out, RST, sb, srl, stall, W1, W2, W3,
       \单周期硬布线控制器_1_alu_src , \单周期硬布线控制器_1_beq , \单周期硬布线控制器_1_blt , \单周期硬布线控制器_1_bne , \单周期硬布线控制器_1_jal ,
       \单周期硬布线控制器_1_jalr , \单周期硬布线控制器_1_lui , \单周期硬布线控制器_1_memtoreg , \单周期硬布线控制器_1_memwrite ,
       \单周期硬布线控制器_1_regwrite , \单周期硬布线控制器_1_s_type , \单周期硬布线控制器_1_sb , \单周期硬布线控制器_1_srl , \单周期硬布线控制器_1_uret ;
  wire [1:0] byte_ad;
  wire [3:0] ID_EX_p35, \单周期硬布线控制器_1_alu_op ;
  wire [4:0] bit_extender_5_out, EX_W_num, MEM_W_num, multiplexer_3_out, multiplexer_4_out, shifter_3_out,
       WB_W_num;
  wire [11:0] multiplexer_5_out;
  wire [12:0] CNT_num;
  wire [15:0] adder_5_out, \LoadUse次数 , \总周期数 , \插入气泡数 , \无条件分支数 , \条件分支成功数 ;
  wire [31:0] adder_4_out, adder_6_out, ALUresult, and_7_out, bit_extender_1_out, bit_extender_2_out,
       bit_extender_3_out, bit_extender_4_out, BJ, DJ, EX_IR, EX_MEM_lu_2, EX_R1, EX_R2, ID_EX_p47,
       ID_EX_p50, ID_EX_p51, ID_EX_p52, ID_IR, ID_R1, ID_R2, IF_IR, MDout, MEM_IR, MEM_WB_aluresult_2,
       MEM_WB_lu_2, MEM_WB_readdata_2, MEM_Writedata, multiplexer_1_out, multiplexer_6_out,
       multiplexer_7_out, multiplexer_8_out, multiplexer_10_out, multiplexer_11_out, PC_4, shifter_1_out,
       shifter_2_out, shifter_4_out, WB_IR;
  wire [31:2] MEM_ALUresult;

  Button \u_总复位  (.out(RST));
  Button _1 (.out(IR1));
  Button _2 (.out(IR2));
  Button _3 (.out(IR3));
  // Probe on \总周期数 
  // Probe on \总周期数 
  Button \u_继续运行  (.out(Go));
  LED #(.active("true")) led_1 (.in(W1));
  LED #(.active("true")) led_2 (.in(W2));
  LED #(.active("true")) led_3 (.in(W3));
  Hex_Digit_Display hex_digit_display_1 (.value(LedData[31:28]));  // open: dp
  // Probe on IF_PC[19:0]
  // RiscV_Probe riscv_probe_1: pin names not known; wires that end beside it: IF_IR
  Hex_Digit_Display hex_digit_display_2 (.value(LedData[23:20]));  // open: dp
  Hex_Digit_Display hex_digit_display_3 (.value(LedData[27:24]));  // open: dp
  // Probe on ID_PC[19:0]
  // RiscV_Probe riscv_probe_2: pin names not known; wires that end beside it: ID_IR
  Hex_Digit_Display hex_digit_display_4 (.value(LedData[15:12]));  // open: dp
  Hex_Digit_Display hex_digit_display_5 (.value(LedData[19:16]));  // open: dp
  Hex_Digit_Display hex_digit_display_6 (.value(LedData[11:8]));  // open: dp
  Hex_Digit_Display hex_digit_display_7 (.value(LedData[7:4]));  // open: dp
  // Probe on EX_PC[19:0]
  // RiscV_Probe riscv_probe_3: pin names not known; wires that end beside it: EX_IR
  Multiplexer #(.select(3), .width(32), .disabled("Z"), .enable("false")) multiplexer_1 (
    .in0(PC_4), .in1(BJ), .in2(ALUresult), .in3({32{1'b0}}), .in4(DJ), .in5({32{1'b0}}), .in6({32{1'b0}}),
    .in7({32{1'b0}}), .out(multiplexer_1_out), .sel({JAL, JALR, B}));
  Hex_Digit_Display hex_digit_display_8 (.value(LedData[3:0]));  // open: dp
  Register #(.width(32), .trigger("rising"), .Select("low")) PC (
    .D(multiplexer_1_out), .en(not_1_out), .Q(IF_PC), .clk(CLK), .clr(RST));
  not not_1 (not_1_out, multiplexer_2_out);
  Multiplexer #(.select(1), .width(1), .disabled("Z"), .enable("false")) multiplexer_2 (
    .in0(stall), .in1(not_2_out), .out(multiplexer_2_out), .sel(halt));
  not not_2 (not_2_out, Go);
  // Probe on \总周期数 
  // Probe on M_PC[19:0]
  // RiscV_Probe riscv_probe_4: pin names not known; wires that end beside it: MEM_IR
  // Probe on \总周期数 
  // Probe on \无条件分支数 
  // Probe on \条件分支成功数 
  // Probe on \插入气泡数 
  // Probe on \LoadUse次数 
  not not_3 (not_3_out, halt);
  Counter #(.width(16), .max('hffff), .ongoal("wrap"), .trigger("rising"), .behavior("new")) counter_1 (
    .count(not_3_out), .Q(\总周期数 ), .clk(CLK), .clr(RST));  // open: load, D, carry, preset, down
  // Probe on IF_PC[11:0]
  // Probe on WB_PC[19:0]
  // RiscV_Probe riscv_probe_5: pin names not known; wires that end beside it: WB_IR
  ROM #(.addrWidth(10), .dataWidth(32), .Select("high")) rom_1 (.addr(IF_PC[11:2]), .data(IF_IR));
  Adder #(.width(32)) adder_1 (.a(IF_PC), .b(32'h4), .out(PC_4));  // open: cin, cout
  // Probe on EX_PC[11:0]
  // Probe on ID_PC[11:0]
  // Probe on M_PC[11:0]
  D_Flip_Flop #(.trigger("high"), .Pre_Clr_Positions("LEGACY"), .NegatePresetClear("false"), .enable("true"), .NewFFLayout("false")) d_ff_1 (.Q(d_ff_1_q));  // open: clk, D, Qn, preset, en, reset
  // Probe on 13'h249
  or or_1 (or_1_out, B, JAL, RST, JALR);
  not not_4 (not_4_out, stall);
  and and_1 (and_1_out, en, not_4_out);
  IF_ID IF_ID (
    .en(and_1_out), .IR(IF_IR), .IR_2(ID_IR), .PC(IF_PC), .PC_2(ID_PC), .CLK(CLK), .RST(or_1_out));  // open: PC_4, PC_4_2, PredictJump, PredictJump_2
  // Probe on WB_PC[11:0]
  Comparator #(.width(13), .mode("twosComplement")) comparator_1 (
    .a(CNT_num), .b(13'h249), .eq(comparator_1_eq), .lt(comparator_1_lt));  // open: gt
  Clock #(.highDuration(1), .lowDuration(1)) clock_1 (.out(clock_1_out));
  \数据相关检测逻辑  \u_数据相关检测逻辑_1  (
    .ID_IR(ID_IR), .EX_WriteReg_num(EX_W_num), .EX_RegWrite(EX_RegWrite), .MEM_WriteReg_num(MEM_W_num),
    .MEM_RegWrite(MEM_RegWrite), .DataHazzard(stall));
  // RiscV_Probe riscv_probe_6: pin names not known; wires that end beside it: ID_IR, 5'b00001
  nand nand_1 (nand_1_out, d_ff_1_q, comparator_1_eq);
  Counter #(.width(13), .max('h1fff), .ongoal("stay"), .trigger("rising"), .behavior("old")) counter_2 (
    .count(comparator_1_lt), .Q(CNT_num), .clk(clock_1_out));  // open: load, D, carry, clr, preset
  assign CLK = nand_1_out ? clock_1_out : 1'bz;  // Controlled_Buffer controlled_buffer_1
  \单周期硬布线控制器  \u_单周期硬布线控制器_1  (
    .Funct({ID_IR[30], ID_IR[25], ID_IR[14:12]}), .OP(ID_IR[6:2]), .ALU_OP(\单周期硬布线控制器_1_alu_op ),
    .MemToReg(\单周期硬布线控制器_1_memtoreg ), .MemWrite(\单周期硬布线控制器_1_memwrite ), .ALU_SRC(\单周期硬布线控制器_1_alu_src ),
    .RegWrite(\单周期硬布线控制器_1_regwrite ), .ecall(ecall), .S_type(\单周期硬布线控制器_1_s_type ),
    .Jalr(\单周期硬布线控制器_1_jalr ), .Beq(\单周期硬布线控制器_1_beq ), .JAL(\单周期硬布线控制器_1_jal ), .Bne(\单周期硬布线控制器_1_bne ),
    .in_3(ID_IR[21]), .uret(\单周期硬布线控制器_1_uret ), .sb(\单周期硬布线控制器_1_sb ), .lui(\单周期硬布线控制器_1_lui ),
    .srl(\单周期硬布线控制器_1_srl ), .blt(\单周期硬布线控制器_1_blt ));  // open: CSRRSI, CSRRCI
  Multiplexer #(.select(1), .width(5), .disabled("Z"), .enable("false")) multiplexer_3 (
    .in0(ID_IR[19:15]), .in1(5'b10001), .out(multiplexer_3_out), .sel(ecall));
  Multiplexer #(.select(1), .width(5), .disabled("Z"), .enable("false")) multiplexer_4 (
    .in0(ID_IR[24:20]), .in1(5'b01010), .out(multiplexer_4_out), .sel(ecall));
  Multiplexer #(.select(1), .width(12), .disabled("Z"), .enable("false")) multiplexer_5 (
    .in0(ID_IR[31:20]), .in1({ID_IR[31:25], ID_IR[11:7]}), .out(multiplexer_5_out), .sel(\单周期硬布线控制器_1_s_type ));
  assign bit_extender_1_out = {{20{multiplexer_5_out[11]}}, multiplexer_5_out};  // Bit_Extender bit_extender_1
  assign bit_extender_2_out = {{20{ID_IR[31]}}, {ID_IR[31], ID_IR[7], ID_IR[30:25], ID_IR[11:8]}};  // Bit_Extender bit_extender_2
  assign bit_extender_3_out = {{12{ID_IR[31]}}, {ID_IR[31], ID_IR[19:12], ID_IR[20], ID_IR[30:21]}};  // Bit_Extender bit_extender_3
  Comparator #(.width(32), .mode("twosComplement")) comparator_2 (
    .a(EX_R1), .b(32'h22), .eq(comparator_2_eq));  // open: gt, lt
  Pull_Resistor #(.pull(1)) pull_resistor_1 (.node(CLK));
  Shifter #(.width(32), .shift("ll")) shifter_1 (.in(bit_extender_2_out), .\dist (5'b00001), .out(shifter_1_out));
  Shifter #(.width(32), .shift("ll")) shifter_2 (.in(bit_extender_3_out), .\dist (5'b00001), .out(shifter_2_out));
  and and_2 (and_2_out, EX_ecall, comparator_2_eq);
  not not_5 (not_5_out, comparator_2_eq);
  and and_3 (and_3_out, not_5_out, EX_ecall, not_6_out);
  not not_6 (not_6_out, Go);
  Register #(.width(32), .trigger("rising"), .Select("low")) register_1 (
    .D(EX_R2), .en(and_2_out), .Q(LedData), .clk(CLK));  // open: clr
  not not_7 (not_7_out, CLK);
  Regifile regifile_1 (
    .Din(RDin), .Clk(not_7_out), .R1(ID_R1), .R2(ID_R2), .WE(RegWrite), .W_num(WB_W_num),
    .R1_num(multiplexer_3_out), .R2_num(multiplexer_4_out));
  and and_4 (and_4_out, Beq, eq);
  and and_5 (and_5_out, Bne, not_8_out);
  not not_8 (not_8_out, eq);
  and and_6 (and_6_out, blt, less);
  or or_2 (B, and_4_out, and_5_out, and_6_out);
  or or_3 (or_3_out, stall, or_1_out);
  // ID_EX ID_EX: pin names not known; wires that end beside it: en, \单周期硬布线控制器_1_beq , \单周期硬布线控制器_1_bne , \单周期硬布线控制器_1_blt , \单周期硬布线控制器_1_memtoreg , \单周期硬布线控制器_1_memwrite , \单周期硬布线控制器_1_alu_op , \单周期硬布线控制器_1_alu_src , \单周期硬布线控制器_1_regwrite , \单周期硬布线控制器_1_jal , \单周期硬布线控制器_1_jalr , \单周期硬布线控制器_1_lui , \单周期硬布线控制器_1_srl , \单周期硬布线控制器_1_sb , \单周期硬布线控制器_1_uret , ecall, ID_R1, ID_R2, ID_IR[11:7], bit_extender_1_out, ID_PC, ID_IR, shifter_1_out, shifter_2_out, {ID_IR[31:12], {12{1'b0}}}, ID_EX_p26, ID_EX_p26, CLK, or_3_out, Beq, Bne, blt, ID_EX_p33, ID_EX_p34, ID_EX_p35, ID_EX_p36, EX_RegWrite, JAL, JALR, ID_EX_p40, srl, ID_EX_p42, EX_ecall, EX_R1, EX_R2, EX_W_num, ID_EX_p47, EX_PC, EX_IR, ID_EX_p50, ID_EX_p51, ID_EX_p52
  Counter #(.width(16), .max('hffff), .ongoal("wrap"), .trigger("rising"), .behavior("new")) counter_3 (
    .count(B), .Q(\条件分支成功数 ), .clk(CLK), .clr(RST));  // open: load, D, carry, preset, down
  Multiplexer #(.select(1), .width(32), .disabled("Z"), .enable("false")) multiplexer_6 (
    .in0(EX_R2), .in1(ID_EX_p47), .out(multiplexer_6_out), .sel(ID_EX_p36));
  assign bit_extender_4_out = {{27{EX_R2[4]}}, EX_R2[4:0]};  // Bit_Extender bit_extender_4
  Adder #(.width(32)) adder_2 (.a(ID_EX_p50), .b(EX_PC), .out(BJ));  // open: cin, cout
  Adder #(.width(32)) adder_3 (.a(ID_EX_p51), .b(EX_PC), .out(DJ));  // open: cin, cout
  or or_4 (or_4_out, JAL, JALR);
  Multiplexer #(.select(1), .width(32), .disabled("Z"), .enable("false")) multiplexer_7 (
    .in0(multiplexer_6_out), .in1(bit_extender_4_out), .out(multiplexer_7_out), .sel(srl));
  Counter #(.width(16), .max('hffff), .ongoal("wrap"), .trigger("rising"), .behavior("new")) counter_4 (
    .count(or_4_out), .Q(\无条件分支数 ), .clk(CLK), .clr(RST));  // open: load, D, carry, preset, down
  EX_MEM EX_MEM (
    .RegWrite(EX_RegWrite), .MemToReg(ID_EX_p33), .MemWrite(ID_EX_p34), .AluResult(ALUresult),
    .WriteData(EX_R2), .WriteReg_num(EX_W_num), .PC(EX_PC), .IR(EX_IR), .JAL(JAL), .JALR(JALR),
    .lui(ID_EX_p40), .sb(ID_EX_p42), .RegWrite_2(MEM_RegWrite), .MemToReg_2(EX_MEM_memtoreg_2),
    .MemWrite_2(MemWrite), .AluResult_2({MEM_ALUresult, byte_ad}), .WriteData_2(MEM_Writedata),
    .WriteReg_num_2(MEM_W_num), .PC_2(M_PC), .IR_2(MEM_IR), .JAL_2(EX_MEM_jal_2), .JALR_2(EX_MEM_jalr_2),
    .lui_2(EX_MEM_lui_2), .sb_2(sb), .CLK(CLK), .lu(ID_EX_p52), .lu_2(EX_MEM_lu_2), .RST(RST), .en(en),
    .halt(and_3_out), .halt_2(EX_MEM_halt_2));  // open: Bj, bj_2
  ALU alu_1 (
    .X(EX_R1), .Y(multiplexer_7_out), .AluOP(ID_EX_p35), .Equal(eq), .Result(ALUresult), .out_6(less));  // open: Result_2, out_4
  assign bit_extender_5_out = {{3{1'b0}}, byte_ad};  // Bit_Extender bit_extender_5
  Multiplexer #(.select(2), .width(32), .disabled("Z"), .enable("false")) multiplexer_8 (
    .in0(32'hffffff00), .in1(32'hffff00ff), .in2(32'hff00ffff), .in3(32'hffffff), .out(multiplexer_8_out),
    .sel(byte_ad));
  Shifter #(.width(5), .shift("ll")) shifter_3 (.in(bit_extender_5_out), .\dist (3'b011), .out(shifter_3_out));
  assign and_7_out = multiplexer_8_out & MDout;  // AND_Gate and_7, 32 bits wide
  Shifter #(.width(32), .shift("ll")) shifter_4 (.in(MEM_Writedata), .\dist (shifter_3_out), .out(shifter_4_out));
  RAM #(.addrWidth(10), .dataWidth(32), .bus("separate"), .Select("high")) ram_1 (
    .addr(MEM_ALUresult[11:2]), .din(MDin), .data(MDout), .str(MemWrite), .clk(CLK), .ld(1'b1), .clr(RST));  // open: sel
  Adder #(.width(32)) adder_4 (.a(and_7_out), .b(shifter_4_out), .out(adder_4_out));  // open: cin, cout
  Adder #(.width(16)) adder_5 (.a(\无条件分支数 ), .b(\条件分支成功数 ), .out(adder_5_out));  // open: cin, cout
  MEM_WB MEM_WB (
    .RegWrite(MEM_RegWrite), .MemToReg(EX_MEM_memtoreg_2), .AluResult({MEM_ALUresult, byte_ad}),
    .ReadData(MDout), .WriteReg_num(MEM_W_num), .PC(M_PC), .IR(MEM_IR), .JAL(EX_MEM_jal_2),
    .JALR(EX_MEM_jalr_2), .lui(EX_MEM_lui_2), .RegWrite_2(RegWrite), .MemToReg_2(MEM_WB_memtoreg_2),
    .AluResult_2(MEM_WB_aluresult_2), .ReadData_2(MEM_WB_readdata_2), .WriteReg_num_2(WB_W_num),
    .PC_2(WB_PC), .IR_2(WB_IR), .JAL_2(MEM_WB_jal_2), .JALR_2(MEM_WB_jalr_2), .lui_2(MEM_WB_lui_2),
    .CLK(CLK), .RST(RST), .en(en), .halt(EX_MEM_halt_2), .halt_2(MEM_WB_halt_2), .lu(EX_MEM_lu_2),
    .lu_2(MEM_WB_lu_2));
  Multiplexer #(.select(1), .width(32), .disabled("Z"), .enable("false")) multiplexer_9 (
    .in0(MEM_Writedata), .in1(adder_4_out), .out(MDin), .sel(sb));
  Shifter #(.width(16), .shift("ll")) shifter_5 (.in(adder_5_out), .\dist (4'b0001), .out(\插入气泡数 ));
  Multiplexer #(.select(1), .width(32), .disabled("Z"), .enable("false")) multiplexer_10 (
    .in0(MEM_WB_aluresult_2), .in1(MEM_WB_readdata_2), .out(multiplexer_10_out), .sel(MEM_WB_memtoreg_2));
  Adder #(.width(32)) adder_6 (.a(WB_PC), .b(32'h4), .out(adder_6_out));  // open: cin, cout
  and and_8 (halt, MEM_WB_halt_2, not_9_out);
  not not_9 (not_9_out, Go);
  or or_5 (or_5_out, MEM_WB_jalr_2, MEM_WB_jal_2);
  Multiplexer #(.select(1), .width(32), .disabled("Z"), .enable("false")) multiplexer_11 (
    .in0(multiplexer_10_out), .in1(adder_6_out), .out(multiplexer_11_out), .sel(or_5_out));
  Multiplexer #(.select(1), .width(32), .disabled("Z"), .enable("false")) multiplexer_12 (
    .in0(multiplexer_11_out), .in1(MEM_WB_lu_2), .out(RDin), .sel(MEM_WB_lui_2));
  not not_10 (en, halt);

  // Other names for the same wires on the sheet: MEM_ALUresult[1:0] = byte_ad; MEM_PC[31:0] = M_PC

  // Notes on the sheet:
  //   中断源
  //   时空图监测，可删除
  //   中断等待指示
  //   数码管输出
  //   指令存储器
  //   contents of rom_1 (hex, n*v repeats v):
  //   800e13 fedc04b7 fff00413 1045413 84e4b3 900533 2200893 73 ba984b7 900533 73 76544b7 900533 73
  //   32104b7 900533 73 fffe0e13 fa0e1ee3 a00893 73
  //   控制位
  //   流水调试日志用
  //   暂停节拍，不能为0
  //   戳工具置1进入计数暂停模式，ctrl+k时钟自动运行到对应节拍暂停
  //   ctrl+k关闭时钟连续运行，将控制位置零，进入单步调试模式调试
  //   指令探针
  //   可计数暂停的时钟源
  //   Beq
  //   Bne
  //   为方便自动评测，需要输出流水线各段保存的PC值，注意是PC不是PC+4，另外ID段寄存器写入信息，Mem段内存写入信息也要输出
  //   R2
  //   数据存储器
endmodule

module \重定向流水线  (
  output RegWrite,
  output MemWrite,
  output [31:0] IF_PC,
  output [31:0] ID_PC,
  output [31:0] EX_PC,
  output [31:0] M_PC,
  output [31:0] WB_PC,
  output [31:0] RDin,
  output [31:0] MDin,
  output [31:0] LedData
);

  wire and_1_out, and_2_out, and_3_out, and_4_out, and_5_out, and_6_out, and_8_out, B, Beq, blt, Bne, branch,
       CLK, clock_1_out, comparator_1_eq, comparator_1_lt, comparator_2_eq, d_ff_1_q, ecall, en, eq,
       EX_ecall, EX_MEM_halt_2, EX_MEM_jal_2, EX_MEM_jalr_2, EX_MEM_lui_2, EX_MEM_memtoreg_2, EX_MemtoReg,
       EX_RegWrite, Go, halt, ID_EX_p28, ID_EX_p36, ID_EX_p38, ID_EX_p42, ID_EX_p44, IR1, IR2, IR3, JAL,
       JALR, less, MEM_RegWrite, MEM_WB_halt_2, MEM_WB_jal_2, MEM_WB_jalr_2, MEM_WB_lui_2, MEM_WB_memtoreg_2,
       multiplexer_2_out, nand_1_out, not_1_out, not_2_out, not_3_out, not_4_out, not_5_out, not_6_out,
       not_7_out, not_8_out, not_9_out, not_10_out, not_11_out, or_3_out, or_4_out, or_5_out, RST, sb, srl,
       stall, W1, W2, W3, \单周期硬布线控制器_1_alu_src , \单周期硬布线控制器_1_beq , \单周期硬布线控制器_1_blt , \单周期硬布线控制器_1_bne ,
       \单周期硬布线控制器_1_jal , \单周期硬布线控制器_1_jalr , \单周期硬布线控制器_1_lui , \单周期硬布线控制器_1_memtoreg ,
       \单周期硬布线控制器_1_memwrite , \单周期硬布线控制器_1_regwrite , \单周期硬布线控制器_1_s_type , \单周期硬布线控制器_1_sb ,
       \单周期硬布线控制器_1_srl , \单周期硬布线控制器_1_uret ;
  wire [1:0] byte_ad, ID_EX_p45, ID_EX_p46, Rsf, Rtf;
  wire [3:0] ID_EX_p37, \单周期硬布线控制器_1_alu_op ;
  wire [4:0] bit_extender_5_out, EX_W_num, MEM_W_num, multiplexer_3_out, multiplexer_4_out, shifter_3_out,
       WB_W_num;
  wire [11:0] multiplexer_5_out;
  wire [12:0] CNT_num;
  wire [15:0] adder_5_out, \LoadUse次数 , shifter_5_out, \总周期数 , \插入气泡数 , \无条件分支数 , \条件分支成功数 ;
  wire [31:0] adder_4_out, adder_6_out, ALUresult, and_7_out, bit_extender_1_out, bit_extender_2_out,
       bit_extender_3_out, bit_extender_4_out, BJ, DJ, EX_IR, EX_MEM_lu_2, EX_R1, EX_R2, ID_EX_p48,
       ID_EX_p49, ID_EX_p54, ID_EX_p55, ID_EX_p56, ID_IR, ID_R1, ID_R2, IF_IR, imm, MDout, MEM_IR,
       MEM_WB_aluresult_2, MEM_WB_lu_2, MEM_WB_readdata_2, MEM_Writedata, multiplexer_1_out,
       multiplexer_8_out, multiplexer_9_out, multiplexer_10_out, multiplexer_12_out, multiplexer_13_out,
       PC_4, shifter_1_out, shifter_2_out, shifter_4_out, WB_IR;
  wire [31:2] MEM_ALUresult;

  Button \u_总复位  (.out(RST));
  Button _1 (.out(IR1));
  Button _2 (.out(IR2));
  Button _3 (.out(IR3));
  // Probe on \总周期数 
  // Probe on \总周期数 
  Button u_go (.out(Go));
  LED #(.active("true")) led_1 (.in(W1));
  LED #(.active("true")) led_2 (.in(W2));
  LED #(.active("true")) led_3 (.in(W3));
  Hex_Digit_Display hex_digit_display_1 (.value(LedData[31:28]));  // open: dp
  // Probe on IF_PC[19:0]
  // RiscV_Probe riscv_probe_1: pin names not known; wires that end beside it: IF_IR
  Hex_Digit_Display hex_digit_display_2 (.value(LedData[27:24]));  // open: dp
  Hex_Digit_Display hex_digit_display_3 (.value(LedData[23:20]));  // open: dp
  // Probe on ID_PC[19:0]
  // RiscV_Probe riscv_probe_2: pin names not known; wires that end beside it: ID_IR
  Hex_Digit_Display hex_digit_display_4 (.value(LedData[19:16]));  // open: dp
  Hex_Digit_Display hex_digit_display_5 (.value(LedData[15:12]));  // open: dp
  Hex_Digit_Display hex_digit_display_6 (.value(LedData[11:8]));  // open: dp
  Hex_Digit_Display hex_digit_display_7 (.value(LedData[7:4]));  // open: dp
  // Probe on EX_PC[19:0]
  // RiscV_Probe riscv_probe_3: pin names not known; wires that end beside it: EX_IR
  Multiplexer #(.select(3), .width(32), .disabled("Z"), .enable("false")) multiplexer_1 (
    .in0(PC_4), .in1(BJ), .in2(ALUresult), .in3({32{1'b0}}), .in4(DJ), .in5({32{1'b0}}), .in6({32{1'b0}}),
    .in7({32{1'b0}}), .out(multiplexer_1_out), .sel({JAL, JALR, B}));
  not not_1 (not_1_out, multiplexer_2_out);
  Multiplexer #(.select(1), .width(1), .disabled("Z"), .enable("false")) multiplexer_2 (
    .in0(stall), .in1(not_2_out), .out(multiplexer_2_out), .sel(halt));
  not not_2 (not_2_out, Go);
  Hex_Digit_Display hex_digit_display_8 (.value(LedData[3:0]));  // open: dp
  Register #(.width(32), .trigger("rising"), .Select("low")) PC (
    .D(multiplexer_1_out), .en(not_1_out), .Q(IF_PC), .clk(CLK), .clr(RST));
  // Probe on \总周期数 
  // Probe on M_PC[19:0]
  // RiscV_Probe riscv_probe_4: pin names not known; wires that end beside it: MEM_IR
  // Probe on \总周期数 
  // Probe on \无条件分支数 
  // Probe on \条件分支成功数 
  // Probe on \插入气泡数 
  // Probe on \LoadUse次数 
  not not_3 (not_3_out, halt);
  Counter #(.width(16), .max('hffff), .ongoal("wrap"), .trigger("rising"), .behavior("new")) counter_1 (
    .count(not_3_out), .Q(\总周期数 ), .clk(CLK), .clr(RST));  // open: load, D, carry, preset, down
  Adder #(.width(32)) adder_1 (.a(IF_PC), .b(32'h4), .out(PC_4));  // open: cin, cout
  // Probe on IF_PC[11:0]
  // Probe on WB_PC[19:0]
  // RiscV_Probe riscv_probe_5: pin names not known; wires that end beside it: WB_IR
  ROM #(.addrWidth(10), .dataWidth(32), .Select("high")) rom_1 (.addr(IF_PC[11:2]), .data(IF_IR));
  // Probe on ID_PC[11:0]
  // Probe on EX_PC[11:0]
  not not_4 (not_4_out, halt);
  // Probe on M_PC[11:0]
  D_Flip_Flop #(.trigger("high"), .Pre_Clr_Positions("LEGACY"), .NegatePresetClear("false"), .enable("true"), .NewFFLayout("false")) d_ff_1 (.Q(d_ff_1_q));  // open: clk, D, Qn, preset, en, reset
  // Probe on 13'h8f7
  not not_5 (not_5_out, stall);
  and and_1 (and_1_out, not_4_out, not_5_out);
  IF_ID IF_ID (
    .en(and_1_out), .IR(IF_IR), .IR_2(ID_IR), .PC(IF_PC), .PC_2(ID_PC), .CLK(CLK), .RST(branch));  // open: PC_4, PC_4_2, PredictJump, PredictJump_2
  // Probe on WB_PC[11:0]
  Comparator #(.width(13), .mode("twosComplement")) comparator_1 (
    .a(CNT_num), .b(13'h8f7), .eq(comparator_1_eq), .lt(comparator_1_lt));  // open: gt
  Clock #(.highDuration(1), .lowDuration(1)) clock_1 (.out(clock_1_out));
  // RiscV_Probe riscv_probe_6: pin names not known; wires that end beside it: ID_IR, 5'b00001
  nand nand_1 (nand_1_out, d_ff_1_q, comparator_1_eq);
  Counter #(.width(13), .max('h1fff), .ongoal("stay"), .trigger("rising"), .behavior("old")) counter_2 (
    .count(comparator_1_lt), .Q(CNT_num), .clk(clock_1_out));  // open: load, D, carry, clr, preset
  assign CLK = nand_1_out ? clock_1_out : 1'bz;  // Controlled_Buffer controlled_buffer_1
  \重定向检测逻辑  \u_重定向检测逻辑_1  (
    .ID_IR(ID_IR), .EX_WriteReg_num(EX_W_num), .EX_RegWrite(EX_RegWrite), .MEM_WriteReg_num(MEM_W_num),
    .MEM_RegWrite(MEM_RegWrite), .EX_MemRead(EX_MemtoReg), .RtForward(Rtf), .RsForward(Rsf), .LoadUse(stall),
    .EX_IR(EX_IR));
  \单周期硬布线控制器  \u_单周期硬布线控制器_1  (
    .Funct({ID_IR[30], ID_IR[25], ID_IR[14:12]}), .OP(ID_IR[6:2]), .ALU_OP(\单周期硬布线控制器_1_alu_op ),
    .MemToReg(\单周期硬布线控制器_1_memtoreg ), .MemWrite(\单周期硬布线控制器_1_memwrite ), .ALU_SRC(\单周期硬布线控制器_1_alu_src ),
    .RegWrite(\单周期硬布线控制器_1_regwrite ), .ecall(ecall), .S_type(\单周期硬布线控制器_1_s_type ),
    .Jalr(\单周期硬布线控制器_1_jalr ), .Beq(\单周期硬布线控制器_1_beq ), .JAL(\单周期硬布线控制器_1_jal ), .Bne(\单周期硬布线控制器_1_bne ),
    .in_3(ID_IR[21]), .uret(\单周期硬布线控制器_1_uret ), .sb(\单周期硬布线控制器_1_sb ), .lui(\单周期硬布线控制器_1_lui ),
    .srl(\单周期硬布线控制器_1_srl ), .blt(\单周期硬布线控制器_1_blt ));  // open: CSRRSI, CSRRCI
  Multiplexer #(.select(1), .width(5), .disabled("Z"), .enable("false")) multiplexer_3 (
    .in0(ID_IR[19:15]), .in1(5'b10001), .out(multiplexer_3_out), .sel(ecall));
  Multiplexer #(.select(1), .width(5), .disabled("Z"), .enable("false")) multiplexer_4 (
    .in0(ID_IR[24:20]), .in1(5'b01010), .out(multiplexer_4_out), .sel(ecall));
  Multiplexer #(.select(1), .width(12), .disabled("Z"), .enable("false")) multiplexer_5 (
    .in0(ID_IR[31:20]), .in1({ID_IR[31:25], ID_IR[11:7]}), .out(multiplexer_5_out), .sel(\单周期硬布线控制器_1_s_type ));
  assign bit_extender_1_out = {{20{multiplexer_5_out[11]}}, multiplexer_5_out};  // Bit_Extender bit_extender_1
  assign bit_extender_2_out = {{20{ID_IR[31]}}, {ID_IR[31], ID_IR[7], ID_IR[30:25], ID_IR[11:8]}};  // Bit_Extender bit_extender_2
  assign bit_extender_3_out = {{12{ID_IR[31]}}, {ID_IR[31], ID_IR[19:12], ID_IR[20], ID_IR[30:21]}};  // Bit_Extender bit_extender_3
  Comparator #(.width(32), .mode("twosComplement")) comparator_2 (
    .a(EX_R1), .b(32'h22), .eq(comparator_2_eq));  // open: gt, lt
  Pull_Resistor #(.pull(1)) pull_resistor_1 (.node(CLK));
  Shifter #(.width(32), .shift("ll")) shifter_1 (.in(bit_extender_2_out), .\dist (5'b00001), .out(shifter_1_out));
  Shifter #(.width(32), .shift("ll")) shifter_2 (.in(bit_extender_3_out), .\dist (5'b00001), .out(shifter_2_out));
  and and_2 (and_2_out, EX_ecall, comparator_2_eq);
  not not_6 (not_6_out, comparator_2_eq);
  and and_3 (and_3_out, not_6_out, EX_ecall);
  Register #(.width(32), .trigger("rising"), .Select("low")) register_1 (
    .D(EX_R2), .en(and_2_out), .Q(LedData), .clk(CLK));  // open: clr
  and and_4 (and_4_out, Beq, eq);
  and and_5 (and_5_out, Bne, not_7_out);
  not not_7 (not_7_out, eq);
  and and_6 (and_6_out, blt, less);
  not not_8 (not_8_out, CLK);
  Regifile regifile_1 (
    .Din(RDin), .Clk(not_8_out), .R1(ID_R1), .R2(ID_R2), .WE(RegWrite), .W_num(WB_W_num),
    .R1_num(multiplexer_3_out), .R2_num(multiplexer_4_out));
  or or_1 (B, and_4_out, and_5_out, and_6_out);
  not not_9 (not_9_out, halt);
  or or_2 (branch, B, RST, JALR, JAL);
  or or_3 (or_3_out, stall, branch);
  // ID_EX ID_EX: pin names not known; wires that end beside it: not_9_out, \单周期硬布线控制器_1_beq , \单周期硬布线控制器_1_bne , \单周期硬布线控制器_1_blt , \单周期硬布线控制器_1_memtoreg , \单周期硬布线控制器_1_memwrite , \单周期硬布线控制器_1_alu_op , \单周期硬布线控制器_1_alu_src , \单周期硬布线控制器_1_regwrite , \单周期硬布线控制器_1_jal , \单周期硬布线控制器_1_jalr , \单周期硬布线控制器_1_lui , \单周期硬布线控制器_1_srl , \单周期硬布线控制器_1_sb , \单周期硬布线控制器_1_uret , Rtf, Rsf, ecall, ID_R1, ID_R2, ID_IR[11:7], bit_extender_1_out, ID_PC, ID_IR, shifter_1_out, shifter_2_out, {ID_IR[31:12], {12{1'b0}}}, ID_EX_p28, ID_EX_p28, CLK, or_3_out, Beq, Bne, blt, EX_MemtoReg, ID_EX_p36, ID_EX_p37, ID_EX_p38, EX_RegWrite, JAL, JALR, ID_EX_p42, srl, ID_EX_p44, ID_EX_p45, ID_EX_p46, EX_ecall, ID_EX_p48, ID_EX_p49, EX_W_num, imm, EX_PC, EX_IR, ID_EX_p54, ID_EX_p55, ID_EX_p56
  Counter #(.width(16), .max('hffff), .ongoal("wrap"), .trigger("rising"), .behavior("new")) counter_3 (
    .count(B), .Q(\条件分支成功数 ), .clk(CLK), .clr(RST));  // open: load, D, carry, preset, down
  Multiplexer #(.select(2), .width(32), .disabled("Z"), .enable("false")) multiplexer_6 (
    .in0(ID_EX_p48), .in1(RDin), .in2({MEM_ALUresult, byte_ad}), .out(EX_R1), .sel(ID_EX_p46));  // open: in3
  Multiplexer #(.select(2), .width(32), .disabled("Z"), .enable("false")) multiplexer_7 (
    .in0(ID_EX_p49), .in1(RDin), .in2({MEM_ALUresult, byte_ad}), .out(EX_R2), .sel(ID_EX_p45));  // open: in3
  Multiplexer #(.select(1), .width(32), .disabled("Z"), .enable("false")) multiplexer_8 (
    .in0(EX_R2), .in1(imm), .out(multiplexer_8_out), .sel(ID_EX_p38));
  assign bit_extender_4_out = {{27{EX_R2[4]}}, EX_R2[4:0]};  // Bit_Extender bit_extender_4
  Adder #(.width(32)) adder_2 (.a(ID_EX_p54), .b(EX_PC), .out(BJ));  // open: cin, cout
  or or_4 (or_4_out, JAL, JALR);
  Multiplexer #(.select(1), .width(32), .disabled("Z"), .enable("false")) multiplexer_9 (
    .in0(multiplexer_8_out), .in1(bit_extender_4_out), .out(multiplexer_9_out), .sel(srl));
  Adder #(.width(32)) adder_3 (.a(ID_EX_p55), .b(EX_PC), .out(DJ));  // open: cin, cout
  Counter #(.width(16), .max('hffff), .ongoal("wrap"), .trigger("rising"), .behavior("new")) counter_4 (
    .count(or_4_out), .Q(\无条件分支数 ), .clk(CLK), .clr(RST));  // open: load, D, carry, preset, down
  EX_MEM EX_MEM (
    .RegWrite(EX_RegWrite), .MemToReg(EX_MemtoReg), .MemWrite(ID_EX_p36), .AluResult(ALUresult),
    .WriteData(EX_R2), .WriteReg_num(EX_W_num), .PC(EX_PC), .IR(EX_IR), .JAL(JAL), .JALR(JALR),
    .lui(ID_EX_p42), .sb(ID_EX_p44), .RegWrite_2(MEM_RegWrite), .MemToReg_2(EX_MEM_memtoreg_2),
    .MemWrite_2(MemWrite), .AluResult_2({MEM_ALUresult, byte_ad}), .WriteData_2(MEM_Writedata),
    .WriteReg_num_2(MEM_W_num), .PC_2(M_PC), .IR_2(MEM_IR), .JAL_2(EX_MEM_jal_2), .JALR_2(EX_MEM_jalr_2),
    .lui_2(EX_MEM_lui_2), .sb_2(sb), .CLK(CLK), .lu(ID_EX_p56), .lu_2(EX_MEM_lu_2), .RST(RST), .en(en),
    .halt(and_3_out), .halt_2(EX_MEM_halt_2));  // open: Bj, bj_2
  ALU alu_1 (
    .X(EX_R1), .Y(multiplexer_9_out), .AluOP(ID_EX_p37), .Equal(eq), .Result(ALUresult), .out_6(less));  // open: Result_2, out_4
  assign bit_extender_5_out = {{3{1'b0}}, byte_ad};  // Bit_Extender bit_extender_5
  Multiplexer #(.select(2), .width(32), .disabled("Z"), .enable("false")) multiplexer_10 (
    .in0(32'hffffff00), .in1(32'hffff00ff), .in2(32'hff00ffff), .in3(32'hffffff), .out(multiplexer_10_out),
    .sel(byte_ad));
  Shifter #(.width(5), .shift("ll")) shifter_3 (.in(bit_extender_5_out), .\dist (3'b011), .out(shifter_3_out));
  assign and_7_out = multiplexer_10_out & MDout;  // AND_Gate and_7, 32 bits wide
  Shifter #(.width(32), .shift("ll")) shifter_4 (.in(MEM_Writedata), .\dist (shifter_3_out), .out(shifter_4_out));
  RAM #(.addrWidth(10), .dataWidth(32), .bus("separate"), .Select("high")) ram_1 (
    .addr(MEM_ALUresult[11:2]), .din(MDin), .data(MDout), .str(MemWrite), .clk(CLK), .ld(1'b1), .clr(RST));  // open: sel
  Adder #(.width(32)) adder_4 (.a(and_7_out), .b(shifter_4_out), .out(adder_4_out));  // open: cin, cout
  Adder #(.width(16)) adder_5 (.a(\条件分支成功数 ), .b(\无条件分支数 ), .out(adder_5_out));  // open: cin, cout
  not not_10 (not_10_out, halt);
  and and_8 (and_8_out, not_10_out, stall);
  MEM_WB MEM_WB (
    .RegWrite(MEM_RegWrite), .MemToReg(EX_MEM_memtoreg_2), .AluResult({MEM_ALUresult, byte_ad}),
    .ReadData(MDout), .WriteReg_num(MEM_W_num), .PC(M_PC), .IR(MEM_IR), .JAL(EX_MEM_jal_2),
    .JALR(EX_MEM_jalr_2), .lui(EX_MEM_lui_2), .RegWrite_2(RegWrite), .MemToReg_2(MEM_WB_memtoreg_2),
    .AluResult_2(MEM_WB_aluresult_2), .ReadData_2(MEM_WB_readdata_2), .WriteReg_num_2(WB_W_num),
    .PC_2(WB_PC), .IR_2(WB_IR), .JAL_2(MEM_WB_jal_2), .JALR_2(MEM_WB_jalr_2), .lui_2(MEM_WB_lui_2),
    .CLK(CLK), .RST(RST), .en(en), .halt(EX_MEM_halt_2), .halt_2(MEM_WB_halt_2), .lu(EX_MEM_lu_2),
    .lu_2(MEM_WB_lu_2));
  not not_11 (not_11_out, Go);
  Multiplexer #(.select(1), .width(32), .disabled("Z"), .enable("false")) multiplexer_11 (
    .in0(MEM_Writedata), .in1(adder_4_out), .out(MDin), .sel(sb));
  Shifter #(.width(16), .shift("ll")) shifter_5 (.in(adder_5_out), .\dist (4'b0001), .out(shifter_5_out));
  Counter #(.width(16), .max('hffff), .ongoal("wrap"), .trigger("rising"), .behavior("new")) counter_5 (
    .count(and_8_out), .Q(\LoadUse次数 ), .clk(CLK), .clr(RST));  // open: load, D, carry, preset, down
  Multiplexer #(.select(1), .width(32), .disabled("Z"), .enable("false")) multiplexer_12 (
    .in0(MEM_WB_aluresult_2), .in1(MEM_WB_readdata_2), .out(multiplexer_12_out), .sel(MEM_WB_memtoreg_2));
  Adder #(.width(32)) adder_6 (.a(WB_PC), .b(32'h4), .out(adder_6_out));  // open: cin, cout
  and and_9 (halt, MEM_WB_halt_2, not_11_out);
  not not_12 (en, halt);
  Adder #(.width(16)) adder_7 (.a(shifter_5_out), .b(\LoadUse次数 ), .out(\插入气泡数 ));  // open: cin, cout
  or or_5 (or_5_out, MEM_WB_jalr_2, MEM_WB_jal_2);
  Multiplexer #(.select(1), .width(32), .disabled("Z"), .enable("false")) multiplexer_13 (
    .in0(multiplexer_12_out), .in1(adder_6_out), .out(multiplexer_13_out), .sel(or_5_out));
  Multiplexer #(.select(1), .width(32), .disabled("Z"), .enable("false")) multiplexer_14 (
    .in0(multiplexer_13_out), .in1(MEM_WB_lu_2), .out(RDin), .sel(MEM_WB_lui_2));

  // Other names for the same wires on the sheet: MEM_ALUresult[1:0] = byte_ad; MEM_PC[31:0] = M_PC

  // Notes on the sheet:
  //   中断源
  //   时空图监测，可删除
  //   中断等待指示
  //   数码管输出
  //   指令存储器
  //   contents of rom_1 (hex, n*v repeats v):
  //   100493 100006f 100493 200913 300993 100006f 100493 200913 300993 100006f 100493 200913 300993
  //   100006f 100493 200913 300993 3b8000ef 100413 100493 1f49493 900533 2200893 73 24d493 48463 fedff06f
  //   900533 2200893 73 100493 249493 900533 2200893 73 48463 fedff06f 100493 1f49493 900533 2200893 73
  //   4034d493 900533 2200893 73 4044d493 900533 2200893 73 4044d493 900533 2200893 73 4044d493 900533
  //   2200893 73 4044d493 900533 2200893 73 4044d493 900533 2200893 73 4044d493 900533 2200893 73 4044d493
  //   900533 2200893 73 100413 1f41993 41f9d993 433 c00913 300b13 140413 f47413 800293 100313 499993
  //   89e9b3 1300533 2200893 73 406282b3 fe0294e3 140413 f00f93 1f47433 1c41413 800293 100313 49d993
  //   89e9b3 1300533 2200893 73 406282b3 fe0294e3 1c45413 406b0b33 b0463 f95ff06f 2b3 fff2c293 829293
  //   ff2e293 500533 2200893 73 fff00413 493 84a023 140413 448493 84a023 140413 448493 84a023 140413
  //   448493 84a023 140413 448493 84a023 140413 448493 84a023 140413 448493 84a023 140413 448493 84a023
  //   140413 448493 84a023 140413 448493 84a023 140413 448493 84a023 140413 448493 84a023 140413 448493
  //   84a023 140413 448493 84a023 140413 448493 84a023 140413 448493 84a023 140413 448493 140413 433
  //   3c00493 42983 4aa03 149a2b3 28663 134a023 1442023 ffc48493 fe9412e3 800533 2200893 73 440413 3c00493
  //   fc9416e3 a00893 73 100293 300313 800493 849493 7648493 1449493 900533 2200893 73 800e13 54d4b3
  //   64d4b3 900533 2200893 73 fffe0e13 fe0e14e3 a00893 73 800e13 fedc04b7 fff00413 1045413 84e4b3 900533
  //   2200893 73 ba984b7 900533 73 76544b7 900533 73 32104b7 900533 73 fffe0e13 fa0e1ee3 a00893 73 313
  //   2000e13 493 100913 930023 900533 2200893 73 12484b3 130313 fffe0e13 fe0e12e3 800e13 313 32483 900533
  //   2200893 73 430313 fffe0e13 fe0e14e3 a00893 73 ff100493 900533 2200893 73 148493 fe04c8e3 a00893 73
  //   413 140413 800533 2200893 73 240413 800533 2200893 73 340413 800533 2200893 73 440413 800533 2200893
  //   73 540413 800533 2200893 73 640413 800533 2200893 73 740413 800533 2200893 73 840413 800533 2200893
  //   2200893 73 8067
  //   控制位
  //   流水调试日志用
  //   暂停节拍，不能为0
  //   戳工具置1进入计数暂停模式，ctrl+k时钟自动运行到对应节拍暂停
  //   ctrl+k关闭时钟连续运行，将控制位置零，进入单步调试模式调试
  //   指令探针
  //   可计数暂停的时钟源
  //   Beq
  //   Bne
  //   为方便自动评测，需要输出流水线各段保存的PC值，注意是PC不是PC+4，另外ID段寄存器写入信息，Mem段内存写入信息也要输出
  //   R2
endmodule

module \单周期_单级中断  (
  input  IR1,
  input  IR2,
  input  IR3,
  output RegWrite,
  output MemWrite,
  output [31:0] PC,
  output [31:0] IR,
  output [31:0] RDin,
  output [31:0] MDin,
  output [31:0] LedData
);

  wire ALUSrc, and_1_out, and_3_out, and_4_out, and_5_out, and_7_out, and_8_out, and_10_out, B, Beq, Blt,
       Bne, CLK, clock_1_out, comparator_1_eq, comparator_2_eq, comparator_3_eq, comparator_4_eq,
       comparator_5_eq, comparator_6_eq, comparator_6_lt, d_ff_1_q, d_ff_2_q, d_ff_3_q, d_ff_4_q,
       demultiplexer_1_out1, demultiplexer_1_out2, demultiplexer_1_out3, ecall, eq, Go, halt, IE_q, Interr,
       InterrEN, Interrupt1, Interrupt2, Interrupt3, IR1_t, IR2_t, IR3_t, IRA, IRB, IRC, JAL, JALR, less,
       lui, MemToReg, nand_1_out, not_1_out, not_2_out, not_3_out, not_4_out, not_5_out, not_6_out, or_1_out,
       or_5_out, or_10_out, or_11_out, or_12_out, or_13_out, RST, sb, srl, uret, uret1, uret2, uret3, W1, W2,
       W3, \单周期硬布线控制器_1_s_type ;
  wire [1:0] priority_encoder_1_out, retReg_q;
  wire [3:0] ALUop;
  wire [4:0] bit_extender_5_out, multiplexer_4_out, multiplexer_7_out, shifter_3_out;
  wire [11:0] multiplexer_5_out;
  wire [12:0] CNT_num;
  wire [15:0] \分支成功数 , \总周期数 ;
  wire [31:0] adder_4_out, ALUresult, and_6_out, bit_extender_1_out, bit_extender_2_out, bit_extender_4_out,
       BJ, DJ, EPC, imm12, InterrAddr, MDout, multiplexer_2_out, multiplexer_3_out, multiplexer_6_out,
       multiplexer_8_out, multiplexer_10_out, multiplexer_11_out, multiplexer_12_out, nextPC, PC_4, R1, R2,
       shifter_1_out, shifter_2_out, shifter_4_out;

  Button \u_继续运行  (.out(Go));
  Button _1 ();  // open: out
  Button _2 ();  // open: out
  Button _3 ();  // open: out
  Button u_RST (.out(RST));
  LED #(.active("true")) led_1 (.in(W1));
  LED #(.active("true")) led_2 (.in(W2));
  LED #(.active("true")) led_3 (.in(W3));
  Hex_Digit_Display hex_digit_display_1 (.value(LedData[31:28]));  // open: dp
  Hex_Digit_Display hex_digit_display_2 (.value(LedData[27:24]));  // open: dp
  Hex_Digit_Display hex_digit_display_3 (.value(LedData[23:20]));  // open: dp
  Hex_Digit_Display hex_digit_display_4 (.value(LedData[19:16]));  // open: dp
  Hex_Digit_Display hex_digit_display_5 (.value(LedData[15:12]));  // open: dp
  Comparator #(.width(16), .mode("twosComplement")) comparator_1 (
    .a(16'h23b), .b(\总周期数 ), .eq(comparator_1_eq));  // open: gt, lt
  Comparator #(.width(16), .mode("twosComplement")) comparator_2 (
    .a(\总周期数 ), .b(16'h1), .eq(comparator_2_eq));  // open: gt, lt
  Comparator #(.width(16), .mode("twosComplement")) comparator_3 (
    .a(\总周期数 ), .b(16'h4), .eq(comparator_3_eq));  // open: gt, lt
  Comparator #(.width(16), .mode("twosComplement")) comparator_4 (
    .a(\总周期数 ), .b(16'h7), .eq(comparator_4_eq));  // open: gt, lt
  Hex_Digit_Display hex_digit_display_6 (.value(LedData[11:8]));  // open: dp
  Hex_Digit_Display hex_digit_display_7 (.value(LedData[7:4]));  // open: dp
  // Probe on \总周期数 
  Multiplexer #(.select(3), .width(32), .disabled("Z"), .enable("false")) multiplexer_1 (
    .in0(PC_4), .in1(BJ), .in2(ALUresult), .in3({32{1'b0}}), .in4(DJ), .in5({32{1'b0}}), .in6({32{1'b0}}),
    .in7({32{1'b0}}), .out(nextPC), .sel({JAL, JALR, B}));
  or or_1 (or_1_out, comparator_1_eq, comparator_2_eq);
  assign IRA = or_1_out ? ~CLK : 1'bz;  // Controlled_Inverter controlled_inverter_1
  assign IRB = comparator_3_eq ? ~CLK : 1'bz;  // Controlled_Inverter controlled_inverter_2
  assign IRC = comparator_4_eq ? ~CLK : 1'bz;  // Controlled_Inverter controlled_inverter_3
  Hex_Digit_Display hex_digit_display_8 (.value(LedData[3:0]));  // open: dp
  not not_1 (not_1_out, halt);
  Counter #(.width(16), .max('hffff), .ongoal("wrap"), .trigger("rising"), .behavior("new")) counter_1 (
    .count(not_1_out), .Q(\总周期数 ), .clk(CLK), .clr(RST));  // open: load, D, carry, preset, down
  Multiplexer #(.select(1), .width(32), .disabled("Z"), .enable("false")) multiplexer_2 (
    .in0(nextPC), .in1(InterrAddr), .out(multiplexer_2_out), .sel(InterrEN));
  Pull_Resistor #(.pull(0)) pull_resistor_1 (.node(IRA));
  Pull_Resistor #(.pull(0)) pull_resistor_2 (.node(IRB));
  Pull_Resistor #(.pull(0)) pull_resistor_3 (.node(IRC));
  Multiplexer #(.select(1), .width(32), .disabled("Z"), .enable("false")) multiplexer_3 (
    .in0(multiplexer_2_out), .in1(EPC), .out(multiplexer_3_out), .sel(uret));
  not not_2 (not_2_out, halt);
  or or_2 (IR1_t, IR1, IRA);
  Register #(.width(32), .trigger("rising"), .Select("low")) u_PC (
    .D(multiplexer_3_out), .en(not_2_out), .Q(PC), .clk(CLK), .clr(RST));
  or or_3 (IR2_t, IR2, IRB);
  Comparator #(.width(32), .mode("twosComplement")) comparator_5 (
    .a(R1), .b(32'h22), .eq(comparator_5_eq));  // open: gt, lt
  Adder #(.width(32)) adder_1 (.a(PC), .b(32'h4), .out(PC_4));  // open: cin, cout
  and and_1 (and_1_out, ecall, comparator_5_eq);
  not not_3 (not_3_out, comparator_5_eq);
  and and_2 (halt, not_3_out, ecall, not_4_out);
  not not_4 (not_4_out, Go);
  // RiscV_Probe riscv_probe_1: pin names not known; wires that end beside it: IR, IR[21], IR[6:2]
  ROM #(.addrWidth(10), .dataWidth(32), .Select("high")) rom_1 (.addr(PC[11:2]), .data(IR));
  or or_4 (IR3_t, IR3, IRC);
  Register #(.width(32), .trigger("rising"), .Select("low")) register_1 (
    .D(R2), .en(and_1_out), .Q(LedData), .clk(CLK));  // open: clr
  \单周期硬布线控制器  \u_单周期硬布线控制器_1  (
    .Funct({IR[30], IR[25], IR[14:12]}), .OP(IR[6:2]), .ALU_OP(ALUop), .MemToReg(MemToReg),
    .MemWrite(MemWrite), .ALU_SRC(ALUSrc), .RegWrite(RegWrite), .ecall(ecall), .S_type(\单周期硬布线控制器_1_s_type ),
    .Jalr(JALR), .Beq(Beq), .JAL(JAL), .Bne(Bne), .in_3(IR[21]), .uret(uret), .sb(sb), .lui(lui), .srl(srl),
    .blt(Blt));  // open: CSRRSI, CSRRCI
  Multiplexer #(.select(1), .width(5), .disabled("Z"), .enable("false")) multiplexer_4 (
    .in0(IR[24:20]), .in1(5'b01010), .out(multiplexer_4_out), .sel(ecall));
  Multiplexer #(.select(1), .width(12), .disabled("Z"), .enable("false")) multiplexer_5 (
    .in0(IR[31:20]), .in1({IR[31:25], IR[11:7]}), .out(multiplexer_5_out), .sel(\单周期硬布线控制器_1_s_type ));
  assign bit_extender_1_out = {{20{IR[31]}}, {IR[31], IR[7], IR[30:25], IR[11:8]}};  // Bit_Extender bit_extender_1
  assign bit_extender_2_out = {{12{IR[31]}}, {IR[31], IR[19:12], IR[20], IR[30:21]}};  // Bit_Extender bit_extender_2
  Multiplexer #(.select(1), .width(32), .disabled("Z"), .enable("false")) multiplexer_6 (
    .in0(ALUresult), .in1(MDout), .out(multiplexer_6_out), .sel(MemToReg));
  Multiplexer #(.select(1), .width(5), .disabled("Z"), .enable("false")) multiplexer_7 (
    .in0(IR[19:15]), .in1(5'b10001), .out(multiplexer_7_out), .sel(ecall));
  assign imm12 = {{20{multiplexer_5_out[11]}}, multiplexer_5_out};  // Bit_Extender bit_extender_3
  Shifter #(.width(32), .shift("ll")) shifter_1 (.in(bit_extender_1_out), .\dist (5'b00001), .out(shifter_1_out));
  Shifter #(.width(32), .shift("ll")) shifter_2 (.in(bit_extender_2_out), .\dist (5'b00001), .out(shifter_2_out));
  or or_5 (or_5_out, JALR, JAL);
  Multiplexer #(.select(1), .width(32), .disabled("Z"), .enable("false")) multiplexer_8 (
    .in0(multiplexer_6_out), .in1(PC_4), .out(multiplexer_8_out), .sel(or_5_out));
  Multiplexer #(.select(1), .width(32), .disabled("Z"), .enable("false")) multiplexer_9 (
    .in0(multiplexer_8_out), .in1({IR[31:12], {12{1'b0}}}), .out(RDin), .sel(lui));
  Regifile regifile_1 (
    .Din(RDin), .Clk(CLK), .R1(R1), .R2(R2), .WE(RegWrite), .W_num(IR[11:7]), .R1_num(multiplexer_7_out),
    .R2_num(multiplexer_4_out));
  Adder #(.width(32)) adder_2 (.a(shifter_1_out), .b(PC), .out(BJ));  // open: cin, cout
  Adder #(.width(32)) adder_3 (.a(shifter_2_out), .b(PC), .out(DJ));  // open: cin, cout
  and and_3 (and_3_out, Beq, eq);
  and and_4 (and_4_out, Bne, not_5_out);
  not not_5 (not_5_out, eq);
  and and_5 (and_5_out, less, Blt);
  or or_6 (B, and_3_out, and_4_out, and_5_out);
  Multiplexer #(.select(1), .width(32), .disabled("Z"), .enable("false")) multiplexer_10 (
    .in0(R2), .in1(imm12), .out(multiplexer_10_out), .sel(ALUSrc));
  assign bit_extender_4_out = {{27{R2[4]}}, R2[4:0]};  // Bit_Extender bit_extender_4
  assign bit_extender_5_out = {{3{1'b0}}, ALUresult[1:0]};  // Bit_Extender bit_extender_5
  D_Flip_Flop #(.trigger("high"), .Pre_Clr_Positions("LEGACY"), .NegatePresetClear("false"), .enable("true"), .NewFFLayout("false")) d_ff_1 (.Q(d_ff_1_q));  // open: clk, D, Qn, preset, en, reset
  // Probe on 13'hb8
  Counter #(.width(16), .max('hffff), .ongoal("wrap"), .trigger("rising"), .behavior("new")) counter_2 (
    .count(B), .Q(\分支成功数 ), .clk(CLK), .clr(RST));  // open: load, D, carry, preset, down
  ALU alu_1 (
    .X(R1), .Y(multiplexer_11_out), .AluOP(ALUop), .Equal(eq), .Result(ALUresult), .out_6(less));  // open: Result_2, out_4
  Multiplexer #(.select(1), .width(32), .disabled("Z"), .enable("false")) multiplexer_11 (
    .in0(multiplexer_10_out), .in1(bit_extender_4_out), .out(multiplexer_11_out), .sel(srl));
  Multiplexer #(.select(2), .width(32), .disabled("Z"), .enable("false")) multiplexer_12 (
    .in0(32'hffffff00), .in1(32'hffff00ff), .in2(32'hff00ffff), .in3(32'hffffff), .out(multiplexer_12_out),
    .sel(ALUresult[1:0]));
  assign and_6_out = multiplexer_12_out & MDout;  // AND_Gate and_6, 32 bits wide
  Shifter #(.width(5), .shift("ll")) shifter_3 (.in(bit_extender_5_out), .\dist (3'b011), .out(shifter_3_out));
  Comparator #(.width(13), .mode("twosComplement")) comparator_6 (
    .a(CNT_num), .b(13'hb8), .eq(comparator_6_eq), .lt(comparator_6_lt));  // open: gt
  Clock #(.highDuration(1), .lowDuration(1)) clock_1 (.out(clock_1_out));
  Adder #(.width(32)) adder_4 (.a(and_6_out), .b(shifter_4_out), .out(adder_4_out));  // open: cin, cout
  Shifter #(.width(32), .shift("ll")) shifter_4 (.in(R2), .\dist (shifter_3_out), .out(shifter_4_out));
  Counter #(.width(13), .max('h1fff), .ongoal("stay"), .trigger("rising"), .behavior("old")) counter_3 (
    .count(comparator_6_lt), .Q(CNT_num), .clk(clock_1_out));  // open: load, D, carry, clr, preset
  Multiplexer #(.select(1), .width(32), .disabled("Z"), .enable("false")) multiplexer_13 (
    .in0(R2), .in1(adder_4_out), .out(MDin), .sel(sb));
  nand nand_1 (nand_1_out, d_ff_1_q, comparator_6_eq);
  RAM #(.addrWidth(10), .dataWidth(32), .bus("separate"), .Select("high")) ram_1 (
    .addr(ALUresult[11:2]), .din(MDin), .data(MDout), .str(MemWrite), .clk(CLK), .ld(1'b1), .clr(RST));  // open: sel
  assign CLK = nand_1_out ? clock_1_out : 1'bz;  // Controlled_Buffer controlled_buffer_1
  Pull_Resistor #(.pull(1)) pull_resistor_4 (.node(CLK));
  D_Flip_Flop #(.trigger("rising"), .Pre_Clr_Positions("LEGACY"), .NegatePresetClear("false"), .enable("true"), .NewFFLayout("false")) d_ff_2 (
    .clk(IR1_t), .D(1'b1), .Q(d_ff_2_q), .reset(Interrupt1));  // open: Qn, preset, en
  or or_7 (W1, Interrupt1, d_ff_2_q);
  or or_8 (W2, Interrupt2, d_ff_3_q);
  or or_9 (W3, Interrupt3, d_ff_4_q);
  Priority_Encoder #(.select(2), .disabled("Z")) priority_encoder_1 (
    .in0(1'b0), .in1(Interrupt1), .in2(Interrupt2), .in3(Interrupt3), .out(priority_encoder_1_out),
    .gs(Interr));  // open: en_out, en_in
  or or_10 (or_10_out, InterrEN, uret);
  D_Flip_Flop #(.trigger("rising"), .Pre_Clr_Positions("LEGACY"), .NegatePresetClear("false"), .enable("true"), .NewFFLayout("false")) d_ff_3 (
    .clk(IR2_t), .D(1'b1), .Q(d_ff_3_q), .reset(Interrupt2));  // open: Qn, preset, en
  D_Flip_Flop #(.trigger("rising"), .Pre_Clr_Positions("LEGACY"), .NegatePresetClear("false"), .enable("true"), .NewFFLayout("false")) d_ff_4 (
    .clk(IR3_t), .D(1'b1), .Q(d_ff_4_q), .reset(Interrupt3));  // open: Qn, preset, en
  Multiplexer #(.select(2), .width(32), .disabled("Z"), .enable("false")) multiplexer_14 (
    .in1(32'h30ac), .in2(32'h3150), .in3(32'h31f4), .out(InterrAddr), .sel(priority_encoder_1_out));  // open: in0
  Register #(.width(1), .trigger("rising"), .Select("low")) IE (
    .D(InterrEN), .en(or_10_out), .Q(IE_q), .clk(CLK));  // open: clr
  Register #(.width(32), .trigger("rising"), .Select("low")) u_EPC (
    .D(nextPC), .en(InterrEN), .Q(EPC), .clk(CLK));  // open: clr
  or or_11 (or_11_out, d_ff_2_q, Interrupt1);
  or or_12 (or_12_out, d_ff_3_q, Interrupt2);
  and and_7 (and_7_out, or_12_out, ~uret2);  // AND_Gate
  or or_13 (or_13_out, d_ff_4_q, Interrupt3);
  and and_8 (and_8_out, or_13_out, ~uret3);  // AND_Gate
  Register #(.width(2), .trigger("rising"), .Select("low")) retReg (
    .D(priority_encoder_1_out), .en(InterrEN), .Q(retReg_q), .clk(CLK));  // open: clr
  not not_6 (not_6_out, IE_q);
  and and_9 (InterrEN, not_6_out, Interr);
  D_Flip_Flop #(.trigger("rising"), .Pre_Clr_Positions("LEGACY"), .NegatePresetClear("false"), .enable("true"), .NewFFLayout("false")) u_IR1 (
    .clk(CLK), .D(and_10_out), .Q(Interrupt1));  // open: Qn, preset, en, reset
  and and_10 (and_10_out, or_11_out, ~uret1);  // AND_Gate
  D_Flip_Flop #(.trigger("rising"), .Pre_Clr_Positions("LEGACY"), .NegatePresetClear("false"), .enable("true"), .NewFFLayout("false")) u_IR2 (
    .clk(CLK), .D(and_7_out), .Q(Interrupt2));  // open: Qn, preset, en, reset
  D_Flip_Flop #(.trigger("rising"), .Pre_Clr_Positions("LEGACY"), .NegatePresetClear("false"), .enable("true"), .NewFFLayout("false")) u_IR3 (
    .clk(CLK), .D(and_8_out), .Q(Interrupt3));  // open: Qn, preset, en, reset
  Demultiplexer #(.select(2), .width(1), .tristate("false"), .disabled("Z"), .enable("false")) demultiplexer_1 (
    .out1(demultiplexer_1_out1), .out2(demultiplexer_1_out2), .out3(demultiplexer_1_out3), .in(1'b1),
    .sel(retReg_q));  // open: out0
  and and_11 (uret1, uret, demultiplexer_1_out1);
  and and_12 (uret2, demultiplexer_1_out2, uret);
  and and_13 (uret3, demultiplexer_1_out3, uret);

  // Other names for the same wires on the sheet: byte_ad[1:0] = ALUresult[1:0]; lu[31:12] = IR[31:12]

  // Notes on the sheet:
  //   中断源
  //   中断等待指示
  //   总复位信号应将除ROM以外所有存储组件全部清零
  //   单级中断测试信号模拟器
  //   数码管输出
  //   数码管输出应该用寄存器锁存，否则显示数据只能一闪而过
  //   指令探针
  //   contents of rom_1 (hex, n*v repeats v):
  //   7d000113 100413 1f41993 41f9d993 433 c00913 800b13 140413 f47413 800293 100313 499993 89e9b3 1300533
  //   2200893 73 406282b3 fe0294e3 140413 f00f93 1f47433 1c41413 800293 100313 49d993 89e9b3 1300533
  //   2200893 73 406282b3 fe0294e3 1c45413 406b0b33 b0463 f95ff06f 2b3 fff2c293 1029293 fff2e293 500533
  //   2200893 73 f5dff06f 1112023 410113 a12023 410113 812023 410113 1312023 410113 1412023 410113 1512023
  //   410113 1612023 410113 100b13 300a13 100a93 1600433 441413 14469b3 1300533 2200893 73 fe0416e3
  //   415a0a33 fe0a10e3 ffc10113 12b03 ffc10113 12a83 ffc10113 12a03 ffc10113 12983 ffc10113 12403
  //   ffc10113 12503 ffc10113 12883 200073 1112023 410113 a12023 410113 812023 410113 1312023 410113
  //   1412023 410113 1512023 410113 1612023 410113 200b13 300a13 100a93 1600433 441413 14469b3 1300533
  //   2200893 73 fe0416e3 415a0a33 fe0a10e3 ffc10113 12b03 ffc10113 12a83 ffc10113 12a03 ffc10113 12983
  //   ffc10113 12403 ffc10113 12503 ffc10113 12883 200073 1112023 410113 a12023 410113 812023 410113
  //   1312023 410113 1412023 410113 1512023 410113 1612023 410113 300b13 300a13 100a93 1600433 441413
  //   14469b3 1300533 2200893 73 fe0416e3 415a0a33 fe0a10e3 ffc10113 12b03 ffc10113 12a83 ffc10113 12a03
  //   ffc10113 12983 ffc10113 12403 ffc10113 12503 ffc10113 12883 200073
  //   指令字
  //   B_type
  //   U_type
  //   为方便自动评测，需要输出PC，IR，寄存器堆写如数据RDin
  //   RAM写使能MemWrite、RAM写入数据MDin等信号
  //   控制位
  //   暂停节拍，不能为0
  //   戳工具置1进入计数暂停模式，ctrl+k时钟自动运行到对应节拍暂停
  //   ctrl+k关闭时钟连续运行，将控制位置零，进入单步调试模式调试
  //   可计数暂停的时钟源
  //   Reset 
  //   Reset 
  //   Reset 
endmodule

module \单周期_多级中断  (
  input  IR1,
  input  IR2,
  input  IR3,
  output RegWrite,
  output MemWrite,
  output [31:0] PC,
  output [31:0] IR,
  output [31:0] RDin,
  output [31:0] MDin,
  output [31:0] LedData
);

  wire ALUSrc, and_1_out, and_3_out, and_8_out, and_9_out, and_10_out, and_12_out, and_13_out, and_14_out, B,
       Beq, Blt, Bne, CLK, clock_1_out, comparator_1_eq, comparator_2_eq, comparator_3_eq, comparator_4_eq,
       comparator_5_eq, comparator_6_eq, comparator_7_eq, comparator_8_eq, comparator_8_lt, CSRRCI, CSRRSI,
       d_ff_1_q, d_ff_2_q, d_ff_3_q, d_ff_4_q, demultiplexer_1_out1, demultiplexer_1_out2,
       demultiplexer_1_out3, demultiplexer_2_out1, demultiplexer_2_out2, demultiplexer_2_out3,
       demultiplexer_3_out0, demultiplexer_3_out1, demultiplexer_3_out2, ecall, eq, Go, halt, Interr,
       InterrEN, Interrupt1, Interrupt2, Interrupt3, IR1_t, IR2_t, IR3_t, IRA, IRB, IRC, JAL, JALR, less,
       lui, MemToReg, nand_1_out, not_1_out, not_2_out, not_3_out, not_4_out, not_5_out, or_1_out, or_2_out,
       or_5_out, or_7_out, or_9_out, or_13_out, or_14_out, or_15_out, priority_encoder_1_gs,
       pull_resistor_1_node, pull_resistor_2_node, pull_resistor_3_node, RST, sb, shield, srl, uret, uret1,
       uret2, uret3, W1, W2, W3, \单周期硬布线控制器_1_s_type ;
  wire [1:0] counter_4_q, InterrNum, InterrPreNum, IR1_q, IR2_q, IR3_q;
  wire [3:0] ALUop;
  wire [4:0] bit_extender_5_out, multiplexer_5_out, multiplexer_7_out, shifter_3_out;
  wire [11:0] multiplexer_6_out;
  wire [12:0] CNT_num;
  wire [15:0] \分支成功数 , \总周期数 ;
  wire [31:0] adder_4_out, ALUresult, and_11_out, bit_extender_1_out, bit_extender_3_out, bit_extender_4_out,
       BJ, DJ, EPC, EPC1_q, EPC2_q, EPC3_q, imm12, InterrAddr, MDout, multiplexer_2_out, multiplexer_3_out,
       multiplexer_8_out, multiplexer_9_out, multiplexer_11_out, multiplexer_12_out, multiplexer_13_out,
       nextPC, PC_4, R1, R2, shifter_1_out, shifter_2_out, shifter_4_out;

  Button \u_继续运行  (.out(Go));
  Button _1 (.out(IRA));
  Button _2 (.out(IRB));
  Button _3 (.out(IRC));
  LED #(.active("true")) led_1 (.in(W1));
  LED #(.active("true")) led_2 (.in(W2));
  LED #(.active("true")) led_3 (.in(W3));
  Hex_Digit_Display hex_digit_display_1 (.value(LedData[31:28]));  // open: dp
  Comparator #(.width(16), .mode("twosComplement")) comparator_1 (
    .a(\总周期数 ), .b(16'h7), .eq(comparator_1_eq));  // open: gt, lt
  Comparator #(.width(16), .mode("twosComplement")) comparator_2 (
    .a(\总周期数 ), .b(16'h241), .eq(comparator_2_eq));  // open: gt, lt
  Hex_Digit_Display hex_digit_display_2 (.value(LedData[23:20]));  // open: dp
  Hex_Digit_Display hex_digit_display_3 (.value(LedData[27:24]));  // open: dp
  Comparator #(.width(16), .mode("twosComplement")) comparator_3 (
    .a(16'h258), .b(\总周期数 ), .eq(comparator_3_eq));  // open: gt, lt
  or or_1 (or_1_out, comparator_3_eq, comparator_4_eq);
  Comparator #(.width(16), .mode("twosComplement")) comparator_4 (
    .a(\总周期数 ), .b(16'h1), .eq(comparator_4_eq));  // open: gt, lt
  Comparator #(.width(16), .mode("twosComplement")) comparator_5 (
    .a(\总周期数 ), .b(16'h4), .eq(comparator_5_eq));  // open: gt, lt
  or or_2 (or_2_out, comparator_1_eq, comparator_2_eq);
  Hex_Digit_Display hex_digit_display_4 (.value(LedData[15:12]));  // open: dp
  Hex_Digit_Display hex_digit_display_5 (.value(LedData[19:16]));  // open: dp
  Pull_Resistor #(.pull(0)) pull_resistor_1 (.node(pull_resistor_1_node));
  assign pull_resistor_1_node = or_1_out ? ~CLK : 1'bz;  // Controlled_Inverter controlled_inverter_1
  Pull_Resistor #(.pull(0)) pull_resistor_2 (.node(pull_resistor_2_node));
  assign pull_resistor_2_node = comparator_5_eq ? ~CLK : 1'bz;  // Controlled_Inverter controlled_inverter_2
  Pull_Resistor #(.pull(0)) pull_resistor_3 (.node(pull_resistor_3_node));
  assign pull_resistor_3_node = or_2_out ? ~CLK : 1'bz;  // Controlled_Inverter controlled_inverter_3
  Hex_Digit_Display hex_digit_display_6 (.value(LedData[11:8]));  // open: dp
  Hex_Digit_Display hex_digit_display_7 (.value(LedData[7:4]));  // open: dp
  // Probe on \总周期数 
  Multiplexer #(.select(3), .width(32), .disabled("Z"), .enable("false")) multiplexer_1 (
    .in0(PC_4), .in1(BJ), .in2(ALUresult), .in3({32{1'b0}}), .in4(DJ), .in5({32{1'b0}}), .in6({32{1'b0}}),
    .in7({32{1'b0}}), .out(nextPC), .sel({JAL, JALR, B}));
  Hex_Digit_Display hex_digit_display_8 (.value(LedData[3:0]));  // open: dp
  not not_1 (not_1_out, halt);
  Counter #(.width(16), .max('hffff), .ongoal("wrap"), .trigger("rising"), .behavior("new")) counter_1 (
    .count(not_1_out), .Q(\总周期数 ), .clk(CLK), .clr(RST));  // open: load, D, carry, preset, down
  Multiplexer #(.select(1), .width(32), .disabled("Z"), .enable("false")) multiplexer_2 (
    .in0(nextPC), .in1(InterrAddr), .out(multiplexer_2_out), .sel(Interr));
  Multiplexer #(.select(1), .width(32), .disabled("Z"), .enable("false")) multiplexer_3 (
    .in0(multiplexer_2_out), .in1(EPC), .out(multiplexer_3_out), .sel(uret));
  not not_2 (not_2_out, halt);
  or or_3 (IR1_t, IR1, IRA);
  Register #(.width(32), .trigger("rising"), .Select("low")) u_PC (
    .D(multiplexer_3_out), .en(not_2_out), .Q(PC), .clk(CLK), .clr(RST));
  or or_4 (IR2_t, IR2, IRB);
  Comparator #(.width(32), .mode("twosComplement")) comparator_6 (
    .a(R1), .b(32'h22), .eq(comparator_6_eq));  // open: gt, lt
  Adder #(.width(32)) adder_1 (.a(PC), .b(32'h4), .out(PC_4));  // open: cin, cout
  Priority_Encoder #(.select(2), .disabled("Z")) priority_encoder_1 (
    .in0(1'b0), .in1(Interrupt1), .in2(Interrupt2), .in3(Interrupt3), .out(InterrNum),
    .gs(priority_encoder_1_gs));  // open: en_out, en_in
  Comparator #(.width(16), .mode("twosComplement")) comparator_7 (
    .a(\总周期数 ), .b({16{1'b0}}), .eq(comparator_7_eq));  // open: gt, lt
  and and_1 (and_1_out, ecall, comparator_6_eq);
  not not_3 (not_3_out, comparator_6_eq);
  not not_4 (not_4_out, Go);
  // RiscV_Probe riscv_probe_1: pin names not known; wires that end beside it: IR, IR[21], IR[6:2]
  Multiplexer #(.select(2), .width(32), .disabled("Z"), .enable("false")) multiplexer_4 (
    .in1(32'h30ac), .in2(32'h3158), .in3(32'h3204), .out(InterrAddr), .sel(InterrNum));  // open: in0
  and and_2 (Interr, priority_encoder_1_gs, InterrEN, shield);
  and and_3 (and_3_out, ~Interr, ~CSRRCI);  // AND_Gate
  or or_5 (or_5_out, CSRRCI, CSRRSI, Interr, uret, comparator_7_eq);
  or or_6 (IR3_t, IR3, IRC);
  Register #(.width(32), .trigger("rising"), .Select("low")) register_1 (
    .D(R2), .en(and_1_out), .Q(LedData), .clk(CLK));  // open: clr
  and and_4 (halt, not_3_out, ecall, not_4_out);
  ROM #(.addrWidth(10), .dataWidth(32), .Select("high")) rom_1 (.addr(PC[11:2]), .data(IR));
  Demultiplexer #(.select(2), .width(1), .tristate("false"), .disabled("Z"), .enable("false")) demultiplexer_1 (
    .out1(demultiplexer_1_out1), .out2(demultiplexer_1_out2), .out3(demultiplexer_1_out3), .in(1'b1),
    .sel(InterrNum));  // open: out0
  Register #(.width(1), .trigger("rising"), .Select("low")) IE (
    .D(and_3_out), .en(or_5_out), .Q(InterrEN), .clk(CLK));  // open: clr
  \单周期硬布线控制器  \u_单周期硬布线控制器_1  (
    .Funct({IR[30], IR[25], IR[14:12]}), .OP(IR[6:2]), .ALU_OP(ALUop), .MemToReg(MemToReg),
    .MemWrite(MemWrite), .ALU_SRC(ALUSrc), .RegWrite(RegWrite), .ecall(ecall), .S_type(\单周期硬布线控制器_1_s_type ),
    .Jalr(JALR), .Beq(Beq), .JAL(JAL), .Bne(Bne), .in_3(IR[21]), .uret(uret), .sb(sb), .lui(lui), .srl(srl),
    .blt(Blt), .CSRRSI(CSRRSI), .CSRRCI(CSRRCI));
  Multiplexer #(.select(1), .width(5), .disabled("Z"), .enable("false")) multiplexer_5 (
    .in0(IR[24:20]), .in1(5'b01010), .out(multiplexer_5_out), .sel(ecall));
  Multiplexer #(.select(1), .width(12), .disabled("Z"), .enable("false")) multiplexer_6 (
    .in0(IR[31:20]), .in1({IR[31:25], IR[11:7]}), .out(multiplexer_6_out), .sel(\单周期硬布线控制器_1_s_type ));
  assign bit_extender_1_out = {{20{IR[31]}}, {IR[31], IR[7], IR[30:25], IR[11:8]}};  // Bit_Extender bit_extender_1
  Pull_Resistor #(.pull(0)) pull_resistor_4 (.node(demultiplexer_1_out1));
  Pull_Resistor #(.pull(0)) pull_resistor_5 (.node(demultiplexer_1_out2));
  Pull_Resistor #(.pull(0)) pull_resistor_6 (.node(demultiplexer_1_out3));
  Multiplexer #(.select(1), .width(5), .disabled("Z"), .enable("false")) multiplexer_7 (
    .in0(IR[19:15]), .in1(5'b10001), .out(multiplexer_7_out), .sel(ecall));
  assign imm12 = {{20{multiplexer_6_out[11]}}, multiplexer_6_out};  // Bit_Extender bit_extender_2
  Shifter #(.width(32), .shift("ll")) shifter_1 (.in(bit_extender_1_out), .\dist (5'b00001), .out(shifter_1_out));
  assign bit_extender_3_out = {{12{IR[31]}}, {IR[31], IR[19:12], IR[20], IR[30:21]}};  // Bit_Extender bit_extender_3
  Shifter #(.width(32), .shift("ll")) shifter_2 (.in(bit_extender_3_out), .\dist (5'b00001), .out(shifter_2_out));
  or or_7 (or_7_out, JALR, JAL);
  Multiplexer #(.select(1), .width(32), .disabled("Z"), .enable("false")) multiplexer_8 (
    .in0(ALUresult), .in1(MDout), .out(multiplexer_8_out), .sel(MemToReg));
  Multiplexer #(.select(1), .width(32), .disabled("Z"), .enable("false")) multiplexer_9 (
    .in0(multiplexer_8_out), .in1(PC_4), .out(multiplexer_9_out), .sel(or_7_out));
  and and_5 (uret1, uret, demultiplexer_1_out1);
  and and_6 (uret2, demultiplexer_1_out2, uret);
  and and_7 (uret3, demultiplexer_1_out3, uret);
  Multiplexer #(.select(1), .width(32), .disabled("Z"), .enable("false")) multiplexer_10 (
    .in0(multiplexer_9_out), .in1({IR[31:12], {12{1'b0}}}), .out(RDin), .sel(lui));
  Regifile regifile_1 (
    .Din(RDin), .Clk(CLK), .R1(R1), .R2(R2), .WE(RegWrite), .W_num(IR[11:7]), .R1_num(multiplexer_7_out),
    .R2_num(multiplexer_5_out));
  Adder #(.width(32)) adder_2 (.a(shifter_1_out), .b(PC), .out(BJ));  // open: cin, cout
  Adder #(.width(32)) adder_3 (.a(shifter_2_out), .b(PC), .out(DJ));  // open: cin, cout
  not not_5 (not_5_out, eq);
  Demultiplexer #(.select(2), .width(1), .tristate("false"), .disabled("Z"), .enable("false")) demultiplexer_2 (
    .out1(demultiplexer_2_out1), .out2(demultiplexer_2_out2), .out3(demultiplexer_2_out3), .in(Interr),
    .sel(InterrNum));  // open: out0
  and and_8 (and_8_out, Beq, eq);
  or or_8 (B, and_8_out, and_9_out, and_10_out);
  and and_9 (and_9_out, Bne, not_5_out);
  and and_10 (and_10_out, less, Blt);
  Multiplexer #(.select(1), .width(32), .disabled("Z"), .enable("false")) multiplexer_11 (
    .in0(R2), .in1(imm12), .out(multiplexer_11_out), .sel(ALUSrc));
  assign bit_extender_4_out = {{27{R2[4]}}, R2[4:0]};  // Bit_Extender bit_extender_4
  assign bit_extender_5_out = {{3{1'b0}}, ALUresult[1:0]};  // Bit_Extender bit_extender_5
  Pull_Resistor #(.pull(0)) pull_resistor_7 (.node(demultiplexer_2_out1));
  Pull_Resistor #(.pull(0)) pull_resistor_8 (.node(demultiplexer_2_out2));
  Pull_Resistor #(.pull(0)) pull_resistor_9 (.node(demultiplexer_2_out3));
  D_Flip_Flop #(.trigger("high"), .Pre_Clr_Positions("LEGACY"), .NegatePresetClear("false"), .enable("true"), .NewFFLayout("false")) d_ff_1 (.Q(d_ff_1_q));  // open: clk, D, Qn, preset, en, reset
  // Probe on 13'hc
  Counter #(.width(16), .max('hffff), .ongoal("wrap"), .trigger("rising"), .behavior("new")) counter_2 (
    .count(B), .Q(\分支成功数 ), .clk(CLK), .clr(RST));  // open: load, D, carry, preset, down
  Multiplexer #(.select(1), .width(32), .disabled("Z"), .enable("false")) multiplexer_12 (
    .in0(multiplexer_11_out), .in1(bit_extender_4_out), .out(multiplexer_12_out), .sel(srl));
  Multiplexer #(.select(2), .width(32), .disabled("Z"), .enable("false")) multiplexer_13 (
    .in0(32'hffffff00), .in1(32'hffff00ff), .in2(32'hff00ffff), .in3(32'hffffff), .out(multiplexer_13_out),
    .sel(ALUresult[1:0]));
  assign and_11_out = multiplexer_13_out & MDout;  // AND_Gate and_11, 32 bits wide
  Shifter #(.width(5), .shift("ll")) shifter_3 (.in(bit_extender_5_out), .\dist (3'b011), .out(shifter_3_out));
  Comparator #(.width(13), .mode("twosComplement")) comparator_8 (
    .a(CNT_num), .b(13'hc), .eq(comparator_8_eq), .lt(comparator_8_lt));  // open: gt
  Clock #(.highDuration(1), .lowDuration(1)) clock_1 (.out(clock_1_out));
  ALU alu_1 (
    .X(R1), .Y(multiplexer_12_out), .AluOP(ALUop), .Equal(eq), .Result(ALUresult), .out_6(less));  // open: Result_2, out_4
  Adder #(.width(32)) adder_4 (.a(and_11_out), .b(shifter_4_out), .out(adder_4_out));  // open: cin, cout
  Shifter #(.width(32), .shift("ll")) shifter_4 (.in(R2), .\dist (shifter_3_out), .out(shifter_4_out));
  Register #(.width(32), .trigger("rising"), .Select("low")) EPC1 (
    .D(nextPC), .en(demultiplexer_2_out1), .Q(EPC1_q), .clk(CLK));  // open: clr
  Register #(.width(32), .trigger("rising"), .Select("low")) EPC2 (
    .D(nextPC), .en(demultiplexer_2_out2), .Q(EPC2_q), .clk(CLK));  // open: clr
  Register #(.width(32), .trigger("rising"), .Select("low")) EPC3 (
    .D(nextPC), .en(demultiplexer_2_out3), .Q(EPC3_q), .clk(CLK));  // open: clr
  Counter #(.width(13), .max('h1fff), .ongoal("stay"), .trigger("rising"), .behavior("old")) counter_3 (
    .count(comparator_8_lt), .Q(CNT_num), .clk(clock_1_out));  // open: load, D, carry, clr, preset
  Multiplexer #(.select(2), .width(32), .disabled("Z"), .enable("false")) multiplexer_14 (
    .in1(EPC1_q), .in2(EPC2_q), .in3(EPC3_q), .out(EPC), .sel(InterrPreNum));  // open: in0
  nand nand_1 (nand_1_out, d_ff_1_q, comparator_8_eq);
  RAM #(.addrWidth(10), .dataWidth(32), .bus("separate"), .Select("high")) ram_1 (
    .addr(ALUresult[11:2]), .din(MDin), .data(MDout), .str(MemWrite), .clk(CLK), .ld(1'b1), .clr(RST));  // open: sel
  Multiplexer #(.select(1), .width(32), .disabled("Z"), .enable("false")) multiplexer_15 (
    .in0(R2), .in1(adder_4_out), .out(MDin), .sel(sb));
  assign CLK = nand_1_out ? clock_1_out : 1'bz;  // Controlled_Buffer controlled_buffer_1
  Pull_Resistor #(.pull(1)) pull_resistor_10 (.node(CLK));
  or or_9 (or_9_out, uret, Interr);
  Counter #(.width(2), .max('h3), .ongoal("wrap"), .trigger("rising"), .behavior("new")) counter_4 (
    .count(or_9_out), .Q(counter_4_q), .clk(CLK), .down(uret));  // open: load, D, carry, clr, preset
  Demultiplexer #(.select(2), .width(1), .tristate("false"), .disabled("Z"), .enable("false")) demultiplexer_3 (
    .out0(demultiplexer_3_out0), .out1(demultiplexer_3_out1), .out2(demultiplexer_3_out2), .in(Interr),
    .sel(counter_4_q));  // open: out3
  Pull_Resistor #(.pull(0)) pull_resistor_11 (.node(demultiplexer_3_out0));
  Pull_Resistor #(.pull(0)) pull_resistor_12 (.node(demultiplexer_3_out1));
  Pull_Resistor #(.pull(0)) pull_resistor_13 (.node(demultiplexer_3_out2));
  or or_10 (W1, Interrupt1, d_ff_2_q);
  or or_11 (W2, Interrupt2, d_ff_3_q);
  or or_12 (W3, Interrupt3, d_ff_4_q);
  D_Flip_Flop #(.trigger("rising"), .Pre_Clr_Positions("LEGACY"), .NegatePresetClear("false"), .enable("true"), .NewFFLayout("false")) d_ff_2 (
    .clk(IR1_t), .D(1'b1), .Q(d_ff_2_q), .reset(Interrupt1));  // open: Qn, preset, en
  D_Flip_Flop #(.trigger("rising"), .Pre_Clr_Positions("LEGACY"), .NegatePresetClear("false"), .enable("true"), .NewFFLayout("false")) d_ff_3 (
    .clk(IR2_t), .D(1'b1), .Q(d_ff_3_q), .reset(Interrupt2));  // open: Qn, preset, en
  D_Flip_Flop #(.trigger("rising"), .Pre_Clr_Positions("LEGACY"), .NegatePresetClear("false"), .enable("true"), .NewFFLayout("false")) d_ff_4 (
    .clk(IR3_t), .D(1'b1), .Q(d_ff_4_q), .reset(Interrupt3));  // open: Qn, preset, en
  Register #(.width(2), .trigger("rising"), .Select("low")) u_IR1 (
    .D(InterrNum), .en(demultiplexer_3_out0), .Q(IR1_q), .clk(CLK));  // open: clr
  Register #(.width(2), .trigger("rising"), .Select("low")) u_IR2 (
    .D(InterrNum), .en(demultiplexer_3_out1), .Q(IR2_q), .clk(CLK));  // open: clr
  Register #(.width(2), .trigger("rising"), .Select("low")) u_IR3 (
    .D(InterrNum), .en(demultiplexer_3_out2), .Q(IR3_q), .clk(CLK));  // open: clr
  or or_13 (or_13_out, d_ff_2_q, Interrupt1);
  or or_14 (or_14_out, d_ff_3_q, Interrupt2);
  or or_15 (or_15_out, d_ff_4_q, Interrupt3);
  Multiplexer #(.select(2), .width(2), .disabled("Z"), .enable("false")) multiplexer_16 (
    .in1(IR1_q), .in2(IR2_q), .in3(IR3_q), .out(InterrPreNum), .sel(counter_4_q));  // open: in0
  and and_12 (and_12_out, or_13_out, ~uret1);  // AND_Gate
  and and_13 (and_13_out, or_14_out, ~uret2);  // AND_Gate
  and and_14 (and_14_out, or_15_out, ~uret3);  // AND_Gate
  D_Flip_Flop #(.trigger("rising"), .Pre_Clr_Positions("LEGACY"), .NegatePresetClear("false"), .enable("true"), .NewFFLayout("false")) IR1_2 (
    .clk(CLK), .D(and_12_out), .Q(Interrupt1));  // open: Qn, preset, en, reset
  D_Flip_Flop #(.trigger("rising"), .Pre_Clr_Positions("LEGACY"), .NegatePresetClear("false"), .enable("true"), .NewFFLayout("false")) IR2_2 (
    .clk(CLK), .D(and_13_out), .Q(Interrupt2));  // open: Qn, preset, en, reset
  D_Flip_Flop #(.trigger("rising"), .Pre_Clr_Positions("LEGACY"), .NegatePresetClear("false"), .enable("true"), .NewFFLayout("false")) IR3_2 (
    .clk(CLK), .D(and_14_out), .Q(Interrupt3));  // open: Qn, preset, en, reset
  Comparator #(.width(2), .mode("unsigned")) comparator_9 (
    .a(InterrPreNum), .b(InterrNum), .lt(shield));  // open: gt, eq
  Pull_Resistor #(.pull(1)) pull_resistor_14 (.node(shield));

  // Other names for the same wires on the sheet: lu[31:12] = IR[31:12]; byte_ad[1:0] = ALUresult[1:0]

  // Notes on the sheet:
  //   中断源
  //   中断等待指示
  //   总复位信号应将除ROM以外所有存储组件全部清零
  //   多级中断测试信号模拟器
  //   数码管输出
  //   数码管输出应该用寄存器锁存，否则显示数据只能一闪而过
  //   指令探针
  //   指令字
  //   contents of rom_1 (hex, n*v repeats v):
  //   7d000113 100413 1f41993 41f9d993 433 c00913 800b13 140413 f47413 800293 100313 499993 89e9b3 1300533
  //   2200893 73 406282b3 fe0294e3 140413 f00f93 1f47433 1c41413 800293 100313 49d993 89e9b3 1300533
  //   2200893 73 406282b3 fe0294e3 1c45413 406b0b33 b0463 f95ff06f 2b3 fff2c293 1029293 fff2e293 500533
  //   2200893 73 f5dff06f 1112023 410113 a12023 410113 812023 410113 1312023 410113 1412023 410113 1512023
  //   410113 1612023 410113 40e073 100b13 300a13 100a93 1600433 441413 14469b3 1300533 2200893 73 fe0416e3
  //   415a0a33 fe0a10e3 40f073 ffc10113 12b03 ffc10113 12a83 ffc10113 12a03 ffc10113 12983 ffc10113 12403
  //   ffc10113 12503 ffc10113 12883 200073 1112023 410113 a12023 410113 812023 410113 1312023 410113
  //   1412023 410113 1512023 410113 1612023 410113 40e073 200b13 300a13 100a93 1600433 441413 14469b3
  //   1300533 2200893 73 fe0416e3 415a0a33 fe0a10e3 40f073 ffc10113 12b03 ffc10113 12a83 ffc10113 12a03
  //   ffc10113 12983 ffc10113 12403 ffc10113 12503 ffc10113 12883 200073 1112023 410113 a12023 410113
  //   812023 410113 1312023 410113 1412023 410113 1512023 410113 1612023 410113 40e073 300b13 300a13
  //   100a93 1600433 441413 14469b3 1300533 2200893 73 fe0416e3 415a0a33 fe0a10e3 40f073 ffc10113 12b03
  //   ffc10113 12a83 ffc10113 12a03 ffc10113 12983 ffc10113 12403 ffc10113 12503 ffc10113 12883 200073
  //   B_type
  //   U_type
  //   为方便自动评测，需要输出PC，IR，寄存器堆写如数据RDin
  //   RAM写使能MemWrite、RAM写入数据MDin等信号
  //   控制位
  //   暂停节拍，不能为0
  //   戳工具置1进入计数暂停模式，ctrl+k时钟自动运行到对应节拍暂停
  //   ctrl+k关闭时钟连续运行，将控制位置零，进入单步调试模式调试
  //   可计数暂停的时钟源
  //   Reset 
  //   Reset 
  //   Reset 
endmodule
module \流水线中断  (
  input  IR1,
  input  IR2,
  input  IR3,
  output RegWrite,
  output MemWrite,
  output [31:0] PC,
  output [31:0] IR,
  output [31:0] RDin,
  output [31:0] MDin,
  output [31:0] LedData
);

  wire and_1_out, and_2_out, and_3_out, and_4_out, and_5_out, and_10_out, and_11_out, and_12_out, and_13_out,
       and_14_out, B, Beq, Blt, Bne, branch, CLK, clock_1_out, comparator_1_eq, comparator_2_eq,
       comparator_3_eq, comparator_4_eq, comparator_5_eq, comparator_5_lt, d_ff_1_q, d_ff_2_q, d_ff_3_q,
       d_ff_4_q, demultiplexer_1_out1, demultiplexer_1_out2, demultiplexer_1_out3, ecall, en, eq, EX_ecall,
       EX_MEM_halt_2, EX_MEM_jal_2, EX_MEM_jalr_2, EX_MEM_lui_2, EX_MEM_memtoreg_2, EX_MemtoReg, EX_RegWrite,
       Go, halt, ID_EX_p27, ID_EX_p35, ID_EX_p37, ID_EX_p41, ID_EX_p43, IE_q, Interr, InterrEN, Interrupt1,
       Interrupt2, Interrupt3, IR1_t, IR2_t, IR3_t, IRA, IRB, IRC, JAL, JALR, less, MEM_RegWrite,
       MEM_WB_halt_2, MEM_WB_jal_2, MEM_WB_jalr_2, MEM_WB_lui_2, MEM_WB_memtoreg_2, multiplexer_4_out,
       nand_1_out, not_1_out, not_2_out, not_3_out, not_4_out, not_5_out, not_6_out, not_7_out, not_8_out,
       not_9_out, not_10_out, not_11_out, not_12_out, not_13_out, or_6_out, or_7_out, or_8_out, or_9_out,
       or_11_out, or_13_out, or_15_out, or_16_out, RST, sb, srl, stall, uret, uret1, uret2, uret3, W1, W2,
       W3, \单周期硬布线控制器_1_alu_src , \单周期硬布线控制器_1_beq , \单周期硬布线控制器_1_blt , \单周期硬布线控制器_1_bne , \单周期硬布线控制器_1_jal ,
       \单周期硬布线控制器_1_jalr , \单周期硬布线控制器_1_lui , \单周期硬布线控制器_1_memtoreg , \单周期硬布线控制器_1_memwrite ,
       \单周期硬布线控制器_1_regwrite , \单周期硬布线控制器_1_s_type , \单周期硬布线控制器_1_sb , \单周期硬布线控制器_1_srl ;
  wire [1:0] byte_ad, ID_EX_p44, ID_EX_p45, priority_encoder_1_out, retReg_q, Rsf, Rtf;
  wire [3:0] ID_EX_p36, \单周期硬布线控制器_1_alu_op ;
  wire [4:0] bit_extender_5_out, EX_W_num, MEM_W_num, multiplexer_7_out, multiplexer_8_out, shifter_3_out,
       WB_W_num;
  wire [11:0] multiplexer_6_out;
  wire [12:0] CNT_num;
  wire [15:0] adder_6_out, \总周期数 , \插入气泡数 , \无条件分支数 , \条件分支成功数 ;
  wire [31:0] adder_4_out, adder_5_out, ALUresult, and_15_out, bit_extender_1_out, bit_extender_2_out,
       bit_extender_3_out, bit_extender_4_out, BJ, DJ, EPC, EX_IR, EX_MEM_lu_2, EX_PC, EX_R1, EX_R2,
       ID_EX_p47, ID_EX_p48, ID_EX_p53, ID_EX_p54, ID_EX_p55, ID_IR, ID_PC, ID_R1, ID_R2, IF_IR, IF_PC, imm,
       InterrAddr, MDout, MEM_IR, MEM_PC, MEM_WB_aluresult_2, MEM_WB_lu_2, MEM_WB_readdata_2, MEM_Writedata,
       multiplexer_2_out, multiplexer_3_out, multiplexer_11_out, multiplexer_12_out, multiplexer_13_out,
       multiplexer_15_out, multiplexer_16_out, nextPC, PC_4, shifter_1_out, shifter_2_out, shifter_4_out,
       WB_IR, WB_PC;
  wire [31:2] MEM_ALUresult;

  Button \u_继续运行  (.out(Go));
  Button _1 (.out(IRA));
  Button _2 (.out(IRB));
  Button _3 (.out(IRC));
  // Probe on \总周期数 
  // Probe on \总周期数 
  Button u_RST (.out(RST));
  LED #(.active("true")) led_1 (.in(W1));
  LED #(.active("true")) led_2 (.in(W2));
  LED #(.active("true")) led_3 (.in(W3));
  Hex_Digit_Display hex_digit_display_1 (.value(LedData[31:28]));  // open: dp
  // Probe on IF_PC[19:0]
  // RiscV_Probe riscv_probe_1: pin names not known; wires that end beside it: IF_IR
  Hex_Digit_Display hex_digit_display_2 (.value(LedData[23:20]));  // open: dp
  Hex_Digit_Display hex_digit_display_3 (.value(LedData[27:24]));  // open: dp
  // Probe on ID_PC[19:0]
  // RiscV_Probe riscv_probe_2: pin names not known; wires that end beside it: ID_IR
  Multiplexer #(.select(3), .width(32), .disabled("Z"), .enable("false")) multiplexer_1 (
    .in0(PC_4), .in1(BJ), .in2(ALUresult), .in3({32{1'b0}}), .in4(DJ), .in5({32{1'b0}}), .in6({32{1'b0}}),
    .in7({32{1'b0}}), .out(nextPC), .sel({JAL, JALR, B}));
  Hex_Digit_Display hex_digit_display_4 (.value(LedData[15:12]));  // open: dp
  Hex_Digit_Display hex_digit_display_5 (.value(LedData[19:16]));  // open: dp
  Multiplexer #(.select(1), .width(32), .disabled("Z"), .enable("false")) multiplexer_2 (
    .in0(nextPC), .in1(InterrAddr), .out(multiplexer_2_out), .sel(InterrEN));
  Multiplexer #(.select(1), .width(32), .disabled("Z"), .enable("false")) multiplexer_3 (
    .in0(multiplexer_2_out), .in1(EPC), .out(multiplexer_3_out), .sel(uret));
  Multiplexer #(.select(1), .width(1), .disabled("Z"), .enable("false")) multiplexer_4 (
    .in0(stall), .in1(not_1_out), .out(multiplexer_4_out), .sel(halt));
  not not_1 (not_1_out, Go);
  Hex_Digit_Display hex_digit_display_6 (.value(LedData[11:8]));  // open: dp
  Hex_Digit_Display hex_digit_display_7 (.value(LedData[7:4]));  // open: dp
  // Probe on \总周期数 
  // Probe on EX_PC[19:0]
  // RiscV_Probe riscv_probe_3: pin names not known; wires that end beside it: EX_IR
  not not_2 (not_2_out, multiplexer_4_out);
  Comparator #(.width(5), .mode("twosComplement")) comparator_1 (
    .a(IF_PC[6:2]), .b(5'b11000), .eq(comparator_1_eq));  // open: gt, lt
  not not_3 (not_3_out, comparator_1_eq);
  Comparator #(.width(5), .mode("twosComplement")) comparator_2 (
    .a(IF_PC[6:2]), .b(5'b11011), .eq(comparator_2_eq));  // open: gt, lt
  not not_4 (not_4_out, comparator_2_eq);
  not not_5 (not_5_out, comparator_3_eq);
  Comparator #(.width(5), .mode("twosComplement")) comparator_3 (
    .a(IF_PC[6:2]), .b(5'b11001), .eq(comparator_3_eq));  // open: gt, lt
  Hex_Digit_Display hex_digit_display_8 (.value(LedData[3:0]));  // open: dp
  Register #(.width(32), .trigger("rising"), .Select("low")) u_PC (
    .D(multiplexer_3_out), .en(not_2_out), .Q(IF_PC), .clk(CLK), .clr(RST));
  and and_1 (and_1_out, not_3_out, not_4_out, not_5_out);
  // Probe on MEM_PC[19:0]
  // RiscV_Probe riscv_probe_4: pin names not known; wires that end beside it: MEM_IR
  not not_6 (not_6_out, halt);
  or or_1 (W1, Interrupt1, d_ff_1_q);
  or or_2 (IR1_t, IR1, IRA);
  Counter #(.width(16), .max('hffff), .ongoal("wrap"), .trigger("rising"), .behavior("new")) counter_1 (
    .count(not_6_out), .Q(\总周期数 ), .clk(CLK), .clr(RST));  // open: load, D, carry, preset, down
  Adder #(.width(32)) adder_1 (.a(IF_PC), .b(32'h4), .out(PC_4));  // open: cin, cout
  D_Flip_Flop #(.trigger("rising"), .Pre_Clr_Positions("LEGACY"), .NegatePresetClear("false"), .enable("true"), .NewFFLayout("false")) d_ff_1 (
    .clk(IR1_t), .D(1'b1), .Q(d_ff_1_q), .reset(Interrupt1));  // open: Qn, preset, en
  D_Flip_Flop #(.trigger("rising"), .Pre_Clr_Positions("LEGACY"), .NegatePresetClear("false"), .enable("true"), .NewFFLayout("false")) d_ff_2 (
    .clk(IR2_t), .D(1'b1), .Q(d_ff_2_q), .reset(Interrupt2));  // open: Qn, preset, en
  or or_3 (W2, Interrupt2, d_ff_2_q);
  D_Flip_Flop #(.trigger("rising"), .Pre_Clr_Positions("LEGACY"), .NegatePresetClear("false"), .enable("true"), .NewFFLayout("false")) d_ff_3 (
    .clk(IR3_t), .D(1'b1), .Q(d_ff_3_q), .reset(Interrupt3));  // open: Qn, preset, en
  or or_4 (W3, Interrupt3, d_ff_3_q);
  Priority_Encoder #(.select(2), .disabled("Z")) priority_encoder_1 (
    .in0(1'b0), .in1(Interrupt1), .in2(Interrupt2), .in3(Interrupt3), .out(priority_encoder_1_out),
    .gs(Interr));  // open: en_out, en_in
  or or_5 (IR2_t, IR2, IRB);
  // Probe on WB_PC[19:0]
  // RiscV_Probe riscv_probe_5: pin names not known; wires that end beside it: WB_IR
  ROM #(.addrWidth(10), .dataWidth(32), .Select("high")) rom_1 (.addr(IF_PC[11:2]), .data(IF_IR));
  or or_6 (or_6_out, d_ff_1_q, Interrupt1);
  or or_7 (or_7_out, d_ff_2_q, Interrupt2);
  or or_8 (or_8_out, d_ff_3_q, Interrupt3);
  Register #(.width(1), .trigger("rising"), .Select("low")) IE (
    .D(InterrEN), .en(or_9_out), .Q(IE_q), .clk(CLK));  // open: clr
  or or_9 (or_9_out, InterrEN, uret);
  not not_7 (not_7_out, stall);
  and and_2 (and_2_out, en, not_7_out);
  IF_ID IF_ID (
    .en(and_2_out), .IR(IF_IR), .IR_2(ID_IR), .PC(IF_PC), .PC_2(ID_PC), .CLK(CLK), .RST(or_11_out));  // open: PC_4, PC_4_2, PredictJump, PredictJump_2
  and and_3 (and_3_out, or_6_out, ~uret1);  // AND_Gate
  and and_4 (and_4_out, or_7_out, ~uret2);  // AND_Gate
  and and_5 (and_5_out, or_8_out, ~uret3);  // AND_Gate
  Multiplexer #(.select(2), .width(32), .disabled("Z"), .enable("false")) multiplexer_5 (
    .in1(32'h30ac), .in2(32'h3150), .in3(32'h31f4), .out(InterrAddr), .sel(priority_encoder_1_out));  // open: in0
  not not_8 (not_8_out, IE_q);
  and and_6 (InterrEN, not_8_out, Interr);
  Register #(.width(32), .trigger("rising"), .Select("low")) u_EPC (
    .D(nextPC), .en(InterrEN), .Q(EPC), .clk(CLK));  // open: clr
  or or_10 (IR3_t, IR3, IRC);
  or or_11 (or_11_out, uret, branch);
  // RiscV_Probe riscv_probe_6: pin names not known; wires that end beside it: ID_IR, 5'b00001
  D_Flip_Flop #(.trigger("rising"), .Pre_Clr_Positions("LEGACY"), .NegatePresetClear("false"), .enable("true"), .NewFFLayout("false")) u_IR1 (
    .clk(CLK), .D(and_3_out), .Q(Interrupt1), .en(and_1_out));  // open: Qn, preset, reset
  D_Flip_Flop #(.trigger("rising"), .Pre_Clr_Positions("LEGACY"), .NegatePresetClear("false"), .enable("true"), .NewFFLayout("false")) u_IR2 (
    .clk(CLK), .D(and_4_out), .Q(Interrupt2), .en(and_1_out));  // open: Qn, preset, reset
  D_Flip_Flop #(.trigger("rising"), .Pre_Clr_Positions("LEGACY"), .NegatePresetClear("false"), .enable("true"), .NewFFLayout("false")) u_IR3 (
    .clk(CLK), .D(and_5_out), .Q(Interrupt3), .en(and_1_out));  // open: Qn, preset, reset
  Register #(.width(2), .trigger("rising"), .Select("low")) retReg (
    .D(priority_encoder_1_out), .en(InterrEN), .Q(retReg_q), .clk(CLK));  // open: clr
  Demultiplexer #(.select(2), .width(1), .tristate("false"), .disabled("Z"), .enable("false")) demultiplexer_1 (
    .out1(demultiplexer_1_out1), .out2(demultiplexer_1_out2), .out3(demultiplexer_1_out3), .in(1'b1),
    .sel(retReg_q));  // open: out0
  \重定向检测逻辑  \u_重定向检测逻辑_1  (
    .ID_IR(ID_IR), .EX_WriteReg_num(EX_W_num), .EX_RegWrite(EX_RegWrite), .MEM_WriteReg_num(MEM_W_num),
    .MEM_RegWrite(MEM_RegWrite), .EX_MemRead(EX_MemtoReg), .RtForward(Rtf), .RsForward(Rsf), .LoadUse(stall),
    .EX_IR(EX_IR));
  \单周期硬布线控制器  \u_单周期硬布线控制器_1  (
    .Funct({ID_IR[30], ID_IR[25], ID_IR[14:12]}), .OP(ID_IR[6:2]), .ALU_OP(\单周期硬布线控制器_1_alu_op ),
    .MemToReg(\单周期硬布线控制器_1_memtoreg ), .MemWrite(\单周期硬布线控制器_1_memwrite ), .ALU_SRC(\单周期硬布线控制器_1_alu_src ),
    .RegWrite(\单周期硬布线控制器_1_regwrite ), .ecall(ecall), .S_type(\单周期硬布线控制器_1_s_type ),
    .Jalr(\单周期硬布线控制器_1_jalr ), .Beq(\单周期硬布线控制器_1_beq ), .JAL(\单周期硬布线控制器_1_jal ), .Bne(\单周期硬布线控制器_1_bne ),
    .in_3(ID_IR[21]), .uret(uret), .sb(\单周期硬布线控制器_1_sb ), .lui(\单周期硬布线控制器_1_lui ), .srl(\单周期硬布线控制器_1_srl ),
    .blt(\单周期硬布线控制器_1_blt ));  // open: CSRRSI, CSRRCI
  Multiplexer #(.select(1), .width(12), .disabled("Z"), .enable("false")) multiplexer_6 (
    .in0(ID_IR[31:20]), .in1({ID_IR[31:25], ID_IR[11:7]}), .out(multiplexer_6_out), .sel(\单周期硬布线控制器_1_s_type ));
  assign bit_extender_1_out = {{20{ID_IR[31]}}, {ID_IR[31], ID_IR[7], ID_IR[30:25], ID_IR[11:8]}};  // Bit_Extender bit_extender_1
  assign bit_extender_2_out = {{12{ID_IR[31]}}, {ID_IR[31], ID_IR[19:12], ID_IR[20], ID_IR[30:21]}};  // Bit_Extender bit_extender_2
  and and_7 (uret1, uret, demultiplexer_1_out1);
  and and_8 (uret2, demultiplexer_1_out2, uret);
  and and_9 (uret3, demultiplexer_1_out3, uret);
  Multiplexer #(.select(1), .width(5), .disabled("Z"), .enable("false")) multiplexer_7 (
    .in0(ID_IR[19:15]), .in1(5'b10001), .out(multiplexer_7_out), .sel(ecall));
  Multiplexer #(.select(1), .width(5), .disabled("Z"), .enable("false")) multiplexer_8 (
    .in0(ID_IR[24:20]), .in1(5'b01010), .out(multiplexer_8_out), .sel(ecall));
  assign bit_extender_3_out = {{20{multiplexer_6_out[11]}}, multiplexer_6_out};  // Bit_Extender bit_extender_3
  Shifter #(.width(32), .shift("ll")) shifter_1 (.in(bit_extender_1_out), .\dist (5'b00001), .out(shifter_1_out));
  Shifter #(.width(32), .shift("ll")) shifter_2 (.in(bit_extender_2_out), .\dist (5'b00001), .out(shifter_2_out));
  and and_10 (and_10_out, EX_ecall, comparator_4_eq);
  Comparator #(.width(32), .mode("twosComplement")) comparator_4 (
    .a(EX_R1), .b(32'h22), .eq(comparator_4_eq));  // open: gt, lt
  not not_9 (not_9_out, comparator_4_eq);
  not not_10 (not_10_out, Go);
  Register #(.width(32), .trigger("rising"), .Select("low")) register_1 (
    .D(EX_R2), .en(and_10_out), .Q(LedData), .clk(CLK));  // open: clr
  and and_11 (and_11_out, not_9_out, EX_ecall, not_10_out);
  not not_11 (not_11_out, eq);
  not not_12 (not_12_out, CLK);
  and and_12 (and_12_out, Beq, eq);
  and and_13 (and_13_out, Bne, not_11_out);
  and and_14 (and_14_out, Blt, less);
  Regifile regifile_1 (
    .Din(RDin), .Clk(not_12_out), .R1(ID_R1), .R2(ID_R2), .WE(RegWrite), .W_num(WB_W_num),
    .R1_num(multiplexer_7_out), .R2_num(multiplexer_8_out));
  D_Flip_Flop #(.trigger("high"), .Pre_Clr_Positions("LEGACY"), .NegatePresetClear("false"), .enable("true"), .NewFFLayout("false")) d_ff_4 (.Q(d_ff_4_q));  // open: clk, D, Qn, preset, en, reset
  // Probe on 13'h35
  or or_12 (B, and_12_out, and_13_out, and_14_out);
  or or_13 (or_13_out, stall, branch);
  // ID_EX ID_EX: pin names not known; wires that end beside it: en, \单周期硬布线控制器_1_beq , \单周期硬布线控制器_1_bne , \单周期硬布线控制器_1_blt , \单周期硬布线控制器_1_memtoreg , \单周期硬布线控制器_1_memwrite , \单周期硬布线控制器_1_alu_op , \单周期硬布线控制器_1_alu_src , \单周期硬布线控制器_1_regwrite , \单周期硬布线控制器_1_jal , \单周期硬布线控制器_1_jalr , \单周期硬布线控制器_1_lui , \单周期硬布线控制器_1_srl , \单周期硬布线控制器_1_sb , Rtf, Rsf, ecall, ID_R1, ID_R2, ID_IR[11:7], bit_extender_3_out, ID_PC, ID_IR, shifter_1_out, shifter_2_out, {ID_IR[31:12], {12{1'b0}}}, ID_EX_p27, ID_EX_p27, CLK, or_13_out, Beq, Bne, Blt, EX_MemtoReg, ID_EX_p35, ID_EX_p36, ID_EX_p37, EX_RegWrite, JAL, JALR, ID_EX_p41, srl, ID_EX_p43, ID_EX_p44, ID_EX_p45, EX_ecall, ID_EX_p47, ID_EX_p48, EX_W_num, imm, EX_PC, EX_IR, ID_EX_p53, ID_EX_p54, ID_EX_p55
  Comparator #(.width(13), .mode("twosComplement")) comparator_5 (
    .a(CNT_num), .b(13'h35), .eq(comparator_5_eq), .lt(comparator_5_lt));  // open: gt
  Clock #(.highDuration(1), .lowDuration(1)) clock_1 (.out(clock_1_out));
  or or_14 (branch, B, RST, JALR, JAL);
  nand nand_1 (nand_1_out, d_ff_4_q, comparator_5_eq);
  Counter #(.width(13), .max('h1fff), .ongoal("stay"), .trigger("rising"), .behavior("old")) counter_2 (
    .count(comparator_5_lt), .Q(CNT_num), .clk(clock_1_out));  // open: load, D, carry, clr, preset
  Multiplexer #(.select(2), .width(32), .disabled("Z"), .enable("false")) multiplexer_9 (
    .in0(ID_EX_p47), .in1(RDin), .in2({MEM_ALUresult, byte_ad}), .out(EX_R1), .sel(ID_EX_p45));  // open: in3
  Multiplexer #(.select(2), .width(32), .disabled("Z"), .enable("false")) multiplexer_10 (
    .in0(ID_EX_p48), .in1(RDin), .in2({MEM_ALUresult, byte_ad}), .out(EX_R2), .sel(ID_EX_p44));  // open: in3
  Adder #(.width(32)) adder_2 (.a(ID_EX_p53), .b(EX_PC), .out(BJ));  // open: cin, cout
  Multiplexer #(.select(1), .width(32), .disabled("Z"), .enable("false")) multiplexer_11 (
    .in0(EX_R2), .in1(imm), .out(multiplexer_11_out), .sel(ID_EX_p37));
  Multiplexer #(.select(1), .width(32), .disabled("Z"), .enable("false")) multiplexer_12 (
    .in0(multiplexer_11_out), .in1(bit_extender_4_out), .out(multiplexer_12_out), .sel(srl));
  assign bit_extender_4_out = {{27{EX_R2[4]}}, EX_R2[4:0]};  // Bit_Extender bit_extender_4
  Adder #(.width(32)) adder_3 (.a(ID_EX_p54), .b(EX_PC), .out(DJ));  // open: cin, cout
  assign CLK = nand_1_out ? clock_1_out : 1'bz;  // Controlled_Buffer controlled_buffer_1
  Pull_Resistor #(.pull(1)) pull_resistor_1 (.node(CLK));
  ALU alu_1 (
    .X(EX_R1), .Y(multiplexer_12_out), .AluOP(ID_EX_p36), .Equal(eq), .Result(ALUresult), .out_6(less));  // open: Result_2, out_4
  EX_MEM EX_MEM (
    .RegWrite(EX_RegWrite), .MemToReg(EX_MemtoReg), .MemWrite(ID_EX_p35), .AluResult(ALUresult),
    .WriteData(EX_R2), .WriteReg_num(EX_W_num), .PC(EX_PC), .IR(EX_IR), .JAL(JAL), .JALR(JALR),
    .lui(ID_EX_p41), .sb(ID_EX_p43), .RegWrite_2(MEM_RegWrite), .MemToReg_2(EX_MEM_memtoreg_2),
    .MemWrite_2(MemWrite), .AluResult_2({MEM_ALUresult, byte_ad}), .WriteData_2(MEM_Writedata),
    .WriteReg_num_2(MEM_W_num), .PC_2(MEM_PC), .IR_2(MEM_IR), .JAL_2(EX_MEM_jal_2), .JALR_2(EX_MEM_jalr_2),
    .lui_2(EX_MEM_lui_2), .sb_2(sb), .CLK(CLK), .lu(ID_EX_p55), .lu_2(EX_MEM_lu_2), .RST(RST), .en(en),
    .halt(and_11_out), .halt_2(EX_MEM_halt_2));  // open: Bj, bj_2
  assign bit_extender_5_out = {{3{1'b0}}, byte_ad};  // Bit_Extender bit_extender_5
  or or_15 (or_15_out, JAL, JALR);
  Multiplexer #(.select(2), .width(32), .disabled("Z"), .enable("false")) multiplexer_13 (
    .in0(32'hffffff00), .in1(32'hffff00ff), .in2(32'hff00ffff), .in3(32'hffffff), .out(multiplexer_13_out),
    .sel(byte_ad));
  assign and_15_out = multiplexer_13_out & MDout;  // AND_Gate and_15, 32 bits wide
  Shifter #(.width(5), .shift("ll")) shifter_3 (.in(bit_extender_5_out), .\dist (3'b011), .out(shifter_3_out));
  Counter #(.width(16), .max('hffff), .ongoal("wrap"), .trigger("rising"), .behavior("new")) counter_3 (
    .count(or_15_out), .Q(\无条件分支数 ), .clk(CLK), .clr(RST));  // open: load, D, carry, preset, down
  Adder #(.width(32)) adder_4 (.a(and_15_out), .b(shifter_4_out), .out(adder_4_out));  // open: cin, cout
  Shifter #(.width(32), .shift("ll")) shifter_4 (.in(MEM_Writedata), .\dist (shifter_3_out), .out(shifter_4_out));
  MEM_WB MEM_WB (
    .RegWrite(MEM_RegWrite), .MemToReg(EX_MEM_memtoreg_2), .AluResult({MEM_ALUresult, byte_ad}),
    .ReadData(MDout), .WriteReg_num(MEM_W_num), .PC(MEM_PC), .IR(MEM_IR), .JAL(EX_MEM_jal_2),
    .JALR(EX_MEM_jalr_2), .lui(EX_MEM_lui_2), .RegWrite_2(RegWrite), .MemToReg_2(MEM_WB_memtoreg_2),
    .AluResult_2(MEM_WB_aluresult_2), .ReadData_2(MEM_WB_readdata_2), .WriteReg_num_2(WB_W_num),
    .PC_2(WB_PC), .IR_2(WB_IR), .JAL_2(MEM_WB_jal_2), .JALR_2(MEM_WB_jalr_2), .lui_2(MEM_WB_lui_2),
    .CLK(CLK), .RST(RST), .en(en), .halt(EX_MEM_halt_2), .halt_2(MEM_WB_halt_2), .lu(EX_MEM_lu_2),
    .lu_2(MEM_WB_lu_2));
  RAM #(.addrWidth(10), .dataWidth(32), .bus("separate"), .Select("high")) ram_1 (
    .addr(MEM_ALUresult[11:2]), .din(MDin), .data(MDout), .str(MemWrite), .clk(CLK), .ld(1'b1), .clr(RST));  // open: sel
  Multiplexer #(.select(1), .width(32), .disabled("Z"), .enable("false")) multiplexer_14 (
    .in0(MEM_Writedata), .in1(adder_4_out), .out(MDin), .sel(sb));
  and and_16 (halt, MEM_WB_halt_2, not_13_out);
  not not_13 (not_13_out, Go);
  or or_16 (or_16_out, MEM_WB_jalr_2, MEM_WB_jal_2);
  Multiplexer #(.select(1), .width(32), .disabled("Z"), .enable("false")) multiplexer_15 (
    .in0(MEM_WB_aluresult_2), .in1(MEM_WB_readdata_2), .out(multiplexer_15_out), .sel(MEM_WB_memtoreg_2));
  Adder #(.width(32)) adder_5 (.a(WB_PC), .b(32'h4), .out(adder_5_out));  // open: cin, cout
  not not_14 (en, halt);
  Adder #(.width(16)) adder_6 (.a(\无条件分支数 ), .b(\条件分支成功数 ), .out(adder_6_out));  // open: cin, cout
  Multiplexer #(.select(1), .width(32), .disabled("Z"), .enable("false")) multiplexer_16 (
    .in0(multiplexer_15_out), .in1(adder_5_out), .out(multiplexer_16_out), .sel(or_16_out));
  Multiplexer #(.select(1), .width(32), .disabled("Z"), .enable("false")) multiplexer_17 (
    .in0(multiplexer_16_out), .in1(MEM_WB_lu_2), .out(RDin), .sel(MEM_WB_lui_2));
  Shifter #(.width(16), .shift("ll")) shifter_5 (.in(adder_6_out), .\dist (4'b0001), .out(\插入气泡数 ));

  // Other names for the same wires on the sheet: MEM_ALUresult[1:0] = byte_ad

  // Notes on the sheet:
  //   中断源
  //   时空图监测，可删除
  //   中断等待指示
  //   数码管输出
  //   R1
  //   指令存储器
  //   contents of rom_1 (hex, n*v repeats v):
  //   7d000113 100413 1f41993 41f9d993 433 c00913 800b13 140413 f47413 800293 100313 499993 89e9b3 1300533
  //   2200893 73 406282b3 fe0294e3 140413 f00f93 1f47433 1c41413 800293 100313 49d993 89e9b3 1300533
  //   2200893 73 406282b3 fe0294e3 1c45413 406b0b33 b0463 f95ff06f 2b3 fff2c293 1029293 fff2e293 500533
  //   2200893 73 f5dff06f 1112023 410113 a12023 410113 812023 410113 1312023 410113 1412023 410113 1512023
  //   410113 1612023 410113 100b13 300a13 100a93 1600433 441413 14469b3 1300533 2200893 73 fe0416e3
  //   415a0a33 fe0a10e3 ffc10113 12b03 ffc10113 12a83 ffc10113 12a03 ffc10113 12983 ffc10113 12403
  //   ffc10113 12503 ffc10113 12883 200073 1112023 410113 a12023 410113 812023 410113 1312023 410113
  //   1412023 410113 1512023 410113 1612023 410113 200b13 300a13 100a93 1600433 441413 14469b3 1300533
  //   2200893 73 fe0416e3 415a0a33 fe0a10e3 ffc10113 12b03 ffc10113 12a83 ffc10113 12a03 ffc10113 12983
  //   ffc10113 12403 ffc10113 12503 ffc10113 12883 200073 1112023 410113 a12023 410113 812023 410113
  //   1312023 410113 1412023 410113 1512023 410113 1612023 410113 300b13 300a13 100a93 1600433 441413
  //   14469b3 1300533 2200893 73 fe0416e3 415a0a33 fe0a10e3 ffc10113 12b03 ffc10113 12a83 ffc10113 12a03
  //   ffc10113 12983 ffc10113 12403 ffc10113 12503 ffc10113 12883 200073
  //   Reset 
  //   指令探针
  //   Reset 
  //   Reset 
  //   为方便自动评测，需要输出PC，IR，寄存器堆写如数据RDin
  //   RAM写使能MemWrite、RAM写入数据MDin等信号
  //   Beq
  //   Bne
  //   控制位
  //   暂停节拍，不能为0
  //   R2
  //   可计数暂停的时钟源
  //   数据存储器
endmodule

module \分支预测  (
  output RegWrite,
  output MemWrite,
  output [31:0] IF_PC,
  output [31:0] ID_PC,
  output [31:0] EX_PC,
  output [31:0] M_PC,
  output [31:0] WB_PC,
  output [31:0] RDin,
  output [31:0] MDin,
  output [31:0] LedData
);

  wire and_1_out, and_2_out, and_3_out, and_4_out, and_5_out, and_6_out, B, Beq, Blt, Bne, btb_1_predictjump,
       CLK, clock_1_out, comparator_1_eq, comparator_1_lt, comparator_2_eq, comparator_3_eq, d_ff_1_q, ecall,
       en, eq, EX_branch, EX_ecall, EX_MEM_halt_2, EX_MEM_jal_2, EX_MEM_jalr_2, EX_MEM_lui_2,
       EX_MEM_memtoreg_2, EX_MemtoReg, EX_RegWrite, Go, halt, ID_EX_p28, ID_EX_p36, ID_EX_p38, ID_EX_p42,
       ID_EX_p44, ID_pre, IR1, IR2, IR3, JAL, JALR, less, loaduse, MEM_RegWrite, MEM_WB_halt_2, MEM_WB_jal_2,
       MEM_WB_jalr_2, MEM_WB_lui_2, MEM_WB_memtoreg_2, multiplexer_4_out, nand_1_out, not_1_out, not_2_out,
       not_3_out, not_4_out, not_5_out, not_6_out, not_7_out, not_9_out, or_2_out, or_3_out, or_4_out,
       or_6_out, PredictErr, PredictJump, RST, sb, srl, W1, W2, W3, \单周期硬布线控制器_1_alu_src , \单周期硬布线控制器_1_beq ,
       \单周期硬布线控制器_1_blt , \单周期硬布线控制器_1_bne , \单周期硬布线控制器_1_jal , \单周期硬布线控制器_1_jalr , \单周期硬布线控制器_1_lui ,
       \单周期硬布线控制器_1_memtoreg , \单周期硬布线控制器_1_memwrite , \单周期硬布线控制器_1_regwrite , \单周期硬布线控制器_1_s_type ,
       \单周期硬布线控制器_1_sb , \单周期硬布线控制器_1_srl ;
  wire [1:0] byte_ad, ID_EX_p45, ID_EX_p46, Rsf, Rtf;
  wire [3:0] ID_EX_p37, \单周期硬布线控制器_1_alu_op ;
  wire [4:0] bit_extender_5_out, EX_W_num, MEM_W_num, multiplexer_8_out, multiplexer_9_out, shifter_3_out,
       WB_W_num;
  wire [11:0] multiplexer_10_out;
  wire [12:0] CNT_num;
  wire [15:0] adder_6_out, \LoadUse次数 , \总周期数 , \插入气泡数 , \无条件分支数 , \条件分支成功数 ;
  wire [31:0] adder_1_out, adder_5_out, adder_7_out, ALUresult, and_7_out, bit_extender_1_out,
       bit_extender_2_out, bit_extender_3_out, bit_extender_4_out, BJ, btb_1_jumpaddr, DJ, EX_IR,
       EX_MEM_lu_2, EX_R1, EX_R2, ID_EX_p48, ID_EX_p49, ID_EX_p55, ID_EX_p56, ID_EX_p57, ID_IR, ID_R1, ID_R2,
       IF_IR, imm, MDout, MEM_IR, MEM_WB_aluresult_2, MEM_WB_lu_2, MEM_WB_readdata_2, MEM_Writedata,
       multiplexer_1_out, multiplexer_2_out, multiplexer_3_out, multiplexer_5_out, multiplexer_6_out,
       multiplexer_7_out, multiplexer_13_out, multiplexer_14_out, multiplexer_15_out, multiplexer_17_out,
       multiplexer_18_out, PC_4, shifter_1_out, shifter_2_out, shifter_4_out, WB_IR;
  wire [31:2] MEM_ALUresult;

  Button \u_总复位  (.out(RST));
  Button _1 (.out(IR1));
  Button _2 (.out(IR2));
  Button _3 (.out(IR3));
  // Probe on \总周期数 
  // Probe on \总周期数 
  Button u_go (.out(Go));
  LED #(.active("true")) led_1 (.in(W1));
  LED #(.active("true")) led_2 (.in(W2));
  LED #(.active("true")) led_3 (.in(W3));
  Hex_Digit_Display hex_digit_display_1 (.value(LedData[31:28]));  // open: dp
  // Probe on IF_PC[19:0]
  // RiscV_Probe riscv_probe_1: pin names not known; wires that end beside it: IF_IR
  Adder #(.width(32)) adder_1 (.a(32'h4), .b(EX_PC), .out(adder_1_out));  // open: cin, cout
  Multiplexer #(.select(1), .width(32), .disabled("Z"), .enable("false")) multiplexer_1 (
    .in0(PC_4), .in1(BJ), .out(multiplexer_1_out), .sel(B));
  Hex_Digit_Display hex_digit_display_2 (.value(LedData[27:24]));  // open: dp
  Hex_Digit_Display hex_digit_display_3 (.value(LedData[23:20]));  // open: dp
  // Probe on ID_PC[19:0]
  // RiscV_Probe riscv_probe_2: pin names not known; wires that end beside it: ID_IR
  Multiplexer #(.select(1), .width(32), .disabled("Z"), .enable("false")) multiplexer_2 (
    .in0(adder_1_out), .in1(multiplexer_1_out), .out(multiplexer_2_out), .sel(B));
  Hex_Digit_Display hex_digit_display_4 (.value(LedData[19:16]));  // open: dp
  Hex_Digit_Display hex_digit_display_5 (.value(LedData[15:12]));  // open: dp
  Multiplexer #(.select(1), .width(32), .disabled("Z"), .enable("false")) multiplexer_3 (
    .in0(multiplexer_7_out), .in1(multiplexer_2_out), .out(multiplexer_3_out), .sel(PredictErr));
  Multiplexer #(.select(1), .width(1), .disabled("Z"), .enable("false")) multiplexer_4 (
    .in0(loaduse), .in1(not_1_out), .out(multiplexer_4_out), .sel(halt));
  not not_1 (not_1_out, Go);
  Hex_Digit_Display hex_digit_display_6 (.value(LedData[11:8]));  // open: dp
  Hex_Digit_Display hex_digit_display_7 (.value(LedData[7:4]));  // open: dp
  // Probe on EX_PC[19:0]
  // RiscV_Probe riscv_probe_3: pin names not known; wires that end beside it: EX_IR
  Multiplexer #(.select(1), .width(32), .disabled("Z"), .enable("false")) multiplexer_5 (
    .in0(multiplexer_3_out), .in1(DJ), .out(multiplexer_5_out), .sel(JAL));
  not not_2 (not_2_out, multiplexer_4_out);
  Hex_Digit_Display hex_digit_display_8 (.value(LedData[3:0]));  // open: dp
  Register #(.width(32), .trigger("rising"), .Select("low")) PC (
    .D(multiplexer_6_out), .en(not_2_out), .Q(IF_PC), .clk(CLK), .clr(RST));
  Multiplexer #(.select(1), .width(32), .disabled("Z"), .enable("false")) multiplexer_6 (
    .in0(multiplexer_5_out), .in1(ALUresult), .out(multiplexer_6_out), .sel(JALR));
  BTB btb_1 (
    .PC(IF_PC), .EX_Branch(EX_branch), .EX_PC(EX_PC), .BranchAddr(BJ), .EX_BranchTaken(B),
    .JumpAddr(btb_1_jumpaddr), .PredictJump(btb_1_predictjump), .CLK(CLK));
  Multiplexer #(.select(1), .width(32), .disabled("Z"), .enable("false")) multiplexer_7 (
    .in0(PC_4), .in1(btb_1_jumpaddr), .out(multiplexer_7_out), .sel(btb_1_predictjump));
  // Probe on \总周期数 
  // Probe on M_PC[19:0]
  // RiscV_Probe riscv_probe_4: pin names not known; wires that end beside it: MEM_IR
  Adder #(.width(32)) adder_2 (.a(32'h4), .b(IF_PC), .out(PC_4));  // open: cin, cout
  // Probe on \总周期数 
  // Probe on \无条件分支数 
  // Probe on \条件分支成功数 
  // Probe on \插入气泡数 
  // Probe on \LoadUse次数 
  not not_3 (not_3_out, halt);
  Counter #(.width(16), .max('hffff), .ongoal("wrap"), .trigger("rising"), .behavior("new")) counter_1 (
    .count(not_3_out), .Q(\总周期数 ), .clk(CLK), .clr(RST));  // open: load, D, carry, preset, down
  // Probe on IF_PC[11:0]
  // Probe on WB_PC[19:0]
  // RiscV_Probe riscv_probe_5: pin names not known; wires that end beside it: WB_IR
  ROM #(.addrWidth(10), .dataWidth(32), .Select("high")) rom_1 (.addr(IF_PC[11:2]), .data(IF_IR));
  // Probe on EX_PC[11:0]
  // Probe on ID_PC[11:0]
  // Probe on M_PC[11:0]
  D_Flip_Flop #(.trigger("high"), .Pre_Clr_Positions("LEGACY"), .NegatePresetClear("false"), .enable("true"), .NewFFLayout("false")) d_ff_1 (.Q(d_ff_1_q));  // open: clk, D, Qn, preset, en, reset
  // Probe on 13'h718
  not not_4 (not_4_out, loaduse);
  and and_1 (and_1_out, en, not_4_out);
  IF_ID IF_ID (
    .en(and_1_out), .IR(IF_IR), .IR_2(ID_IR), .PC(IF_PC), .PC_2(ID_PC), .PredictJump(btb_1_predictjump),
    .PredictJump_2(ID_pre), .CLK(CLK), .RST(PredictErr));  // open: PC_4, PC_4_2
  // Probe on WB_PC[11:0]
  Comparator #(.width(13), .mode("twosComplement")) comparator_1 (
    .a(CNT_num), .b(13'h718), .eq(comparator_1_eq), .lt(comparator_1_lt));  // open: gt
  Clock #(.highDuration(1), .lowDuration(1)) clock_1 (.out(clock_1_out));
  // RiscV_Probe riscv_probe_6: pin names not known; wires that end beside it: ID_IR, 5'b00001
  nand nand_1 (nand_1_out, d_ff_1_q, comparator_1_eq);
  Counter #(.width(13), .max('h1fff), .ongoal("stay"), .trigger("rising"), .behavior("old")) counter_2 (
    .count(comparator_1_lt), .Q(CNT_num), .clk(clock_1_out));  // open: load, D, carry, clr, preset
  assign CLK = nand_1_out ? clock_1_out : 1'bz;  // Controlled_Buffer controlled_buffer_1
  \重定向检测逻辑  \u_重定向检测逻辑_1  (
    .ID_IR(ID_IR), .EX_WriteReg_num(EX_W_num), .EX_RegWrite(EX_RegWrite), .MEM_WriteReg_num(MEM_W_num),
    .MEM_RegWrite(MEM_RegWrite), .EX_MemRead(EX_MemtoReg), .RtForward(Rtf), .RsForward(Rsf),
    .LoadUse(loaduse), .EX_IR(EX_IR));
  \单周期硬布线控制器  \u_单周期硬布线控制器_1  (
    .Funct({ID_IR[30], ID_IR[25], ID_IR[14:12]}), .OP(ID_IR[6:2]), .ALU_OP(\单周期硬布线控制器_1_alu_op ),
    .MemToReg(\单周期硬布线控制器_1_memtoreg ), .MemWrite(\单周期硬布线控制器_1_memwrite ), .ALU_SRC(\单周期硬布线控制器_1_alu_src ),
    .RegWrite(\单周期硬布线控制器_1_regwrite ), .ecall(ecall), .S_type(\单周期硬布线控制器_1_s_type ),
    .Jalr(\单周期硬布线控制器_1_jalr ), .Beq(\单周期硬布线控制器_1_beq ), .JAL(\单周期硬布线控制器_1_jal ), .Bne(\单周期硬布线控制器_1_bne ),
    .in_3(ID_IR[21]), .sb(\单周期硬布线控制器_1_sb ), .lui(\单周期硬布线控制器_1_lui ), .srl(\单周期硬布线控制器_1_srl ),
    .blt(\单周期硬布线控制器_1_blt ));  // open: uret, CSRRSI, CSRRCI
  Multiplexer #(.select(1), .width(5), .disabled("Z"), .enable("false")) multiplexer_8 (
    .in0(ID_IR[19:15]), .in1(5'b10001), .out(multiplexer_8_out), .sel(ecall));
  Multiplexer #(.select(1), .width(5), .disabled("Z"), .enable("false")) multiplexer_9 (
    .in0(ID_IR[24:20]), .in1(5'b01010), .out(multiplexer_9_out), .sel(ecall));
  assign bit_extender_1_out = {{20{multiplexer_10_out[11]}}, multiplexer_10_out};  // Bit_Extender bit_extender_1
  Multiplexer #(.select(1), .width(12), .disabled("Z"), .enable("false")) multiplexer_10 (
    .in0(ID_IR[31:20]), .in1({ID_IR[31:25], ID_IR[11:7]}), .out(multiplexer_10_out),
    .sel(\单周期硬布线控制器_1_s_type ));
  assign bit_extender_2_out = {{20{ID_IR[31]}}, {ID_IR[31], ID_IR[7], ID_IR[30:25], ID_IR[11:8]}};  // Bit_Extender bit_extender_2
  assign bit_extender_3_out = {{12{ID_IR[31]}}, {ID_IR[31], ID_IR[19:12], ID_IR[20], ID_IR[30:21]}};  // Bit_Extender bit_extender_3
  Comparator #(.width(32), .mode("twosComplement")) comparator_2 (
    .a(EX_R1), .b(32'h22), .eq(comparator_2_eq));  // open: gt, lt
  Pull_Resistor #(.pull(1)) pull_resistor_1 (.node(CLK));
  Shifter #(.width(32), .shift("ll")) shifter_1 (.in(bit_extender_2_out), .\dist (5'b00001), .out(shifter_1_out));
  Shifter #(.width(32), .shift("ll")) shifter_2 (.in(bit_extender_3_out), .\dist (5'b00001), .out(shifter_2_out));
  and and_2 (and_2_out, EX_ecall, comparator_2_eq);
  not not_5 (not_5_out, comparator_2_eq);
  and and_3 (and_3_out, not_5_out, EX_ecall);
  Register #(.width(32), .trigger("rising"), .Select("low")) register_1 (
    .D(EX_R2), .en(and_2_out), .Q(LedData), .clk(CLK));  // open: clr
  and and_4 (and_4_out, Beq, eq);
  and and_5 (and_5_out, Bne, not_6_out);
  not not_6 (not_6_out, eq);
  and and_6 (and_6_out, Blt, less);
  not not_7 (not_7_out, CLK);
  Regifile regifile_1 (
    .Din(RDin), .Clk(not_7_out), .R1(ID_R1), .R2(ID_R2), .WE(RegWrite), .W_num(WB_W_num),
    .R1_num(multiplexer_8_out), .R2_num(multiplexer_9_out));
  or or_1 (B, and_4_out, and_5_out, and_6_out);
  or or_2 (or_2_out, loaduse, PredictErr);
  // ID_EX ID_EX: pin names not known; wires that end beside it: en, \单周期硬布线控制器_1_beq , \单周期硬布线控制器_1_bne , \单周期硬布线控制器_1_blt , \单周期硬布线控制器_1_memtoreg , \单周期硬布线控制器_1_memwrite , \单周期硬布线控制器_1_alu_op , \单周期硬布线控制器_1_alu_src , \单周期硬布线控制器_1_regwrite , \单周期硬布线控制器_1_jal , \单周期硬布线控制器_1_jalr , \单周期硬布线控制器_1_lui , \单周期硬布线控制器_1_srl , \单周期硬布线控制器_1_sb , Rtf, Rsf, ecall, ID_R1, ID_R2, ID_IR[11:7], bit_extender_1_out, ID_PC, ID_IR, ID_pre, shifter_1_out, shifter_2_out, {ID_IR[31:12], {12{1'b0}}}, ID_EX_p28, ID_EX_p28, CLK, or_2_out, Beq, Bne, Blt, EX_MemtoReg, ID_EX_p36, ID_EX_p37, ID_EX_p38, EX_RegWrite, JAL, JALR, ID_EX_p42, srl, ID_EX_p44, ID_EX_p45, ID_EX_p46, EX_ecall, ID_EX_p48, ID_EX_p49, EX_W_num, imm, EX_PC, EX_IR, PredictJump, ID_EX_p55, ID_EX_p56, ID_EX_p57
  or or_3 (or_3_out, B, JAL, JALR);
  Multiplexer #(.select(2), .width(32), .disabled("Z"), .enable("false")) multiplexer_11 (
    .in0(ID_EX_p48), .in1(RDin), .in2({MEM_ALUresult, byte_ad}), .out(EX_R1), .sel(ID_EX_p46));  // open: in3
  Multiplexer #(.select(2), .width(32), .disabled("Z"), .enable("false")) multiplexer_12 (
    .in0(ID_EX_p49), .in1(RDin), .in2({MEM_ALUresult, byte_ad}), .out(EX_R2), .sel(ID_EX_p45));  // open: in3
  Multiplexer #(.select(1), .width(32), .disabled("Z"), .enable("false")) multiplexer_13 (
    .in0(EX_R2), .in1(imm), .out(multiplexer_13_out), .sel(ID_EX_p38));
  assign bit_extender_4_out = {{27{EX_R2[4]}}, EX_R2[4:0]};  // Bit_Extender bit_extender_4
  Adder #(.width(32)) adder_3 (.a(ID_EX_p55), .b(EX_PC), .out(BJ));  // open: cin, cout
  Adder #(.width(32)) adder_4 (.a(ID_EX_p56), .b(EX_PC), .out(DJ));  // open: cin, cout
  or or_4 (or_4_out, JAL, JALR);
  Comparator #(.width(1), .mode("twosComplement")) comparator_3 (
    .a(or_3_out), .b(PredictJump), .eq(comparator_3_eq));  // open: gt, lt
  not not_8 (PredictErr, comparator_3_eq);
  or or_5 (EX_branch, Beq, Bne, Blt);
  Multiplexer #(.select(1), .width(32), .disabled("Z"), .enable("false")) multiplexer_14 (
    .in0(multiplexer_13_out), .in1(bit_extender_4_out), .out(multiplexer_14_out), .sel(srl));
  Counter #(.width(16), .max('hffff), .ongoal("wrap"), .trigger("rising"), .behavior("new")) counter_3 (
    .count(or_4_out), .Q(\无条件分支数 ), .clk(CLK), .clr(RST));  // open: load, D, carry, preset, down
  EX_MEM EX_MEM (
    .RegWrite(EX_RegWrite), .MemToReg(EX_MemtoReg), .MemWrite(ID_EX_p36), .AluResult(ALUresult),
    .WriteData(EX_R2), .WriteReg_num(EX_W_num), .PC(EX_PC), .IR(EX_IR), .JAL(JAL), .JALR(JALR),
    .lui(ID_EX_p42), .sb(ID_EX_p44), .RegWrite_2(MEM_RegWrite), .MemToReg_2(EX_MEM_memtoreg_2),
    .MemWrite_2(MemWrite), .AluResult_2({MEM_ALUresult, byte_ad}), .WriteData_2(MEM_Writedata),
    .WriteReg_num_2(MEM_W_num), .PC_2(M_PC), .IR_2(MEM_IR), .JAL_2(EX_MEM_jal_2), .JALR_2(EX_MEM_jalr_2),
    .lui_2(EX_MEM_lui_2), .sb_2(sb), .CLK(CLK), .lu(ID_EX_p57), .lu_2(EX_MEM_lu_2), .RST(RST), .en(en),
    .halt(and_3_out), .halt_2(EX_MEM_halt_2));  // open: Bj, bj_2
  ALU alu_1 (
    .X(EX_R1), .Y(multiplexer_14_out), .AluOP(ID_EX_p37), .Equal(eq), .Result(ALUresult), .out_6(less));  // open: Result_2, out_4
  assign bit_extender_5_out = {{3{1'b0}}, byte_ad};  // Bit_Extender bit_extender_5
  Multiplexer #(.select(2), .width(32), .disabled("Z"), .enable("false")) multiplexer_15 (
    .in0(32'hffffff00), .in1(32'hffff00ff), .in2(32'hff00ffff), .in3(32'hffffff), .out(multiplexer_15_out),
    .sel(byte_ad));
  Shifter #(.width(5), .shift("ll")) shifter_3 (.in(bit_extender_5_out), .\dist (3'b011), .out(shifter_3_out));
  assign and_7_out = multiplexer_15_out & MDout;  // AND_Gate and_7, 32 bits wide
  Shifter #(.width(32), .shift("ll")) shifter_4 (.in(MEM_Writedata), .\dist (shifter_3_out), .out(shifter_4_out));
  RAM #(.addrWidth(10), .dataWidth(32), .bus("separate"), .Select("high")) ram_1 (
    .addr(MEM_ALUresult[11:2]), .din(MDin), .data(MDout), .str(MemWrite), .clk(CLK), .ld(1'b1), .clr(RST));  // open: sel
  Adder #(.width(32)) adder_5 (.a(and_7_out), .b(shifter_4_out), .out(adder_5_out));  // open: cin, cout
  Adder #(.width(16)) adder_6 (.a(\无条件分支数 ), .b(\条件分支成功数 ), .out(adder_6_out));  // open: cin, cout
  MEM_WB MEM_WB (
    .RegWrite(MEM_RegWrite), .MemToReg(EX_MEM_memtoreg_2), .AluResult({MEM_ALUresult, byte_ad}),
    .ReadData(MDout), .WriteReg_num(MEM_W_num), .PC(M_PC), .IR(MEM_IR), .JAL(EX_MEM_jal_2),
    .JALR(EX_MEM_jalr_2), .lui(EX_MEM_lui_2), .RegWrite_2(RegWrite), .MemToReg_2(MEM_WB_memtoreg_2),
    .AluResult_2(MEM_WB_aluresult_2), .ReadData_2(MEM_WB_readdata_2), .WriteReg_num_2(WB_W_num),
    .PC_2(WB_PC), .IR_2(WB_IR), .JAL_2(MEM_WB_jal_2), .JALR_2(MEM_WB_jalr_2), .lui_2(MEM_WB_lui_2),
    .CLK(CLK), .RST(RST), .en(en), .halt(EX_MEM_halt_2), .halt_2(MEM_WB_halt_2), .lu(EX_MEM_lu_2),
    .lu_2(MEM_WB_lu_2));
  Multiplexer #(.select(1), .width(32), .disabled("Z"), .enable("false")) multiplexer_16 (
    .in0(MEM_Writedata), .in1(adder_5_out), .out(MDin), .sel(sb));
  Shifter #(.width(16), .shift("ll")) shifter_5 (.in(adder_6_out), .\dist (4'b0001), .out(\插入气泡数 ));
  Multiplexer #(.select(1), .width(32), .disabled("Z"), .enable("false")) multiplexer_17 (
    .in0(MEM_WB_aluresult_2), .in1(MEM_WB_readdata_2), .out(multiplexer_17_out), .sel(MEM_WB_memtoreg_2));
  Adder #(.width(32)) adder_7 (.a(WB_PC), .b(32'h4), .out(adder_7_out));  // open: cin, cout
  and and_8 (halt, MEM_WB_halt_2, not_9_out);
  not not_9 (not_9_out, Go);
  or or_6 (or_6_out, MEM_WB_jalr_2, MEM_WB_jal_2);
  Multiplexer #(.select(1), .width(32), .disabled("Z"), .enable("false")) multiplexer_18 (
    .in0(multiplexer_17_out), .in1(adder_7_out), .out(multiplexer_18_out), .sel(or_6_out));
  not not_10 (en, halt);
  Multiplexer #(.select(1), .width(32), .disabled("Z"), .enable("false")) multiplexer_19 (
    .in0(multiplexer_18_out), .in1(MEM_WB_lu_2), .out(RDin), .sel(MEM_WB_lui_2));

  // Other names for the same wires on the sheet: BranchAddr[31:0] = BJ; EX_branchtaken = B;
  //   MEM_ALUresult[1:0] = byte_ad; MEM_PC[31:0] = M_PC

  // Notes on the sheet:
  //   中断源
  //   时空图监测，可删除
  //   中断等待指示
  //   数码管输出
  //   指令存储器
  //   R1
  //   contents of rom_1 (hex, n*v repeats v):
  //   100493 100006f 100493 200913 300993 100006f 100493 200913 300993 100006f 100493 200913 300993
  //   100006f 100493 200913 300993 3b8000ef 100413 100493 1f49493 900533 2200893 73 24d493 48463 fedff06f
  //   900533 2200893 73 100493 249493 900533 2200893 73 48463 fedff06f 100493 1f49493 900533 2200893 73
  //   4034d493 900533 2200893 73 4044d493 900533 2200893 73 4044d493 900533 2200893 73 4044d493 900533
  //   2200893 73 4044d493 900533 2200893 73 4044d493 900533 2200893 73 4044d493 900533 2200893 73 4044d493
  //   900533 2200893 73 100413 1f41993 41f9d993 433 c00913 300b13 140413 f47413 800293 100313 499993
  //   89e9b3 1300533 2200893 73 406282b3 fe0294e3 140413 f00f93 1f47433 1c41413 800293 100313 49d993
  //   89e9b3 1300533 2200893 73 406282b3 fe0294e3 1c45413 406b0b33 b0463 f95ff06f 2b3 fff2c293 829293
  //   ff2e293 500533 2200893 73 fff00413 493 84a023 140413 448493 84a023 140413 448493 84a023 140413
  //   448493 84a023 140413 448493 84a023 140413 448493 84a023 140413 448493 84a023 140413 448493 84a023
  //   140413 448493 84a023 140413 448493 84a023 140413 448493 84a023 140413 448493 84a023 140413 448493
  //   84a023 140413 448493 84a023 140413 448493 84a023 140413 448493 84a023 140413 448493 140413 433
  //   3c00493 42983 4aa03 149a2b3 28663 134a023 1442023 ffc48493 fe9412e3 800533 2200893 73 440413 3c00493
  //   fc9416e3 a00893 73 100293 300313 800493 849493 7648493 1449493 900533 2200893 73 800e13 54d4b3
  //   64d4b3 900533 2200893 73 fffe0e13 fe0e14e3 a00893 73 800e13 fedc04b7 fff00413 1045413 84e4b3 900533
  //   2200893 73 ba984b7 900533 73 76544b7 900533 73 32104b7 900533 73 fffe0e13 fa0e1ee3 a00893 73 313
  //   2000e13 493 100913 930023 900533 2200893 73 12484b3 130313 fffe0e13 fe0e12e3 800e13 313 32483 900533
  //   2200893 73 430313 fffe0e13 fe0e14e3 a00893 73 ff100493 900533 2200893 73 148493 fe04c8e3 a00893 73
  //   413 140413 800533 2200893 73 240413 800533 2200893 73 340413 800533 2200893 73 440413 800533 2200893
  //   73 540413 800533 2200893 73 640413 800533 2200893 73 740413 800533 2200893 73 840413 800533 2200893
  //   2200893 73 8067
  //   控制位
  //   流水调试日志用
  //   指令探针
  //   可计数暂停的时钟源
  //   Beq
  //   Bne
  //   为方便自动评测，需要输出流水线各段保存的PC值，注意是PC不是PC+4，另外ID段寄存器写入信息，Mem段内存写入信息也要输出
  //   R2
  //   数据存储器
endmodule

// 单周期硬布线控制器
module \单周期硬布线控制器  (
  input  [4:0] OP,
  input  [4:0] Funct,
  input  in_3,
  output [3:0] ALU_OP,
  output uret,
  output MemToReg,
  output ecall,
  output MemWrite,
  output ALU_SRC,
  output RegWrite,
  output S_type,
  output Beq,
  output Bne,
  output Jalr,
  output JAL,
  output sb,
  output lui,
  output srl,
  output blt,
  output CSRRCI,
  output CSRRSI
);

  wire \控制信号自动生成_1_ecall ;

  \运算控制器自动生成  \u_运算控制器自动生成_1  (
    .OP2(OP[0]), .OP3(OP[1]), .OP4(OP[2]), .OP5(OP[3]), .OP6(OP[4]), .F12(Funct[0]), .F13(Funct[1]),
    .F14(Funct[2]), .F25(Funct[3]), .F30(Funct[4]), .S0(ALU_OP[0]), .S1(ALU_OP[1]), .S2(ALU_OP[2]),
    .S3(ALU_OP[3]));
  \控制信号自动生成  \u_控制信号自动生成_1  (
    .OP2(OP[0]), .OP3(OP[1]), .MemToReg(MemToReg), .OP4(OP[2]), .OP5(OP[3]), .OP6(OP[4]), .F12(Funct[0]),
    .MemWrite(MemWrite), .F13(Funct[1]), .F14(Funct[2]), .F25(Funct[3]), .F30(Funct[4]), .ALU_SRC(ALU_SRC),
    .RegWrite(RegWrite), .ecall(\控制信号自动生成_1_ecall ), .S_Type(S_type), .BEQ(Beq), .BNE(Bne), .JALR(Jalr),
    .JAL(JAL), .sb(sb), .lui(lui), .srl(srl), .blt(blt), .CSRRCI(CSRRCI), .CSRRSI(CSRRSI));
  and and_1 (uret, in_3, \控制信号自动生成_1_ecall );
  and and_2 (ecall, ~in_3, \控制信号自动生成_1_ecall );  // AND_Gate

  // Other names for the same wires on the sheet: IR21 = in_3; OP_CODE[4:0] = OP

  // Notes on the sheet:
  //   运算器控制器，根据指令生成运算器功能选择信号
endmodule

// 运算器控制器
module \运算控制器自动生成  (
  input  OP2,
  input  OP3,
  input  OP4,
  input  OP5,
  input  OP6,
  input  F12,
  input  F13,
  input  F14,
  input  F25,
  input  F30,
  output S0,
  output S1,
  output S2,
  output S3
);

  wire and_1_out, and_2_out, and_3_out, and_4_out, and_5_out, and_6_out, and_7_out, and_8_out, and_9_out,
       and_10_out, and_11_out, and_12_out, and_13_out, and_14_out, and_15_out, and_16_out, and_17_out,
       and_18_out, and_19_out, and_20_out, and_21_out, and_22_out, and_23_out, and_24_out, and_25_out,
       and_26_out, and_27_out, and_28_out, and_29_out, and_30_out, and_31_out, and_32_out, and_33_out,
       and_34_out, and_35_out, and_36_out, and_37_out, and_38_out, and_39_out, and_40_out, and_41_out,
       and_42_out, and_43_out, and_44_out, not_1_out, not_2_out, not_3_out, not_4_out, not_5_out, not_6_out,
       not_7_out, not_8_out, not_9_out, not_10_out, not_11_out, not_12_out, not_13_out, not_14_out,
       not_15_out, not_16_out, not_17_out, not_18_out, not_19_out, not_20_out, not_21_out, not_22_out,
       not_23_out, not_24_out, not_25_out, not_26_out, not_27_out, not_28_out, not_29_out, not_30_out,
       not_31_out, not_32_out, not_33_out, not_34_out, not_35_out, not_36_out, not_37_out, not_38_out,
       not_39_out, not_40_out, not_41_out, not_42_out, not_43_out, not_44_out, not_45_out, not_46_out,
       not_47_out, not_48_out, not_49_out, not_50_out, not_51_out, not_52_out, not_53_out, not_54_out,
       not_55_out, not_56_out, not_57_out, not_58_out, not_59_out, not_60_out, not_61_out, not_62_out,
       not_63_out, not_64_out, not_65_out, not_66_out, not_67_out, not_68_out, not_69_out, not_70_out,
       not_71_out, not_72_out, not_73_out, not_74_out, not_75_out, not_76_out, not_77_out, not_78_out,
       not_79_out, not_80_out, not_81_out, not_82_out, not_83_out, not_84_out, not_85_out, not_86_out,
       not_87_out, not_88_out, not_89_out, not_90_out, not_91_out, not_92_out, not_93_out, not_94_out,
       not_95_out, not_96_out, not_97_out, not_98_out, not_99_out, not_100_out, not_101_out, not_102_out,
       not_103_out, not_104_out, not_105_out, not_106_out, not_107_out, not_108_out, not_109_out,
       not_110_out, not_111_out, not_112_out, not_113_out, not_114_out, not_115_out, not_116_out,
       not_117_out, not_118_out, not_119_out, not_120_out, not_121_out, not_122_out, not_123_out,
       not_124_out, not_125_out, not_126_out, not_127_out, not_128_out, not_129_out, not_130_out,
       not_131_out, not_132_out, not_133_out, not_134_out, not_135_out, not_136_out, not_137_out,
       not_138_out, not_139_out, not_140_out, not_141_out, not_142_out, not_143_out, not_144_out,
       not_145_out, not_146_out, not_147_out, not_148_out, not_149_out, not_150_out, not_151_out,
       not_152_out, not_153_out, not_154_out, not_155_out, not_156_out, not_157_out, not_158_out,
       not_159_out, not_160_out, not_161_out, not_162_out, not_163_out, not_164_out, not_165_out,
       not_166_out, not_167_out, not_168_out, not_169_out, not_170_out, not_171_out, not_172_out,
       not_173_out, not_174_out, not_175_out, not_176_out, not_177_out, not_178_out, not_179_out,
       not_180_out, not_181_out, not_182_out, not_183_out, not_184_out, not_185_out, not_186_out,
       not_187_out, not_188_out, not_189_out, not_190_out, not_191_out, not_192_out, not_193_out,
       not_194_out, not_195_out, not_196_out, not_197_out, not_198_out, not_199_out, not_200_out,
       not_201_out, not_202_out, not_203_out, not_204_out, not_205_out, not_206_out, not_207_out,
       not_208_out, not_209_out, not_210_out, not_211_out, not_212_out, not_213_out, not_214_out,
       not_215_out, not_216_out, not_217_out, not_218_out, not_219_out, not_220_out, not_221_out,
       not_222_out, not_223_out, not_224_out, not_225_out, not_226_out, not_227_out, not_228_out,
       not_229_out, not_230_out, not_231_out, not_232_out, not_233_out, not_234_out, not_235_out,
       not_236_out, not_237_out, not_238_out, not_239_out, not_240_out, not_241_out, not_242_out,
       not_243_out, not_244_out, not_245_out, not_246_out, not_247_out, not_248_out, not_249_out,
       not_250_out, not_251_out, not_252_out, not_253_out;

  not not_1 (not_1_out, F30);
  not not_2 (not_2_out, F25);
  not not_3 (not_3_out, F14);
  not not_4 (not_4_out, F13);
  not not_5 (not_5_out, F12);
  not not_6 (not_6_out, OP6);
  not not_7 (not_7_out, OP3);
  not not_8 (not_8_out, OP2);
  not not_9 (not_9_out, F30);
  not not_10 (not_10_out, F25);
  not not_11 (not_11_out, OP6);
  not not_12 (not_12_out, OP3);
  not not_13 (not_13_out, OP2);
  not not_14 (not_14_out, F30);
  not not_15 (not_15_out, F25);
  not not_16 (not_16_out, F14);
  not not_17 (not_17_out, F12);
  not not_18 (not_18_out, OP6);
  not not_19 (not_19_out, OP3);
  not not_20 (not_20_out, OP2);
  not not_21 (not_21_out, F14);
  not not_22 (not_22_out, F13);
  not not_23 (not_23_out, F12);
  not not_24 (not_24_out, OP6);
  not not_25 (not_25_out, OP5);
  not not_26 (not_26_out, OP3);
  not not_27 (not_27_out, OP2);
  not not_28 (not_28_out, OP6);
  not not_29 (not_29_out, OP5);
  not not_30 (not_30_out, OP3);
  not not_31 (not_31_out, OP2);
  not not_32 (not_32_out, F13);
  not not_33 (not_33_out, F12);
  not not_34 (not_34_out, OP6);
  not not_35 (not_35_out, OP5);
  not not_36 (not_36_out, OP3);
  not not_37 (not_37_out, OP2);
  not not_38 (not_38_out, F14);
  not not_39 (not_39_out, F12);
  not not_40 (not_40_out, OP6);
  not not_41 (not_41_out, OP5);
  not not_42 (not_42_out, OP3);
  not not_43 (not_43_out, OP2);
  not not_44 (not_44_out, F25);
  not not_45 (not_45_out, F13);
  not not_46 (not_46_out, OP6);
  not not_47 (not_47_out, OP5);
  not not_48 (not_48_out, OP3);
  not not_49 (not_49_out, OP2);
  not not_50 (not_50_out, F14);
  not not_51 (not_51_out, F12);
  not not_52 (not_52_out, OP6);
  not not_53 (not_53_out, OP5);
  not not_54 (not_54_out, OP4);
  not not_55 (not_55_out, OP3);
  not not_56 (not_56_out, OP2);
  not not_57 (not_57_out, F14);
  not not_58 (not_58_out, F12);
  not not_59 (not_59_out, OP6);
  not not_60 (not_60_out, OP4);
  not not_61 (not_61_out, OP3);
  not not_62 (not_62_out, OP2);
  not not_63 (not_63_out, F14);
  not not_64 (not_64_out, F13);
  not not_65 (not_65_out, F12);
  not not_66 (not_66_out, OP4);
  not not_67 (not_67_out, OP3);
  not not_68 (not_68_out, OP2);
  not not_69 (not_69_out, F14);
  not not_70 (not_70_out, F13);
  not not_71 (not_71_out, OP4);
  not not_72 (not_72_out, OP3);
  not not_73 (not_73_out, OP2);
  not not_74 (not_74_out, OP4);
  not not_75 (not_75_out, F14);
  not not_76 (not_76_out, F13);
  not not_77 (not_77_out, F12);
  not not_78 (not_78_out, OP4);
  not not_79 (not_79_out, OP3);
  not not_80 (not_80_out, F14);
  not not_81 (not_81_out, F13);
  not not_82 (not_82_out, F12);
  not not_83 (not_83_out, OP6);
  not not_84 (not_84_out, OP4);
  not not_85 (not_85_out, OP3);
  not not_86 (not_86_out, OP2);
  not not_87 (not_87_out, F13);
  not not_88 (not_88_out, F12);
  not not_89 (not_89_out, OP4);
  not not_90 (not_90_out, OP3);
  not not_91 (not_91_out, OP2);
  not not_92 (not_92_out, F25);
  not not_93 (not_93_out, F14);
  not not_94 (not_94_out, F13);
  not not_95 (not_95_out, F12);
  not not_96 (not_96_out, OP6);
  not not_97 (not_97_out, OP3);
  not not_98 (not_98_out, OP2);
  not not_99 (not_99_out, F30);
  not not_100 (not_100_out, F25);
  not not_101 (not_101_out, OP6);
  not not_102 (not_102_out, OP3);
  not not_103 (not_103_out, OP2);
  not not_104 (not_104_out, F30);
  not not_105 (not_105_out, F25);
  not not_106 (not_106_out, F14);
  not not_107 (not_107_out, F12);
  not not_108 (not_108_out, OP6);
  not not_109 (not_109_out, OP3);
  not not_110 (not_110_out, OP2);
  not not_111 (not_111_out, OP6);
  not not_112 (not_112_out, OP5);
  not not_113 (not_113_out, OP3);
  not not_114 (not_114_out, OP2);
  not not_115 (not_115_out, F14);
  not not_116 (not_116_out, F12);
  not not_117 (not_117_out, OP6);
  not not_118 (not_118_out, OP5);
  not not_119 (not_119_out, OP3);
  not not_120 (not_120_out, OP2);
  not not_121 (not_121_out, F30);
  not not_122 (not_122_out, F25);
  not not_123 (not_123_out, F13);
  not not_124 (not_124_out, OP6);
  not not_125 (not_125_out, OP5);
  not not_126 (not_126_out, OP3);
  not not_127 (not_127_out, OP2);
  not not_128 (not_128_out, F30);
  not not_129 (not_129_out, F25);
  not not_130 (not_130_out, F13);
  not not_131 (not_131_out, OP6);
  not not_132 (not_132_out, OP3);
  not not_133 (not_133_out, OP2);
  not not_134 (not_134_out, F13);
  not not_135 (not_135_out, F12);
  not not_136 (not_136_out, OP4);
  not not_137 (not_137_out, OP3);
  not not_138 (not_138_out, OP2);
  not not_139 (not_139_out, F30);
  not not_140 (not_140_out, F25);
  not not_141 (not_141_out, F14);
  not not_142 (not_142_out, F13);
  not not_143 (not_143_out, F12);
  not not_144 (not_144_out, OP6);
  not not_145 (not_145_out, OP3);
  not not_146 (not_146_out, OP2);
  not not_147 (not_147_out, F25);
  not not_148 (not_148_out, F14);
  not not_149 (not_149_out, F13);
  not not_150 (not_150_out, F12);
  not not_151 (not_151_out, OP6);
  not not_152 (not_152_out, OP3);
  not not_153 (not_153_out, OP2);
  not not_154 (not_154_out, F30);
  not not_155 (not_155_out, F25);
  not not_156 (not_156_out, OP6);
  not not_157 (not_157_out, OP3);
  not not_158 (not_158_out, OP2);
  not not_159 (not_159_out, F30);
  not not_160 (not_160_out, F25);
  not not_161 (not_161_out, F14);
  not not_162 (not_162_out, OP6);
  not not_163 (not_163_out, OP3);
  not not_164 (not_164_out, OP2);
  not not_165 (not_165_out, F14);
  not not_166 (not_166_out, F13);
  not not_167 (not_167_out, F12);
  not not_168 (not_168_out, OP6);
  not not_169 (not_169_out, OP5);
  not not_170 (not_170_out, OP3);
  not not_171 (not_171_out, OP2);
  not not_172 (not_172_out, OP6);
  not not_173 (not_173_out, OP5);
  not not_174 (not_174_out, OP3);
  not not_175 (not_175_out, OP2);
  not not_176 (not_176_out, F14);
  not not_177 (not_177_out, F12);
  not not_178 (not_178_out, OP6);
  not not_179 (not_179_out, OP5);
  not not_180 (not_180_out, OP4);
  not not_181 (not_181_out, OP3);
  not not_182 (not_182_out, OP2);
  not not_183 (not_183_out, F14);
  not not_184 (not_184_out, F12);
  not not_185 (not_185_out, OP6);
  not not_186 (not_186_out, OP4);
  not not_187 (not_187_out, OP3);
  not not_188 (not_188_out, OP2);
  not not_189 (not_189_out, F14);
  not not_190 (not_190_out, F13);
  not not_191 (not_191_out, F12);
  not not_192 (not_192_out, OP4);
  not not_193 (not_193_out, OP3);
  not not_194 (not_194_out, OP2);
  not not_195 (not_195_out, F14);
  not not_196 (not_196_out, F13);
  not not_197 (not_197_out, OP4);
  not not_198 (not_198_out, OP3);
  not not_199 (not_199_out, OP2);
  not not_200 (not_200_out, OP4);
  not not_201 (not_201_out, F14);
  not not_202 (not_202_out, F13);
  not not_203 (not_203_out, F12);
  not not_204 (not_204_out, OP4);
  not not_205 (not_205_out, OP3);
  not not_206 (not_206_out, F14);
  not not_207 (not_207_out, F13);
  not not_208 (not_208_out, F12);
  not not_209 (not_209_out, OP6);
  not not_210 (not_210_out, OP4);
  not not_211 (not_211_out, OP3);
  not not_212 (not_212_out, OP2);
  not not_213 (not_213_out, F30);
  not not_214 (not_214_out, F25);
  not not_215 (not_215_out, F12);
  not not_216 (not_216_out, OP6);
  not not_217 (not_217_out, OP3);
  not not_218 (not_218_out, OP2);
  not not_219 (not_219_out, F30);
  not not_220 (not_220_out, F25);
  not not_221 (not_221_out, F14);
  not not_222 (not_222_out, F12);
  not not_223 (not_223_out, OP6);
  not not_224 (not_224_out, OP3);
  not not_225 (not_225_out, OP2);
  not not_226 (not_226_out, F30);
  not not_227 (not_227_out, F25);
  not not_228 (not_228_out, F14);
  not not_229 (not_229_out, OP6);
  not not_230 (not_230_out, OP3);
  not not_231 (not_231_out, OP2);
  not not_232 (not_232_out, F12);
  not not_233 (not_233_out, OP6);
  not not_234 (not_234_out, OP5);
  not not_235 (not_235_out, OP3);
  not not_236 (not_236_out, OP2);
  not not_237 (not_237_out, F13);
  not not_238 (not_238_out, F12);
  not not_239 (not_239_out, OP6);
  not not_240 (not_240_out, OP5);
  not not_241 (not_241_out, OP3);
  not not_242 (not_242_out, OP2);
  not not_243 (not_243_out, F14);
  not not_244 (not_244_out, F12);
  not not_245 (not_245_out, OP6);
  not not_246 (not_246_out, OP5);
  not not_247 (not_247_out, OP3);
  not not_248 (not_248_out, OP2);
  not not_249 (not_249_out, F13);
  not not_250 (not_250_out, F12);
  not not_251 (not_251_out, OP4);
  not not_252 (not_252_out, OP3);
  not not_253 (not_253_out, OP2);
  and and_1 (and_1_out, not_1_out, not_2_out, not_3_out, not_4_out, not_5_out, not_6_out, OP5, OP4, not_7_out, not_8_out);
  and and_2 (and_2_out, not_9_out, not_10_out, F14, F13, F12, not_11_out, OP5, OP4, not_12_out, not_13_out);
  and and_3 (and_3_out, not_14_out, not_15_out, not_16_out, F13, not_17_out, not_18_out, OP5, OP4, not_19_out, not_20_out);
  and and_4 (and_4_out, not_21_out, not_22_out, not_23_out, not_24_out, not_25_out, OP4, not_26_out, not_27_out);
  and and_5 (and_5_out, F14, F13, F12, not_28_out, not_29_out, OP4, not_30_out, not_31_out);
  and and_6 (and_6_out, F14, not_32_out, not_33_out, not_34_out, not_35_out, OP4, not_36_out, not_37_out);
  and and_7 (and_7_out, not_38_out, F13, not_39_out, not_40_out, not_41_out, OP4, not_42_out, not_43_out);
  and and_8 (and_8_out, F30, not_44_out, F14, not_45_out, F12, not_46_out, not_47_out, OP4, not_48_out, not_49_out);
  and and_9 (and_9_out, not_50_out, F13, not_51_out, not_52_out, not_53_out, not_54_out, not_55_out, not_56_out);
  and and_10 (and_10_out, not_57_out, F13, not_58_out, not_59_out, OP5, not_60_out, not_61_out, not_62_out);
  and and_11 (and_11_out, not_63_out, not_64_out, not_65_out, OP6, OP5, not_66_out, not_67_out, not_68_out);
  and and_12 (and_12_out, not_69_out, not_70_out, F12, OP6, OP5, not_71_out, not_72_out, not_73_out);
  and and_13 (and_13_out, OP6, OP5, not_74_out, OP3, OP2);
  and and_14 (and_14_out, not_75_out, not_76_out, not_77_out, OP6, OP5, not_78_out, not_79_out, OP2);
  and and_15 (and_15_out, not_80_out, not_81_out, not_82_out, not_83_out, OP5, not_84_out, not_85_out, not_86_out);
  and and_16 (and_16_out, F14, not_87_out, not_88_out, OP6, OP5, not_89_out, not_90_out, not_91_out);
  and and_17 (and_17_out, F30, not_92_out, not_93_out, not_94_out, not_95_out, not_96_out, OP5, OP4, not_97_out, not_98_out);
  and and_18 (and_18_out, not_99_out, not_100_out, F14, F13, F12, not_101_out, OP5, OP4, not_102_out, not_103_out);
  and and_19 (and_19_out, not_104_out, not_105_out, not_106_out, F13, not_107_out, not_108_out, OP5, OP4, not_109_out, not_110_out);
  and and_20 (and_20_out, F14, F13, F12, not_111_out, not_112_out, OP4, not_113_out, not_114_out);
  and and_21 (and_21_out, not_115_out, F13, not_116_out, not_117_out, not_118_out, OP4, not_119_out, not_120_out);
  and and_22 (and_22_out, not_121_out, not_122_out, F14, not_123_out, F12, not_124_out, not_125_out, OP4, not_126_out, not_127_out);
  and and_23 (and_23_out, not_128_out, not_129_out, F14, not_130_out, F12, not_131_out, OP5, OP4, not_132_out, not_133_out);
  and and_24 (and_24_out, F14, not_134_out, not_135_out, OP6, OP5, not_136_out, not_137_out, not_138_out);
  and and_25 (and_25_out, not_139_out, not_140_out, not_141_out, not_142_out, not_143_out, not_144_out, OP5, OP4, not_145_out, not_146_out);
  and and_26 (and_26_out, F30, not_147_out, not_148_out, not_149_out, not_150_out, not_151_out, OP5, OP4, not_152_out, not_153_out);
  and and_27 (and_27_out, not_154_out, not_155_out, F14, F13, F12, not_156_out, OP5, OP4, not_157_out, not_158_out);
  and and_28 (and_28_out, not_159_out, not_160_out, not_161_out, F13, F12, not_162_out, OP5, OP4, not_163_out, not_164_out);
  and and_29 (and_29_out, not_165_out, not_166_out, not_167_out, not_168_out, not_169_out, OP4, not_170_out, not_171_out);
  and and_30 (and_30_out, F14, F13, F12, not_172_out, not_173_out, OP4, not_174_out, not_175_out);
  and and_31 (and_31_out, not_176_out, F13, not_177_out, not_178_out, not_179_out, not_180_out, not_181_out, not_182_out);
  and and_32 (and_32_out, not_183_out, F13, not_184_out, not_185_out, OP5, not_186_out, not_187_out, not_188_out);
  and and_33 (and_33_out, not_189_out, not_190_out, not_191_out, OP6, OP5, not_192_out, not_193_out, not_194_out);
  and and_34 (and_34_out, not_195_out, not_196_out, F12, OP6, OP5, not_197_out, not_198_out, not_199_out);
  and and_35 (and_35_out, OP6, OP5, not_200_out, OP3, OP2);
  and and_36 (and_36_out, not_201_out, not_202_out, not_203_out, OP6, OP5, not_204_out, not_205_out, OP2);
  and and_37 (and_37_out, not_206_out, not_207_out, not_208_out, not_209_out, OP5, not_210_out, not_211_out, not_212_out);
  and and_38 (and_38_out, not_213_out, not_214_out, F14, F13, not_215_out, not_216_out, OP5, OP4, not_217_out, not_218_out);
  and and_39 (and_39_out, not_219_out, not_220_out, not_221_out, F13, not_222_out, not_223_out, OP5, OP4, not_224_out, not_225_out);
  and and_40 (and_40_out, not_226_out, not_227_out, not_228_out, F13, F12, not_229_out, OP5, OP4, not_230_out, not_231_out);
  and and_41 (and_41_out, F14, F13, not_232_out, not_233_out, not_234_out, OP4, not_235_out, not_236_out);
  and and_42 (and_42_out, F14, not_237_out, not_238_out, not_239_out, not_240_out, OP4, not_241_out, not_242_out);
  and and_43 (and_43_out, not_243_out, F13, not_244_out, not_245_out, not_246_out, OP4, not_247_out, not_248_out);
  and and_44 (and_44_out, F14, not_249_out, not_250_out, OP6, OP5, not_251_out, not_252_out, not_253_out);
  or or_1 (S0, and_1_out, and_2_out, and_3_out, and_4_out, and_5_out, and_6_out, and_7_out, and_8_out, and_9_out, and_10_out, and_11_out, and_12_out, and_13_out, and_14_out, and_15_out, and_16_out);
  or or_2 (S1, and_17_out, and_18_out, and_19_out, and_20_out, and_21_out, and_22_out, and_23_out, and_24_out);
  or or_3 (S2, and_25_out, and_26_out, and_27_out, and_28_out, and_29_out, and_30_out, and_31_out, and_32_out, and_33_out, and_34_out, and_35_out, and_36_out, and_37_out);
  or or_4 (S3, and_38_out, and_39_out, and_40_out, and_41_out, and_42_out, and_43_out, and_44_out);
endmodule

// 控制信号生成
module \控制信号自动生成  (
  input  OP2,
  input  OP3,
  input  OP4,
  input  OP5,
  input  OP6,
  input  F12,
  input  F13,
  input  F14,
  input  F25,
  input  F30,
  output MemToReg,
  output MemWrite,
  output ALU_SRC,
  output RegWrite,
  output ecall,
  output S_Type,
  output BEQ,
  output BNE,
  output JALR,
  output JAL,
  output sb,
  output lui,
  output srl,
  output blt,
  output CSRRCI,
  output CSRRSI
);

  wire and_3_out, and_4_out, and_5_out, and_6_out, and_7_out, and_8_out, and_9_out, and_10_out, and_11_out,
       and_12_out, and_13_out, and_14_out, and_15_out, and_16_out, and_17_out, and_18_out, and_19_out,
       and_20_out, and_21_out, and_22_out, and_23_out, and_24_out, and_25_out, and_26_out, and_27_out,
       and_28_out, not_1_out, not_2_out, not_3_out, not_4_out, not_5_out, not_6_out, not_7_out, not_8_out,
       not_9_out, not_10_out, not_11_out, not_12_out, not_13_out, not_14_out, not_15_out, not_16_out,
       not_17_out, not_18_out, not_19_out, not_20_out, not_21_out, not_22_out, not_23_out, not_24_out,
       not_25_out, not_26_out, not_27_out, not_28_out, not_29_out, not_30_out, not_31_out, not_32_out,
       not_33_out, not_34_out, not_35_out, not_36_out, not_37_out, not_38_out, not_39_out, not_40_out,
       not_41_out, not_42_out, not_43_out, not_44_out, not_45_out, not_46_out, not_47_out, not_48_out,
       not_49_out, not_50_out, not_51_out, not_52_out, not_53_out, not_54_out, not_55_out, not_56_out,
       not_57_out, not_58_out, not_59_out, not_60_out, not_61_out, not_62_out, not_63_out, not_64_out,
       not_65_out, not_66_out, not_67_out, not_68_out, not_69_out, not_70_out, not_71_out, not_72_out,
       not_73_out, not_74_out, not_75_out, not_76_out, not_77_out, not_78_out, not_79_out, not_80_out,
       not_81_out, not_82_out, not_83_out, not_84_out, not_85_out, not_86_out, not_87_out, not_88_out,
       not_89_out, not_90_out, not_91_out, not_92_out, not_93_out, not_94_out, not_95_out, not_96_out,
       not_97_out, not_98_out, not_99_out, not_100_out, not_101_out, not_102_out, not_103_out, not_104_out,
       not_105_out, not_106_out, not_107_out, not_108_out, not_109_out, not_110_out, not_111_out,
       not_112_out, not_113_out, not_114_out, not_115_out, not_116_out, not_117_out, not_118_out,
       not_119_out, not_120_out, not_121_out, not_122_out, not_123_out, not_124_out, not_125_out,
       not_126_out, not_127_out, not_128_out, not_129_out, not_130_out, not_131_out, not_132_out,
       not_133_out, not_134_out, not_135_out, not_136_out, not_137_out, not_138_out, not_139_out,
       not_140_out, not_141_out, not_142_out, not_143_out, not_144_out, not_145_out, not_146_out,
       not_147_out, not_148_out, not_149_out, not_150_out, not_151_out, not_152_out, not_153_out,
       not_154_out, not_155_out, not_156_out, not_157_out, not_158_out, not_159_out, not_160_out,
       not_161_out, not_162_out, not_163_out, not_164_out, not_165_out, not_166_out, not_167_out,
       not_168_out, not_169_out, not_170_out, not_171_out, not_172_out, not_173_out, not_174_out,
       not_175_out, not_176_out, not_177_out, not_178_out, not_179_out, not_180_out, not_181_out,
       not_182_out, not_183_out, not_184_out, not_185_out, not_186_out, not_187_out, not_188_out,
       not_189_out, not_190_out, not_191_out, not_192_out, not_193_out, not_194_out, not_195_out,
       not_196_out, not_197_out, not_198_out, not_199_out, not_200_out, not_201_out, not_202_out,
       not_203_out, not_204_out, not_205_out, not_206_out, not_207_out, not_208_out, not_209_out,
       not_210_out, not_211_out;

  not not_1 (not_1_out, OP2);
  not not_2 (not_2_out, OP3);
  not not_3 (not_3_out, OP4);
  not not_4 (not_4_out, OP5);
  not not_5 (not_5_out, OP6);
  not not_6 (not_6_out, F12);
  not not_7 (not_7_out, F14);
  not not_8 (not_8_out, OP2);
  not not_9 (not_9_out, OP3);
  not not_10 (not_10_out, OP4);
  not not_11 (not_11_out, OP6);
  not not_12 (not_12_out, F12);
  not not_13 (not_13_out, F14);
  not not_14 (not_14_out, OP2);
  not not_15 (not_15_out, OP3);
  not not_16 (not_16_out, OP5);
  not not_17 (not_17_out, OP6);
  not not_18 (not_18_out, F12);
  not not_19 (not_19_out, F14);
  not not_20 (not_20_out, OP2);
  not not_21 (not_21_out, OP3);
  not not_22 (not_22_out, OP4);
  not not_23 (not_23_out, OP6);
  not not_24 (not_24_out, F12);
  not not_25 (not_25_out, F14);
  not not_26 (not_26_out, OP2);
  not not_27 (not_27_out, OP3);
  not not_28 (not_28_out, OP5);
  not not_29 (not_29_out, OP6);
  not not_30 (not_30_out, F12);
  not not_31 (not_31_out, OP2);
  not not_32 (not_32_out, OP3);
  not not_33 (not_33_out, OP5);
  not not_34 (not_34_out, OP6);
  not not_35 (not_35_out, F13);
  not not_36 (not_36_out, F14);
  not not_37 (not_37_out, OP2);
  not not_38 (not_38_out, OP3);
  not not_39 (not_39_out, OP5);
  not not_40 (not_40_out, OP6);
  not not_41 (not_41_out, F13);
  not not_42 (not_42_out, F25);
  not not_43 (not_43_out, OP2);
  not not_44 (not_44_out, OP3);
  not not_45 (not_45_out, OP5);
  not not_46 (not_46_out, OP6);
  not not_47 (not_47_out, OP3);
  not not_48 (not_48_out, OP4);
  not not_49 (not_49_out, F12);
  not not_50 (not_50_out, F13);
  not not_51 (not_51_out, F14);
  not not_52 (not_52_out, F30);
  not not_53 (not_53_out, F25);
  not not_54 (not_54_out, F14);
  not not_55 (not_55_out, F13);
  not not_56 (not_56_out, F12);
  not not_57 (not_57_out, OP6);
  not not_58 (not_58_out, OP3);
  not not_59 (not_59_out, OP2);
  not not_60 (not_60_out, F25);
  not not_61 (not_61_out, F14);
  not not_62 (not_62_out, F13);
  not not_63 (not_63_out, F12);
  not not_64 (not_64_out, OP6);
  not not_65 (not_65_out, OP3);
  not not_66 (not_66_out, OP2);
  not not_67 (not_67_out, F30);
  not not_68 (not_68_out, F25);
  not not_69 (not_69_out, OP6);
  not not_70 (not_70_out, OP3);
  not not_71 (not_71_out, OP2);
  not not_72 (not_72_out, F30);
  not not_73 (not_73_out, F25);
  not not_74 (not_74_out, F12);
  not not_75 (not_75_out, OP6);
  not not_76 (not_76_out, OP3);
  not not_77 (not_77_out, OP2);
  not not_78 (not_78_out, F30);
  not not_79 (not_79_out, F25);
  not not_80 (not_80_out, F14);
  not not_81 (not_81_out, F12);
  not not_82 (not_82_out, OP6);
  not not_83 (not_83_out, OP3);
  not not_84 (not_84_out, OP2);
  not not_85 (not_85_out, F30);
  not not_86 (not_86_out, F25);
  not not_87 (not_87_out, F14);
  not not_88 (not_88_out, OP6);
  not not_89 (not_89_out, OP3);
  not not_90 (not_90_out, OP2);
  not not_91 (not_91_out, F14);
  not not_92 (not_92_out, F13);
  not not_93 (not_93_out, F12);
  not not_94 (not_94_out, OP6);
  not not_95 (not_95_out, OP5);
  not not_96 (not_96_out, OP3);
  not not_97 (not_97_out, OP2);
  not not_98 (not_98_out, OP6);
  not not_99 (not_99_out, OP5);
  not not_100 (not_100_out, OP3);
  not not_101 (not_101_out, OP2);
  not not_102 (not_102_out, F12);
  not not_103 (not_103_out, OP6);
  not not_104 (not_104_out, OP5);
  not not_105 (not_105_out, OP3);
  not not_106 (not_106_out, OP2);
  not not_107 (not_107_out, F13);
  not not_108 (not_108_out, F12);
  not not_109 (not_109_out, OP6);
  not not_110 (not_110_out, OP5);
  not not_111 (not_111_out, OP3);
  not not_112 (not_112_out, OP2);
  not not_113 (not_113_out, F14);
  not not_114 (not_114_out, F12);
  not not_115 (not_115_out, OP6);
  not not_116 (not_116_out, OP5);
  not not_117 (not_117_out, OP3);
  not not_118 (not_118_out, OP2);
  not not_119 (not_119_out, F14);
  not not_120 (not_120_out, F13);
  not not_121 (not_121_out, OP6);
  not not_122 (not_122_out, OP5);
  not not_123 (not_123_out, OP3);
  not not_124 (not_124_out, OP2);
  not not_125 (not_125_out, F30);
  not not_126 (not_126_out, F25);
  not not_127 (not_127_out, F13);
  not not_128 (not_128_out, OP6);
  not not_129 (not_129_out, OP5);
  not not_130 (not_130_out, OP3);
  not not_131 (not_131_out, OP2);
  not not_132 (not_132_out, F25);
  not not_133 (not_133_out, F13);
  not not_134 (not_134_out, OP6);
  not not_135 (not_135_out, OP5);
  not not_136 (not_136_out, OP3);
  not not_137 (not_137_out, OP2);
  not not_138 (not_138_out, F14);
  not not_139 (not_139_out, F12);
  not not_140 (not_140_out, OP6);
  not not_141 (not_141_out, OP5);
  not not_142 (not_142_out, OP4);
  not not_143 (not_143_out, OP3);
  not not_144 (not_144_out, OP2);
  not not_145 (not_145_out, OP4);
  not not_146 (not_146_out, F14);
  not not_147 (not_147_out, F13);
  not not_148 (not_148_out, F12);
  not not_149 (not_149_out, OP4);
  not not_150 (not_150_out, OP3);
  not not_151 (not_151_out, F30);
  not not_152 (not_152_out, F25);
  not not_153 (not_153_out, F13);
  not not_154 (not_154_out, OP6);
  not not_155 (not_155_out, OP3);
  not not_156 (not_156_out, OP2);
  not not_157 (not_157_out, OP6);
  not not_158 (not_158_out, OP3);
  not not_159 (not_159_out, OP2);
  not not_160 (not_160_out, OP3);
  not not_161 (not_161_out, F12);
  not not_162 (not_162_out, F13);
  not not_163 (not_163_out, F14);
  not not_164 (not_164_out, OP2);
  not not_165 (not_165_out, OP3);
  not not_166 (not_166_out, OP4);
  not not_167 (not_167_out, OP6);
  not not_168 (not_168_out, F12);
  not not_169 (not_169_out, F14);
  not not_170 (not_170_out, OP2);
  not not_171 (not_171_out, OP3);
  not not_172 (not_172_out, OP4);
  not not_173 (not_173_out, F12);
  not not_174 (not_174_out, F13);
  not not_175 (not_175_out, F14);
  not not_176 (not_176_out, OP2);
  not not_177 (not_177_out, OP3);
  not not_178 (not_178_out, OP4);
  not not_179 (not_179_out, F13);
  not not_180 (not_180_out, F14);
  not not_181 (not_181_out, OP3);
  not not_182 (not_182_out, OP4);
  not not_183 (not_183_out, F12);
  not not_184 (not_184_out, F13);
  not not_185 (not_185_out, F14);
  not not_186 (not_186_out, OP4);
  not not_187 (not_187_out, OP2);
  not not_188 (not_188_out, OP3);
  not not_189 (not_189_out, OP4);
  not not_190 (not_190_out, OP6);
  not not_191 (not_191_out, F12);
  not not_192 (not_192_out, F13);
  not not_193 (not_193_out, F14);
  not not_194 (not_194_out, OP3);
  not not_195 (not_195_out, OP6);
  not not_196 (not_196_out, OP2);
  not not_197 (not_197_out, OP3);
  not not_198 (not_198_out, OP6);
  not not_199 (not_199_out, F13);
  not not_200 (not_200_out, F25);
  not not_201 (not_201_out, F30);
  not not_202 (not_202_out, OP2);
  not not_203 (not_203_out, OP3);
  not not_204 (not_204_out, OP4);
  not not_205 (not_205_out, F12);
  not not_206 (not_206_out, F13);
  not not_207 (not_207_out, OP2);
  not not_208 (not_208_out, OP3);
  not not_209 (not_209_out, OP2);
  not not_210 (not_210_out, OP3);
  not not_211 (not_211_out, F12);
  and and_1 (MemToReg, not_1_out, not_2_out, not_3_out, not_4_out, not_5_out, not_6_out, F13, not_7_out);
  and and_2 (MemWrite, not_8_out, not_9_out, not_10_out, OP5, not_11_out, not_12_out, not_13_out);
  and and_3 (and_3_out, not_14_out, not_15_out, not_16_out, not_17_out, not_18_out, F13, not_19_out);
  and and_4 (and_4_out, not_20_out, not_21_out, not_22_out, OP5, not_23_out, not_24_out, not_25_out);
  and and_5 (and_5_out, not_26_out, not_27_out, OP4, not_28_out, not_29_out, not_30_out);
  and and_6 (and_6_out, not_31_out, not_32_out, OP4, not_33_out, not_34_out, not_35_out, not_36_out);
  and and_7 (and_7_out, not_37_out, not_38_out, OP4, not_39_out, not_40_out, not_41_out, not_42_out);
  and and_8 (and_8_out, not_43_out, not_44_out, OP4, not_45_out, not_46_out, F13, F14);
  and and_9 (and_9_out, OP2, not_47_out, not_48_out, OP5, OP6, not_49_out, not_50_out, not_51_out);
  and and_10 (and_10_out, not_52_out, not_53_out, not_54_out, not_55_out, not_56_out, not_57_out, OP5, OP4, not_58_out, not_59_out);
  and and_11 (and_11_out, F30, not_60_out, not_61_out, not_62_out, not_63_out, not_64_out, OP5, OP4, not_65_out, not_66_out);
  and and_12 (and_12_out, not_67_out, not_68_out, F14, F13, F12, not_69_out, OP5, OP4, not_70_out, not_71_out);
  and and_13 (and_13_out, not_72_out, not_73_out, F14, F13, not_74_out, not_75_out, OP5, OP4, not_76_out, not_77_out);
  and and_14 (and_14_out, not_78_out, not_79_out, not_80_out, F13, not_81_out, not_82_out, OP5, OP4, not_83_out, not_84_out);
  and and_15 (and_15_out, not_85_out, not_86_out, not_87_out, F13, F12, not_88_out, OP5, OP4, not_89_out, not_90_out);
  and and_16 (and_16_out, not_91_out, not_92_out, not_93_out, not_94_out, not_95_out, OP4, not_96_out, not_97_out);
  and and_17 (and_17_out, F14, F13, F12, not_98_out, not_99_out, OP4, not_100_out, not_101_out);
  and and_18 (and_18_out, F14, F13, not_102_out, not_103_out, not_104_out, OP4, not_105_out, not_106_out);
  and and_19 (and_19_out, F14, not_107_out, not_108_out, not_109_out, not_110_out, OP4, not_111_out, not_112_out);
  and and_20 (and_20_out, not_113_out, F13, not_114_out, not_115_out, not_116_out, OP4, not_117_out, not_118_out);
  and and_21 (and_21_out, not_119_out, not_120_out, F12, not_121_out, not_122_out, OP4, not_123_out, not_124_out);
  and and_22 (and_22_out, not_125_out, not_126_out, F14, not_127_out, F12, not_128_out, not_129_out, OP4, not_130_out, not_131_out);
  and and_23 (and_23_out, F30, not_132_out, F14, not_133_out, F12, not_134_out, not_135_out, OP4, not_136_out, not_137_out);
  and and_24 (and_24_out, not_138_out, F13, not_139_out, not_140_out, not_141_out, not_142_out, not_143_out, not_144_out);
  and and_25 (and_25_out, OP6, OP5, not_145_out, OP3, OP2);
  and and_26 (and_26_out, not_146_out, not_147_out, not_148_out, OP6, OP5, not_149_out, not_150_out, OP2);
  and and_27 (and_27_out, not_151_out, not_152_out, F14, not_153_out, F12, not_154_out, OP5, OP4, not_155_out, not_156_out);
  and and_28 (and_28_out, not_157_out, OP5, OP4, not_158_out, OP2);
  and and_29 (ecall, not_159_out, not_160_out, OP4, OP5, OP6, not_161_out, not_162_out, not_163_out);
  and and_30 (S_Type, not_164_out, not_165_out, not_166_out, OP5, not_167_out, not_168_out, not_169_out);
  and and_31 (BEQ, not_170_out, not_171_out, not_172_out, OP5, OP6, not_173_out, not_174_out, not_175_out);
  and and_32 (BNE, not_176_out, not_177_out, not_178_out, OP5, OP6, F12, not_179_out, not_180_out);
  and and_33 (JALR, OP2, not_181_out, not_182_out, OP5, OP6, not_183_out, not_184_out, not_185_out);
  and and_34 (JAL, OP2, OP3, not_186_out, OP5, OP6);
  and and_35 (sb, not_187_out, not_188_out, not_189_out, OP5, not_190_out, not_191_out, not_192_out, not_193_out);
  and and_36 (lui, OP2, not_194_out, OP4, OP5, not_195_out);
  and and_37 (srl, not_196_out, not_197_out, OP4, OP5, not_198_out, F12, not_199_out, F14, not_200_out, not_201_out);
  and and_38 (blt, not_202_out, not_203_out, not_204_out, OP5, OP6, not_205_out, not_206_out, F14);
  and and_39 (CSRRCI, not_207_out, not_208_out, OP4, OP5, OP6, F12, F13, F14);
  and and_40 (CSRRSI, not_209_out, not_210_out, OP4, OP5, OP6, not_211_out, F13, F14);
  or or_1 (ALU_SRC, and_3_out, and_4_out, and_5_out, and_6_out, and_7_out, and_8_out, and_9_out);
  or or_2 (RegWrite, and_10_out, and_11_out, and_12_out, and_13_out, and_14_out, and_15_out, and_16_out, and_17_out, and_18_out, and_19_out, and_20_out, and_21_out, and_22_out, and_23_out, and_24_out, and_25_out, and_26_out, and_27_out, and_28_out);
endmodule

module \中断按键参考电路  (
  input  \同步清零信号 ,
  output \与中断屏蔽位与 
);

  wire \_1号中断_out , and_1_out, clock_1_out, d_ff_1_q, or_1_out, or_2_out;

  Clock #(.highDuration(1), .lowDuration(1)) clock_1 (.out(clock_1_out));
  Button \_1号中断  (.out(\_1号中断_out ));
  LED #(.active("true")) \_1号中断等待指示灯  (.in(or_1_out));
  or or_1 (or_1_out, \与中断屏蔽位与 , d_ff_1_q);
  D_Flip_Flop #(.trigger("rising"), .Pre_Clr_Positions("LEGACY"), .NegatePresetClear("false"), .enable("true"), .NewFFLayout("false")) d_ff_1 (
    .clk(\_1号中断_out ), .D(1'b1), .Q(d_ff_1_q), .reset(\与中断屏蔽位与 ));  // open: Qn, preset, en
  or or_2 (or_2_out, d_ff_1_q, \与中断屏蔽位与 );
  and and_1 (and_1_out, or_2_out, ~\同步清零信号 );  // AND_Gate
  D_Flip_Flop #(.trigger("rising"), .Pre_Clr_Positions("LEGACY"), .NegatePresetClear("false"), .enable("true"), .NewFFLayout("false")) IR1 (
    .clk(clock_1_out), .D(and_1_out), .Q(\与中断屏蔽位与 ));  // open: Qn, preset, en, reset

  // Notes on the sheet:
  //   中断信号采样参考电路
  //   Reset 
endmodule

module IF_ID (
  input  en,
  input  RST,
  input  [31:0] IR,
  input  [31:0] PC_4,
  input  [31:0] PC,
  input  PredictJump,
  input  CLK,
  output [31:0] IR_2,
  output [31:0] PC_4_2,
  output [31:0] PC_2,
  output PredictJump_2
);

  wire multiplexer_4_out;
  wire [31:0] multiplexer_1_out, multiplexer_2_out, multiplexer_3_out;

  Multiplexer #(.select(1), .width(32), .disabled("Z"), .enable("false")) multiplexer_1 (
    .in0(IR), .in1({32{1'b0}}), .out(multiplexer_1_out), .sel(RST));
  Multiplexer #(.select(1), .width(32), .disabled("Z"), .enable("false")) multiplexer_2 (
    .in0(PC_4), .in1({32{1'b0}}), .out(multiplexer_2_out), .sel(RST));
  Multiplexer #(.select(1), .width(32), .disabled("Z"), .enable("false")) multiplexer_3 (
    .in0(PC), .in1({32{1'b0}}), .out(multiplexer_3_out), .sel(RST));
  Multiplexer #(.select(1), .width(1), .disabled("Z"), .enable("false")) multiplexer_4 (
    .in0(PredictJump), .in1(1'b0), .out(multiplexer_4_out), .sel(RST));
  Register #(.width(32), .trigger("rising"), .Select("low")) u_IR (
    .D(multiplexer_1_out), .en(en), .Q(IR_2), .clk(CLK));  // open: clr
  Register #(.width(32), .trigger("rising"), .Select("low")) u_PC_4 (
    .D(multiplexer_2_out), .en(en), .Q(PC_4_2), .clk(CLK));  // open: clr
  Register #(.width(32), .trigger("rising"), .Select("low")) u_PC (
    .D(multiplexer_3_out), .en(en), .Q(PC_2), .clk(CLK));  // open: clr
  Register #(.width(1), .trigger("rising"), .Select("low")) u_PredictJump (
    .D(multiplexer_4_out), .en(en), .Q(PredictJump_2), .clk(CLK));  // open: clr
endmodule

module ID_EX (
  input  RST,
  input  en,
  input  RegWrite,
  input  MemToReg,
  input  MemWrite,
  input  [3:0] AluOP,
  input  Beq,
  input  AluSrc,
  input  Bne,
  input  [31:0] R1,
  input  [31:0] R2,
  input  [4:0] WriteReg_num,
  input  [31:0] imm32B,
  input  [31:0] imm32U,
  input  [31:0] PC,
  input  [31:0] IR,
  input  JAL,
  input  JALR,
  input  [31:0] imm32J,
  input  uret,
  input  srl,
  input  [1:0] Rtf,
  input  PredictJump,
  input  blt,
  input  sb,
  input  [1:0] Rsf,
  input  lui,
  input  ecall,
  input  [31:0] imm,
  input  predictjump_2,
  input  CLK,
  output RegWrite_2,
  output MemToReg_2,
  output MemWrite_2,
  output [3:0] AluOP_2,
  output Beq_2,
  output AluSrc_2,
  output Bne_2,
  output [31:0] R1_2,
  output [31:0] R2_2,
  output [4:0] WriteReg_num_2,
  output [31:0] imm32B_2,
  output [31:0] imm32U_2,
  output [31:0] PC_2,
  output [31:0] IR_2,
  output JAL_2,
  output JALR_2,
  output [31:0] imm32J_2,
  output uret_2,
  output srl_2,
  output [1:0] Rtf_2,
  output PredictJump_3,
  output blt_2,
  output sb_2,
  output [1:0] Rsf_2,
  output lui_2,
  output ecall_2,
  output [31:0] imm_2,
  output predictjump_4
);

  wire multiplexer_1_out, multiplexer_2_out, multiplexer_3_out, multiplexer_5_out, multiplexer_6_out,
       multiplexer_7_out, multiplexer_15_out, multiplexer_16_out, multiplexer_18_out, multiplexer_19_out,
       multiplexer_21_out, multiplexer_22_out, multiplexer_23_out, multiplexer_25_out, multiplexer_26_out,
       multiplexer_28_out;
  wire [1:0] multiplexer_20_out, multiplexer_24_out;
  wire [3:0] multiplexer_4_out;
  wire [4:0] multiplexer_10_out;
  wire [31:0] multiplexer_8_out, multiplexer_9_out, multiplexer_11_out, multiplexer_12_out,
       multiplexer_13_out, multiplexer_14_out, multiplexer_17_out, multiplexer_27_out;

  Multiplexer #(.select(1), .width(1), .disabled("Z"), .enable("false")) multiplexer_1 (
    .in0(RegWrite), .in1(1'b0), .out(multiplexer_1_out), .sel(RST));
  Multiplexer #(.select(1), .width(1), .disabled("Z"), .enable("false")) multiplexer_2 (
    .in0(MemToReg), .in1(1'b0), .out(multiplexer_2_out), .sel(RST));
  Multiplexer #(.select(1), .width(1), .disabled("Z"), .enable("false")) multiplexer_3 (
    .in0(MemWrite), .in1(1'b0), .out(multiplexer_3_out), .sel(RST));
  Multiplexer #(.select(1), .width(4), .disabled("Z"), .enable("false")) multiplexer_4 (
    .in0(AluOP), .in1(4'b0000), .out(multiplexer_4_out), .sel(RST));
  Multiplexer #(.select(1), .width(1), .disabled("Z"), .enable("false")) multiplexer_5 (
    .in0(Beq), .in1(1'b0), .out(multiplexer_5_out), .sel(RST));
  Multiplexer #(.select(1), .width(1), .disabled("Z"), .enable("false")) multiplexer_6 (
    .in0(AluSrc), .in1(1'b0), .out(multiplexer_6_out), .sel(RST));
  Multiplexer #(.select(1), .width(1), .disabled("Z"), .enable("false")) multiplexer_7 (
    .in0(Bne), .in1(1'b0), .out(multiplexer_7_out), .sel(RST));
  Multiplexer #(.select(1), .width(32), .disabled("Z"), .enable("false")) multiplexer_8 (
    .in0(R1), .in1({32{1'b0}}), .out(multiplexer_8_out), .sel(RST));
  Multiplexer #(.select(1), .width(32), .disabled("Z"), .enable("false")) multiplexer_9 (
    .in0(R2), .in1({32{1'b0}}), .out(multiplexer_9_out), .sel(RST));
  Multiplexer #(.select(1), .width(5), .disabled("Z"), .enable("false")) multiplexer_10 (
    .in0(WriteReg_num), .in1({5{1'b0}}), .out(multiplexer_10_out), .sel(RST));
  Multiplexer #(.select(1), .width(32), .disabled("Z"), .enable("false")) multiplexer_11 (
    .in0(imm32B), .in1({32{1'b0}}), .out(multiplexer_11_out), .sel(RST));
  Multiplexer #(.select(1), .width(32), .disabled("Z"), .enable("false")) multiplexer_12 (
    .in0(imm32U), .in1({32{1'b0}}), .out(multiplexer_12_out), .sel(RST));
  Multiplexer #(.select(1), .width(32), .disabled("Z"), .enable("false")) multiplexer_13 (
    .in0(PC), .in1({32{1'b0}}), .out(multiplexer_13_out), .sel(RST));
  Multiplexer #(.select(1), .width(32), .disabled("Z"), .enable("false")) multiplexer_14 (
    .in0(IR), .in1({32{1'b0}}), .out(multiplexer_14_out), .sel(RST));
  Multiplexer #(.select(1), .width(1), .disabled("Z"), .enable("false")) multiplexer_15 (
    .in0(JAL), .in1(1'b0), .out(multiplexer_15_out), .sel(RST));
  Multiplexer #(.select(1), .width(1), .disabled("Z"), .enable("false")) multiplexer_16 (
    .in0(JALR), .in1(1'b0), .out(multiplexer_16_out), .sel(RST));
  Multiplexer #(.select(1), .width(32), .disabled("Z"), .enable("false")) multiplexer_17 (
    .in0(imm32J), .in1({32{1'b0}}), .out(multiplexer_17_out), .sel(RST));
  Multiplexer #(.select(1), .width(1), .disabled("Z"), .enable("false")) multiplexer_18 (
    .in0(uret), .in1(1'b0), .out(multiplexer_18_out), .sel(RST));
  Multiplexer #(.select(1), .width(1), .disabled("Z"), .enable("false")) multiplexer_19 (
    .in0(srl), .in1(1'b0), .out(multiplexer_19_out), .sel(RST));
  Multiplexer #(.select(1), .width(2), .disabled("Z"), .enable("false")) multiplexer_20 (
    .in0(Rtf), .in1(2'b00), .out(multiplexer_20_out), .sel(RST));
  Multiplexer #(.select(1), .width(1), .disabled("Z"), .enable("false")) multiplexer_21 (
    .in0(PredictJump), .in1(1'b0), .out(multiplexer_21_out), .sel(RST));
  Multiplexer #(.select(1), .width(1), .disabled("Z"), .enable("false")) multiplexer_22 (
    .in0(blt), .in1(1'b0), .out(multiplexer_22_out), .sel(RST));
  Multiplexer #(.select(1), .width(1), .disabled("Z"), .enable("false")) multiplexer_23 (
    .in0(sb), .in1(1'b0), .out(multiplexer_23_out), .sel(RST));
  Multiplexer #(.select(1), .width(2), .disabled("Z"), .enable("false")) multiplexer_24 (
    .in0(Rsf), .in1(2'b00), .out(multiplexer_24_out), .sel(RST));
  Multiplexer #(.select(1), .width(1), .disabled("Z"), .enable("false")) multiplexer_25 (
    .in0(lui), .in1(1'b0), .out(multiplexer_25_out), .sel(RST));
  Multiplexer #(.select(1), .width(1), .disabled("Z"), .enable("false")) multiplexer_26 (
    .in0(ecall), .in1(1'b0), .out(multiplexer_26_out), .sel(RST));
  Multiplexer #(.select(1), .width(32), .disabled("Z"), .enable("false")) multiplexer_27 (
    .in0(imm), .in1({32{1'b0}}), .out(multiplexer_27_out), .sel(RST));
  Multiplexer #(.select(1), .width(1), .disabled("Z"), .enable("false")) multiplexer_28 (
    .in0(predictjump_2), .in1(1'b0), .out(multiplexer_28_out), .sel(RST));
  Register #(.width(1), .trigger("rising"), .Select("low")) register_1 (
    .D(multiplexer_1_out), .en(en), .Q(RegWrite_2), .clk(CLK));  // open: clr
  Register #(.width(1), .trigger("rising"), .Select("low")) register_2 (
    .D(multiplexer_2_out), .en(en), .Q(MemToReg_2), .clk(CLK));  // open: clr
  Register #(.width(1), .trigger("rising"), .Select("low")) register_3 (
    .D(multiplexer_3_out), .en(en), .Q(MemWrite_2), .clk(CLK));  // open: clr
  Register #(.width(4), .trigger("rising"), .Select("low")) register_4 (
    .D(multiplexer_4_out), .en(en), .Q(AluOP_2), .clk(CLK));  // open: clr
  Register #(.width(1), .trigger("rising"), .Select("low")) register_5 (
    .D(multiplexer_5_out), .en(en), .Q(Beq_2), .clk(CLK));  // open: clr
  Register #(.width(1), .trigger("rising"), .Select("low")) register_6 (
    .D(multiplexer_6_out), .en(en), .Q(AluSrc_2), .clk(CLK));  // open: clr
  Register #(.width(1), .trigger("rising"), .Select("low")) register_7 (
    .D(multiplexer_7_out), .en(en), .Q(Bne_2), .clk(CLK));  // open: clr
  Register #(.width(32), .trigger("rising"), .Select("low")) register_8 (
    .D(multiplexer_8_out), .en(en), .Q(R1_2), .clk(CLK));  // open: clr
  Register #(.width(32), .trigger("rising"), .Select("low")) register_9 (
    .D(multiplexer_9_out), .en(en), .Q(R2_2), .clk(CLK));  // open: clr
  Register #(.width(5), .trigger("rising"), .Select("low")) register_10 (
    .D(multiplexer_10_out), .en(en), .Q(WriteReg_num_2), .clk(CLK));  // open: clr
  Register #(.width(32), .trigger("rising"), .Select("low")) register_11 (
    .D(multiplexer_11_out), .en(en), .Q(imm32B_2), .clk(CLK));  // open: clr
  Register #(.width(32), .trigger("rising"), .Select("low")) register_12 (
    .D(multiplexer_12_out), .en(en), .Q(imm32U_2), .clk(CLK));  // open: clr
  Register #(.width(32), .trigger("rising"), .Select("low")) register_13 (
    .D(multiplexer_13_out), .en(en), .Q(PC_2), .clk(CLK));  // open: clr
  Register #(.width(32), .trigger("rising"), .Select("low")) register_14 (
    .D(multiplexer_14_out), .en(en), .Q(IR_2), .clk(CLK));  // open: clr
  Register #(.width(1), .trigger("rising"), .Select("low")) register_15 (
    .D(multiplexer_15_out), .en(en), .Q(JAL_2), .clk(CLK));  // open: clr
  Register #(.width(1), .trigger("rising"), .Select("low")) register_16 (
    .D(multiplexer_16_out), .en(en), .Q(JALR_2), .clk(CLK));  // open: clr
  Register #(.width(32), .trigger("rising"), .Select("low")) register_17 (
    .D(multiplexer_17_out), .en(en), .Q(imm32J_2), .clk(CLK));  // open: clr
  Register #(.width(1), .trigger("rising"), .Select("low")) register_18 (
    .D(multiplexer_18_out), .en(en), .Q(uret_2), .clk(CLK));  // open: clr
  Register #(.width(1), .trigger("rising"), .Select("low")) register_19 (
    .D(multiplexer_19_out), .en(en), .Q(srl_2), .clk(CLK));  // open: clr
  Register #(.width(2), .trigger("rising"), .Select("low")) register_20 (
    .D(multiplexer_20_out), .en(en), .Q(Rtf_2), .clk(CLK));  // open: clr
  Register #(.width(1), .trigger("rising"), .Select("low")) register_21 (
    .D(multiplexer_21_out), .en(en), .Q(PredictJump_3), .clk(CLK));  // open: clr
  Register #(.width(1), .trigger("rising"), .Select("low")) register_22 (
    .D(multiplexer_22_out), .en(en), .Q(blt_2), .clk(CLK));  // open: clr
  Register #(.width(1), .trigger("rising"), .Select("low")) register_23 (
    .D(multiplexer_23_out), .en(en), .Q(sb_2), .clk(CLK));  // open: clr
  Register #(.width(2), .trigger("rising"), .Select("low")) register_24 (
    .D(multiplexer_24_out), .en(en), .Q(Rsf_2), .clk(CLK));  // open: clr
  Register #(.width(1), .trigger("rising"), .Select("low")) register_25 (
    .D(multiplexer_25_out), .en(en), .Q(lui_2), .clk(CLK));  // open: clr
  Register #(.width(1), .trigger("rising"), .Select("low")) register_26 (
    .D(multiplexer_26_out), .en(en), .Q(ecall_2), .clk(CLK));  // open: clr
  Register #(.width(32), .trigger("rising"), .Select("low")) register_27 (
    .D(multiplexer_27_out), .en(en), .Q(imm_2), .clk(CLK));  // open: clr
  Register #(.width(1), .trigger("rising"), .Select("low")) register_28 (
    .D(multiplexer_28_out), .en(en), .Q(predictjump_4), .clk(CLK));  // open: clr
endmodule

module EX_MEM (
  input  RegWrite,
  input  MemToReg,
  input  MemWrite,
  input  [31:0] AluResult,
  input  [31:0] WriteData,
  input  [4:0] WriteReg_num,
  input  [31:0] PC,
  input  [31:0] IR,
  input  JAL,
  input  JALR,
  input  [31:0] Bj,
  input  lui,
  input  sb,
  input  [31:0] lu,
  input  halt,
  input  CLK,
  input  en,
  input  RST,
  output RegWrite_2,
  output MemToReg_2,
  output MemWrite_2,
  output [31:0] AluResult_2,
  output [31:0] WriteData_2,
  output [4:0] WriteReg_num_2,
  output [31:0] PC_2,
  output [31:0] IR_2,
  output JAL_2,
  output JALR_2,
  output [31:0] bj_2,
  output lui_2,
  output sb_2,
  output [31:0] lu_2,
  output halt_2
);

  Register #(.width(1), .trigger("rising"), .Select("low")) register_1 (
    .D(RegWrite), .en(en), .Q(RegWrite_2), .clk(CLK), .clr(RST));
  Register #(.width(1), .trigger("rising"), .Select("low")) register_2 (
    .D(MemToReg), .en(en), .Q(MemToReg_2), .clk(CLK), .clr(RST));
  Register #(.width(1), .trigger("rising"), .Select("low")) register_3 (
    .D(MemWrite), .en(en), .Q(MemWrite_2), .clk(CLK), .clr(RST));
  Register #(.width(32), .trigger("rising"), .Select("low")) register_4 (
    .D(AluResult), .en(en), .Q(AluResult_2), .clk(CLK), .clr(RST));
  Register #(.width(32), .trigger("rising"), .Select("low")) register_5 (
    .D(WriteData), .en(en), .Q(WriteData_2), .clk(CLK), .clr(RST));
  Register #(.width(5), .trigger("rising"), .Select("low")) register_6 (
    .D(WriteReg_num), .en(en), .Q(WriteReg_num_2), .clk(CLK), .clr(RST));
  Register #(.width(32), .trigger("rising"), .Select("low")) u_PC (.D(PC), .en(en), .Q(PC_2), .clk(CLK), .clr(RST));
  Register #(.width(32), .trigger("rising"), .Select("low")) u_IR (.D(IR), .en(en), .Q(IR_2), .clk(CLK), .clr(RST));
  Register #(.width(1), .trigger("rising"), .Select("low")) u_JAL (.D(JAL), .en(en), .Q(JAL_2), .clk(CLK), .clr(RST));
  Register #(.width(1), .trigger("rising"), .Select("low")) u_JALR (
    .D(JALR), .en(en), .Q(JALR_2), .clk(CLK), .clr(RST));
  Register #(.width(32), .trigger("rising"), .Select("low")) PC_4 (.D(Bj), .en(en), .Q(bj_2), .clk(CLK), .clr(RST));
  Register #(.width(1), .trigger("rising"), .Select("low")) u_lui (.D(lui), .en(en), .Q(lui_2), .clk(CLK), .clr(RST));
  Register #(.width(1), .trigger("rising"), .Select("low")) u_sb (.D(sb), .en(en), .Q(sb_2), .clk(CLK), .clr(RST));
  Register #(.width(32), .trigger("rising"), .Select("low")) u_lu (.D(lu), .en(en), .Q(lu_2), .clk(CLK), .clr(RST));
  Register #(.width(1), .trigger("rising"), .Select("low")) u_halt (
    .D(halt), .en(en), .Q(halt_2), .clk(CLK), .clr(RST));
endmodule

module MEM_WB (
  input  RegWrite,
  input  MemToReg,
  input  [31:0] AluResult,
  input  [31:0] ReadData,
  input  [4:0] WriteReg_num,
  input  [31:0] PC,
  input  [31:0] IR,
  input  [31:0] lu,
  input  JAL,
  input  JALR,
  input  lui,
  input  halt,
  input  CLK,
  input  en,
  input  RST,
  output RegWrite_2,
  output MemToReg_2,
  output [31:0] AluResult_2,
  output [31:0] ReadData_2,
  output [4:0] WriteReg_num_2,
  output [31:0] PC_2,
  output [31:0] IR_2,
  output [31:0] lu_2,
  output JAL_2,
  output JALR_2,
  output lui_2,
  output halt_2
);

  Register #(.width(1), .trigger("rising"), .Select("low")) register_1 (
    .D(RegWrite), .en(en), .Q(RegWrite_2), .clk(CLK), .clr(RST));
  Register #(.width(1), .trigger("rising"), .Select("low")) register_2 (
    .D(MemToReg), .en(en), .Q(MemToReg_2), .clk(CLK), .clr(RST));
  Register #(.width(32), .trigger("rising"), .Select("low")) register_3 (
    .D(AluResult), .en(en), .Q(AluResult_2), .clk(CLK), .clr(RST));
  Register #(.width(32), .trigger("rising"), .Select("low")) register_4 (
    .D(ReadData), .en(en), .Q(ReadData_2), .clk(CLK), .clr(RST));
  Register #(.width(5), .trigger("rising"), .Select("low")) register_5 (
    .D(WriteReg_num), .en(en), .Q(WriteReg_num_2), .clk(CLK), .clr(RST));
  Register #(.width(32), .trigger("rising"), .Select("low")) u_PC (.D(PC), .en(en), .Q(PC_2), .clk(CLK), .clr(RST));
  Register #(.width(32), .trigger("rising"), .Select("low")) u_IR (.D(IR), .en(en), .Q(IR_2), .clk(CLK), .clr(RST));
  Register #(.width(32), .trigger("rising"), .Select("low")) u_lu (.D(lu), .en(en), .Q(lu_2), .clk(CLK), .clr(RST));
  Register #(.width(1), .trigger("rising"), .Select("low")) u_JAL (.D(JAL), .en(en), .Q(JAL_2), .clk(CLK), .clr(RST));
  Register #(.width(1), .trigger("rising"), .Select("low")) u_JALR (
    .D(JALR), .en(en), .Q(JALR_2), .clk(CLK), .clr(RST));
  Register #(.width(1), .trigger("rising"), .Select("low")) u_lui (.D(lui), .en(en), .Q(lui_2), .clk(CLK), .clr(RST));
  Register #(.width(1), .trigger("rising"), .Select("low")) u_halt (
    .D(halt), .en(en), .Q(halt_2), .clk(CLK), .clr(RST));
endmodule

module \数据相关检测逻辑  (
  input  [31:0] ID_IR,
  input  [4:0] EX_WriteReg_num,
  input  EX_RegWrite,
  input  [4:0] MEM_WriteReg_num,
  input  MEM_RegWrite,
  output DataHazzard
);

  wire and_2_out, and_3_out, and_4_out, and_5_out, comparator_1_eq, comparator_2_eq, comparator_3_eq,
       comparator_4_eq, comparator_5_eq, comparator_6_eq, comparator_7_eq, comparator_8_eq, comparator_9_eq,
       comparator_10_eq, comparator_11_eq, comparator_12_eq, IR__ecall_URET, not_1_out, not_2_out, or_2_out,
       RsUsed, RtUsed;
  wire [4:0] multiplexer_1_out, multiplexer_2_out;

  Multiplexer #(.select(1), .width(5), .disabled("Z"), .enable("false")) multiplexer_1 (
    .in0(ID_IR[19:15]), .in1(5'b01010), .out(multiplexer_1_out), .sel(IR__ecall_URET));
  Multiplexer #(.select(1), .width(5), .disabled("Z"), .enable("false")) multiplexer_2 (
    .in0(ID_IR[24:20]), .in1(5'b10001), .out(multiplexer_2_out), .sel(IR__ecall_URET));
  Comparator #(.width(5), .mode("twosComplement")) comparator_1 (
    .a(ID_IR[6:2]), .b(5'b01100), .eq(comparator_1_eq));  // open: gt, lt
  Comparator #(.width(5), .mode("twosComplement")) comparator_2 (
    .a(ID_IR[6:2]), .b(5'b01000), .eq(comparator_2_eq));  // open: gt, lt
  Comparator #(.width(5), .mode("twosComplement")) comparator_3 (
    .a(ID_IR[6:2]), .b(5'b11000), .eq(comparator_3_eq));  // open: gt, lt
  Comparator #(.width(5), .mode("twosComplement")) comparator_4 (
    .a(ID_IR[6:2]), .b(5'b11100), .eq(comparator_4_eq));  // open: gt, lt
  Comparator #(.width(3), .mode("twosComplement")) comparator_5 (
    .a(ID_IR[14:12]), .b(3'b000), .eq(comparator_5_eq));  // open: gt, lt
  Comparator #(.width(5), .mode("twosComplement")) comparator_6 (
    .a(ID_IR[6:2]), .b(5'b11011), .eq(comparator_6_eq));  // open: gt, lt
  Comparator #(.width(5), .mode("twosComplement")) comparator_7 (
    .a({5{1'b0}}), .b(multiplexer_1_out), .eq(comparator_7_eq));  // open: gt, lt
  Comparator #(.width(5), .mode("twosComplement")) comparator_8 (
    .a({5{1'b0}}), .b(multiplexer_2_out), .eq(comparator_8_eq));  // open: gt, lt
  Comparator #(.width(5), .mode("twosComplement")) comparator_9 (
    .a(multiplexer_2_out), .b(EX_WriteReg_num), .eq(comparator_9_eq));  // open: gt, lt
  Comparator #(.width(5), .mode("twosComplement")) comparator_10 (
    .a(multiplexer_1_out), .b(EX_WriteReg_num), .eq(comparator_10_eq));  // open: gt, lt
  Comparator #(.width(5), .mode("twosComplement")) comparator_11 (
    .a(multiplexer_2_out), .b(MEM_WriteReg_num), .eq(comparator_11_eq));  // open: gt, lt
  Comparator #(.width(5), .mode("twosComplement")) comparator_12 (
    .a(multiplexer_1_out), .b(MEM_WriteReg_num), .eq(comparator_12_eq));  // open: gt, lt
  and and_1 (IR__ecall_URET, comparator_4_eq, comparator_5_eq);
  not not_1 (not_1_out, comparator_7_eq);
  not not_2 (not_2_out, comparator_8_eq);
  or or_1 (RsUsed, comparator_1_eq, comparator_2_eq, comparator_3_eq, IR__ecall_URET);
  or or_2 (or_2_out, IR__ecall_URET, comparator_6_eq);
  not not_3 (RtUsed, or_2_out);
  and and_2 (and_2_out, RsUsed, not_2_out, EX_RegWrite, comparator_9_eq);
  and and_3 (and_3_out, RtUsed, not_1_out, EX_RegWrite, comparator_10_eq);
  and and_4 (and_4_out, RsUsed, not_2_out, MEM_RegWrite, comparator_11_eq);
  and and_5 (and_5_out, RtUsed, not_1_out, MEM_RegWrite, comparator_12_eq);
  or or_3 (DataHazzard, and_2_out, and_3_out, and_4_out, and_5_out);

  // Notes on the sheet:
  //   opcode
  //   IR==sw?
  //   IR==beq/bne?
  //   opcode==0x1c?
  //   func3==0?
  //   IR==jal?
  //   rt
  //   rs
  //   IR==R型指令？
  //   IR==ecall/URET?
  //   if IR=R型指令/sw/beq/bne then RsUsed=1
  //   if IR=ecall/jal/uret then RtUsed=0
endmodule
module \重定向检测逻辑  (
  input  [31:0] ID_IR,
  input  [4:0] EX_WriteReg_num,
  input  EX_RegWrite,
  input  [4:0] MEM_WriteReg_num,
  input  MEM_RegWrite,
  input  EX_MemRead,
  input  [31:0] EX_IR,
  output [1:0] RtForward,
  output [1:0] RsForward,
  output LoadUse
);

  wire and_1_out, and_2_out, and_3_out, and_5_out, comparator_1_eq, comparator_2_eq, comparator_3_eq,
       comparator_4_eq, comparator_5_eq, comparator_6_eq, comparator_7_eq, comparator_8_eq, comparator_9_eq,
       comparator_11_eq, comparator_12_eq, IR__ecall, not_1_out, not_2_out, not_4_out, not_5_out, or_2_out,
       RsUsed, RtUsed;
  wire [4:0] multiplexer_1_out, multiplexer_2_out;

  // Probe on ID_IR[19:15]
  // Probe on ID_IR[24:20]
  Multiplexer #(.select(1), .width(5), .disabled("Z"), .enable("false")) multiplexer_1 (
    .in0(ID_IR[19:15]), .in1(5'b10001), .out(multiplexer_1_out), .sel(IR__ecall));
  Multiplexer #(.select(1), .width(5), .disabled("Z"), .enable("false")) multiplexer_2 (
    .in0(ID_IR[24:20]), .in1(5'b01010), .out(multiplexer_2_out), .sel(IR__ecall));
  Comparator #(.width(5), .mode("twosComplement")) comparator_1 (
    .a({5{1'b0}}), .b(multiplexer_1_out), .eq(comparator_1_eq));  // open: gt, lt
  not not_1 (not_1_out, comparator_1_eq);
  Comparator #(.width(5), .mode("twosComplement")) comparator_2 (
    .a({5{1'b0}}), .b(multiplexer_2_out), .eq(comparator_2_eq));  // open: gt, lt
  not not_2 (not_2_out, comparator_2_eq);
  Comparator #(.width(5), .mode("twosComplement")) comparator_3 (
    .a(multiplexer_2_out), .b(EX_WriteReg_num), .eq(comparator_3_eq));  // open: gt, lt
  Comparator #(.width(5), .mode("twosComplement")) comparator_4 (
    .a(multiplexer_1_out), .b(EX_WriteReg_num), .eq(comparator_4_eq));  // open: gt, lt
  Comparator #(.width(5), .mode("twosComplement")) comparator_5 (
    .a(multiplexer_2_out), .b(MEM_WriteReg_num), .eq(comparator_5_eq));  // open: gt, lt
  Comparator #(.width(5), .mode("twosComplement")) comparator_6 (
    .a(multiplexer_1_out), .b(MEM_WriteReg_num), .eq(comparator_6_eq));  // open: gt, lt
  Comparator #(.width(5), .mode("twosComplement")) comparator_7 (
    .a(ID_IR[6:2]), .b(5'b01100), .eq(comparator_7_eq));  // open: gt, lt
  Comparator #(.width(5), .mode("twosComplement")) comparator_8 (
    .a(ID_IR[6:2]), .b(5'b01000), .eq(comparator_8_eq));  // open: gt, lt
  Comparator #(.width(5), .mode("twosComplement")) comparator_9 (
    .a(ID_IR[6:2]), .b(5'b11000), .eq(comparator_9_eq));  // open: gt, lt
  Comparator #(.width(32), .mode("twosComplement")) comparator_10 (
    .a(ID_IR), .b(32'h73), .eq(IR__ecall));  // open: gt, lt
  Comparator #(.width(5), .mode("twosComplement")) comparator_11 (
    .a(ID_IR[6:2]), .b(5'b11011), .eq(comparator_11_eq));  // open: gt, lt
  or or_1 (RsUsed, comparator_7_eq, comparator_8_eq, comparator_9_eq, IR__ecall);
  not not_3 (RtUsed, comparator_11_eq);
  and and_1 (and_1_out, RsUsed, not_2_out, EX_MemRead, comparator_3_eq);
  and and_2 (and_2_out, RtUsed, not_1_out, EX_MemRead, comparator_4_eq);
  and and_3 (and_3_out, RsUsed, not_2_out, MEM_RegWrite, comparator_5_eq);
  and and_4 (RtForward[1], RsUsed, not_2_out, EX_RegWrite, comparator_3_eq);
  and and_5 (and_5_out, RtUsed, not_1_out, MEM_RegWrite, comparator_6_eq);
  and and_6 (RsForward[1], RtUsed, not_1_out, EX_RegWrite, comparator_4_eq);
  or or_2 (or_2_out, and_1_out, and_2_out);
  and and_7 (RtForward[0], and_3_out, not_4_out);
  not not_4 (not_4_out, RtForward[1]);
  and and_8 (RsForward[0], and_5_out, not_5_out);
  not not_5 (not_5_out, RsForward[1]);
  Comparator #(.width(5), .mode("twosComplement")) comparator_12 (
    .a(EX_IR[6:2]), .b(5'b01101), .eq(comparator_12_eq));  // open: gt, lt
  or or_3 (LoadUse, or_2_out, comparator_12_eq);

  // Notes on the sheet:
  //   opcode
  //   rt
  //   rs
  //   IR==R型指令？
  //   IR==sw?
  //   IR==beq/bne?
  //   opcode==0x1c?
  //   IR==jal?
  //   IR==ecall?
  //   if IR=R型指令/sw/beq/bne then RsUsed=1
  //   if IR=ecall/jal/uret then RtUsed=0
  //   ID段与MEM段数据相关
  //   ID段与EX段数据相关
  //   lui
endmodule

// ALU
module ALU (
  input  [31:0] X,
  input  [31:0] Y,
  input  [3:0] AluOP,
  output out_4,
  output Equal,
  output out_6,
  output [31:0] Result,
  output [31:0] Result_2
);

  wire [0:0] comparator_1_lt, comparator_2_lt;
  wire [31:0] adder_1_out, AND_out, divider_1_out, divider_1_rem, multiplier_1_cout, multiplier_1_out,
       NOR_out, OR_out, shifter_1_out, shifter_2_out, shifter_3_out, subtractor_1_out, XOR_out;

  assign AND_out = X & Y;  // AND_Gate AND, 32 bits wide
  assign OR_out = X | Y;  // OR_Gate OR, 32 bits wide
  Shifter #(.width(32), .shift("ll")) shifter_1 (.in(X), .\dist (Y[4:0]), .out(shifter_1_out));
  Shifter #(.width(32), .shift("ar")) shifter_2 (.in(X), .\dist (Y[4:0]), .out(shifter_2_out));
  Shifter #(.width(32), .shift("lr")) shifter_3 (.in(X), .\dist (Y[4:0]), .out(shifter_3_out));
  Multiplier #(.width(32)) multiplier_1 (.a(X), .b(Y), .out(multiplier_1_out), .cout(multiplier_1_cout));  // open: cin
  Divider #(.width(32)) divider_1 (.a(X), .b(Y), .out(divider_1_out), .rem(divider_1_rem));  // open: upper
  Adder #(.width(32)) adder_1 (.a(X), .b(Y), .out(adder_1_out));  // open: cin, cout
  Subtractor #(.width(32)) subtractor_1 (.a(X), .b(Y), .out(subtractor_1_out));  // open: bin, bout
  assign XOR_out = X ^ Y;  // XOR_Gate XOR, 32 bits wide
  assign NOR_out = ~(X | Y);  // NOR_Gate NOR, 32 bits wide
  Comparator #(.width(32), .mode("twosComplement")) comparator_1 (
    .a(X), .b(Y), .eq(Equal), .lt(comparator_1_lt[0]));  // open: gt
  Comparator #(.width(32), .mode("unsigned")) comparator_2 (.a(X), .b(Y), .lt(comparator_2_lt[0]));  // open: gt, eq
  Multiplexer #(.select(4), .width(32), .disabled("Z"), .enable("false")) multiplexer_1 (
    .in0(shifter_1_out), .in1(shifter_2_out), .in2(shifter_3_out), .in3(multiplier_1_out),
    .in4(divider_1_out), .in5(adder_1_out), .in6(subtractor_1_out), .in7(AND_out), .in8(OR_out),
    .in9(XOR_out), .in10(NOR_out), .in11({{31{1'b0}}, comparator_1_lt[0]}),
    .in12({{31{1'b0}}, comparator_2_lt[0]}), .in13({32{1'b0}}), .in14({32{1'b0}}), .in15({32{1'b0}}),
    .out(Result), .sel(AluOP));
  Multiplexer #(.select(4), .width(32), .disabled("Z"), .enable("false")) multiplexer_2 (
    .in0({32{1'b0}}), .in1({32{1'b0}}), .in2({32{1'b0}}), .in3(multiplier_1_cout), .in4(divider_1_rem),
    .in5({32{1'b0}}), .in6({32{1'b0}}), .in7({32{1'b0}}), .in8({32{1'b0}}), .in9({32{1'b0}}),
    .in10({32{1'b0}}), .in11({32{1'b0}}), .in12({32{1'b0}}), .in13({32{1'b0}}), .in14({32{1'b0}}),
    .in15({32{1'b0}}), .out(Result_2), .sel(AluOP));
  Multiplexer #(.select(4), .width(1), .disabled("Z"), .enable("false")) multiplexer_3 (
    .in0(1'b0), .in1(1'b0), .in2(1'b0), .in3(1'b0), .in4(1'b0), .in5(1'b0), .in6(1'b0), .in7(1'b0),
    .in8(1'b0), .in9(1'b0), .in10(1'b0), .in11(comparator_1_lt[0]), .in12(comparator_2_lt[0]), .in13(1'b0),
    .in14(1'b0), .in15(1'b0), .out(out_6), .sel(AluOP));
  not not_1 (out_4, out_6);

  // Other names for the same wires on the sheet: Result2[31:0] = Result_2; S[3:0] = AluOP; tunnel = out_6;
  //   tunnel_t = out_4

  // Notes on the sheet:
  //   不要改变此引脚区域内容，也不要改变ALU封装形式
  //   输入引脚
  //   输出引脚
endmodule

module Regifile (
  input  [31:0] Din,
  input  Clk,
  input  WE,
  input  [4:0] R1_num,
  input  [4:0] W_num,
  input  [4:0] R2_num,
  output [31:0] R1,
  output [31:0] R2
);

  // RegisterFile registerfile_1: pin names not known; wires that end beside it: Din, Clk, WE, W_num, R1_num, R2_num, R1, R2
endmodule

module BTB (
  input  [31:0] PC,
  input  EX_Branch,
  input  [31:0] EX_PC,
  input  CLK,
  input  [31:0] BranchAddr,
  input  EX_BranchTaken,
  output [31:0] JumpAddr,
  output PredictJump
);

  wire comparator_1_eq, comparator_2_eq, or_1_out, \八路cache_1_miss ;
  wire [1:0] \八路cache_1_pc_state , \八路cache_1_writepc_state , \分支预测状态机_1_次态 ;

  \八路cache  \u_八路cache_1  (
    .CLK(CLK), .PC(PC), .WritePC(EX_PC), .WriteAddr(BranchAddr), .WriteEN(EX_Branch),
    .WriteState(\分支预测状态机_1_次态 ), .Miss(\八路cache_1_miss ), .JumpAddress(JumpAddr),
    .PC_State(\八路cache_1_pc_state ), .WritePC_state(\八路cache_1_writepc_state ));  // open: WriteHit
  \分支预测状态机  \u_分支预测状态机_1  (.Jump(EX_BranchTaken), .in_2(\八路cache_1_writepc_state ), .\次态 (\分支预测状态机_1_次态 ));
  Comparator #(.width(2), .mode("twosComplement")) comparator_1 (
    .a(\八路cache_1_pc_state ), .b(2'b10), .eq(comparator_1_eq));  // open: gt, lt
  Comparator #(.width(2), .mode("twosComplement")) comparator_2 (
    .a(\八路cache_1_pc_state ), .b(2'b11), .eq(comparator_2_eq));  // open: gt, lt
  or or_1 (or_1_out, comparator_1_eq, comparator_2_eq);
  Multiplexer #(.select(1), .width(1), .disabled("Z"), .enable("false")) multiplexer_1 (
    .in0(or_1_out), .in1(1'b0), .out(PredictJump), .sel(\八路cache_1_miss ));

  // Notes on the sheet:
  //   EX段的分支指令实际是否跳转，1为跳转
  //   指令命中不需要更新
  //   指令没有命中
  //   指令命中但需要更新
endmodule

module \分支预测状态机  (
  input  Jump,
  input  [1:0] in_2,
  output [1:0] \次态 
);

  wire and_1_out, and_2_out, and_3_out, and_4_out, not_1_out, not_2_out, not_3_out, not_4_out, not_5_out;

  not not_1 (not_1_out, in_2[0]);
  not not_2 (not_2_out, Jump);
  not not_3 (not_3_out, in_2[0]);
  not not_4 (not_4_out, in_2[1]);
  not not_5 (not_5_out, in_2[0]);
  and and_1 (and_1_out, in_2[1], not_1_out);
  and and_2 (and_2_out, Jump, in_2[0]);
  and and_3 (and_3_out, not_2_out, in_2[1], not_3_out);
  and and_4 (and_4_out, Jump, not_4_out, not_5_out);
  or or_1 (\次态 [1], and_1_out, and_2_out);
  or or_2 (\次态 [0], and_3_out, and_4_out);
endmodule

module \单路cache  (
  input  CLK,
  input  EN,
  input  Valid,
  input  [31:0] \分支指令地址 ,
  input  [31:0] \分支目标地址 ,
  input  [1:0] \分支预测历史位 ,
  input  [31:0] \置换标记位 ,
  output Valid_2,
  output [31:0] \分支指令地址_2 ,
  output [31:0] \分支目标地址_2 ,
  output [1:0] \分支预测历史位_2 ,
  output [31:0] \置换标记位_2 
);

  Register #(.width(1), .trigger("rising"), .Select("low")) u_Valid (
    .D(Valid), .en(EN), .Q(Valid_2), .clk(CLK));  // open: clr
  Register #(.width(32), .trigger("rising"), .Select("low")) \u_分支指令地址  (
    .D(\分支指令地址 ), .en(EN), .Q(\分支指令地址_2 ), .clk(CLK));  // open: clr
  Register #(.width(32), .trigger("rising"), .Select("low")) \u_分支目标地址  (
    .D(\分支目标地址 ), .en(EN), .Q(\分支目标地址_2 ), .clk(CLK));  // open: clr
  Register #(.width(2), .trigger("rising"), .Select("low")) \u_分支预测历史位  (
    .D(\分支预测历史位 ), .en(EN), .Q(\分支预测历史位_2 ), .clk(CLK));  // open: clr
  Register #(.width(32), .trigger("rising"), .Select("low")) \u_置换标记位  (
    .D(\置换标记位 ), .en(EN), .Q(\置换标记位_2 ), .clk(CLK));  // open: clr
endmodule

module \八路cache  (
  input  CLK,
  input  [31:0] PC,
  input  [31:0] WritePC,
  input  [31:0] WriteAddr,
  input  WriteEN,
  input  [1:0] WriteState,
  output Miss,
  output [31:0] JumpAddress,
  output [1:0] PC_State,
  output [1:0] WritePC_state,
  output WriteHit
);

  wire and_1_out, and_10_out, and_11_out, and_12_out, and_13_out, and_14_out, and_15_out, and_16_out,
       and_17_out, and_26_out, and_27_out, and_28_out, and_29_out, and_30_out, and_31_out, and_32_out,
       and_33_out, cache0EN, cache0hit, cache0Valid, cache1EN, cache1hit, cache1Valid, cache2EN, cache2hit,
       cache2Valid, cache3EN, cache3hit, cache3Valid, cache4EN, cache4hit, cache4Valid, cache5EN, cache5hit,
       cache5Valid, cache6EN, cache6hit, cache6Valid, cache7EN, cache7hit, cache7Valid, comparator_1_eq,
       comparator_2_eq, comparator_3_eq, comparator_4_eq, comparator_5_eq, comparator_6_eq, comparator_7_eq,
       comparator_8_eq, comparator_9_eq, comparator_10_eq, comparator_11_eq, comparator_12_eq,
       comparator_13_eq, comparator_14_eq, comparator_15_eq, comparator_16_eq, counter_1_carry,
       decoder_1_out0, decoder_1_out1, decoder_1_out2, decoder_1_out3, decoder_1_out4, decoder_1_out5,
       decoder_1_out6, decoder_1_out7, or_2_out, or_3_out, or_4_out, or_5_out, or_6_out, or_7_out, or_8_out,
       or_9_out, or_10_out;
  wire [1:0] \cache0_分支预测历史位_2 , \cache1_分支预测历史位_2 , \cache2_分支预测历史位_2 , \cache3_分支预测历史位_2 ,
       \cache4_分支预测历史位_2 , \cache5_分支预测历史位_2 , \cache6_分支预测历史位_2 , \cache7_分支预测历史位_2 ,
       controlled_buffer_1_out, controlled_buffer_9_out;
  wire [2:0] counter_1_q;
  wire [31:0] \cache0_分支指令地址_2 , \cache0_分支目标地址_2 , \cache1_分支指令地址_2 , \cache1_分支目标地址_2 , \cache2_分支指令地址_2 ,
       \cache2_分支目标地址_2 , \cache3_分支指令地址_2 , \cache3_分支目标地址_2 , \cache4_分支指令地址_2 , \cache4_分支目标地址_2 ,
       \cache5_分支指令地址_2 , \cache5_分支目标地址_2 , \cache6_分支指令地址_2 , \cache6_分支目标地址_2 , \cache7_分支指令地址_2 ,
       \cache7_分支目标地址_2 ;

  and and_1 (and_1_out, ~WriteHit, WriteEN);  // AND_Gate
  Comparator #(.width(32), .mode("twosComplement")) comparator_1 (
    .a(WritePC), .b(\cache0_分支指令地址_2 ), .eq(comparator_1_eq));  // open: gt, lt
  Comparator #(.width(32), .mode("twosComplement")) comparator_2 (
    .a(WritePC), .b(\cache1_分支指令地址_2 ), .eq(comparator_2_eq));  // open: gt, lt
  Comparator #(.width(32), .mode("twosComplement")) comparator_3 (
    .a(WritePC), .b(\cache2_分支指令地址_2 ), .eq(comparator_3_eq));  // open: gt, lt
  Comparator #(.width(32), .mode("twosComplement")) comparator_4 (
    .a(WritePC), .b(\cache3_分支指令地址_2 ), .eq(comparator_4_eq));  // open: gt, lt
  Comparator #(.width(32), .mode("twosComplement")) comparator_5 (
    .a(WritePC), .b(\cache4_分支指令地址_2 ), .eq(comparator_5_eq));  // open: gt, lt
  Comparator #(.width(32), .mode("twosComplement")) comparator_6 (
    .a(WritePC), .b(\cache5_分支指令地址_2 ), .eq(comparator_6_eq));  // open: gt, lt
  Comparator #(.width(32), .mode("twosComplement")) comparator_7 (
    .a(WritePC), .b(\cache6_分支指令地址_2 ), .eq(comparator_7_eq));  // open: gt, lt
  Comparator #(.width(32), .mode("twosComplement")) comparator_8 (
    .a(WritePC), .b(\cache7_分支指令地址_2 ), .eq(comparator_8_eq));  // open: gt, lt
  Counter #(.width(3), .max('h7), .ongoal("wrap"), .trigger("rising"), .behavior("new")) counter_1 (
    .load(counter_1_carry), .D(3'b000), .count(and_1_out), .Q(counter_1_q), .carry(counter_1_carry), .clk(CLK));  // open: clr, preset, down
  and and_2 (cache0hit, cache0Valid, comparator_1_eq);
  and and_3 (cache1hit, cache1Valid, comparator_2_eq);
  and and_4 (cache2hit, cache2Valid, comparator_3_eq);
  and and_5 (cache3hit, cache3Valid, comparator_4_eq);
  and and_6 (cache4hit, cache4Valid, comparator_5_eq);
  and and_7 (cache5hit, cache5Valid, comparator_6_eq);
  and and_8 (cache6hit, cache6Valid, comparator_7_eq);
  and and_9 (cache7hit, cache6Valid, comparator_8_eq);
  Decoder #(.select(3), .tristate("false"), .disabled("Z"), .enable("false")) decoder_1 (
    .out0(decoder_1_out0), .out1(decoder_1_out1), .out2(decoder_1_out2), .out3(decoder_1_out3),
    .out4(decoder_1_out4), .out5(decoder_1_out5), .out6(decoder_1_out6), .out7(decoder_1_out7),
    .sel(counter_1_q));
  \单路cache  cache0 (
    .CLK(CLK), .EN(cache0EN), .Valid(1'b1), .\分支指令地址 (WritePC), .\分支目标地址 (WriteAddr), .\分支预测历史位 (WriteState),
    .Valid_2(cache0Valid), .\分支指令地址_2 (\cache0_分支指令地址_2 ), .\分支目标地址_2 (\cache0_分支目标地址_2 ),
    .\分支预测历史位_2 (\cache0_分支预测历史位_2 ));  // open: 置换标记位, 置换标记位_2
  \单路cache  cache1 (
    .CLK(CLK), .EN(cache1EN), .Valid(1'b1), .\分支指令地址 (WritePC), .\分支目标地址 (WriteAddr), .\分支预测历史位 (WriteState),
    .Valid_2(cache1Valid), .\分支指令地址_2 (\cache1_分支指令地址_2 ), .\分支目标地址_2 (\cache1_分支目标地址_2 ),
    .\分支预测历史位_2 (\cache1_分支预测历史位_2 ));  // open: 置换标记位, 置换标记位_2
  \单路cache  cache2 (
    .CLK(CLK), .EN(cache2EN), .Valid(1'b1), .\分支指令地址 (WritePC), .\分支目标地址 (WriteAddr), .\分支预测历史位 (WriteState),
    .Valid_2(cache2Valid), .\分支指令地址_2 (\cache2_分支指令地址_2 ), .\分支目标地址_2 (\cache2_分支目标地址_2 ),
    .\分支预测历史位_2 (\cache2_分支预测历史位_2 ));  // open: 置换标记位, 置换标记位_2
  \单路cache  cache3 (
    .CLK(CLK), .EN(cache3EN), .Valid(1'b1), .\分支指令地址 (WritePC), .\分支目标地址 (WriteAddr), .\分支预测历史位 (WriteState),
    .Valid_2(cache3Valid), .\分支指令地址_2 (\cache3_分支指令地址_2 ), .\分支目标地址_2 (\cache3_分支目标地址_2 ),
    .\分支预测历史位_2 (\cache3_分支预测历史位_2 ));  // open: 置换标记位, 置换标记位_2
  \单路cache  cache4 (
    .CLK(CLK), .EN(cache4EN), .Valid(1'b1), .\分支指令地址 (WritePC), .\分支目标地址 (WriteAddr), .\分支预测历史位 (WriteState),
    .Valid_2(cache4Valid), .\分支指令地址_2 (\cache4_分支指令地址_2 ), .\分支目标地址_2 (\cache4_分支目标地址_2 ),
    .\分支预测历史位_2 (\cache4_分支预测历史位_2 ));  // open: 置换标记位, 置换标记位_2
  \单路cache  cache5 (
    .CLK(CLK), .EN(cache5EN), .Valid(1'b1), .\分支指令地址 (WritePC), .\分支目标地址 (WriteAddr), .\分支预测历史位 (WriteState),
    .Valid_2(cache5Valid), .\分支指令地址_2 (\cache5_分支指令地址_2 ), .\分支目标地址_2 (\cache5_分支目标地址_2 ),
    .\分支预测历史位_2 (\cache5_分支预测历史位_2 ));  // open: 置换标记位, 置换标记位_2
  \单路cache  cache6 (
    .CLK(CLK), .EN(cache6EN), .Valid(1'b1), .\分支指令地址 (WritePC), .\分支目标地址 (WriteAddr), .\分支预测历史位 (WriteState),
    .Valid_2(cache6Valid), .\分支指令地址_2 (\cache6_分支指令地址_2 ), .\分支目标地址_2 (\cache6_分支目标地址_2 ),
    .\分支预测历史位_2 (\cache6_分支预测历史位_2 ));  // open: 置换标记位, 置换标记位_2
  \单路cache  cache7 (
    .CLK(CLK), .EN(cache7EN), .Valid(1'b1), .\分支指令地址 (WritePC), .\分支目标地址 (WriteAddr), .\分支预测历史位 (WriteState),
    .Valid_2(cache7Valid), .\分支指令地址_2 (\cache7_分支指令地址_2 ), .\分支目标地址_2 (\cache7_分支目标地址_2 ),
    .\分支预测历史位_2 (\cache7_分支预测历史位_2 ));  // open: 置换标记位, 置换标记位_2
  and and_10 (and_10_out, WriteEN, ~WriteHit, decoder_1_out0);  // AND_Gate
  and and_11 (and_11_out, WriteEN, ~WriteHit, decoder_1_out1);  // AND_Gate
  and and_12 (and_12_out, WriteEN, ~WriteHit, decoder_1_out2);  // AND_Gate
  and and_13 (and_13_out, WriteEN, ~WriteHit, decoder_1_out3);  // AND_Gate
  and and_14 (and_14_out, WriteEN, ~WriteHit, decoder_1_out4);  // AND_Gate
  and and_15 (and_15_out, WriteEN, ~WriteHit, decoder_1_out5);  // AND_Gate
  and and_16 (and_16_out, WriteEN, ~WriteHit, decoder_1_out6);  // AND_Gate
  and and_17 (and_17_out, WriteEN, ~WriteHit, decoder_1_out7);  // AND_Gate
  assign controlled_buffer_1_out = cache0hit ? \cache0_分支预测历史位_2  : 2'bz;  // Controlled_Buffer controlled_buffer_1
  assign controlled_buffer_1_out = cache1hit ? \cache1_分支预测历史位_2  : 2'bz;  // Controlled_Buffer controlled_buffer_2
  assign controlled_buffer_1_out = cache2hit ? \cache2_分支预测历史位_2  : 2'bz;  // Controlled_Buffer controlled_buffer_3
  assign controlled_buffer_1_out = cache3hit ? \cache3_分支预测历史位_2  : 2'bz;  // Controlled_Buffer controlled_buffer_4
  assign controlled_buffer_1_out = cache4hit ? \cache4_分支预测历史位_2  : 2'bz;  // Controlled_Buffer controlled_buffer_5
  assign controlled_buffer_1_out = cache5hit ? \cache5_分支预测历史位_2  : 2'bz;  // Controlled_Buffer controlled_buffer_6
  assign controlled_buffer_1_out = cache6hit ? \cache6_分支预测历史位_2  : 2'bz;  // Controlled_Buffer controlled_buffer_7
  assign controlled_buffer_1_out = cache7hit ? \cache7_分支预测历史位_2  : 2'bz;  // Controlled_Buffer controlled_buffer_8
  or or_1 (WriteHit, cache0hit, cache1hit, cache2hit, cache3hit, cache4hit, cache5hit, cache6hit, cache7hit);
  or or_2 (or_2_out, cache0hit, and_10_out);
  and and_18 (cache0EN, or_2_out, WriteEN);
  or or_3 (or_3_out, cache1hit, and_11_out);
  and and_19 (cache1EN, or_3_out, WriteEN);
  or or_4 (or_4_out, cache2hit, and_12_out);
  and and_20 (cache2EN, or_4_out, WriteEN);
  or or_5 (or_5_out, cache3hit, and_13_out);
  and and_21 (cache3EN, or_5_out, WriteEN);
  or or_6 (or_6_out, cache4hit, and_14_out);
  and and_22 (cache4EN, or_6_out, WriteEN);
  or or_7 (or_7_out, cache5hit, and_15_out);
  and and_23 (cache5EN, or_7_out, WriteEN);
  or or_8 (or_8_out, cache6hit, and_16_out);
  and and_24 (cache6EN, or_8_out, WriteEN);
  or or_9 (or_9_out, cache7hit, and_17_out);
  and and_25 (cache7EN, or_9_out, WriteEN);
  Comparator #(.width(32), .mode("twosComplement")) comparator_9 (
    .a(PC), .b(\cache0_分支指令地址_2 ), .eq(comparator_9_eq));  // open: gt, lt
  Comparator #(.width(32), .mode("twosComplement")) comparator_10 (
    .a(PC), .b(\cache1_分支指令地址_2 ), .eq(comparator_10_eq));  // open: gt, lt
  Comparator #(.width(32), .mode("twosComplement")) comparator_11 (
    .a(PC), .b(\cache2_分支指令地址_2 ), .eq(comparator_11_eq));  // open: gt, lt
  Comparator #(.width(32), .mode("twosComplement")) comparator_12 (
    .a(PC), .b(\cache3_分支指令地址_2 ), .eq(comparator_12_eq));  // open: gt, lt
  Comparator #(.width(32), .mode("twosComplement")) comparator_13 (
    .a(PC), .b(\cache4_分支指令地址_2 ), .eq(comparator_13_eq));  // open: gt, lt
  Comparator #(.width(32), .mode("twosComplement")) comparator_14 (
    .a(PC), .b(\cache5_分支指令地址_2 ), .eq(comparator_14_eq));  // open: gt, lt
  Comparator #(.width(32), .mode("twosComplement")) comparator_15 (
    .a(PC), .b(\cache6_分支指令地址_2 ), .eq(comparator_15_eq));  // open: gt, lt
  Comparator #(.width(32), .mode("twosComplement")) comparator_16 (
    .a(PC), .b(\cache7_分支指令地址_2 ), .eq(comparator_16_eq));  // open: gt, lt
  and and_26 (and_26_out, cache0Valid, comparator_9_eq);
  assign controlled_buffer_9_out = and_26_out ? \cache0_分支预测历史位_2  : 2'bz;  // Controlled_Buffer controlled_buffer_9
  and and_27 (and_27_out, cache1Valid, comparator_10_eq);
  assign controlled_buffer_9_out = and_27_out ? \cache1_分支预测历史位_2  : 2'bz;  // Controlled_Buffer controlled_buffer_10
  and and_28 (and_28_out, cache2Valid, comparator_11_eq);
  assign controlled_buffer_9_out = and_28_out ? \cache2_分支预测历史位_2  : 2'bz;  // Controlled_Buffer controlled_buffer_11
  and and_29 (and_29_out, cache3Valid, comparator_12_eq);
  assign controlled_buffer_9_out = and_29_out ? \cache3_分支预测历史位_2  : 2'bz;  // Controlled_Buffer controlled_buffer_12
  and and_30 (and_30_out, cache4Valid, comparator_13_eq);
  assign controlled_buffer_9_out = and_30_out ? \cache4_分支预测历史位_2  : 2'bz;  // Controlled_Buffer controlled_buffer_13
  and and_31 (and_31_out, cache5Valid, comparator_14_eq);
  assign controlled_buffer_9_out = and_31_out ? \cache5_分支预测历史位_2  : 2'bz;  // Controlled_Buffer controlled_buffer_14
  and and_32 (and_32_out, cache6Valid, comparator_15_eq);
  assign controlled_buffer_9_out = and_32_out ? \cache6_分支预测历史位_2  : 2'bz;  // Controlled_Buffer controlled_buffer_15
  and and_33 (and_33_out, cache7Valid, comparator_16_eq);
  assign controlled_buffer_9_out = and_33_out ? \cache7_分支预测历史位_2  : 2'bz;  // Controlled_Buffer controlled_buffer_16
  assign JumpAddress = and_26_out ? \cache0_分支目标地址_2  : 32'bz;  // Controlled_Buffer controlled_buffer_17
  assign JumpAddress = and_27_out ? \cache1_分支目标地址_2  : 32'bz;  // Controlled_Buffer controlled_buffer_18
  assign JumpAddress = and_28_out ? \cache2_分支目标地址_2  : 32'bz;  // Controlled_Buffer controlled_buffer_19
  assign JumpAddress = and_29_out ? \cache3_分支目标地址_2  : 32'bz;  // Controlled_Buffer controlled_buffer_20
  assign JumpAddress = and_30_out ? \cache4_分支目标地址_2  : 32'bz;  // Controlled_Buffer controlled_buffer_21
  assign JumpAddress = and_31_out ? \cache5_分支目标地址_2  : 32'bz;  // Controlled_Buffer controlled_buffer_22
  assign JumpAddress = and_32_out ? \cache6_分支目标地址_2  : 32'bz;  // Controlled_Buffer controlled_buffer_23
  assign JumpAddress = and_33_out ? \cache7_分支目标地址_2  : 32'bz;  // Controlled_Buffer controlled_buffer_24
  or or_10 (or_10_out, and_26_out, and_27_out, and_28_out, and_29_out, and_30_out, and_31_out, and_32_out, and_33_out);
  not not_1 (Miss, or_10_out);
  Multiplexer #(.select(1), .width(2), .disabled("Z"), .enable("false")) multiplexer_1 (
    .in0(controlled_buffer_9_out), .in1(2'b01), .out(PC_State), .sel(Miss));
  Multiplexer #(.select(1), .width(2), .disabled("Z"), .enable("false")) multiplexer_2 (
    .in0(2'b01), .in1(controlled_buffer_1_out), .out(WritePC_state), .sel(WriteHit));

  // Other names for the same wires on the sheet: cachehit = WriteHit

  // Notes on the sheet:
  //   写入时 如果命中 cachexEN=1
  //   如果未命中 根据decd电路找到要写入的路
  //   写入：
  //   如果要写入的分支指令已在BTB中，直接修改
  //   读取：将PC和各个cache的分支指令地址并发比较并输出命中的那一路的分支目标地址，都未命中则Miss为1
  //   如果要写入的分支指令没有在BTB中，选择需要写入的一路，并将要写入的分支指令地址和分支目标地址写入BTB
endmodule

module \封装正确性测试  (
);

  wire IR1, IR2, IR3, MemW, RegW;
  wire [31:0] EX_PC, ID_PC, IF_PC, IR, LED, MDin, MDinr, MEM_PC, PC, RDin, RDinr, WB_PC;

  \单周期RISC_V  \u_单周期risc_v_1  (
    .IR1(IR1), .IR2(IR2), .IR3(IR3), .RegWrite(RegW), .MemWrite(MemW), .PC(PC), .IR(IR), .RDin(RDin),
    .MDin(MDin), .LedData(LED));
  \气泡流水线  \u_气泡流水线_1  (
    .RegWrite(RegW), .MemWrite(MemW), .IF_PC(IF_PC), .ID_PC(ID_PC), .EX_PC(EX_PC), .M_PC(MEM_PC),
    .WB_PC(WB_PC), .RDin(RDinr), .MDin(MDinr), .LedData(LED));
  \单周期_单级中断  \u_单周期_单级中断_1  (
    .IR1(IR1), .IR2(IR2), .IR3(IR3), .RegWrite(RegW), .MemWrite(MemW), .PC(PC), .IR(IR), .RDin(RDin),
    .MDin(MDin), .LedData(LED));
  \理想流水线  \u_理想流水线_1  (
    .RegWrite(RegW), .MemWrite(MemW), .IF_PC(IF_PC), .ID_PC(ID_PC), .EX_PC(EX_PC), .M_PC(MEM_PC),
    .WB_PC(WB_PC), .RDin(RDinr), .MDin(MDinr), .LedData(LED));
  \重定向流水线  \u_重定向流水线_1  (
    .RegWrite(RegW), .MemWrite(MemW), .IF_PC(IF_PC), .ID_PC(ID_PC), .EX_PC(EX_PC), .M_PC(MEM_PC),
    .WB_PC(WB_PC), .RDin(RDinr), .MDin(MDinr), .LedData(LED));
  \单周期_多级中断  \u_单周期_多级中断_1  (
    .IR1(IR1), .IR2(IR2), .IR3(IR3), .RegWrite(RegW), .MemWrite(MemW), .PC(PC), .IR(IR), .RDin(RDin),
    .MDin(MDin), .LedData(LED));

  // Notes on the sheet:
  //   单周期封装测试
  //   气泡流水封装测试
  //   单周期+单级中断封装测试
  //   请检查上面封装有无位宽不匹配，引脚标签是否和连接的标签相对应，否则无法在educoder平台上正确测试
  //   理想流水封装测试
  //   重定向流水封装测试
  //   单周期+多级中断封装测试
endmodule
