// Logisim project lmq.circ as structural Verilog
module \单周期RISC_V  (
  output RegWrite,
  output MemWrite,
  output [31:0] PC,
  output [31:0] IR,
  output [31:0] RDin,
  output [31:0] MDin,
  output [31:0] LedData
);

  wire alu_1_equal, alu_1_out_4, and_1_out, and_3_out, and_4_out, and_5_out, and_6_out, Beq, Bgeu, Bne, CLK,
       clock_1_out, comparator_1_eq, comparator_1_lt, comparator_2_eq, d_ff_1_q, ecall, Go, halt, JAL, JALR,
       lb, nand_1_out, not_1_out, not_2_out, not_3_out, not_4_out, or_1_out, or_2_out, RST, S_type,
       \单周期硬布线控制器_1_alu_src , \单周期硬布线控制器_1_memtoreg ;
  wire [0:0] multiplexer_7_out;
  wire [3:0] \单周期硬布线控制器_1_alu_op ;
  wire [4:0] multiplexer_3_out, multiplexer_4_out;
  wire [12:0] CNT_num;
  wire [15:0] \总周期数 ;
  wire [30:0] multiplexer_7_out_2;
  wire [31:0] adder_1_out, adder_2_out, alu_1_result, ImmGen_imm, \l指令分线器_1_imm32_2 , multiplexer_1_out,
       multiplexer_2_out, multiplexer_6_out, R1, ram_1_data, shifter_1_out;

  Button \u_继续运行  (.out(Go));
  Multiplexer #(.select(1), .width(32), .disabled("Z"), .enable("false")) multiplexer_1 (
    .in0(adder_2_out), .in1({multiplexer_7_out_2, 1'b0}), .out(multiplexer_1_out), .sel(JALR));
  Hex_Digit_Display hex_digit_display_1 (.value(LedData[31:28]));  // open: dp
  Multiplexer #(.select(1), .width(32), .disabled("Z"), .enable("false")) multiplexer_2 (
    .in0(adder_1_out), .in1(multiplexer_1_out), .out(multiplexer_2_out), .sel(or_2_out));
  not not_1 (not_1_out, halt);
  Hex_Digit_Display hex_digit_display_2 (.value(LedData[23:20]));  // open: dp
  Hex_Digit_Display hex_digit_display_3 (.value(LedData[27:24]));  // open: dp
  // Probe on PC
  Register #(.width(32), .trigger("rising"), .Select("low")) u_PC (
    .D(multiplexer_2_out), .en(not_1_out), .Q(PC), .clk(CLK), .clr(RST));
  Hex_Digit_Display hex_digit_display_4 (.value(LedData[19:16]));  // open: dp
  Hex_Digit_Display hex_digit_display_5 (.value(LedData[15:12]));  // open: dp
  Adder #(.width(32)) adder_1 (.a(PC), .b(32'h4), .out(adder_1_out));  // open: cin, cout
  Hex_Digit_Display hex_digit_display_6 (.value(LedData[7:4]));  // open: dp
  Hex_Digit_Display hex_digit_display_7 (.value(LedData[11:8]));  // open: dp
  // Probe on \总周期数 
  // RiscV_Probe riscv_probe_1: pin names not known; wires that end beside it: 32'h4, IR
  ROM #(.addrWidth(10), .dataWidth(32), .Select("high")) rom_1 (.addr(PC[11:2]), .data(IR));
  Hex_Digit_Display hex_digit_display_8 (.value(LedData[3:0]));  // open: dp
  D_Flip_Flop #(.trigger("high"), .Pre_Clr_Positions("LEGACY"), .NegatePresetClear("false"), .enable("true"), .NewFFLayout("false")) d_ff_1 (.Q(d_ff_1_q));  // open: clk, D, Qn, preset, en, reset
  // Probe on 13'h50
  Comparator #(.width(13), .mode("twosComplement")) comparator_1 (
    .a(CNT_num), .b(13'h50), .eq(comparator_1_eq), .lt(comparator_1_lt));  // open: gt
  Clock #(.highDuration(1), .lowDuration(1)) clock_1 (.out(clock_1_out));
  \单周期硬布线控制器  \u_单周期硬布线控制器_1  (
    .Funct({IR[30], IR[25], IR[14:12]}), .OP(IR[6:2]), .ALU_OP(\单周期硬布线控制器_1_alu_op ),
    .MemToReg(\单周期硬布线控制器_1_memtoreg ), .MemWrite(MemWrite), .ALU_SRC(\单周期硬布线控制器_1_alu_src ),
    .RegWrite(RegWrite), .ecall(ecall), .S_type(S_type), .Jalr(JALR), .Beq(Beq), .JAL(JAL), .Bne(Bne),
    .in_3(IR[21]), .BGUE(Bgeu), .lb(lb));  // open: uret, csrrsi, csrrci
  nand nand_1 (nand_1_out, d_ff_1_q, comparator_1_eq);
  Counter #(.width(13), .max('h1fff), .ongoal("stay"), .trigger("rising"), .behavior("old")) counter_1 (
    .count(comparator_1_lt), .Q(CNT_num), .clk(clock_1_out));  // open: load, D, carry, clr, preset
  Multiplexer #(.select(1), .width(5), .disabled("Z"), .enable("false")) multiplexer_3 (
    .in0(IR[19:15]), .in1(5'b10001), .out(multiplexer_3_out), .sel(ecall));
  Multiplexer #(.select(1), .width(5), .disabled("Z"), .enable("false")) multiplexer_4 (
    .in0(IR[24:20]), .in1(5'b01010), .out(multiplexer_4_out), .sel(ecall));
  \ImmGen_封装版  ImmGen (.IR(IR), .Imm(ImmGen_imm));
  Multiplexer #(.select(1), .width(32), .disabled("Z"), .enable("false")) multiplexer_5 (
    .in0({multiplexer_7_out_2, multiplexer_7_out[0]}), .in1(adder_1_out), .out(RDin), .sel(or_1_out));
  and and_1 (and_1_out, nand_1_out, ~halt);  // AND_Gate
  Counter #(.width(16), .max('hffff), .ongoal("wrap"), .trigger("rising"), .behavior("new")) counter_2 (
    .count(and_1_out), .Q(\总周期数 ), .clk(clock_1_out));  // open: load, D, carry, clr, preset, down
  or or_1 (or_1_out, JAL, JALR);
  assign CLK = nand_1_out ? clock_1_out : 1'bz;  // Controlled_Buffer controlled_buffer_1
  Pull_Resistor #(.pull(1)) pull_resistor_1 (.node(CLK));
  Regifile regifile_1 (
    .Din(RDin), .Clk(CLK), .R1(R1), .R2(MDin), .WE(RegWrite), .W_num(IR[11:7]), .R1_num(multiplexer_3_out),
    .R2_num(multiplexer_4_out));
  Multiplexer #(.select(1), .width(32), .disabled("Z"), .enable("false")) multiplexer_6 (
    .in0(MDin), .in1(ImmGen_imm), .out(multiplexer_6_out), .sel(\单周期硬布线控制器_1_alu_src ));
  Shifter #(.width(32), .shift("ll")) shifter_1 (.in(ImmGen_imm), .\dist (5'b00001), .out(shifter_1_out));
  ALU alu_1 (
    .X(R1), .Y(multiplexer_6_out), .AluOP(\单周期硬布线控制器_1_alu_op ), .Equal(alu_1_equal), .Result(alu_1_result),
    .out_4(alu_1_out_4));  // open: Result_2, out_6
  Adder #(.width(32)) adder_2 (.a(shifter_1_out), .b(PC), .out(adder_2_out));  // open: cin, cout
  Comparator #(.width(32), .mode("twosComplement")) comparator_2 (
    .a(R1), .b(32'h22), .eq(comparator_2_eq));  // open: gt, lt
  not not_2 (not_2_out, comparator_2_eq);
  and and_2 (halt, not_2_out, ecall, not_3_out);
  not not_3 (not_3_out, Go);
  and and_3 (and_3_out, Beq, alu_1_equal);
  and and_4 (and_4_out, Bne, not_4_out);
  not not_4 (not_4_out, alu_1_equal);
  and and_5 (and_5_out, Bgeu, alu_1_out_4);
  and and_6 (and_6_out, ecall, comparator_2_eq);
  Register #(.width(32), .trigger("rising"), .Select("low")) register_1 (
    .D(MDin), .en(and_6_out), .Q(LedData), .clk(CLK));  // open: clr
  or or_2 (or_2_out, and_3_out, and_4_out, JAL, JALR, and_5_out);
  \L指令分线器  \l指令分线器_1  (.lb(lb), .Imm32_2(\l指令分线器_1_imm32_2 ), .Imm32(ram_1_data), .offset(alu_1_result[1:0]));
  RAM #(.addrWidth(10), .dataWidth(32), .bus("separate"), .Select("low")) ram_1 (
    .addr(alu_1_result[11:2]), .din(MDin), .data(ram_1_data), .str(MemWrite), .clk(CLK));  // open: sel, ld, clr
  Multiplexer #(.select(1), .width(32), .disabled("Z"), .enable("false")) multiplexer_7 (
    .in0(alu_1_result), .in1(\l指令分线器_1_imm32_2 ), .out({multiplexer_7_out_2, multiplexer_7_out[0]}),
    .sel(\单周期硬布线控制器_1_memtoreg ));

  // Other names for the same wires on the sheet: R2[31:0] = MDin

  // Notes on the sheet:
  //   数码管输出
  //   指令探针
  //   指令存储器
  //   contents of rom_1 (hex, n*v repeats v):
  //   100493 100006f 100493 200913 300993 100006f 100493 200913 300993 100006f 100493 200913 300993
  //   100006f 100493 200913 300993 3e0000ef 100413 100493 1f49493 900533 2200893 73 24d493 48463 fedff06f
  //   900533 2200893 73 100493 249493 900533 2200893 73 48463 fedff06f 100493 1f49493 900533 2200893 73
  //   4034d493 900533 2200893 73 4044d493 900533 2200893 73 4044d493 900533 2200893 73 4044d493 900533
  //   2200893 73 4044d493 900533 2200893 73 4044d493 900533 2200893 73 4044d493 900533 2200893 73 4044d493
  //   900533 2200893 73 100413 1f41993 41f9d993 433 c00913 300b13 140413 f47413 800293 100313 499993
  //   89e9b3 1300533 2200893 73 406282b3 fe0294e3 140413 f00f93 1f47433 1c41413 800293 100313 49d993
  //   89e9b3 1300533 2200893 73 406282b3 fe0294e3 1c45413 406b0b33 b0463 f95ff06f 2b3 fff2c293 829293
  //   ff2e293 500533 2200893 73 fff00413 493 84a023 140413 448493 84a023 140413 448493 84a023 140413
  //   448493 84a023 140413 448493 84a023 140413 448493 84a023 140413 448493 84a023 140413 448493 84a023
  //   140413 448493 84a023 140413 448493 84a023 140413 448493 84a023 140413 448493 84a023 140413 448493
  //   84a023 140413 448493 84a023 140413 448493 84a023 140413 448493 84a023 140413 448493 140413 433
  //   3c00493 42983 4aa03 149a2b3 28663 134a023 1442023 ffc48493 fe9412e3 800533 2200893 73 440413 3c00493
  //   fc9416e3 3200893 73 100293 300313 800493 849493 7648493 900533 2200893 73 800e13 5494b3 6494b3
  //   900533 2200893 73 fffe0e13 fe0e14e3 a00893 73 100293 300313 800493 849493 7648493 1449493 900533
  //   2200893 73 800e13 54d4b3 64d4b3 900533 2200893 73 fffe0e13 fe0e14e3 a00893 73 313 1000e13 8400493
  //   849493 8348493 400913 891913 490913 849493 8248493 849493 8148493 891913 490913 891913 490913 932023
  //   12484b3 430313 fffe0e13 fe0e18e3 2000e13 313 30483 900533 2200893 73 130313 fffe0e13 fe0e14e3 a00893
  //   73 f00493 100913 409909b3 900533 2200893 73 fff48493 ff29f6e3 a00893 73 a00893 73 413 140413 800533
  //   2200893 73 240413 800533 2200893 73 340413 800533 2200893 73 440413 800533 2200893 73 540413 800533
  //   2200893 73 640413 800533 2200893 73 740413 800533 2200893 73 840413 800533 2200893 2200893 73 8067
  //   PC
  //   PC+4
  //   控制位
  //   暂停节拍，不能为0
  //   指令字
  //   JAL
  //   JALR
  //   MemToReg
  //   MemWrite
  //   AluOP
  //   AluSrcB
  //   RegWrite
  //   可计数暂停的时钟源
  //   数据存储器
endmodule

// 单周期硬布线控制器
module \单周期硬布线控制器  (
  input  [4:0] OP,
  input  [4:0] Funct,
  input  in_3,
  output [3:0] ALU_OP,
  output uret,
  output MemToReg,
  output ecall,
  output MemWrite,
  output ALU_SRC,
  output RegWrite,
  output S_type,
  output Beq,
  output Bne,
  output Jalr,
  output JAL,
  output BGUE,
  output lb,
  output csrrsi,
  output csrrci
);

  wire \控制信号自动生成_ccab_1_ecall ;

  \运算控制器自动生成_CCAB  \u_运算控制器自动生成_ccab_1  (
    .OP2(OP[0]), .OP3(OP[1]), .OP4(OP[2]), .OP5(OP[3]), .OP6(OP[4]), .F12(Funct[0]), .F13(Funct[1]),
    .F14(Funct[2]), .F25(Funct[3]), .F30(Funct[4]), .S0(ALU_OP[0]), .S1(ALU_OP[1]), .S2(ALU_OP[2]),
    .S3(ALU_OP[3]));
  \控制信号自动生成_CCAB  \u_控制信号自动生成_ccab_1  (
    .OP2(OP[0]), .OP3(OP[1]), .OP4(OP[2]), .OP5(OP[3]), .OP6(OP[4]), .F12(Funct[0]), .F13(Funct[1]),
    .F14(Funct[2]), .F25(Funct[3]), .F30(Funct[4]), .MemToReg(MemToReg), .MemWrite(MemWrite),
    .ALU_SRC(ALU_SRC), .RegWrite(RegWrite), .ecall(\控制信号自动生成_ccab_1_ecall ), .S_Type(S_type), .BEQ(Beq),
    .BNE(Bne), .JALR(Jalr), .JAL(JAL), .BGEU(BGUE), .lb(lb), .csrrsi(csrrsi), .csrrci(csrrci));
  and and_1 (uret, in_3, \控制信号自动生成_ccab_1_ecall );
  and and_2 (ecall, ~in_3, \控制信号自动生成_ccab_1_ecall );  // AND_Gate

  // Other names for the same wires on the sheet: IR21 = in_3; OP_CODE[4:0] = OP
endmodule

// 运算器控制器
module \运算控制器自动生成  (
  input  OP2,
  input  OP3,
  input  OP4,
  input  OP5,
  input  OP6,
  input  F12,
  input  F13,
  input  F14,
  input  F25,
  input  F30,
  output S0,
  output S1,
  output S2,
  output S3
);

  wire and_1_out, and_2_out, and_3_out, and_4_out, and_5_out, and_6_out, and_7_out, and_8_out, and_9_out,
       and_10_out, and_11_out, and_12_out, and_13_out, and_14_out, and_15_out, and_16_out, and_17_out,
       and_18_out, and_19_out, and_20_out, and_21_out, and_22_out, and_23_out, and_24_out, and_25_out,
       and_26_out, and_27_out, and_28_out, and_29_out, and_30_out, and_31_out, and_32_out, and_33_out,
       and_34_out, not_1_out, not_2_out, not_3_out, not_4_out, not_5_out, not_6_out, not_7_out, not_8_out,
       not_9_out, not_10_out, not_11_out, not_12_out, not_13_out, not_14_out, not_15_out, not_16_out,
       not_17_out, not_18_out, not_19_out, not_20_out, not_21_out, not_22_out, not_23_out, not_24_out,
       not_25_out, not_26_out, not_27_out, not_28_out, not_29_out, not_30_out, not_31_out, not_32_out,
       not_33_out, not_34_out, not_35_out, not_36_out, not_37_out, not_38_out, not_39_out, not_40_out,
       not_41_out, not_42_out, not_43_out, not_44_out, not_45_out, not_46_out, not_47_out, not_48_out,
       not_49_out, not_50_out, not_51_out, not_52_out, not_53_out, not_54_out, not_55_out, not_56_out,
       not_57_out, not_58_out, not_59_out, not_60_out, not_61_out, not_62_out, not_63_out, not_64_out,
       not_65_out, not_66_out, not_67_out, not_68_out, not_69_out, not_70_out, not_71_out, not_72_out,
       not_73_out, not_74_out, not_75_out, not_76_out, not_77_out, not_78_out, not_79_out, not_80_out,
       not_81_out, not_82_out, not_83_out, not_84_out, not_85_out, not_86_out, not_87_out, not_88_out,
       not_89_out, not_90_out, not_91_out, not_92_out, not_93_out, not_94_out, not_95_out, not_96_out,
       not_97_out, not_98_out, not_99_out, not_100_out, not_101_out, not_102_out, not_103_out, not_104_out,
       not_105_out, not_106_out, not_107_out, not_108_out, not_109_out, not_110_out, not_111_out,
       not_112_out, not_113_out, not_114_out, not_115_out, not_116_out, not_117_out, not_118_out,
       not_119_out, not_120_out, not_121_out, not_122_out, not_123_out, not_124_out, not_125_out,
       not_126_out, not_127_out, not_128_out, not_129_out, not_130_out, not_131_out, not_132_out,
       not_133_out, not_134_out, not_135_out, not_136_out, not_137_out, not_138_out, not_139_out,
       not_140_out, not_141_out, not_142_out, not_143_out, not_144_out, not_145_out, not_146_out,
       not_147_out, not_148_out, not_149_out, not_150_out, not_151_out, not_152_out, not_153_out,
       not_154_out, not_155_out, not_156_out, not_157_out, not_158_out, not_159_out, not_160_out,
       not_161_out, not_162_out, not_163_out, not_164_out, not_165_out, not_166_out, not_167_out,
       not_168_out, not_169_out, not_170_out, not_171_out, not_172_out, not_173_out, not_174_out,
       not_175_out, not_176_out, not_177_out, not_178_out, not_179_out, not_180_out, not_181_out,
       not_182_out, not_183_out, not_184_out, not_185_out, not_186_out, not_187_out, not_188_out,
       not_189_out, not_190_out, not_191_out, not_192_out, not_193_out, not_194_out, not_195_out,
       not_196_out, not_197_out, not_198_out, not_199_out, not_200_out, not_201_out, not_202_out,
       not_203_out, not_204_out, not_205_out, not_206_out;

  not not_1 (not_1_out, F30);
  not not_2 (not_2_out, F25);
  not not_3 (not_3_out, F14);
  not not_4 (not_4_out, F13);
  not not_5 (not_5_out, F12);
  not not_6 (not_6_out, OP6);
  not not_7 (not_7_out, OP3);
  not not_8 (not_8_out, OP2);
  not not_9 (not_9_out, F30);
  not not_10 (not_10_out, F25);
  not not_11 (not_11_out, OP6);
  not not_12 (not_12_out, OP3);
  not not_13 (not_13_out, OP2);
  not not_14 (not_14_out, F30);
  not not_15 (not_15_out, F25);
  not not_16 (not_16_out, F14);
  not not_17 (not_17_out, F12);
  not not_18 (not_18_out, OP6);
  not not_19 (not_19_out, OP3);
  not not_20 (not_20_out, OP2);
  not not_21 (not_21_out, F14);
  not not_22 (not_22_out, F13);
  not not_23 (not_23_out, F12);
  not not_24 (not_24_out, OP6);
  not not_25 (not_25_out, OP5);
  not not_26 (not_26_out, OP3);
  not not_27 (not_27_out, OP2);
  not not_28 (not_28_out, OP6);
  not not_29 (not_29_out, OP5);
  not not_30 (not_30_out, OP3);
  not not_31 (not_31_out, OP2);
  not not_32 (not_32_out, F13);
  not not_33 (not_33_out, F12);
  not not_34 (not_34_out, OP6);
  not not_35 (not_35_out, OP5);
  not not_36 (not_36_out, OP3);
  not not_37 (not_37_out, OP2);
  not not_38 (not_38_out, F14);
  not not_39 (not_39_out, F12);
  not not_40 (not_40_out, OP6);
  not not_41 (not_41_out, OP5);
  not not_42 (not_42_out, OP3);
  not not_43 (not_43_out, OP2);
  not not_44 (not_44_out, F25);
  not not_45 (not_45_out, F13);
  not not_46 (not_46_out, OP6);
  not not_47 (not_47_out, OP5);
  not not_48 (not_48_out, OP3);
  not not_49 (not_49_out, OP2);
  not not_50 (not_50_out, F14);
  not not_51 (not_51_out, F12);
  not not_52 (not_52_out, OP6);
  not not_53 (not_53_out, OP5);
  not not_54 (not_54_out, OP4);
  not not_55 (not_55_out, OP3);
  not not_56 (not_56_out, OP2);
  not not_57 (not_57_out, F14);
  not not_58 (not_58_out, F12);
  not not_59 (not_59_out, OP6);
  not not_60 (not_60_out, OP4);
  not not_61 (not_61_out, OP3);
  not not_62 (not_62_out, OP2);
  not not_63 (not_63_out, F14);
  not not_64 (not_64_out, F13);
  not not_65 (not_65_out, F12);
  not not_66 (not_66_out, OP4);
  not not_67 (not_67_out, OP3);
  not not_68 (not_68_out, OP2);
  not not_69 (not_69_out, F14);
  not not_70 (not_70_out, F13);
  not not_71 (not_71_out, OP4);
  not not_72 (not_72_out, OP3);
  not not_73 (not_73_out, OP2);
  not not_74 (not_74_out, F25);
  not not_75 (not_75_out, F14);
  not not_76 (not_76_out, F13);
  not not_77 (not_77_out, F12);
  not not_78 (not_78_out, OP6);
  not not_79 (not_79_out, OP3);
  not not_80 (not_80_out, OP2);
  not not_81 (not_81_out, F30);
  not not_82 (not_82_out, F25);
  not not_83 (not_83_out, OP6);
  not not_84 (not_84_out, OP3);
  not not_85 (not_85_out, OP2);
  not not_86 (not_86_out, F30);
  not not_87 (not_87_out, F25);
  not not_88 (not_88_out, F14);
  not not_89 (not_89_out, F12);
  not not_90 (not_90_out, OP6);
  not not_91 (not_91_out, OP3);
  not not_92 (not_92_out, OP2);
  not not_93 (not_93_out, OP6);
  not not_94 (not_94_out, OP5);
  not not_95 (not_95_out, OP3);
  not not_96 (not_96_out, OP2);
  not not_97 (not_97_out, F14);
  not not_98 (not_98_out, F12);
  not not_99 (not_99_out, OP6);
  not not_100 (not_100_out, OP5);
  not not_101 (not_101_out, OP3);
  not not_102 (not_102_out, OP2);
  not not_103 (not_103_out, F30);
  not not_104 (not_104_out, F25);
  not not_105 (not_105_out, F13);
  not not_106 (not_106_out, OP6);
  not not_107 (not_107_out, OP5);
  not not_108 (not_108_out, OP3);
  not not_109 (not_109_out, OP2);
  not not_110 (not_110_out, F30);
  not not_111 (not_111_out, F25);
  not not_112 (not_112_out, F14);
  not not_113 (not_113_out, F13);
  not not_114 (not_114_out, F12);
  not not_115 (not_115_out, OP6);
  not not_116 (not_116_out, OP3);
  not not_117 (not_117_out, OP2);
  not not_118 (not_118_out, F25);
  not not_119 (not_119_out, F14);
  not not_120 (not_120_out, F13);
  not not_121 (not_121_out, F12);
  not not_122 (not_122_out, OP6);
  not not_123 (not_123_out, OP3);
  not not_124 (not_124_out, OP2);
  not not_125 (not_125_out, F30);
  not not_126 (not_126_out, F25);
  not not_127 (not_127_out, OP6);
  not not_128 (not_128_out, OP3);
  not not_129 (not_129_out, OP2);
  not not_130 (not_130_out, F30);
  not not_131 (not_131_out, F25);
  not not_132 (not_132_out, F14);
  not not_133 (not_133_out, OP6);
  not not_134 (not_134_out, OP3);
  not not_135 (not_135_out, OP2);
  not not_136 (not_136_out, F14);
  not not_137 (not_137_out, F13);
  not not_138 (not_138_out, F12);
  not not_139 (not_139_out, OP6);
  not not_140 (not_140_out, OP5);
  not not_141 (not_141_out, OP3);
  not not_142 (not_142_out, OP2);
  not not_143 (not_143_out, OP6);
  not not_144 (not_144_out, OP5);
  not not_145 (not_145_out, OP3);
  not not_146 (not_146_out, OP2);
  not not_147 (not_147_out, F14);
  not not_148 (not_148_out, F12);
  not not_149 (not_149_out, OP6);
  not not_150 (not_150_out, OP5);
  not not_151 (not_151_out, OP4);
  not not_152 (not_152_out, OP3);
  not not_153 (not_153_out, OP2);
  not not_154 (not_154_out, F14);
  not not_155 (not_155_out, F12);
  not not_156 (not_156_out, OP6);
  not not_157 (not_157_out, OP4);
  not not_158 (not_158_out, OP3);
  not not_159 (not_159_out, OP2);
  not not_160 (not_160_out, F14);
  not not_161 (not_161_out, F13);
  not not_162 (not_162_out, F12);
  not not_163 (not_163_out, OP4);
  not not_164 (not_164_out, OP3);
  not not_165 (not_165_out, OP2);
  not not_166 (not_166_out, F14);
  not not_167 (not_167_out, F13);
  not not_168 (not_168_out, OP4);
  not not_169 (not_169_out, OP3);
  not not_170 (not_170_out, OP2);
  not not_171 (not_171_out, F30);
  not not_172 (not_172_out, F25);
  not not_173 (not_173_out, F12);
  not not_174 (not_174_out, OP6);
  not not_175 (not_175_out, OP3);
  not not_176 (not_176_out, OP2);
  not not_177 (not_177_out, F30);
  not not_178 (not_178_out, F25);
  not not_179 (not_179_out, F14);
  not not_180 (not_180_out, F12);
  not not_181 (not_181_out, OP6);
  not not_182 (not_182_out, OP3);
  not not_183 (not_183_out, OP2);
  not not_184 (not_184_out, F30);
  not not_185 (not_185_out, F25);
  not not_186 (not_186_out, F14);
  not not_187 (not_187_out, OP6);
  not not_188 (not_188_out, OP3);
  not not_189 (not_189_out, OP2);
  not not_190 (not_190_out, F12);
  not not_191 (not_191_out, OP6);
  not not_192 (not_192_out, OP5);
  not not_193 (not_193_out, OP3);
  not not_194 (not_194_out, OP2);
  not not_195 (not_195_out, F13);
  not not_196 (not_196_out, F12);
  not not_197 (not_197_out, OP6);
  not not_198 (not_198_out, OP5);
  not not_199 (not_199_out, OP3);
  not not_200 (not_200_out, OP2);
  not not_201 (not_201_out, F14);
  not not_202 (not_202_out, F12);
  not not_203 (not_203_out, OP6);
  not not_204 (not_204_out, OP5);
  not not_205 (not_205_out, OP3);
  not not_206 (not_206_out, OP2);
  and and_1 (and_1_out, not_1_out, not_2_out, not_3_out, not_4_out, not_5_out, not_6_out, OP5, OP4, not_7_out, not_8_out);
  and and_2 (and_2_out, not_9_out, not_10_out, F14, F13, F12, not_11_out, OP5, OP4, not_12_out, not_13_out);
  and and_3 (and_3_out, not_14_out, not_15_out, not_16_out, F13, not_17_out, not_18_out, OP5, OP4, not_19_out, not_20_out);
  and and_4 (and_4_out, not_21_out, not_22_out, not_23_out, not_24_out, not_25_out, OP4, not_26_out, not_27_out);
  and and_5 (and_5_out, F14, F13, F12, not_28_out, not_29_out, OP4, not_30_out, not_31_out);
  and and_6 (and_6_out, F14, not_32_out, not_33_out, not_34_out, not_35_out, OP4, not_36_out, not_37_out);
  and and_7 (and_7_out, not_38_out, F13, not_39_out, not_40_out, not_41_out, OP4, not_42_out, not_43_out);
  and and_8 (and_8_out, F30, not_44_out, F14, not_45_out, F12, not_46_out, not_47_out, OP4, not_48_out, not_49_out);
  and and_9 (and_9_out, not_50_out, F13, not_51_out, not_52_out, not_53_out, not_54_out, not_55_out, not_56_out);
  and and_10 (and_10_out, not_57_out, F13, not_58_out, not_59_out, OP5, not_60_out, not_61_out, not_62_out);
  and and_11 (and_11_out, not_63_out, not_64_out, not_65_out, OP6, OP5, not_66_out, not_67_out, not_68_out);
  and and_12 (and_12_out, not_69_out, not_70_out, F12, OP6, OP5, not_71_out, not_72_out, not_73_out);
  and and_13 (and_13_out, F30, not_74_out, not_75_out, not_76_out, not_77_out, not_78_out, OP5, OP4, not_79_out, not_80_out);
  and and_14 (and_14_out, not_81_out, not_82_out, F14, F13, F12, not_83_out, OP5, OP4, not_84_out, not_85_out);
  and and_15 (and_15_out, not_86_out, not_87_out, not_88_out, F13, not_89_out, not_90_out, OP5, OP4, not_91_out, not_92_out);
  and and_16 (and_16_out, F14, F13, F12, not_93_out, not_94_out, OP4, not_95_out, not_96_out);
  and and_17 (and_17_out, not_97_out, F13, not_98_out, not_99_out, not_100_out, OP4, not_101_out, not_102_out);
  and and_18 (and_18_out, not_103_out, not_104_out, F14, not_105_out, F12, not_106_out, not_107_out, OP4, not_108_out, not_109_out);
  and and_19 (and_19_out, not_110_out, not_111_out, not_112_out, not_113_out, not_114_out, not_115_out, OP5, OP4, not_116_out, not_117_out);
  and and_20 (and_20_out, F30, not_118_out, not_119_out, not_120_out, not_121_out, not_122_out, OP5, OP4, not_123_out, not_124_out);
  and and_21 (and_21_out, not_125_out, not_126_out, F14, F13, F12, not_127_out, OP5, OP4, not_128_out, not_129_out);
  and and_22 (and_22_out, not_130_out, not_131_out, not_132_out, F13, F12, not_133_out, OP5, OP4, not_134_out, not_135_out);
  and and_23 (and_23_out, not_136_out, not_137_out, not_138_out, not_139_out, not_140_out, OP4, not_141_out, not_142_out);
  and and_24 (and_24_out, F14, F13, F12, not_143_out, not_144_out, OP4, not_145_out, not_146_out);
  and and_25 (and_25_out, not_147_out, F13, not_148_out, not_149_out, not_150_out, not_151_out, not_152_out, not_153_out);
  and and_26 (and_26_out, not_154_out, F13, not_155_out, not_156_out, OP5, not_157_out, not_158_out, not_159_out);
  and and_27 (and_27_out, not_160_out, not_161_out, not_162_out, OP6, OP5, not_163_out, not_164_out, not_165_out);
  and and_28 (and_28_out, not_166_out, not_167_out, F12, OP6, OP5, not_168_out, not_169_out, not_170_out);
  and and_29 (and_29_out, not_171_out, not_172_out, F14, F13, not_173_out, not_174_out, OP5, OP4, not_175_out, not_176_out);
  and and_30 (and_30_out, not_177_out, not_178_out, not_179_out, F13, not_180_out, not_181_out, OP5, OP4, not_182_out, not_183_out);
  and and_31 (and_31_out, not_184_out, not_185_out, not_186_out, F13, F12, not_187_out, OP5, OP4, not_188_out, not_189_out);
  and and_32 (and_32_out, F14, F13, not_190_out, not_191_out, not_192_out, OP4, not_193_out, not_194_out);
  and and_33 (and_33_out, F14, not_195_out, not_196_out, not_197_out, not_198_out, OP4, not_199_out, not_200_out);
  and and_34 (and_34_out, not_201_out, F13, not_202_out, not_203_out, not_204_out, OP4, not_205_out, not_206_out);
  or or_1 (S0, and_1_out, and_2_out, and_3_out, and_4_out, and_5_out, and_6_out, and_7_out, and_8_out, and_9_out, and_10_out, and_11_out, and_12_out);
  or or_2 (S1, and_13_out, and_14_out, and_15_out, and_16_out, and_17_out, and_18_out);
  or or_3 (S2, and_19_out, and_20_out, and_21_out, and_22_out, and_23_out, and_24_out, and_25_out, and_26_out, and_27_out, and_28_out);
  or or_4 (S3, and_29_out, and_30_out, and_31_out, and_32_out, and_33_out, and_34_out);
endmodule

// 控制信号生成
module \控制信号自动生成  (
  input  OP2,
  input  OP3,
  input  OP4,
  input  OP5,
  input  OP6,
  input  F12,
  input  F13,
  input  F14,
  input  F25,
  input  F30,
  output MemToReg,
  output MemWrite,
  output ALU_SRC,
  output RegWrite,
  output ecall,
  output S_Type,
  output BEQ,
  output BNE,
  output JALR,
  output JAL
);

  wire and_3_out, and_4_out, and_5_out, and_6_out, and_7_out, and_8_out, and_9_out, and_10_out, and_11_out,
       and_12_out, and_13_out, and_14_out, and_15_out, and_16_out, and_17_out, and_18_out, and_19_out,
       and_20_out, and_21_out, and_22_out, and_23_out, and_24_out, and_25_out, and_26_out, and_27_out,
       and_28_out, and_29_out, and_30_out, not_1_out, not_2_out, not_3_out, not_4_out, not_5_out, not_6_out,
       not_7_out, not_8_out, not_9_out, not_10_out, not_11_out, not_12_out, not_13_out, not_14_out,
       not_15_out, not_16_out, not_17_out, not_18_out, not_19_out, not_20_out, not_21_out, not_22_out,
       not_23_out, not_24_out, not_25_out, not_26_out, not_27_out, not_28_out, not_29_out, not_30_out,
       not_31_out, not_32_out, not_33_out, not_34_out, not_35_out, not_36_out, not_37_out, not_38_out,
       not_39_out, not_40_out, not_41_out, not_42_out, not_43_out, not_44_out, not_45_out, not_46_out,
       not_47_out, not_48_out, not_49_out, not_50_out, not_51_out, not_52_out, not_53_out, not_54_out,
       not_55_out, not_56_out, not_57_out, not_58_out, not_59_out, not_60_out, not_61_out, not_62_out,
       not_63_out, not_64_out, not_65_out, not_66_out, not_67_out, not_68_out, not_69_out, not_70_out,
       not_71_out, not_72_out, not_73_out, not_74_out, not_75_out, not_76_out, not_77_out, not_78_out,
       not_79_out, not_80_out, not_81_out, not_82_out, not_83_out, not_84_out, not_85_out, not_86_out,
       not_87_out, not_88_out, not_89_out, not_90_out, not_91_out, not_92_out, not_93_out, not_94_out,
       not_95_out, not_96_out, not_97_out, not_98_out, not_99_out, not_100_out, not_101_out, not_102_out,
       not_103_out, not_104_out, not_105_out, not_106_out, not_107_out, not_108_out, not_109_out,
       not_110_out, not_111_out, not_112_out, not_113_out, not_114_out, not_115_out, not_116_out,
       not_117_out, not_118_out, not_119_out, not_120_out, not_121_out, not_122_out, not_123_out,
       not_124_out, not_125_out, not_126_out, not_127_out, not_128_out, not_129_out, not_130_out,
       not_131_out, not_132_out, not_133_out, not_134_out, not_135_out, not_136_out, not_137_out,
       not_138_out, not_139_out, not_140_out, not_141_out, not_142_out, not_143_out, not_144_out,
       not_145_out, not_146_out, not_147_out, not_148_out, not_149_out, not_150_out, not_151_out,
       not_152_out, not_153_out, not_154_out, not_155_out, not_156_out, not_157_out, not_158_out,
       not_159_out, not_160_out, not_161_out, not_162_out, not_163_out, not_164_out, not_165_out,
       not_166_out, not_167_out, not_168_out, not_169_out, not_170_out, not_171_out, not_172_out,
       not_173_out, not_174_out, not_175_out, not_176_out, not_177_out, not_178_out, not_179_out,
       not_180_out, not_181_out, not_182_out, not_183_out, not_184_out, not_185_out, not_186_out,
       not_187_out, not_188_out, not_189_out, not_190_out, not_191_out, not_192_out, not_193_out,
       not_194_out, not_195_out, not_196_out, not_197_out, not_198_out, not_199_out, not_200_out,
       not_201_out, not_202_out, not_203_out, not_204_out, not_205_out, not_206_out, not_207_out;

  not not_1 (not_1_out, OP2);
  not not_2 (not_2_out, OP3);
  not not_3 (not_3_out, OP4);
  not not_4 (not_4_out, OP5);
  not not_5 (not_5_out, OP6);
  not not_6 (not_6_out, F12);
  not not_7 (not_7_out, F14);
  not not_8 (not_8_out, OP2);
  not not_9 (not_9_out, OP3);
  not not_10 (not_10_out, OP4);
  not not_11 (not_11_out, OP6);
  not not_12 (not_12_out, F12);
  not not_13 (not_13_out, F14);
  not not_14 (not_14_out, F14);
  not not_15 (not_15_out, F13);
  not not_16 (not_16_out, F12);
  not not_17 (not_17_out, OP6);
  not not_18 (not_18_out, OP5);
  not not_19 (not_19_out, OP3);
  not not_20 (not_20_out, OP2);
  not not_21 (not_21_out, OP6);
  not not_22 (not_22_out, OP5);
  not not_23 (not_23_out, OP3);
  not not_24 (not_24_out, OP2);
  not not_25 (not_25_out, F12);
  not not_26 (not_26_out, OP6);
  not not_27 (not_27_out, OP5);
  not not_28 (not_28_out, OP3);
  not not_29 (not_29_out, OP2);
  not not_30 (not_30_out, F13);
  not not_31 (not_31_out, F12);
  not not_32 (not_32_out, OP6);
  not not_33 (not_33_out, OP5);
  not not_34 (not_34_out, OP3);
  not not_35 (not_35_out, OP2);
  not not_36 (not_36_out, F14);
  not not_37 (not_37_out, F12);
  not not_38 (not_38_out, OP6);
  not not_39 (not_39_out, OP5);
  not not_40 (not_40_out, OP3);
  not not_41 (not_41_out, OP2);
  not not_42 (not_42_out, F14);
  not not_43 (not_43_out, F13);
  not not_44 (not_44_out, OP6);
  not not_45 (not_45_out, OP5);
  not not_46 (not_46_out, OP3);
  not not_47 (not_47_out, OP2);
  not not_48 (not_48_out, F30);
  not not_49 (not_49_out, F25);
  not not_50 (not_50_out, F13);
  not not_51 (not_51_out, OP6);
  not not_52 (not_52_out, OP5);
  not not_53 (not_53_out, OP3);
  not not_54 (not_54_out, OP2);
  not not_55 (not_55_out, F25);
  not not_56 (not_56_out, F13);
  not not_57 (not_57_out, OP6);
  not not_58 (not_58_out, OP5);
  not not_59 (not_59_out, OP3);
  not not_60 (not_60_out, OP2);
  not not_61 (not_61_out, F14);
  not not_62 (not_62_out, F12);
  not not_63 (not_63_out, OP6);
  not not_64 (not_64_out, OP5);
  not not_65 (not_65_out, OP4);
  not not_66 (not_66_out, OP3);
  not not_67 (not_67_out, OP2);
  not not_68 (not_68_out, F14);
  not not_69 (not_69_out, F12);
  not not_70 (not_70_out, OP6);
  not not_71 (not_71_out, OP4);
  not not_72 (not_72_out, OP3);
  not not_73 (not_73_out, OP2);
  not not_74 (not_74_out, F14);
  not not_75 (not_75_out, F13);
  not not_76 (not_76_out, F12);
  not not_77 (not_77_out, OP4);
  not not_78 (not_78_out, OP3);
  not not_79 (not_79_out, F30);
  not not_80 (not_80_out, F25);
  not not_81 (not_81_out, F14);
  not not_82 (not_82_out, F13);
  not not_83 (not_83_out, F12);
  not not_84 (not_84_out, OP6);
  not not_85 (not_85_out, OP3);
  not not_86 (not_86_out, OP2);
  not not_87 (not_87_out, F25);
  not not_88 (not_88_out, F14);
  not not_89 (not_89_out, F13);
  not not_90 (not_90_out, F12);
  not not_91 (not_91_out, OP6);
  not not_92 (not_92_out, OP3);
  not not_93 (not_93_out, OP2);
  not not_94 (not_94_out, F30);
  not not_95 (not_95_out, F25);
  not not_96 (not_96_out, OP6);
  not not_97 (not_97_out, OP3);
  not not_98 (not_98_out, OP2);
  not not_99 (not_99_out, F30);
  not not_100 (not_100_out, F25);
  not not_101 (not_101_out, F12);
  not not_102 (not_102_out, OP6);
  not not_103 (not_103_out, OP3);
  not not_104 (not_104_out, OP2);
  not not_105 (not_105_out, F30);
  not not_106 (not_106_out, F25);
  not not_107 (not_107_out, F14);
  not not_108 (not_108_out, F12);
  not not_109 (not_109_out, OP6);
  not not_110 (not_110_out, OP3);
  not not_111 (not_111_out, OP2);
  not not_112 (not_112_out, F30);
  not not_113 (not_113_out, F25);
  not not_114 (not_114_out, F14);
  not not_115 (not_115_out, OP6);
  not not_116 (not_116_out, OP3);
  not not_117 (not_117_out, OP2);
  not not_118 (not_118_out, F14);
  not not_119 (not_119_out, F13);
  not not_120 (not_120_out, F12);
  not not_121 (not_121_out, OP6);
  not not_122 (not_122_out, OP5);
  not not_123 (not_123_out, OP3);
  not not_124 (not_124_out, OP2);
  not not_125 (not_125_out, OP6);
  not not_126 (not_126_out, OP5);
  not not_127 (not_127_out, OP3);
  not not_128 (not_128_out, OP2);
  not not_129 (not_129_out, F12);
  not not_130 (not_130_out, OP6);
  not not_131 (not_131_out, OP5);
  not not_132 (not_132_out, OP3);
  not not_133 (not_133_out, OP2);
  not not_134 (not_134_out, F13);
  not not_135 (not_135_out, F12);
  not not_136 (not_136_out, OP6);
  not not_137 (not_137_out, OP5);
  not not_138 (not_138_out, OP3);
  not not_139 (not_139_out, OP2);
  not not_140 (not_140_out, F14);
  not not_141 (not_141_out, F12);
  not not_142 (not_142_out, OP6);
  not not_143 (not_143_out, OP5);
  not not_144 (not_144_out, OP3);
  not not_145 (not_145_out, OP2);
  not not_146 (not_146_out, F14);
  not not_147 (not_147_out, F13);
  not not_148 (not_148_out, OP6);
  not not_149 (not_149_out, OP5);
  not not_150 (not_150_out, OP3);
  not not_151 (not_151_out, OP2);
  not not_152 (not_152_out, F30);
  not not_153 (not_153_out, F25);
  not not_154 (not_154_out, F13);
  not not_155 (not_155_out, OP6);
  not not_156 (not_156_out, OP5);
  not not_157 (not_157_out, OP3);
  not not_158 (not_158_out, OP2);
  not not_159 (not_159_out, F25);
  not not_160 (not_160_out, F13);
  not not_161 (not_161_out, OP6);
  not not_162 (not_162_out, OP5);
  not not_163 (not_163_out, OP3);
  not not_164 (not_164_out, OP2);
  not not_165 (not_165_out, F14);
  not not_166 (not_166_out, F12);
  not not_167 (not_167_out, OP6);
  not not_168 (not_168_out, OP5);
  not not_169 (not_169_out, OP4);
  not not_170 (not_170_out, OP3);
  not not_171 (not_171_out, OP2);
  not not_172 (not_172_out, OP4);
  not not_173 (not_173_out, F14);
  not not_174 (not_174_out, F13);
  not not_175 (not_175_out, F12);
  not not_176 (not_176_out, OP4);
  not not_177 (not_177_out, OP3);
  not not_178 (not_178_out, OP2);
  not not_179 (not_179_out, OP3);
  not not_180 (not_180_out, F12);
  not not_181 (not_181_out, F13);
  not not_182 (not_182_out, F14);
  not not_183 (not_183_out, F25);
  not not_184 (not_184_out, F30);
  not not_185 (not_185_out, OP2);
  not not_186 (not_186_out, OP3);
  not not_187 (not_187_out, OP4);
  not not_188 (not_188_out, OP6);
  not not_189 (not_189_out, F12);
  not not_190 (not_190_out, F14);
  not not_191 (not_191_out, OP2);
  not not_192 (not_192_out, OP3);
  not not_193 (not_193_out, OP4);
  not not_194 (not_194_out, F12);
  not not_195 (not_195_out, F13);
  not not_196 (not_196_out, F14);
  not not_197 (not_197_out, OP2);
  not not_198 (not_198_out, OP3);
  not not_199 (not_199_out, OP4);
  not not_200 (not_200_out, F13);
  not not_201 (not_201_out, F14);
  not not_202 (not_202_out, OP3);
  not not_203 (not_203_out, OP4);
  not not_204 (not_204_out, F12);
  not not_205 (not_205_out, F13);
  not not_206 (not_206_out, F14);
  not not_207 (not_207_out, OP4);
  and and_1 (MemToReg, not_1_out, not_2_out, not_3_out, not_4_out, not_5_out, not_6_out, F13, not_7_out);
  and and_2 (MemWrite, not_8_out, not_9_out, not_10_out, OP5, not_11_out, not_12_out, F13, not_13_out);
  and and_3 (and_3_out, not_14_out, not_15_out, not_16_out, not_17_out, not_18_out, OP4, not_19_out, not_20_out);
  and and_4 (and_4_out, F14, F13, F12, not_21_out, not_22_out, OP4, not_23_out, not_24_out);
  and and_5 (and_5_out, F14, F13, not_25_out, not_26_out, not_27_out, OP4, not_28_out, not_29_out);
  and and_6 (and_6_out, F14, not_30_out, not_31_out, not_32_out, not_33_out, OP4, not_34_out, not_35_out);
  and and_7 (and_7_out, not_36_out, F13, not_37_out, not_38_out, not_39_out, OP4, not_40_out, not_41_out);
  and and_8 (and_8_out, not_42_out, not_43_out, F12, not_44_out, not_45_out, OP4, not_46_out, not_47_out);
  and and_9 (and_9_out, not_48_out, not_49_out, F14, not_50_out, F12, not_51_out, not_52_out, OP4, not_53_out, not_54_out);
  and and_10 (and_10_out, F30, not_55_out, F14, not_56_out, F12, not_57_out, not_58_out, OP4, not_59_out, not_60_out);
  and and_11 (and_11_out, not_61_out, F13, not_62_out, not_63_out, not_64_out, not_65_out, not_66_out, not_67_out);
  and and_12 (and_12_out, not_68_out, F13, not_69_out, not_70_out, OP5, not_71_out, not_72_out, not_73_out);
  and and_13 (and_13_out, not_74_out, not_75_out, not_76_out, OP6, OP5, not_77_out, not_78_out, OP2);
  and and_14 (and_14_out, not_79_out, not_80_out, not_81_out, not_82_out, not_83_out, not_84_out, OP5, OP4, not_85_out, not_86_out);
  and and_15 (and_15_out, F30, not_87_out, not_88_out, not_89_out, not_90_out, not_91_out, OP5, OP4, not_92_out, not_93_out);
  and and_16 (and_16_out, not_94_out, not_95_out, F14, F13, F12, not_96_out, OP5, OP4, not_97_out, not_98_out);
  and and_17 (and_17_out, not_99_out, not_100_out, F14, F13, not_101_out, not_102_out, OP5, OP4, not_103_out, not_104_out);
  and and_18 (and_18_out, not_105_out, not_106_out, not_107_out, F13, not_108_out, not_109_out, OP5, OP4, not_110_out, not_111_out);
  and and_19 (and_19_out, not_112_out, not_113_out, not_114_out, F13, F12, not_115_out, OP5, OP4, not_116_out, not_117_out);
  and and_20 (and_20_out, not_118_out, not_119_out, not_120_out, not_121_out, not_122_out, OP4, not_123_out, not_124_out);
  and and_21 (and_21_out, F14, F13, F12, not_125_out, not_126_out, OP4, not_127_out, not_128_out);
  and and_22 (and_22_out, F14, F13, not_129_out, not_130_out, not_131_out, OP4, not_132_out, not_133_out);
  and and_23 (and_23_out, F14, not_134_out, not_135_out, not_136_out, not_137_out, OP4, not_138_out, not_139_out);
  and and_24 (and_24_out, not_140_out, F13, not_141_out, not_142_out, not_143_out, OP4, not_144_out, not_145_out);
  and and_25 (and_25_out, not_146_out, not_147_out, F12, not_148_out, not_149_out, OP4, not_150_out, not_151_out);
  and and_26 (and_26_out, not_152_out, not_153_out, F14, not_154_out, F12, not_155_out, not_156_out, OP4, not_157_out, not_158_out);
  and and_27 (and_27_out, F30, not_159_out, F14, not_160_out, F12, not_161_out, not_162_out, OP4, not_163_out, not_164_out);
  and and_28 (and_28_out, not_165_out, F13, not_166_out, not_167_out, not_168_out, not_169_out, not_170_out, not_171_out);
  and and_29 (and_29_out, OP6, OP5, not_172_out, OP3, OP2);
  and and_30 (and_30_out, not_173_out, not_174_out, not_175_out, OP6, OP5, not_176_out, not_177_out, OP2);
  and and_31 (ecall, not_178_out, not_179_out, OP4, OP5, OP6, not_180_out, not_181_out, not_182_out, not_183_out, not_184_out);
  and and_32 (S_Type, not_185_out, not_186_out, not_187_out, OP5, not_188_out, not_189_out, F13, not_190_out);
  and and_33 (BEQ, not_191_out, not_192_out, not_193_out, OP5, OP6, not_194_out, not_195_out, not_196_out);
  and and_34 (BNE, not_197_out, not_198_out, not_199_out, OP5, OP6, F12, not_200_out, not_201_out);
  and and_35 (JALR, OP2, not_202_out, not_203_out, OP5, OP6, not_204_out, not_205_out, not_206_out);
  and and_36 (JAL, OP2, OP3, not_207_out, OP5, OP6);
  or or_1 (ALU_SRC, and_3_out, and_4_out, and_5_out, and_6_out, and_7_out, and_8_out, and_9_out, and_10_out, and_11_out, and_12_out, and_13_out);
  or or_2 (RegWrite, and_14_out, and_15_out, and_16_out, and_17_out, and_18_out, and_19_out, and_20_out, and_21_out, and_22_out, and_23_out, and_24_out, and_25_out, and_26_out, and_27_out, and_28_out, and_29_out, and_30_out);
endmodule

module \运算控制器自动生成_CCAB  (
  input  OP2,
  input  OP3,
  input  OP4,
  input  OP5,
  input  OP6,
  input  F12,
  input  F13,
  input  F14,
  input  F25,
  input  F30,
  output S0,
  output S1,
  output S2,
  output S3
);

  wire and_1_out, and_2_out, and_3_out, and_4_out, and_5_out, and_6_out, and_7_out, and_8_out, and_9_out,
       and_10_out, and_11_out, and_12_out, and_13_out, and_14_out, and_15_out, and_16_out, and_17_out,
       and_18_out, and_19_out, and_20_out, and_21_out, and_22_out, and_23_out, and_24_out, and_25_out,
       and_26_out, and_27_out, and_28_out, and_29_out, and_30_out, and_31_out, and_32_out, and_33_out,
       and_34_out, and_35_out, and_36_out, and_37_out, and_38_out, and_39_out, and_40_out, and_41_out,
       not_1_out, not_2_out, not_3_out, not_4_out, not_5_out, not_6_out, not_7_out, not_8_out, not_9_out,
       not_10_out, not_11_out, not_12_out, not_13_out, not_14_out, not_15_out, not_16_out, not_17_out,
       not_18_out, not_19_out, not_20_out, not_21_out, not_22_out, not_23_out, not_24_out, not_25_out,
       not_26_out, not_27_out, not_28_out, not_29_out, not_30_out, not_31_out, not_32_out, not_33_out,
       not_34_out, not_35_out, not_36_out, not_37_out, not_38_out, not_39_out, not_40_out, not_41_out,
       not_42_out, not_43_out, not_44_out, not_45_out, not_46_out, not_47_out, not_48_out, not_49_out,
       not_50_out, not_51_out, not_52_out, not_53_out, not_54_out, not_55_out, not_56_out, not_57_out,
       not_58_out, not_59_out, not_60_out, not_61_out, not_62_out, not_63_out, not_64_out, not_65_out,
       not_66_out, not_67_out, not_68_out, not_69_out, not_70_out, not_71_out, not_72_out, not_73_out,
       not_74_out, not_75_out, not_76_out, not_77_out, not_78_out, not_79_out, not_80_out, not_81_out,
       not_82_out, not_83_out, not_84_out, not_85_out, not_86_out, not_87_out, not_88_out, not_89_out,
       not_90_out, not_91_out, not_92_out, not_93_out, not_94_out, not_95_out, not_96_out, not_97_out,
       not_98_out, not_99_out, not_100_out, not_101_out, not_102_out, not_103_out, not_104_out, not_105_out,
       not_106_out, not_107_out, not_108_out, not_109_out, not_110_out, not_111_out, not_112_out,
       not_113_out, not_114_out, not_115_out, not_116_out, not_117_out, not_118_out, not_119_out,
       not_120_out, not_121_out, not_122_out, not_123_out, not_124_out, not_125_out, not_126_out,
       not_127_out, not_128_out, not_129_out, not_130_out, not_131_out, not_132_out, not_133_out,
       not_134_out, not_135_out, not_136_out, not_137_out, not_138_out, not_139_out, not_140_out,
       not_141_out, not_142_out, not_143_out, not_144_out, not_145_out, not_146_out, not_147_out,
       not_148_out, not_149_out, not_150_out, not_151_out, not_152_out, not_153_out, not_154_out,
       not_155_out, not_156_out, not_157_out, not_158_out, not_159_out, not_160_out, not_161_out,
       not_162_out, not_163_out, not_164_out, not_165_out, not_166_out, not_167_out, not_168_out,
       not_169_out, not_170_out, not_171_out, not_172_out, not_173_out, not_174_out, not_175_out,
       not_176_out, not_177_out, not_178_out, not_179_out, not_180_out, not_181_out, not_182_out,
       not_183_out, not_184_out, not_185_out, not_186_out, not_187_out, not_188_out, not_189_out,
       not_190_out, not_191_out, not_192_out, not_193_out, not_194_out, not_195_out, not_196_out,
       not_197_out, not_198_out, not_199_out, not_200_out, not_201_out, not_202_out, not_203_out,
       not_204_out, not_205_out, not_206_out, not_207_out, not_208_out, not_209_out, not_210_out,
       not_211_out, not_212_out, not_213_out, not_214_out, not_215_out, not_216_out, not_217_out,
       not_218_out, not_219_out, not_220_out, not_221_out, not_222_out, not_223_out, not_224_out,
       not_225_out, not_226_out, not_227_out, not_228_out, not_229_out, not_230_out, not_231_out,
       not_232_out, not_233_out, not_234_out, not_235_out, not_236_out, not_237_out, not_238_out,
       not_239_out, not_240_out, not_241_out, not_242_out, not_243_out, not_244_out;

  not not_1 (not_1_out, F30);
  not not_2 (not_2_out, F25);
  not not_3 (not_3_out, F14);
  not not_4 (not_4_out, F13);
  not not_5 (not_5_out, F12);
  not not_6 (not_6_out, OP6);
  not not_7 (not_7_out, OP3);
  not not_8 (not_8_out, OP2);
  not not_9 (not_9_out, F30);
  not not_10 (not_10_out, F25);
  not not_11 (not_11_out, OP6);
  not not_12 (not_12_out, OP3);
  not not_13 (not_13_out, OP2);
  not not_14 (not_14_out, F30);
  not not_15 (not_15_out, F25);
  not not_16 (not_16_out, F14);
  not not_17 (not_17_out, F12);
  not not_18 (not_18_out, OP6);
  not not_19 (not_19_out, OP3);
  not not_20 (not_20_out, OP2);
  not not_21 (not_21_out, F14);
  not not_22 (not_22_out, F13);
  not not_23 (not_23_out, F12);
  not not_24 (not_24_out, OP6);
  not not_25 (not_25_out, OP5);
  not not_26 (not_26_out, OP3);
  not not_27 (not_27_out, OP2);
  not not_28 (not_28_out, OP6);
  not not_29 (not_29_out, OP5);
  not not_30 (not_30_out, OP3);
  not not_31 (not_31_out, OP2);
  not not_32 (not_32_out, F13);
  not not_33 (not_33_out, F12);
  not not_34 (not_34_out, OP6);
  not not_35 (not_35_out, OP5);
  not not_36 (not_36_out, OP3);
  not not_37 (not_37_out, OP2);
  not not_38 (not_38_out, F14);
  not not_39 (not_39_out, F12);
  not not_40 (not_40_out, OP6);
  not not_41 (not_41_out, OP5);
  not not_42 (not_42_out, OP3);
  not not_43 (not_43_out, OP2);
  not not_44 (not_44_out, F25);
  not not_45 (not_45_out, F13);
  not not_46 (not_46_out, OP6);
  not not_47 (not_47_out, OP5);
  not not_48 (not_48_out, OP3);
  not not_49 (not_49_out, OP2);
  not not_50 (not_50_out, F14);
  not not_51 (not_51_out, F12);
  not not_52 (not_52_out, OP6);
  not not_53 (not_53_out, OP5);
  not not_54 (not_54_out, OP4);
  not not_55 (not_55_out, OP3);
  not not_56 (not_56_out, OP2);
  not not_57 (not_57_out, F14);
  not not_58 (not_58_out, F12);
  not not_59 (not_59_out, OP6);
  not not_60 (not_60_out, OP4);
  not not_61 (not_61_out, OP3);
  not not_62 (not_62_out, OP2);
  not not_63 (not_63_out, F14);
  not not_64 (not_64_out, F13);
  not not_65 (not_65_out, F12);
  not not_66 (not_66_out, OP4);
  not not_67 (not_67_out, OP3);
  not not_68 (not_68_out, OP2);
  not not_69 (not_69_out, F14);
  not not_70 (not_70_out, F13);
  not not_71 (not_71_out, OP4);
  not not_72 (not_72_out, OP3);
  not not_73 (not_73_out, OP2);
  not not_74 (not_74_out, F14);
  not not_75 (not_75_out, F13);
  not not_76 (not_76_out, F12);
  not not_77 (not_77_out, OP4);
  not not_78 (not_78_out, OP3);
  not not_79 (not_79_out, F14);
  not not_80 (not_80_out, F13);
  not not_81 (not_81_out, F12);
  not not_82 (not_82_out, OP6);
  not not_83 (not_83_out, OP5);
  not not_84 (not_84_out, OP4);
  not not_85 (not_85_out, OP3);
  not not_86 (not_86_out, OP2);
  not not_87 (not_87_out, F25);
  not not_88 (not_88_out, F14);
  not not_89 (not_89_out, F13);
  not not_90 (not_90_out, F12);
  not not_91 (not_91_out, OP6);
  not not_92 (not_92_out, OP3);
  not not_93 (not_93_out, OP2);
  not not_94 (not_94_out, F30);
  not not_95 (not_95_out, F25);
  not not_96 (not_96_out, OP6);
  not not_97 (not_97_out, OP3);
  not not_98 (not_98_out, OP2);
  not not_99 (not_99_out, F30);
  not not_100 (not_100_out, F25);
  not not_101 (not_101_out, F14);
  not not_102 (not_102_out, F12);
  not not_103 (not_103_out, OP6);
  not not_104 (not_104_out, OP3);
  not not_105 (not_105_out, OP2);
  not not_106 (not_106_out, OP6);
  not not_107 (not_107_out, OP5);
  not not_108 (not_108_out, OP3);
  not not_109 (not_109_out, OP2);
  not not_110 (not_110_out, F14);
  not not_111 (not_111_out, F12);
  not not_112 (not_112_out, OP6);
  not not_113 (not_113_out, OP5);
  not not_114 (not_114_out, OP3);
  not not_115 (not_115_out, OP2);
  not not_116 (not_116_out, F30);
  not not_117 (not_117_out, F25);
  not not_118 (not_118_out, F13);
  not not_119 (not_119_out, OP6);
  not not_120 (not_120_out, OP5);
  not not_121 (not_121_out, OP3);
  not not_122 (not_122_out, OP2);
  not not_123 (not_123_out, F30);
  not not_124 (not_124_out, F25);
  not not_125 (not_125_out, F13);
  not not_126 (not_126_out, OP6);
  not not_127 (not_127_out, OP3);
  not not_128 (not_128_out, OP2);
  not not_129 (not_129_out, F30);
  not not_130 (not_130_out, F25);
  not not_131 (not_131_out, F14);
  not not_132 (not_132_out, F13);
  not not_133 (not_133_out, F12);
  not not_134 (not_134_out, OP6);
  not not_135 (not_135_out, OP3);
  not not_136 (not_136_out, OP2);
  not not_137 (not_137_out, F25);
  not not_138 (not_138_out, F14);
  not not_139 (not_139_out, F13);
  not not_140 (not_140_out, F12);
  not not_141 (not_141_out, OP6);
  not not_142 (not_142_out, OP3);
  not not_143 (not_143_out, OP2);
  not not_144 (not_144_out, F30);
  not not_145 (not_145_out, F25);
  not not_146 (not_146_out, OP6);
  not not_147 (not_147_out, OP3);
  not not_148 (not_148_out, OP2);
  not not_149 (not_149_out, F30);
  not not_150 (not_150_out, F25);
  not not_151 (not_151_out, F14);
  not not_152 (not_152_out, OP6);
  not not_153 (not_153_out, OP3);
  not not_154 (not_154_out, OP2);
  not not_155 (not_155_out, F14);
  not not_156 (not_156_out, F13);
  not not_157 (not_157_out, F12);
  not not_158 (not_158_out, OP6);
  not not_159 (not_159_out, OP5);
  not not_160 (not_160_out, OP3);
  not not_161 (not_161_out, OP2);
  not not_162 (not_162_out, OP6);
  not not_163 (not_163_out, OP5);
  not not_164 (not_164_out, OP3);
  not not_165 (not_165_out, OP2);
  not not_166 (not_166_out, F14);
  not not_167 (not_167_out, F12);
  not not_168 (not_168_out, OP6);
  not not_169 (not_169_out, OP5);
  not not_170 (not_170_out, OP4);
  not not_171 (not_171_out, OP3);
  not not_172 (not_172_out, OP2);
  not not_173 (not_173_out, F14);
  not not_174 (not_174_out, F12);
  not not_175 (not_175_out, OP6);
  not not_176 (not_176_out, OP4);
  not not_177 (not_177_out, OP3);
  not not_178 (not_178_out, OP2);
  not not_179 (not_179_out, F14);
  not not_180 (not_180_out, F13);
  not not_181 (not_181_out, F12);
  not not_182 (not_182_out, OP4);
  not not_183 (not_183_out, OP3);
  not not_184 (not_184_out, OP2);
  not not_185 (not_185_out, F14);
  not not_186 (not_186_out, F13);
  not not_187 (not_187_out, OP4);
  not not_188 (not_188_out, OP3);
  not not_189 (not_189_out, OP2);
  not not_190 (not_190_out, F14);
  not not_191 (not_191_out, F13);
  not not_192 (not_192_out, F12);
  not not_193 (not_193_out, OP4);
  not not_194 (not_194_out, OP3);
  not not_195 (not_195_out, F14);
  not not_196 (not_196_out, F13);
  not not_197 (not_197_out, F12);
  not not_198 (not_198_out, OP6);
  not not_199 (not_199_out, OP5);
  not not_200 (not_200_out, OP4);
  not not_201 (not_201_out, OP3);
  not not_202 (not_202_out, OP2);
  not not_203 (not_203_out, OP4);
  not not_204 (not_204_out, OP3);
  not not_205 (not_205_out, OP2);
  not not_206 (not_206_out, F30);
  not not_207 (not_207_out, F25);
  not not_208 (not_208_out, F12);
  not not_209 (not_209_out, OP6);
  not not_210 (not_210_out, OP3);
  not not_211 (not_211_out, OP2);
  not not_212 (not_212_out, F30);
  not not_213 (not_213_out, F25);
  not not_214 (not_214_out, F14);
  not not_215 (not_215_out, F12);
  not not_216 (not_216_out, OP6);
  not not_217 (not_217_out, OP3);
  not not_218 (not_218_out, OP2);
  not not_219 (not_219_out, F30);
  not not_220 (not_220_out, F25);
  not not_221 (not_221_out, F14);
  not not_222 (not_222_out, OP6);
  not not_223 (not_223_out, OP3);
  not not_224 (not_224_out, OP2);
  not not_225 (not_225_out, F12);
  not not_226 (not_226_out, OP6);
  not not_227 (not_227_out, OP5);
  not not_228 (not_228_out, OP3);
  not not_229 (not_229_out, OP2);
  not not_230 (not_230_out, F13);
  not not_231 (not_231_out, F12);
  not not_232 (not_232_out, OP6);
  not not_233 (not_233_out, OP5);
  not not_234 (not_234_out, OP3);
  not not_235 (not_235_out, OP2);
  not not_236 (not_236_out, F14);
  not not_237 (not_237_out, F12);
  not not_238 (not_238_out, OP6);
  not not_239 (not_239_out, OP5);
  not not_240 (not_240_out, OP3);
  not not_241 (not_241_out, OP2);
  not not_242 (not_242_out, OP4);
  not not_243 (not_243_out, OP3);
  not not_244 (not_244_out, OP2);
  and and_1 (and_1_out, not_1_out, not_2_out, not_3_out, not_4_out, not_5_out, not_6_out, OP5, OP4, not_7_out, not_8_out);
  and and_2 (and_2_out, not_9_out, not_10_out, F14, F13, F12, not_11_out, OP5, OP4, not_12_out, not_13_out);
  and and_3 (and_3_out, not_14_out, not_15_out, not_16_out, F13, not_17_out, not_18_out, OP5, OP4, not_19_out, not_20_out);
  and and_4 (and_4_out, not_21_out, not_22_out, not_23_out, not_24_out, not_25_out, OP4, not_26_out, not_27_out);
  and and_5 (and_5_out, F14, F13, F12, not_28_out, not_29_out, OP4, not_30_out, not_31_out);
  and and_6 (and_6_out, F14, not_32_out, not_33_out, not_34_out, not_35_out, OP4, not_36_out, not_37_out);
  and and_7 (and_7_out, not_38_out, F13, not_39_out, not_40_out, not_41_out, OP4, not_42_out, not_43_out);
  and and_8 (and_8_out, F30, not_44_out, F14, not_45_out, F12, not_46_out, not_47_out, OP4, not_48_out, not_49_out);
  and and_9 (and_9_out, not_50_out, F13, not_51_out, not_52_out, not_53_out, not_54_out, not_55_out, not_56_out);
  and and_10 (and_10_out, not_57_out, F13, not_58_out, not_59_out, OP5, not_60_out, not_61_out, not_62_out);
  and and_11 (and_11_out, not_63_out, not_64_out, not_65_out, OP6, OP5, not_66_out, not_67_out, not_68_out);
  and and_12 (and_12_out, not_69_out, not_70_out, F12, OP6, OP5, not_71_out, not_72_out, not_73_out);
  and and_13 (and_13_out, not_74_out, not_75_out, not_76_out, OP6, OP5, not_77_out, not_78_out, OP2);
  and and_14 (and_14_out, not_79_out, not_80_out, not_81_out, not_82_out, not_83_out, not_84_out, not_85_out, not_86_out);
  and and_15 (and_15_out, F30, not_87_out, not_88_out, not_89_out, not_90_out, not_91_out, OP5, OP4, not_92_out, not_93_out);
  and and_16 (and_16_out, not_94_out, not_95_out, F14, F13, F12, not_96_out, OP5, OP4, not_97_out, not_98_out);
  and and_17 (and_17_out, not_99_out, not_100_out, not_101_out, F13, not_102_out, not_103_out, OP5, OP4, not_104_out, not_105_out);
  and and_18 (and_18_out, F14, F13, F12, not_106_out, not_107_out, OP4, not_108_out, not_109_out);
  and and_19 (and_19_out, not_110_out, F13, not_111_out, not_112_out, not_113_out, OP4, not_114_out, not_115_out);
  and and_20 (and_20_out, not_116_out, not_117_out, F14, not_118_out, F12, not_119_out, not_120_out, OP4, not_121_out, not_122_out);
  and and_21 (and_21_out, not_123_out, not_124_out, F14, not_125_out, F12, not_126_out, OP5, OP4, not_127_out, not_128_out);
  and and_22 (and_22_out, not_129_out, not_130_out, not_131_out, not_132_out, not_133_out, not_134_out, OP5, OP4, not_135_out, not_136_out);
  and and_23 (and_23_out, F30, not_137_out, not_138_out, not_139_out, not_140_out, not_141_out, OP5, OP4, not_142_out, not_143_out);
  and and_24 (and_24_out, not_144_out, not_145_out, F14, F13, F12, not_146_out, OP5, OP4, not_147_out, not_148_out);
  and and_25 (and_25_out, not_149_out, not_150_out, not_151_out, F13, F12, not_152_out, OP5, OP4, not_153_out, not_154_out);
  and and_26 (and_26_out, not_155_out, not_156_out, not_157_out, not_158_out, not_159_out, OP4, not_160_out, not_161_out);
  and and_27 (and_27_out, F14, F13, F12, not_162_out, not_163_out, OP4, not_164_out, not_165_out);
  and and_28 (and_28_out, not_166_out, F13, not_167_out, not_168_out, not_169_out, not_170_out, not_171_out, not_172_out);
  and and_29 (and_29_out, not_173_out, F13, not_174_out, not_175_out, OP5, not_176_out, not_177_out, not_178_out);
  and and_30 (and_30_out, not_179_out, not_180_out, not_181_out, OP6, OP5, not_182_out, not_183_out, not_184_out);
  and and_31 (and_31_out, not_185_out, not_186_out, F12, OP6, OP5, not_187_out, not_188_out, not_189_out);
  and and_32 (and_32_out, not_190_out, not_191_out, not_192_out, OP6, OP5, not_193_out, not_194_out, OP2);
  and and_33 (and_33_out, not_195_out, not_196_out, not_197_out, not_198_out, not_199_out, not_200_out, not_201_out, not_202_out);
  and and_34 (and_34_out, F14, F13, F12, OP6, OP5, not_203_out, not_204_out, not_205_out);
  and and_35 (and_35_out, not_206_out, not_207_out, F14, F13, not_208_out, not_209_out, OP5, OP4, not_210_out, not_211_out);
  and and_36 (and_36_out, not_212_out, not_213_out, not_214_out, F13, not_215_out, not_216_out, OP5, OP4, not_217_out, not_218_out);
  and and_37 (and_37_out, not_219_out, not_220_out, not_221_out, F13, F12, not_222_out, OP5, OP4, not_223_out, not_224_out);
  and and_38 (and_38_out, F14, F13, not_225_out, not_226_out, not_227_out, OP4, not_228_out, not_229_out);
  and and_39 (and_39_out, F14, not_230_out, not_231_out, not_232_out, not_233_out, OP4, not_234_out, not_235_out);
  and and_40 (and_40_out, not_236_out, F13, not_237_out, not_238_out, not_239_out, OP4, not_240_out, not_241_out);
  and and_41 (and_41_out, F14, F13, F12, OP6, OP5, not_242_out, not_243_out, not_244_out);
  or or_1 (S0, and_1_out, and_2_out, and_3_out, and_4_out, and_5_out, and_6_out, and_7_out, and_8_out, and_9_out, and_10_out, and_11_out, and_12_out, and_13_out, and_14_out);
  or or_2 (S1, and_15_out, and_16_out, and_17_out, and_18_out, and_19_out, and_20_out, and_21_out);
  or or_3 (S2, and_22_out, and_23_out, and_24_out, and_25_out, and_26_out, and_27_out, and_28_out, and_29_out, and_30_out, and_31_out, and_32_out, and_33_out, and_34_out);
  or or_4 (S3, and_35_out, and_36_out, and_37_out, and_38_out, and_39_out, and_40_out, and_41_out);
endmodule

module \控制信号自动生成_CCAB  (
  input  OP2,
  input  OP3,
  input  OP4,
  input  OP5,
  input  OP6,
  input  F12,
  input  F13,
  input  F14,
  input  F25,
  input  F30,
  output MemToReg,
  output MemWrite,
  output ALU_SRC,
  output RegWrite,
  output ecall,
  output S_Type,
  output BEQ,
  output BNE,
  output JALR,
  output JAL,
  output BGEU,
  output lb,
  output csrrsi,
  output csrrci
);

  wire and_1_out, and_2_out, and_4_out, and_5_out, and_6_out, and_7_out, and_8_out, and_9_out, and_10_out,
       and_11_out, and_12_out, and_13_out, and_14_out, and_15_out, and_16_out, and_17_out, and_18_out,
       and_19_out, and_20_out, not_1_out, not_2_out, not_3_out, not_4_out, not_5_out, not_6_out, not_7_out,
       not_8_out, not_9_out, not_10_out, not_11_out, not_12_out, not_13_out, not_14_out, not_15_out,
       not_16_out, not_17_out, not_18_out, not_19_out, not_20_out, not_21_out, not_22_out, not_23_out,
       not_24_out, not_25_out, not_26_out, not_27_out, not_28_out, not_29_out, not_30_out, not_31_out,
       not_32_out, not_33_out, not_34_out, not_35_out, not_36_out, not_37_out, not_38_out, not_39_out,
       not_40_out, not_41_out, not_42_out, not_43_out, not_44_out, not_45_out, not_46_out, not_47_out,
       not_48_out, not_49_out, not_50_out, not_51_out, not_52_out, not_53_out, not_54_out, not_55_out,
       not_56_out, not_57_out, not_58_out, not_59_out, not_60_out, not_61_out, not_62_out, not_63_out,
       not_64_out, not_65_out, not_66_out, not_67_out, not_68_out, not_69_out, not_70_out, not_71_out,
       not_72_out, not_73_out, not_74_out, not_75_out, not_76_out, not_77_out, not_78_out, not_79_out,
       not_80_out, not_81_out, not_82_out, not_83_out, not_84_out, not_85_out, not_86_out, not_87_out,
       not_88_out, not_89_out, not_90_out, not_91_out, not_92_out, not_93_out, not_94_out, not_95_out,
       not_96_out, not_97_out, not_98_out, not_99_out, not_100_out, not_101_out, not_102_out, not_103_out,
       not_104_out, not_105_out, not_106_out, not_107_out, not_108_out, not_109_out, not_110_out,
       not_111_out, not_112_out, not_113_out, not_114_out, not_115_out, not_116_out, not_117_out,
       not_118_out, not_119_out, not_120_out, not_121_out, not_122_out, not_123_out, not_124_out,
       not_125_out, not_126_out, not_127_out, not_128_out, not_129_out, not_130_out, not_131_out,
       not_132_out, not_133_out, not_134_out, not_135_out, not_136_out, not_137_out, not_138_out,
       not_139_out, not_140_out, not_141_out, not_142_out;

  not not_1 (not_1_out, F14);
  not not_2 (not_2_out, F12);
  not not_3 (not_3_out, OP6);
  not not_4 (not_4_out, OP5);
  not not_5 (not_5_out, OP4);
  not not_6 (not_6_out, OP3);
  not not_7 (not_7_out, OP2);
  not not_8 (not_8_out, F14);
  not not_9 (not_9_out, F13);
  not not_10 (not_10_out, F12);
  not not_11 (not_11_out, OP6);
  not not_12 (not_12_out, OP5);
  not not_13 (not_13_out, OP4);
  not not_14 (not_14_out, OP3);
  not not_15 (not_15_out, OP2);
  not not_16 (not_16_out, OP2);
  not not_17 (not_17_out, OP3);
  not not_18 (not_18_out, OP4);
  not not_19 (not_19_out, OP6);
  not not_20 (not_20_out, F12);
  not not_21 (not_21_out, F14);
  not not_22 (not_22_out, OP2);
  not not_23 (not_23_out, OP3);
  not not_24 (not_24_out, OP5);
  not not_25 (not_25_out, OP6);
  not not_26 (not_26_out, F12);
  not not_27 (not_27_out, F14);
  not not_28 (not_28_out, OP2);
  not not_29 (not_29_out, OP3);
  not not_30 (not_30_out, OP4);
  not not_31 (not_31_out, OP6);
  not not_32 (not_32_out, F12);
  not not_33 (not_33_out, F14);
  not not_34 (not_34_out, OP2);
  not not_35 (not_35_out, OP3);
  not not_36 (not_36_out, OP5);
  not not_37 (not_37_out, OP6);
  not not_38 (not_38_out, F12);
  not not_39 (not_39_out, OP2);
  not not_40 (not_40_out, OP3);
  not not_41 (not_41_out, OP5);
  not not_42 (not_42_out, OP6);
  not not_43 (not_43_out, F13);
  not not_44 (not_44_out, F14);
  not not_45 (not_45_out, OP2);
  not not_46 (not_46_out, OP3);
  not not_47 (not_47_out, OP5);
  not not_48 (not_48_out, OP6);
  not not_49 (not_49_out, F13);
  not not_50 (not_50_out, F25);
  not not_51 (not_51_out, OP2);
  not not_52 (not_52_out, OP3);
  not not_53 (not_53_out, OP5);
  not not_54 (not_54_out, OP6);
  not not_55 (not_55_out, OP3);
  not not_56 (not_56_out, OP4);
  not not_57 (not_57_out, F12);
  not not_58 (not_58_out, F13);
  not not_59 (not_59_out, F14);
  not not_60 (not_60_out, OP2);
  not not_61 (not_61_out, OP3);
  not not_62 (not_62_out, OP5);
  not not_63 (not_63_out, OP6);
  not not_64 (not_64_out, F12);
  not not_65 (not_65_out, F14);
  not not_66 (not_66_out, OP2);
  not not_67 (not_67_out, OP3);
  not not_68 (not_68_out, OP5);
  not not_69 (not_69_out, OP6);
  not not_70 (not_70_out, F12);
  not not_71 (not_71_out, OP2);
  not not_72 (not_72_out, OP3);
  not not_73 (not_73_out, OP5);
  not not_74 (not_74_out, OP6);
  not not_75 (not_75_out, F13);
  not not_76 (not_76_out, F14);
  not not_77 (not_77_out, OP2);
  not not_78 (not_78_out, OP3);
  not not_79 (not_79_out, OP5);
  not not_80 (not_80_out, OP6);
  not not_81 (not_81_out, F13);
  not not_82 (not_82_out, F25);
  not not_83 (not_83_out, OP2);
  not not_84 (not_84_out, OP3);
  not not_85 (not_85_out, OP6);
  not not_86 (not_86_out, F12);
  not not_87 (not_87_out, F13);
  not not_88 (not_88_out, F14);
  not not_89 (not_89_out, F25);
  not not_90 (not_90_out, OP2);
  not not_91 (not_91_out, OP3);
  not not_92 (not_92_out, OP6);
  not not_93 (not_93_out, F12);
  not not_94 (not_94_out, F25);
  not not_95 (not_95_out, F30);
  not not_96 (not_96_out, OP2);
  not not_97 (not_97_out, OP3);
  not not_98 (not_98_out, OP5);
  not not_99 (not_99_out, OP6);
  not not_100 (not_100_out, OP2);
  not not_101 (not_101_out, OP3);
  not not_102 (not_102_out, OP6);
  not not_103 (not_103_out, F25);
  not not_104 (not_104_out, F30);
  not not_105 (not_105_out, OP4);
  not not_106 (not_106_out, F12);
  not not_107 (not_107_out, F13);
  not not_108 (not_108_out, F14);
  not not_109 (not_109_out, OP4);
  not not_110 (not_110_out, OP2);
  not not_111 (not_111_out, OP3);
  not not_112 (not_112_out, F12);
  not not_113 (not_113_out, F13);
  not not_114 (not_114_out, F14);
  not not_115 (not_115_out, F25);
  not not_116 (not_116_out, F30);
  not not_117 (not_117_out, OP2);
  not not_118 (not_118_out, OP3);
  not not_119 (not_119_out, OP4);
  not not_120 (not_120_out, OP6);
  not not_121 (not_121_out, F12);
  not not_122 (not_122_out, F14);
  not not_123 (not_123_out, OP2);
  not not_124 (not_124_out, OP3);
  not not_125 (not_125_out, OP4);
  not not_126 (not_126_out, F12);
  not not_127 (not_127_out, F13);
  not not_128 (not_128_out, F14);
  not not_129 (not_129_out, OP2);
  not not_130 (not_130_out, OP3);
  not not_131 (not_131_out, OP4);
  not not_132 (not_132_out, F13);
  not not_133 (not_133_out, F14);
  not not_134 (not_134_out, OP3);
  not not_135 (not_135_out, OP4);
  not not_136 (not_136_out, F12);
  not not_137 (not_137_out, F13);
  not not_138 (not_138_out, F14);
  not not_139 (not_139_out, OP4);
  not not_140 (not_140_out, OP2);
  not not_141 (not_141_out, OP3);
  not not_142 (not_142_out, OP4);
  and and_1 (and_1_out, not_1_out, F13, not_2_out, not_3_out, not_4_out, not_5_out, not_6_out, not_7_out);
  and and_2 (and_2_out, not_8_out, not_9_out, not_10_out, not_11_out, not_12_out, not_13_out, not_14_out, not_15_out);
  and and_3 (MemWrite, not_16_out, not_17_out, not_18_out, OP5, not_19_out, not_20_out, F13, not_21_out);
  and and_4 (and_4_out, not_22_out, not_23_out, not_24_out, not_25_out, not_26_out, not_27_out);
  and and_5 (and_5_out, not_28_out, not_29_out, not_30_out, not_31_out, not_32_out, F13, not_33_out);
  and and_6 (and_6_out, not_34_out, not_35_out, OP4, not_36_out, not_37_out, not_38_out);
  and and_7 (and_7_out, not_39_out, not_40_out, OP4, not_41_out, not_42_out, not_43_out, not_44_out);
  and and_8 (and_8_out, not_45_out, not_46_out, OP4, not_47_out, not_48_out, not_49_out, not_50_out);
  and and_9 (and_9_out, not_51_out, not_52_out, OP4, not_53_out, not_54_out, F13, F14);
  and and_10 (and_10_out, OP2, not_55_out, not_56_out, OP5, OP6, not_57_out, not_58_out, not_59_out);
  and and_11 (and_11_out, not_60_out, not_61_out, not_62_out, not_63_out, not_64_out, not_65_out);
  and and_12 (and_12_out, not_66_out, not_67_out, OP4, not_68_out, not_69_out, not_70_out);
  and and_13 (and_13_out, not_71_out, not_72_out, OP4, not_73_out, not_74_out, not_75_out, not_76_out);
  and and_14 (and_14_out, not_77_out, not_78_out, OP4, not_79_out, not_80_out, not_81_out, not_82_out);
  and and_15 (and_15_out, not_83_out, not_84_out, OP4, not_85_out, not_86_out, not_87_out, not_88_out, not_89_out);
  and and_16 (and_16_out, not_90_out, not_91_out, OP4, not_92_out, not_93_out, F13, not_94_out, not_95_out);
  and and_17 (and_17_out, not_96_out, not_97_out, OP4, not_98_out, not_99_out, F13, F14);
  and and_18 (and_18_out, not_100_out, not_101_out, OP4, OP5, not_102_out, F12, not_103_out, not_104_out);
  and and_19 (and_19_out, OP2, not_105_out, OP5, OP6, not_106_out, not_107_out, not_108_out);
  and and_20 (and_20_out, OP2, OP3, not_109_out, OP5, OP6);
  and and_21 (ecall, not_110_out, not_111_out, OP4, OP5, OP6, not_112_out, not_113_out, not_114_out, not_115_out, not_116_out);
  and and_22 (S_Type, not_117_out, not_118_out, not_119_out, OP5, not_120_out, not_121_out, F13, not_122_out);
  and and_23 (BEQ, not_123_out, not_124_out, not_125_out, OP5, OP6, not_126_out, not_127_out, not_128_out);
  and and_24 (BNE, not_129_out, not_130_out, not_131_out, OP5, OP6, F12, not_132_out, not_133_out);
  and and_25 (JALR, OP2, not_134_out, not_135_out, OP5, OP6, not_136_out, not_137_out, not_138_out);
  and and_26 (JAL, OP2, OP3, not_139_out, OP5, OP6);
  and and_27 (BGEU, not_140_out, not_141_out, not_142_out, OP5, OP6, F12, F13, F14);
  and and_28 (csrrsi, ~OP2, ~OP3, OP4, OP5, OP6, ~F12, F13, F14);  // AND_Gate
  and and_29 (csrrci, ~OP2, ~OP3, OP4, OP5, OP6, F12, F13, F14);  // AND_Gate
  or or_1 (MemToReg, and_1_out, and_2_out);
  or or_2 (ALU_SRC, and_4_out, and_5_out, and_6_out, and_7_out, and_8_out, and_9_out, and_10_out);
  and and_30 (lb, ~OP2, ~OP3, ~OP4, ~OP5, ~OP6, ~F12, ~F13, ~F14);  // AND_Gate
  or or_3 (RegWrite, and_11_out, and_12_out, and_13_out, and_14_out, and_15_out, and_16_out, and_17_out, and_18_out, and_19_out, and_20_out);
endmodule

// ALU
module ALU (
  input  [31:0] X,
  input  [31:0] Y,
  input  [3:0] AluOP,
  output out_4,
  output Equal,
  output out_6,
  output [31:0] Result,
  output [31:0] Result_2
);

  wire [0:0] comparator_1_lt, comparator_2_lt;
  wire [31:0] adder_1_out, AND_out, divider_1_out, divider_1_rem, multiplier_1_cout, multiplier_1_out,
       NOR_out, OR_out, shifter_1_out, shifter_2_out, shifter_3_out, subtractor_1_out, XOR_out;

  assign AND_out = X & Y;  // AND_Gate AND, 32 bits wide
  assign OR_out = X | Y;  // OR_Gate OR, 32 bits wide
  Shifter #(.width(32), .shift("ll")) shifter_1 (.in(X), .\dist (Y[4:0]), .out(shifter_1_out));
  Shifter #(.width(32), .shift("ar")) shifter_2 (.in(X), .\dist (Y[4:0]), .out(shifter_2_out));
  Shifter #(.width(32), .shift("lr")) shifter_3 (.in(X), .\dist (Y[4:0]), .out(shifter_3_out));
  Multiplier #(.width(32)) multiplier_1 (.a(X), .b(Y), .out(multiplier_1_out), .cout(multiplier_1_cout));  // open: cin
  Divider #(.width(32)) divider_1 (.a(X), .b(Y), .out(divider_1_out), .rem(divider_1_rem));  // open: upper
  Adder #(.width(32)) adder_1 (.a(X), .b(Y), .out(adder_1_out));  // open: cin, cout
  Subtractor #(.width(32)) subtractor_1 (.a(X), .b(Y), .out(subtractor_1_out));  // open: bin, bout
  assign XOR_out = X ^ Y;  // XOR_Gate XOR, 32 bits wide
  assign NOR_out = ~(X | Y);  // NOR_Gate NOR, 32 bits wide
  Comparator #(.width(32), .mode("twosComplement")) comparator_1 (
    .a(X), .b(Y), .eq(Equal), .lt(comparator_1_lt[0]));  // open: gt
  Comparator #(.width(32), .mode("unsigned")) comparator_2 (.a(X), .b(Y), .lt(comparator_2_lt[0]));  // open: gt, eq
  Multiplexer #(.select(4), .width(32), .disabled("Z"), .enable("false")) multiplexer_1 (
    .in0(shifter_1_out), .in1(shifter_2_out), .in2(shifter_3_out), .in3(multiplier_1_out),
    .in4(divider_1_out), .in5(adder_1_out), .in6(subtractor_1_out), .in7(AND_out), .in8(OR_out),
    .in9(XOR_out), .in10(NOR_out), .in11({{31{1'b0}}, comparator_1_lt[0]}),
    .in12({{31{1'b0}}, comparator_2_lt[0]}), .in13({32{1'b0}}), .in14({32{1'b0}}), .in15({32{1'b0}}),
    .out(Result), .sel(AluOP));
  Multiplexer #(.select(4), .width(32), .disabled("Z"), .enable("false")) multiplexer_2 (
    .in0({32{1'b0}}), .in1({32{1'b0}}), .in2({32{1'b0}}), .in3(multiplier_1_cout), .in4(divider_1_rem),
    .in5({32{1'b0}}), .in6({32{1'b0}}), .in7({32{1'b0}}), .in8({32{1'b0}}), .in9({32{1'b0}}),
    .in10({32{1'b0}}), .in11({32{1'b0}}), .in12({32{1'b0}}), .in13({32{1'b0}}), .in14({32{1'b0}}),
    .in15({32{1'b0}}), .out(Result_2), .sel(AluOP));
  Multiplexer #(.select(4), .width(1), .disabled("Z"), .enable("false")) multiplexer_3 (
    .in0(1'b0), .in1(1'b0), .in2(1'b0), .in3(1'b0), .in4(1'b0), .in5(1'b0), .in6(1'b0), .in7(1'b0),
    .in8(1'b0), .in9(1'b0), .in10(1'b0), .in11(comparator_1_lt[0]), .in12(comparator_2_lt[0]), .in13(1'b0),
    .in14(1'b0), .in15(1'b0), .out(out_6), .sel(AluOP));
  not not_1 (out_4, out_6);

  // Other names for the same wires on the sheet: Result2[31:0] = Result_2; S[3:0] = AluOP; tunnel = out_6;
  //   tunnel_t = out_4

  // Notes on the sheet:
  //   不要改变此引脚区域内容，也不要改变ALU封装形式
  //   输入引脚
  //   输出引脚
endmodule

module Regifile (
  input  [31:0] Din,
  input  Clk,
  input  WE,
  input  [4:0] R1_num,
  input  [4:0] W_num,
  input  [4:0] R2_num,
  output [31:0] R1,
  output [31:0] R2
);

  // RegisterFile registerfile_1: pin names not known; wires that end beside it: Din, Clk, WE, W_num, R1_num, R2_num, R1, R2
endmodule

module \气泡流水线  (
  output RegWrite,
  output MemWrite,
  output [31:0] IF_PC,
  output [31:0] ID_PC,
  output [31:0] EX_PC,
  output [31:0] M_PC,
  output [31:0] WB_PC,
  output [31:0] RDin,
  output [31:0] MDin,
  output [31:0] LedData
);

  wire alu_1_equal, alu_1_out_4, AluSrcB, and_1_out, and_3_out, and_4_out, and_5_out, and_6_out, and_7_out,
       Beq, Bgeu, Bne, CLK, clock_1_out, clock_2_out, comparator_1_eq, comparator_2_eq, comparator_2_lt,
       d_ff_1_q, ecall, EX_MEM_jal_2, EX_MEM_jalr_2, EX_MEM_lb_2, EX_MEM_memtoreg_2, EX_MEM_regwrite_2,
       Flush, Go, halt, ID_EX_alusrc_2, ID_EX_beq_2, ID_EX_bgeu_2, ID_EX_bne_2, ID_EX_jal_2, ID_EX_jalr_2,
       ID_EX_lb_2, ID_EX_memtoreg_2, ID_EX_memwrite_2, ID_EX_regwrite_2, JAL, JALR, lb, MEM_WB_memtoreg_2,
       MemToReg, MemWrite_t, nand_1_out, not_1_out, not_2_out, not_3_out, not_4_out, not_5_out, not_6_out,
       not_7_out, not_8_out, or_1_out, or_2_out, or_3_out, or_4_out, RegWrite_t, RST, S_type, Stall,
       undriven, WB_JAL, WB_JALR, \单周期硬布线控制器_1_uret ;
  wire [3:0] AluOP, ID_EX_aluop_2;
  wire [4:0] EX_MEM_writereg_num_2, ID_EX_writereg_num_2, MEM_WB_writereg_num_2, multiplexer_3_out,
       multiplexer_4_out;
  wire [12:0] CNT_num;
  wire [15:0] \分支跳转次数 , \总周期数 , \插入气泡数 ;
  wire [31:0] adder_1_out, adder_2_out, alu_1_result, EX_IR, EX_MEM_aluresult_2, EX_MEM_pc_4_2, ID_EX_pc_4_2,
       ID_EX_r1_2, ID_EX_r2_2, ID_EX_signimm_2, ID_IR, IF_ID_pc_4_2, IF_IR, ImmGen_imm, \l指令分线器_1_imm32_2 ,
       MEM_IR, MEM_WB_aluresult_2, MEM_WB_pc_4_2, MEM_WB_readdata_2, multiplexer_1_out, multiplexer_2_out,
       multiplexer_6_out, multiplexer_7_out, R1, R2, ram_1_data, shifter_1_out, WB_IR;

  Button \u_总复位  (.out(RST));
  // Probe on \总周期数 
  // Probe on \总周期数 
  Button \u_继续运行  (.out(Go));
  Multiplexer #(.select(1), .width(32), .disabled("Z"), .enable("false")) multiplexer_1 (
    .in0(adder_2_out), .in1({alu_1_result[31:1], 1'b0}), .out(multiplexer_1_out), .sel(ID_EX_jalr_2));
  Hex_Digit_Display hex_digit_display_1 (.value(LedData[31:28]));  // open: dp
  // Probe on IF_PC[19:0]
  // RiscV_Probe riscv_probe_1: pin names not known; wires that end beside it: IF_IR
  Multiplexer #(.select(1), .width(32), .disabled("Z"), .enable("false")) multiplexer_2 (
    .in0(adder_1_out), .in1(multiplexer_1_out), .out(multiplexer_2_out), .sel(or_4_out));
  Hex_Digit_Display hex_digit_display_2 (.value(LedData[23:20]));  // open: dp
  Hex_Digit_Display hex_digit_display_3 (.value(LedData[27:24]));  // open: dp
  // Probe on ID_PC[19:0]
  // RiscV_Probe riscv_probe_2: pin names not known; wires that end beside it: ID_IR
  Register #(.width(32), .trigger("rising"), .Select("low")) PC (
    .D(multiplexer_2_out), .en(not_1_out), .Q(IF_PC), .clk(CLK), .clr(RST));
  not not_1 (not_1_out, or_1_out);
  or or_1 (or_1_out, halt, Stall);
  Hex_Digit_Display hex_digit_display_4 (.value(LedData[19:16]));  // open: dp
  Hex_Digit_Display hex_digit_display_5 (.value(LedData[15:12]));  // open: dp
  Hex_Digit_Display hex_digit_display_6 (.value(LedData[7:4]));  // open: dp
  Hex_Digit_Display hex_digit_display_7 (.value(LedData[11:8]));  // open: dp
  Clock #(.highDuration(1), .lowDuration(1)) clock_1 (.out(clock_1_out));
  // Probe on EX_PC[19:0]
  // RiscV_Probe riscv_probe_3: pin names not known; wires that end beside it: clock_1_out, EX_IR, CLK
  Hex_Digit_Display hex_digit_display_8 (.value(LedData[3:0]));  // open: dp
  ROM #(.addrWidth(10), .dataWidth(32), .Select("high")) rom_1 (.addr(IF_PC[11:2]), .data(IF_IR));
  Adder #(.width(32)) adder_1 (.a(IF_PC), .b(32'h4), .out(adder_1_out));  // open: cin, cout
  // Probe on \总周期数 
  // Probe on M_PC[19:0]
  // RiscV_Probe riscv_probe_4: pin names not known; wires that end beside it: MEM_IR
  not not_2 (not_2_out, Flush);
  Comparator #(.width(32), .mode("twosComplement")) comparator_1 (
    .a(R1), .b(32'h22), .eq(comparator_1_eq));  // open: gt, lt
  // RiscV_Probe riscv_probe_5: pin names not known; wires that end beside it: 32'h4, ID_IR
  // Probe on \总周期数 
  // Probe on \分支跳转次数 
  // Probe on \插入气泡数 
  and and_1 (and_1_out, ecall, not_2_out, comparator_1_eq);
  not not_3 (not_3_out, comparator_1_eq);
  and and_2 (halt, not_3_out, ecall, not_4_out, not_5_out);
  not not_4 (not_4_out, Flush);
  not not_5 (not_5_out, Go);
  \相关处理逻辑  \u_相关处理逻辑_1  (
    .ID_IR(ID_IR), .EX_WriteReg_num(ID_EX_writereg_num_2), .EX_WriteReg(ID_EX_regwrite_2),
    .MEM_WriteReg_num(EX_MEM_writereg_num_2), .MEM_WriteReg(EX_MEM_regwrite_2), .BranchTaken(or_4_out),
    .Flush(Flush), .Stall(Stall));
  or or_2 (or_2_out, Stall, halt);
  not not_6 (not_6_out, or_2_out);
  IF_ID IF_ID (
    .IR(IF_IR), .PC_4(adder_1_out), .IR_2(ID_IR), .PC_4_2(IF_ID_pc_4_2), .CLK(CLK), .PC(IF_PC), .PC_2(ID_PC),
    .CLR(or_4_out), .EN(not_6_out));  // open: PredictJump, PredictJump_2
  // Probe on IF_PC[11:0]
  // Probe on WB_PC[19:0]
  // RiscV_Probe riscv_probe_6: pin names not known; wires that end beside it: WB_IR
  Register #(.width(32), .trigger("rising"), .Select("low")) register_1 (
    .D(R2), .en(and_1_out), .Q(LedData), .clk(CLK));  // open: clr
  // Probe on ID_PC[11:0]
  // Probe on EX_PC[11:0]
  // Probe on M_PC[11:0]
  D_Flip_Flop #(.trigger("high"), .Pre_Clr_Positions("LEGACY"), .NegatePresetClear("false"), .enable("true"), .NewFFLayout("false")) d_ff_1 (.Q(d_ff_1_q));  // open: clk, D, Qn, preset, en, reset
  // Probe on 13'he20
  \单周期硬布线控制器  \u_单周期硬布线控制器_1  (
    .Funct({ID_IR[30], ID_IR[25], ID_IR[14:12]}), .OP(ID_IR[6:2]), .ALU_OP(AluOP), .MemToReg(MemToReg),
    .MemWrite(MemWrite_t), .ALU_SRC(AluSrcB), .RegWrite(RegWrite_t), .ecall(ecall), .S_type(S_type),
    .Jalr(JALR), .Beq(Beq), .JAL(JAL), .Bne(Bne), .in_3(ID_IR[21]), .uret(\单周期硬布线控制器_1_uret ), .BGUE(Bgeu),
    .lb(lb));  // open: csrrsi, csrrci
  Multiplexer #(.select(1), .width(5), .disabled("Z"), .enable("false")) multiplexer_3 (
    .in0(ID_IR[19:15]), .in1(5'b10001), .out(multiplexer_3_out), .sel(ecall));
  Multiplexer #(.select(1), .width(5), .disabled("Z"), .enable("false")) multiplexer_4 (
    .in0(ID_IR[24:20]), .in1(5'b01010), .out(multiplexer_4_out), .sel(ecall));
  ImmGen ImmGen (
    .S_type(S_type), .Beq(Beq), .Bne(Bne), .JAL(JAL), .Imm12(ID_IR), .Imm_sw({ID_IR[31:25], ID_IR[11:7]}),
    .Imm_beq_bne_bgeu({ID_IR[31], ID_IR[7], ID_IR[30:25], ID_IR[11:8]}),
    .Imm_jal({ID_IR[31], ID_IR[19:12], ID_IR[20], ID_IR[30:21]}), .Imm(ImmGen_imm), .Bgeu(Bgeu));
  // Probe on WB_PC[11:0]
  Comparator #(.width(13), .mode("twosComplement")) comparator_2 (
    .a(CNT_num), .b(13'he20), .eq(comparator_2_eq), .lt(comparator_2_lt));  // open: gt
  Clock #(.highDuration(1), .lowDuration(1)) clock_2 (.out(clock_2_out));
  Multiplexer #(.select(1), .width(32), .disabled("Z"), .enable("false")) multiplexer_5 (
    .in0(multiplexer_7_out), .in1(MEM_WB_pc_4_2), .out(RDin), .sel(or_3_out));
  nand nand_1 (nand_1_out, d_ff_1_q, comparator_2_eq);
  Counter #(.width(13), .max('h1fff), .ongoal("stay"), .trigger("rising"), .behavior("old")) counter_1 (
    .count(comparator_2_lt), .Q(CNT_num), .clk(clock_2_out));  // open: load, D, carry, clr, preset
  or or_3 (or_3_out, WB_JAL, WB_JALR);
  assign CLK = nand_1_out ? clock_2_out : 1'bz;  // Controlled_Buffer controlled_buffer_1
  and and_3 (and_3_out, ~halt, nand_1_out);  // AND_Gate
  Counter #(.width(16), .max('hffff), .ongoal("wrap"), .trigger("rising"), .behavior("new")) counter_2 (
    .count(and_3_out), .Q(\总周期数 ), .clk(clock_2_out));  // open: load, D, carry, clr, preset, down
  not not_7 (not_7_out, CLK);
  Regifile regifile_1 (
    .Din(RDin), .Clk(not_7_out), .R1(R1), .R2(R2), .WE(RegWrite), .W_num(MEM_WB_writereg_num_2),
    .R1_num(multiplexer_3_out), .R2_num(multiplexer_4_out));
  Pull_Resistor #(.pull(1)) pull_resistor_1 (.node(CLK));
  ID_EX ID_EX (
    .RegWrite(RegWrite_t), .MemToReg(MemToReg), .MemWrite(MemWrite_t), .AluOP(AluOP), .Beq(Beq),
    .AluSrc(AluSrcB), .R1(R1), .R2(R2), .WriteReg_num(ID_IR[11:7]), .SignImm(ImmGen_imm), .CLK(CLK),
    .RegWrite_2(ID_EX_regwrite_2), .MemToReg_2(ID_EX_memtoreg_2), .MemWrite_2(ID_EX_memwrite_2),
    .AluOP_2(ID_EX_aluop_2), .Beq_2(ID_EX_beq_2), .AluSrc_2(ID_EX_alusrc_2), .R1_2(ID_EX_r1_2),
    .R2_2(ID_EX_r2_2), .WriteReg_num_2(ID_EX_writereg_num_2), .SignImm_2(ID_EX_signimm_2), .Bne(Bne),
    .Bne_2(ID_EX_bne_2), .PC(ID_PC), .PC_2(EX_PC), .IR(ID_IR), .IR_2(EX_IR), .CLR(Flush), .JAL(JAL),
    .JALR(JALR), .JAL_2(ID_EX_jal_2), .JALR_2(ID_EX_jalr_2), .PC_4(IF_ID_pc_4_2), .PC_4_2(ID_EX_pc_4_2),
    .halt(halt), .Bgeu(Bgeu), .Bgeu_2(ID_EX_bgeu_2), .lb(lb), .lb_2(ID_EX_lb_2));  // open: RsForward, RsForward_2, RtForward, RtForward_2, ecall, ecall_2, PredictJump, PredictJump_2, csrrsi, csrrrsi, csrrci, csrrrci, uret, uret_2
  Counter #(.width(16), .max('hffff), .ongoal("wrap"), .trigger("rising"), .behavior("new")) counter_3 (
    .count(Stall), .Q(\插入气泡数 ), .clk(CLK));  // open: load, D, carry, clr, preset, down
  Multiplexer #(.select(1), .width(32), .disabled("Z"), .enable("false")) multiplexer_6 (
    .in0(ID_EX_r2_2), .in1(ID_EX_signimm_2), .out(multiplexer_6_out), .sel(ID_EX_alusrc_2));
  Shifter #(.width(32), .shift("ll")) shifter_1 (.in(ID_EX_signimm_2), .\dist (5'b00001), .out(shifter_1_out));
  and and_4 (and_4_out, Flush, ~Stall);  // AND_Gate
  Counter #(.width(16), .max('hffff), .ongoal("wrap"), .trigger("rising"), .behavior("new")) counter_4 (
    .count(and_4_out), .Q(\分支跳转次数 ), .clk(CLK));  // open: load, D, carry, clr, preset, down
  ALU alu_1 (
    .X(ID_EX_r1_2), .Y(multiplexer_6_out), .AluOP(ID_EX_aluop_2), .Equal(alu_1_equal), .Result(alu_1_result),
    .out_4(alu_1_out_4));  // open: Result_2, out_6
  Adder #(.width(32)) adder_2 (.a(shifter_1_out), .b(EX_PC), .out(adder_2_out));  // open: cin, cout
  not not_8 (not_8_out, alu_1_equal);
  EX_MEM EX_MEM (
    .RegWrite(ID_EX_regwrite_2), .MemToReg(ID_EX_memtoreg_2), .MemWrite(ID_EX_memwrite_2),
    .AluResult(alu_1_result), .WriteData(ID_EX_r2_2), .WriteReg_num(ID_EX_writereg_num_2),
    .RegWrite_2(EX_MEM_regwrite_2), .MemToReg_2(EX_MEM_memtoreg_2), .MemWrite_2(MemWrite),
    .AluResult_2(EX_MEM_aluresult_2), .WriteData_2(MDin), .WriteReg_num_2(EX_MEM_writereg_num_2), .CLK(CLK),
    .PC(EX_PC), .PC_2(M_PC), .IR(EX_IR), .IR_2(MEM_IR), .JAL(ID_EX_jal_2), .JAL_2(EX_MEM_jal_2),
    .JALR(ID_EX_jalr_2), .JALR_2(EX_MEM_jalr_2), .PC_4(ID_EX_pc_4_2), .PC_4_2(EX_MEM_pc_4_2),
    .lb(ID_EX_lb_2), .lb_2(EX_MEM_lb_2), .URET(undriven));  // open: URET_2
  and and_5 (and_5_out, ID_EX_beq_2, alu_1_equal);
  and and_6 (and_6_out, ID_EX_bne_2, not_8_out);
  and and_7 (and_7_out, ID_EX_bgeu_2, alu_1_out_4);
  or or_4 (or_4_out, and_5_out, and_6_out, ID_EX_jal_2, ID_EX_jalr_2, and_7_out);
  RAM #(.addrWidth(10), .dataWidth(32), .bus("separate"), .Select("high")) ram_1 (
    .addr(EX_MEM_aluresult_2[11:2]), .din(MDin), .data(ram_1_data), .str(MemWrite), .clk(CLK));  // open: sel, ld, clr
  \L指令分线器  \l指令分线器_1  (
    .lb(EX_MEM_lb_2), .Imm32_2(\l指令分线器_1_imm32_2 ), .Imm32(ram_1_data), .offset(EX_MEM_aluresult_2[1:0]));
  MEM_WB MEM_WB (
    .RegWrite(EX_MEM_regwrite_2), .MemToReg(EX_MEM_memtoreg_2), .AluResult(EX_MEM_aluresult_2),
    .ReadData(\l指令分线器_1_imm32_2 ), .WriteReg_num(EX_MEM_writereg_num_2), .RegWrite_2(RegWrite),
    .MemToReg_2(MEM_WB_memtoreg_2), .AluResult_2(MEM_WB_aluresult_2), .ReadData_2(MEM_WB_readdata_2),
    .WriteReg_num_2(MEM_WB_writereg_num_2), .CLK(CLK), .PC(M_PC), .PC_2(WB_PC), .IR(MEM_IR), .IR_2(WB_IR),
    .JAL(EX_MEM_jal_2), .JALR(EX_MEM_jalr_2), .JAL_2(WB_JAL), .JALR_2(WB_JALR), .PC_4(EX_MEM_pc_4_2),
    .PC_4_2(MEM_WB_pc_4_2));
  Multiplexer #(.select(1), .width(32), .disabled("Z"), .enable("false")) multiplexer_7 (
    .in0(MEM_WB_aluresult_2), .in1(MEM_WB_readdata_2), .out(multiplexer_7_out), .sel(MEM_WB_memtoreg_2));

  // Other names for the same wires on the sheet: IR[31:0] = ID_IR; MEM_MemWrite = MemWrite; MEM_PC[31:0] = M_PC;
  //   PC[31:0] = IF_PC; WB_RegWrite = RegWrite

  // Notes on the sheet:
  //   时空图监测，可删除
  //   JALR
  //   BranchTaken
  //   数码管输出
  //   IF
  //   指令存储器
  //   contents of rom_1 (hex, n*v repeats v):
  //   100493 100006f 100493 200913 300993 100006f 100493 200913 300993 100006f 100493 200913 300993
  //   100006f 100493 200913 300993 3e0000ef 100413 100493 1f49493 900533 2200893 73 24d493 48463 fedff06f
  //   900533 2200893 73 100493 249493 900533 2200893 73 48463 fedff06f 100493 1f49493 900533 2200893 73
  //   4034d493 900533 2200893 73 4044d493 900533 2200893 73 4044d493 900533 2200893 73 4044d493 900533
  //   2200893 73 4044d493 900533 2200893 73 4044d493 900533 2200893 73 4044d493 900533 2200893 73 4044d493
  //   900533 2200893 73 100413 1f41993 41f9d993 433 c00913 300b13 140413 f47413 800293 100313 499993
  //   89e9b3 1300533 2200893 73 406282b3 fe0294e3 140413 f00f93 1f47433 1c41413 800293 100313 49d993
  //   89e9b3 1300533 2200893 73 406282b3 fe0294e3 1c45413 406b0b33 b0463 f95ff06f 2b3 fff2c293 829293
  //   ff2e293 500533 2200893 73 fff00413 493 84a023 140413 448493 84a023 140413 448493 84a023 140413
  //   448493 84a023 140413 448493 84a023 140413 448493 84a023 140413 448493 84a023 140413 448493 84a023
  //   140413 448493 84a023 140413 448493 84a023 140413 448493 84a023 140413 448493 84a023 140413 448493
  //   84a023 140413 448493 84a023 140413 448493 84a023 140413 448493 84a023 140413 448493 140413 433
  //   3c00493 42983 4aa03 149a2b3 28663 134a023 1442023 ffc48493 fe9412e3 800533 2200893 73 440413 3c00493
  //   fc9416e3 3200893 73 100293 300313 800493 849493 7648493 900533 2200893 73 800e13 5494b3 6494b3
  //   900533 2200893 73 fffe0e13 fe0e14e3 a00893 73 100293 300313 800493 849493 7648493 1449493 900533
  //   2200893 73 800e13 54d4b3 64d4b3 900533 2200893 73 fffe0e13 fe0e14e3 a00893 73 313 1000e13 8400493
  //   849493 8348493 400913 891913 490913 849493 8248493 849493 8148493 891913 490913 891913 490913 932023
  //   12484b3 430313 fffe0e13 fe0e18e3 2000e13 313 30483 900533 2200893 73 130313 fffe0e13 fe0e14e3 a00893
  //   73 f00493 100913 409909b3 900533 2200893 73 fff48493 ff29f6e3 a00893 73 a00893 73 413 140413 800533
  //   2200893 73 240413 800533 2200893 73 340413 800533 2200893 73 440413 800533 2200893 73 540413 800533
  //   2200893 73 640413 800533 2200893 73 740413 800533 2200893 73 840413 800533 2200893 2200893 73 8067
  //   PC+4
  //   指令探针
  //   为1则暂停
  //   ID.IR
  //   指令字
  //   控制位
  //   JAL
  //   JALR
  //   URET
  //   sw
  //   beq/bne
  //   jal
  //   流水调试日志用
  //   暂停节拍，不能为0
  //   Beq
  //   Bne
  //   AluOP
  //   AluSrcB
  //   RegWrite
  //   ID
  //   MemToReg
  //   MemWrite
  //   可计数暂停的时钟源
  //   SignImm
  //   PC+4
  //   Flush
  //   R1
  //   R2
  //   WriteReg#
  //   EX
  //   PC+SignImm
  //   EX.RegWrite
  //   RegWrite
  //   MemToReg
  //   WriteReg#
  //   EX.WriteReg#
  //   Beq
  //   Bne
  //   JAL
  //   JALR
  //   MemWrite
  //   AluResult
  //   WriteData
  //   PC+4
  //   BranchTaken
  //   BranchTaken
  //   数据存储器
  //   MEM.RegWrite
  //   MEM
  //   PC+4
  //   MEM.WriteReg#
  //   RegWrite
  //   MemToReg
  //   AluResult
  //   ReadData
  //   WriteReg#
  //   WB
endmodule
module \重定向流水线  (
  output RegWrite,
  output MemWrite,
  output [31:0] IF_PC,
  output [31:0] ID_PC,
  output [31:0] EX_PC,
  output [31:0] M_PC,
  output [31:0] WB_PC,
  output [31:0] RDin,
  output [31:0] MDin,
  output [31:0] LedData
);

  wire alu_1_equal, alu_1_out_4, AluSrcB, and_1_out, and_3_out, and_4_out, and_5_out, and_6_out, and_7_out,
       Beq, Bgeu, Bne, CLK, clock_1_out, comparator_1_eq, comparator_2_eq, comparator_2_lt, d_ff_1_q, ecall,
       EX_ecall, EX_MEM_jal_2, EX_MEM_jalr_2, EX_MEM_lb_2, EX_MEM_memtoreg_2, EX_MEM_regwrite_2, Flush, Go,
       halt, ID_EX_alusrc_2, ID_EX_beq_2, ID_EX_bgeu_2, ID_EX_bne_2, ID_EX_jal_2, ID_EX_jalr_2, ID_EX_lb_2,
       ID_EX_memtoreg_2, ID_EX_memwrite_2, ID_EX_regwrite_2, JAL, JALR, lb, MEM_WB_memtoreg_2, MemToReg,
       MemWrite_t, nand_1_out, not_1_out, not_2_out, not_3_out, not_4_out, not_5_out, not_7_out, not_8_out,
       not_9_out, not_10_out, or_1_out, or_2_out, or_3_out, or_4_out, RegWrite_t, RST, S_type, Stall,
       undriven, WB_JAL, WB_JALR, \单周期硬布线控制器_1_uret ;
  wire [0:0] alu_1_result_2;
  wire [1:0] ID_EX_rsforward_2, ID_EX_rtforward_2, \相关处理逻辑_重定向_1_r1forward , \相关处理逻辑_重定向_1_r2forward ;
  wire [3:0] AluOP, ID_EX_aluop_2;
  wire [4:0] EX_MEM_writereg_num_2, ID_EX_writereg_num_2, MEM_WB_writereg_num_2, multiplexer_3_out,
       multiplexer_4_out;
  wire [12:0] CNT_num;
  wire [15:0] \LoadUse次数 , \分支跳转次数 , \总周期数 ;
  wire [31:0] adder_1_out, adder_2_out, EX_IR, EX_MEM_aluresult_2, EX_MEM_pc_4_2, ID_EX_pc_4_2, ID_EX_r1_2,
       ID_EX_r2_2, ID_EX_signimm_2, ID_IR, IF_ID_pc_4_2, IF_IR, ImmGen_imm, \l指令分线器_1_imm32_2 , MEM_IR,
       MEM_WB_aluresult_2, MEM_WB_pc_4_2, MEM_WB_readdata_2, multiplexer_1_out, multiplexer_2_out,
       multiplexer_7_out, multiplexer_9_out, R1, R2, ram_1_data, regifile_1_r1, regifile_1_r2, shifter_1_out,
       WB_IR;
  wire [31:1] alu_1_result;

  Button \u_总复位  (.out(RST));
  // Probe on \总周期数 
  // Probe on \总周期数 
  Button \u_继续运行  (.out(Go));
  // Probe on IF_PC[19:0]
  // RiscV_Probe riscv_probe_1: pin names not known; wires that end beside it: IF_IR
  Multiplexer #(.select(1), .width(32), .disabled("Z"), .enable("false")) multiplexer_1 (
    .in0(adder_2_out), .in1({alu_1_result, 1'b0}), .out(multiplexer_1_out), .sel(ID_EX_jalr_2));
  Hex_Digit_Display hex_digit_display_1 (.value(LedData[31:28]));  // open: dp
  Hex_Digit_Display hex_digit_display_2 (.value(LedData[27:24]));  // open: dp
  Multiplexer #(.select(1), .width(32), .disabled("Z"), .enable("false")) multiplexer_2 (
    .in0(adder_1_out), .in1(multiplexer_1_out), .out(multiplexer_2_out), .sel(or_4_out));
  not not_1 (not_1_out, or_1_out);
  or or_1 (or_1_out, halt, Stall);
  Hex_Digit_Display hex_digit_display_3 (.value(LedData[19:16]));  // open: dp
  Hex_Digit_Display hex_digit_display_4 (.value(LedData[23:20]));  // open: dp
  // Probe on ID_PC[19:0]
  // RiscV_Probe riscv_probe_2: pin names not known; wires that end beside it: ID_IR
  Register #(.width(32), .trigger("rising"), .Select("low")) PC (
    .D(multiplexer_2_out), .en(not_1_out), .Q(IF_PC), .clk(CLK), .clr(RST));
  Hex_Digit_Display hex_digit_display_5 (.value(LedData[11:8]));  // open: dp
  Hex_Digit_Display hex_digit_display_6 (.value(LedData[15:12]));  // open: dp
  Hex_Digit_Display hex_digit_display_7 (.value(LedData[3:0]));  // open: dp
  Hex_Digit_Display hex_digit_display_8 (.value(LedData[7:4]));  // open: dp
  // Probe on EX_PC[19:0]
  // RiscV_Probe riscv_probe_3: pin names not known; wires that end beside it: EX_IR
  // RiscV_Probe riscv_probe_4: pin names not known; wires that end beside it: MEM_IR
  // RiscV_Probe riscv_probe_5: pin names not known; wires that end beside it: 32'h4, ID_IR
  ROM #(.addrWidth(10), .dataWidth(32), .Select("high")) rom_1 (.addr(IF_PC[11:2]), .data(IF_IR));
  Adder #(.width(32)) adder_1 (.a(IF_PC), .b(32'h4), .out(adder_1_out));  // open: cin, cout
  // Probe on \总周期数 
  // Probe on M_PC[19:0]
  not not_2 (not_2_out, Flush);
  and and_1 (and_1_out, EX_ecall, not_2_out, comparator_1_eq);
  Comparator #(.width(32), .mode("twosComplement")) comparator_1 (
    .a(R1), .b(32'h22), .eq(comparator_1_eq));  // open: gt, lt
  not not_3 (not_3_out, comparator_1_eq);
  not not_4 (not_4_out, Flush);
  not not_5 (not_5_out, Go);
  \相关处理逻辑_重定向  \u_相关处理逻辑_重定向_1  (
    .ID_IR(ID_IR), .EX_WriteReg_num(ID_EX_writereg_num_2), .EX_WriteReg(ID_EX_regwrite_2),
    .MEM_WriteReg_num(EX_MEM_writereg_num_2), .MEM_WriteReg(EX_MEM_regwrite_2),
    .EX_MemRead(ID_EX_memtoreg_2), .BranchTaken(or_4_out), .R1Forward(\相关处理逻辑_重定向_1_r1forward ),
    .R2Forward(\相关处理逻辑_重定向_1_r2forward ), .Stall(Stall), .Flush(Flush));  // open: PredictErr, IF_ID_CLR, ID_EX_CLR
  // NOT_Gate not_6 has open pins: in=Stall, out=open
  or or_2 (or_2_out, Stall, halt);
  // Probe on \总周期数 
  // Probe on \分支跳转次数 
  // Probe on \LoadUse次数 
  // Probe on \LoadUse次数 
  // Probe on WB_PC[19:0]
  // RiscV_Probe riscv_probe_6: pin names not known; wires that end beside it: WB_IR
  Register #(.width(32), .trigger("rising"), .Select("low")) register_1 (
    .D(R2), .en(and_1_out), .Q(LedData), .clk(CLK));  // open: clr
  and and_2 (halt, not_3_out, EX_ecall, not_4_out, not_5_out);
  not not_7 (not_7_out, or_2_out);
  IF_ID IF_ID (
    .IR(IF_IR), .PC_4(adder_1_out), .IR_2(ID_IR), .PC_4_2(IF_ID_pc_4_2), .CLK(CLK), .PC(IF_PC), .PC_2(ID_PC),
    .CLR(or_4_out), .EN(not_7_out));  // open: PredictJump, PredictJump_2
  // Probe on IF_PC[11:0]
  // Probe on ID_PC[11:0]
  // Probe on EX_PC[11:0]
  D_Flip_Flop #(.trigger("high"), .Pre_Clr_Positions("LEGACY"), .NegatePresetClear("false"), .enable("true"), .NewFFLayout("false")) d_ff_1 (.Q(d_ff_1_q));  // open: clk, D, Qn, preset, en, reset
  // Probe on WB_PC[11:0]
  // Probe on M_PC[11:0]
  // Probe on 13'h8ee
  \单周期硬布线控制器  \u_单周期硬布线控制器_1  (
    .Funct({ID_IR[30], ID_IR[25], ID_IR[14:12]}), .OP(ID_IR[6:2]), .ALU_OP(AluOP), .MemToReg(MemToReg),
    .MemWrite(MemWrite_t), .ALU_SRC(AluSrcB), .RegWrite(RegWrite_t), .ecall(ecall), .S_type(S_type),
    .Jalr(JALR), .Beq(Beq), .JAL(JAL), .Bne(Bne), .in_3(ID_IR[21]), .uret(\单周期硬布线控制器_1_uret ), .BGUE(Bgeu),
    .lb(lb));  // open: csrrsi, csrrci
  Multiplexer #(.select(1), .width(5), .disabled("Z"), .enable("false")) multiplexer_3 (
    .in0(ID_IR[19:15]), .in1(5'b10001), .out(multiplexer_3_out), .sel(ecall));
  Multiplexer #(.select(1), .width(5), .disabled("Z"), .enable("false")) multiplexer_4 (
    .in0(ID_IR[24:20]), .in1(5'b01010), .out(multiplexer_4_out), .sel(ecall));
  ImmGen ImmGen (
    .S_type(S_type), .Beq(Beq), .Bne(Bne), .JAL(JAL), .Imm12(ID_IR), .Imm_sw({ID_IR[31:25], ID_IR[11:7]}),
    .Imm_beq_bne_bgeu({ID_IR[31], ID_IR[7], ID_IR[30:25], ID_IR[11:8]}),
    .Imm_jal({ID_IR[31], ID_IR[19:12], ID_IR[20], ID_IR[30:21]}), .Imm(ImmGen_imm), .Bgeu(Bgeu));
  Comparator #(.width(13), .mode("twosComplement")) comparator_2 (
    .a(CNT_num), .b(13'h8ee), .eq(comparator_2_eq), .lt(comparator_2_lt));  // open: gt
  Clock #(.highDuration(1), .lowDuration(1)) clock_1 (.out(clock_1_out));
  Multiplexer #(.select(1), .width(32), .disabled("Z"), .enable("false")) multiplexer_5 (
    .in0(multiplexer_9_out), .in1(MEM_WB_pc_4_2), .out(RDin), .sel(or_3_out));
  or or_3 (or_3_out, WB_JAL, WB_JALR);
  nand nand_1 (nand_1_out, d_ff_1_q, comparator_2_eq);
  Counter #(.width(13), .max('h1fff), .ongoal("stay"), .trigger("rising"), .behavior("old")) counter_1 (
    .count(comparator_2_lt), .Q(CNT_num), .clk(clock_1_out));  // open: load, D, carry, clr, preset
  not not_8 (not_8_out, halt);
  and and_3 (and_3_out, not_8_out, nand_1_out);
  assign CLK = nand_1_out ? clock_1_out : 1'bz;  // Controlled_Buffer controlled_buffer_1
  Pull_Resistor #(.pull(1)) pull_resistor_1 (.node(CLK));
  Counter #(.width(16), .max('hffff), .ongoal("wrap"), .trigger("rising"), .behavior("new")) counter_2 (
    .count(and_3_out), .Q(\总周期数 ), .clk(clock_1_out));  // open: load, D, carry, clr, preset, down
  not not_9 (not_9_out, CLK);
  Regifile regifile_1 (
    .Din(RDin), .Clk(not_9_out), .R1(regifile_1_r1), .R2(regifile_1_r2), .WE(RegWrite),
    .W_num(MEM_WB_writereg_num_2), .R1_num(multiplexer_3_out), .R2_num(multiplexer_4_out));
  Counter #(.width(16), .max('hffff), .ongoal("wrap"), .trigger("rising"), .behavior("new")) counter_3 (
    .count(Stall), .Q(\LoadUse次数 ), .clk(CLK));  // open: load, D, carry, clr, preset, down
  ID_EX ID_EX (
    .RegWrite(RegWrite_t), .MemToReg(MemToReg), .MemWrite(MemWrite_t), .AluOP(AluOP), .Beq(Beq),
    .AluSrc(AluSrcB), .R1(regifile_1_r1), .R2(regifile_1_r2), .WriteReg_num(ID_IR[11:7]),
    .SignImm(ImmGen_imm), .CLK(CLK), .RegWrite_2(ID_EX_regwrite_2), .MemToReg_2(ID_EX_memtoreg_2),
    .MemWrite_2(ID_EX_memwrite_2), .AluOP_2(ID_EX_aluop_2), .Beq_2(ID_EX_beq_2), .AluSrc_2(ID_EX_alusrc_2),
    .R1_2(ID_EX_r1_2), .R2_2(ID_EX_r2_2), .WriteReg_num_2(ID_EX_writereg_num_2), .SignImm_2(ID_EX_signimm_2),
    .Bne(Bne), .Bne_2(ID_EX_bne_2), .PC(ID_PC), .PC_2(EX_PC), .IR(ID_IR), .IR_2(EX_IR), .CLR(Flush),
    .JAL(JAL), .JALR(JALR), .JAL_2(ID_EX_jal_2), .JALR_2(ID_EX_jalr_2), .PC_4(IF_ID_pc_4_2),
    .PC_4_2(ID_EX_pc_4_2), .RsForward(\相关处理逻辑_重定向_1_r1forward ), .RsForward_2(ID_EX_rsforward_2),
    .RtForward(\相关处理逻辑_重定向_1_r2forward ), .RtForward_2(ID_EX_rtforward_2), .ecall(ecall), .ecall_2(EX_ecall),
    .halt(halt), .Bgeu(Bgeu), .Bgeu_2(ID_EX_bgeu_2), .lb(lb), .lb_2(ID_EX_lb_2));  // open: PredictJump, PredictJump_2, csrrsi, csrrrsi, csrrci, csrrrci, uret, uret_2
  Multiplexer #(.select(2), .width(32), .disabled("Z"), .enable("false")) multiplexer_6 (
    .in0(ID_EX_r1_2), .in1(multiplexer_9_out), .in2(EX_MEM_aluresult_2), .out(R1), .sel(ID_EX_rtforward_2));  // open: in3
  Multiplexer #(.select(2), .width(32), .disabled("Z"), .enable("false")) multiplexer_7 (
    .in0(ID_EX_r2_2), .in1(multiplexer_9_out), .in2(EX_MEM_aluresult_2), .out(multiplexer_7_out),
    .sel(ID_EX_rsforward_2));  // open: in3
  and and_4 (and_4_out, Flush, ~Stall);  // AND_Gate
  Counter #(.width(16), .max('hffff), .ongoal("wrap"), .trigger("rising"), .behavior("new")) counter_4 (
    .count(and_4_out), .Q(\分支跳转次数 ), .clk(CLK));  // open: load, D, carry, clr, preset, down
  Multiplexer #(.select(1), .width(32), .disabled("Z"), .enable("false")) multiplexer_8 (
    .in0(multiplexer_7_out), .in1(ID_EX_signimm_2), .out(R2), .sel(ID_EX_alusrc_2));
  Shifter #(.width(32), .shift("ll")) shifter_1 (.in(ID_EX_signimm_2), .\dist (5'b00001), .out(shifter_1_out));
  ALU alu_1 (
    .X(R1), .Y(R2), .AluOP(ID_EX_aluop_2), .Equal(alu_1_equal), .Result({alu_1_result, alu_1_result_2[0]}),
    .out_4(alu_1_out_4));  // open: Result_2, out_6
  Adder #(.width(32)) adder_2 (.a(shifter_1_out), .b(EX_PC), .out(adder_2_out));  // open: cin, cout
  and and_5 (and_5_out, ID_EX_beq_2, alu_1_equal);
  and and_6 (and_6_out, ID_EX_bne_2, not_10_out);
  not not_10 (not_10_out, alu_1_equal);
  and and_7 (and_7_out, ID_EX_bgeu_2, alu_1_out_4);
  EX_MEM EX_MEM (
    .RegWrite(ID_EX_regwrite_2), .MemToReg(ID_EX_memtoreg_2), .MemWrite(ID_EX_memwrite_2),
    .AluResult({alu_1_result, alu_1_result_2[0]}), .WriteData(multiplexer_7_out),
    .WriteReg_num(ID_EX_writereg_num_2), .RegWrite_2(EX_MEM_regwrite_2), .MemToReg_2(EX_MEM_memtoreg_2),
    .MemWrite_2(MemWrite), .AluResult_2(EX_MEM_aluresult_2), .WriteData_2(MDin),
    .WriteReg_num_2(EX_MEM_writereg_num_2), .CLK(CLK), .PC(EX_PC), .PC_2(M_PC), .IR(EX_IR), .IR_2(MEM_IR),
    .JAL(ID_EX_jal_2), .JAL_2(EX_MEM_jal_2), .JALR(ID_EX_jalr_2), .JALR_2(EX_MEM_jalr_2),
    .PC_4(ID_EX_pc_4_2), .PC_4_2(EX_MEM_pc_4_2), .lb(ID_EX_lb_2), .lb_2(EX_MEM_lb_2), .URET(undriven));  // open: URET_2
  or or_4 (or_4_out, and_5_out, and_6_out, ID_EX_jal_2, ID_EX_jalr_2, and_7_out);
  \L指令分线器  \l指令分线器_1  (
    .lb(EX_MEM_lb_2), .Imm32_2(\l指令分线器_1_imm32_2 ), .Imm32(ram_1_data), .offset(EX_MEM_aluresult_2[1:0]));
  RAM #(.addrWidth(10), .dataWidth(32), .bus("separate"), .Select("high")) ram_1 (
    .addr(EX_MEM_aluresult_2[11:2]), .din(MDin), .data(ram_1_data), .str(MemWrite), .clk(CLK));  // open: sel, ld, clr
  MEM_WB MEM_WB (
    .RegWrite(EX_MEM_regwrite_2), .MemToReg(EX_MEM_memtoreg_2), .AluResult(EX_MEM_aluresult_2),
    .ReadData(\l指令分线器_1_imm32_2 ), .WriteReg_num(EX_MEM_writereg_num_2), .RegWrite_2(RegWrite),
    .MemToReg_2(MEM_WB_memtoreg_2), .AluResult_2(MEM_WB_aluresult_2), .ReadData_2(MEM_WB_readdata_2),
    .WriteReg_num_2(MEM_WB_writereg_num_2), .CLK(CLK), .PC(M_PC), .PC_2(WB_PC), .IR(MEM_IR), .IR_2(WB_IR),
    .JAL(EX_MEM_jal_2), .JALR(EX_MEM_jalr_2), .JAL_2(WB_JAL), .JALR_2(WB_JALR), .PC_4(EX_MEM_pc_4_2),
    .PC_4_2(MEM_WB_pc_4_2));
  Multiplexer #(.select(1), .width(32), .disabled("Z"), .enable("false")) multiplexer_9 (
    .in0(MEM_WB_aluresult_2), .in1(MEM_WB_readdata_2), .out(multiplexer_9_out), .sel(MEM_WB_memtoreg_2));

  // Other names for the same wires on the sheet: IR[31:0] = ID_IR; MEM_MemWrite = MemWrite; MEM_PC[31:0] = M_PC;
  //   PC[31:0] = IF_PC; WB_RegWrite = RegWrite; 插入气泡数[15:0] = \LoadUse次数 

  // Notes on the sheet:
  //   JALR
  //   BranchTaken
  //   数码管输出
  //   出现Load-Use时，使PC寄存器和IF/ID流水寄存器暂停，在EX段插入气泡
  //   IF
  //   指令探针
  //   指令存储器
  //   contents of rom_1 (hex, n*v repeats v):
  //   100493 100006f 100493 200913 300993 100006f 100493 200913 300993 100006f 100493 200913 300993
  //   100006f 100493 200913 300993 3e0000ef 100413 100493 1f49493 900533 2200893 73 24d493 48463 fedff06f
  //   900533 2200893 73 100493 249493 900533 2200893 73 48463 fedff06f 100493 1f49493 900533 2200893 73
  //   4034d493 900533 2200893 73 4044d493 900533 2200893 73 4044d493 900533 2200893 73 4044d493 900533
  //   2200893 73 4044d493 900533 2200893 73 4044d493 900533 2200893 73 4044d493 900533 2200893 73 4044d493
  //   900533 2200893 73 100413 1f41993 41f9d993 433 c00913 300b13 140413 f47413 800293 100313 499993
  //   89e9b3 1300533 2200893 73 406282b3 fe0294e3 140413 f00f93 1f47433 1c41413 800293 100313 49d993
  //   89e9b3 1300533 2200893 73 406282b3 fe0294e3 1c45413 406b0b33 b0463 f95ff06f 2b3 fff2c293 829293
  //   ff2e293 500533 2200893 73 fff00413 493 84a023 140413 448493 84a023 140413 448493 84a023 140413
  //   448493 84a023 140413 448493 84a023 140413 448493 84a023 140413 448493 84a023 140413 448493 84a023
  //   140413 448493 84a023 140413 448493 84a023 140413 448493 84a023 140413 448493 84a023 140413 448493
  //   84a023 140413 448493 84a023 140413 448493 84a023 140413 448493 84a023 140413 448493 140413 433
  //   3c00493 42983 4aa03 149a2b3 28663 134a023 1442023 ffc48493 fe9412e3 800533 2200893 73 440413 3c00493
  //   fc9416e3 3200893 73 100293 300313 800493 849493 7648493 900533 2200893 73 800e13 5494b3 6494b3
  //   900533 2200893 73 fffe0e13 fe0e14e3 a00893 73 100293 300313 800493 849493 7648493 1449493 900533
  //   2200893 73 800e13 54d4b3 64d4b3 900533 2200893 73 fffe0e13 fe0e14e3 a00893 73 313 1000e13 8400493
  //   849493 8348493 400913 891913 490913 849493 8248493 849493 8148493 891913 490913 891913 490913 932023
  //   12484b3 430313 fffe0e13 fe0e18e3 2000e13 313 30483 900533 2200893 73 130313 fffe0e13 fe0e14e3 a00893
  //   73 f00493 100913 409909b3 900533 2200893 73 fff48493 ff29f6e3 a00893 73 a00893 73 413 140413 800533
  //   2200893 73 240413 800533 2200893 73 340413 800533 2200893 73 440413 800533 2200893 73 540413 800533
  //   2200893 73 640413 800533 2200893 73 740413 800533 2200893 73 840413 800533 2200893 2200893 73 8067
  //   PC+4
  //   ID.IR
  //   指令字
  //   控制位
  //   暂停节拍，不能为0
  //   JAL
  //   JALR
  //   URET
  //   sw
  //   beq/bne/bgeu
  //   jal
  //   流水调试日志用
  //   ID
  //   Beq
  //   Bne
  //   MemToReg
  //   MemWrite
  //   AluOP
  //   AluSrcB
  //   RegWrite
  //   可计数暂停的时钟源
  //   Rt
  //   Rs
  //   R1
  //   R2
  //   WriteReg#
  //   SignImm
  //   PC+4
  //   为方便自动评测，需要输出流水线各段保存的PC值，注意是PC不是PC+4，另外ID段寄存器写入信息，Mem段内存写入信息也要输出
  //   EX
  //   EX.MemRead
  //   PC+SignImm
  //   EX.RegWrite
  //   Bgeu
  //   AluResult
  //   WriteData
  //   WriteReg#
  //   PC+4
  //   EX.WriteReg#
  //   BranchTaken
  //   Beq
  //   Bne
  //   JAL
  //   JALR
  //   RegWrite
  //   MemToReg
  //   MemWrite
  //   BranchTaken
  //   MEM
  //   数据存储器
  //   MEM.RegWrite
  //   PC+4
  //   MEM.WriteReg#
  //   RegWrite
  //   MemToReg
  //   JAL
  //   JALR
  //   AluResult
  //   ReadData
  //   WriteReg#
  //   MEM.PC
  //   MEM.IR
  //   PC+4
  //   WB
endmodule

module \重定向流水线_动态预测  (
  output RegWrite,
  output MemWrite,
  output [31:0] IF_PC,
  output [31:0] ID_PC,
  output [31:0] EX_PC,
  output [31:0] M_PC,
  output [31:0] WB_PC,
  output [31:0] RDin,
  output [31:0] MDin,
  output [31:0] LedData
);

  wire alu_1_equal, alu_1_out_4, AluSrcB, and_1_out, and_2_out, and_4_out, and_5_out, and_6_out, and_7_out,
       Beq, Bgeu, Bne, BTB_predictjump, CLK, clock_1_out, comparator_1_eq, comparator_1_lt, comparator_2_eq,
       comparator_3_eq, d_ff_1_q, ecall, EX_Branch, EX_BranchTaken, EX_ecall, EX_MEM_jal_2, EX_MEM_jalr_2,
       EX_MEM_lb_2, EX_MEM_memtoreg_2, EX_MEM_regwrite_2, Flush, Go, halt, ID_EX_alusrc_2, ID_EX_beq_2,
       ID_EX_bgeu_2, ID_EX_bne_2, ID_EX_jal_2, ID_EX_jalr_2, ID_EX_lb_2, ID_EX_memtoreg_2, ID_EX_memwrite_2,
       ID_EX_regwrite_2, IF_ID_predictjump_2, IR1, IR2, IR3, JAL, JALR, lb, MEM_WB_memtoreg_2, MemToReg,
       MemWrite_t, nand_1_out, not_1_out, not_2_out, not_3_out, not_4_out, not_5_out, not_6_out, not_7_out,
       not_8_out, or_1_out, or_2_out, or_3_out, PredictErr, PredictJump, RegWrite_t, RST, S_type, Stall,
       undriven, W1, W2, W3, WB_JAL, WB_JALR, \单周期硬布线控制器_1_uret , \相关处理逻辑_重定向_1_id_ex_clr ,
       \相关处理逻辑_重定向_1_if_id_clr ;
  wire [0:0] alu_1_result;
  wire [1:0] ID_EX_rsforward_2, ID_EX_rtforward_2, \相关处理逻辑_重定向_1_r1forward , \相关处理逻辑_重定向_1_r2forward ;
  wire [3:0] AluOP, ID_EX_aluop_2;
  wire [4:0] EX_MEM_writereg_num_2, ID_EX_writereg_num_2, MEM_WB_writereg_num_2, multiplexer_5_out,
       multiplexer_6_out;
  wire [12:0] CNT_num;
  wire [15:0] \LoadUse次数 , \总周期数 , \无条件分支数 , \条件分支成功数 ;
  wire [30:0] alu_1_result_2;
  wire [31:0] adder_1_out, adder_2_out, BranchAddr, BTB_jumpaddr, EX_IR, EX_MEM_aluresult_2, EX_MEM_pc_4_2,
       EX_PC_4, ID_EX_r1_2, ID_EX_r2_2, ID_EX_signimm_2, ID_IR, IF_ID_pc_4_2, IF_IR, \immgen_封装版_1_imm ,
       \l指令分线器_1_imm32_2 , MEM_IR, MEM_WB_aluresult_2, MEM_WB_pc_4_2, MEM_WB_readdata_2, multiplexer_2_out,
       multiplexer_3_out, multiplexer_4_out, multiplexer_9_out, multiplexer_11_out, R1, R2, ram_1_data,
       regifile_1_r1, regifile_1_r2, shifter_1_out, WB_IR;

  Button \u_总复位  (.out(RST));
  Button _1 (.out(IR1));
  Button _2 (.out(IR2));
  Button _3 (.out(IR3));
  // Probe on \总周期数 
  // Probe on \总周期数 
  Multiplexer #(.select(1), .width(32), .disabled("Z"), .enable("false")) multiplexer_1 (
    .in0(adder_2_out), .in1({alu_1_result_2, 1'b0}), .out(BranchAddr), .sel(ID_EX_jalr_2));
  Button \u_继续运行  (.out(Go));
  LED #(.active("true")) led_1 (.in(W1));
  LED #(.active("true")) led_2 (.in(W2));
  LED #(.active("true")) led_3 (.in(W3));
  Multiplexer #(.select(1), .width(32), .disabled("Z"), .enable("false")) multiplexer_2 (
    .in0(EX_PC_4), .in1(BranchAddr), .out(multiplexer_2_out), .sel(EX_BranchTaken));
  Hex_Digit_Display hex_digit_display_1 (.value(LedData[31:28]));  // open: dp
  // Probe on IF_PC[19:0]
  // RiscV_Probe riscv_probe_1: pin names not known; wires that end beside it: IF_IR
  Multiplexer #(.select(1), .width(32), .disabled("Z"), .enable("false")) multiplexer_3 (
    .in0(multiplexer_4_out), .in1(multiplexer_2_out), .out(multiplexer_3_out), .sel(PredictErr));
  Hex_Digit_Display hex_digit_display_2 (.value(LedData[23:20]));  // open: dp
  Hex_Digit_Display hex_digit_display_3 (.value(LedData[27:24]));  // open: dp
  // Probe on ID_PC[19:0]
  // RiscV_Probe riscv_probe_2: pin names not known; wires that end beside it: ID_IR
  Hex_Digit_Display hex_digit_display_4 (.value(LedData[19:16]));  // open: dp
  Hex_Digit_Display hex_digit_display_5 (.value(LedData[15:12]));  // open: dp
  Register #(.width(32), .trigger("rising"), .Select("low")) PC (
    .D(multiplexer_3_out), .en(not_1_out), .Q(IF_PC), .clk(CLK), .clr(RST));
  not not_1 (not_1_out, or_1_out);
  or or_1 (or_1_out, halt, Stall);
  Hex_Digit_Display hex_digit_display_6 (.value(LedData[11:8]));  // open: dp
  Hex_Digit_Display hex_digit_display_7 (.value(LedData[7:4]));  // open: dp
  // Probe on EX_PC[19:0]
  // RiscV_Probe riscv_probe_3: pin names not known; wires that end beside it: EX_IR
  BTB BTB (
    .PC(IF_PC), .EX_PC(EX_PC), .BranchAddr(BranchAddr), .EX_Branch(EX_Branch),
    .EX_BranchTaken(EX_BranchTaken), .JumpAddr(BTB_jumpaddr), .PredictJump(BTB_predictjump), .CLK(CLK));
  Multiplexer #(.select(1), .width(32), .disabled("Z"), .enable("false")) multiplexer_4 (
    .in0(adder_1_out), .in1(BTB_jumpaddr), .out(multiplexer_4_out), .sel(BTB_predictjump));
  Hex_Digit_Display hex_digit_display_8 (.value(LedData[3:0]));  // open: dp
  // Probe on \总周期数 
  // Probe on M_PC[19:0]
  // RiscV_Probe riscv_probe_4: pin names not known; wires that end beside it: MEM_IR
  // Probe on \总周期数 
  // Probe on \无条件分支数 
  // Probe on \条件分支成功数 
  // Probe on \LoadUse次数 
  // Probe on \LoadUse次数 
  // Probe on IF_PC[11:0]
  // Probe on WB_PC[19:0]
  // RiscV_Probe riscv_probe_5: pin names not known; wires that end beside it: WB_IR
  ROM #(.addrWidth(10), .dataWidth(32), .Select("high")) rom_1 (.addr(IF_PC[11:2]), .data(IF_IR));
  Adder #(.width(32)) adder_1 (.a(IF_PC), .b(32'h4), .out(adder_1_out));  // open: cin, cout
  // Probe on ID_PC[11:0]
  \相关处理逻辑_重定向  \u_相关处理逻辑_重定向_1  (
    .ID_IR(ID_IR), .EX_WriteReg_num(ID_EX_writereg_num_2), .EX_WriteReg(ID_EX_regwrite_2),
    .MEM_WriteReg_num(EX_MEM_writereg_num_2), .MEM_WriteReg(EX_MEM_regwrite_2),
    .EX_MemRead(ID_EX_memtoreg_2), .BranchTaken(EX_BranchTaken), .R1Forward(\相关处理逻辑_重定向_1_r1forward ),
    .R2Forward(\相关处理逻辑_重定向_1_r2forward ), .Stall(Stall), .Flush(Flush), .PredictErr(PredictErr),
    .IF_ID_CLR(\相关处理逻辑_重定向_1_if_id_clr ), .ID_EX_CLR(\相关处理逻辑_重定向_1_id_ex_clr ));
  or or_2 (or_2_out, Stall, halt);
  // RiscV_Probe riscv_probe_6: pin names not known; wires that end beside it: ID_IR
  // Probe on EX_PC[11:0]
  // Probe on M_PC[11:0]
  D_Flip_Flop #(.trigger("high"), .Pre_Clr_Positions("LEGACY"), .NegatePresetClear("false"), .enable("true"), .NewFFLayout("false")) d_ff_1 (.Q(d_ff_1_q));  // open: clk, D, Qn, preset, en, reset
  // Probe on 13'h6d6
  not not_2 (not_2_out, or_2_out);
  IF_ID IF_ID (
    .IR(IF_IR), .PC_4(adder_1_out), .IR_2(ID_IR), .PC_4_2(IF_ID_pc_4_2), .CLK(CLK), .PC(IF_PC), .PC_2(ID_PC),
    .CLR(\相关处理逻辑_重定向_1_if_id_clr ), .EN(not_2_out), .PredictJump(BTB_predictjump),
    .PredictJump_2(IF_ID_predictjump_2));
  // Probe on WB_PC[11:0]
  Comparator #(.width(13), .mode("twosComplement")) comparator_1 (
    .a(CNT_num), .b(13'h6d6), .eq(comparator_1_eq), .lt(comparator_1_lt));  // open: gt
  Clock #(.highDuration(1), .lowDuration(1)) clock_1 (.out(clock_1_out));
  nand nand_1 (nand_1_out, d_ff_1_q, comparator_1_eq);
  Counter #(.width(13), .max('h1fff), .ongoal("stay"), .trigger("rising"), .behavior("old")) counter_1 (
    .count(comparator_1_lt), .Q(CNT_num), .clk(clock_1_out));  // open: load, D, carry, clr, preset
  and and_1 (and_1_out, nand_1_out, ~halt);  // AND_Gate
  Counter #(.width(16), .max('hffff), .ongoal("wrap"), .trigger("rising"), .behavior("new")) counter_2 (
    .count(and_1_out), .Q(\总周期数 ), .clk(clock_1_out));  // open: load, D, carry, clr, preset, down
  \单周期硬布线控制器  \u_单周期硬布线控制器_1  (
    .Funct({ID_IR[30], ID_IR[25], ID_IR[14:12]}), .OP(ID_IR[6:2]), .ALU_OP(AluOP), .MemToReg(MemToReg),
    .MemWrite(MemWrite_t), .ALU_SRC(AluSrcB), .RegWrite(RegWrite_t), .ecall(ecall), .S_type(S_type),
    .Jalr(JALR), .Beq(Beq), .JAL(JAL), .Bne(Bne), .in_3(ID_IR[21]), .uret(\单周期硬布线控制器_1_uret ), .BGUE(Bgeu),
    .lb(lb));  // open: csrrsi, csrrci
  Multiplexer #(.select(1), .width(5), .disabled("Z"), .enable("false")) multiplexer_5 (
    .in0(ID_IR[19:15]), .in1(5'b10001), .out(multiplexer_5_out), .sel(ecall));
  Multiplexer #(.select(1), .width(5), .disabled("Z"), .enable("false")) multiplexer_6 (
    .in0(ID_IR[24:20]), .in1(5'b01010), .out(multiplexer_6_out), .sel(ecall));
  assign CLK = nand_1_out ? clock_1_out : 1'bz;  // Controlled_Buffer controlled_buffer_1
  Pull_Resistor #(.pull(1)) pull_resistor_1 (.node(CLK));
  \ImmGen_封装版  \immgen_封装版_1  (.IR(ID_IR), .Imm(\immgen_封装版_1_imm ));
  Multiplexer #(.select(1), .width(32), .disabled("Z"), .enable("false")) multiplexer_7 (
    .in0(multiplexer_11_out), .in1(MEM_WB_pc_4_2), .out(RDin), .sel(or_3_out));
  or or_3 (or_3_out, WB_JAL, WB_JALR);
  not not_3 (not_3_out, Flush);
  Comparator #(.width(32), .mode("twosComplement")) comparator_2 (
    .a(R1), .b(32'h22), .eq(comparator_2_eq));  // open: gt, lt
  not not_4 (not_4_out, CLK);
  Regifile regifile_1 (
    .Din(RDin), .Clk(not_4_out), .R1(regifile_1_r1), .R2(regifile_1_r2), .WE(RegWrite),
    .W_num(MEM_WB_writereg_num_2), .R1_num(multiplexer_5_out), .R2_num(multiplexer_6_out));
  and and_2 (and_2_out, EX_ecall, not_3_out, comparator_2_eq);
  not not_5 (not_5_out, comparator_2_eq);
  not not_6 (not_6_out, Flush);
  not not_7 (not_7_out, Go);
  Register #(.width(32), .trigger("rising"), .Select("low")) register_1 (
    .D(R2), .en(and_2_out), .Q(LedData), .clk(CLK));  // open: clr
  and and_3 (halt, not_5_out, EX_ecall, not_6_out, not_7_out);
  ID_EX ID_EX (
    .RegWrite(RegWrite_t), .MemToReg(MemToReg), .MemWrite(MemWrite_t), .AluOP(AluOP), .Beq(Beq),
    .AluSrc(AluSrcB), .R1(regifile_1_r1), .R2(regifile_1_r2), .WriteReg_num(ID_IR[11:7]),
    .SignImm(\immgen_封装版_1_imm ), .CLK(CLK), .RegWrite_2(ID_EX_regwrite_2), .MemToReg_2(ID_EX_memtoreg_2),
    .MemWrite_2(ID_EX_memwrite_2), .AluOP_2(ID_EX_aluop_2), .Beq_2(ID_EX_beq_2), .AluSrc_2(ID_EX_alusrc_2),
    .R1_2(ID_EX_r1_2), .R2_2(ID_EX_r2_2), .WriteReg_num_2(ID_EX_writereg_num_2), .SignImm_2(ID_EX_signimm_2),
    .Bne(Bne), .Bne_2(ID_EX_bne_2), .PC(ID_PC), .PC_2(EX_PC), .IR(ID_IR), .IR_2(EX_IR),
    .CLR(\相关处理逻辑_重定向_1_id_ex_clr ), .JAL(JAL), .JALR(JALR), .JAL_2(ID_EX_jal_2), .JALR_2(ID_EX_jalr_2),
    .PC_4(IF_ID_pc_4_2), .PC_4_2(EX_PC_4), .RsForward(\相关处理逻辑_重定向_1_r1forward ),
    .RsForward_2(ID_EX_rsforward_2), .RtForward(\相关处理逻辑_重定向_1_r2forward ), .RtForward_2(ID_EX_rtforward_2),
    .ecall(ecall), .ecall_2(EX_ecall), .halt(halt), .PredictJump(IF_ID_predictjump_2),
    .PredictJump_2(PredictJump), .Bgeu(Bgeu), .Bgeu_2(ID_EX_bgeu_2), .lb(lb), .lb_2(ID_EX_lb_2));  // open: csrrsi, csrrrsi, csrrci, csrrrci, uret, uret_2
  or or_4 (EX_Branch, ID_EX_beq_2, ID_EX_bne_2, ID_EX_jal_2, ID_EX_jalr_2);
  Multiplexer #(.select(2), .width(32), .disabled("Z"), .enable("false")) multiplexer_8 (
    .in0(ID_EX_r1_2), .in1(multiplexer_11_out), .in2(EX_MEM_aluresult_2), .out(R1), .sel(ID_EX_rtforward_2));  // open: in3
  Multiplexer #(.select(2), .width(32), .disabled("Z"), .enable("false")) multiplexer_9 (
    .in0(ID_EX_r2_2), .in1(multiplexer_11_out), .in2(EX_MEM_aluresult_2), .out(multiplexer_9_out),
    .sel(ID_EX_rsforward_2));  // open: in3
  Multiplexer #(.select(1), .width(32), .disabled("Z"), .enable("false")) multiplexer_10 (
    .in0(multiplexer_9_out), .in1(ID_EX_signimm_2), .out(R2), .sel(ID_EX_alusrc_2));
  Shifter #(.width(32), .shift("ll")) shifter_1 (.in(ID_EX_signimm_2), .\dist (5'b00001), .out(shifter_1_out));
  Counter #(.width(16), .max('hffff), .ongoal("wrap"), .trigger("rising"), .behavior("new")) counter_3 (
    .count(Stall), .Q(\LoadUse次数 ), .clk(CLK));  // open: load, D, carry, clr, preset, down
  ALU alu_1 (
    .X(R1), .Y(R2), .AluOP(ID_EX_aluop_2), .Equal(alu_1_equal), .Result({alu_1_result_2, alu_1_result[0]}),
    .out_4(alu_1_out_4));  // open: Result_2, out_6
  Adder #(.width(32)) adder_2 (.a(shifter_1_out), .b(EX_PC), .out(adder_2_out));  // open: cin, cout
  and and_4 (and_4_out, ID_EX_beq_2, alu_1_equal);
  and and_5 (and_5_out, ID_EX_bne_2, not_8_out);
  not not_8 (not_8_out, alu_1_equal);
  and and_6 (and_6_out, EX_Branch, ~PredictErr);  // AND_Gate
  or or_5 (EX_BranchTaken, and_4_out, and_5_out, ID_EX_jal_2, ID_EX_jalr_2, and_7_out);
  and and_7 (and_7_out, ID_EX_bgeu_2, alu_1_out_4);
  Counter #(.width(16), .max('hffff), .ongoal("wrap"), .trigger("rising"), .behavior("new")) counter_4 (
    .count(and_6_out), .Q(\条件分支成功数 ), .clk(CLK));  // open: load, D, carry, clr, preset, down
  EX_MEM EX_MEM (
    .RegWrite(ID_EX_regwrite_2), .MemToReg(ID_EX_memtoreg_2), .MemWrite(ID_EX_memwrite_2),
    .AluResult({alu_1_result_2, alu_1_result[0]}), .WriteData(multiplexer_9_out),
    .WriteReg_num(ID_EX_writereg_num_2), .RegWrite_2(EX_MEM_regwrite_2), .MemToReg_2(EX_MEM_memtoreg_2),
    .MemWrite_2(MemWrite), .AluResult_2(EX_MEM_aluresult_2), .WriteData_2(MDin),
    .WriteReg_num_2(EX_MEM_writereg_num_2), .CLK(CLK), .PC(EX_PC), .PC_2(M_PC), .IR(EX_IR), .IR_2(MEM_IR),
    .JAL(ID_EX_jal_2), .JAL_2(EX_MEM_jal_2), .JALR(ID_EX_jalr_2), .JALR_2(EX_MEM_jalr_2), .PC_4(EX_PC_4),
    .PC_4_2(EX_MEM_pc_4_2), .lb(ID_EX_lb_2), .lb_2(EX_MEM_lb_2), .URET(undriven));  // open: URET_2
  Comparator #(.width(1), .mode("twosComplement")) comparator_3 (
    .a(EX_BranchTaken), .b(PredictJump), .eq(comparator_3_eq));  // open: gt, lt
  not not_9 (PredictErr, comparator_3_eq);
  RAM #(.addrWidth(10), .dataWidth(32), .bus("separate"), .Select("high")) ram_1 (
    .addr(EX_MEM_aluresult_2[11:2]), .din(MDin), .data(ram_1_data), .str(MemWrite), .clk(CLK));  // open: sel, ld, clr
  \L指令分线器  \l指令分线器_1  (
    .lb(EX_MEM_lb_2), .Imm32_2(\l指令分线器_1_imm32_2 ), .Imm32(ram_1_data), .offset(EX_MEM_aluresult_2[1:0]));
  MEM_WB MEM_WB (
    .RegWrite(EX_MEM_regwrite_2), .MemToReg(EX_MEM_memtoreg_2), .AluResult(EX_MEM_aluresult_2),
    .ReadData(\l指令分线器_1_imm32_2 ), .WriteReg_num(EX_MEM_writereg_num_2), .RegWrite_2(RegWrite),
    .MemToReg_2(MEM_WB_memtoreg_2), .AluResult_2(MEM_WB_aluresult_2), .ReadData_2(MEM_WB_readdata_2),
    .WriteReg_num_2(MEM_WB_writereg_num_2), .CLK(CLK), .PC(M_PC), .PC_2(WB_PC), .IR(MEM_IR), .IR_2(WB_IR),
    .JAL(EX_MEM_jal_2), .JALR(EX_MEM_jalr_2), .JAL_2(WB_JAL), .JALR_2(WB_JALR), .PC_4(EX_MEM_pc_4_2),
    .PC_4_2(MEM_WB_pc_4_2));
  Multiplexer #(.select(1), .width(32), .disabled("Z"), .enable("false")) multiplexer_11 (
    .in0(MEM_WB_aluresult_2), .in1(MEM_WB_readdata_2), .out(multiplexer_11_out), .sel(MEM_WB_memtoreg_2));

  // Other names for the same wires on the sheet: IR[31:0] = ID_IR; MEM_MemWrite = MemWrite; MEM_PC[31:0] = M_PC;
  //   PC[31:0] = IF_PC; WB_RegWrite = RegWrite; 插入气泡数[15:0] = \LoadUse次数 

  // Notes on the sheet:
  //   中断源
  //   时空图监测，可删除
  //   JALR
  //   中断等待指示
  //   BranchTaken
  //   预测成功
  //   预测失败，计算地址
  //   预测地址
  //   数码管输出
  //   PC+4
  //   分支地址
  //   IF
  //   指令探针
  //   指令存储器
  //   contents of rom_1 (hex, n*v repeats v):
  //   100493 100006f 100493 200913 300993 100006f 100493 200913 300993 100006f 100493 200913 300993
  //   100006f 100493 200913 300993 3e0000ef 100413 100493 1f49493 900533 2200893 73 24d493 48463 fedff06f
  //   900533 2200893 73 100493 249493 900533 2200893 73 48463 fedff06f 100493 1f49493 900533 2200893 73
  //   4034d493 900533 2200893 73 4044d493 900533 2200893 73 4044d493 900533 2200893 73 4044d493 900533
  //   2200893 73 4044d493 900533 2200893 73 4044d493 900533 2200893 73 4044d493 900533 2200893 73 4044d493
  //   900533 2200893 73 100413 1f41993 41f9d993 433 c00913 300b13 140413 f47413 800293 100313 499993
  //   89e9b3 1300533 2200893 73 406282b3 fe0294e3 140413 f00f93 1f47433 1c41413 800293 100313 49d993
  //   89e9b3 1300533 2200893 73 406282b3 fe0294e3 1c45413 406b0b33 b0463 f95ff06f 2b3 fff2c293 829293
  //   ff2e293 500533 2200893 73 fff00413 493 84a023 140413 448493 84a023 140413 448493 84a023 140413
  //   448493 84a023 140413 448493 84a023 140413 448493 84a023 140413 448493 84a023 140413 448493 84a023
  //   140413 448493 84a023 140413 448493 84a023 140413 448493 84a023 140413 448493 84a023 140413 448493
  //   84a023 140413 448493 84a023 140413 448493 84a023 140413 448493 84a023 140413 448493 140413 433
  //   3c00493 42983 4aa03 149a2b3 28663 134a023 1442023 ffc48493 fe9412e3 800533 2200893 73 440413 3c00493
  //   fc9416e3 3200893 73 100293 300313 800493 849493 7648493 900533 2200893 73 800e13 5494b3 6494b3
  //   900533 2200893 73 fffe0e13 fe0e14e3 a00893 73 100293 300313 800493 849493 7648493 1449493 900533
  //   2200893 73 800e13 54d4b3 64d4b3 900533 2200893 73 fffe0e13 fe0e14e3 a00893 73 313 1000e13 8400493
  //   849493 8348493 400913 891913 490913 849493 8248493 849493 8148493 891913 490913 891913 490913 932023
  //   12484b3 430313 fffe0e13 fe0e18e3 2000e13 313 30483 900533 2200893 73 130313 fffe0e13 fe0e14e3 a00893
  //   73 f00493 100913 409909b3 900533 2200893 73 fff48493 ff29f6e3 a00893 73 a00893 73 413 140413 800533
  //   2200893 73 240413 800533 2200893 73 340413 800533 2200893 73 440413 800533 2200893 73 540413 800533
  //   2200893 73 640413 800533 2200893 73 740413 800533 2200893 73 840413 800533 2200893 2200893 73 8067
  //   PC+4
  //   流水调试日志用
  //   控制位
  //   暂停节拍，不能为0
  //   ID.IR
  //   指令字
  //   JAL
  //   JALR
  //   URET
  //   ID
  //   Bne
  //   MemToReg
  //   MemWrite
  //   AluOP
  //   AluSrcB
  //   RegWrite
  //   可计数暂停的时钟源
  //   Rt
  //   Rs
  //   为方便自动评测，需要输出流水线各段保存的PC值，注意是PC不是PC+4，另外ID段寄存器写入信息，Mem段内存写入信息也要输出
  //   R1
  //   R2
  //   PC+4
  //   为1则暂停
  //   EX.MemRead
  //   EX.RegWrite
  //   PC+SignImm
  //   EX.WriteReg#
  //   Beq
  //   Bne
  //   JAL
  //   JALR
  //   EX
  //   PC+4
  //   BranchTaken
  //   数据存储器
  //   MEM
  //   PC+4
  //   WB
endmodule

module \中断按键参考电路  (
  input  \同步清零信号 ,
  output \与中断屏蔽位与 
);

  wire \_1号中断_out , and_1_out, clock_1_out, d_ff_1_q, or_1_out, or_2_out;

  Clock #(.highDuration(1), .lowDuration(1)) clock_1 (.out(clock_1_out));
  Button \_1号中断  (.out(\_1号中断_out ));
  LED #(.active("true")) \_1号中断等待指示灯  (.in(or_1_out));
  or or_1 (or_1_out, \与中断屏蔽位与 , d_ff_1_q);
  D_Flip_Flop #(.trigger("rising"), .Pre_Clr_Positions("LEGACY"), .NegatePresetClear("false"), .enable("true"), .NewFFLayout("false")) d_ff_1 (
    .clk(\_1号中断_out ), .D(1'b1), .Q(d_ff_1_q), .reset(\与中断屏蔽位与 ));  // open: Qn, preset, en
  or or_2 (or_2_out, d_ff_1_q, \与中断屏蔽位与 );
  and and_1 (and_1_out, or_2_out, ~\同步清零信号 );  // AND_Gate
  D_Flip_Flop #(.trigger("rising"), .Pre_Clr_Positions("LEGACY"), .NegatePresetClear("false"), .enable("true"), .NewFFLayout("false")) IR1 (
    .clk(clock_1_out), .D(and_1_out), .Q(\与中断屏蔽位与 ));  // open: Qn, preset, en, reset

  // Notes on the sheet:
  //   中断信号采样参考电路
  //   Reset 
endmodule

module \单周期_多级中断  (
  input  IR1,
  input  IR2,
  input  IR3,
  output RegWrite,
  output MemWrite,
  output [31:0] PC,
  output [31:0] IR,
  output [31:0] RDin,
  output [31:0] MDin,
  output [31:0] LedData
);

  wire \_1号中断响应 , \_1号中断已响应 , \_2号中断响应 , \_2号中断已响应 , \_3号中断响应 , \_3号中断已响应 , alu_1_equal, alu_1_out_4,
       and_1_out, and_2_out, and_4_out, and_5_out, and_6_out, and_7_out, and_8_out, and_9_out, and_10_out,
       and_11_out, and_12_out, and_13_out, and_14_out, and_15_out, and_16_out, and_17_out, and_18_out,
       and_19_out, and_20_out, and_21_out, and_22_out, and_23_out, and_24_out, and_25_out, and_26_out,
       and_27_out, and_31_out, and_32_out, and_33_out, and_34_out, and_35_out, and_36_out, Beq, Bgeu, Bne,
       CLK, clock_2_out, comparator_1_eq, comparator_2_eq, comparator_2_lt, comparator_3_eq, comparator_4_eq,
       comparator_5_eq, comparator_6_eq, comparator_7_eq, comparator_11_eq, comparator_12_eq,
       controlled_inverter_1_out, controlled_inverter_2_out, controlled_inverter_3_out, csrrci, csrrsi,
       d_ff_1_q, ecall, Go, halt, IE, \IE已初始化_q , In2_Exist, In3_Exist, IR1_t, IR2_t, IR3_t, IRA, IRB, IRC,
       JAL, JALR, lb, nand_1_out, not_1_out, not_2_out, not_3_out, not_4_out, not_5_out, not_6_out,
       not_7_out, not_8_out, not_9_out, not_10_out, not_11_out, or_1_out, or_2_out, or_6_out, or_7_out,
       or_8_out, or_9_out, register_1_q, register_3_q, register_4_q, register_5_q, register_6_q,
       register_7_q, RST, RST_IRA, RST_IRB, RST_IRC, S_type, undriven, undriven_2, undriven_3, URET, W1, W2,
       W3, \中断信号产生_1_ir1与中断屏蔽位与 , \中断信号产生_1_ir2与中断屏蔽位与 , \中断信号产生_1_ir3与中断屏蔽位与 , \中断信号寄存器1_q , \中断信号寄存器2_q ,
       \中断信号寄存器3_q , \中断响应 , \单周期硬布线控制器_1_alu_src , \单周期硬布线控制器_1_memtoreg ;
  wire [1:0] priority_encoder_1_out;
  wire [2:0] decoder_1_out1;
  wire [3:0] \单周期硬布线控制器_1_alu_op ;
  wire [4:0] multiplexer_5_out, multiplexer_6_out;
  wire [12:0] CNT_num;
  wire [15:0] \总周期数 ;
  wire [31:0] adder_1_out, adder_2_out, alu_1_result, EPC, EPC1, EPC2, EPC3, ImmGen_imm, \l指令分线器_1_imm32_2 ,
       multiplexer_1_out, multiplexer_3_out, multiplexer_4_out, multiplexer_8_out, multiplexer_11_out,
       NextAddr, R1, ram_1_data, shifter_1_out, \中断程序入口地址 ;

  Clock #(.highDuration(1), .lowDuration(1)) clock_1 ();  // open: out
  Button _1 (.out(IRA));
  Button _2 (.out(IRB));
  Button _3 (.out(IRC));
  Button \u_继续运行  (.out(Go));
  LED #(.active("true")) led_1 (.in(W1));
  LED #(.active("true")) led_2 (.in(W2));
  LED #(.active("true")) led_3 (.in(W3));
  // Probe on \总周期数 
  Multiplexer #(.select(1), .width(32), .disabled("Z"), .enable("false")) multiplexer_1 (
    .in0(adder_2_out), .in1({multiplexer_11_out[31:1], 1'b0}), .out(multiplexer_1_out), .sel(JALR));
  Register #(.width(1), .trigger("rising"), .Select("low")) \IE已初始化  (
    .D(1'b1), .Q(\IE已初始化_q ), .clk(CLK));  // open: en, clr
  Hex_Digit_Display hex_digit_display_1 (.value(LedData[31:28]));  // open: dp
  // Probe on \总周期数 
  Multiplexer #(.select(1), .width(32), .disabled("Z"), .enable("false")) multiplexer_2 (
    .in0(adder_1_out), .in1(multiplexer_1_out), .out(NextAddr), .sel(or_7_out));
  not not_1 (not_1_out, register_1_q);
  Register #(.width(1), .trigger("rising"), .Select("low")) register_1 (
    .D(\IE已初始化_q ), .Q(register_1_q), .clk(CLK));  // open: en, clr
  Hex_Digit_Display hex_digit_display_2 (.value(LedData[23:20]));  // open: dp
  Hex_Digit_Display hex_digit_display_3 (.value(LedData[27:24]));  // open: dp
  and and_1 (and_1_out, not_1_out, \IE已初始化_q );
  Hex_Digit_Display hex_digit_display_4 (.value(LedData[19:16]));  // open: dp
  Hex_Digit_Display hex_digit_display_5 (.value(LedData[15:12]));  // open: dp
  Comparator #(.width(32), .mode("twosComplement")) comparator_1 (
    .a(R1), .b(32'h22), .eq(comparator_1_eq));  // open: gt, lt
  Multiplexer #(.select(1), .width(32), .disabled("Z"), .enable("false")) multiplexer_3 (
    .in0(NextAddr), .in1(\中断程序入口地址 ), .out(multiplexer_3_out), .sel(\中断响应 ));
  Multiplexer #(.select(1), .width(32), .disabled("Z"), .enable("false")) multiplexer_4 (
    .in0(multiplexer_3_out), .in1(EPC), .out(multiplexer_4_out), .sel(URET));
  Hex_Digit_Display hex_digit_display_6 (.value(LedData[11:8]));  // open: dp
  Hex_Digit_Display hex_digit_display_7 (.value(LedData[7:4]));  // open: dp
  // Probe on \总周期数 
  and and_2 (and_2_out, ecall, comparator_1_eq);
  not not_2 (not_2_out, comparator_1_eq);
  and and_3 (halt, not_2_out, ecall, not_3_out);
  not not_3 (not_3_out, Go);
  Register #(.width(32), .trigger("rising"), .Select("low")) u_PC (
    .D(multiplexer_4_out), .en(not_4_out), .Q(PC), .clk(CLK), .clr(RST));
  not not_4 (not_4_out, halt);
  and and_4 (and_4_out, register_3_q, CLK);
  or or_1 (or_1_out, and_1_out, URET, and_4_out);
  Register #(.width(1), .trigger("rising"), .Select("low")) \u_中断使能寄存器IE  (
    .Q(IE), .clk(CLK), .clr(or_2_out), .preset(or_1_out));  // open: D, en, cs
  or or_2 (or_2_out, and_6_out, and_5_out);
  and and_5 (and_5_out, register_4_q, CLK);
  and and_6 (and_6_out, \中断响应 , CLK);
  Hex_Digit_Display hex_digit_display_8 (.value(LedData[3:0]));  // open: dp
  Register #(.width(32), .trigger("rising"), .Select("low")) register_2 (
    .D(MDin), .en(and_2_out), .Q(LedData), .clk(CLK));  // open: clr
  \中断信号产生  \u_中断信号产生_1  (
    .CLK(CLK), .IR1(IR1_t), .W1(W1), .\同步清零信号 (RST_IRA), .IR2(IR2_t), .W2(W2), .\同步清零信号_2 (RST_IRB),
    .IR3(IR3_t), .W3(W3), .\同步清零信号_3 (RST_IRC), .\IR1与中断屏蔽位与 (\中断信号产生_1_ir1与中断屏蔽位与 ),
    .\IR2与中断屏蔽位与 (\中断信号产生_1_ir2与中断屏蔽位与 ), .\IR3与中断屏蔽位与 (\中断信号产生_1_ir3与中断屏蔽位与 ));
  Register #(.width(1), .trigger("rising"), .Select("low")) register_3 (
    .D(csrrsi), .Q(register_3_q), .clk(CLK));  // open: en, clr
  Register #(.width(1), .trigger("rising"), .Select("low")) register_4 (
    .D(csrrci), .Q(register_4_q), .clk(CLK));  // open: en, clr
  // RiscV_Probe riscv_probe_1: pin names not known; wires that end beside it: 32'h4, IR
  Adder #(.width(32)) adder_1 (.a(PC), .b(32'h4), .out(adder_1_out));  // open: cin, cout
  or or_3 (IR1_t, IR1, IRA);
  D_Flip_Flop #(.trigger("high"), .Pre_Clr_Positions("LEGACY"), .NegatePresetClear("false"), .enable("true"), .NewFFLayout("false")) d_ff_1 (.Q(d_ff_1_q));  // open: clk, D, Qn, preset, en, reset
  // Probe on 13'h10
  ROM #(.addrWidth(10), .dataWidth(32), .Select("high")) rom_1 (.addr(PC[11:2]), .data(IR));
  Register #(.width(1), .trigger("rising"), .Select("low")) register_5 (
    .D(\中断信号产生_1_ir1与中断屏蔽位与 ), .Q(register_5_q), .clk(CLK));  // open: en, clr
  or or_4 (IR2_t, IR2, IRB);
  Comparator #(.width(13), .mode("twosComplement")) comparator_2 (
    .a(CNT_num), .b(13'h10), .eq(comparator_2_eq), .lt(comparator_2_lt));  // open: gt
  Clock #(.highDuration(1), .lowDuration(1)) clock_2 (.out(clock_2_out));
  and and_7 (and_7_out, \中断信号产生_1_ir1与中断屏蔽位与 , not_5_out);
  not not_5 (not_5_out, register_5_q);
  not not_6 (not_6_out, register_6_q);
  Register #(.width(1), .trigger("rising"), .Select("low")) register_6 (
    .D(\中断信号产生_1_ir2与中断屏蔽位与 ), .Q(register_6_q), .clk(CLK));  // open: en, clr
  Register #(.width(1), .trigger("rising"), .Select("low")) register_7 (
    .D(\中断信号产生_1_ir3与中断屏蔽位与 ), .Q(register_7_q), .clk(CLK));  // open: en, clr
  not not_7 (not_7_out, register_7_q);
  nand nand_1 (nand_1_out, d_ff_1_q, comparator_2_eq);
  Counter #(.width(13), .max('h1fff), .ongoal("stay"), .trigger("rising"), .behavior("old")) counter_1 (
    .count(comparator_2_lt), .Q(CNT_num), .clk(clock_2_out));  // open: load, D, carry, clr, preset
  \单周期硬布线控制器  \u_单周期硬布线控制器_1  (
    .Funct({IR[30], IR[25], IR[14:12]}), .OP(IR[6:2]), .ALU_OP(\单周期硬布线控制器_1_alu_op ),
    .MemToReg(\单周期硬布线控制器_1_memtoreg ), .MemWrite(MemWrite), .ALU_SRC(\单周期硬布线控制器_1_alu_src ),
    .RegWrite(RegWrite), .ecall(ecall), .S_type(S_type), .Jalr(JALR), .Beq(Beq), .JAL(JAL), .Bne(Bne),
    .in_3(IR[21]), .uret(URET), .BGUE(Bgeu), .lb(lb), .csrrsi(csrrsi), .csrrci(csrrci));
  Multiplexer #(.select(1), .width(5), .disabled("Z"), .enable("false")) multiplexer_5 (
    .in0(IR[19:15]), .in1(5'b10001), .out(multiplexer_5_out), .sel(ecall));
  Multiplexer #(.select(1), .width(5), .disabled("Z"), .enable("false")) multiplexer_6 (
    .in0(IR[24:20]), .in1(5'b01010), .out(multiplexer_6_out), .sel(ecall));
  and and_8 (and_8_out, and_7_out, CLK);
  and and_9 (and_9_out, CLK, \_1号中断响应 );
  and and_10 (and_10_out, \中断信号产生_1_ir2与中断屏蔽位与 , not_6_out);
  and and_11 (and_11_out, and_10_out, CLK);
  and and_12 (and_12_out, CLK, \_2号中断响应 );
  and and_13 (and_13_out, \中断信号产生_1_ir3与中断屏蔽位与 , not_7_out);
  and and_14 (and_14_out, and_13_out, CLK);
  and and_15 (and_15_out, CLK, \_3号中断响应 );
  or or_5 (IR3_t, IR3, IRC);
  assign CLK = nand_1_out ? clock_2_out : 1'bz;  // Controlled_Buffer controlled_buffer_1
  Counter #(.width(16), .max('hffff), .ongoal("wrap"), .trigger("rising"), .behavior("new")) counter_2 (
    .count(nand_1_out), .Q(\总周期数 ), .clk(clock_2_out));  // open: load, D, carry, clr, preset, down
  \ImmGen_封装版  ImmGen (.IR(IR), .Imm(ImmGen_imm));
  Multiplexer #(.select(1), .width(32), .disabled("Z"), .enable("false")) multiplexer_7 (
    .in0(multiplexer_11_out), .in1(adder_1_out), .out(RDin), .sel(or_6_out));
  or or_6 (or_6_out, JAL, JALR);
  Priority_Encoder #(.select(2), .disabled("Z")) priority_encoder_1 (
    .in0(1'b1), .in1(\中断信号产生_1_ir1与中断屏蔽位与 ), .in2(\中断信号产生_1_ir2与中断屏蔽位与 ), .in3(\中断信号产生_1_ir3与中断屏蔽位与 ),
    .out(priority_encoder_1_out), .en_in(1'b1));  // open: gs, en_out
  Register #(.width(1), .trigger("rising"), .Select("low")) \u_中断信号寄存器1  (
    .Q(\中断信号寄存器1_q ), .clr(and_9_out), .preset(and_8_out));  // open: D, en, clk, cs
  Register #(.width(1), .trigger("rising"), .Select("low")) \u_中断信号寄存器2  (
    .Q(\中断信号寄存器2_q ), .clr(and_12_out), .preset(and_11_out));  // open: D, en, clk, cs
  Register #(.width(1), .trigger("rising"), .Select("low")) \u_中断信号寄存器3  (
    .Q(\中断信号寄存器3_q ), .clr(and_15_out), .preset(and_14_out));  // open: D, en, clk, cs
  Pull_Resistor #(.pull(1)) pull_resistor_1 (.node(CLK));
  Regifile regifile_1 (
    .Din(RDin), .Clk(CLK), .R1(R1), .R2(MDin), .WE(RegWrite), .W_num(IR[11:7]), .R1_num(multiplexer_5_out),
    .R2_num(multiplexer_6_out));
  and and_16 (and_16_out, \中断信号寄存器1_q , IE);
  and and_17 (and_17_out, and_16_out, CLK);
  and and_18 (and_18_out, CLK, \_1号中断已响应 );
  and and_19 (and_19_out, \中断信号寄存器2_q , IE);
  and and_20 (and_20_out, and_19_out, CLK);
  and and_21 (and_21_out, CLK, \_2号中断已响应 );
  and and_22 (and_22_out, \中断信号寄存器3_q , IE);
  and and_23 (and_23_out, and_22_out, CLK);
  and and_24 (and_24_out, CLK, \_3号中断已响应 );
  Multiplexer #(.select(1), .width(32), .disabled("Z"), .enable("false")) multiplexer_8 (
    .in0(MDin), .in1(ImmGen_imm), .out(multiplexer_8_out), .sel(\单周期硬布线控制器_1_alu_src ));
  Shifter #(.width(32), .shift("ll")) shifter_1 (.in(ImmGen_imm), .\dist (5'b00001), .out(shifter_1_out));
  Multiplexer #(.select(2), .width(32), .disabled("Z"), .enable("false")) multiplexer_9 (
    .in1(32'h30ac), .in2(32'h3158), .in3(32'h3204), .out(\中断程序入口地址 ), .sel(priority_encoder_1_out));  // open: in0
  Register #(.width(1), .trigger("rising"), .Select("low")) register_8 (
    .D(undriven), .Q(\_1号中断响应 ), .clr(and_18_out), .cs(undriven), .preset(and_17_out));  // open: en, clk
  Register #(.width(1), .trigger("rising"), .Select("low")) register_9 (
    .D(undriven_2), .Q(\_2号中断响应 ), .clr(and_21_out), .cs(undriven_2), .preset(and_20_out));  // open: en, clk
  Register #(.width(1), .trigger("rising"), .Select("low")) register_10 (
    .D(undriven_3), .Q(\_3号中断响应 ), .clr(and_24_out), .cs(undriven_3), .preset(and_23_out));  // open: en, clk
  ALU alu_1 (
    .X(R1), .Y(multiplexer_8_out), .AluOP(\单周期硬布线控制器_1_alu_op ), .Equal(alu_1_equal), .Result(alu_1_result),
    .out_4(alu_1_out_4));  // open: Result_2, out_6
  Adder #(.width(32)) adder_2 (.a(shifter_1_out), .b(PC), .out(adder_2_out));  // open: cin, cout
  not not_8 (not_8_out, alu_1_equal);
  and and_25 (and_25_out, Beq, alu_1_equal);
  and and_26 (and_26_out, Bne, not_8_out);
  and and_27 (and_27_out, Bgeu, alu_1_out_4);
  RAM #(.addrWidth(10), .dataWidth(32), .bus("separate"), .Select("low")) ram_1 (
    .addr(alu_1_result[11:2]), .din(MDin), .data(ram_1_data), .str(MemWrite), .clk(CLK));  // open: sel, ld, clr
  Decoder #(.select(2), .tristate("false"), .disabled("Z"), .enable("false")) decoder_1 (
    .out1(decoder_1_out1[0]), .out2(decoder_1_out1[1]), .out3(decoder_1_out1[2]), .sel(priority_encoder_1_out));  // open: out0
  not not_9 (not_9_out, CLK);
  or or_7 (or_7_out, and_25_out, and_26_out, JAL, JALR, and_27_out);
  \L指令分线器  \l指令分线器_1  (.lb(lb), .Imm32_2(\l指令分线器_1_imm32_2 ), .Imm32(ram_1_data), .offset(alu_1_result[1:0]));
  Multiplexer #(.select(3), .width(32), .disabled("Z"), .enable("false")) multiplexer_10 (
    .in1(EPC1), .in2(EPC2), .in3(EPC2), .in4(EPC3), .in5(EPC3), .in6(EPC3), .in7(EPC3), .out(EPC),
    .sel(decoder_1_out1));  // open: in0
  Register #(.width(32), .trigger("rising"), .Select("low")) u_EPC1 (
    .D(NextAddr), .en(\_1号中断响应 ), .Q(EPC1), .clk(not_9_out));  // open: clr
  Register #(.width(32), .trigger("rising"), .Select("low")) u_EPC2 (
    .D(NextAddr), .en(\_2号中断响应 ), .Q(EPC2), .clk(not_10_out));  // open: clr
  not not_10 (not_10_out, CLK);
  Register #(.width(32), .trigger("rising"), .Select("low")) u_EPC3 (
    .D(NextAddr), .en(\_3号中断响应 ), .Q(EPC3), .clk(not_11_out));  // open: clr
  not not_11 (not_11_out, CLK);
  Multiplexer #(.select(1), .width(32), .disabled("Z"), .enable("false")) multiplexer_11 (
    .in0(alu_1_result), .in1(\l指令分线器_1_imm32_2 ), .out(multiplexer_11_out), .sel(\单周期硬布线控制器_1_memtoreg ));
  and and_28 (RST_IRA, decoder_1_out1[0], URET);
  and and_29 (RST_IRB, decoder_1_out1[1], URET);
  and and_30 (RST_IRC, decoder_1_out1[2], URET);
  Comparator #(.width(16), .mode("twosComplement")) comparator_3 (
    .a(16'h258), .b(\总周期数 ), .eq(comparator_3_eq));  // open: gt, lt
  Comparator #(.width(16), .mode("twosComplement")) comparator_4 (
    .a(\总周期数 ), .b(16'h1), .eq(comparator_4_eq));  // open: gt, lt
  Comparator #(.width(16), .mode("twosComplement")) comparator_5 (
    .a(\总周期数 ), .b(16'h4), .eq(comparator_5_eq));  // open: gt, lt
  Comparator #(.width(16), .mode("twosComplement")) comparator_6 (
    .a(\总周期数 ), .b(16'h7), .eq(comparator_6_eq));  // open: gt, lt
  Comparator #(.width(16), .mode("twosComplement")) comparator_7 (
    .a(\总周期数 ), .b(16'h241), .eq(comparator_7_eq));  // open: gt, lt
  or or_8 (or_8_out, comparator_3_eq, comparator_4_eq);
  assign controlled_inverter_1_out = or_8_out ? ~CLK : 1'bz;  // Controlled_Inverter controlled_inverter_1
  assign controlled_inverter_2_out = comparator_5_eq ? ~CLK : 1'bz;  // Controlled_Inverter controlled_inverter_2
  or or_9 (or_9_out, comparator_6_eq, comparator_7_eq);
  assign controlled_inverter_3_out = or_9_out ? ~CLK : 1'bz;  // Controlled_Inverter controlled_inverter_3
  Pull_Resistor #(.pull(0)) pull_resistor_2 (.node(controlled_inverter_1_out));
  Pull_Resistor #(.pull(0)) pull_resistor_3 (.node(controlled_inverter_2_out));
  Pull_Resistor #(.pull(0)) pull_resistor_4 (.node(controlled_inverter_3_out));
  and and_31 (and_31_out, \_1号中断响应 , ~In2_Exist, ~In3_Exist);  // AND_Gate
  and and_32 (and_32_out, \_2号中断响应 , ~In3_Exist);  // AND_Gate
  Comparator #(.width(32), .mode("twosComplement")) comparator_8 (
    .a(PC), .b(32'h30ac), .eq(\_1号中断已响应 ));  // open: gt, lt
  Comparator #(.width(32), .mode("twosComplement")) comparator_9 (
    .a(PC), .b(32'h3158), .eq(\_2号中断已响应 ));  // open: gt, lt
  Comparator #(.width(32), .mode("twosComplement")) comparator_10 (
    .a(PC), .b(32'h3204), .eq(\_3号中断已响应 ));  // open: gt, lt
  or or_10 (\中断响应 , and_31_out, and_32_out, \_3号中断响应 );
  Register #(.width(1), .trigger("rising"), .Select("low")) u_In2_Exist (
    .Q(In2_Exist), .clr(and_34_out), .preset(and_33_out));  // open: D, en, clk, cs
  and and_33 (and_33_out, CLK, \_2号中断已响应 );
  and and_34 (and_34_out, CLK, comparator_11_eq);
  Comparator #(.width(32), .mode("twosComplement")) comparator_11 (
    .a(PC), .b(32'h3200), .eq(comparator_11_eq));  // open: gt, lt
  and and_35 (and_35_out, CLK, \_3号中断已响应 );
  Register #(.width(1), .trigger("rising"), .Select("low")) u_In3_Exist (
    .Q(In3_Exist), .clr(and_36_out), .preset(and_35_out));  // open: D, en, clk, cs
  and and_36 (and_36_out, CLK, comparator_12_eq);
  Comparator #(.width(32), .mode("twosComplement")) comparator_12 (
    .a(PC), .b(32'h32ac), .eq(comparator_12_eq));  // open: gt, lt

  // Other names for the same wires on the sheet: R2[31:0] = MDin

  // Notes on the sheet:
  //   中断源
  //   中断等待指示
  //   总复位信号应将除ROM以外所有存储组件全部清零
  //   如果出现中断请求信号 且IE=1 进入中断程序
  //   进入中断程序 关中断
  //   csrrsi 开中断
  //   csrrci 关中断
  //   URET 开中断
  //   数码管输出
  //   数码管输出应该用寄存器锁存，否则显示数据只能一闪而过
  //   否则 将中断请求信号存在中断请求寄存器中
  //   控制位
  //   指令探针
  //   指令存储器
  //   PC+4
  //   暂停节拍，不能为0
  //   指令字
  //   contents of rom_1 (hex, n*v repeats v):
  //   7d000113 100413 1f41993 41f9d993 433 c00913 800b13 140413 f47413 800293 100313 499993 89e9b3 1300533
  //   2200893 73 406282b3 fe0294e3 140413 f00f93 1f47433 1c41413 800293 100313 49d993 89e9b3 1300533
  //   2200893 73 406282b3 fe0294e3 1c45413 406b0b33 b0463 f95ff06f 2b3 fff2c293 1029293 fff2e293 500533
  //   2200893 73 f5dff06f 1112023 410113 a12023 410113 812023 410113 1312023 410113 1412023 410113 1512023
  //   410113 1612023 410113 40e073 100b13 300a13 100a93 1600433 441413 14469b3 1300533 2200893 73 fe0416e3
  //   415a0a33 fe0a10e3 40f073 ffc10113 12b03 ffc10113 12a83 ffc10113 12a03 ffc10113 12983 ffc10113 12403
  //   ffc10113 12503 ffc10113 12883 200073 1112023 410113 a12023 410113 812023 410113 1312023 410113
  //   1412023 410113 1512023 410113 1612023 410113 40e073 200b13 300a13 100a93 1600433 441413 14469b3
  //   1300533 2200893 73 fe0416e3 415a0a33 fe0a10e3 40f073 ffc10113 12b03 ffc10113 12a83 ffc10113 12a03
  //   ffc10113 12983 ffc10113 12403 ffc10113 12503 ffc10113 12883 200073 1112023 410113 a12023 410113
  //   812023 410113 1312023 410113 1412023 410113 1512023 410113 1612023 410113 40e073 300b13 300a13
  //   100a93 1600433 441413 14469b3 1300533 2200893 73 fe0416e3 415a0a33 fe0a10e3 40f073 ffc10113 12b03
  //   ffc10113 12a83 ffc10113 12a03 ffc10113 12983 ffc10113 12403 ffc10113 12503 ffc10113 12883 200073
  //   PC
  //   JAL
  //   JALR
  //   MemToReg
  //   MemWrite
  //   AluOP
  //   AluSrcB
  //   RegWrite
  //   可计数暂停的时钟源
  //   已响应1号中断，进入1号中断程序
  //   为方便自动评测，需要输出PC，IR，寄存器堆写如数据RDin
  //   RAM写使能MemWrite、RAM写入数据MDin等信号
  //   数据存储器
  //   多级中断测试信号模拟器
endmodule

module \流水线中断  (
  input  IR1,
  input  IR2,
  input  IR3
);

  wire \_1号中断响应 , \_1号中断已响应 , \_2号中断响应 , \_2号中断已响应 , \_3号中断响应 , \_3号中断已响应 , alu_1_equal, alu_1_out_4,
       AluSrcB, and_1_out, and_2_out, and_3_out, and_4_out, and_5_out, and_6_out, and_7_out, and_8_out,
       and_9_out, and_10_out, and_11_out, and_12_out, and_13_out, and_14_out, and_15_out, and_16_out,
       and_17_out, and_18_out, and_19_out, and_20_out, and_21_out, and_22_out, and_23_out, and_24_out,
       and_29_out, and_30_out, and_31_out, and_32_out, and_33_out, and_37_out, and_38_out, and_39_out,
       and_40_out, Beq, Bgeu, Bne, btb_1_predictjump, CLK, clock_1_out, comparator_1_eq, comparator_2_eq,
       comparator_3_eq, comparator_4_eq, comparator_4_lt, comparator_5_eq, comparator_6_eq, comparator_7_eq,
       comparator_8_eq, comparator_9_eq, comparator_10_eq, comparator_11_eq, comparator_12_eq,
       controlled_inverter_1_out, controlled_inverter_2_out, controlled_inverter_3_out, csrrci, csrrsi,
       d_ff_1_q, ecall, EX_Branch, EX_BranchTaken, EX_csrrci, EX_csrrsi, EX_ecall, EX_MEM_jal_2,
       EX_MEM_jalr_2, EX_MEM_lb_2, EX_MEM_memtoreg_2, EX_MEM_regwrite_2, EX_URET, Flush, Go, halt,
       ID_EX_alusrc_2, ID_EX_beq_2, ID_EX_bgeu_2, ID_EX_bne_2, ID_EX_jal_2, ID_EX_jalr_2, ID_EX_lb_2,
       ID_EX_memtoreg_2, ID_EX_memwrite_2, ID_EX_regwrite_2, IE, \IE已初始化_q , IF_ID_predictjump_2, In2_Exist,
       In3_Exist, IR1_t, IR2_t, IR3_t, IRA, IRB, IRC, JAL, JALR, lb, MEM_MemWrite, MEM_URET,
       MEM_WB_memtoreg_2, MEM_WB_regwrite_2, MemToReg, MemWrite, nand_1_out, not_1_out, not_2_out, not_3_out,
       not_4_out, not_5_out, not_6_out, not_7_out, not_8_out, not_9_out, not_10_out, not_11_out, not_12_out,
       not_13_out, not_14_out, not_15_out, not_16_out, or_4_out, or_5_out, or_6_out, or_7_out, or_8_out,
       or_9_out, or_10_out, PredictErr, PredictJump, register_1_q, register_2_q, register_3_q, register_4_q,
       register_5_q, register_6_q, RegWrite, RST, RST_IRA, RST_IRB, RST_IRC, S_type, Stall, undriven,
       undriven_2, undriven_3, URET, W1, W2, W3, WB_JAL, WB_JALR, \中断信号产生_1_ir1与中断屏蔽位与 ,
       \中断信号产生_1_ir2与中断屏蔽位与 , \中断信号产生_1_ir3与中断屏蔽位与 , \中断信号寄存器1_q , \中断信号寄存器2_q , \中断信号寄存器3_q , \中断响应 ,
       \相关处理逻辑_重定向_1_id_ex_clr , \相关处理逻辑_重定向_1_if_id_clr ;
  wire [0:0] alu_1_result;
  wire [1:0] ID_EX_rsforward_2, ID_EX_rtforward_2, priority_encoder_1_out, \相关处理逻辑_重定向_1_r1forward ,
       \相关处理逻辑_重定向_1_r2forward ;
  wire [2:0] decoder_1_out1;
  wire [3:0] AluOP, ID_EX_aluop_2;
  wire [4:0] EX_MEM_writereg_num_2, ID_EX_writereg_num_2, MEM_WB_writereg_num_2, multiplexer_7_out,
       multiplexer_8_out;
  wire [12:0] CNT_num;
  wire [15:0] \总周期数 ;
  wire [30:0] alu_1_result_2;
  wire [31:0] adder_1_out, adder_2_out, BranchAddr, btb_1_jumpaddr, EPC, EPC1, EPC2, EPC3, EX_IR,
       EX_MEM_aluresult_2, EX_MEM_pc_4_2, EX_PC, EX_PC_4, ID_EX_r1_2, ID_EX_r2_2, ID_EX_signimm_2, ID_IR,
       ID_PC, IF_ID_pc_4_2, IF_IR, IF_PC, \immgen_封装版_1_imm , LedData, \l指令分线器_1_imm32_2 , MDin, MEM_IR,
       MEM_PC, MEM_WB_aluresult_2, MEM_WB_pc_4_2, MEM_WB_readdata_2, multiplexer_2_out, multiplexer_3_out,
       multiplexer_4_out, multiplexer_5_out, multiplexer_6_out, multiplexer_11_out, multiplexer_15_out,
       multiplexer_17_out, NextAddr, R1, R2, ram_1_data, RDin, regifile_1_r1, regifile_1_r2, shifter_1_out,
       WB_IR, WB_PC, \中断程序入口地址 ;

  Button \u_总复位  (.out(RST));
  Button _1 (.out(IRA));
  Button _2 (.out(IRB));
  Button _3 (.out(IRC));
  // Probe on \总周期数 
  // Probe on \总周期数 
  Multiplexer #(.select(1), .width(32), .disabled("Z"), .enable("false")) multiplexer_1 (
    .in0(adder_2_out), .in1({alu_1_result_2, 1'b0}), .out(BranchAddr), .sel(ID_EX_jalr_2));
  or or_1 (IR1_t, IR1, IRA);
  Button \u_继续运行  (.out(Go));
  LED #(.active("true")) led_1 (.in(W1));
  LED #(.active("true")) led_2 (.in(W2));
  LED #(.active("true")) led_3 (.in(W3));
  Multiplexer #(.select(1), .width(32), .disabled("Z"), .enable("false")) multiplexer_2 (
    .in0(EX_PC_4), .in1(BranchAddr), .out(multiplexer_2_out), .sel(EX_BranchTaken));
  Hex_Digit_Display hex_digit_display_1 (.value(LedData[31:28]));  // open: dp
  // Probe on IF_PC[19:0]
  // RiscV_Probe riscv_probe_1: pin names not known; wires that end beside it: IF_IR
  Multiplexer #(.select(1), .width(32), .disabled("Z"), .enable("false")) multiplexer_3 (
    .in0(multiplexer_6_out), .in1(multiplexer_2_out), .out(multiplexer_3_out), .sel(PredictErr));
  or or_2 (IR2_t, IR2, IRB);
  Hex_Digit_Display hex_digit_display_2 (.value(LedData[27:24]));  // open: dp
  Hex_Digit_Display hex_digit_display_3 (.value(LedData[23:20]));  // open: dp
  // Probe on ID_PC[19:0]
  // RiscV_Probe riscv_probe_2: pin names not known; wires that end beside it: ID_IR
  Register #(.width(1), .trigger("rising"), .Select("low")) \IE已初始化  (
    .D(1'b1), .Q(\IE已初始化_q ), .clk(CLK));  // open: en, clr
  Hex_Digit_Display hex_digit_display_4 (.value(LedData[15:12]));  // open: dp
  Hex_Digit_Display hex_digit_display_5 (.value(LedData[19:16]));  // open: dp
  Multiplexer #(.select(1), .width(32), .disabled("Z"), .enable("false")) multiplexer_4 (
    .in0(multiplexer_3_out), .in1(\中断程序入口地址 ), .out(multiplexer_4_out), .sel(\中断响应 ));
  Multiplexer #(.select(1), .width(32), .disabled("Z"), .enable("false")) multiplexer_5 (
    .in0(multiplexer_4_out), .in1(EPC), .out(multiplexer_5_out), .sel(EX_URET));
  Register #(.width(1), .trigger("rising"), .Select("low")) register_1 (
    .D(\IE已初始化_q ), .Q(register_1_q), .clk(CLK));  // open: en, clr
  not not_1 (not_1_out, register_1_q);
  or or_3 (IR3_t, IR3, IRC);
  Hex_Digit_Display hex_digit_display_6 (.value(LedData[7:4]));  // open: dp
  Hex_Digit_Display hex_digit_display_7 (.value(LedData[11:8]));  // open: dp
  // Probe on EX_PC[19:0]
  // RiscV_Probe riscv_probe_3: pin names not known; wires that end beside it: EX_IR
  Register #(.width(32), .trigger("rising"), .Select("low")) PC (
    .D(multiplexer_5_out), .en(not_2_out), .Q(IF_PC), .clk(CLK), .clr(RST));
  not not_2 (not_2_out, or_4_out);
  or or_4 (or_4_out, halt, Stall);
  BTB btb_1 (
    .PC(IF_PC), .EX_PC(EX_PC), .BranchAddr(BranchAddr), .EX_Branch(EX_Branch),
    .EX_BranchTaken(EX_BranchTaken), .JumpAddr(btb_1_jumpaddr), .PredictJump(btb_1_predictjump), .CLK(CLK));
  Multiplexer #(.select(1), .width(32), .disabled("Z"), .enable("false")) multiplexer_6 (
    .in0(adder_1_out), .in1(btb_1_jumpaddr), .out(multiplexer_6_out), .sel(btb_1_predictjump));
  and and_1 (and_1_out, not_1_out, \IE已初始化_q );
  Hex_Digit_Display hex_digit_display_8 (.value(LedData[3:0]));  // open: dp
  // Probe on MEM_PC[19:0]
  // RiscV_Probe riscv_probe_4: pin names not known; wires that end beside it: MEM_IR
  and and_2 (and_2_out, register_2_q, CLK);
  or or_5 (or_5_out, and_1_out, EX_URET, and_2_out);
  Register #(.width(1), .trigger("rising"), .Select("low")) \u_中断使能寄存器IE  (
    .Q(IE), .clk(CLK), .clr(or_6_out), .preset(or_5_out));  // open: D, en, cs
  or or_6 (or_6_out, and_4_out, and_3_out);
  and and_3 (and_3_out, register_3_q, CLK);
  and and_4 (and_4_out, \中断响应 , CLK);
  Comparator #(.width(16), .mode("twosComplement")) comparator_1 (
    .a(\总周期数 ), .b(16'h1), .eq(comparator_1_eq));  // open: gt, lt
  Comparator #(.width(16), .mode("twosComplement")) comparator_2 (
    .a(\总周期数 ), .b(16'h7), .eq(comparator_2_eq));  // open: gt, lt
  Comparator #(.width(16), .mode("twosComplement")) comparator_3 (
    .a(\总周期数 ), .b(16'h4), .eq(comparator_3_eq));  // open: gt, lt
  \中断信号产生  \u_中断信号产生_1  (
    .CLK(CLK), .IR1(IR1_t), .W1(W1), .\同步清零信号 (RST_IRA), .IR2(IR2_t), .W2(W2), .\同步清零信号_2 (RST_IRB),
    .IR3(IR3_t), .W3(W3), .\同步清零信号_3 (RST_IRC), .\IR1与中断屏蔽位与 (\中断信号产生_1_ir1与中断屏蔽位与 ),
    .\IR2与中断屏蔽位与 (\中断信号产生_1_ir2与中断屏蔽位与 ), .\IR3与中断屏蔽位与 (\中断信号产生_1_ir3与中断屏蔽位与 ));
  assign controlled_inverter_1_out = comparator_1_eq ? ~CLK : 1'bz;  // Controlled_Inverter controlled_inverter_1
  assign controlled_inverter_2_out = comparator_2_eq ? ~CLK : 1'bz;  // Controlled_Inverter controlled_inverter_2
  assign controlled_inverter_3_out = comparator_3_eq ? ~CLK : 1'bz;  // Controlled_Inverter controlled_inverter_3
  // Probe on WB_PC[19:0]
  // RiscV_Probe riscv_probe_5: pin names not known; wires that end beside it: WB_IR, IRA, IRB, IRC
  not not_3 (not_3_out, MEM_URET);
  ROM #(.addrWidth(10), .dataWidth(32), .Select("high")) rom_1 (.addr(IF_PC[11:2]), .data(IF_IR));
  Adder #(.width(32)) adder_1 (.a(IF_PC), .b(32'h4), .out(adder_1_out));  // open: cin, cout
  Register #(.width(1), .trigger("rising"), .Select("low")) register_2 (
    .D(EX_csrrsi), .Q(register_2_q), .clk(CLK));  // open: en, clr
  Register #(.width(1), .trigger("rising"), .Select("low")) register_3 (
    .D(EX_csrrci), .Q(register_3_q), .clk(CLK));  // open: en, clr
  Pull_Resistor #(.pull(0)) pull_resistor_1 (.node(controlled_inverter_1_out));
  Pull_Resistor #(.pull(0)) pull_resistor_2 (.node(controlled_inverter_2_out));
  Pull_Resistor #(.pull(0)) pull_resistor_3 (.node(controlled_inverter_3_out));
  \相关处理逻辑_重定向  \u_相关处理逻辑_重定向_1  (
    .ID_IR(ID_IR), .EX_WriteReg_num(ID_EX_writereg_num_2), .EX_WriteReg(ID_EX_regwrite_2),
    .MEM_WriteReg_num(EX_MEM_writereg_num_2), .MEM_WriteReg(EX_MEM_regwrite_2),
    .EX_MemRead(ID_EX_memtoreg_2), .BranchTaken(EX_BranchTaken), .R1Forward(\相关处理逻辑_重定向_1_r1forward ),
    .R2Forward(\相关处理逻辑_重定向_1_r2forward ), .Stall(Stall), .Flush(Flush), .PredictErr(PredictErr),
    .IF_ID_CLR(\相关处理逻辑_重定向_1_if_id_clr ), .ID_EX_CLR(\相关处理逻辑_重定向_1_id_ex_clr ));
  and and_5 (and_5_out, not_3_out, \中断响应 );
  or or_7 (or_7_out, Stall, halt);
  // RiscV_Probe riscv_probe_6: pin names not known; wires that end beside it: ID_IR
  D_Flip_Flop #(.trigger("high"), .Pre_Clr_Positions("LEGACY"), .NegatePresetClear("false"), .enable("true"), .NewFFLayout("false")) d_ff_1 (.Q(d_ff_1_q));  // open: clk, D, Qn, preset, en, reset
  // Probe on 13'h10
  or or_8 (or_8_out, and_5_out, EX_URET, \相关处理逻辑_重定向_1_if_id_clr );
  not not_4 (not_4_out, or_7_out);
  IF_ID IF_ID (
    .IR(IF_IR), .PC_4(adder_1_out), .IR_2(ID_IR), .PC_4_2(IF_ID_pc_4_2), .CLK(CLK), .PC(IF_PC), .PC_2(ID_PC),
    .CLR(or_8_out), .EN(not_4_out), .PredictJump(btb_1_predictjump), .PredictJump_2(IF_ID_predictjump_2));
  not not_5 (not_5_out, register_4_q);
  Register #(.width(1), .trigger("rising"), .Select("low")) register_4 (
    .D(\中断信号产生_1_ir1与中断屏蔽位与 ), .Q(register_4_q), .clk(CLK));  // open: en, clr
  not not_6 (not_6_out, register_5_q);
  Register #(.width(1), .trigger("rising"), .Select("low")) register_5 (
    .D(\中断信号产生_1_ir2与中断屏蔽位与 ), .Q(register_5_q), .clk(CLK));  // open: en, clr
  Register #(.width(1), .trigger("rising"), .Select("low")) register_6 (
    .D(\中断信号产生_1_ir3与中断屏蔽位与 ), .Q(register_6_q), .clk(CLK));  // open: en, clr
  not not_7 (not_7_out, register_6_q);
  Comparator #(.width(13), .mode("twosComplement")) comparator_4 (
    .a(CNT_num), .b(13'h10), .eq(comparator_4_eq), .lt(comparator_4_lt));  // open: gt
  Clock #(.highDuration(1), .lowDuration(1)) clock_1 (.out(clock_1_out));
  and and_6 (and_6_out, \中断信号产生_1_ir1与中断屏蔽位与 , not_5_out);
  and and_7 (and_7_out, and_6_out, CLK);
  and and_8 (and_8_out, CLK, \_1号中断响应 );
  and and_9 (and_9_out, \中断信号产生_1_ir2与中断屏蔽位与 , not_6_out);
  and and_10 (and_10_out, \中断信号产生_1_ir3与中断屏蔽位与 , not_7_out);
  nand nand_1 (nand_1_out, d_ff_1_q, comparator_4_eq);
  Counter #(.width(13), .max('h1fff), .ongoal("stay"), .trigger("rising"), .behavior("old")) counter_1 (
    .count(comparator_4_lt), .Q(CNT_num), .clk(clock_1_out));  // open: load, D, carry, clr, preset
  Priority_Encoder #(.select(2), .disabled("Z")) priority_encoder_1 (
    .in0(1'b1), .in1(\中断信号产生_1_ir1与中断屏蔽位与 ), .in2(\中断信号产生_1_ir2与中断屏蔽位与 ), .in3(\中断信号产生_1_ir3与中断屏蔽位与 ),
    .out(priority_encoder_1_out), .en_in(1'b1));  // open: gs, en_out
  Register #(.width(1), .trigger("rising"), .Select("low")) \u_中断信号寄存器1  (
    .Q(\中断信号寄存器1_q ), .clr(and_8_out), .preset(and_7_out));  // open: D, en, clk, cs
  and and_11 (and_11_out, and_9_out, CLK);
  Register #(.width(1), .trigger("rising"), .Select("low")) \u_中断信号寄存器2  (
    .Q(\中断信号寄存器2_q ), .clr(and_12_out), .preset(and_11_out));  // open: D, en, clk, cs
  and and_12 (and_12_out, CLK, \_2号中断响应 );
  and and_13 (and_13_out, and_10_out, CLK);
  Register #(.width(1), .trigger("rising"), .Select("low")) \u_中断信号寄存器3  (
    .Q(\中断信号寄存器3_q ), .clr(and_14_out), .preset(and_13_out));  // open: D, en, clk, cs
  and and_14 (and_14_out, CLK, \_3号中断响应 );
  Counter #(.width(16), .max('hffff), .ongoal("wrap"), .trigger("rising"), .behavior("new")) counter_2 (
    .count(nand_1_out), .Q(\总周期数 ), .clk(clock_1_out));  // open: load, D, carry, clr, preset, down
  \单周期硬布线控制器  \u_单周期硬布线控制器_1  (
    .Funct({ID_IR[30], ID_IR[25], ID_IR[14:12]}), .OP(ID_IR[6:2]), .ALU_OP(AluOP), .MemToReg(MemToReg),
    .MemWrite(MemWrite), .ALU_SRC(AluSrcB), .RegWrite(RegWrite), .ecall(ecall), .S_type(S_type), .Jalr(JALR),
    .Beq(Beq), .JAL(JAL), .Bne(Bne), .in_3(ID_IR[21]), .uret(URET), .BGUE(Bgeu), .lb(lb), .csrrsi(csrrsi),
    .csrrci(csrrci));
  Multiplexer #(.select(1), .width(5), .disabled("Z"), .enable("false")) multiplexer_7 (
    .in0(ID_IR[19:15]), .in1(5'b10001), .out(multiplexer_7_out), .sel(ecall));
  Multiplexer #(.select(1), .width(5), .disabled("Z"), .enable("false")) multiplexer_8 (
    .in0(ID_IR[24:20]), .in1(5'b01010), .out(multiplexer_8_out), .sel(ecall));
  assign CLK = nand_1_out ? clock_1_out : 1'bz;  // Controlled_Buffer controlled_buffer_1
  Pull_Resistor #(.pull(1)) pull_resistor_4 (.node(CLK));
  \ImmGen_封装版  \immgen_封装版_1  (.IR(ID_IR), .Imm(\immgen_封装版_1_imm ));
  Multiplexer #(.select(1), .width(32), .disabled("Z"), .enable("false")) multiplexer_9 (
    .in0(multiplexer_17_out), .in1(MEM_WB_pc_4_2), .out(RDin), .sel(or_9_out));
  and and_15 (and_15_out, \中断信号寄存器1_q , IE);
  and and_16 (and_16_out, \中断信号寄存器2_q , IE);
  and and_17 (and_17_out, \中断信号寄存器3_q , IE);
  or or_9 (or_9_out, WB_JAL, WB_JALR);
  Multiplexer #(.select(2), .width(32), .disabled("Z"), .enable("false")) multiplexer_10 (
    .in1(32'h30ac), .in2(32'h3158), .in3(32'h3204), .out(\中断程序入口地址 ), .sel(priority_encoder_1_out));  // open: in0
  and and_18 (and_18_out, and_15_out, CLK);
  Register #(.width(1), .trigger("rising"), .Select("low")) register_7 (
    .D(undriven), .Q(\_1号中断响应 ), .clr(and_19_out), .cs(undriven), .preset(and_18_out));  // open: en, clk
  and and_19 (and_19_out, CLK, \_1号中断已响应 );
  and and_20 (and_20_out, and_16_out, CLK);
  Register #(.width(1), .trigger("rising"), .Select("low")) register_8 (
    .D(undriven_2), .Q(\_2号中断响应 ), .clr(and_21_out), .cs(undriven_2), .preset(and_20_out));  // open: en, clk
  and and_21 (and_21_out, CLK, \_2号中断已响应 );
  and and_22 (and_22_out, and_17_out, CLK);
  Register #(.width(1), .trigger("rising"), .Select("low")) register_9 (
    .D(undriven_3), .Q(\_3号中断响应 ), .clr(and_23_out), .cs(undriven_3), .preset(and_22_out));  // open: en, clk
  and and_23 (and_23_out, CLK, \_3号中断已响应 );
  not not_8 (not_8_out, CLK);
  Regifile regifile_1 (
    .Din(RDin), .Clk(not_8_out), .R1(regifile_1_r1), .R2(regifile_1_r2), .WE(MEM_WB_regwrite_2),
    .W_num(MEM_WB_writereg_num_2), .R1_num(multiplexer_7_out), .R2_num(multiplexer_8_out));
  not not_9 (not_9_out, Flush);
  Comparator #(.width(32), .mode("twosComplement")) comparator_5 (
    .a(R1), .b(32'h22), .eq(comparator_5_eq));  // open: gt, lt
  not not_10 (not_10_out, Flush);
  and and_24 (and_24_out, EX_ecall, not_9_out, comparator_5_eq);
  Register #(.width(32), .trigger("rising"), .Select("low")) register_10 (
    .D(R2), .en(and_24_out), .Q(LedData), .clk(CLK));  // open: clr
  not not_11 (not_11_out, comparator_5_eq);
  and and_25 (halt, not_11_out, EX_ecall, not_10_out, not_12_out);
  not not_12 (not_12_out, Go);
  or or_10 (or_10_out, \中断响应 , EX_URET, \相关处理逻辑_重定向_1_id_ex_clr );
  ID_EX ID_EX (
    .RegWrite(RegWrite), .MemToReg(MemToReg), .MemWrite(MemWrite), .AluOP(AluOP), .Beq(Beq),
    .AluSrc(AluSrcB), .R1(regifile_1_r1), .R2(regifile_1_r2), .WriteReg_num(ID_IR[11:7]),
    .SignImm(\immgen_封装版_1_imm ), .CLK(CLK), .RegWrite_2(ID_EX_regwrite_2), .MemToReg_2(ID_EX_memtoreg_2),
    .MemWrite_2(ID_EX_memwrite_2), .AluOP_2(ID_EX_aluop_2), .Beq_2(ID_EX_beq_2), .AluSrc_2(ID_EX_alusrc_2),
    .R1_2(ID_EX_r1_2), .R2_2(ID_EX_r2_2), .WriteReg_num_2(ID_EX_writereg_num_2), .SignImm_2(ID_EX_signimm_2),
    .Bne(Bne), .Bne_2(ID_EX_bne_2), .PC(ID_PC), .PC_2(EX_PC), .IR(ID_IR), .IR_2(EX_IR), .CLR(or_10_out),
    .JAL(JAL), .JALR(JALR), .JAL_2(ID_EX_jal_2), .JALR_2(ID_EX_jalr_2), .PC_4(IF_ID_pc_4_2),
    .PC_4_2(EX_PC_4), .RsForward(\相关处理逻辑_重定向_1_r1forward ), .RsForward_2(ID_EX_rsforward_2),
    .RtForward(\相关处理逻辑_重定向_1_r2forward ), .RtForward_2(ID_EX_rtforward_2), .ecall(ecall), .ecall_2(EX_ecall),
    .halt(halt), .PredictJump(IF_ID_predictjump_2), .PredictJump_2(PredictJump), .Bgeu(Bgeu),
    .Bgeu_2(ID_EX_bgeu_2), .lb(lb), .lb_2(ID_EX_lb_2), .csrrsi(csrrsi), .csrrrsi(EX_csrrsi), .csrrci(csrrci),
    .csrrrci(EX_csrrci), .uret(URET), .uret_2(EX_URET));
  Decoder #(.select(2), .tristate("false"), .disabled("Z"), .enable("false")) decoder_1 (
    .out1(decoder_1_out1[0]), .out2(decoder_1_out1[1]), .out3(decoder_1_out1[2]), .sel(priority_encoder_1_out));  // open: out0
  Multiplexer #(.select(2), .width(32), .disabled("Z"), .enable("false")) multiplexer_11 (
    .in0(ID_EX_r2_2), .in1(multiplexer_17_out), .in2(EX_MEM_aluresult_2), .out(multiplexer_11_out),
    .sel(ID_EX_rsforward_2));  // open: in3
  Multiplexer #(.select(3), .width(32), .disabled("Z"), .enable("false")) multiplexer_12 (
    .in1(EPC1), .in2(EPC2), .in3(EPC2), .in4(EPC3), .in5(EPC3), .in6(EPC3), .in7(EPC3), .out(EPC),
    .sel(decoder_1_out1));  // open: in0
  Register #(.width(32), .trigger("rising"), .Select("low")) u_EPC1 (
    .D(NextAddr), .en(\_1号中断响应 ), .Q(EPC1), .clk(not_13_out));  // open: clr
  not not_13 (not_13_out, CLK);
  Register #(.width(32), .trigger("rising"), .Select("low")) u_EPC2 (
    .D(NextAddr), .en(\_2号中断响应 ), .Q(EPC2), .clk(not_14_out));  // open: clr
  not not_14 (not_14_out, CLK);
  Register #(.width(32), .trigger("rising"), .Select("low")) u_EPC3 (
    .D(NextAddr), .en(\_3号中断响应 ), .Q(EPC3), .clk(not_15_out));  // open: clr
  not not_15 (not_15_out, CLK);
  or or_11 (EX_Branch, ID_EX_beq_2, ID_EX_bne_2, ID_EX_jal_2, ID_EX_jalr_2);
  Multiplexer #(.select(2), .width(32), .disabled("Z"), .enable("false")) multiplexer_13 (
    .in0(ID_EX_r1_2), .in1(multiplexer_17_out), .in2(EX_MEM_aluresult_2), .out(R1), .sel(ID_EX_rtforward_2));  // open: in3
  Multiplexer #(.select(1), .width(32), .disabled("Z"), .enable("false")) multiplexer_14 (
    .in0(multiplexer_11_out), .in1(ID_EX_signimm_2), .out(R2), .sel(ID_EX_alusrc_2));
  Shifter #(.width(32), .shift("ll")) shifter_1 (.in(ID_EX_signimm_2), .\dist (5'b00001), .out(shifter_1_out));
  ALU alu_1 (
    .X(R1), .Y(R2), .AluOP(ID_EX_aluop_2), .Equal(alu_1_equal), .Result({alu_1_result_2, alu_1_result[0]}),
    .out_4(alu_1_out_4));  // open: Result_2, out_6
  Adder #(.width(32)) adder_2 (.a(shifter_1_out), .b(EX_PC), .out(adder_2_out));  // open: cin, cout
  and and_26 (RST_IRA, decoder_1_out1[0], EX_URET);
  and and_27 (RST_IRB, decoder_1_out1[1], EX_URET);
  and and_28 (RST_IRC, decoder_1_out1[2], EX_URET);
  and and_29 (and_29_out, ID_EX_beq_2, alu_1_equal);
  and and_30 (and_30_out, ID_EX_bne_2, not_16_out);
  not not_16 (not_16_out, alu_1_equal);
  Comparator #(.width(32), .mode("twosComplement")) comparator_6 (
    .a({32{1'b0}}), .b(ID_PC), .eq(comparator_6_eq));  // open: gt, lt
  Multiplexer #(.select(1), .width(32), .disabled("Z"), .enable("false")) multiplexer_15 (
    .in0(ID_PC), .in1(IF_PC), .out(multiplexer_15_out), .sel(comparator_6_eq));
  or or_12 (EX_BranchTaken, and_29_out, and_30_out, ID_EX_jal_2, ID_EX_jalr_2, and_31_out);
  and and_31 (and_31_out, ID_EX_bgeu_2, alu_1_out_4);
  EX_MEM EX_MEM (
    .RegWrite(ID_EX_regwrite_2), .MemToReg(ID_EX_memtoreg_2), .MemWrite(ID_EX_memwrite_2),
    .AluResult({alu_1_result_2, alu_1_result[0]}), .WriteData(multiplexer_11_out),
    .WriteReg_num(ID_EX_writereg_num_2), .RegWrite_2(EX_MEM_regwrite_2), .MemToReg_2(EX_MEM_memtoreg_2),
    .MemWrite_2(MEM_MemWrite), .AluResult_2(EX_MEM_aluresult_2), .WriteData_2(MDin),
    .WriteReg_num_2(EX_MEM_writereg_num_2), .CLK(CLK), .PC(EX_PC), .PC_2(MEM_PC), .IR(EX_IR), .IR_2(MEM_IR),
    .JAL(ID_EX_jal_2), .JAL_2(EX_MEM_jal_2), .JALR(ID_EX_jalr_2), .JALR_2(EX_MEM_jalr_2), .PC_4(EX_PC_4),
    .PC_4_2(EX_MEM_pc_4_2), .lb(ID_EX_lb_2), .lb_2(EX_MEM_lb_2), .URET(EX_URET), .URET_2(MEM_URET));
  not not_17 (PredictErr, comparator_7_eq);
  Comparator #(.width(1), .mode("twosComplement")) comparator_7 (
    .a(EX_BranchTaken), .b(PredictJump), .eq(comparator_7_eq));  // open: gt, lt
  Multiplexer #(.select(1), .width(32), .disabled("Z"), .enable("false")) multiplexer_16 (
    .in0(multiplexer_15_out), .in1(BranchAddr), .out(NextAddr), .sel(EX_Branch));
  RAM #(.addrWidth(10), .dataWidth(32), .bus("separate"), .Select("high")) ram_1 (
    .addr(EX_MEM_aluresult_2[11:2]), .din(MDin), .data(ram_1_data), .str(MEM_MemWrite), .clk(CLK));  // open: sel, ld, clr
  and and_32 (and_32_out, \_1号中断响应 , ~In2_Exist, ~In3_Exist);  // AND_Gate
  and and_33 (and_33_out, \_2号中断响应 , ~In3_Exist);  // AND_Gate
  Comparator #(.width(32), .mode("twosComplement")) comparator_8 (
    .a(IF_PC), .b(32'h30ac), .eq(comparator_8_eq));  // open: gt, lt
  Comparator #(.width(32), .mode("twosComplement")) comparator_9 (
    .a(IF_PC), .b(32'h3158), .eq(comparator_9_eq));  // open: gt, lt
  Comparator #(.width(32), .mode("twosComplement")) comparator_10 (
    .a(IF_PC), .b(32'h3204), .eq(comparator_10_eq));  // open: gt, lt
  \L指令分线器  \l指令分线器_1  (
    .lb(EX_MEM_lb_2), .Imm32_2(\l指令分线器_1_imm32_2 ), .Imm32(ram_1_data), .offset(EX_MEM_aluresult_2[1:0]));
  or or_13 (\中断响应 , and_32_out, and_33_out, \_3号中断响应 );
  MEM_WB MEM_WB (
    .RegWrite(EX_MEM_regwrite_2), .MemToReg(EX_MEM_memtoreg_2), .AluResult(EX_MEM_aluresult_2),
    .ReadData(\l指令分线器_1_imm32_2 ), .WriteReg_num(EX_MEM_writereg_num_2), .RegWrite_2(MEM_WB_regwrite_2),
    .MemToReg_2(MEM_WB_memtoreg_2), .AluResult_2(MEM_WB_aluresult_2), .ReadData_2(MEM_WB_readdata_2),
    .WriteReg_num_2(MEM_WB_writereg_num_2), .CLK(CLK), .PC(MEM_PC), .PC_2(WB_PC), .IR(MEM_IR), .IR_2(WB_IR),
    .JAL(EX_MEM_jal_2), .JALR(EX_MEM_jalr_2), .JAL_2(WB_JAL), .JALR_2(WB_JALR), .PC_4(EX_MEM_pc_4_2),
    .PC_4_2(MEM_WB_pc_4_2));
  Multiplexer #(.select(1), .width(32), .disabled("Z"), .enable("false")) multiplexer_17 (
    .in0(MEM_WB_aluresult_2), .in1(MEM_WB_readdata_2), .out(multiplexer_17_out), .sel(MEM_WB_memtoreg_2));
  and and_34 (\_1号中断已响应 , \_1号中断响应 , comparator_8_eq);
  and and_35 (\_2号中断已响应 , \_2号中断响应 , comparator_9_eq);
  and and_36 (\_3号中断已响应 , \_3号中断响应 , comparator_10_eq);
  and and_37 (and_37_out, CLK, \_2号中断已响应 );
  Register #(.width(1), .trigger("rising"), .Select("low")) u_In2_Exist (
    .Q(In2_Exist), .clr(and_38_out), .preset(and_37_out));  // open: D, en, clk, cs
  and and_38 (and_38_out, CLK, comparator_11_eq);
  Comparator #(.width(32), .mode("twosComplement")) comparator_11 (
    .a(EX_PC), .b(32'h3200), .eq(comparator_11_eq));  // open: gt, lt
  and and_39 (and_39_out, CLK, \_3号中断已响应 );
  Register #(.width(1), .trigger("rising"), .Select("low")) u_In3_Exist (
    .Q(In3_Exist), .clr(and_40_out), .preset(and_39_out));  // open: D, en, clk, cs
  and and_40 (and_40_out, CLK, comparator_12_eq);
  Comparator #(.width(32), .mode("twosComplement")) comparator_12 (
    .a(EX_PC), .b(32'h32ac), .eq(comparator_12_eq));  // open: gt, lt

  // Other names for the same wires on the sheet: IR[31:0] = ID_IR; PC[31:0] = IF_PC

  // Notes on the sheet:
  //   中断源
  //   JALR
  //   中断等待指示
  //   BranchTaken
  //   数码管输出
  //   如果出现中断请求信号 且IE=1 进入中断程序
  //   进入中断程序 关中断
  //   csrrsi 开中断
  //   csrrci 关中断
  //   URET 开中断
  //   IF
  //   否则 将中断请求信号存在中断请求寄存器中
  //   指令探针
  //   指令存储器
  //   contents of rom_1 (hex, n*v repeats v):
  //   7d000113 100413 1f41993 41f9d993 433 c00913 800b13 140413 f47413 800293 100313 499993 89e9b3 1300533
  //   2200893 73 406282b3 fe0294e3 140413 f00f93 1f47433 1c41413 800293 100313 49d993 89e9b3 1300533
  //   2200893 73 406282b3 fe0294e3 1c45413 406b0b33 b0463 f95ff06f 2b3 fff2c293 1029293 fff2e293 500533
  //   2200893 73 f5dff06f 1112023 410113 a12023 410113 812023 410113 1312023 410113 1412023 410113 1512023
  //   410113 1612023 410113 40e073 100b13 300a13 100a93 1600433 441413 14469b3 1300533 2200893 73 fe0416e3
  //   415a0a33 fe0a10e3 40f073 ffc10113 12b03 ffc10113 12a83 ffc10113 12a03 ffc10113 12983 ffc10113 12403
  //   ffc10113 12503 ffc10113 12883 200073 1112023 410113 a12023 410113 812023 410113 1312023 410113
  //   1412023 410113 1512023 410113 1612023 410113 40e073 200b13 300a13 100a93 1600433 441413 14469b3
  //   1300533 2200893 73 fe0416e3 415a0a33 fe0a10e3 40f073 ffc10113 12b03 ffc10113 12a83 ffc10113 12a03
  //   ffc10113 12983 ffc10113 12403 ffc10113 12503 ffc10113 12883 200073 1112023 410113 a12023 410113
  //   812023 410113 1312023 410113 1412023 410113 1512023 410113 1612023 410113 40e073 300b13 300a13
  //   100a93 1600433 441413 14469b3 1300533 2200893 73 fe0416e3 415a0a33 fe0a10e3 40f073 ffc10113 12b03
  //   ffc10113 12a83 ffc10113 12a03 ffc10113 12983 ffc10113 12403 ffc10113 12503 ffc10113 12883 200073
  //   PC+4
  //   ID.IR
  //   指令字
  //   ID
  //   已响应1号中断，进入1号中断程序
  //   PC+4
  //   为1则暂停
  //   EX.MemRead
  //   EX.RegWrite
  //   PC+SignImm
  //   EX.WriteReg#
  //   Beq
  //   Bne
  //   JAL
  //   JALR
  //   EX
  //   PC+4
  //   BranchTaken
  //   数据存储器
  //   MEM
  //   PC+4
  //   WB
endmodule

module ImmGen (
  input  S_type,
  input  Beq,
  input  Bne,
  input  Bgeu,
  input  [31:0] Imm12,
  input  JAL,
  input  [11:0] Imm_sw,
  input  [11:0] Imm_beq_bne_bgeu,
  input  [19:0] Imm_jal,
  output [31:0] Imm
);

  wire not_1_out, or_1_out, or_2_out;

  not not_1 (not_1_out, or_1_out);
  or or_1 (or_1_out, S_type, Beq, Bne, Bgeu, JAL);
  assign Imm = not_1_out ? {{21{Imm12[31]}}, Imm12[30:20]} : 32'bz;  // Controlled_Buffer controlled_buffer_1
  assign Imm = S_type ? {{21{Imm_sw[11]}}, Imm_sw[10:0]} : 32'bz;  // Controlled_Buffer controlled_buffer_2
  or or_2 (or_2_out, Beq, Bne, Bgeu);
  assign Imm = or_2_out ? {{21{Imm_beq_bne_bgeu[11]}}, Imm_beq_bne_bgeu[10:0]} : 32'bz;  // Controlled_Buffer controlled_buffer_3
  assign Imm = JAL ? {{13{Imm_jal[19]}}, Imm_jal[18:0]} : 32'bz;  // Controlled_Buffer controlled_buffer_4
endmodule

module \ImmGen_封装版  (
  input  [31:0] IR,
  output [31:0] Imm
);

  wire comparator_1_eq, comparator_2_eq, comparator_3_eq, not_1_out, or_1_out;

  Comparator #(.width(5), .mode("twosComplement")) comparator_1 (
    .a(5'b01000), .b(IR[6:2]), .eq(comparator_1_eq));  // open: gt, lt
  Comparator #(.width(5), .mode("twosComplement")) comparator_2 (
    .a(5'b11000), .b(IR[6:2]), .eq(comparator_2_eq));  // open: gt, lt
  Comparator #(.width(5), .mode("twosComplement")) comparator_3 (
    .a(5'b11011), .b(IR[6:2]), .eq(comparator_3_eq));  // open: gt, lt
  or or_1 (or_1_out, comparator_1_eq, comparator_2_eq, comparator_3_eq);
  not not_1 (not_1_out, or_1_out);
  assign Imm = not_1_out ? {{21{IR[31]}}, IR[30:20]} : 32'bz;  // Controlled_Buffer controlled_buffer_1
  assign Imm = comparator_1_eq ? {{21{IR[31]}}, IR[30:25], IR[11:7]} : 32'bz;  // Controlled_Buffer controlled_buffer_2
  assign Imm = comparator_2_eq ? {{21{IR[31]}}, IR[7], IR[30:25], IR[11:8]} : 32'bz;  // Controlled_Buffer controlled_buffer_3
  assign Imm = comparator_3_eq ? {{13{IR[31]}}, IR[19:12], IR[20], IR[30:21]} : 32'bz;  // Controlled_Buffer controlled_buffer_4

  // Notes on the sheet:
  //   Imm_sw
  //   Imm_B型指令
  //   Imm_JAL
  //   Imm12
  //   S_type
  //   B型指令
  //   JAL
endmodule

module IF_ID (
  input  CLR,
  input  EN,
  input  [31:0] IR,
  input  [31:0] PC_4,
  input  [31:0] PC,
  input  PredictJump,
  input  CLK,
  output [31:0] IR_2,
  output [31:0] PC_4_2,
  output [31:0] PC_2,
  output PredictJump_2
);

  wire multiplexer_4_out;
  wire [31:0] multiplexer_1_out, multiplexer_2_out, multiplexer_3_out;

  Multiplexer #(.select(1), .width(32), .disabled("Z"), .enable("false")) multiplexer_1 (
    .in0(IR), .in1({32{1'b0}}), .out(multiplexer_1_out), .sel(CLR));
  Multiplexer #(.select(1), .width(32), .disabled("Z"), .enable("false")) multiplexer_2 (
    .in0(PC_4), .in1({32{1'b0}}), .out(multiplexer_2_out), .sel(CLR));
  Multiplexer #(.select(1), .width(32), .disabled("Z"), .enable("false")) multiplexer_3 (
    .in0(PC), .in1({32{1'b0}}), .out(multiplexer_3_out), .sel(CLR));
  Multiplexer #(.select(1), .width(1), .disabled("Z"), .enable("false")) multiplexer_4 (
    .in0(PredictJump), .in1(1'b0), .out(multiplexer_4_out), .sel(CLR));
  Register #(.width(32), .trigger("rising"), .Select("low")) u_IR (
    .D(multiplexer_1_out), .en(EN), .Q(IR_2), .clk(CLK));  // open: clr
  Register #(.width(32), .trigger("rising"), .Select("low")) u_PC_4 (
    .D(multiplexer_2_out), .en(EN), .Q(PC_4_2), .clk(CLK));  // open: clr
  Register #(.width(32), .trigger("rising"), .Select("low")) u_PC (
    .D(multiplexer_3_out), .en(EN), .Q(PC_2), .clk(CLK));  // open: clr
  Register #(.width(1), .trigger("rising"), .Select("low")) u_PredictJump (
    .D(multiplexer_4_out), .en(EN), .Q(PredictJump_2), .clk(CLK));  // open: clr
endmodule

module ID_EX (
  input  CLR,
  input  halt,
  input  RegWrite,
  input  MemToReg,
  input  MemWrite,
  input  [3:0] AluOP,
  input  Beq,
  input  AluSrc,
  input  [31:0] R1,
  input  [31:0] R2,
  input  [4:0] WriteReg_num,
  input  [31:0] SignImm,
  input  Bne,
  input  [31:0] PC,
  input  [31:0] IR,
  input  JAL,
  input  JALR,
  input  [31:0] PC_4,
  input  [1:0] RsForward,
  input  [1:0] RtForward,
  input  ecall,
  input  PredictJump,
  input  Bgeu,
  input  lb,
  input  csrrsi,
  input  csrrci,
  input  uret,
  input  CLK,
  output RegWrite_2,
  output MemToReg_2,
  output MemWrite_2,
  output [3:0] AluOP_2,
  output Beq_2,
  output AluSrc_2,
  output [31:0] R1_2,
  output [31:0] R2_2,
  output [4:0] WriteReg_num_2,
  output [31:0] SignImm_2,
  output Bne_2,
  output [31:0] PC_2,
  output [31:0] IR_2,
  output JAL_2,
  output JALR_2,
  output [31:0] PC_4_2,
  output [1:0] RsForward_2,
  output [1:0] RtForward_2,
  output ecall_2,
  output PredictJump_2,
  output Bgeu_2,
  output lb_2,
  output csrrrsi,
  output csrrrci,
  output uret_2
);

  wire multiplexer_1_out, multiplexer_2_out, multiplexer_3_out, multiplexer_5_out, multiplexer_6_out,
       multiplexer_11_out, multiplexer_14_out, multiplexer_15_out, multiplexer_19_out, multiplexer_20_out,
       multiplexer_21_out, multiplexer_22_out, multiplexer_23_out, multiplexer_24_out, multiplexer_25_out,
       not_1_out, register_2_q;
  wire [1:0] multiplexer_17_out, multiplexer_18_out;
  wire [3:0] multiplexer_4_out;
  wire [4:0] multiplexer_9_out;
  wire [31:0] IR_q, multiplexer_7_out, multiplexer_8_out, multiplexer_10_out, multiplexer_12_out,
       multiplexer_13_out, multiplexer_16_out, PC_q;

  Multiplexer #(.select(1), .width(1), .disabled("Z"), .enable("false")) multiplexer_1 (
    .in0(RegWrite), .in1(1'b0), .out(multiplexer_1_out), .sel(CLR));
  Multiplexer #(.select(1), .width(1), .disabled("Z"), .enable("false")) multiplexer_2 (
    .in0(MemToReg), .in1(1'b0), .out(multiplexer_2_out), .sel(CLR));
  Multiplexer #(.select(1), .width(1), .disabled("Z"), .enable("false")) multiplexer_3 (
    .in0(MemWrite), .in1(1'b0), .out(multiplexer_3_out), .sel(CLR));
  Multiplexer #(.select(1), .width(4), .disabled("Z"), .enable("false")) multiplexer_4 (
    .in0(AluOP), .in1(4'b0000), .out(multiplexer_4_out), .sel(CLR));
  Multiplexer #(.select(1), .width(1), .disabled("Z"), .enable("false")) multiplexer_5 (
    .in0(Beq), .in1(1'b0), .out(multiplexer_5_out), .sel(CLR));
  Multiplexer #(.select(1), .width(1), .disabled("Z"), .enable("false")) multiplexer_6 (
    .in0(AluSrc), .in1(1'b0), .out(multiplexer_6_out), .sel(CLR));
  Multiplexer #(.select(1), .width(32), .disabled("Z"), .enable("false")) multiplexer_7 (
    .in0(R1), .in1({32{1'b0}}), .out(multiplexer_7_out), .sel(CLR));
  Multiplexer #(.select(1), .width(32), .disabled("Z"), .enable("false")) multiplexer_8 (
    .in0(R2), .in1({32{1'b0}}), .out(multiplexer_8_out), .sel(CLR));
  Multiplexer #(.select(1), .width(5), .disabled("Z"), .enable("false")) multiplexer_9 (
    .in0(WriteReg_num), .in1({5{1'b0}}), .out(multiplexer_9_out), .sel(CLR));
  Multiplexer #(.select(1), .width(32), .disabled("Z"), .enable("false")) multiplexer_10 (
    .in0(SignImm), .in1({32{1'b0}}), .out(multiplexer_10_out), .sel(CLR));
  Multiplexer #(.select(1), .width(1), .disabled("Z"), .enable("false")) multiplexer_11 (
    .in0(Bne), .in1(1'b0), .out(multiplexer_11_out), .sel(CLR));
  Multiplexer #(.select(1), .width(32), .disabled("Z"), .enable("false")) multiplexer_12 (
    .in0(PC), .in1({32{1'b0}}), .out(multiplexer_12_out), .sel(CLR));
  Multiplexer #(.select(1), .width(32), .disabled("Z"), .enable("false")) multiplexer_13 (
    .in0(IR), .in1({32{1'b0}}), .out(multiplexer_13_out), .sel(CLR));
  Multiplexer #(.select(1), .width(1), .disabled("Z"), .enable("false")) multiplexer_14 (
    .in0(JAL), .in1(1'b0), .out(multiplexer_14_out), .sel(CLR));
  Multiplexer #(.select(1), .width(1), .disabled("Z"), .enable("false")) multiplexer_15 (
    .in0(JALR), .in1(1'b0), .out(multiplexer_15_out), .sel(CLR));
  Multiplexer #(.select(1), .width(32), .disabled("Z"), .enable("false")) multiplexer_16 (
    .in0(PC_4), .in1({32{1'b0}}), .out(multiplexer_16_out), .sel(CLR));
  Multiplexer #(.select(1), .width(2), .disabled("Z"), .enable("false")) multiplexer_17 (
    .in0(RsForward), .in1(2'b00), .out(multiplexer_17_out), .sel(CLR));
  Multiplexer #(.select(1), .width(2), .disabled("Z"), .enable("false")) multiplexer_18 (
    .in0(RtForward), .in1(2'b00), .out(multiplexer_18_out), .sel(CLR));
  Multiplexer #(.select(1), .width(1), .disabled("Z"), .enable("false")) multiplexer_19 (
    .in0(ecall), .in1(1'b0), .out(multiplexer_19_out), .sel(CLR));
  Multiplexer #(.select(1), .width(1), .disabled("Z"), .enable("false")) multiplexer_20 (
    .in0(PredictJump), .in1(1'b0), .out(multiplexer_20_out), .sel(CLR));
  Multiplexer #(.select(1), .width(1), .disabled("Z"), .enable("false")) multiplexer_21 (
    .in0(Bgeu), .in1(1'b0), .out(multiplexer_21_out), .sel(CLR));
  Multiplexer #(.select(1), .width(1), .disabled("Z"), .enable("false")) multiplexer_22 (
    .in0(lb), .in1(1'b0), .out(multiplexer_22_out), .sel(CLR));
  Multiplexer #(.select(1), .width(1), .disabled("Z"), .enable("false")) multiplexer_23 (
    .in0(csrrsi), .in1(1'b0), .out(multiplexer_23_out), .sel(CLR));
  Multiplexer #(.select(1), .width(1), .disabled("Z"), .enable("false")) multiplexer_24 (
    .in0(csrrci), .in1(1'b0), .out(multiplexer_24_out), .sel(CLR));
  Multiplexer #(.select(1), .width(1), .disabled("Z"), .enable("false")) multiplexer_25 (
    .in0(uret), .in1(1'b0), .out(multiplexer_25_out), .sel(CLR));
  not not_1 (not_1_out, halt);
  Register #(.width(1), .trigger("rising"), .Select("low")) u_RegWrite (
    .D(multiplexer_1_out), .Q(RegWrite_2), .clk(CLK));  // open: en, clr
  Register #(.width(1), .trigger("rising"), .Select("low")) u_MemToReg (
    .D(multiplexer_2_out), .Q(MemToReg_2), .clk(CLK));  // open: en, clr
  Register #(.width(1), .trigger("rising"), .Select("low")) u_MemWrite (
    .D(multiplexer_3_out), .Q(MemWrite_2), .clk(CLK));  // open: en, clr
  Register #(.width(4), .trigger("rising"), .Select("low")) u_AluOP (
    .D(multiplexer_4_out), .Q(AluOP_2), .clk(CLK));  // open: en, clr
  Register #(.width(1), .trigger("rising"), .Select("low")) Branch (
    .D(multiplexer_5_out), .Q(Beq_2), .clk(CLK));  // open: en, clr
  Register #(.width(1), .trigger("rising"), .Select("low")) u_AluSrc (
    .D(multiplexer_6_out), .Q(AluSrc_2), .clk(CLK));  // open: en, clr
  Register #(.width(32), .trigger("rising"), .Select("low")) u_R1 (
    .D(multiplexer_7_out), .Q(R1_2), .clk(CLK));  // open: en, clr
  Register #(.width(32), .trigger("rising"), .Select("low")) R2_num (
    .D(multiplexer_8_out), .Q(R2_2), .clk(CLK));  // open: en, clr
  Register #(.width(5), .trigger("rising"), .Select("low")) u_WriteReg_num (
    .D(multiplexer_9_out), .Q(WriteReg_num_2), .clk(CLK));  // open: en, clr
  Register #(.width(32), .trigger("rising"), .Select("low")) u_SignImm (
    .D(multiplexer_10_out), .Q(SignImm_2), .clk(CLK));  // open: en, clr
  Register #(.width(1), .trigger("rising"), .Select("low")) register_1 (
    .D(multiplexer_11_out), .Q(Bne_2), .clk(CLK));  // open: en, clr
  Register #(.width(1), .trigger("rising"), .Select("low")) register_2 (
    .D(halt), .Q(register_2_q), .clk(CLK));  // open: en, clr
  Register #(.width(32), .trigger("rising"), .Select("low")) u_PC (
    .D(multiplexer_12_out), .en(not_1_out), .Q(PC_q), .clk(CLK));  // open: clr
  Register #(.width(32), .trigger("rising"), .Select("low")) u_IR (
    .D(multiplexer_13_out), .en(not_1_out), .Q(IR_q), .clk(CLK));  // open: clr
  Register #(.width(1), .trigger("rising"), .Select("low")) u_JAL (
    .D(multiplexer_14_out), .Q(JAL_2), .clk(CLK));  // open: en, clr
  Register #(.width(1), .trigger("rising"), .Select("low")) u_JALR (
    .D(multiplexer_15_out), .Q(JALR_2), .clk(CLK));  // open: en, clr
  Register #(.width(32), .trigger("rising"), .Select("low")) u_PC_4 (
    .D(multiplexer_16_out), .Q(PC_4_2), .clk(CLK));  // open: en, clr
  Register #(.width(2), .trigger("rising"), .Select("low")) u_RsForward (
    .D(multiplexer_17_out), .Q(RsForward_2), .clk(CLK));  // open: en, clr
  Register #(.width(2), .trigger("rising"), .Select("low")) u_RtForward (
    .D(multiplexer_18_out), .Q(RtForward_2), .clk(CLK));  // open: en, clr
  Register #(.width(1), .trigger("rising"), .Select("low")) u_ecall (
    .D(multiplexer_19_out), .en(not_1_out), .Q(ecall_2), .clk(CLK));  // open: clr
  Register #(.width(1), .trigger("rising"), .Select("low")) u_PredictJump (
    .D(multiplexer_20_out), .Q(PredictJump_2), .clk(CLK));  // open: en, clr
  Register #(.width(1), .trigger("rising"), .Select("low")) u_Bgeu (
    .D(multiplexer_21_out), .Q(Bgeu_2), .clk(CLK));  // open: en, clr
  Register #(.width(1), .trigger("rising"), .Select("low")) u_lb (
    .D(multiplexer_22_out), .Q(lb_2), .clk(CLK));  // open: en, clr
  Register #(.width(1), .trigger("rising"), .Select("low")) u_csrrsi (
    .D(multiplexer_23_out), .Q(csrrrsi), .clk(CLK));  // open: en, clr
  Register #(.width(1), .trigger("rising"), .Select("low")) u_csrrci (
    .D(multiplexer_24_out), .Q(csrrrci), .clk(CLK));  // open: en, clr
  Register #(.width(1), .trigger("rising"), .Select("low")) u_uret (
    .D(multiplexer_25_out), .Q(uret_2), .clk(CLK));  // open: en, clr
  Multiplexer #(.select(1), .width(32), .disabled("Z"), .enable("false")) multiplexer_26 (
    .in0(PC_q), .in1({32{1'b0}}), .out(PC_2), .sel(register_2_q));
  Multiplexer #(.select(1), .width(32), .disabled("Z"), .enable("false")) multiplexer_27 (
    .in0(IR_q), .in1({32{1'b0}}), .out(IR_2), .sel(register_2_q));
endmodule

module EX_MEM (
  input  RegWrite,
  input  MemToReg,
  input  MemWrite,
  input  [31:0] AluResult,
  input  [31:0] WriteData,
  input  [4:0] WriteReg_num,
  input  [31:0] PC,
  input  [31:0] IR,
  input  JAL,
  input  JALR,
  input  [31:0] PC_4,
  input  lb,
  input  URET,
  input  CLK,
  output RegWrite_2,
  output MemToReg_2,
  output MemWrite_2,
  output [31:0] AluResult_2,
  output [31:0] WriteData_2,
  output [4:0] WriteReg_num_2,
  output [31:0] PC_2,
  output [31:0] IR_2,
  output JAL_2,
  output JALR_2,
  output [31:0] PC_4_2,
  output lb_2,
  output URET_2
);

  Register #(.width(1), .trigger("rising"), .Select("low")) register_1 (
    .D(RegWrite), .Q(RegWrite_2), .clk(CLK));  // open: en, clr
  Register #(.width(1), .trigger("rising"), .Select("low")) register_2 (
    .D(MemToReg), .Q(MemToReg_2), .clk(CLK));  // open: en, clr
  Register #(.width(1), .trigger("rising"), .Select("low")) register_3 (
    .D(MemWrite), .Q(MemWrite_2), .clk(CLK));  // open: en, clr
  Register #(.width(32), .trigger("rising"), .Select("low")) register_4 (
    .D(AluResult), .Q(AluResult_2), .clk(CLK));  // open: en, clr
  Register #(.width(32), .trigger("rising"), .Select("low")) register_5 (
    .D(WriteData), .Q(WriteData_2), .clk(CLK));  // open: en, clr
  Register #(.width(5), .trigger("rising"), .Select("low")) register_6 (
    .D(WriteReg_num), .Q(WriteReg_num_2), .clk(CLK));  // open: en, clr
  Register #(.width(32), .trigger("rising"), .Select("low")) u_PC (.D(PC), .Q(PC_2), .clk(CLK));  // open: en, clr
  Register #(.width(32), .trigger("rising"), .Select("low")) u_IR (.D(IR), .Q(IR_2), .clk(CLK));  // open: en, clr
  Register #(.width(1), .trigger("rising"), .Select("low")) u_JAL (.D(JAL), .Q(JAL_2), .clk(CLK));  // open: en, clr
  Register #(.width(1), .trigger("rising"), .Select("low")) u_JALR (.D(JALR), .Q(JALR_2), .clk(CLK));  // open: en, clr
  Register #(.width(32), .trigger("rising"), .Select("low")) u_PC_4 (.D(PC_4), .Q(PC_4_2), .clk(CLK));  // open: en, clr
  Register #(.width(1), .trigger("rising"), .Select("low")) u_lb (.D(lb), .Q(lb_2), .clk(CLK));  // open: en, clr
  Register #(.width(1), .trigger("rising"), .Select("low")) u_URET (.D(URET), .Q(URET_2), .clk(CLK));  // open: en, clr
endmodule

module MEM_WB (
  input  RegWrite,
  input  MemToReg,
  input  [31:0] AluResult,
  input  [31:0] ReadData,
  input  [4:0] WriteReg_num,
  input  [31:0] PC,
  input  [31:0] IR,
  input  JAL,
  input  JALR,
  input  [31:0] PC_4,
  input  CLK,
  output RegWrite_2,
  output MemToReg_2,
  output [31:0] AluResult_2,
  output [31:0] ReadData_2,
  output [4:0] WriteReg_num_2,
  output [31:0] PC_2,
  output [31:0] IR_2,
  output JAL_2,
  output JALR_2,
  output [31:0] PC_4_2
);

  Register #(.width(1), .trigger("rising"), .Select("low")) register_1 (
    .D(RegWrite), .Q(RegWrite_2), .clk(CLK));  // open: en, clr
  Register #(.width(1), .trigger("rising"), .Select("low")) register_2 (
    .D(MemToReg), .Q(MemToReg_2), .clk(CLK));  // open: en, clr
  Register #(.width(32), .trigger("rising"), .Select("low")) register_3 (
    .D(AluResult), .Q(AluResult_2), .clk(CLK));  // open: en, clr
  Register #(.width(32), .trigger("rising"), .Select("low")) register_4 (
    .D(ReadData), .Q(ReadData_2), .clk(CLK));  // open: en, clr
  Register #(.width(5), .trigger("rising"), .Select("low")) register_5 (
    .D(WriteReg_num), .Q(WriteReg_num_2), .clk(CLK));  // open: en, clr
  Register #(.width(32), .trigger("rising"), .Select("low")) u_PC (.D(PC), .Q(PC_2), .clk(CLK));  // open: en, clr
  Register #(.width(32), .trigger("rising"), .Select("low")) u_IR (.D(IR), .Q(IR_2), .clk(CLK));  // open: en, clr
  Register #(.width(1), .trigger("rising"), .Select("low")) u_JAL (.D(JAL), .Q(JAL_2), .clk(CLK));  // open: en, clr
  Register #(.width(1), .trigger("rising"), .Select("low")) u_JALR (.D(JALR), .Q(JALR_2), .clk(CLK));  // open: en, clr
  Register #(.width(32), .trigger("rising"), .Select("low")) u_PC_4 (.D(PC_4), .Q(PC_4_2), .clk(CLK));  // open: en, clr
endmodule

module \数据冲突检测器  (
  input  [31:0] ID_IR,
  input  [4:0] EX_WriteReg_num,
  input  EX_RegWrite,
  input  [4:0] MEM_WriteReg_num,
  input  MEM_RegWrite,
  output DataHazzard
);

  wire and_2_out, and_3_out, and_4_out, and_5_out, comparator_1_eq, comparator_2_eq, comparator_3_eq,
       comparator_4_eq, comparator_5_eq, comparator_6_eq, comparator_7_eq, comparator_8_eq, comparator_9_eq,
       comparator_10_eq, comparator_11_eq, comparator_12_eq, IR__ecall_URET, not_1_out, not_2_out, or_2_out,
       RsUsed, RtUsed;
  wire [4:0] multiplexer_1_out, multiplexer_2_out;

  Multiplexer #(.select(1), .width(5), .disabled("Z"), .enable("false")) multiplexer_1 (
    .in0(ID_IR[19:15]), .in1(5'b01010), .out(multiplexer_1_out), .sel(IR__ecall_URET));
  Multiplexer #(.select(1), .width(5), .disabled("Z"), .enable("false")) multiplexer_2 (
    .in0(ID_IR[24:20]), .in1(5'b10001), .out(multiplexer_2_out), .sel(IR__ecall_URET));
  Comparator #(.width(5), .mode("twosComplement")) comparator_1 (
    .a(ID_IR[6:2]), .b(5'b01100), .eq(comparator_1_eq));  // open: gt, lt
  Comparator #(.width(5), .mode("twosComplement")) comparator_2 (
    .a(ID_IR[6:2]), .b(5'b01000), .eq(comparator_2_eq));  // open: gt, lt
  Comparator #(.width(5), .mode("twosComplement")) comparator_3 (
    .a(ID_IR[6:2]), .b(5'b11000), .eq(comparator_3_eq));  // open: gt, lt
  Comparator #(.width(5), .mode("twosComplement")) comparator_4 (
    .a(ID_IR[6:2]), .b(5'b11100), .eq(comparator_4_eq));  // open: gt, lt
  Comparator #(.width(3), .mode("twosComplement")) comparator_5 (
    .a(ID_IR[14:12]), .b(3'b000), .eq(comparator_5_eq));  // open: gt, lt
  Comparator #(.width(5), .mode("twosComplement")) comparator_6 (
    .a(ID_IR[6:2]), .b(5'b11011), .eq(comparator_6_eq));  // open: gt, lt
  and and_1 (IR__ecall_URET, comparator_4_eq, comparator_5_eq);
  Comparator #(.width(5), .mode("twosComplement")) comparator_7 (
    .a({5{1'b0}}), .b(multiplexer_1_out), .eq(comparator_7_eq));  // open: gt, lt
  not not_1 (not_1_out, comparator_7_eq);
  Comparator #(.width(5), .mode("twosComplement")) comparator_8 (
    .a({5{1'b0}}), .b(multiplexer_2_out), .eq(comparator_8_eq));  // open: gt, lt
  not not_2 (not_2_out, comparator_8_eq);
  Comparator #(.width(5), .mode("twosComplement")) comparator_9 (
    .a(multiplexer_2_out), .b(EX_WriteReg_num), .eq(comparator_9_eq));  // open: gt, lt
  Comparator #(.width(5), .mode("twosComplement")) comparator_10 (
    .a(multiplexer_1_out), .b(EX_WriteReg_num), .eq(comparator_10_eq));  // open: gt, lt
  Comparator #(.width(5), .mode("twosComplement")) comparator_11 (
    .a(multiplexer_2_out), .b(MEM_WriteReg_num), .eq(comparator_11_eq));  // open: gt, lt
  Comparator #(.width(5), .mode("twosComplement")) comparator_12 (
    .a(multiplexer_1_out), .b(MEM_WriteReg_num), .eq(comparator_12_eq));  // open: gt, lt
  or or_1 (RsUsed, comparator_1_eq, comparator_2_eq, comparator_3_eq, IR__ecall_URET);
  not not_3 (RtUsed, or_2_out);
  or or_2 (or_2_out, IR__ecall_URET, comparator_6_eq);
  and and_2 (and_2_out, RsUsed, not_2_out, EX_RegWrite, comparator_9_eq);
  and and_3 (and_3_out, RtUsed, not_1_out, EX_RegWrite, comparator_10_eq);
  and and_4 (and_4_out, RsUsed, not_2_out, MEM_RegWrite, comparator_11_eq);
  and and_5 (and_5_out, RtUsed, not_1_out, MEM_RegWrite, comparator_12_eq);
  or or_3 (DataHazzard, and_2_out, and_3_out, and_4_out, and_5_out);

  // Notes on the sheet:
  //   opcode
  //   rt
  //   rs
  //   IR==R型指令？
  //   IR==sw?
  //   IR==beq/bne?
  //   opcode==0x1c?
  //   func3==0?
  //   IR==jal?
  //   IR==ecall/URET?
  //   if IR=ecall/jal/uret then RtUsed=0
  //   if IR=R型指令/sw/beq/bne then RsUsed=1
endmodule
module \相关处理逻辑  (
  input  [31:0] ID_IR,
  input  [4:0] EX_WriteReg_num,
  input  EX_WriteReg,
  input  [4:0] MEM_WriteReg_num,
  input  MEM_WriteReg,
  input  BranchTaken,
  output Stall,
  output Flush
);

  \数据冲突检测器  \u_数据冲突检测器  (
    .ID_IR(ID_IR), .EX_WriteReg_num(EX_WriteReg_num), .EX_RegWrite(EX_WriteReg),
    .MEM_WriteReg_num(MEM_WriteReg_num), .MEM_RegWrite(MEM_WriteReg), .DataHazzard(Stall));
  or or_1 (Flush, Stall, BranchTaken);

  // Notes on the sheet:
  //   出现分支或数据冲突 使ID/EX流水寄存器清空
  //   发生数据冲突 使PC和IF/ID流水寄存器暂停，忽略时钟的信号
endmodule

module \数据冲突检测器_重定向  (
  input  [31:0] ID_IR,
  input  [4:0] EX_WriteReg_num,
  input  EX_RegWrite,
  input  [4:0] MEM_WriteReg_num,
  input  MEM_RegWrite,
  input  EX_MemRead,
  output [1:0] RsForward,
  output [1:0] RtForward,
  output LoadUse
);

  wire and_1_out, and_2_out, and_3_out, and_5_out, comparator_1_eq, comparator_2_eq, comparator_3_eq,
       comparator_4_eq, comparator_5_eq, comparator_6_eq, comparator_7_eq, comparator_8_eq, comparator_9_eq,
       comparator_11_eq, IR__ecall, not_1_out, not_2_out, not_4_out, not_5_out, RsUsed, RtUsed;
  wire [4:0] multiplexer_1_out, multiplexer_2_out;

  // Probe on ID_IR[19:15]
  // Probe on ID_IR[24:20]
  Multiplexer #(.select(1), .width(5), .disabled("Z"), .enable("false")) multiplexer_1 (
    .in0(ID_IR[19:15]), .in1(5'b10001), .out(multiplexer_1_out), .sel(IR__ecall));
  Multiplexer #(.select(1), .width(5), .disabled("Z"), .enable("false")) multiplexer_2 (
    .in0(ID_IR[24:20]), .in1(5'b01010), .out(multiplexer_2_out), .sel(IR__ecall));
  Comparator #(.width(5), .mode("twosComplement")) comparator_1 (
    .a({5{1'b0}}), .b(multiplexer_1_out), .eq(comparator_1_eq));  // open: gt, lt
  not not_1 (not_1_out, comparator_1_eq);
  Comparator #(.width(5), .mode("twosComplement")) comparator_2 (
    .a({5{1'b0}}), .b(multiplexer_2_out), .eq(comparator_2_eq));  // open: gt, lt
  not not_2 (not_2_out, comparator_2_eq);
  Comparator #(.width(5), .mode("twosComplement")) comparator_3 (
    .a(multiplexer_2_out), .b(EX_WriteReg_num), .eq(comparator_3_eq));  // open: gt, lt
  Comparator #(.width(5), .mode("twosComplement")) comparator_4 (
    .a(multiplexer_1_out), .b(EX_WriteReg_num), .eq(comparator_4_eq));  // open: gt, lt
  Comparator #(.width(5), .mode("twosComplement")) comparator_5 (
    .a(multiplexer_2_out), .b(MEM_WriteReg_num), .eq(comparator_5_eq));  // open: gt, lt
  Comparator #(.width(5), .mode("twosComplement")) comparator_6 (
    .a(multiplexer_1_out), .b(MEM_WriteReg_num), .eq(comparator_6_eq));  // open: gt, lt
  Comparator #(.width(5), .mode("twosComplement")) comparator_7 (
    .a(ID_IR[6:2]), .b(5'b01100), .eq(comparator_7_eq));  // open: gt, lt
  Comparator #(.width(5), .mode("twosComplement")) comparator_8 (
    .a(ID_IR[6:2]), .b(5'b01000), .eq(comparator_8_eq));  // open: gt, lt
  Comparator #(.width(5), .mode("twosComplement")) comparator_9 (
    .a(ID_IR[6:2]), .b(5'b11000), .eq(comparator_9_eq));  // open: gt, lt
  Comparator #(.width(32), .mode("twosComplement")) comparator_10 (
    .a(ID_IR), .b(32'h73), .eq(IR__ecall));  // open: gt, lt
  Comparator #(.width(5), .mode("twosComplement")) comparator_11 (
    .a(ID_IR[6:2]), .b(5'b11011), .eq(comparator_11_eq));  // open: gt, lt
  or or_1 (RsUsed, comparator_7_eq, comparator_8_eq, comparator_9_eq, IR__ecall);
  not not_3 (RtUsed, comparator_11_eq);
  and and_1 (and_1_out, RsUsed, not_2_out, EX_MemRead, comparator_3_eq);
  and and_2 (and_2_out, RtUsed, not_1_out, EX_MemRead, comparator_4_eq);
  and and_3 (and_3_out, RsUsed, not_2_out, MEM_RegWrite, comparator_5_eq);
  and and_4 (RsForward[1], RsUsed, not_2_out, EX_RegWrite, comparator_3_eq);
  and and_5 (and_5_out, RtUsed, not_1_out, MEM_RegWrite, comparator_6_eq);
  and and_6 (RtForward[1], RtUsed, not_1_out, EX_RegWrite, comparator_4_eq);
  or or_2 (LoadUse, and_1_out, and_2_out);
  and and_7 (RsForward[0], and_3_out, not_4_out);
  not not_4 (not_4_out, RsForward[1]);
  and and_8 (RtForward[0], and_5_out, not_5_out);
  not not_5 (not_5_out, RtForward[1]);

  // Notes on the sheet:
  //   opcode
  //   rt
  //   rs
  //   IR==R型指令？
  //   IR==sw?
  //   IR==beq/bne?
  //   opcode==0x1c?
  //   IR==jal?
  //   IR==ecall?
  //   if IR=R型指令/sw/beq/bne then RsUsed=1
  //   if IR=ecall/jal/uret then RtUsed=0
  //   ID段与MEM段数据相关
  //   ID段与EX段数据相关
endmodule

module \相关处理逻辑_重定向  (
  input  [31:0] ID_IR,
  input  [4:0] EX_WriteReg_num,
  input  EX_WriteReg,
  input  [4:0] MEM_WriteReg_num,
  input  MEM_WriteReg,
  input  EX_MemRead,
  input  BranchTaken,
  input  PredictErr,
  output [1:0] R1Forward,
  output [1:0] R2Forward,
  output Stall,
  output Flush,
  output IF_ID_CLR,
  output ID_EX_CLR
);

  \数据冲突检测器_重定向  \u_数据冲突检测器_重定向_1  (
    .ID_IR(ID_IR), .EX_WriteReg_num(EX_WriteReg_num), .EX_RegWrite(EX_WriteReg),
    .MEM_WriteReg_num(MEM_WriteReg_num), .MEM_RegWrite(MEM_WriteReg), .EX_MemRead(EX_MemRead),
    .RsForward(R1Forward), .RtForward(R2Forward), .LoadUse(Stall));
  or or_1 (Flush, Stall, BranchTaken);
  or or_2 (ID_EX_CLR, Stall, PredictErr);

  assign IF_ID_CLR = PredictErr;

  // Notes on the sheet:
  //   LoadUse
  //   发生数据冲突时，对从寄存器中读取的数据重定向
  //   出现分支或者LoadUse时，使IF/ID流水寄存器和ID/EX流水寄存器清空，消除ID和EX段误取的指令
  //   发生Load-Use时，IF和ID段暂停，使PC寄存器，IF/ID流水寄存器，ID/EX流水寄存器暂停，在EX段插入气泡
endmodule

module \相关处理逻辑_重定向_动态预测  (
  input  [31:0] ID_IR,
  input  [4:0] EX_WriteReg_num,
  input  EX_WriteReg,
  input  [4:0] MEM_WriteReg_num,
  input  MEM_WriteReg,
  input  EX_MemRead,
  input  BranchTaken,
  output [1:0] R1Forward,
  output [1:0] R2Forward,
  output Stall,
  output Flush
);

  \数据冲突检测器_重定向  \u_数据冲突检测器_重定向_1  (
    .ID_IR(ID_IR), .EX_WriteReg_num(EX_WriteReg_num), .EX_RegWrite(EX_WriteReg),
    .MEM_WriteReg_num(MEM_WriteReg_num), .MEM_RegWrite(MEM_WriteReg), .EX_MemRead(EX_MemRead),
    .RsForward(R1Forward), .RtForward(R2Forward), .LoadUse(Stall));
  or or_1 (Flush, Stall, BranchTaken);

  // Notes on the sheet:
  //   LoadUse
  //   发生数据冲突时，对从寄存器中读取的数据重定向
  //   出现分支或者LoadUse时，使IF/ID流水寄存器和ID/EX流水寄存器清空，消除ID和EX段误取的指令
  //   发生Load-Use时，IF和ID段暂停，使PC寄存器，IF/ID流水寄存器，ID/EX流水寄存器暂停，在EX段插入气泡
endmodule

module \双预测位状态机  (
  input  Jump,
  input  [1:0] in_2,
  output [1:0] \次态 
);

  wire and_1_out, and_2_out, and_3_out, and_4_out, not_1_out, not_2_out, not_3_out, not_4_out, not_5_out;

  not not_1 (not_1_out, in_2[0]);
  not not_2 (not_2_out, Jump);
  not not_3 (not_3_out, in_2[0]);
  not not_4 (not_4_out, in_2[1]);
  not not_5 (not_5_out, in_2[0]);
  and and_1 (and_1_out, in_2[1], not_1_out);
  and and_2 (and_2_out, Jump, in_2[0]);
  and and_3 (and_3_out, not_2_out, in_2[1], not_3_out);
  and and_4 (and_4_out, Jump, not_4_out, not_5_out);
  or or_1 (\次态 [1], and_1_out, and_2_out);
  or or_2 (\次态 [0], and_3_out, and_4_out);
endmodule

module BTB (
  input  [31:0] PC,
  input  EX_Branch,
  input  [31:0] EX_PC,
  input  CLK,
  input  [31:0] BranchAddr,
  input  EX_BranchTaken,
  output [31:0] JumpAddr,
  output PredictJump
);

  wire comparator_1_eq, comparator_2_eq, \n8路cache_1_miss , or_1_out;
  wire [1:0] \n8路cache_1_pc_state , \n8路cache_1_writepc_state , \双预测位状态机_1_次态 ;

  \_8路cache  \u_8路cache_1  (
    .CLK(CLK), .PC(PC), .WritePC(EX_PC), .WriteAddr(BranchAddr), .WriteEN(EX_Branch),
    .WriteState(\双预测位状态机_1_次态 ), .Miss(\n8路cache_1_miss ), .JumpAddress(JumpAddr),
    .PC_State(\n8路cache_1_pc_state ), .WritePC_state(\n8路cache_1_writepc_state ));  // open: WriteHit
  \双预测位状态机  \u_双预测位状态机_1  (.Jump(EX_BranchTaken), .\次态 (\双预测位状态机_1_次态 ), .in_2(\n8路cache_1_writepc_state ));
  Comparator #(.width(2), .mode("twosComplement")) comparator_1 (
    .a(\n8路cache_1_pc_state ), .b(2'b10), .eq(comparator_1_eq));  // open: gt, lt
  Comparator #(.width(2), .mode("twosComplement")) comparator_2 (
    .a(\n8路cache_1_pc_state ), .b(2'b11), .eq(comparator_2_eq));  // open: gt, lt
  or or_1 (or_1_out, comparator_1_eq, comparator_2_eq);
  Multiplexer #(.select(1), .width(1), .disabled("Z"), .enable("false")) multiplexer_1 (
    .in0(or_1_out), .in1(1'b0), .out(PredictJump), .sel(\n8路cache_1_miss ));

  // Notes on the sheet:
  //   EX段的分支指令实际是否跳转，1为跳转
  //   指令命中不需要更新
  //   指令没有命中
  //   指令命中但需要更新
endmodule

module \单路cache  (
  input  CLK,
  input  EN,
  input  Valid,
  input  [31:0] \分支指令地址 ,
  input  [31:0] \分支目标地址 ,
  input  [1:0] \分支预测历史位 ,
  input  [31:0] \置换标记位 ,
  output Valid_2,
  output [31:0] \分支指令地址_2 ,
  output [31:0] \分支目标地址_2 ,
  output [1:0] \分支预测历史位_2 ,
  output [31:0] \置换标记位_2 
);

  Register #(.width(1), .trigger("rising"), .Select("low")) u_Valid (
    .D(Valid), .en(EN), .Q(Valid_2), .clk(CLK));  // open: clr
  Register #(.width(32), .trigger("rising"), .Select("low")) \u_分支指令地址  (
    .D(\分支指令地址 ), .en(EN), .Q(\分支指令地址_2 ), .clk(CLK));  // open: clr
  Register #(.width(32), .trigger("rising"), .Select("low")) \u_分支目标地址  (
    .D(\分支目标地址 ), .en(EN), .Q(\分支目标地址_2 ), .clk(CLK));  // open: clr
  Register #(.width(2), .trigger("rising"), .Select("low")) \u_分支预测历史位  (
    .D(\分支预测历史位 ), .en(EN), .Q(\分支预测历史位_2 ), .clk(CLK));  // open: clr
  Register #(.width(32), .trigger("rising"), .Select("low")) \u_置换标记位  (
    .D(\置换标记位 ), .en(EN), .Q(\置换标记位_2 ), .clk(CLK));  // open: clr
endmodule

module \_8路cache  (
  input  CLK,
  input  [31:0] PC,
  input  [31:0] WritePC,
  input  [31:0] WriteAddr,
  input  WriteEN,
  input  [1:0] WriteState,
  output Miss,
  output [31:0] JumpAddress,
  output [1:0] PC_State,
  output [1:0] WritePC_state,
  output WriteHit
);

  wire and_1_out, and_10_out, and_11_out, and_12_out, and_13_out, and_14_out, and_15_out, and_16_out,
       and_17_out, and_26_out, and_27_out, and_28_out, and_29_out, and_30_out, and_31_out, and_32_out,
       and_33_out, cache0EN, cache0hit, cache0Valid, cache1EN, cache1hit, cache1Valid, cache2EN, cache2hit,
       cache2Valid, cache3EN, cache3hit, cache3Valid, cache4EN, cache4hit, cache4Valid, cache5EN, cache5hit,
       cache5Valid, cache6EN, cache6hit, cache6Valid, cache7EN, cache7hit, cache7Valid, comparator_1_eq,
       comparator_2_eq, comparator_3_eq, comparator_4_eq, comparator_5_eq, comparator_6_eq, comparator_7_eq,
       comparator_8_eq, comparator_9_eq, comparator_10_eq, comparator_11_eq, comparator_12_eq,
       comparator_13_eq, comparator_14_eq, comparator_15_eq, comparator_16_eq, counter_1_carry,
       decoder_1_out0, decoder_1_out1, decoder_1_out2, decoder_1_out3, decoder_1_out4, decoder_1_out5,
       decoder_1_out6, decoder_1_out7, or_2_out, or_3_out, or_4_out, or_5_out, or_6_out, or_7_out, or_8_out,
       or_9_out, or_10_out;
  wire [1:0] \cache0_分支预测历史位_2 , \cache1_分支预测历史位_2 , \cache2_分支预测历史位_2 , \cache3_分支预测历史位_2 ,
       \cache4_分支预测历史位_2 , \cache5_分支预测历史位_2 , \cache6_分支预测历史位_2 , \cache7_分支预测历史位_2 ,
       controlled_buffer_1_out, controlled_buffer_9_out;
  wire [2:0] counter_1_q;
  wire [31:0] \cache0_分支指令地址_2 , \cache0_分支目标地址_2 , \cache1_分支指令地址_2 , \cache1_分支目标地址_2 , \cache2_分支指令地址_2 ,
       \cache2_分支目标地址_2 , \cache3_分支指令地址_2 , \cache3_分支目标地址_2 , \cache4_分支指令地址_2 , \cache4_分支目标地址_2 ,
       \cache5_分支指令地址_2 , \cache5_分支目标地址_2 , \cache6_分支指令地址_2 , \cache6_分支目标地址_2 , \cache7_分支指令地址_2 ,
       \cache7_分支目标地址_2 ;

  and and_1 (and_1_out, ~WriteHit, WriteEN);  // AND_Gate
  Comparator #(.width(32), .mode("twosComplement")) comparator_1 (
    .a(WritePC), .b(\cache0_分支指令地址_2 ), .eq(comparator_1_eq));  // open: gt, lt
  Comparator #(.width(32), .mode("twosComplement")) comparator_2 (
    .a(WritePC), .b(\cache1_分支指令地址_2 ), .eq(comparator_2_eq));  // open: gt, lt
  Comparator #(.width(32), .mode("twosComplement")) comparator_3 (
    .a(WritePC), .b(\cache2_分支指令地址_2 ), .eq(comparator_3_eq));  // open: gt, lt
  Comparator #(.width(32), .mode("twosComplement")) comparator_4 (
    .a(WritePC), .b(\cache3_分支指令地址_2 ), .eq(comparator_4_eq));  // open: gt, lt
  Comparator #(.width(32), .mode("twosComplement")) comparator_5 (
    .a(WritePC), .b(\cache4_分支指令地址_2 ), .eq(comparator_5_eq));  // open: gt, lt
  Comparator #(.width(32), .mode("twosComplement")) comparator_6 (
    .a(WritePC), .b(\cache5_分支指令地址_2 ), .eq(comparator_6_eq));  // open: gt, lt
  Comparator #(.width(32), .mode("twosComplement")) comparator_7 (
    .a(WritePC), .b(\cache6_分支指令地址_2 ), .eq(comparator_7_eq));  // open: gt, lt
  Comparator #(.width(32), .mode("twosComplement")) comparator_8 (
    .a(WritePC), .b(\cache7_分支指令地址_2 ), .eq(comparator_8_eq));  // open: gt, lt
  Counter #(.width(3), .max('h7), .ongoal("wrap"), .trigger("rising"), .behavior("new")) counter_1 (
    .load(counter_1_carry), .D(3'b000), .count(and_1_out), .Q(counter_1_q), .carry(counter_1_carry), .clk(CLK));  // open: clr, preset, down
  and and_2 (cache0hit, cache0Valid, comparator_1_eq);
  and and_3 (cache1hit, cache1Valid, comparator_2_eq);
  and and_4 (cache2hit, cache2Valid, comparator_3_eq);
  and and_5 (cache3hit, cache3Valid, comparator_4_eq);
  and and_6 (cache4hit, cache4Valid, comparator_5_eq);
  and and_7 (cache5hit, cache5Valid, comparator_6_eq);
  and and_8 (cache6hit, cache6Valid, comparator_7_eq);
  and and_9 (cache7hit, cache6Valid, comparator_8_eq);
  Decoder #(.select(3), .tristate("false"), .disabled("Z"), .enable("false")) decoder_1 (
    .out0(decoder_1_out0), .out1(decoder_1_out1), .out2(decoder_1_out2), .out3(decoder_1_out3),
    .out4(decoder_1_out4), .out5(decoder_1_out5), .out6(decoder_1_out6), .out7(decoder_1_out7),
    .sel(counter_1_q));
  \单路cache  cache0 (
    .CLK(CLK), .EN(cache0EN), .Valid(1'b1), .\分支指令地址 (WritePC), .\分支目标地址 (WriteAddr), .\分支预测历史位 (WriteState),
    .Valid_2(cache0Valid), .\分支指令地址_2 (\cache0_分支指令地址_2 ), .\分支目标地址_2 (\cache0_分支目标地址_2 ),
    .\分支预测历史位_2 (\cache0_分支预测历史位_2 ));  // open: 置换标记位, 置换标记位_2
  \单路cache  cache1 (
    .CLK(CLK), .EN(cache1EN), .Valid(1'b1), .\分支指令地址 (WritePC), .\分支目标地址 (WriteAddr), .\分支预测历史位 (WriteState),
    .Valid_2(cache1Valid), .\分支指令地址_2 (\cache1_分支指令地址_2 ), .\分支目标地址_2 (\cache1_分支目标地址_2 ),
    .\分支预测历史位_2 (\cache1_分支预测历史位_2 ));  // open: 置换标记位, 置换标记位_2
  \单路cache  cache2 (
    .CLK(CLK), .EN(cache2EN), .Valid(1'b1), .\分支指令地址 (WritePC), .\分支目标地址 (WriteAddr), .\分支预测历史位 (WriteState),
    .Valid_2(cache2Valid), .\分支指令地址_2 (\cache2_分支指令地址_2 ), .\分支目标地址_2 (\cache2_分支目标地址_2 ),
    .\分支预测历史位_2 (\cache2_分支预测历史位_2 ));  // open: 置换标记位, 置换标记位_2
  \单路cache  cache3 (
    .CLK(CLK), .EN(cache3EN), .Valid(1'b1), .\分支指令地址 (WritePC), .\分支目标地址 (WriteAddr), .\分支预测历史位 (WriteState),
    .Valid_2(cache3Valid), .\分支指令地址_2 (\cache3_分支指令地址_2 ), .\分支目标地址_2 (\cache3_分支目标地址_2 ),
    .\分支预测历史位_2 (\cache3_分支预测历史位_2 ));  // open: 置换标记位, 置换标记位_2
  \单路cache  cache4 (
    .CLK(CLK), .EN(cache4EN), .Valid(1'b1), .\分支指令地址 (WritePC), .\分支目标地址 (WriteAddr), .\分支预测历史位 (WriteState),
    .Valid_2(cache4Valid), .\分支指令地址_2 (\cache4_分支指令地址_2 ), .\分支目标地址_2 (\cache4_分支目标地址_2 ),
    .\分支预测历史位_2 (\cache4_分支预测历史位_2 ));  // open: 置换标记位, 置换标记位_2
  \单路cache  cache5 (
    .CLK(CLK), .EN(cache5EN), .Valid(1'b1), .\分支指令地址 (WritePC), .\分支目标地址 (WriteAddr), .\分支预测历史位 (WriteState),
    .Valid_2(cache5Valid), .\分支指令地址_2 (\cache5_分支指令地址_2 ), .\分支目标地址_2 (\cache5_分支目标地址_2 ),
    .\分支预测历史位_2 (\cache5_分支预测历史位_2 ));  // open: 置换标记位, 置换标记位_2
  \单路cache  cache6 (
    .CLK(CLK), .EN(cache6EN), .Valid(1'b1), .\分支指令地址 (WritePC), .\分支目标地址 (WriteAddr), .\分支预测历史位 (WriteState),
    .Valid_2(cache6Valid), .\分支指令地址_2 (\cache6_分支指令地址_2 ), .\分支目标地址_2 (\cache6_分支目标地址_2 ),
    .\分支预测历史位_2 (\cache6_分支预测历史位_2 ));  // open: 置换标记位, 置换标记位_2
  \单路cache  cache7 (
    .CLK(CLK), .EN(cache7EN), .Valid(1'b1), .\分支指令地址 (WritePC), .\分支目标地址 (WriteAddr), .\分支预测历史位 (WriteState),
    .Valid_2(cache7Valid), .\分支指令地址_2 (\cache7_分支指令地址_2 ), .\分支目标地址_2 (\cache7_分支目标地址_2 ),
    .\分支预测历史位_2 (\cache7_分支预测历史位_2 ));  // open: 置换标记位, 置换标记位_2
  and and_10 (and_10_out, WriteEN, ~WriteHit, decoder_1_out0);  // AND_Gate
  and and_11 (and_11_out, WriteEN, ~WriteHit, decoder_1_out1);  // AND_Gate
  and and_12 (and_12_out, WriteEN, ~WriteHit, decoder_1_out2);  // AND_Gate
  and and_13 (and_13_out, WriteEN, ~WriteHit, decoder_1_out3);  // AND_Gate
  and and_14 (and_14_out, WriteEN, ~WriteHit, decoder_1_out4);  // AND_Gate
  and and_15 (and_15_out, WriteEN, ~WriteHit, decoder_1_out5);  // AND_Gate
  and and_16 (and_16_out, WriteEN, ~WriteHit, decoder_1_out6);  // AND_Gate
  and and_17 (and_17_out, WriteEN, ~WriteHit, decoder_1_out7);  // AND_Gate
  assign controlled_buffer_1_out = cache0hit ? \cache0_分支预测历史位_2  : 2'bz;  // Controlled_Buffer controlled_buffer_1
  assign controlled_buffer_1_out = cache1hit ? \cache1_分支预测历史位_2  : 2'bz;  // Controlled_Buffer controlled_buffer_2
  assign controlled_buffer_1_out = cache2hit ? \cache2_分支预测历史位_2  : 2'bz;  // Controlled_Buffer controlled_buffer_3
  assign controlled_buffer_1_out = cache3hit ? \cache3_分支预测历史位_2  : 2'bz;  // Controlled_Buffer controlled_buffer_4
  assign controlled_buffer_1_out = cache4hit ? \cache4_分支预测历史位_2  : 2'bz;  // Controlled_Buffer controlled_buffer_5
  assign controlled_buffer_1_out = cache5hit ? \cache5_分支预测历史位_2  : 2'bz;  // Controlled_Buffer controlled_buffer_6
  assign controlled_buffer_1_out = cache6hit ? \cache6_分支预测历史位_2  : 2'bz;  // Controlled_Buffer controlled_buffer_7
  assign controlled_buffer_1_out = cache7hit ? \cache7_分支预测历史位_2  : 2'bz;  // Controlled_Buffer controlled_buffer_8
  or or_1 (WriteHit, cache0hit, cache1hit, cache2hit, cache3hit, cache4hit, cache5hit, cache6hit, cache7hit);
  or or_2 (or_2_out, cache0hit, and_10_out);
  and and_18 (cache0EN, or_2_out, WriteEN);
  or or_3 (or_3_out, cache1hit, and_11_out);
  and and_19 (cache1EN, or_3_out, WriteEN);
  or or_4 (or_4_out, cache2hit, and_12_out);
  and and_20 (cache2EN, or_4_out, WriteEN);
  or or_5 (or_5_out, cache3hit, and_13_out);
  and and_21 (cache3EN, or_5_out, WriteEN);
  or or_6 (or_6_out, cache4hit, and_14_out);
  and and_22 (cache4EN, or_6_out, WriteEN);
  or or_7 (or_7_out, cache5hit, and_15_out);
  and and_23 (cache5EN, or_7_out, WriteEN);
  or or_8 (or_8_out, cache6hit, and_16_out);
  and and_24 (cache6EN, or_8_out, WriteEN);
  or or_9 (or_9_out, cache7hit, and_17_out);
  and and_25 (cache7EN, or_9_out, WriteEN);
  Comparator #(.width(32), .mode("twosComplement")) comparator_9 (
    .a(PC), .b(\cache0_分支指令地址_2 ), .eq(comparator_9_eq));  // open: gt, lt
  Comparator #(.width(32), .mode("twosComplement")) comparator_10 (
    .a(PC), .b(\cache1_分支指令地址_2 ), .eq(comparator_10_eq));  // open: gt, lt
  Comparator #(.width(32), .mode("twosComplement")) comparator_11 (
    .a(PC), .b(\cache2_分支指令地址_2 ), .eq(comparator_11_eq));  // open: gt, lt
  Comparator #(.width(32), .mode("twosComplement")) comparator_12 (
    .a(PC), .b(\cache3_分支指令地址_2 ), .eq(comparator_12_eq));  // open: gt, lt
  Comparator #(.width(32), .mode("twosComplement")) comparator_13 (
    .a(PC), .b(\cache4_分支指令地址_2 ), .eq(comparator_13_eq));  // open: gt, lt
  Comparator #(.width(32), .mode("twosComplement")) comparator_14 (
    .a(PC), .b(\cache5_分支指令地址_2 ), .eq(comparator_14_eq));  // open: gt, lt
  Comparator #(.width(32), .mode("twosComplement")) comparator_15 (
    .a(PC), .b(\cache6_分支指令地址_2 ), .eq(comparator_15_eq));  // open: gt, lt
  Comparator #(.width(32), .mode("twosComplement")) comparator_16 (
    .a(PC), .b(\cache7_分支指令地址_2 ), .eq(comparator_16_eq));  // open: gt, lt
  and and_26 (and_26_out, cache0Valid, comparator_9_eq);
  assign controlled_buffer_9_out = and_26_out ? \cache0_分支预测历史位_2  : 2'bz;  // Controlled_Buffer controlled_buffer_9
  and and_27 (and_27_out, cache1Valid, comparator_10_eq);
  assign controlled_buffer_9_out = and_27_out ? \cache1_分支预测历史位_2  : 2'bz;  // Controlled_Buffer controlled_buffer_10
  and and_28 (and_28_out, cache2Valid, comparator_11_eq);
  assign controlled_buffer_9_out = and_28_out ? \cache2_分支预测历史位_2  : 2'bz;  // Controlled_Buffer controlled_buffer_11
  and and_29 (and_29_out, cache3Valid, comparator_12_eq);
  assign controlled_buffer_9_out = and_29_out ? \cache3_分支预测历史位_2  : 2'bz;  // Controlled_Buffer controlled_buffer_12
  and and_30 (and_30_out, cache4Valid, comparator_13_eq);
  assign controlled_buffer_9_out = and_30_out ? \cache4_分支预测历史位_2  : 2'bz;  // Controlled_Buffer controlled_buffer_13
  and and_31 (and_31_out, cache5Valid, comparator_14_eq);
  assign controlled_buffer_9_out = and_31_out ? \cache5_分支预测历史位_2  : 2'bz;  // Controlled_Buffer controlled_buffer_14
  and and_32 (and_32_out, cache6Valid, comparator_15_eq);
  assign controlled_buffer_9_out = and_32_out ? \cache6_分支预测历史位_2  : 2'bz;  // Controlled_Buffer controlled_buffer_15
  and and_33 (and_33_out, cache7Valid, comparator_16_eq);
  assign controlled_buffer_9_out = and_33_out ? \cache7_分支预测历史位_2  : 2'bz;  // Controlled_Buffer controlled_buffer_16
  assign JumpAddress = and_26_out ? \cache0_分支目标地址_2  : 32'bz;  // Controlled_Buffer controlled_buffer_17
  assign JumpAddress = and_27_out ? \cache1_分支目标地址_2  : 32'bz;  // Controlled_Buffer controlled_buffer_18
  assign JumpAddress = and_28_out ? \cache2_分支目标地址_2  : 32'bz;  // Controlled_Buffer controlled_buffer_19
  assign JumpAddress = and_29_out ? \cache3_分支目标地址_2  : 32'bz;  // Controlled_Buffer controlled_buffer_20
  assign JumpAddress = and_30_out ? \cache4_分支目标地址_2  : 32'bz;  // Controlled_Buffer controlled_buffer_21
  assign JumpAddress = and_31_out ? \cache5_分支目标地址_2  : 32'bz;  // Controlled_Buffer controlled_buffer_22
  assign JumpAddress = and_32_out ? \cache6_分支目标地址_2  : 32'bz;  // Controlled_Buffer controlled_buffer_23
  assign JumpAddress = and_33_out ? \cache7_分支目标地址_2  : 32'bz;  // Controlled_Buffer controlled_buffer_24
  or or_10 (or_10_out, and_26_out, and_27_out, and_28_out, and_29_out, and_30_out, and_31_out, and_32_out, and_33_out);
  not not_1 (Miss, or_10_out);
  Multiplexer #(.select(1), .width(2), .disabled("Z"), .enable("false")) multiplexer_1 (
    .in0(controlled_buffer_9_out), .in1(2'b01), .out(PC_State), .sel(Miss));
  Multiplexer #(.select(1), .width(2), .disabled("Z"), .enable("false")) multiplexer_2 (
    .in0(2'b01), .in1(controlled_buffer_1_out), .out(WritePC_state), .sel(WriteHit));

  // Other names for the same wires on the sheet: cachehit = WriteHit

  // Notes on the sheet:
  //   写入时 如果命中 cachexEN=1
  //   如果未命中 根据decd电路找到要写入的路
  //   写入：
  //   如果要写入的分支指令已在BTB中，直接修改
  //   读取：将PC和各个cache的分支指令地址并发比较并输出命中的那一路的分支目标地址，都未命中则Miss为1
  //   如果要写入的分支指令没有在BTB中，选择需要写入的一路，并将要写入的分支指令地址和分支目标地址写入BTB
endmodule

module \L指令分线器  (
  input  lb,
  input  [1:0] offset,
  input  [31:0] Imm32,
  output [31:0] Imm32_2
);

  wire [31:0] multiplexer_1_out;

  Multiplexer #(.select(2), .width(8), .disabled("Z"), .enable("false")) multiplexer_1 (
    .in0(Imm32[7:0]), .in1(Imm32[15:8]), .in2(Imm32[23:16]), .in3(Imm32[31:24]),
    .out({multiplexer_1_out[31], multiplexer_1_out[6:0]}), .sel(offset));
  Multiplexer #(.select(1), .width(32), .disabled("Z"), .enable("false")) multiplexer_2 (
    .in0(Imm32), .in1({{25{multiplexer_1_out[31]}}, multiplexer_1_out[6:0]}), .out(Imm32_2), .sel(lb));
endmodule

module \中断信号产生  (
  input  CLK,
  input  IR1,
  input  \同步清零信号 ,
  input  IR2,
  input  \同步清零信号_2 ,
  input  IR3,
  input  \同步清零信号_3 ,
  output \IR1与中断屏蔽位与 ,
  output W1,
  output \IR2与中断屏蔽位与 ,
  output W2,
  output \IR3与中断屏蔽位与 ,
  output W3
);

  wire and_1_out, and_2_out, and_3_out, d_ff_1_q, d_ff_2_q, d_ff_3_q, or_4_out, or_5_out, or_6_out;

  or or_1 (W1, \IR1与中断屏蔽位与 , d_ff_1_q);
  or or_2 (W2, \IR2与中断屏蔽位与 , d_ff_2_q);
  or or_3 (W3, \IR3与中断屏蔽位与 , d_ff_3_q);
  D_Flip_Flop #(.trigger("rising"), .Pre_Clr_Positions("LEGACY"), .NegatePresetClear("false"), .enable("true"), .NewFFLayout("false")) d_ff_1 (
    .clk(IR1), .D(1'b1), .Q(d_ff_1_q), .reset(\IR1与中断屏蔽位与 ));  // open: Qn, preset, en
  D_Flip_Flop #(.trigger("rising"), .Pre_Clr_Positions("LEGACY"), .NegatePresetClear("false"), .enable("true"), .NewFFLayout("false")) d_ff_2 (
    .clk(IR2), .D(1'b1), .Q(d_ff_2_q), .reset(\IR2与中断屏蔽位与 ));  // open: Qn, preset, en
  D_Flip_Flop #(.trigger("rising"), .Pre_Clr_Positions("LEGACY"), .NegatePresetClear("false"), .enable("true"), .NewFFLayout("false")) d_ff_3 (
    .clk(IR3), .D(1'b1), .Q(d_ff_3_q), .reset(\IR3与中断屏蔽位与 ));  // open: Qn, preset, en
  or or_4 (or_4_out, d_ff_1_q, \IR1与中断屏蔽位与 );
  or or_5 (or_5_out, d_ff_2_q, \IR2与中断屏蔽位与 );
  or or_6 (or_6_out, d_ff_3_q, \IR3与中断屏蔽位与 );
  and and_1 (and_1_out, or_4_out, ~\同步清零信号 );  // AND_Gate
  and and_2 (and_2_out, or_5_out, ~\同步清零信号_2 );  // AND_Gate
  and and_3 (and_3_out, or_6_out, ~\同步清零信号_3 );  // AND_Gate
  D_Flip_Flop #(.trigger("rising"), .Pre_Clr_Positions("LEGACY"), .NegatePresetClear("false"), .enable("true"), .NewFFLayout("false")) \IR1中断请求寄存器  (
    .clk(CLK), .D(and_1_out), .Q(\IR1与中断屏蔽位与 ));  // open: Qn, preset, en, reset
  D_Flip_Flop #(.trigger("rising"), .Pre_Clr_Positions("LEGACY"), .NegatePresetClear("false"), .enable("true"), .NewFFLayout("false")) \IR2中断请求寄存器  (
    .clk(CLK), .D(and_2_out), .Q(\IR2与中断屏蔽位与 ));  // open: Qn, preset, en, reset
  D_Flip_Flop #(.trigger("rising"), .Pre_Clr_Positions("LEGACY"), .NegatePresetClear("false"), .enable("true"), .NewFFLayout("false")) \IR3中断请求寄存器  (
    .clk(CLK), .D(and_3_out), .Q(\IR3与中断屏蔽位与 ));  // open: Qn, preset, en, reset

  // Notes on the sheet:
  //   Reset 
  //   Reset 
  //   Reset 
endmodule
