// Logisim project zyt.circ as structural Verilog: 34 circuits, main circuit ◇单周期RISC-V
module \单周期RISC_V  (
  input  IR1,
  input  IR2,
  input  IR3,
  output RegWrite,
  output MemWrite,
  output [31:0] PC,
  output [31:0] IR,
  output [31:0] RDin,
  output [31:0] MDin,
  output [31:0] LedData
);

  wire alu_1_equal, alu_1_out_6, and_3_out, and_4_out, and_5_out, CLK, clock_1_out, comparator_1_eq,
       comparator_2_eq, comparator_2_lt, d_ff_1_q, ecall, Go, halt, IR1_t, IR2_t, IR3_t, IRA, IRB, IRC, JALR,
       nand_1_out, not_1_out, not_2_out, not_3_out, not_4_out, not_5_out, or_1_out, or_2_out, or_3_out,
       or_7_out, or_8_out, riscv_probe_1_p3, RST, sb, ss, W1, W2, W3, \单周期硬布线控制器_1_alu_src ,
       \单周期硬布线控制器_1_beq , \单周期硬布线控制器_1_blt , \单周期硬布线控制器_1_bne , \单周期硬布线控制器_1_jal , \单周期硬布线控制器_1_memtoreg ,
       \单周期硬布线控制器_1_s_type ;
  wire [3:0] \单周期硬布线控制器_1_alu_op ;
  wire [4:0] multiplexer_2_out, multiplexer_3_out;
  wire [11:0] alu_1_result, multiplexer_4_out;
  wire [12:0] CNT_num;
  wire [15:0] \总周期数 ;
  wire [31:0] adder_1_out, adder_2_out, bit_extender_1_out, bit_extender_2_out, bit_extender_3_out,
       multiplexer_1_out, multiplexer_6_out, multiplexer_7_out, multiplexer_8_out, multiplexer_9_out,
       multiplexer_10_out, ram_1_dout, regifile_1_r1, shifter_1_out;
  wire [31:12] alu_1_result_2;

  Button \u_继续运行  (.out(Go));
  Button _1 (.out(IRA));
  Button _2 (.out(IRB));
  Button _3 (.out(IRC));
  LED #(.active("true")) led_1 (.in(W1));
  LED #(.active("true")) led_2 (.in(W2));
  LED #(.active("true")) led_3 (.in(W3));
  or or_1 (or_1_out, \单周期硬布线控制器_1_jal , JALR, or_7_out);
  Multiplexer #(.select(1), .width(32), .disabled("Z"), .enable("false")) multiplexer_1 (
    .in0(adder_1_out), .in1(multiplexer_9_out), .out(multiplexer_1_out), .sel(or_1_out));
  not not_1 (not_1_out, halt);
  Hex_Digit_Display hex_digit_display_1 (.value(LedData[31:28]));  // open: dp
  Register #(.width(32), .trigger("rising"), .Select("low")) u_PC (
    .D(multiplexer_1_out), .en(or_2_out), .Q(PC), .clk(CLK), .clr(RST));
  or or_2 (or_2_out, Go, not_1_out);
  Adder #(.width(32)) adder_1 (.a(PC), .b(32'h4), .out(adder_1_out));  // open: cin, cout
  Hex_Digit_Display hex_digit_display_2 (.value(LedData[23:20]));  // open: dp
  Hex_Digit_Display hex_digit_display_3 (.value(LedData[27:24]));  // open: dp
  Hex_Digit_Display hex_digit_display_4 (.value(LedData[19:16]));  // open: dp
  Hex_Digit_Display hex_digit_display_5 (.value(LedData[15:12]));  // open: dp
  or or_3 (or_3_out, \单周期硬布线控制器_1_jal , JALR);
  // RiscV_Probe riscv_probe_1: pin names not known; wires that end beside it: PC[11:2], IR, riscv_probe_1_p3
  Hex_Digit_Display hex_digit_display_6 (.value(LedData[7:4]));  // open: dp
  Hex_Digit_Display hex_digit_display_7 (.value(LedData[11:8]));  // open: dp
  // Probe on \总周期数 
  ROM #(.addrWidth(10), .dataWidth(32), .Select("high")) rom_1 (.addr(PC[11:2]), .data(IR));
  Hex_Digit_Display hex_digit_display_8 (.value(LedData[3:0]));  // open: dp
  \单周期硬布线控制器  \u_单周期硬布线控制器_1  (
    .Funct({IR[30], IR[25], IR[14:12]}), .OP(IR[6:2]), .ALU_OP(\单周期硬布线控制器_1_alu_op ),
    .MemToReg(\单周期硬布线控制器_1_memtoreg ), .MemWrite(MemWrite), .ALU_SRC(\单周期硬布线控制器_1_alu_src ),
    .RegWrite(RegWrite), .ecall(ecall), .S_type(\单周期硬布线控制器_1_s_type ), .Jalr(JALR), .Beq(\单周期硬布线控制器_1_beq ),
    .JAL(\单周期硬布线控制器_1_jal ), .Bne(\单周期硬布线控制器_1_bne ), .in_3(IR[21]), .uret(riscv_probe_1_p3),
    .blt(\单周期硬布线控制器_1_blt ), .sb(sb));  // open: csrrsi, csrrci
  Multiplexer #(.select(1), .width(5), .disabled("Z"), .enable("false")) multiplexer_2 (
    .in0(IR[19:15]), .in1(5'b10001), .out(multiplexer_2_out), .sel(ecall));
  Multiplexer #(.select(1), .width(5), .disabled("Z"), .enable("false")) multiplexer_3 (
    .in0(IR[24:20]), .in1(5'b01010), .out(multiplexer_3_out), .sel(ecall));
  Multiplexer #(.select(1), .width(12), .disabled("Z"), .enable("false")) multiplexer_4 (
    .in0(IR[31:20]), .in1({IR[31:25], IR[11:7]}), .out(multiplexer_4_out), .sel(\单周期硬布线控制器_1_s_type ));
  or or_4 (IR1_t, IR1, IRA);
  assign bit_extender_1_out = {{20{IR[31]}}, {IR[31], IR[7], IR[30:25], IR[11:8]}};  // Bit_Extender bit_extender_1
  assign bit_extender_2_out = {{12{IR[31]}}, {IR[31], IR[19:12], IR[20], IR[30:21]}};  // Bit_Extender bit_extender_2
  Multiplexer #(.select(1), .width(32), .disabled("Z"), .enable("false")) multiplexer_5 (
    .in0(multiplexer_10_out), .in1(adder_1_out), .out(RDin), .sel(or_3_out));
  or or_5 (IR2_t, IR2, IRB);
  Regifile regifile_1 (
    .Din(RDin), .Clk(CLK), .R1(regifile_1_r1), .R2(MDin), .WE(RegWrite), .W_num(IR[11:7]),
    .R1_num(multiplexer_2_out), .R2_num(multiplexer_3_out));
  assign bit_extender_3_out = {{20{multiplexer_4_out[11]}}, multiplexer_4_out};  // Bit_Extender bit_extender_3
  Multiplexer #(.select(1), .width(32), .disabled("Z"), .enable("false")) multiplexer_6 (
    .in0(bit_extender_2_out), .in1(bit_extender_1_out), .out(multiplexer_6_out), .sel(or_7_out));
  Multiplexer #(.select(1), .width(32), .disabled("Z"), .enable("false")) multiplexer_7 (
    .in0(MDin), .in1(bit_extender_3_out), .out(multiplexer_7_out), .sel(\单周期硬布线控制器_1_alu_src ));
  Multiplexer #(.select(1), .width(32), .disabled("Z"), .enable("false")) multiplexer_8 (
    .in0(LedData), .in1(MDin), .out(multiplexer_8_out), .sel(ss));
  or or_6 (IR3_t, IR3, IRC);
  Comparator #(.width(32), .mode("twosComplement")) comparator_1 (
    .a(32'h22), .b(regifile_1_r1), .eq(comparator_1_eq));  // open: gt, lt
  and and_1 (ss, comparator_1_eq, ecall);
  not not_2 (not_2_out, comparator_1_eq);
  and and_2 (halt, not_2_out, ecall);
  not not_3 (not_3_out, alu_1_equal);
  and and_3 (and_3_out, \单周期硬布线控制器_1_beq , alu_1_equal);
  ALU alu_1 (
    .X(regifile_1_r1), .Y(multiplexer_7_out), .AluOP(\单周期硬布线控制器_1_alu_op ), .Equal(alu_1_equal),
    .Result({alu_1_result_2, alu_1_result}), .out_6(alu_1_out_6));  // open: Result_2, out_4
  Shifter #(.width(32), .shift("ll")) shifter_1 (.in(multiplexer_6_out), .\dist (5'b00001), .out(shifter_1_out));
  and and_4 (and_4_out, \单周期硬布线控制器_1_bne , not_3_out);
  Adder #(.width(32)) adder_2 (.a(shifter_1_out), .b(PC), .out(adder_2_out));  // open: cin, cout
  and and_5 (and_5_out, \单周期硬布线控制器_1_blt , alu_1_out_6);
  RAM ram_1 (
    .Mode(sb), .\字节地址 (alu_1_result), .Din(MDin), .CLK(CLK), .str(MemWrite), .id(not_4_out), .Dout(ram_1_dout));
  not not_4 (not_4_out, MemWrite);
  Multiplexer #(.select(1), .width(32), .disabled("Z"), .enable("false")) multiplexer_9 (
    .in0(adder_2_out), .in1({alu_1_result_2, alu_1_result}), .out(multiplexer_9_out), .sel(JALR));
  or or_7 (or_7_out, and_4_out, and_5_out, and_3_out);
  Register #(.width(32), .trigger("rising"), .Select("low")) register_1 (
    .D(multiplexer_8_out), .en(ss), .Q(LedData), .clk(CLK));  // open: clr
  Multiplexer #(.select(1), .width(32), .disabled("Z"), .enable("false")) multiplexer_10 (
    .in0({alu_1_result_2, alu_1_result}), .in1(ram_1_dout), .out(multiplexer_10_out),
    .sel(\单周期硬布线控制器_1_memtoreg ));
  D_Flip_Flop #(.trigger("high"), .Pre_Clr_Positions("LEGACY"), .NegatePresetClear("false"), .enable("true"), .NewFFLayout("false")) d_ff_1 (.Q(d_ff_1_q));  // open: clk, D, Qn, preset, en, reset
  // Probe on 13'hc
  Comparator #(.width(13), .mode("twosComplement")) comparator_2 (
    .a(CNT_num), .b(13'hc), .eq(comparator_2_eq), .lt(comparator_2_lt));  // open: gt
  Clock #(.highDuration(1), .lowDuration(1)) clock_1 (.out(clock_1_out));
  Counter #(.width(13), .max('h1fff), .ongoal("stay"), .trigger("rising"), .behavior("old")) counter_1 (
    .count(comparator_2_lt), .Q(CNT_num), .clk(clock_1_out));  // open: load, D, carry, clr, preset
  nand nand_1 (nand_1_out, d_ff_1_q, comparator_2_eq);
  or or_8 (or_8_out, Go, not_5_out);
  not not_5 (not_5_out, halt);
  assign CLK = nand_1_out ? clock_1_out : 1'bz;  // Controlled_Buffer controlled_buffer_1
  Pull_Resistor #(.pull(1)) pull_resistor_1 (.node(CLK));
  Counter #(.width(16), .max('hffff), .ongoal("wrap"), .trigger("rising"), .behavior("new")) counter_2 (
    .count(or_8_out), .Q(\总周期数 ), .clk(CLK));  // open: load, D, carry, clr, preset, down

  // Notes on the sheet:
  //   中断源
  //   中断等待指示
  //   数码管输出
  //   指令探针
  //   指令存储器
  //   指令字
  //   contents of rom_1 (hex, n*v repeats v):
  //   100493 100006f 100493 200913 300993 100006f 100493 200913 300993 100006f 100493 200913 300993
  //   100006f 100493 200913 300993 3ac000ef 100413 100493 1f49493 900533 2200893 73 24d493 48463 fedff06f
  //   900533 2200893 73 100493 249493 900533 2200893 73 48463 fedff06f 100493 1f49493 900533 2200893 73
  //   4034d493 900533 2200893 73 4044d493 900533 2200893 73 4044d493 900533 2200893 73 4044d493 900533
  //   2200893 73 4044d493 900533 2200893 73 4044d493 900533 2200893 73 4044d493 900533 2200893 73 4044d493
  //   900533 2200893 73 100413 1f41993 41f9d993 433 c00913 300b13 140413 f47413 800293 100313 499993
  //   89e9b3 1300533 2200893 73 406282b3 fe0294e3 140413 f00f93 1f47433 1c41413 800293 100313 49d993
  //   89e9b3 1300533 2200893 73 406282b3 fe0294e3 1c45413 406b0b33 b0463 f95ff06f 2b3 fff2c293 829293
  //   ff2e293 500533 2200893 73 fff00413 493 84a023 140413 448493 84a023 140413 448493 84a023 140413
  //   448493 84a023 140413 448493 84a023 140413 448493 84a023 140413 448493 84a023 140413 448493 84a023
  //   140413 448493 84a023 140413 448493 84a023 140413 448493 84a023 140413 448493 84a023 140413 448493
  //   84a023 140413 448493 84a023 140413 448493 84a023 140413 448493 84a023 140413 448493 140413 433
  //   3c00493 42983 4aa03 149a2b3 28663 134a023 1442023 ffc48493 fe9412e3 800533 2200893 73 440413 3c00493
  //   fc9416e3 3200893 73 100293 300313 800493 849493 7648493 1449493 900533 2200893 73 800e13 54d4b3
  //   64d4b3 900533 2200893 73 fffe0e13 fe0e14e3 a00893 73 fff00293 7700493 849493 7748493 900533 2200893
  //   73 1000e13 54c4b3 900533 2200893 73 fffe0e13 fe0e16e3 a00893 73 313 2000e13 493 100913 930023 900533
  //   2200893 73 12484b3 130313 fffe0e13 fe0e12e3 800e13 313 32483 900533 2200893 73 430313 fffe0e13
  //   fe0e14e3 a00893 73 ff100493 900533 2200893 73 148493 fe04c8e3 a00893 73 a00893 73 413 140413 800533
  //   2200893 73 240413 800533 2200893 73 340413 800533 2200893 73 440413 800533 2200893 73 540413 800533
  //   2200893 73 640413 800533 2200893 73 740413 800533 2200893 73 840413 800533 2200893 2200893 73 8067
  //   JAL
  //   JALR
  //   URET
  //   Beq
  //   Bne
  //   MemToReg
  //   MemWrite
  //   AluOP
  //   AluSrcB
  //   RegWrite
  //   数据存储器
  //   为方便自动评测，需要输出PC，IR，寄存器堆写如数据RDin
  //   RAM写使能MemWrite、RAM写入数据MDin等信号
  //   控制位
  //   暂停节拍，不能为0
  //   戳工具置1进入计数暂停模式，ctrl+k时钟自动运行到对应节拍暂停
  //   ctrl+k关闭时钟连续运行，将控制位置零，进入单步调试模式调试
  //   用这个时钟源需要去掉电路中的其他时钟源
  //   可计数暂停的时钟源
endmodule

// 单周期硬布线控制器
module \单周期硬布线控制器  (
  input  [4:0] OP,
  input  [4:0] Funct,
  input  in_3,
  output [3:0] ALU_OP,
  output uret,
  output MemToReg,
  output ecall,
  output MemWrite,
  output ALU_SRC,
  output RegWrite,
  output S_type,
  output Beq,
  output Bne,
  output Jalr,
  output JAL,
  output csrrsi,
  output blt,
  output csrrci,
  output sb
);

  wire \控制信号自动生成_1_ecall ;

  \运算控制器自动生成  \u_运算控制器自动生成_1  (
    .OP2(OP[0]), .OP3(OP[1]), .OP4(OP[2]), .OP5(OP[3]), .OP6(OP[4]), .F12(Funct[0]), .F13(Funct[1]),
    .F14(Funct[2]), .F25(Funct[3]), .F30(Funct[4]), .S0(ALU_OP[0]), .S1(ALU_OP[1]), .S2(ALU_OP[2]),
    .S3(ALU_OP[3]));
  \控制信号自动生成  \u_控制信号自动生成_1  (
    .OP2(OP[0]), .OP3(OP[1]), .MemToReg(MemToReg), .OP4(OP[2]), .OP5(OP[3]), .OP6(OP[4]), .F12(Funct[0]),
    .F13(Funct[1]), .F14(Funct[2]), .MemWrite(MemWrite), .F25(Funct[3]), .F30(Funct[4]), .ALU_SRC(ALU_SRC),
    .RegWrite(RegWrite), .ecall(\控制信号自动生成_1_ecall ), .S_Type(S_type), .BEQ(Beq), .BNE(Bne), .JALR(Jalr),
    .JAL(JAL), .BLT(blt), .SB(sb), .csrrsi(csrrsi), .csrrci(csrrci));
  and and_1 (uret, in_3, \控制信号自动生成_1_ecall );
  and and_2 (ecall, ~in_3, \控制信号自动生成_1_ecall );  // AND_Gate

  // Other names for the same wires on the sheet: IR21 = in_3; OP_CODE[4:0] = OP

  // Notes on the sheet:
  //   运算器控制器，根据指令生成运算器功能选择信号
  //   控制信号生成，产生数据通路需要的其他控制信号
endmodule

// 运算器控制器
module \运算控制器自动生成  (
  input  OP2,
  input  OP3,
  input  OP4,
  input  OP5,
  input  OP6,
  input  F12,
  input  F13,
  input  F14,
  input  F25,
  input  F30,
  output S0,
  output S1,
  output S2,
  output S3
);

  wire and_1_out, and_2_out, and_3_out, and_4_out, and_5_out, and_6_out, and_7_out, and_8_out, and_9_out,
       and_10_out, and_11_out, and_12_out, and_13_out, and_14_out, and_15_out, and_16_out, and_17_out,
       and_18_out, and_19_out, and_20_out, and_21_out, and_22_out, and_23_out, and_24_out, and_25_out,
       and_26_out, and_27_out, and_28_out, and_29_out, and_30_out, and_31_out, and_32_out, and_33_out,
       and_34_out, and_35_out, and_36_out, and_37_out, and_38_out, and_39_out, and_40_out, not_1_out,
       not_2_out, not_3_out, not_4_out, not_5_out, not_6_out, not_7_out, not_8_out, not_9_out, not_10_out,
       not_11_out, not_12_out, not_13_out, not_14_out, not_15_out, not_16_out, not_17_out, not_18_out,
       not_19_out, not_20_out, not_21_out, not_22_out, not_23_out, not_24_out, not_25_out, not_26_out,
       not_27_out, not_28_out, not_29_out, not_30_out, not_31_out, not_32_out, not_33_out, not_34_out,
       not_35_out, not_36_out, not_37_out, not_38_out, not_39_out, not_40_out, not_41_out, not_42_out,
       not_43_out, not_44_out, not_45_out, not_46_out, not_47_out, not_48_out, not_49_out, not_50_out,
       not_51_out, not_52_out, not_53_out, not_54_out, not_55_out, not_56_out, not_57_out, not_58_out,
       not_59_out, not_60_out, not_61_out, not_62_out, not_63_out, not_64_out, not_65_out, not_66_out,
       not_67_out, not_68_out, not_69_out, not_70_out, not_71_out, not_72_out, not_73_out, not_74_out,
       not_75_out, not_76_out, not_77_out, not_78_out, not_79_out, not_80_out, not_81_out, not_82_out,
       not_83_out, not_84_out, not_85_out, not_86_out, not_87_out, not_88_out, not_89_out, not_90_out,
       not_91_out, not_92_out, not_93_out, not_94_out, not_95_out, not_96_out, not_97_out, not_98_out,
       not_99_out, not_100_out, not_101_out, not_102_out, not_103_out, not_104_out, not_105_out, not_106_out,
       not_107_out, not_108_out, not_109_out, not_110_out, not_111_out, not_112_out, not_113_out,
       not_114_out, not_115_out, not_116_out, not_117_out, not_118_out, not_119_out, not_120_out,
       not_121_out, not_122_out, not_123_out, not_124_out, not_125_out, not_126_out, not_127_out,
       not_128_out, not_129_out, not_130_out, not_131_out, not_132_out, not_133_out, not_134_out,
       not_135_out, not_136_out, not_137_out, not_138_out, not_139_out, not_140_out, not_141_out,
       not_142_out, not_143_out, not_144_out, not_145_out, not_146_out, not_147_out, not_148_out,
       not_149_out, not_150_out, not_151_out, not_152_out, not_153_out, not_154_out, not_155_out,
       not_156_out, not_157_out, not_158_out, not_159_out, not_160_out, not_161_out, not_162_out,
       not_163_out, not_164_out, not_165_out, not_166_out, not_167_out, not_168_out, not_169_out,
       not_170_out, not_171_out, not_172_out, not_173_out, not_174_out, not_175_out, not_176_out,
       not_177_out, not_178_out, not_179_out, not_180_out, not_181_out, not_182_out, not_183_out,
       not_184_out, not_185_out, not_186_out, not_187_out, not_188_out, not_189_out, not_190_out,
       not_191_out, not_192_out, not_193_out, not_194_out, not_195_out, not_196_out, not_197_out,
       not_198_out, not_199_out, not_200_out, not_201_out, not_202_out, not_203_out, not_204_out,
       not_205_out, not_206_out, not_207_out, not_208_out, not_209_out, not_210_out, not_211_out,
       not_212_out, not_213_out, not_214_out, not_215_out, not_216_out, not_217_out, not_218_out,
       not_219_out, not_220_out, not_221_out, not_222_out, not_223_out, not_224_out, not_225_out,
       not_226_out, not_227_out, not_228_out, not_229_out, not_230_out, not_231_out, not_232_out,
       not_233_out, not_234_out, not_235_out, not_236_out, not_237_out, not_238_out, not_239_out,
       not_240_out, not_241_out, not_242_out, not_243_out;

  not not_1 (not_1_out, F30);
  not not_2 (not_2_out, F25);
  not not_3 (not_3_out, F14);
  not not_4 (not_4_out, F13);
  not not_5 (not_5_out, F12);
  not not_6 (not_6_out, OP6);
  not not_7 (not_7_out, OP3);
  not not_8 (not_8_out, OP2);
  not not_9 (not_9_out, F30);
  not not_10 (not_10_out, F25);
  not not_11 (not_11_out, OP6);
  not not_12 (not_12_out, OP3);
  not not_13 (not_13_out, OP2);
  not not_14 (not_14_out, F30);
  not not_15 (not_15_out, F25);
  not not_16 (not_16_out, F14);
  not not_17 (not_17_out, F12);
  not not_18 (not_18_out, OP6);
  not not_19 (not_19_out, OP3);
  not not_20 (not_20_out, OP2);
  not not_21 (not_21_out, F14);
  not not_22 (not_22_out, F13);
  not not_23 (not_23_out, F12);
  not not_24 (not_24_out, OP6);
  not not_25 (not_25_out, OP5);
  not not_26 (not_26_out, OP3);
  not not_27 (not_27_out, OP2);
  not not_28 (not_28_out, OP6);
  not not_29 (not_29_out, OP5);
  not not_30 (not_30_out, OP3);
  not not_31 (not_31_out, OP2);
  not not_32 (not_32_out, F13);
  not not_33 (not_33_out, F12);
  not not_34 (not_34_out, OP6);
  not not_35 (not_35_out, OP5);
  not not_36 (not_36_out, OP3);
  not not_37 (not_37_out, OP2);
  not not_38 (not_38_out, F14);
  not not_39 (not_39_out, F12);
  not not_40 (not_40_out, OP6);
  not not_41 (not_41_out, OP5);
  not not_42 (not_42_out, OP3);
  not not_43 (not_43_out, OP2);
  not not_44 (not_44_out, F25);
  not not_45 (not_45_out, F13);
  not not_46 (not_46_out, OP6);
  not not_47 (not_47_out, OP5);
  not not_48 (not_48_out, OP3);
  not not_49 (not_49_out, OP2);
  not not_50 (not_50_out, F14);
  not not_51 (not_51_out, F12);
  not not_52 (not_52_out, OP6);
  not not_53 (not_53_out, OP5);
  not not_54 (not_54_out, OP4);
  not not_55 (not_55_out, OP3);
  not not_56 (not_56_out, OP2);
  not not_57 (not_57_out, F14);
  not not_58 (not_58_out, F12);
  not not_59 (not_59_out, OP6);
  not not_60 (not_60_out, OP4);
  not not_61 (not_61_out, OP3);
  not not_62 (not_62_out, OP2);
  not not_63 (not_63_out, F14);
  not not_64 (not_64_out, F13);
  not not_65 (not_65_out, F12);
  not not_66 (not_66_out, OP4);
  not not_67 (not_67_out, OP3);
  not not_68 (not_68_out, F30);
  not not_69 (not_69_out, F25);
  not not_70 (not_70_out, F13);
  not not_71 (not_71_out, F12);
  not not_72 (not_72_out, OP6);
  not not_73 (not_73_out, OP3);
  not not_74 (not_74_out, OP2);
  not not_75 (not_75_out, F14);
  not not_76 (not_76_out, F13);
  not not_77 (not_77_out, F12);
  not not_78 (not_78_out, OP6);
  not not_79 (not_79_out, OP4);
  not not_80 (not_80_out, OP3);
  not not_81 (not_81_out, OP2);
  not not_82 (not_82_out, F13);
  not not_83 (not_83_out, F12);
  not not_84 (not_84_out, OP4);
  not not_85 (not_85_out, OP3);
  not not_86 (not_86_out, OP2);
  not not_87 (not_87_out, F25);
  not not_88 (not_88_out, F14);
  not not_89 (not_89_out, F13);
  not not_90 (not_90_out, F12);
  not not_91 (not_91_out, OP6);
  not not_92 (not_92_out, OP3);
  not not_93 (not_93_out, OP2);
  not not_94 (not_94_out, F30);
  not not_95 (not_95_out, F25);
  not not_96 (not_96_out, OP6);
  not not_97 (not_97_out, OP3);
  not not_98 (not_98_out, OP2);
  not not_99 (not_99_out, F30);
  not not_100 (not_100_out, F25);
  not not_101 (not_101_out, F14);
  not not_102 (not_102_out, F12);
  not not_103 (not_103_out, OP6);
  not not_104 (not_104_out, OP3);
  not not_105 (not_105_out, OP2);
  not not_106 (not_106_out, OP6);
  not not_107 (not_107_out, OP5);
  not not_108 (not_108_out, OP3);
  not not_109 (not_109_out, OP2);
  not not_110 (not_110_out, F14);
  not not_111 (not_111_out, F12);
  not not_112 (not_112_out, OP6);
  not not_113 (not_113_out, OP5);
  not not_114 (not_114_out, OP3);
  not not_115 (not_115_out, OP2);
  not not_116 (not_116_out, F30);
  not not_117 (not_117_out, F25);
  not not_118 (not_118_out, F13);
  not not_119 (not_119_out, OP6);
  not not_120 (not_120_out, OP5);
  not not_121 (not_121_out, OP3);
  not not_122 (not_122_out, OP2);
  not not_123 (not_123_out, F30);
  not not_124 (not_124_out, F25);
  not not_125 (not_125_out, F13);
  not not_126 (not_126_out, OP6);
  not not_127 (not_127_out, OP3);
  not not_128 (not_128_out, OP2);
  not not_129 (not_129_out, F13);
  not not_130 (not_130_out, F12);
  not not_131 (not_131_out, OP4);
  not not_132 (not_132_out, OP3);
  not not_133 (not_133_out, OP2);
  not not_134 (not_134_out, F30);
  not not_135 (not_135_out, F25);
  not not_136 (not_136_out, F14);
  not not_137 (not_137_out, F13);
  not not_138 (not_138_out, F12);
  not not_139 (not_139_out, OP6);
  not not_140 (not_140_out, OP3);
  not not_141 (not_141_out, OP2);
  not not_142 (not_142_out, F25);
  not not_143 (not_143_out, F14);
  not not_144 (not_144_out, F13);
  not not_145 (not_145_out, F12);
  not not_146 (not_146_out, OP6);
  not not_147 (not_147_out, OP3);
  not not_148 (not_148_out, OP2);
  not not_149 (not_149_out, F30);
  not not_150 (not_150_out, F25);
  not not_151 (not_151_out, OP6);
  not not_152 (not_152_out, OP3);
  not not_153 (not_153_out, OP2);
  not not_154 (not_154_out, F30);
  not not_155 (not_155_out, F25);
  not not_156 (not_156_out, F14);
  not not_157 (not_157_out, OP6);
  not not_158 (not_158_out, OP3);
  not not_159 (not_159_out, OP2);
  not not_160 (not_160_out, F14);
  not not_161 (not_161_out, F13);
  not not_162 (not_162_out, F12);
  not not_163 (not_163_out, OP6);
  not not_164 (not_164_out, OP5);
  not not_165 (not_165_out, OP3);
  not not_166 (not_166_out, OP2);
  not not_167 (not_167_out, OP6);
  not not_168 (not_168_out, OP5);
  not not_169 (not_169_out, OP3);
  not not_170 (not_170_out, OP2);
  not not_171 (not_171_out, F14);
  not not_172 (not_172_out, F12);
  not not_173 (not_173_out, OP6);
  not not_174 (not_174_out, OP5);
  not not_175 (not_175_out, OP4);
  not not_176 (not_176_out, OP3);
  not not_177 (not_177_out, OP2);
  not not_178 (not_178_out, F14);
  not not_179 (not_179_out, F12);
  not not_180 (not_180_out, OP6);
  not not_181 (not_181_out, OP4);
  not not_182 (not_182_out, OP3);
  not not_183 (not_183_out, OP2);
  not not_184 (not_184_out, F14);
  not not_185 (not_185_out, F13);
  not not_186 (not_186_out, F12);
  not not_187 (not_187_out, OP4);
  not not_188 (not_188_out, OP3);
  not not_189 (not_189_out, F14);
  not not_190 (not_190_out, F13);
  not not_191 (not_191_out, F12);
  not not_192 (not_192_out, OP6);
  not not_193 (not_193_out, OP4);
  not not_194 (not_194_out, OP3);
  not not_195 (not_195_out, OP2);
  not not_196 (not_196_out, F30);
  not not_197 (not_197_out, F25);
  not not_198 (not_198_out, F12);
  not not_199 (not_199_out, OP6);
  not not_200 (not_200_out, OP3);
  not not_201 (not_201_out, OP2);
  not not_202 (not_202_out, F30);
  not not_203 (not_203_out, F25);
  not not_204 (not_204_out, F14);
  not not_205 (not_205_out, F12);
  not not_206 (not_206_out, OP6);
  not not_207 (not_207_out, OP3);
  not not_208 (not_208_out, OP2);
  not not_209 (not_209_out, F30);
  not not_210 (not_210_out, F25);
  not not_211 (not_211_out, F14);
  not not_212 (not_212_out, OP6);
  not not_213 (not_213_out, OP3);
  not not_214 (not_214_out, OP2);
  not not_215 (not_215_out, F12);
  not not_216 (not_216_out, OP6);
  not not_217 (not_217_out, OP5);
  not not_218 (not_218_out, OP3);
  not not_219 (not_219_out, OP2);
  not not_220 (not_220_out, F13);
  not not_221 (not_221_out, F12);
  not not_222 (not_222_out, OP6);
  not not_223 (not_223_out, OP5);
  not not_224 (not_224_out, OP3);
  not not_225 (not_225_out, OP2);
  not not_226 (not_226_out, F14);
  not not_227 (not_227_out, F12);
  not not_228 (not_228_out, OP6);
  not not_229 (not_229_out, OP5);
  not not_230 (not_230_out, OP3);
  not not_231 (not_231_out, OP2);
  not not_232 (not_232_out, F30);
  not not_233 (not_233_out, F25);
  not not_234 (not_234_out, F13);
  not not_235 (not_235_out, F12);
  not not_236 (not_236_out, OP6);
  not not_237 (not_237_out, OP3);
  not not_238 (not_238_out, OP2);
  not not_239 (not_239_out, F13);
  not not_240 (not_240_out, F12);
  not not_241 (not_241_out, OP4);
  not not_242 (not_242_out, OP3);
  not not_243 (not_243_out, OP2);
  and and_1 (and_1_out, not_1_out, not_2_out, not_3_out, not_4_out, not_5_out, not_6_out, OP5, OP4, not_7_out, not_8_out);
  and and_2 (and_2_out, not_9_out, not_10_out, F14, F13, F12, not_11_out, OP5, OP4, not_12_out, not_13_out);
  and and_3 (and_3_out, not_14_out, not_15_out, not_16_out, F13, not_17_out, not_18_out, OP5, OP4, not_19_out, not_20_out);
  and and_4 (and_4_out, not_21_out, not_22_out, not_23_out, not_24_out, not_25_out, OP4, not_26_out, not_27_out);
  and and_5 (and_5_out, F14, F13, F12, not_28_out, not_29_out, OP4, not_30_out, not_31_out);
  and and_6 (and_6_out, F14, not_32_out, not_33_out, not_34_out, not_35_out, OP4, not_36_out, not_37_out);
  and and_7 (and_7_out, not_38_out, F13, not_39_out, not_40_out, not_41_out, OP4, not_42_out, not_43_out);
  and and_8 (and_8_out, F30, not_44_out, F14, not_45_out, F12, not_46_out, not_47_out, OP4, not_48_out, not_49_out);
  and and_9 (and_9_out, not_50_out, F13, not_51_out, not_52_out, not_53_out, not_54_out, not_55_out, not_56_out);
  and and_10 (and_10_out, not_57_out, F13, not_58_out, not_59_out, OP5, not_60_out, not_61_out, not_62_out);
  and and_11 (and_11_out, not_63_out, not_64_out, not_65_out, OP6, OP5, not_66_out, not_67_out, OP2);
  and and_12 (and_12_out, not_68_out, not_69_out, F14, not_70_out, not_71_out, not_72_out, OP5, OP4, not_73_out, not_74_out);
  and and_13 (and_13_out, not_75_out, not_76_out, not_77_out, not_78_out, OP5, not_79_out, not_80_out, not_81_out);
  and and_14 (and_14_out, F14, not_82_out, not_83_out, OP6, OP5, not_84_out, not_85_out, not_86_out);
  and and_15 (and_15_out, F30, not_87_out, not_88_out, not_89_out, not_90_out, not_91_out, OP5, OP4, not_92_out, not_93_out);
  and and_16 (and_16_out, not_94_out, not_95_out, F14, F13, F12, not_96_out, OP5, OP4, not_97_out, not_98_out);
  and and_17 (and_17_out, not_99_out, not_100_out, not_101_out, F13, not_102_out, not_103_out, OP5, OP4, not_104_out, not_105_out);
  and and_18 (and_18_out, F14, F13, F12, not_106_out, not_107_out, OP4, not_108_out, not_109_out);
  and and_19 (and_19_out, not_110_out, F13, not_111_out, not_112_out, not_113_out, OP4, not_114_out, not_115_out);
  and and_20 (and_20_out, not_116_out, not_117_out, F14, not_118_out, F12, not_119_out, not_120_out, OP4, not_121_out, not_122_out);
  and and_21 (and_21_out, not_123_out, not_124_out, F14, not_125_out, F12, not_126_out, OP5, OP4, not_127_out, not_128_out);
  and and_22 (and_22_out, F14, not_129_out, not_130_out, OP6, OP5, not_131_out, not_132_out, not_133_out);
  and and_23 (and_23_out, not_134_out, not_135_out, not_136_out, not_137_out, not_138_out, not_139_out, OP5, OP4, not_140_out, not_141_out);
  and and_24 (and_24_out, F30, not_142_out, not_143_out, not_144_out, not_145_out, not_146_out, OP5, OP4, not_147_out, not_148_out);
  and and_25 (and_25_out, not_149_out, not_150_out, F14, F13, F12, not_151_out, OP5, OP4, not_152_out, not_153_out);
  and and_26 (and_26_out, not_154_out, not_155_out, not_156_out, F13, F12, not_157_out, OP5, OP4, not_158_out, not_159_out);
  and and_27 (and_27_out, not_160_out, not_161_out, not_162_out, not_163_out, not_164_out, OP4, not_165_out, not_166_out);
  and and_28 (and_28_out, F14, F13, F12, not_167_out, not_168_out, OP4, not_169_out, not_170_out);
  and and_29 (and_29_out, not_171_out, F13, not_172_out, not_173_out, not_174_out, not_175_out, not_176_out, not_177_out);
  and and_30 (and_30_out, not_178_out, F13, not_179_out, not_180_out, OP5, not_181_out, not_182_out, not_183_out);
  and and_31 (and_31_out, not_184_out, not_185_out, not_186_out, OP6, OP5, not_187_out, not_188_out, OP2);
  and and_32 (and_32_out, not_189_out, not_190_out, not_191_out, not_192_out, OP5, not_193_out, not_194_out, not_195_out);
  and and_33 (and_33_out, not_196_out, not_197_out, F14, F13, not_198_out, not_199_out, OP5, OP4, not_200_out, not_201_out);
  and and_34 (and_34_out, not_202_out, not_203_out, not_204_out, F13, not_205_out, not_206_out, OP5, OP4, not_207_out, not_208_out);
  and and_35 (and_35_out, not_209_out, not_210_out, not_211_out, F13, F12, not_212_out, OP5, OP4, not_213_out, not_214_out);
  and and_36 (and_36_out, F14, F13, not_215_out, not_216_out, not_217_out, OP4, not_218_out, not_219_out);
  and and_37 (and_37_out, F14, not_220_out, not_221_out, not_222_out, not_223_out, OP4, not_224_out, not_225_out);
  and and_38 (and_38_out, not_226_out, F13, not_227_out, not_228_out, not_229_out, OP4, not_230_out, not_231_out);
  and and_39 (and_39_out, not_232_out, not_233_out, F14, not_234_out, not_235_out, not_236_out, OP5, OP4, not_237_out, not_238_out);
  and and_40 (and_40_out, F14, not_239_out, not_240_out, OP6, OP5, not_241_out, not_242_out, not_243_out);
  or or_1 (S0, and_1_out, and_2_out, and_3_out, and_4_out, and_5_out, and_6_out, and_7_out, and_8_out, and_9_out, and_10_out, and_11_out, and_12_out, and_13_out, and_14_out);
  or or_2 (S1, and_15_out, and_16_out, and_17_out, and_18_out, and_19_out, and_20_out, and_21_out, and_22_out);
  or or_3 (S2, and_23_out, and_24_out, and_25_out, and_26_out, and_27_out, and_28_out, and_29_out, and_30_out, and_31_out, and_32_out);
  or or_4 (S3, and_33_out, and_34_out, and_35_out, and_36_out, and_37_out, and_38_out, and_39_out, and_40_out);
endmodule

// 控制信号生成
module \控制信号自动生成  (
  input  OP2,
  input  OP3,
  input  OP4,
  input  OP5,
  input  OP6,
  input  F12,
  input  F13,
  input  F14,
  input  F25,
  input  F30,
  output MemToReg,
  output MemWrite,
  output ALU_SRC,
  output RegWrite,
  output ecall,
  output S_Type,
  output BEQ,
  output BNE,
  output JALR,
  output JAL,
  output BLT,
  output SB,
  output csrrsi,
  output csrrci
);

  wire and_2_out, and_3_out, and_4_out, and_5_out, and_6_out, and_7_out, and_8_out, and_9_out, and_10_out,
       and_11_out, and_12_out, and_13_out, and_14_out, and_15_out, and_16_out, and_17_out, and_18_out,
       and_19_out, and_20_out, and_21_out, and_22_out, and_23_out, and_24_out, and_25_out, and_26_out,
       and_27_out, and_28_out, and_29_out, and_30_out, and_31_out, and_32_out, and_33_out, and_34_out,
       and_36_out, and_37_out, not_1_out, not_2_out, not_3_out, not_4_out, not_5_out, not_6_out, not_7_out,
       not_8_out, not_9_out, not_10_out, not_11_out, not_12_out, not_13_out, not_14_out, not_15_out,
       not_16_out, not_17_out, not_18_out, not_19_out, not_20_out, not_21_out, not_22_out, not_23_out,
       not_24_out, not_25_out, not_26_out, not_27_out, not_28_out, not_29_out, not_30_out, not_31_out,
       not_32_out, not_33_out, not_34_out, not_35_out, not_36_out, not_37_out, not_38_out, not_39_out,
       not_40_out, not_41_out, not_42_out, not_43_out, not_44_out, not_45_out, not_46_out, not_47_out,
       not_48_out, not_49_out, not_50_out, not_51_out, not_52_out, not_53_out, not_54_out, not_55_out,
       not_56_out, not_57_out, not_58_out, not_59_out, not_60_out, not_61_out, not_62_out, not_63_out,
       not_64_out, not_65_out, not_66_out, not_67_out, not_68_out, not_69_out, not_70_out, not_71_out,
       not_72_out, not_73_out, not_74_out, not_75_out, not_76_out, not_77_out, not_78_out, not_79_out,
       not_80_out, not_81_out, not_82_out, not_83_out, not_84_out, not_85_out, not_86_out, not_87_out,
       not_88_out, not_89_out, not_90_out, not_91_out, not_92_out, not_93_out, not_94_out, not_95_out,
       not_96_out, not_97_out, not_98_out, not_99_out, not_100_out, not_101_out, not_102_out, not_103_out,
       not_104_out, not_105_out, not_106_out, not_107_out, not_108_out, not_109_out, not_110_out,
       not_111_out, not_112_out, not_113_out, not_114_out, not_115_out, not_116_out, not_117_out,
       not_118_out, not_119_out, not_120_out, not_121_out, not_122_out, not_123_out, not_124_out,
       not_125_out, not_126_out, not_127_out, not_128_out, not_129_out, not_130_out, not_131_out,
       not_132_out, not_133_out, not_134_out, not_135_out, not_136_out, not_137_out, not_138_out,
       not_139_out, not_140_out, not_141_out, not_142_out, not_143_out, not_144_out, not_145_out,
       not_146_out, not_147_out, not_148_out, not_149_out, not_150_out, not_151_out, not_152_out,
       not_153_out, not_154_out, not_155_out, not_156_out, not_157_out, not_158_out, not_159_out,
       not_160_out, not_161_out, not_162_out, not_163_out, not_164_out, not_165_out, not_166_out,
       not_167_out, not_168_out, not_169_out, not_170_out, not_171_out, not_172_out, not_173_out,
       not_174_out, not_175_out, not_176_out, not_177_out, not_178_out, not_179_out, not_180_out,
       not_181_out, not_182_out, not_183_out, not_184_out, not_185_out, not_186_out, not_187_out,
       not_188_out, not_189_out, not_190_out, not_191_out, not_192_out, not_193_out, not_194_out,
       not_195_out, not_196_out, not_197_out, not_198_out, not_199_out, not_200_out, not_201_out,
       not_202_out, not_203_out, not_204_out, not_205_out, not_206_out, not_207_out, not_208_out,
       not_209_out, not_210_out, not_211_out, not_212_out, not_213_out, not_214_out, not_215_out,
       not_216_out, not_217_out, not_218_out, not_219_out, not_220_out, not_221_out, not_222_out,
       not_223_out, not_224_out, not_225_out, not_226_out, not_227_out, not_228_out, not_229_out,
       not_230_out, not_231_out, not_232_out, not_233_out, not_234_out, not_235_out, not_236_out,
       not_237_out, not_238_out, not_239_out, not_240_out, not_241_out, not_242_out, not_243_out,
       not_244_out, not_245_out, not_246_out, not_247_out, not_248_out, not_249_out, not_250_out,
       not_251_out, not_252_out, not_253_out, not_254_out, not_255_out, not_256_out, not_257_out,
       not_258_out, not_259_out, not_260_out, not_261_out, not_262_out;

  not not_1 (not_1_out, F14);
  not not_2 (not_2_out, F12);
  not not_3 (not_3_out, OP6);
  not not_4 (not_4_out, OP5);
  not not_5 (not_5_out, OP4);
  not not_6 (not_6_out, OP3);
  not not_7 (not_7_out, OP2);
  not not_8 (not_8_out, F14);
  not not_9 (not_9_out, F12);
  not not_10 (not_10_out, OP6);
  not not_11 (not_11_out, OP4);
  not not_12 (not_12_out, OP3);
  not not_13 (not_13_out, OP2);
  not not_14 (not_14_out, F14);
  not not_15 (not_15_out, F13);
  not not_16 (not_16_out, F12);
  not not_17 (not_17_out, OP6);
  not not_18 (not_18_out, OP4);
  not not_19 (not_19_out, OP3);
  not not_20 (not_20_out, OP2);
  not not_21 (not_21_out, F14);
  not not_22 (not_22_out, F13);
  not not_23 (not_23_out, F12);
  not not_24 (not_24_out, OP6);
  not not_25 (not_25_out, OP5);
  not not_26 (not_26_out, OP3);
  not not_27 (not_27_out, OP2);
  not not_28 (not_28_out, OP6);
  not not_29 (not_29_out, OP5);
  not not_30 (not_30_out, OP3);
  not not_31 (not_31_out, OP2);
  not not_32 (not_32_out, F12);
  not not_33 (not_33_out, OP6);
  not not_34 (not_34_out, OP5);
  not not_35 (not_35_out, OP3);
  not not_36 (not_36_out, OP2);
  not not_37 (not_37_out, F13);
  not not_38 (not_38_out, F12);
  not not_39 (not_39_out, OP6);
  not not_40 (not_40_out, OP5);
  not not_41 (not_41_out, OP3);
  not not_42 (not_42_out, OP2);
  not not_43 (not_43_out, F14);
  not not_44 (not_44_out, F12);
  not not_45 (not_45_out, OP6);
  not not_46 (not_46_out, OP5);
  not not_47 (not_47_out, OP3);
  not not_48 (not_48_out, OP2);
  not not_49 (not_49_out, F30);
  not not_50 (not_50_out, F25);
  not not_51 (not_51_out, F14);
  not not_52 (not_52_out, F13);
  not not_53 (not_53_out, OP6);
  not not_54 (not_54_out, OP5);
  not not_55 (not_55_out, OP3);
  not not_56 (not_56_out, OP2);
  not not_57 (not_57_out, F30);
  not not_58 (not_58_out, F25);
  not not_59 (not_59_out, F13);
  not not_60 (not_60_out, OP6);
  not not_61 (not_61_out, OP5);
  not not_62 (not_62_out, OP3);
  not not_63 (not_63_out, OP2);
  not not_64 (not_64_out, F25);
  not not_65 (not_65_out, F13);
  not not_66 (not_66_out, OP6);
  not not_67 (not_67_out, OP5);
  not not_68 (not_68_out, OP3);
  not not_69 (not_69_out, OP2);
  not not_70 (not_70_out, F14);
  not not_71 (not_71_out, F12);
  not not_72 (not_72_out, OP6);
  not not_73 (not_73_out, OP5);
  not not_74 (not_74_out, OP4);
  not not_75 (not_75_out, OP3);
  not not_76 (not_76_out, OP2);
  not not_77 (not_77_out, F14);
  not not_78 (not_78_out, F12);
  not not_79 (not_79_out, OP6);
  not not_80 (not_80_out, OP4);
  not not_81 (not_81_out, OP3);
  not not_82 (not_82_out, OP2);
  not not_83 (not_83_out, F14);
  not not_84 (not_84_out, F13);
  not not_85 (not_85_out, F12);
  not not_86 (not_86_out, OP4);
  not not_87 (not_87_out, OP3);
  not not_88 (not_88_out, F14);
  not not_89 (not_89_out, F13);
  not not_90 (not_90_out, F12);
  not not_91 (not_91_out, OP6);
  not not_92 (not_92_out, OP4);
  not not_93 (not_93_out, OP3);
  not not_94 (not_94_out, OP2);
  not not_95 (not_95_out, F30);
  not not_96 (not_96_out, F25);
  not not_97 (not_97_out, F14);
  not not_98 (not_98_out, F13);
  not not_99 (not_99_out, F12);
  not not_100 (not_100_out, OP6);
  not not_101 (not_101_out, OP3);
  not not_102 (not_102_out, OP2);
  not not_103 (not_103_out, F25);
  not not_104 (not_104_out, F14);
  not not_105 (not_105_out, F13);
  not not_106 (not_106_out, F12);
  not not_107 (not_107_out, OP6);
  not not_108 (not_108_out, OP3);
  not not_109 (not_109_out, OP2);
  not not_110 (not_110_out, F30);
  not not_111 (not_111_out, F25);
  not not_112 (not_112_out, OP6);
  not not_113 (not_113_out, OP3);
  not not_114 (not_114_out, OP2);
  not not_115 (not_115_out, F30);
  not not_116 (not_116_out, F25);
  not not_117 (not_117_out, F12);
  not not_118 (not_118_out, OP6);
  not not_119 (not_119_out, OP3);
  not not_120 (not_120_out, OP2);
  not not_121 (not_121_out, F30);
  not not_122 (not_122_out, F25);
  not not_123 (not_123_out, F14);
  not not_124 (not_124_out, F12);
  not not_125 (not_125_out, OP6);
  not not_126 (not_126_out, OP3);
  not not_127 (not_127_out, OP2);
  not not_128 (not_128_out, F30);
  not not_129 (not_129_out, F25);
  not not_130 (not_130_out, F14);
  not not_131 (not_131_out, OP6);
  not not_132 (not_132_out, OP3);
  not not_133 (not_133_out, OP2);
  not not_134 (not_134_out, F14);
  not not_135 (not_135_out, F13);
  not not_136 (not_136_out, F12);
  not not_137 (not_137_out, OP6);
  not not_138 (not_138_out, OP5);
  not not_139 (not_139_out, OP3);
  not not_140 (not_140_out, OP2);
  not not_141 (not_141_out, OP6);
  not not_142 (not_142_out, OP5);
  not not_143 (not_143_out, OP3);
  not not_144 (not_144_out, OP2);
  not not_145 (not_145_out, F12);
  not not_146 (not_146_out, OP6);
  not not_147 (not_147_out, OP5);
  not not_148 (not_148_out, OP3);
  not not_149 (not_149_out, OP2);
  not not_150 (not_150_out, F13);
  not not_151 (not_151_out, F12);
  not not_152 (not_152_out, OP6);
  not not_153 (not_153_out, OP5);
  not not_154 (not_154_out, OP3);
  not not_155 (not_155_out, OP2);
  not not_156 (not_156_out, F14);
  not not_157 (not_157_out, F12);
  not not_158 (not_158_out, OP6);
  not not_159 (not_159_out, OP5);
  not not_160 (not_160_out, OP3);
  not not_161 (not_161_out, OP2);
  not not_162 (not_162_out, F30);
  not not_163 (not_163_out, F25);
  not not_164 (not_164_out, F14);
  not not_165 (not_165_out, F13);
  not not_166 (not_166_out, OP6);
  not not_167 (not_167_out, OP5);
  not not_168 (not_168_out, OP3);
  not not_169 (not_169_out, OP2);
  not not_170 (not_170_out, F30);
  not not_171 (not_171_out, F25);
  not not_172 (not_172_out, F13);
  not not_173 (not_173_out, OP6);
  not not_174 (not_174_out, OP5);
  not not_175 (not_175_out, OP3);
  not not_176 (not_176_out, OP2);
  not not_177 (not_177_out, F25);
  not not_178 (not_178_out, F13);
  not not_179 (not_179_out, OP6);
  not not_180 (not_180_out, OP5);
  not not_181 (not_181_out, OP3);
  not not_182 (not_182_out, OP2);
  not not_183 (not_183_out, F14);
  not not_184 (not_184_out, F12);
  not not_185 (not_185_out, OP6);
  not not_186 (not_186_out, OP5);
  not not_187 (not_187_out, OP4);
  not not_188 (not_188_out, OP3);
  not not_189 (not_189_out, OP2);
  not not_190 (not_190_out, OP4);
  not not_191 (not_191_out, F14);
  not not_192 (not_192_out, F13);
  not not_193 (not_193_out, F12);
  not not_194 (not_194_out, OP4);
  not not_195 (not_195_out, OP3);
  not not_196 (not_196_out, F30);
  not not_197 (not_197_out, F25);
  not not_198 (not_198_out, F13);
  not not_199 (not_199_out, OP6);
  not not_200 (not_200_out, OP3);
  not not_201 (not_201_out, OP2);
  not not_202 (not_202_out, F30);
  not not_203 (not_203_out, F25);
  not not_204 (not_204_out, F13);
  not not_205 (not_205_out, F12);
  not not_206 (not_206_out, OP6);
  not not_207 (not_207_out, OP3);
  not not_208 (not_208_out, OP2);
  not not_209 (not_209_out, F30);
  not not_210 (not_210_out, F25);
  not not_211 (not_211_out, F14);
  not not_212 (not_212_out, F13);
  not not_213 (not_213_out, F12);
  not not_214 (not_214_out, OP3);
  not not_215 (not_215_out, OP2);
  not not_216 (not_216_out, F14);
  not not_217 (not_217_out, F12);
  not not_218 (not_218_out, OP6);
  not not_219 (not_219_out, OP4);
  not not_220 (not_220_out, OP3);
  not not_221 (not_221_out, OP2);
  not not_222 (not_222_out, F14);
  not not_223 (not_223_out, F13);
  not not_224 (not_224_out, F12);
  not not_225 (not_225_out, OP6);
  not not_226 (not_226_out, OP4);
  not not_227 (not_227_out, OP3);
  not not_228 (not_228_out, OP2);
  not not_229 (not_229_out, F14);
  not not_230 (not_230_out, F13);
  not not_231 (not_231_out, F12);
  not not_232 (not_232_out, OP4);
  not not_233 (not_233_out, OP3);
  not not_234 (not_234_out, OP2);
  not not_235 (not_235_out, F14);
  not not_236 (not_236_out, F13);
  not not_237 (not_237_out, OP4);
  not not_238 (not_238_out, OP3);
  not not_239 (not_239_out, OP2);
  not not_240 (not_240_out, F14);
  not not_241 (not_241_out, F13);
  not not_242 (not_242_out, F12);
  not not_243 (not_243_out, OP4);
  not not_244 (not_244_out, OP3);
  not not_245 (not_245_out, OP4);
  not not_246 (not_246_out, F13);
  not not_247 (not_247_out, F12);
  not not_248 (not_248_out, OP4);
  not not_249 (not_249_out, OP3);
  not not_250 (not_250_out, OP2);
  not not_251 (not_251_out, F14);
  not not_252 (not_252_out, F13);
  not not_253 (not_253_out, F12);
  not not_254 (not_254_out, OP6);
  not not_255 (not_255_out, OP4);
  not not_256 (not_256_out, OP3);
  not not_257 (not_257_out, OP2);
  not not_258 (not_258_out, F12);
  not not_259 (not_259_out, OP3);
  not not_260 (not_260_out, OP2);
  not not_261 (not_261_out, OP3);
  not not_262 (not_262_out, OP2);
  and and_1 (MemToReg, not_1_out, F13, not_2_out, not_3_out, not_4_out, not_5_out, not_6_out, not_7_out);
  and and_2 (and_2_out, not_8_out, F13, not_9_out, not_10_out, OP5, not_11_out, not_12_out, not_13_out);
  and and_3 (and_3_out, not_14_out, not_15_out, not_16_out, not_17_out, OP5, not_18_out, not_19_out, not_20_out);
  and and_4 (and_4_out, not_21_out, not_22_out, not_23_out, not_24_out, not_25_out, OP4, not_26_out, not_27_out);
  and and_5 (and_5_out, F14, F13, F12, not_28_out, not_29_out, OP4, not_30_out, not_31_out);
  and and_6 (and_6_out, F14, F13, not_32_out, not_33_out, not_34_out, OP4, not_35_out, not_36_out);
  and and_7 (and_7_out, F14, not_37_out, not_38_out, not_39_out, not_40_out, OP4, not_41_out, not_42_out);
  and and_8 (and_8_out, not_43_out, F13, not_44_out, not_45_out, not_46_out, OP4, not_47_out, not_48_out);
  and and_9 (and_9_out, not_49_out, not_50_out, not_51_out, not_52_out, F12, not_53_out, not_54_out, OP4, not_55_out, not_56_out);
  and and_10 (and_10_out, not_57_out, not_58_out, F14, not_59_out, F12, not_60_out, not_61_out, OP4, not_62_out, not_63_out);
  and and_11 (and_11_out, F30, not_64_out, F14, not_65_out, F12, not_66_out, not_67_out, OP4, not_68_out, not_69_out);
  and and_12 (and_12_out, not_70_out, F13, not_71_out, not_72_out, not_73_out, not_74_out, not_75_out, not_76_out);
  and and_13 (and_13_out, not_77_out, F13, not_78_out, not_79_out, OP5, not_80_out, not_81_out, not_82_out);
  and and_14 (and_14_out, not_83_out, not_84_out, not_85_out, OP6, OP5, not_86_out, not_87_out, OP2);
  and and_15 (and_15_out, not_88_out, not_89_out, not_90_out, not_91_out, OP5, not_92_out, not_93_out, not_94_out);
  and and_16 (and_16_out, not_95_out, not_96_out, not_97_out, not_98_out, not_99_out, not_100_out, OP5, OP4, not_101_out, not_102_out);
  and and_17 (and_17_out, F30, not_103_out, not_104_out, not_105_out, not_106_out, not_107_out, OP5, OP4, not_108_out, not_109_out);
  and and_18 (and_18_out, not_110_out, not_111_out, F14, F13, F12, not_112_out, OP5, OP4, not_113_out, not_114_out);
  and and_19 (and_19_out, not_115_out, not_116_out, F14, F13, not_117_out, not_118_out, OP5, OP4, not_119_out, not_120_out);
  and and_20 (and_20_out, not_121_out, not_122_out, not_123_out, F13, not_124_out, not_125_out, OP5, OP4, not_126_out, not_127_out);
  and and_21 (and_21_out, not_128_out, not_129_out, not_130_out, F13, F12, not_131_out, OP5, OP4, not_132_out, not_133_out);
  and and_22 (and_22_out, not_134_out, not_135_out, not_136_out, not_137_out, not_138_out, OP4, not_139_out, not_140_out);
  and and_23 (and_23_out, F14, F13, F12, not_141_out, not_142_out, OP4, not_143_out, not_144_out);
  and and_24 (and_24_out, F14, F13, not_145_out, not_146_out, not_147_out, OP4, not_148_out, not_149_out);
  and and_25 (and_25_out, F14, not_150_out, not_151_out, not_152_out, not_153_out, OP4, not_154_out, not_155_out);
  and and_26 (and_26_out, not_156_out, F13, not_157_out, not_158_out, not_159_out, OP4, not_160_out, not_161_out);
  and and_27 (and_27_out, not_162_out, not_163_out, not_164_out, not_165_out, F12, not_166_out, not_167_out, OP4, not_168_out, not_169_out);
  and and_28 (and_28_out, not_170_out, not_171_out, F14, not_172_out, F12, not_173_out, not_174_out, OP4, not_175_out, not_176_out);
  and and_29 (and_29_out, F30, not_177_out, F14, not_178_out, F12, not_179_out, not_180_out, OP4, not_181_out, not_182_out);
  and and_30 (and_30_out, not_183_out, F13, not_184_out, not_185_out, not_186_out, not_187_out, not_188_out, not_189_out);
  and and_31 (and_31_out, OP6, OP5, not_190_out, OP3, OP2);
  and and_32 (and_32_out, not_191_out, not_192_out, not_193_out, OP6, OP5, not_194_out, not_195_out, OP2);
  and and_33 (and_33_out, not_196_out, not_197_out, F14, not_198_out, F12, not_199_out, OP5, OP4, not_200_out, not_201_out);
  and and_34 (and_34_out, not_202_out, not_203_out, F14, not_204_out, not_205_out, not_206_out, OP5, OP4, not_207_out, not_208_out);
  and and_35 (ecall, not_209_out, not_210_out, not_211_out, not_212_out, not_213_out, OP6, OP5, OP4, not_214_out, not_215_out);
  and and_36 (and_36_out, not_216_out, F13, not_217_out, not_218_out, OP5, not_219_out, not_220_out, not_221_out);
  and and_37 (and_37_out, not_222_out, not_223_out, not_224_out, not_225_out, OP5, not_226_out, not_227_out, not_228_out);
  and and_38 (BEQ, not_229_out, not_230_out, not_231_out, OP6, OP5, not_232_out, not_233_out, not_234_out);
  and and_39 (BNE, not_235_out, not_236_out, F12, OP6, OP5, not_237_out, not_238_out, not_239_out);
  and and_40 (JALR, not_240_out, not_241_out, not_242_out, OP6, OP5, not_243_out, not_244_out, OP2);
  and and_41 (JAL, OP6, OP5, not_245_out, OP3, OP2);
  and and_42 (BLT, F14, not_246_out, not_247_out, OP6, OP5, not_248_out, not_249_out, not_250_out);
  and and_43 (SB, not_251_out, not_252_out, not_253_out, not_254_out, OP5, not_255_out, not_256_out, not_257_out);
  and and_44 (csrrsi, F14, F13, not_258_out, OP6, OP5, OP4, not_259_out, not_260_out);
  and and_45 (csrrci, F14, F13, F12, OP6, OP5, OP4, not_261_out, not_262_out);
  or or_1 (MemWrite, and_2_out, and_3_out);
  or or_2 (S_Type, and_36_out, and_37_out);
  or or_3 (ALU_SRC, and_4_out, and_5_out, and_6_out, and_7_out, and_8_out, and_9_out, and_10_out, and_11_out, and_12_out, and_13_out, and_14_out, and_15_out);
  or or_4 (RegWrite, and_16_out, and_17_out, and_18_out, and_19_out, and_20_out, and_21_out, and_22_out, and_23_out, and_24_out, and_25_out, and_26_out, and_27_out, and_28_out, and_29_out, and_30_out, and_31_out, and_32_out, and_33_out, and_34_out);
endmodule

// ALU
module ALU (
  input  [31:0] X,
  input  [31:0] Y,
  input  [3:0] AluOP,
  output out_4,
  output Equal,
  output out_6,
  output [31:0] Result,
  output [31:0] Result_2
);

  wire [0:0] comparator_1_lt, comparator_2_lt;
  wire [31:0] adder_1_out, AND_out, divider_1_out, divider_1_rem, multiplier_1_cout, multiplier_1_out,
       NOR_out, OR_out, shifter_1_out, shifter_2_out, shifter_3_out, subtractor_1_out, XOR_out;

  assign AND_out = X & Y;  // AND_Gate AND, 32 bits wide
  assign OR_out = X | Y;  // OR_Gate OR, 32 bits wide
  Shifter #(.width(32), .shift("ll")) shifter_1 (.in(X), .\dist (Y[4:0]), .out(shifter_1_out));
  Shifter #(.width(32), .shift("ar")) shifter_2 (.in(X), .\dist (Y[4:0]), .out(shifter_2_out));
  Shifter #(.width(32), .shift("lr")) shifter_3 (.in(X), .\dist (Y[4:0]), .out(shifter_3_out));
  Multiplier #(.width(32)) multiplier_1 (.a(X), .b(Y), .out(multiplier_1_out), .cout(multiplier_1_cout));  // open: cin
  Divider #(.width(32)) divider_1 (.a(X), .b(Y), .out(divider_1_out), .rem(divider_1_rem));  // open: upper
  Adder #(.width(32)) adder_1 (.a(X), .b(Y), .out(adder_1_out));  // open: cin, cout
  Subtractor #(.width(32)) subtractor_1 (.a(X), .b(Y), .out(subtractor_1_out));  // open: bin, bout
  assign XOR_out = X ^ Y;  // XOR_Gate XOR, 32 bits wide
  assign NOR_out = ~(X | Y);  // NOR_Gate NOR, 32 bits wide
  Comparator #(.width(32), .mode("twosComplement")) comparator_1 (
    .a(X), .b(Y), .eq(Equal), .lt(comparator_1_lt[0]));  // open: gt
  Comparator #(.width(32), .mode("unsigned")) comparator_2 (.a(X), .b(Y), .lt(comparator_2_lt[0]));  // open: gt, eq
  Multiplexer #(.select(4), .width(32), .disabled("Z"), .enable("false")) multiplexer_1 (
    .in0(shifter_1_out), .in1(shifter_2_out), .in2(shifter_3_out), .in3(multiplier_1_out),
    .in4(divider_1_out), .in5(adder_1_out), .in6(subtractor_1_out), .in7(AND_out), .in8(OR_out),
    .in9(XOR_out), .in10(NOR_out), .in11({{31{1'b0}}, comparator_1_lt[0]}),
    .in12({{31{1'b0}}, comparator_2_lt[0]}), .in13({32{1'b0}}), .in14({32{1'b0}}), .in15({32{1'b0}}),
    .out(Result), .sel(AluOP));
  Multiplexer #(.select(4), .width(32), .disabled("Z"), .enable("false")) multiplexer_2 (
    .in0({32{1'b0}}), .in1({32{1'b0}}), .in2({32{1'b0}}), .in3(multiplier_1_cout), .in4(divider_1_rem),
    .in5({32{1'b0}}), .in6({32{1'b0}}), .in7({32{1'b0}}), .in8({32{1'b0}}), .in9({32{1'b0}}),
    .in10({32{1'b0}}), .in11({32{1'b0}}), .in12({32{1'b0}}), .in13({32{1'b0}}), .in14({32{1'b0}}),
    .in15({32{1'b0}}), .out(Result_2), .sel(AluOP));
  Multiplexer #(.select(4), .width(1), .disabled("Z"), .enable("false")) multiplexer_3 (
    .in0(1'b0), .in1(1'b0), .in2(1'b0), .in3(1'b0), .in4(1'b0), .in5(1'b0), .in6(1'b0), .in7(1'b0),
    .in8(1'b0), .in9(1'b0), .in10(1'b0), .in11(comparator_1_lt[0]), .in12(comparator_2_lt[0]), .in13(1'b0),
    .in14(1'b0), .in15(1'b0), .out(out_6), .sel(AluOP));
  not not_1 (out_4, out_6);

  // Other names for the same wires on the sheet: Result2[31:0] = Result_2; S[3:0] = AluOP; tunnel = out_6;
  //   tunnel_t = out_4

  // Notes on the sheet:
  //   不要改变此引脚区域内容，也不要改变ALU封装形式
  //   输入引脚
  //   输出引脚
endmodule

module Regifile (
  input  [31:0] Din,
  input  Clk,
  input  WE,
  input  [4:0] R1_num,
  input  [4:0] W_num,
  input  [4:0] R2_num,
  output [31:0] R1,
  output [31:0] R2
);

  // RegisterFile registerfile_1: pin names not known; wires that end beside it: Din, Clk, WE, W_num, R1_num, R2_num, R1, R2
endmodule

module \理想流水线  (
  output RegWrite,
  output MemWrite,
  output [31:0] IF_PC,
  output [31:0] ID_PC,
  output [31:0] EX_PC,
  output [31:0] M_PC,
  output [31:0] WB_PC,
  output [31:0] RDin,
  output [31:0] MDin,
  output [31:0] LedData
);

  wire alu_1_p2, alu_1_p6, alu_1_p7, and_3_out, and_4_out, and_5_out, CLK, clock_1_out, comparator_1_eq,
       comparator_1_lt, comparator_2_eq, d_ff_1_q, ecall, ecall2, ex_blt, ex_mem2_1_jalout,
       ex_mem2_1_jalrout, ex_mem2_1_memtoreg_2, ex_mem2_1_regwrite_2, ex_sb, Go, halt, halt1, halt2, id_sb,
       IR1, IR2, IR3, JALR, JJ, mem_sb, mem_wb2_1_jalout, mem_wb2_1_jalrout, mem_wb2_1_memtoreg_2,
       nand_1_out, not_1_out, not_2_out, not_3_out, not_4_out, not_5_out, not_6_out, not_7_out, not_8_out,
       not_9_out, or_1_out, or_2_out, or_3_out, or_4_out, RST, ss, W1, W2, W3, \单周期硬布线控制器_1_s_type ;
  wire [2:0] JJUin, JJUout;
  wire [3:0] id_ex2_1_aluopout, \单周期硬布线控制器_1_alu_op ;
  wire [4:0] ex_mem2_1_writereg_num_2, id_ex2_1_writereg_num_2, multiplexer_2_out, multiplexer_3_out, W_F;
  wire [6:0] signalin, signalout;
  wire [11:0] multiplexer_4_out;
  wire [12:0] CNT_num;
  wire [15:0] \LoadUse次数 , \总周期数 , \插入气泡数 , \无条件分支数 , \条件分支成功数 ;
  wire [31:0] adder_1_out, adder_2_out, alu_1_p8, bit_extender_1_out, bit_extender_2_out, bit_extender_3_out,
       EX_IR, ex_mem2_1_alu_result_2, id_ex2_1_b_imm_2, id_ex2_1_i_s_imm_2, id_ex2_1_j_imm_2, id_ex2_1_r1_2,
       id_ex2_1_r2_2, ID_IR, IF_IR, IR, MEM_IR, mem_wb2_1_alu_result_2, mem_wb2_1_memdata_2,
       multiplexer_1_out, multiplexer_6_out, multiplexer_7_out, multiplexer_8_out, multiplexer_9_out,
       multiplexer_10_out, PC_F, ram_1_dout, regifile_1_r1, regifile_1_r2, rom_1_data, shifter_1_out, WB_IR;

  Button \u_总复位  (.out(RST));
  Button _1 (.out(IR1));
  Button _2 (.out(IR2));
  Button _3 (.out(IR3));
  // Probe on \总周期数 
  // Probe on \总周期数 
  Button \u_继续运行  (.out(Go));
  LED #(.active("true")) led_1 (.in(W1));
  LED #(.active("true")) led_2 (.in(W2));
  LED #(.active("true")) led_3 (.in(W3));
  Hex_Digit_Display hex_digit_display_1 (.value(LedData[31:28]));  // open: dp
  // Probe on IF_PC[19:0]
  // RiscV_Probe riscv_probe_1: pin names not known; wires that end beside it: IF_IR
  Multiplexer #(.select(1), .width(32), .disabled("Z"), .enable("false")) multiplexer_1 (
    .in0(adder_1_out), .in1(multiplexer_9_out), .out(multiplexer_1_out), .sel(or_1_out));
  Hex_Digit_Display hex_digit_display_2 (.value(LedData[27:24]));  // open: dp
  Hex_Digit_Display hex_digit_display_3 (.value(LedData[23:20]));  // open: dp
  // Probe on ID_PC[19:0]
  // RiscV_Probe riscv_probe_2: pin names not known; wires that end beside it: ID_IR
  or or_1 (or_1_out, JJUout[0], JALR, or_3_out);
  or or_2 (or_2_out, Go, not_1_out);
  not not_1 (not_1_out, halt2);
  Adder #(.width(32)) adder_1 (.a(IF_PC), .b(32'h4), .out(adder_1_out));  // open: cin, cout
  Hex_Digit_Display hex_digit_display_4 (.value(LedData[15:12]));  // open: dp
  Hex_Digit_Display hex_digit_display_5 (.value(LedData[19:16]));  // open: dp
  Register #(.width(32), .trigger("rising"), .Select("low")) PC (
    .D(multiplexer_1_out), .en(or_2_out), .Q(IF_PC), .clk(CLK), .clr(RST));
  Hex_Digit_Display hex_digit_display_6 (.value(LedData[11:8]));  // open: dp
  Hex_Digit_Display hex_digit_display_7 (.value(LedData[7:4]));  // open: dp
  // Probe on EX_PC[19:0]
  // RiscV_Probe riscv_probe_3: pin names not known; wires that end beside it: EX_IR
  Hex_Digit_Display hex_digit_display_8 (.value(LedData[3:0]));  // open: dp
  // RiscV_Probe riscv_probe_4: pin names not known; wires that end beside it: IF_PC[11:2], IR, halt2
  ROM #(.addrWidth(10), .dataWidth(32), .Select("high")) rom_1 (.addr(IF_PC[11:2]), .data(rom_1_data));
  // Probe on \总周期数 
  // Probe on M_PC[19:0]
  // RiscV_Probe riscv_probe_5: pin names not known; wires that end beside it: MEM_IR
  IF_ID2 if_id2_1 (
    .IRin(rom_1_data), .PCin(IF_PC), .clk(CLK), .stop(not_2_out), .IRout(IR), .PCout(ID_PC));  // open: bubble
  not not_2 (not_2_out, halt2);
  // Probe on \总周期数 
  // Probe on \无条件分支数 
  // Probe on \条件分支成功数 
  // Probe on \插入气泡数 
  // Probe on \LoadUse次数 
  // Probe on IF_PC[11:0]
  // Probe on WB_PC[19:0]
  // RiscV_Probe riscv_probe_6: pin names not known; wires that end beside it: WB_IR
  // Probe on EX_PC[11:0]
  // Probe on ID_PC[11:0]
  \单周期硬布线控制器  \u_单周期硬布线控制器_1  (
    .Funct({IR[30], IR[25], IR[14:12]}), .OP(IR[6:2]), .ALU_OP(\单周期硬布线控制器_1_alu_op ), .MemToReg(signalin[3]),
    .MemWrite(signalin[2]), .ALU_SRC(signalin[1]), .RegWrite(signalin[0]), .ecall(ecall),
    .S_type(\单周期硬布线控制器_1_s_type ), .Jalr(JJUin[1]), .Beq(signalin[6]), .JAL(JJUin[0]), .Bne(signalin[4]),
    .in_3(IR[21]), .uret(JJUin[2]), .blt(signalin[5]), .sb(id_sb));  // open: csrrsi, csrrci
  Multiplexer #(.select(1), .width(5), .disabled("Z"), .enable("false")) multiplexer_2 (
    .in0(IR[19:15]), .in1(5'b10001), .out(multiplexer_2_out), .sel(ecall));
  Multiplexer #(.select(1), .width(5), .disabled("Z"), .enable("false")) multiplexer_3 (
    .in0(IR[24:20]), .in1(5'b01010), .out(multiplexer_3_out), .sel(ecall));
  Multiplexer #(.select(1), .width(12), .disabled("Z"), .enable("false")) multiplexer_4 (
    .in0(IR[31:20]), .in1({IR[31:25], IR[11:7]}), .out(multiplexer_4_out), .sel(\单周期硬布线控制器_1_s_type ));
  Multiplexer #(.select(1), .width(32), .disabled("Z"), .enable("false")) multiplexer_5 (
    .in0(multiplexer_10_out), .in1(PC_F), .out(RDin), .sel(JJ));
  // Probe on M_PC[11:0]
  D_Flip_Flop #(.trigger("high"), .Pre_Clr_Positions("LEGACY"), .NegatePresetClear("false"), .enable("true"), .NewFFLayout("false")) d_ff_1 (.Q(d_ff_1_q));  // open: clk, D, Qn, preset, en, reset
  // Probe on 13'h14
  assign bit_extender_1_out = {{20{multiplexer_4_out[11]}}, multiplexer_4_out};  // Bit_Extender bit_extender_1
  assign bit_extender_2_out = {{20{IR[31]}}, {IR[31], IR[7], IR[30:25], IR[11:8]}};  // Bit_Extender bit_extender_2
  assign bit_extender_3_out = {{12{IR[31]}}, {IR[31], IR[19:12], IR[20], IR[30:21]}};  // Bit_Extender bit_extender_3
  // Probe on WB_PC[11:0]
  Comparator #(.width(13), .mode("twosComplement")) comparator_1 (
    .a(CNT_num), .b(13'h14), .eq(comparator_1_eq), .lt(comparator_1_lt));  // open: gt
  Clock #(.highDuration(1), .lowDuration(1)) clock_1 (.out(clock_1_out));
  Regifile regifile_1 (
    .Din(RDin), .Clk(CLK), .R1(regifile_1_r1), .R2(regifile_1_r2), .WE(RegWrite), .W_num(W_F),
    .R1_num(multiplexer_2_out), .R2_num(multiplexer_3_out));
  nand nand_1 (nand_1_out, d_ff_1_q, comparator_1_eq);
  Counter #(.width(13), .max('h1fff), .ongoal("stay"), .trigger("rising"), .behavior("old")) counter_1 (
    .count(comparator_1_lt), .Q(CNT_num), .clk(clock_1_out));  // open: load, D, carry, clr, preset
  not not_3 (not_3_out, halt2);
  assign CLK = nand_1_out ? clock_1_out : 1'bz;  // Controlled_Buffer controlled_buffer_1
  ID_EX2 id_ex2_1 (
    .signal(signalin), .ecall(ecall), .JJU(JJUin), .AluOp(\单周期硬布线控制器_1_alu_op ), .R1(regifile_1_r1),
    .R2(regifile_1_r2), .I_S_imm(bit_extender_1_out), .B_imm(bit_extender_2_out), .J_imm(bit_extender_3_out),
    .PCin(ID_PC), .WriteReg_num(IR[11:7]), .CLK(CLK), .stop(not_3_out),
    .signalout({signalout[6], ex_blt, signalout[4:0]}), .ecallout(ecall2),
    .JJUout({JJUout[2], JALR, JJUout[0]}), .AluOpout(id_ex2_1_aluopout), .R1_2(id_ex2_1_r1_2),
    .R2_2(id_ex2_1_r2_2), .I_S_imm_2(id_ex2_1_i_s_imm_2), .B_imm_2(id_ex2_1_b_imm_2),
    .J_imm_2(id_ex2_1_j_imm_2), .PCout(EX_PC), .WriteReg_num_2(id_ex2_1_writereg_num_2), .sb(id_sb),
    .sb_2(ex_sb));  // open: bubble
  Pull_Resistor #(.pull(1)) pull_resistor_1 (.node(CLK));
  Multiplexer #(.select(1), .width(32), .disabled("Z"), .enable("false")) multiplexer_6 (
    .in0(id_ex2_1_j_imm_2), .in1(id_ex2_1_b_imm_2), .out(multiplexer_6_out), .sel(or_3_out));
  Comparator #(.width(32), .mode("twosComplement")) comparator_2 (
    .a(32'h22), .b(id_ex2_1_r1_2), .eq(comparator_2_eq));  // open: gt, lt
  Multiplexer #(.select(1), .width(32), .disabled("Z"), .enable("false")) multiplexer_7 (
    .in0(id_ex2_1_r2_2), .in1(id_ex2_1_i_s_imm_2), .out(multiplexer_7_out), .sel(signalout[1]));
  and and_1 (ss, comparator_2_eq, ecall2);
  Multiplexer #(.select(1), .width(32), .disabled("Z"), .enable("false")) multiplexer_8 (
    .in0(LedData), .in1(id_ex2_1_r2_2), .out(multiplexer_8_out), .sel(ss));
  not not_4 (not_4_out, comparator_2_eq);
  and and_2 (halt, not_4_out, ecall2);
  // ALU alu_1: pin names not known; wires that end beside it: id_ex2_1_r1_2, alu_1_p2, multiplexer_7_out, alu_1_p2, id_ex2_1_aluopout, alu_1_p6, alu_1_p7, alu_1_p8
  Shifter #(.width(32), .shift("ll")) shifter_1 (.in(multiplexer_6_out), .\dist (5'b00001), .out(shifter_1_out));
  and and_3 (and_3_out, ex_blt, alu_1_p7);
  and and_4 (and_4_out, signalout[4], not_5_out);
  not not_5 (not_5_out, alu_1_p6);
  and and_5 (and_5_out, signalout[6], alu_1_p6);
  Adder #(.width(32)) adder_2 (.a(shifter_1_out), .b(EX_PC), .out(adder_2_out));  // open: cin, cout
  or or_3 (or_3_out, and_4_out, and_3_out, and_5_out);
  EX_MEM2 ex_mem2_1 (
    .JALin(JJUout[0]), .JALRin(JALR), .RegWrite(signalout[0]), .MemToReg(signalout[3]),
    .MemWrite(signalout[2]), .Write_Data(id_ex2_1_r2_2), .ALU_Result(alu_1_p8),
    .WriteReg_num(id_ex2_1_writereg_num_2), .PCin(EX_PC), .haltin(halt), .CLK(CLK), .stop(not_6_out),
    .JALout(ex_mem2_1_jalout), .JALRout(ex_mem2_1_jalrout), .RegWrite_2(ex_mem2_1_regwrite_2),
    .MemToReg_2(ex_mem2_1_memtoreg_2), .MemWrite_2(MemWrite), .Write_Data_2(MDin),
    .ALU_Result_2(ex_mem2_1_alu_result_2), .WriteReg_num_2(ex_mem2_1_writereg_num_2), .PCout(M_PC),
    .haltout(halt1), .sb(ex_sb), .sb_2(mem_sb));  // open: bubble
  not not_6 (not_6_out, halt2);
  Multiplexer #(.select(1), .width(32), .disabled("Z"), .enable("false")) multiplexer_9 (
    .in0(adder_2_out), .in1(alu_1_p8), .out(multiplexer_9_out), .sel(JALR));
  or or_4 (or_4_out, Go, not_7_out);
  not not_7 (not_7_out, halt2);
  Register #(.width(32), .trigger("rising"), .Select("low")) register_1 (
    .D(multiplexer_8_out), .en(ss), .Q(LedData), .clk(CLK));  // open: clr
  RAM ram_1 (
    .Mode(mem_sb), .\字节地址 (ex_mem2_1_alu_result_2[11:0]), .Din(MDin), .CLK(CLK), .str(MemWrite),
    .id(not_8_out), .Dout(ram_1_dout));
  not not_8 (not_8_out, MemWrite);
  Counter #(.width(16), .max('hffff), .ongoal("wrap"), .trigger("rising"), .behavior("new")) counter_2 (
    .D(16'h1), .count(or_4_out), .Q(\总周期数 ), .clk(CLK));  // open: load, carry, clr, preset, down
  MEM_WB2 mem_wb2_1 (
    .halt(halt1), .JAL(ex_mem2_1_jalout), .JALR(ex_mem2_1_jalrout), .RegWrite(ex_mem2_1_regwrite_2),
    .MemToReg(ex_mem2_1_memtoreg_2), .ALU_Result(ex_mem2_1_alu_result_2), .MemData(ram_1_dout),
    .WriteReg_num(ex_mem2_1_writereg_num_2), .PC(M_PC), .CLK(CLK), .stop(not_9_out), .haltout(halt2),
    .JALout(mem_wb2_1_jalout), .JALRout(mem_wb2_1_jalrout), .RegWrite_2(RegWrite),
    .MemToReg_2(mem_wb2_1_memtoreg_2), .ALU_Result_2(mem_wb2_1_alu_result_2),
    .MemData_2(mem_wb2_1_memdata_2), .WriteReg_num_2(W_F), .PCout(WB_PC));  // open: bubble
  not not_9 (not_9_out, halt2);
  Multiplexer #(.select(1), .width(32), .disabled("Z"), .enable("false")) multiplexer_10 (
    .in0(mem_wb2_1_alu_result_2), .in1(mem_wb2_1_memdata_2), .out(multiplexer_10_out),
    .sel(mem_wb2_1_memtoreg_2));
  or or_5 (JJ, mem_wb2_1_jalout, mem_wb2_1_jalrout);
  Adder #(.width(32)) adder_3 (.a(WB_PC), .b(32'h4), .out(PC_F));  // open: cin, cout

  // Other names for the same wires on the sheet: W_num[4:0] = IR[11:7]; JJUout[1] = JALR; MEM_PC[31:0] = M_PC;
  //   PC[31:0] = IF_PC; signalout[5] = ex_blt

  // Notes on the sheet:
  //   中断源
  //   时空图监测，可删除
  //   中断等待指示
  //   数码管输出
  //   指令探针
  //   指令存储器
  //   contents of rom_1 (hex, n*v repeats v):
  //   413 493 913 993 46413 14e493 296913 39e993 842023 942223 1242423 1342623 a00893 493 913 993 73
  //   JAL
  //   JALR
  //   URET
  //   控制位
  //   Beq
  //   Bne
  //   MemToReg
  //   MemWrite
  //   AluOP
  //   AluSrcB
  //   RegWrite
  //   流水调试日志用
  //   暂停节拍，不能为0
  //   用这个时钟源需要去掉电路中的其他时钟源
  //   戳工具置1进入计数暂停模式，ctrl+k时钟自动运行到对应节拍暂停
  //   ctrl+k关闭时钟连续运行，将控制位置零，进入单步调试模式调试
  //   可计数暂停的时钟源
  //   为方便自动评测，需要输出流水线各段保存的PC值，注意是PC不是PC+4，另外ID段寄存器写入信息，Mem段内存写入信息也要输出
  //   数据存储器
endmodule

module \气泡流水线  (
  output RegWrite,
  output MemWrite,
  output [31:0] IF_PC,
  output [31:0] ID_PC,
  output [31:0] EX_PC,
  output [31:0] M_PC,
  output [31:0] WB_PC,
  output [31:0] RDin,
  output [31:0] MDin,
  output [31:0] LedData
);

  wire alu_1_p2, alu_1_p6, alu_1_p7, and_1_out, and_2_out, and_5_out, and_6_out, and_7_out, and_8_out,
       and_9_out, and_10_out, and_11_out, and_12_out, B, branchtaken, CLK, clock_1_out, comparator_1_eq,
       comparator_1_lt, comparator_2_eq, d_ff_1_q, DH, ecall, ecall2, ex_blt, ex_mem2_1_jalout,
       ex_mem2_1_jalrout, ex_mem2_1_memtoreg_2, ex_sb, EXRegwrite, Go, H, halt, halt1, halt2, ID_EX_Flush,
       id_sb, IR1, IR2, IR3, jAL, JALR, JJ, mem_sb, mem_wb2_1_jalout, mem_wb2_1_jalrout,
       mem_wb2_1_memtoreg_2, MEMRegwrite, multiplexer_10_out, multiplexer_11_out, multiplexer_13_out,
       nand_1_out, not_1_out, not_2_out, not_3_out, not_4_out, not_5_out, not_6_out, not_7_out, not_8_out,
       not_9_out, not_10_out, riscv_probe_1_p1, rs2used, RST, s, ss, W1, W2, W3;
  wire [2:0] JJUout;
  wire [2:1] JJUin;
  wire [3:0] id_ex2_1_aluopout, \单周期硬布线控制器_1_alu_op ;
  wire [4:0] EXW, MEMW, rs, rt, W_F;
  wire [6:0] signalin;
  wire [6:1] signalout;
  wire [11:0] multiplexer_4_out;
  wire [12:0] CNT_num;
  wire [15:0] \LoadUse次数 , \总周期数 , \插入气泡数 , \无条件分支数 , \条件分支成功数 ;
  wire [31:0] adder_1_out, adder_2_out, alu_1_p8, bit_extender_1_out, bit_extender_2_out, bit_extender_3_out,
       EX_IR, ex_mem2_1_alu_result_2, id_ex2_1_b_imm_2, id_ex2_1_i_s_imm_2, id_ex2_1_j_imm_2, id_ex2_1_r1_2,
       id_ex2_1_r2_2, ID_IR, IF_IR, IR, MEM_IR, mem_wb2_1_alu_result_2, mem_wb2_1_memdata_2,
       multiplexer_1_out, multiplexer_6_out, multiplexer_7_out, multiplexer_8_out, multiplexer_9_out,
       multiplexer_12_out, PC_F, ram_1_dout, \regifile_下降沿_1_r1 , \regifile_下降沿_1_r2 , rom_1_data,
       shifter_1_out, WB_IR;

  Button \u_总复位  (.out(RST));
  Button _1 (.out(IR1));
  Button _2 (.out(IR2));
  Button _3 (.out(IR3));
  // Probe on \总周期数 
  // Probe on \总周期数 
  Button \u_继续运行  (.out(Go));
  LED #(.active("true")) led_1 (.in(W1));
  LED #(.active("true")) led_2 (.in(W2));
  LED #(.active("true")) led_3 (.in(W3));
  not not_1 (not_1_out, halt2);
  Counter #(.width(16), .max('hffff), .ongoal("stay"), .trigger("rising"), .behavior("new")) counter_1 (
    .load(RST), .D({16{1'b0}}), .count(not_1_out), .Q(\总周期数 ), .clk(CLK));  // open: carry, clr, preset, down
  Hex_Digit_Display hex_digit_display_1 (.value(LedData[31:28]));  // open: dp
  Hex_Digit_Display hex_digit_display_2 (.value(LedData[27:24]));  // open: dp
  // Probe on IF_PC[19:0]
  // RiscV_Probe riscv_probe_1: pin names not known; wires that end beside it: riscv_probe_1_p1, IF_IR
  not not_2 (not_2_out, DH);
  Hex_Digit_Display hex_digit_display_3 (.value(LedData[23:20]));  // open: dp
  Hex_Digit_Display hex_digit_display_4 (.value(LedData[19:16]));  // open: dp
  or or_1 (branchtaken, JJUout[0], JALR, B);
  and and_1 (and_1_out, H, not_2_out);
  Multiplexer #(.select(1), .width(32), .disabled("Z"), .enable("false")) multiplexer_1 (
    .in0(adder_1_out), .in1(multiplexer_9_out), .out(multiplexer_1_out), .sel(branchtaken));
  Hex_Digit_Display hex_digit_display_5 (.value(LedData[15:12]));  // open: dp
  Hex_Digit_Display hex_digit_display_6 (.value(LedData[11:8]));  // open: dp
  // Probe on ID_PC[19:0]
  // RiscV_Probe riscv_probe_2: pin names not known; wires that end beside it: ID_IR
  Register #(.width(32), .trigger("rising"), .Select("low")) PC (
    .D(multiplexer_1_out), .en(and_1_out), .Q(IF_PC), .clk(CLK), .clr(RST));
  Adder #(.width(32)) adder_1 (.a(IF_PC), .b(32'h4), .out(adder_1_out));  // open: cin, cout
  Hex_Digit_Display hex_digit_display_7 (.value(LedData[3:0]));  // open: dp
  Hex_Digit_Display hex_digit_display_8 (.value(LedData[7:4]));  // open: dp
  // Probe on EX_PC[19:0]
  // RiscV_Probe riscv_probe_3: pin names not known; wires that end beside it: EX_IR, riscv_probe_1_p1
  // RiscV_Probe riscv_probe_4: pin names not known; wires that end beside it: IF_PC[11:2], IR
  not not_3 (not_3_out, DH);
  // Probe on \总周期数 
  // Probe on M_PC[19:0]
  // RiscV_Probe riscv_probe_5: pin names not known; wires that end beside it: MEM_IR
  ROM #(.addrWidth(10), .dataWidth(32), .Select("high")) rom_1 (.addr(IF_PC[11:2]), .data(rom_1_data));
  IF_ID2 if_id2_1 (
    .IRin(rom_1_data), .PCin(IF_PC), .clk(CLK), .bubble(branchtaken), .stop(and_2_out), .IRout(IR),
    .PCout(ID_PC));
  and and_2 (and_2_out, not_3_out, H);
  // Probe on \总周期数 
  // Probe on \无条件分支数 
  // Probe on \条件分支成功数 
  // Probe on \插入气泡数 
  // Probe on \LoadUse次数 
  // Probe on IF_PC[11:0]
  // Probe on WB_PC[19:0]
  // RiscV_Probe riscv_probe_6: pin names not known; wires that end beside it: WB_IR
  // Probe on ID_PC[11:0]
  // Probe on EX_PC[11:0]
  \单周期硬布线控制器  \u_单周期硬布线控制器_1  (
    .Funct({IR[30], IR[25], IR[14:12]}), .OP(IR[6:2]), .ALU_OP(\单周期硬布线控制器_1_alu_op ), .MemToReg(signalin[3]),
    .MemWrite(signalin[2]), .ALU_SRC(signalin[1]), .RegWrite(signalin[0]), .ecall(ecall), .S_type(s),
    .Jalr(JJUin[1]), .Beq(signalin[6]), .JAL(jAL), .Bne(signalin[4]), .in_3(IR[21]), .uret(JJUin[2]),
    .blt(signalin[5]), .sb(id_sb));  // open: csrrsi, csrrci
  Multiplexer #(.select(1), .width(5), .disabled("Z"), .enable("false")) multiplexer_2 (
    .in0(IR[19:15]), .in1(5'b10001), .out(rs), .sel(ecall));
  Multiplexer #(.select(1), .width(5), .disabled("Z"), .enable("false")) multiplexer_3 (
    .in0(IR[24:20]), .in1(5'b01010), .out(rt), .sel(ecall));
  Multiplexer #(.select(1), .width(12), .disabled("Z"), .enable("false")) multiplexer_4 (
    .in0(IR[31:20]), .in1({IR[31:25], IR[11:7]}), .out(multiplexer_4_out), .sel(s));
  Multiplexer #(.select(1), .width(32), .disabled("Z"), .enable("false")) multiplexer_5 (
    .in0(multiplexer_12_out), .in1(PC_F), .out(RDin), .sel(JJ));
  // Probe on M_PC[11:0]
  D_Flip_Flop #(.trigger("high"), .Pre_Clr_Positions("LEGACY"), .NegatePresetClear("false"), .enable("true"), .NewFFLayout("false")) d_ff_1 (.Q(d_ff_1_q));  // open: clk, D, Qn, preset, en, reset
  // Probe on 13'hc
  \Regifile_下降沿  \regifile_下降沿_1  (
    .Din(RDin), .Clk(CLK), .R1(\regifile_下降沿_1_r1 ), .R2(\regifile_下降沿_1_r2 ), .WE(RegWrite), .W_num(W_F),
    .R1_num(rs), .R2_num(rt));
  assign bit_extender_1_out = {{20{multiplexer_4_out[11]}}, multiplexer_4_out};  // Bit_Extender bit_extender_1
  assign bit_extender_2_out = {{20{IR[31]}}, {IR[31], IR[7], IR[30:25], IR[11:8]}};  // Bit_Extender bit_extender_2
  assign bit_extender_3_out = {{12{IR[31]}}, {IR[31], IR[19:12], IR[20], IR[30:21]}};  // Bit_Extender bit_extender_3
  // Probe on WB_PC[11:0]
  Comparator #(.width(13), .mode("twosComplement")) comparator_1 (
    .a(CNT_num), .b(13'hc), .eq(comparator_1_eq), .lt(comparator_1_lt));  // open: gt
  Clock #(.highDuration(1), .lowDuration(1)) clock_1 (.out(clock_1_out));
  Counter #(.width(13), .max('h1fff), .ongoal("stay"), .trigger("rising"), .behavior("old")) counter_2 (
    .count(comparator_1_lt), .Q(CNT_num), .clk(clock_1_out));  // open: load, D, carry, clr, preset
  or or_2 (ID_EX_Flush, DH, branchtaken);
  nand nand_1 (nand_1_out, d_ff_1_q, comparator_1_eq);
  ID_EX2 id_ex2_1 (
    .signal(signalin), .ecall(ecall), .JJU({JJUin, jAL}), .AluOp(\单周期硬布线控制器_1_alu_op ),
    .R1(\regifile_下降沿_1_r1 ), .R2(\regifile_下降沿_1_r2 ), .I_S_imm(bit_extender_1_out),
    .B_imm(bit_extender_2_out), .J_imm(bit_extender_3_out), .PCin(ID_PC), .WriteReg_num(IR[11:7]), .CLK(CLK),
    .bubble(ID_EX_Flush), .stop(H), .signalout({signalout[6], ex_blt, signalout[4:1], EXRegwrite}),
    .ecallout(ecall2), .JJUout({JJUout[2], JALR, JJUout[0]}), .AluOpout(id_ex2_1_aluopout),
    .R1_2(id_ex2_1_r1_2), .R2_2(id_ex2_1_r2_2), .I_S_imm_2(id_ex2_1_i_s_imm_2), .B_imm_2(id_ex2_1_b_imm_2),
    .J_imm_2(id_ex2_1_j_imm_2), .PCout(EX_PC), .WriteReg_num_2(EXW), .sb(id_sb), .sb_2(ex_sb));
  assign CLK = nand_1_out ? clock_1_out : 1'bz;  // Controlled_Buffer controlled_buffer_1
  Pull_Resistor #(.pull(1)) pull_resistor_1 (.node(CLK));
  Multiplexer #(.select(1), .width(32), .disabled("Z"), .enable("false")) multiplexer_6 (
    .in0(id_ex2_1_j_imm_2), .in1(id_ex2_1_b_imm_2), .out(multiplexer_6_out), .sel(B));
  Comparator #(.width(32), .mode("twosComplement")) comparator_2 (
    .a(32'h22), .b(id_ex2_1_r1_2), .eq(comparator_2_eq));  // open: gt, lt
  Multiplexer #(.select(1), .width(32), .disabled("Z"), .enable("false")) multiplexer_7 (
    .in0(id_ex2_1_r2_2), .in1(id_ex2_1_i_s_imm_2), .out(multiplexer_7_out), .sel(signalout[1]));
  and and_3 (ss, comparator_2_eq, ecall2);
  Multiplexer #(.select(1), .width(32), .disabled("Z"), .enable("false")) multiplexer_8 (
    .in0(LedData), .in1(id_ex2_1_r2_2), .out(multiplexer_8_out), .sel(ss));
  not not_4 (not_4_out, comparator_2_eq);
  and and_4 (halt, not_4_out, ecall2);
  // ALU alu_1: pin names not known; wires that end beside it: id_ex2_1_r1_2, alu_1_p2, multiplexer_7_out, alu_1_p2, id_ex2_1_aluopout, alu_1_p6, alu_1_p7, alu_1_p8
  Shifter #(.width(32), .shift("ll")) shifter_1 (.in(multiplexer_6_out), .\dist (5'b00001), .out(shifter_1_out));
  and and_5 (and_5_out, ex_blt, alu_1_p7);
  not not_5 (not_5_out, alu_1_p6);
  and and_6 (and_6_out, signalout[6], alu_1_p6);
  Adder #(.width(32)) adder_2 (.a(shifter_1_out), .b(EX_PC), .out(adder_2_out));  // open: cin, cout
  and and_7 (and_7_out, signalout[4], not_5_out);
  or or_3 (B, and_7_out, and_5_out, and_6_out);
  EX_MEM2 ex_mem2_1 (
    .JALin(JJUout[0]), .JALRin(JALR), .RegWrite(EXRegwrite), .MemToReg(signalout[3]),
    .MemWrite(signalout[2]), .Write_Data(id_ex2_1_r2_2), .ALU_Result(alu_1_p8), .WriteReg_num(EXW),
    .PCin(EX_PC), .haltin(halt), .CLK(CLK), .bubble(1'b0), .stop(H), .JALout(ex_mem2_1_jalout),
    .JALRout(ex_mem2_1_jalrout), .RegWrite_2(MEMRegwrite), .MemToReg_2(ex_mem2_1_memtoreg_2),
    .MemWrite_2(MemWrite), .Write_Data_2(MDin), .ALU_Result_2(ex_mem2_1_alu_result_2), .WriteReg_num_2(MEMW),
    .PCout(M_PC), .haltout(halt1), .sb(ex_sb), .sb_2(mem_sb));
  Multiplexer #(.select(1), .width(32), .disabled("Z"), .enable("false")) multiplexer_9 (
    .in0(adder_2_out), .in1(alu_1_p8), .out(multiplexer_9_out), .sel(JALR));
  Multiplexer #(.select(1), .width(1), .disabled("Z"), .enable("false")) multiplexer_10 (
    .in0(and_8_out), .in1(1'b0), .out(multiplexer_10_out), .sel(CLK));
  and and_8 (and_8_out, JJ, CLK);
  Register #(.width(32), .trigger("rising"), .Select("low")) register_1 (
    .D(multiplexer_8_out), .en(ss), .Q(LedData), .clk(CLK));  // open: clr
  Counter #(.width(16), .max('hffff), .ongoal("wrap"), .trigger("rising"), .behavior("old")) counter_3 (
    .count(1'b1), .Q(\无条件分支数 ), .clk(multiplexer_10_out), .clr(RST));  // open: load, D, carry, preset
  RAM ram_1 (
    .Mode(mem_sb), .\字节地址 (ex_mem2_1_alu_result_2[11:0]), .Din(MDin), .CLK(CLK), .str(MemWrite),
    .id(not_6_out), .Dout(ram_1_dout));
  not not_6 (not_6_out, MemWrite);
  or or_4 (H, not_7_out, Go);
  not not_7 (not_7_out, halt2);
  MEM_WB2 mem_wb2_1 (
    .halt(halt1), .JAL(ex_mem2_1_jalout), .JALR(ex_mem2_1_jalrout), .RegWrite(MEMRegwrite),
    .MemToReg(ex_mem2_1_memtoreg_2), .ALU_Result(ex_mem2_1_alu_result_2), .MemData(ram_1_dout),
    .WriteReg_num(MEMW), .PC(M_PC), .CLK(CLK), .bubble(1'b0), .stop(H), .haltout(halt2),
    .JALout(mem_wb2_1_jalout), .JALRout(mem_wb2_1_jalrout), .RegWrite_2(RegWrite),
    .MemToReg_2(mem_wb2_1_memtoreg_2), .ALU_Result_2(mem_wb2_1_alu_result_2),
    .MemData_2(mem_wb2_1_memdata_2), .WriteReg_num_2(W_F), .PCout(WB_PC));
  Counter #(.width(16), .max('hffff), .ongoal("wrap"), .trigger("rising"), .behavior("old")) counter_4 (
    .count(1'b1), .Q(\条件分支成功数 ), .clk(multiplexer_11_out), .clr(RST));  // open: load, D, carry, preset
  Multiplexer #(.select(1), .width(1), .disabled("Z"), .enable("false")) multiplexer_11 (
    .in0(and_9_out), .in1(1'b0), .out(multiplexer_11_out), .sel(CLK));
  and and_9 (and_9_out, B, CLK);
  Multiplexer #(.select(1), .width(32), .disabled("Z"), .enable("false")) multiplexer_12 (
    .in0(mem_wb2_1_alu_result_2), .in1(mem_wb2_1_memdata_2), .out(multiplexer_12_out),
    .sel(mem_wb2_1_memtoreg_2));
  or or_5 (JJ, mem_wb2_1_jalout, mem_wb2_1_jalrout);
  Adder #(.width(32)) adder_3 (.a(WB_PC), .b(32'h4), .out(PC_F));  // open: cin, cout
  Counter #(.width(16), .max('hffff), .ongoal("wrap"), .trigger("rising"), .behavior("old")) counter_5 (
    .count(1'b1), .Q(\插入气泡数 ), .clk(multiplexer_13_out), .clr(RST));  // open: load, D, carry, preset
  Multiplexer #(.select(1), .width(1), .disabled("Z"), .enable("false")) multiplexer_13 (
    .in0(and_10_out), .in1(1'b0), .out(multiplexer_13_out), .sel(CLK));
  and and_10 (and_10_out, and_11_out, CLK);
  and and_11 (and_11_out, ~halt2, DH);  // AND_Gate
  not not_8 (not_8_out, signalin[1]);
  and and_12 (and_12_out, not_8_out, not_9_out);
  not not_9 (not_9_out, jAL);
  not not_10 (not_10_out, jAL);
  DataHazzard datahazzard_1 (
    .RsUsed(not_10_out), .RtUsed(rs2used), .EXRW(EXRegwrite), .MEMRW(MEMRegwrite), .rs(rs), .rt(rt),
    .exw(EXW), .memw(MEMW), .DH(DH));
  or or_6 (rs2used, s, and_12_out);

  // Other names for the same wires on the sheet: W_num[4:0] = IR[11:7]; IF_ID_Flush = branchtaken; JJUin[0] = jAL;
  //   JJUout[1] = JALR; MEM_PC[31:0] = M_PC; PC[31:0] = IF_PC; src = signalin[1];
  //   signalout (some bits) = {ex_blt, EXRegwrite}

  // Notes on the sheet:
  //   中断源
  //   中断等待指示
  //   数码管输出
  //   时空图监测，可删除
  //   指令探针
  //   指令存储器
  //   contents of rom_1 (hex, n*v repeats v):
  //   100493 100006f 100493 200913 300993 100006f 100493 200913 300993 100006f 100493 200913 300993
  //   100006f 100493 200913 300993 3ac000ef 100413 100493 1f49493 900533 2200893 73 24d493 48463 fedff06f
  //   900533 2200893 73 100493 249493 900533 2200893 73 48463 fedff06f 100493 1f49493 900533 2200893 73
  //   4034d493 900533 2200893 73 4044d493 900533 2200893 73 4044d493 900533 2200893 73 4044d493 900533
  //   2200893 73 4044d493 900533 2200893 73 4044d493 900533 2200893 73 4044d493 900533 2200893 73 4044d493
  //   900533 2200893 73 100413 1f41993 41f9d993 433 c00913 300b13 140413 f47413 800293 100313 499993
  //   89e9b3 1300533 2200893 73 406282b3 fe0294e3 140413 f00f93 1f47433 1c41413 800293 100313 49d993
  //   89e9b3 1300533 2200893 73 406282b3 fe0294e3 1c45413 406b0b33 b0463 f95ff06f 2b3 fff2c293 829293
  //   ff2e293 500533 2200893 73 fff00413 493 84a023 140413 448493 84a023 140413 448493 84a023 140413
  //   448493 84a023 140413 448493 84a023 140413 448493 84a023 140413 448493 84a023 140413 448493 84a023
  //   140413 448493 84a023 140413 448493 84a023 140413 448493 84a023 140413 448493 84a023 140413 448493
  //   84a023 140413 448493 84a023 140413 448493 84a023 140413 448493 84a023 140413 448493 140413 433
  //   3c00493 42983 4aa03 149a2b3 28663 134a023 1442023 ffc48493 fe9412e3 800533 2200893 73 440413 3c00493
  //   fc9416e3 3200893 73 100293 300313 800493 849493 7648493 1449493 900533 2200893 73 800e13 54d4b3
  //   64d4b3 900533 2200893 73 fffe0e13 fe0e14e3 a00893 73 fff00293 7700493 849493 7748493 900533 2200893
  //   73 1000e13 54c4b3 900533 2200893 73 fffe0e13 fe0e16e3 a00893 73 313 2000e13 493 100913 930023 900533
  //   2200893 73 12484b3 130313 fffe0e13 fe0e12e3 800e13 313 32483 900533 2200893 73 430313 fffe0e13
  //   fe0e14e3 a00893 73 ff100493 900533 2200893 73 148493 fe04c8e3 a00893 73 a00893 73 413 140413 800533
  //   2200893 73 240413 800533 2200893 73 340413 800533 2200893 73 440413 800533 2200893 73 540413 800533
  //   2200893 73 640413 800533 2200893 73 740413 800533 2200893 73 840413 800533 2200893 2200893 73 8067
  //   JAL
  //   JALR
  //   URET
  //   Beq
  //   Bne
  //   MemToReg
  //   MemWrite
  //   AluOP
  //   AluSrcB
  //   RegWrite
  //   流水调试日志用
  //   控制位
  //   暂停节拍，不能为0
  //   戳工具置1进入计数暂停模式，ctrl+k时钟自动运行到对应节拍暂停
  //   ctrl+k关闭时钟连续运行，将控制位置零，进入单步调试模式调试
  //   可计数暂停的时钟源
  //   为方便自动评测，需要输出流水线各段保存的PC值，注意是PC不是PC+4，另外ID段寄存器写入信息，Mem段内存写入信息也要输出
  //   数据存储器
endmodule

module \重定向流水线  (
  output RegWrite,
  output MemWrite,
  output [31:0] IF_PC,
  output [31:0] ID_PC,
  output [31:0] EX_PC,
  output [31:0] M_PC,
  output [31:0] WB_PC,
  output [31:0] RDin,
  output [31:0] MDin,
  output [31:0] LedData
);

  wire alu_1_p2, alu_1_p6, alu_1_p7, and_1_out, and_2_out, and_3_out, and_4_out, and_5_out, and_6_out,
       and_9_out, and_10_out, and_11_out, and_12_out, and_13_out, and_14_out, and_15_out, and_16_out,
       and_17_out, and_18_out, and_19_out, B, branchtaken, CLK, clock_1_out, comparator_1_eq,
       comparator_2_eq, comparator_3_eq, comparator_4_eq, comparator_5_eq, comparator_5_lt, comparator_6_eq,
       comparator_7_eq, comparator_8_eq, comparator_9_eq, comparator_10_eq, comparator_11_eq,
       comparator_12_eq, comparator_13_eq, comparator_14_eq, d_ff_1_q, ecall, ecall2, ex_blt,
       ex_mem2_1_jalout, ex_mem2_1_jalrout, ex_mem2_1_memtoreg_2, EX_MemToReg, EX_RegWrite, ex_sb, Go, H,
       halt, halt1, halt2, id_sb, IR1, IR2, IR3, jAL, JALR, JJ, loaduse, MEM_RegWrite, mem_sb,
       mem_wb2_1_jalout, mem_wb2_1_jalrout, mem_wb2_1_memtoreg_2, multiplexer_16_out, multiplexer_17_out,
       multiplexer_19_out, multiplexer_20_out, nand_1_out, not_1_out, not_2_out, not_3_out, not_4_out,
       not_5_out, not_6_out, not_7_out, not_8_out, not_9_out, not_10_out, not_11_out, not_13_out, not_14_out,
       not_15_out, not_16_out, or_2_out, RST, RsUsed, RtUsed, s, ss, W1, W2, W3;
  wire [1:0] ex_RsF, ex_RtF, multiplexer_2_out, multiplexer_12_out, RsForward, RtForward;
  wire [2:0] JJUout;
  wire [2:1] JJUin;
  wire [3:0] id_ex3_1_aluopout, \单周期硬布线控制器_1_alu_op ;
  wire [4:0] EXW, MEMW, rs, rt, W_F;
  wire [6:0] signalin;
  wire [6:1] signalout;
  wire [11:0] multiplexer_6_out;
  wire [12:0] CNT_num;
  wire [15:0] \LoadUse次数 , \总周期数 , \插入气泡数 , \无条件分支数 , \条件分支成功数 ;
  wire [31:0] adder_1_out, adder_2_out, alu_1_p8, bit_extender_1_out, bit_extender_2_out, bit_extender_3_out,
       EX_IR, id_ex3_1_b_imm_2, id_ex3_1_i_s_imm_2, id_ex3_1_j_imm_2, ID_IR, IF_IR, IR, mem_a, MEM_IR,
       mem_wb2_1_alu_result_2, mem_wb2_1_memdata_2, multiplexer_1_out, multiplexer_8_out, multiplexer_10_out,
       multiplexer_11_out, multiplexer_15_out, PC_F, R1, R2, R11, R22, ram_1_dout, \regifile_下降沿_1_r1 ,
       \regifile_下降沿_1_r2 , rom_1_data, shifter_1_out, wb_a, WB_IR;

  Button \u_总复位  (.out(RST));
  Button _1 (.out(IR1));
  Button _2 (.out(IR2));
  Button _3 (.out(IR3));
  // Probe on \总周期数 
  // Probe on \总周期数 
  Button \u_继续运行  (.out(Go));
  LED #(.active("true")) led_1 (.in(W1));
  LED #(.active("true")) led_2 (.in(W2));
  LED #(.active("true")) led_3 (.in(W3));
  not not_1 (not_1_out, halt2);
  Counter #(.width(16), .max('hffff), .ongoal("stay"), .trigger("rising"), .behavior("new")) counter_1 (
    .load(RST), .D({16{1'b0}}), .count(not_1_out), .Q(\总周期数 ), .clk(CLK));  // open: carry, clr, preset, down
  or or_1 (branchtaken, JJUout[0], JALR, B);
  Multiplexer #(.select(1), .width(32), .disabled("Z"), .enable("false")) multiplexer_1 (
    .in0(adder_1_out), .in1(multiplexer_15_out), .out(multiplexer_1_out), .sel(branchtaken));
  not not_2 (not_2_out, loaduse);
  Hex_Digit_Display hex_digit_display_1 (.value(LedData[31:28]));  // open: dp
  // Probe on IF_PC[19:0]
  // RiscV_Probe riscv_probe_1: pin names not known; wires that end beside it: IF_IR
  Register #(.width(32), .trigger("rising"), .Select("low")) PC (
    .D(multiplexer_1_out), .en(and_1_out), .Q(IF_PC), .clk(CLK), .clr(RST));
  and and_1 (and_1_out, not_2_out, H);
  Adder #(.width(32)) adder_1 (.a(IF_PC), .b(32'h4), .out(adder_1_out));  // open: cin, cout
  Hex_Digit_Display hex_digit_display_2 (.value(LedData[27:24]));  // open: dp
  Hex_Digit_Display hex_digit_display_3 (.value(LedData[23:20]));  // open: dp
  // Probe on ID_PC[19:0]
  // RiscV_Probe riscv_probe_2: pin names not known; wires that end beside it: ID_IR
  Comparator #(.width(5), .mode("twosComplement")) comparator_1 (
    .a(rs), .b({5{1'b0}}), .eq(comparator_1_eq));  // open: gt, lt
  Comparator #(.width(5), .mode("twosComplement")) comparator_2 (
    .a(rs), .b(EXW), .eq(comparator_2_eq));  // open: gt, lt
  Comparator #(.width(5), .mode("twosComplement")) comparator_3 (
    .a(rs), .b({5{1'b0}}), .eq(comparator_3_eq));  // open: gt, lt
  Comparator #(.width(5), .mode("twosComplement")) comparator_4 (
    .a(rs), .b(MEMW), .eq(comparator_4_eq));  // open: gt, lt
  Hex_Digit_Display hex_digit_display_4 (.value(LedData[15:12]));  // open: dp
  Hex_Digit_Display hex_digit_display_5 (.value(LedData[19:16]));  // open: dp
  not not_3 (not_3_out, loaduse);
  not not_4 (not_4_out, comparator_1_eq);
  not not_5 (not_5_out, comparator_3_eq);
  Hex_Digit_Display hex_digit_display_6 (.value(LedData[11:8]));  // open: dp
  Hex_Digit_Display hex_digit_display_7 (.value(LedData[7:4]));  // open: dp
  // Probe on EX_PC[19:0]
  // RiscV_Probe riscv_probe_3: pin names not known; wires that end beside it: EX_IR
  // RiscV_Probe riscv_probe_4: pin names not known; wires that end beside it: IF_PC[11:2], IR
  ROM #(.addrWidth(10), .dataWidth(32), .Select("high")) rom_1 (.addr(IF_PC[11:2]), .data(rom_1_data));
  and and_2 (and_2_out, not_3_out, H);
  and and_3 (and_3_out, EX_RegWrite, RsUsed, not_4_out, comparator_2_eq);
  and and_4 (and_4_out, MEM_RegWrite, RsUsed, not_5_out, comparator_4_eq);
  Hex_Digit_Display hex_digit_display_8 (.value(LedData[3:0]));  // open: dp
  IF_ID2 if_id2_1 (
    .IRin(rom_1_data), .PCin(IF_PC), .clk(CLK), .bubble(branchtaken), .stop(and_2_out), .IRout(IR),
    .PCout(ID_PC));
  Multiplexer #(.select(1), .width(2), .disabled("Z"), .enable("false")) multiplexer_2 (
    .in0(2'b00), .in1(2'b01), .out(multiplexer_2_out), .sel(and_4_out));
  // Probe on \总周期数 
  // Probe on M_PC[19:0]
  // RiscV_Probe riscv_probe_5: pin names not known; wires that end beside it: MEM_IR
  Multiplexer #(.select(1), .width(2), .disabled("Z"), .enable("false")) multiplexer_3 (
    .in0(multiplexer_2_out), .in1(2'b10), .out(RsForward), .sel(and_3_out));
  // Probe on \总周期数 
  // Probe on \无条件分支数 
  // Probe on \条件分支成功数 
  // Probe on \插入气泡数 
  // Probe on \LoadUse次数 
  \单周期硬布线控制器  \u_单周期硬布线控制器_1  (
    .Funct({IR[30], IR[25], IR[14:12]}), .OP(IR[6:2]), .ALU_OP(\单周期硬布线控制器_1_alu_op ), .MemToReg(signalin[3]),
    .MemWrite(signalin[2]), .ALU_SRC(signalin[1]), .RegWrite(signalin[0]), .ecall(ecall), .S_type(s),
    .Jalr(JJUin[1]), .Beq(signalin[6]), .JAL(jAL), .Bne(signalin[4]), .in_3(IR[21]), .uret(JJUin[2]),
    .blt(signalin[5]), .sb(id_sb));  // open: csrrsi, csrrci
  // Probe on IF_PC[11:0]
  // Probe on WB_PC[19:0]
  // RiscV_Probe riscv_probe_6: pin names not known; wires that end beside it: WB_IR
  Multiplexer #(.select(1), .width(5), .disabled("Z"), .enable("false")) multiplexer_4 (
    .in0(IR[19:15]), .in1(5'b10001), .out(rs), .sel(ecall));
  Multiplexer #(.select(1), .width(5), .disabled("Z"), .enable("false")) multiplexer_5 (
    .in0(IR[24:20]), .in1(5'b01010), .out(rt), .sel(ecall));
  Multiplexer #(.select(1), .width(12), .disabled("Z"), .enable("false")) multiplexer_6 (
    .in0(IR[31:20]), .in1({IR[31:25], IR[11:7]}), .out(multiplexer_6_out), .sel(s));
  assign bit_extender_1_out = {{20{IR[31]}}, {IR[31], IR[7], IR[30:25], IR[11:8]}};  // Bit_Extender bit_extender_1
  assign bit_extender_2_out = {{12{IR[31]}}, {IR[31], IR[19:12], IR[20], IR[30:21]}};  // Bit_Extender bit_extender_2
  Multiplexer #(.select(1), .width(32), .disabled("Z"), .enable("false")) multiplexer_7 (
    .in0(wb_a), .in1(PC_F), .out(RDin), .sel(JJ));
  // Probe on EX_PC[11:0]
  // Probe on ID_PC[11:0]
  \Regifile_下降沿  \regifile_下降沿_1  (
    .Din(RDin), .Clk(CLK), .R1(\regifile_下降沿_1_r1 ), .R2(\regifile_下降沿_1_r2 ), .WE(RegWrite), .W_num(W_F),
    .R1_num(rs), .R2_num(rt));
  assign bit_extender_3_out = {{20{multiplexer_6_out[11]}}, multiplexer_6_out};  // Bit_Extender bit_extender_3
  // Probe on M_PC[11:0]
  D_Flip_Flop #(.trigger("high"), .Pre_Clr_Positions("LEGACY"), .NegatePresetClear("false"), .enable("true"), .NewFFLayout("false")) d_ff_1 (.Q(d_ff_1_q));  // open: clk, D, Qn, preset, en, reset
  // Probe on 13'hc
  // Probe on WB_PC[11:0]
  Comparator #(.width(13), .mode("twosComplement")) comparator_5 (
    .a(CNT_num), .b(13'hc), .eq(comparator_5_eq), .lt(comparator_5_lt));  // open: gt
  Clock #(.highDuration(1), .lowDuration(1)) clock_1 (.out(clock_1_out));
  or or_2 (or_2_out, loaduse, branchtaken);
  nand nand_1 (nand_1_out, d_ff_1_q, comparator_5_eq);
  Counter #(.width(13), .max('h1fff), .ongoal("stay"), .trigger("rising"), .behavior("old")) counter_2 (
    .count(comparator_5_lt), .Q(CNT_num), .clk(clock_1_out));  // open: load, D, carry, clr, preset
  ID_EX3 id_ex3_1 (
    .signal(signalin), .ecall(ecall), .JJU({JJUin, jAL}), .AluOp(\单周期硬布线控制器_1_alu_op ),
    .R1(\regifile_下降沿_1_r1 ), .R2(\regifile_下降沿_1_r2 ), .I_S_imm(bit_extender_3_out),
    .B_imm(bit_extender_1_out), .J_imm(bit_extender_2_out), .PCin(ID_PC), .WriteReg_num(IR[11:7]),
    .RsForward(RsForward), .RtForward(RtForward), .CLK(CLK), .bubble(or_2_out), .stop(H),
    .signalout({signalout[6], ex_blt, signalout[4], EX_MemToReg, signalout[2:1], EX_RegWrite}),
    .ecallout(ecall2), .JJUout({JJUout[2], JALR, JJUout[0]}), .AluOpout(id_ex3_1_aluopout), .R1_2(R1),
    .R2_2(R2), .I_S_imm_2(id_ex3_1_i_s_imm_2), .B_imm_2(id_ex3_1_b_imm_2), .J_imm_2(id_ex3_1_j_imm_2),
    .PCout(EX_PC), .WriteReg_num_2(EXW), .RsForward_2(ex_RsF), .RtForward_2(ex_RtF), .sb(id_sb), .sb_2(ex_sb));
  Comparator #(.width(5), .mode("twosComplement")) comparator_6 (
    .a(rt), .b({5{1'b0}}), .eq(comparator_6_eq));  // open: gt, lt
  Comparator #(.width(5), .mode("twosComplement")) comparator_7 (
    .a(rt), .b(EXW), .eq(comparator_7_eq));  // open: gt, lt
  Comparator #(.width(5), .mode("twosComplement")) comparator_8 (
    .a(rt), .b({5{1'b0}}), .eq(comparator_8_eq));  // open: gt, lt
  Comparator #(.width(5), .mode("twosComplement")) comparator_9 (
    .a(rt), .b(MEMW), .eq(comparator_9_eq));  // open: gt, lt
  assign CLK = nand_1_out ? clock_1_out : 1'bz;  // Controlled_Buffer controlled_buffer_1
  Multiplexer #(.select(1), .width(32), .disabled("Z"), .enable("false")) multiplexer_8 (
    .in0(id_ex3_1_j_imm_2), .in1(id_ex3_1_b_imm_2), .out(multiplexer_8_out), .sel(B));
  Multiplexer #(.select(2), .width(32), .disabled("Z"), .enable("false")) multiplexer_9 (
    .in0(R1), .in1(wb_a), .in2(mem_a), .out(R11), .sel(ex_RsF));  // open: in3
  not not_6 (not_6_out, comparator_6_eq);
  not not_7 (not_7_out, comparator_8_eq);
  Pull_Resistor #(.pull(1)) pull_resistor_1 (.node(CLK));
  Multiplexer #(.select(1), .width(32), .disabled("Z"), .enable("false")) multiplexer_10 (
    .in0(R22), .in1(id_ex3_1_i_s_imm_2), .out(multiplexer_10_out), .sel(signalout[1]));
  Multiplexer #(.select(1), .width(32), .disabled("Z"), .enable("false")) multiplexer_11 (
    .in0(LedData), .in1(R22), .out(multiplexer_11_out), .sel(ss));
  and and_5 (and_5_out, EX_RegWrite, RtUsed, not_6_out, comparator_7_eq);
  and and_6 (and_6_out, MEM_RegWrite, RtUsed, not_7_out, comparator_9_eq);
  Comparator #(.width(32), .mode("twosComplement")) comparator_10 (
    .a(32'h22), .b(R11), .eq(comparator_10_eq));  // open: gt, lt
  and and_7 (ss, comparator_10_eq, ecall2);
  not not_8 (not_8_out, comparator_10_eq);
  and and_8 (halt, not_8_out, ecall2);
  Multiplexer #(.select(1), .width(2), .disabled("Z"), .enable("false")) multiplexer_12 (
    .in0(2'b00), .in1(2'b01), .out(multiplexer_12_out), .sel(and_6_out));
  not not_9 (not_9_out, alu_1_p6);
  // ALU alu_1: pin names not known; wires that end beside it: R11, alu_1_p2, multiplexer_10_out, alu_1_p2, id_ex3_1_aluopout, alu_1_p6, alu_1_p7, alu_1_p8
  Shifter #(.width(32), .shift("ll")) shifter_1 (.in(multiplexer_8_out), .\dist (5'b00001), .out(shifter_1_out));
  Multiplexer #(.select(2), .width(32), .disabled("Z"), .enable("false")) multiplexer_13 (
    .in0(R2), .in1(wb_a), .in2(mem_a), .out(R22), .sel(ex_RtF));  // open: in3
  Multiplexer #(.select(1), .width(2), .disabled("Z"), .enable("false")) multiplexer_14 (
    .in0(multiplexer_12_out), .in1(2'b10), .out(RtForward), .sel(and_5_out));
  and and_9 (and_9_out, ex_blt, alu_1_p7);
  and and_10 (and_10_out, signalout[4], not_9_out);
  and and_11 (and_11_out, signalout[6], alu_1_p6);
  Adder #(.width(32)) adder_2 (.a(shifter_1_out), .b(EX_PC), .out(adder_2_out));  // open: cin, cout
  or or_3 (B, and_10_out, and_9_out, and_11_out);
  EX_MEM2 ex_mem2_1 (
    .JALin(JJUout[0]), .JALRin(JALR), .RegWrite(EX_RegWrite), .MemToReg(EX_MemToReg),
    .MemWrite(signalout[2]), .Write_Data(R22), .ALU_Result(alu_1_p8), .WriteReg_num(EXW), .PCin(EX_PC),
    .haltin(halt), .CLK(CLK), .bubble(1'b0), .stop(H), .JALout(ex_mem2_1_jalout),
    .JALRout(ex_mem2_1_jalrout), .RegWrite_2(MEM_RegWrite), .MemToReg_2(ex_mem2_1_memtoreg_2),
    .MemWrite_2(MemWrite), .Write_Data_2(MDin), .ALU_Result_2(mem_a), .WriteReg_num_2(MEMW), .PCout(M_PC),
    .haltout(halt1), .sb(ex_sb), .sb_2(mem_sb));
  Multiplexer #(.select(1), .width(32), .disabled("Z"), .enable("false")) multiplexer_15 (
    .in0(adder_2_out), .in1(alu_1_p8), .out(multiplexer_15_out), .sel(JALR));
  Register #(.width(32), .trigger("rising"), .Select("low")) register_1 (
    .D(multiplexer_11_out), .en(ss), .Q(LedData), .clk(CLK));  // open: clr
  not not_10 (not_10_out, signalin[1]);
  and and_12 (and_12_out, not_10_out, not_11_out);
  not not_11 (not_11_out, jAL);
  not not_12 (RsUsed, jAL);
  or or_4 (RtUsed, s, and_12_out);
  Counter #(.width(16), .max('hffff), .ongoal("wrap"), .trigger("rising"), .behavior("old")) counter_3 (
    .count(1'b1), .Q(\无条件分支数 ), .clk(multiplexer_16_out), .clr(RST));  // open: load, D, carry, preset
  Multiplexer #(.select(1), .width(1), .disabled("Z"), .enable("false")) multiplexer_16 (
    .in0(and_13_out), .in1(1'b0), .out(multiplexer_16_out), .sel(CLK));
  and and_13 (and_13_out, JJ, CLK);
  RAM ram_1 (
    .Mode(mem_sb), .\字节地址 (mem_a[11:0]), .Din(MDin), .CLK(CLK), .str(MemWrite), .id(not_13_out),
    .Dout(ram_1_dout));
  not not_13 (not_13_out, MemWrite);
  MEM_WB2 mem_wb2_1 (
    .halt(halt1), .JAL(ex_mem2_1_jalout), .JALR(ex_mem2_1_jalrout), .RegWrite(MEM_RegWrite),
    .MemToReg(ex_mem2_1_memtoreg_2), .ALU_Result(mem_a), .MemData(ram_1_dout), .WriteReg_num(MEMW),
    .PC(M_PC), .CLK(CLK), .bubble(1'b0), .stop(H), .haltout(halt2), .JALout(mem_wb2_1_jalout),
    .JALRout(mem_wb2_1_jalrout), .RegWrite_2(RegWrite), .MemToReg_2(mem_wb2_1_memtoreg_2),
    .ALU_Result_2(mem_wb2_1_alu_result_2), .MemData_2(mem_wb2_1_memdata_2), .WriteReg_num_2(W_F),
    .PCout(WB_PC));
  Comparator #(.width(5), .mode("twosComplement")) comparator_11 (
    .a(rs), .b({5{1'b0}}), .eq(comparator_11_eq));  // open: gt, lt
  Comparator #(.width(5), .mode("twosComplement")) comparator_12 (
    .a(rs), .b(EXW), .eq(comparator_12_eq));  // open: gt, lt
  Comparator #(.width(5), .mode("twosComplement")) comparator_13 (
    .a(rt), .b({5{1'b0}}), .eq(comparator_13_eq));  // open: gt, lt
  Multiplexer #(.select(1), .width(1), .disabled("Z"), .enable("false")) multiplexer_17 (
    .in0(and_14_out), .in1(1'b0), .out(multiplexer_17_out), .sel(CLK));
  and and_14 (and_14_out, B, CLK);
  Multiplexer #(.select(1), .width(32), .disabled("Z"), .enable("false")) multiplexer_18 (
    .in0(mem_wb2_1_alu_result_2), .in1(mem_wb2_1_memdata_2), .out(wb_a), .sel(mem_wb2_1_memtoreg_2));
  not not_14 (not_14_out, comparator_11_eq);
  not not_15 (not_15_out, comparator_13_eq);
  Comparator #(.width(5), .mode("twosComplement")) comparator_14 (
    .a(EXW), .b(rt), .eq(comparator_14_eq));  // open: gt, lt
  Counter #(.width(16), .max('hffff), .ongoal("wrap"), .trigger("rising"), .behavior("old")) counter_4 (
    .count(1'b1), .Q(\条件分支成功数 ), .clk(multiplexer_17_out), .clr(RST));  // open: load, D, carry, preset
  or or_5 (JJ, mem_wb2_1_jalout, mem_wb2_1_jalrout);
  Adder #(.width(32)) adder_3 (.a(WB_PC), .b(32'h4), .out(PC_F));  // open: cin, cout
  or or_6 (H, not_16_out, Go);
  not not_16 (not_16_out, halt2);
  and and_15 (and_15_out, EX_MemToReg, RsUsed, not_14_out, comparator_12_eq);
  and and_16 (and_16_out, EX_MemToReg, not_15_out, comparator_14_eq, RtUsed);
  or or_7 (loaduse, and_15_out, and_16_out);
  and and_17 (and_17_out, ~halt2, loaduse);  // AND_Gate
  Counter #(.width(16), .max('hffff), .ongoal("wrap"), .trigger("rising"), .behavior("old")) counter_5 (
    .count(1'b1), .Q(\插入气泡数 ), .clk(multiplexer_19_out), .clr(RST));  // open: load, D, carry, preset
  Multiplexer #(.select(1), .width(1), .disabled("Z"), .enable("false")) multiplexer_19 (
    .in0(and_18_out), .in1(1'b0), .out(multiplexer_19_out), .sel(CLK));
  and and_18 (and_18_out, and_17_out, CLK);
  Counter #(.width(16), .max('hffff), .ongoal("wrap"), .trigger("rising"), .behavior("old")) counter_6 (
    .count(1'b1), .Q(\LoadUse次数 ), .clk(multiplexer_20_out), .clr(RST));  // open: load, D, carry, preset
  Multiplexer #(.select(1), .width(1), .disabled("Z"), .enable("false")) multiplexer_20 (
    .in0(and_19_out), .in1(1'b0), .out(multiplexer_20_out), .sel(CLK));
  and and_19 (and_19_out, loaduse, CLK);

  // Other names for the same wires on the sheet: W_num[4:0] = IR[11:7]; JJUin[0] = jAL; JJUout[1] = JALR;
  //   MEM_PC[31:0] = M_PC; PC[31:0] = IF_PC; src = signalin[1];
  //   signalout (some bits) = {ex_blt, EX_MemToReg, EX_RegWrite}

  // Notes on the sheet:
  //   中断源
  //   时空图监测，可删除
  //   中断等待指示
  //   数码管输出
  //   指令探针
  //   指令存储器
  //   contents of rom_1 (hex, n*v repeats v):
  //   100493 100006f 100493 200913 300993 100006f 100493 200913 300993 100006f 100493 200913 300993
  //   100006f 100493 200913 300993 3ac000ef 100413 100493 1f49493 900533 2200893 73 24d493 48463 fedff06f
  //   900533 2200893 73 100493 249493 900533 2200893 73 48463 fedff06f 100493 1f49493 900533 2200893 73
  //   4034d493 900533 2200893 73 4044d493 900533 2200893 73 4044d493 900533 2200893 73 4044d493 900533
  //   2200893 73 4044d493 900533 2200893 73 4044d493 900533 2200893 73 4044d493 900533 2200893 73 4044d493
  //   900533 2200893 73 100413 1f41993 41f9d993 433 c00913 300b13 140413 f47413 800293 100313 499993
  //   89e9b3 1300533 2200893 73 406282b3 fe0294e3 140413 f00f93 1f47433 1c41413 800293 100313 49d993
  //   89e9b3 1300533 2200893 73 406282b3 fe0294e3 1c45413 406b0b33 b0463 f95ff06f 2b3 fff2c293 829293
  //   ff2e293 500533 2200893 73 fff00413 493 84a023 140413 448493 84a023 140413 448493 84a023 140413
  //   448493 84a023 140413 448493 84a023 140413 448493 84a023 140413 448493 84a023 140413 448493 84a023
  //   140413 448493 84a023 140413 448493 84a023 140413 448493 84a023 140413 448493 84a023 140413 448493
  //   84a023 140413 448493 84a023 140413 448493 84a023 140413 448493 84a023 140413 448493 140413 433
  //   3c00493 42983 4aa03 149a2b3 28663 134a023 1442023 ffc48493 fe9412e3 800533 2200893 73 440413 3c00493
  //   fc9416e3 3200893 73 100293 300313 800493 849493 7648493 1449493 900533 2200893 73 800e13 54d4b3
  //   64d4b3 900533 2200893 73 fffe0e13 fe0e14e3 a00893 73 fff00293 7700493 849493 7748493 900533 2200893
  //   73 1000e13 54c4b3 900533 2200893 73 fffe0e13 fe0e16e3 a00893 73 313 2000e13 493 100913 930023 900533
  //   2200893 73 12484b3 130313 fffe0e13 fe0e12e3 800e13 313 32483 900533 2200893 73 430313 fffe0e13
  //   fe0e14e3 a00893 73 ff100493 900533 2200893 73 148493 fe04c8e3 a00893 73 a00893 73 413 140413 800533
  //   2200893 73 240413 800533 2200893 73 340413 800533 2200893 73 440413 800533 2200893 73 540413 800533
  //   2200893 73 640413 800533 2200893 73 740413 800533 2200893 73 840413 800533 2200893 2200893 73 8067
  //   JAL
  //   JALR
  //   Beq
  //   Bne
  //   URET
  //   MemToReg
  //   MemWrite
  //   AluOP
  //   AluSrcB
  //   RegWrite
  //   控制位
  //   流水调试日志用
  //   暂停节拍，不能为0
  //   可计数暂停的时钟源
  //   为方便自动评测，需要输出流水线各段保存的PC值，注意是PC不是PC+4，另外ID段寄存器写入信息，Mem段内存写入信息也要输出
  //   数据存储器
endmodule
module \中断  (
  input  clk,
  input  \_1号 ,
  input  clear,
  input  [1:0] clrid,
  input  \_2号 ,
  input  \_3号 ,
  output _1ing,
  output [1:0] ingid,
  output _2ing,
  output [31:0] address,
  output _3ing
);

  wire and_1_out, and_2_out, and_3_out, c0, c1, c2, c3, d_ff_1_q, d_ff_2_q, d_ff_3_q, IR1_q, IR2_q, IR3_q,
       or_4_out, or_5_out, or_6_out;

  or or_1 (_1ing, IR1_q, d_ff_1_q);
  or or_2 (_2ing, IR2_q, d_ff_2_q);
  or or_3 (_3ing, IR3_q, d_ff_3_q);
  D_Flip_Flop #(.trigger("rising"), .Pre_Clr_Positions("LEGACY"), .NegatePresetClear("false"), .enable("true"), .NewFFLayout("false")) d_ff_1 (
    .clk(\_1号 ), .D(1'b1), .Q(d_ff_1_q), .reset(IR1_q));  // open: Qn, preset, en
  D_Flip_Flop #(.trigger("rising"), .Pre_Clr_Positions("LEGACY"), .NegatePresetClear("false"), .enable("true"), .NewFFLayout("false")) d_ff_2 (
    .clk(\_2号 ), .D(1'b1), .Q(d_ff_2_q), .reset(IR2_q));  // open: Qn, preset, en
  D_Flip_Flop #(.trigger("rising"), .Pre_Clr_Positions("LEGACY"), .NegatePresetClear("false"), .enable("true"), .NewFFLayout("false")) d_ff_3 (
    .clk(\_3号 ), .D(1'b1), .Q(d_ff_3_q), .reset(IR3_q));  // open: Qn, preset, en
  or or_4 (or_4_out, d_ff_1_q, IR1_q);
  or or_5 (or_5_out, d_ff_2_q, IR2_q);
  or or_6 (or_6_out, d_ff_3_q, IR3_q);
  and and_1 (and_1_out, or_4_out, ~c1);  // AND_Gate
  and and_2 (and_2_out, or_5_out, ~c2);  // AND_Gate
  and and_3 (and_3_out, or_6_out, ~c3);  // AND_Gate
  D_Flip_Flop #(.trigger("rising"), .Pre_Clr_Positions("LEGACY"), .NegatePresetClear("false"), .enable("true"), .NewFFLayout("false")) IR1 (
    .clk(clk), .D(and_1_out), .Q(IR1_q));  // open: Qn, preset, en, reset
  D_Flip_Flop #(.trigger("rising"), .Pre_Clr_Positions("LEGACY"), .NegatePresetClear("false"), .enable("true"), .NewFFLayout("false")) IR2 (
    .clk(clk), .D(and_2_out), .Q(IR2_q));  // open: Qn, preset, en, reset
  D_Flip_Flop #(.trigger("rising"), .Pre_Clr_Positions("LEGACY"), .NegatePresetClear("false"), .enable("true"), .NewFFLayout("false")) IR3 (
    .clk(clk), .D(and_3_out), .Q(IR3_q));  // open: Qn, preset, en, reset
  Priority_Encoder #(.select(2), .disabled("Z")) priority_encoder_1 (
    .in0(1'b1), .in1(IR1_q), .in2(IR2_q), .in3(IR3_q), .out(ingid));  // open: gs, en_out, en_in
  Decoder #(.select(2), .tristate("false"), .disabled(0), .enable("true")) decoder_1 (
    .out0(c0), .out1(c1), .out2(c2), .out3(c3), .sel(clrid), .en(clear));
  Multiplexer #(.select(2), .width(32), .disabled("Z"), .enable("false")) multiplexer_1 (
    .in1(32'h30ac), .in2(32'h3150), .in3(32'h31f4), .out(address), .sel(ingid));  // open: in0

  // Notes on the sheet:
  //   Reset 
  //   Reset 
  //   Reset 
endmodule

module \单周期_单级中断  (
  input  IR1,
  input  IR2,
  input  IR3,
  output RegWrite,
  output MemWrite,
  output [31:0] PC,
  output [31:0] IR,
  output [31:0] RDin,
  output [31:0] MDin,
  output [31:0] LedData
);

  wire alu_1_equal, alu_1_out_6, and_3_out, and_4_out, and_5_out, CLK, clock_1_out, comparator_1_eq,
       comparator_2_eq, comparator_3_eq, comparator_4_eq, comparator_5_eq, comparator_6_eq, comparator_6_lt,
       controlled_inverter_1_out, controlled_inverter_2_out, controlled_inverter_3_out, d_ff_1_q, ecall, Go,
       halt, IR1_t, IR2_t, IR3_t, IRA, IRB, IRC, JALR, nand_1_out, not_1_out, not_2_out, not_3_out,
       not_4_out, not_5_out, or_1_out, or_2_out, or_3_out, or_4_out, or_5_out, or_9_out, or_10_out, RST, sb,
       ss, Uret, W1, W2, W3, \中断响应 , \单周期硬布线控制器_1_alu_src , \单周期硬布线控制器_1_beq , \单周期硬布线控制器_1_blt ,
       \单周期硬布线控制器_1_bne , \单周期硬布线控制器_1_jal , \单周期硬布线控制器_1_memtoreg , \单周期硬布线控制器_1_s_type ;
  wire [1:0] id, register_1_q;
  wire [3:0] \单周期硬布线控制器_1_alu_op ;
  wire [4:0] multiplexer_4_out, multiplexer_5_out;
  wire [11:0] multiplexer_6_out;
  wire [12:0] CNT_num;
  wire [15:0] \总周期数 ;
  wire [31:0] adder_1_out, adder_2_out, alu_1_result, bit_extender_1_out, bit_extender_2_out,
       bit_extender_3_out, intPC, multiplexer_2_out, multiplexer_3_out, multiplexer_8_out, multiplexer_9_out,
       multiplexer_10_out, multiplexer_11_out, multiplexer_12_out, PCN, ram_1_dout, regifile_1_r1,
       shifter_1_out, \中断地址 ;

  Button \u_继续运行  (.out(Go));
  Button _1 (.out(IRA));
  Button _2 (.out(IRB));
  Button _3 (.out(IRC));
  LED #(.active("true")) led_1 (.in(W1));
  LED #(.active("true")) led_2 (.in(W2));
  LED #(.active("true")) led_3 (.in(W3));
  or or_1 (or_1_out, \单周期硬布线控制器_1_jal , JALR, or_9_out);
  Hex_Digit_Display hex_digit_display_1 (.value(LedData[31:28]));  // open: dp
  Comparator #(.width(16), .mode("twosComplement")) comparator_1 (
    .a(16'h23b), .b(\总周期数 ), .eq(comparator_1_eq));  // open: gt, lt
  Comparator #(.width(16), .mode("twosComplement")) comparator_2 (
    .a(\总周期数 ), .b(16'h1), .eq(comparator_2_eq));  // open: gt, lt
  Comparator #(.width(16), .mode("twosComplement")) comparator_3 (
    .a(\总周期数 ), .b(16'h4), .eq(comparator_3_eq));  // open: gt, lt
  Comparator #(.width(16), .mode("twosComplement")) comparator_4 (
    .a(\总周期数 ), .b(16'h7), .eq(comparator_4_eq));  // open: gt, lt
  Multiplexer #(.select(1), .width(32), .disabled("Z"), .enable("false")) multiplexer_1 (
    .in0(adder_1_out), .in1(multiplexer_11_out), .out(PCN), .sel(or_1_out));
  Multiplexer #(.select(1), .width(32), .disabled("Z"), .enable("false")) multiplexer_2 (
    .in0(PCN), .in1(\中断地址 ), .out(multiplexer_2_out), .sel(\中断响应 ));
  Hex_Digit_Display hex_digit_display_2 (.value(LedData[27:24]));  // open: dp
  Hex_Digit_Display hex_digit_display_3 (.value(LedData[23:20]));  // open: dp
  or or_2 (or_2_out, comparator_1_eq, comparator_2_eq);
  assign controlled_inverter_1_out = or_2_out ? ~CLK : 1'bz;  // Controlled_Inverter controlled_inverter_1
  assign controlled_inverter_2_out = comparator_3_eq ? ~CLK : 1'bz;  // Controlled_Inverter controlled_inverter_2
  assign controlled_inverter_3_out = comparator_4_eq ? ~CLK : 1'bz;  // Controlled_Inverter controlled_inverter_3
  Multiplexer #(.select(1), .width(32), .disabled("Z"), .enable("false")) multiplexer_3 (
    .in0(multiplexer_2_out), .in1(intPC), .out(multiplexer_3_out), .sel(Uret));
  Hex_Digit_Display hex_digit_display_4 (.value(LedData[15:12]));  // open: dp
  Hex_Digit_Display hex_digit_display_5 (.value(LedData[19:16]));  // open: dp
  Pull_Resistor #(.pull(0)) pull_resistor_1 (.node(controlled_inverter_1_out));
  Pull_Resistor #(.pull(0)) pull_resistor_2 (.node(controlled_inverter_2_out));
  Pull_Resistor #(.pull(0)) pull_resistor_3 (.node(controlled_inverter_3_out));
  not not_1 (not_1_out, halt);
  Register #(.width(2), .trigger("falling"), .Select("low")) register_1 (
    .D(id), .Q(register_1_q), .clk(or_3_out));  // open: en, clr
  or or_3 (or_3_out, Uret, \中断响应 );
  Hex_Digit_Display hex_digit_display_6 (.value(LedData[7:4]));  // open: dp
  Hex_Digit_Display hex_digit_display_7 (.value(LedData[11:8]));  // open: dp
  // Probe on \总周期数 
  Register #(.width(32), .trigger("rising"), .Select("low")) u_PC (
    .D(multiplexer_3_out), .en(or_4_out), .Q(PC), .clk(CLK), .clr(RST));
  or or_4 (or_4_out, Go, not_1_out);
  Adder #(.width(32)) adder_1 (.a(PC), .b(32'h4), .out(adder_1_out));  // open: cin, cout
  Hex_Digit_Display hex_digit_display_8 (.value(LedData[3:0]));  // open: dp
  \中断响应  \u_中断响应_1  (
    .clk(CLK), .\_1号 (IR1_t), .next(\中断响应 ), .nextid(id), .\_2号 (IR2_t), .\_3号 (IR3_t), .\中断响应 (\中断响应 ),
    .\开中断 (Uret), .\关中断 (\中断响应 ));
  \中断  \u_中断_1  (
    .ingid(id), .\_1号 (IR1_t), .\_2号 (IR2_t), .\_3号 (IR3_t), ._1ing(W1), ._2ing(W2), ._3ing(W3),
    .address(\中断地址 ), .clear(Uret), .clrid(register_1_q), .clk(CLK));
  or or_5 (or_5_out, \单周期硬布线控制器_1_jal , JALR);
  // RiscV_Probe riscv_probe_1: pin names not known; wires that end beside it: PC[11:2], IR
  or or_6 (IR1_t, IR1, IRA);
  ROM #(.addrWidth(10), .dataWidth(32), .Select("high")) rom_1 (.addr(PC[11:2]), .data(IR));
  or or_7 (IR2_t, IR2, IRB);
  \单周期硬布线控制器  \u_单周期硬布线控制器_1  (
    .Funct({IR[30], IR[25], IR[14:12]}), .OP(IR[6:2]), .ALU_OP(\单周期硬布线控制器_1_alu_op ),
    .MemToReg(\单周期硬布线控制器_1_memtoreg ), .MemWrite(MemWrite), .ALU_SRC(\单周期硬布线控制器_1_alu_src ),
    .RegWrite(RegWrite), .ecall(ecall), .S_type(\单周期硬布线控制器_1_s_type ), .Jalr(JALR), .Beq(\单周期硬布线控制器_1_beq ),
    .JAL(\单周期硬布线控制器_1_jal ), .Bne(\单周期硬布线控制器_1_bne ), .in_3(IR[21]), .uret(Uret), .blt(\单周期硬布线控制器_1_blt ),
    .sb(sb));  // open: csrrsi, csrrci
  Multiplexer #(.select(1), .width(5), .disabled("Z"), .enable("false")) multiplexer_4 (
    .in0(IR[19:15]), .in1(5'b10001), .out(multiplexer_4_out), .sel(ecall));
  Multiplexer #(.select(1), .width(5), .disabled("Z"), .enable("false")) multiplexer_5 (
    .in0(IR[24:20]), .in1(5'b01010), .out(multiplexer_5_out), .sel(ecall));
  Multiplexer #(.select(1), .width(12), .disabled("Z"), .enable("false")) multiplexer_6 (
    .in0(IR[31:20]), .in1({IR[31:25], IR[11:7]}), .out(multiplexer_6_out), .sel(\单周期硬布线控制器_1_s_type ));
  Multiplexer #(.select(1), .width(32), .disabled("Z"), .enable("false")) multiplexer_7 (
    .in0(multiplexer_12_out), .in1(adder_1_out), .out(RDin), .sel(or_5_out));
  or or_8 (IR3_t, IR3, IRC);
  assign bit_extender_1_out = {{20{IR[31]}}, {IR[31], IR[7], IR[30:25], IR[11:8]}};  // Bit_Extender bit_extender_1
  assign bit_extender_2_out = {{12{IR[31]}}, {IR[31], IR[19:12], IR[20], IR[30:21]}};  // Bit_Extender bit_extender_2
  Register #(.width(32), .trigger("rising"), .Select("low")) register_2 (
    .D(PCN), .en(\中断响应 ), .Q(intPC), .clk(CLK));  // open: clr
  Regifile regifile_1 (
    .Din(RDin), .Clk(CLK), .R1(regifile_1_r1), .R2(MDin), .WE(RegWrite), .W_num(IR[11:7]),
    .R1_num(multiplexer_4_out), .R2_num(multiplexer_5_out));
  assign bit_extender_3_out = {{20{multiplexer_6_out[11]}}, multiplexer_6_out};  // Bit_Extender bit_extender_3
  Multiplexer #(.select(1), .width(32), .disabled("Z"), .enable("false")) multiplexer_8 (
    .in0(bit_extender_2_out), .in1(bit_extender_1_out), .out(multiplexer_8_out), .sel(or_9_out));
  Comparator #(.width(32), .mode("twosComplement")) comparator_5 (
    .a(32'h22), .b(regifile_1_r1), .eq(comparator_5_eq));  // open: gt, lt
  Multiplexer #(.select(1), .width(32), .disabled("Z"), .enable("false")) multiplexer_9 (
    .in0(MDin), .in1(bit_extender_3_out), .out(multiplexer_9_out), .sel(\单周期硬布线控制器_1_alu_src ));
  Multiplexer #(.select(1), .width(32), .disabled("Z"), .enable("false")) multiplexer_10 (
    .in0(LedData), .in1(MDin), .out(multiplexer_10_out), .sel(ss));
  not not_2 (not_2_out, comparator_5_eq);
  ALU alu_1 (
    .X(regifile_1_r1), .Y(multiplexer_9_out), .AluOP(\单周期硬布线控制器_1_alu_op ), .Equal(alu_1_equal),
    .Result(alu_1_result), .out_6(alu_1_out_6));  // open: Result_2, out_4
  and and_1 (ss, comparator_5_eq, ecall);
  and and_2 (halt, not_2_out, ecall);
  not not_3 (not_3_out, alu_1_equal);
  and and_3 (and_3_out, \单周期硬布线控制器_1_beq , alu_1_equal);
  Shifter #(.width(32), .shift("ll")) shifter_1 (.in(multiplexer_8_out), .\dist (5'b00001), .out(shifter_1_out));
  and and_4 (and_4_out, \单周期硬布线控制器_1_bne , not_3_out);
  Adder #(.width(32)) adder_2 (.a(shifter_1_out), .b(PC), .out(adder_2_out));  // open: cin, cout
  and and_5 (and_5_out, \单周期硬布线控制器_1_blt , alu_1_out_6);
  RAM ram_1 (
    .Mode(sb), .\字节地址 (alu_1_result[11:0]), .Din(MDin), .CLK(CLK), .str(MemWrite), .id(not_4_out),
    .Dout(ram_1_dout));
  not not_4 (not_4_out, MemWrite);
  Multiplexer #(.select(1), .width(32), .disabled("Z"), .enable("false")) multiplexer_11 (
    .in0(adder_2_out), .in1(alu_1_result), .out(multiplexer_11_out), .sel(JALR));
  D_Flip_Flop #(.trigger("high"), .Pre_Clr_Positions("LEGACY"), .NegatePresetClear("false"), .enable("true"), .NewFFLayout("false")) d_ff_1 (.Q(d_ff_1_q));  // open: clk, D, Qn, preset, en, reset
  // Probe on 13'hc
  or or_9 (or_9_out, and_4_out, and_5_out, and_3_out);
  Register #(.width(32), .trigger("rising"), .Select("low")) register_3 (
    .D(multiplexer_10_out), .en(ss), .Q(LedData), .clk(CLK));  // open: clr
  Comparator #(.width(13), .mode("twosComplement")) comparator_6 (
    .a(CNT_num), .b(13'hc), .eq(comparator_6_eq), .lt(comparator_6_lt));  // open: gt
  Clock #(.highDuration(1), .lowDuration(1)) clock_1 (.out(clock_1_out));
  Multiplexer #(.select(1), .width(32), .disabled("Z"), .enable("false")) multiplexer_12 (
    .in0(alu_1_result), .in1(ram_1_dout), .out(multiplexer_12_out), .sel(\单周期硬布线控制器_1_memtoreg ));
  Counter #(.width(13), .max('h1fff), .ongoal("stay"), .trigger("rising"), .behavior("old")) counter_1 (
    .count(comparator_6_lt), .Q(CNT_num), .clk(clock_1_out));  // open: load, D, carry, clr, preset
  nand nand_1 (nand_1_out, d_ff_1_q, comparator_6_eq);
  assign CLK = nand_1_out ? clock_1_out : 1'bz;  // Controlled_Buffer controlled_buffer_1
  Pull_Resistor #(.pull(1)) pull_resistor_4 (.node(CLK));
  or or_10 (or_10_out, Go, not_5_out);
  not not_5 (not_5_out, halt);
  Counter #(.width(16), .max('hffff), .ongoal("wrap"), .trigger("rising"), .behavior("new")) counter_2 (
    .count(or_10_out), .Q(\总周期数 ), .clk(CLK));  // open: load, D, carry, clr, preset, down

  // Notes on the sheet:
  //   中断源
  //   中断等待指示
  //   总复位信号应将除ROM以外所有存储组件全部清零
  //   单级中断测试信号模拟器
  //   数码管输出
  //   数码管输出应该用寄存器锁存，否则显示数据只能一闪而过
  //   指令探针
  //   指令存储器
  //   指令字
  //   contents of rom_1 (hex, n*v repeats v):
  //   7d000113 100413 1f41993 41f9d993 433 c00913 800b13 140413 f47413 800293 100313 499993 89e9b3 1300533
  //   2200893 73 406282b3 fe0294e3 140413 f00f93 1f47433 1c41413 800293 100313 49d993 89e9b3 1300533
  //   2200893 73 406282b3 fe0294e3 1c45413 406b0b33 b0463 f95ff06f 2b3 fff2c293 1029293 fff2e293 500533
  //   2200893 73 f5dff06f 1112023 410113 a12023 410113 812023 410113 1312023 410113 1412023 410113 1512023
  //   410113 1612023 410113 100b13 300a13 100a93 1600433 441413 14469b3 1300533 2200893 73 fe0416e3
  //   415a0a33 fe0a10e3 ffc10113 12b03 ffc10113 12a83 ffc10113 12a03 ffc10113 12983 ffc10113 12403
  //   ffc10113 12503 ffc10113 12883 200073 1112023 410113 a12023 410113 812023 410113 1312023 410113
  //   1412023 410113 1512023 410113 1612023 410113 200b13 300a13 100a93 1600433 441413 14469b3 1300533
  //   2200893 73 fe0416e3 415a0a33 fe0a10e3 ffc10113 12b03 ffc10113 12a83 ffc10113 12a03 ffc10113 12983
  //   ffc10113 12403 ffc10113 12503 ffc10113 12883 200073 1112023 410113 a12023 410113 812023 410113
  //   1312023 410113 1412023 410113 1512023 410113 1612023 410113 300b13 300a13 100a93 1600433 441413
  //   14469b3 1300533 2200893 73 fe0416e3 415a0a33 fe0a10e3 ffc10113 12b03 ffc10113 12a83 ffc10113 12a03
  //   ffc10113 12983 ffc10113 12403 ffc10113 12503 ffc10113 12883 200073
  //   JAL
  //   JALR
  //   URET
  //   Beq
  //   Bne
  //   MemToReg
  //   MemWrite
  //   AluOP
  //   AluSrcB
  //   RegWrite
  //   为方便自动评测，需要输出PC，IR，寄存器堆写如数据RDin
  //   RAM写使能MemWrite、RAM写入数据MDin等信号
  //   数据存储器
  //   控制位
  //   暂停节拍，不能为0
  //   戳工具置1进入计数暂停模式，ctrl+k时钟自动运行到对应节拍暂停
  //   ctrl+k关闭时钟连续运行，将控制位置零，进入单步调试模式调试
  //   可计数暂停的时钟源
endmodule

module \单周期_多级中断  (
  input  IR1,
  input  IR2,
  input  IR3,
  output RegWrite,
  output MemWrite,
  output [31:0] PC,
  output [31:0] IR,
  output [31:0] RDin,
  output [31:0] MDin,
  output [31:0] LedData
);

  wire alu_1_equal, alu_1_out_6, and_3_out, and_4_out, and_5_out, CLK, clock_1_out, comparator_1_eq,
       comparator_2_eq, comparator_3_eq, comparator_4_eq, comparator_5_eq, comparator_6_eq, comparator_7_eq,
       comparator_8_eq, comparator_8_lt, csrrci, csrrsi, d_ff_1_q, ecall, equal, Go, halt, IR1_t, IR2_t,
       IR3_t, IRA, IRB, IRC, JALR, nand_1_out, not_1_out, not_3_out, not_4_out, not_5_out, not_6_out,
       or_1_out, or_2_out, or_3_out, or_4_out, or_5_out, or_6_out, or_7_out, or_9_out, or_13_out, or_14_out,
       pull_resistor_1_node, pull_resistor_2_node, pull_resistor_3_node, RST, sb, ss, Uret, W1, W2, W3,
       \中断响应 , \单周期硬布线控制器_1_alu_src , \单周期硬布线控制器_1_beq , \单周期硬布线控制器_1_blt , \单周期硬布线控制器_1_bne ,
       \单周期硬布线控制器_1_jal , \单周期硬布线控制器_1_memtoreg , \单周期硬布线控制器_1_s_type , \堆栈 ;
  wire [1:0] id, register_1_q;
  wire [3:0] \单周期硬布线控制器_1_alu_op ;
  wire [4:0] multiplexer_4_out, multiplexer_5_out;
  wire [11:0] multiplexer_7_out;
  wire [12:0] CNT_num;
  wire [15:0] \总周期数 ;
  wire [31:0] adder_1_out, adder_2_out, alu_1_result, bit_extender_1_out, bit_extender_2_out,
       bit_extender_3_out, intPC, multiplexer_2_out, multiplexer_3_out, multiplexer_6_out, multiplexer_9_out,
       multiplexer_10_out, multiplexer_11_out, multiplexer_12_out, multiplexer_13_out, multiplexer_14_out,
       multiplexer_15_out, multiplexer_16_out, PCN, ram_1_dout, regifile_1_r1, register_3_q, register_4_q,
       register_6_q, shifter_1_out, \断点 ;

  Button \u_继续运行  (.out(Go));
  Button _1 (.out(IRA));
  Button _2 (.out(IRB));
  Button _3 (.out(IRC));
  LED #(.active("true")) led_1 (.in(W1));
  LED #(.active("true")) led_2 (.in(W2));
  LED #(.active("true")) led_3 (.in(W3));
  or or_1 (or_1_out, \单周期硬布线控制器_1_jal , JALR, or_13_out);
  Hex_Digit_Display hex_digit_display_1 (.value(LedData[31:28]));  // open: dp
  Comparator #(.width(16), .mode("twosComplement")) comparator_1 (
    .a(\总周期数 ), .b(16'h7), .eq(comparator_1_eq));  // open: gt, lt
  Comparator #(.width(16), .mode("twosComplement")) comparator_2 (
    .a(\总周期数 ), .b(16'h241), .eq(comparator_2_eq));  // open: gt, lt
  Multiplexer #(.select(1), .width(32), .disabled("Z"), .enable("false")) multiplexer_1 (
    .in0(adder_1_out), .in1(multiplexer_14_out), .out(PCN), .sel(or_1_out));
  Hex_Digit_Display hex_digit_display_2 (.value(LedData[27:24]));  // open: dp
  Hex_Digit_Display hex_digit_display_3 (.value(LedData[23:20]));  // open: dp
  Comparator #(.width(16), .mode("twosComplement")) comparator_3 (
    .a(16'h258), .b(\总周期数 ), .eq(comparator_3_eq));  // open: gt, lt
  or or_2 (or_2_out, comparator_3_eq, comparator_4_eq);
  Comparator #(.width(16), .mode("twosComplement")) comparator_4 (
    .a(\总周期数 ), .b(16'h1), .eq(comparator_4_eq));  // open: gt, lt
  Comparator #(.width(16), .mode("twosComplement")) comparator_5 (
    .a(\总周期数 ), .b(16'h4), .eq(comparator_5_eq));  // open: gt, lt
  or or_3 (or_3_out, comparator_1_eq, comparator_2_eq);
  Multiplexer #(.select(1), .width(32), .disabled("Z"), .enable("false")) multiplexer_2 (
    .in0(PCN), .in1(\断点 ), .out(multiplexer_2_out), .sel(\中断响应 ));
  Multiplexer #(.select(1), .width(32), .disabled("Z"), .enable("false")) multiplexer_3 (
    .in0(multiplexer_2_out), .in1(intPC), .out(multiplexer_3_out), .sel(Uret));
  Hex_Digit_Display hex_digit_display_4 (.value(LedData[19:16]));  // open: dp
  Hex_Digit_Display hex_digit_display_5 (.value(LedData[15:12]));  // open: dp
  Pull_Resistor #(.pull(0)) pull_resistor_1 (.node(pull_resistor_1_node));
  assign pull_resistor_1_node = or_2_out ? ~CLK : 1'bz;  // Controlled_Inverter controlled_inverter_1
  Pull_Resistor #(.pull(0)) pull_resistor_2 (.node(pull_resistor_2_node));
  assign pull_resistor_2_node = comparator_5_eq ? ~CLK : 1'bz;  // Controlled_Inverter controlled_inverter_2
  Pull_Resistor #(.pull(0)) pull_resistor_3 (.node(pull_resistor_3_node));
  assign pull_resistor_3_node = or_3_out ? ~CLK : 1'bz;  // Controlled_Inverter controlled_inverter_3
  Hex_Digit_Display hex_digit_display_6 (.value(LedData[7:4]));  // open: dp
  Hex_Digit_Display hex_digit_display_7 (.value(LedData[11:8]));  // open: dp
  // Probe on \总周期数 
  Register #(.width(32), .trigger("rising"), .Select("low")) u_PC (
    .D(multiplexer_3_out), .en(or_4_out), .Q(PC), .clk(CLK), .clr(RST));
  or or_4 (or_4_out, Go, not_1_out);
  not not_1 (not_1_out, halt);
  Adder #(.width(32)) adder_1 (.a(PC), .b(32'h4), .out(adder_1_out));  // open: cin, cout
  or or_5 (or_5_out, Uret, csrrsi);
  Hex_Digit_Display hex_digit_display_8 (.value(LedData[3:0]));  // open: dp
  \中断响应多级  \u_中断响应多级_1  (
    .clk(CLK), .\_1号 (IR1_t), .next(\中断响应 ), .nextid(id), .\_2号 (IR2_t), .\_3号 (IR3_t), .\中断响应 (\中断响应 ),
    .\开中断 (or_5_out), .\关中断 (or_7_out), .equal(equal));
  \中断多级  \u_中断多级_1  (
    .clk(CLK), .\_1号 (IR1_t), ._1ing(W1), .clear(Uret), .\_2号 (IR2_t), ._2ing(W2), .\_3号 (IR3_t), ._3ing(W3),
    .ingid(id), .address(\断点 ));
  or or_6 (or_6_out, \单周期硬布线控制器_1_jal , JALR);
  or or_7 (or_7_out, \中断响应 , csrrci);
  or or_8 (IR1_t, IR1, IRA);
  // RiscV_Probe riscv_probe_1: pin names not known; wires that end beside it: PC[11:2], IR
  ROM #(.addrWidth(10), .dataWidth(32), .Select("high")) rom_1 (.addr(PC[11:2]), .data(IR));
  or or_9 (or_9_out, Uret, \中断响应 );
  or or_10 (IR2_t, IR2, IRB);
  Register #(.width(2), .trigger("falling"), .Select("low")) register_1 (
    .D(id), .Q(register_1_q), .clk(or_9_out));  // open: en, clr
  \单周期硬布线控制器  \u_单周期硬布线控制器_1  (
    .Funct({IR[30], IR[25], IR[14:12]}), .OP(IR[6:2]), .ALU_OP(\单周期硬布线控制器_1_alu_op ),
    .MemToReg(\单周期硬布线控制器_1_memtoreg ), .MemWrite(MemWrite), .ALU_SRC(\单周期硬布线控制器_1_alu_src ),
    .RegWrite(RegWrite), .ecall(ecall), .S_type(\单周期硬布线控制器_1_s_type ), .Jalr(JALR), .Beq(\单周期硬布线控制器_1_beq ),
    .JAL(\单周期硬布线控制器_1_jal ), .Bne(\单周期硬布线控制器_1_bne ), .in_3(IR[21]), .uret(Uret), .blt(\单周期硬布线控制器_1_blt ),
    .sb(sb), .csrrsi(csrrsi), .csrrci(csrrci));
  Multiplexer #(.select(1), .width(5), .disabled("Z"), .enable("false")) multiplexer_4 (
    .in0(IR[19:15]), .in1(5'b10001), .out(multiplexer_4_out), .sel(ecall));
  Multiplexer #(.select(1), .width(5), .disabled("Z"), .enable("false")) multiplexer_5 (
    .in0(IR[24:20]), .in1(5'b01010), .out(multiplexer_5_out), .sel(ecall));
  Multiplexer #(.select(1), .width(32), .disabled("Z"), .enable("false")) multiplexer_6 (
    .in0(PCN), .in1(register_3_q), .out(multiplexer_6_out), .sel(csrrci));
  not not_2 (equal, comparator_6_eq);
  Comparator #(.width(2), .mode("twosComplement")) comparator_6 (
    .a(id), .b(register_1_q), .eq(comparator_6_eq));  // open: gt, lt
  or or_11 (IR3_t, IR3, IRC);
  Multiplexer #(.select(1), .width(12), .disabled("Z"), .enable("false")) multiplexer_7 (
    .in0(IR[31:20]), .in1({IR[31:25], IR[11:7]}), .out(multiplexer_7_out), .sel(\单周期硬布线控制器_1_s_type ));
  assign bit_extender_1_out = {{20{IR[31]}}, {IR[31], IR[7], IR[30:25], IR[11:8]}};  // Bit_Extender bit_extender_1
  assign bit_extender_2_out = {{12{IR[31]}}, {IR[31], IR[19:12], IR[20], IR[30:21]}};  // Bit_Extender bit_extender_2
  Multiplexer #(.select(1), .width(32), .disabled("Z"), .enable("false")) multiplexer_8 (
    .in0(multiplexer_16_out), .in1(adder_1_out), .out(RDin), .sel(or_6_out));
  Register #(.width(32), .trigger("rising"), .Select("low")) register_2 (
    .D(multiplexer_6_out), .en(or_7_out), .Q(intPC), .clk(CLK));  // open: clr
  assign bit_extender_3_out = {{20{multiplexer_7_out[11]}}, multiplexer_7_out};  // Bit_Extender bit_extender_3
  Multiplexer #(.select(1), .width(32), .disabled("Z"), .enable("false")) multiplexer_9 (
    .in0(bit_extender_2_out), .in1(bit_extender_1_out), .out(multiplexer_9_out), .sel(or_13_out));
  Multiplexer #(.select(1), .width(32), .disabled("Z"), .enable("false")) multiplexer_10 (
    .in0(intPC), .in1(register_4_q), .out(multiplexer_10_out), .sel(csrrci));
  Regifile regifile_1 (
    .Din(RDin), .Clk(CLK), .R1(regifile_1_r1), .R2(MDin), .WE(RegWrite), .W_num(IR[11:7]),
    .R1_num(multiplexer_4_out), .R2_num(multiplexer_5_out));
  Multiplexer #(.select(1), .width(32), .disabled("Z"), .enable("false")) multiplexer_11 (
    .in0(MDin), .in1(bit_extender_3_out), .out(multiplexer_11_out), .sel(\单周期硬布线控制器_1_alu_src ));
  Multiplexer #(.select(1), .width(32), .disabled("Z"), .enable("false")) multiplexer_12 (
    .in0(LedData), .in1(MDin), .out(multiplexer_12_out), .sel(ss));
  Comparator #(.width(32), .mode("twosComplement")) comparator_7 (
    .a(32'h22), .b(regifile_1_r1), .eq(comparator_7_eq));  // open: gt, lt
  and and_1 (ss, comparator_7_eq, ecall);
  not not_3 (not_3_out, comparator_7_eq);
  and and_2 (halt, not_3_out, ecall);
  or or_12 (\堆栈 , csrrci, csrrsi);
  Register #(.width(32), .trigger("rising"), .Select("low")) register_3 (
    .D(multiplexer_10_out), .en(\堆栈 ), .Q(register_3_q), .clk(CLK));  // open: clr
  Multiplexer #(.select(1), .width(32), .disabled("Z"), .enable("false")) multiplexer_13 (
    .in0(register_3_q), .in1(register_6_q), .out(multiplexer_13_out), .sel(csrrci));
  not not_4 (not_4_out, alu_1_equal);
  and and_3 (and_3_out, \单周期硬布线控制器_1_beq , alu_1_equal);
  ALU alu_1 (
    .X(regifile_1_r1), .Y(multiplexer_11_out), .AluOP(\单周期硬布线控制器_1_alu_op ), .Equal(alu_1_equal),
    .Result(alu_1_result), .out_6(alu_1_out_6));  // open: Result_2, out_4
  Shifter #(.width(32), .shift("ll")) shifter_1 (.in(multiplexer_9_out), .\dist (5'b00001), .out(shifter_1_out));
  and and_4 (and_4_out, \单周期硬布线控制器_1_bne , not_4_out);
  Adder #(.width(32)) adder_2 (.a(shifter_1_out), .b(PC), .out(adder_2_out));  // open: cin, cout
  Register #(.width(32), .trigger("rising"), .Select("low")) register_4 (
    .D(multiplexer_13_out), .en(\堆栈 ), .Q(register_4_q), .clk(CLK));  // open: clr
  and and_5 (and_5_out, \单周期硬布线控制器_1_blt , alu_1_out_6);
  not not_5 (not_5_out, MemWrite);
  Multiplexer #(.select(1), .width(32), .disabled("Z"), .enable("false")) multiplexer_14 (
    .in0(adder_2_out), .in1(alu_1_result), .out(multiplexer_14_out), .sel(JALR));
  Multiplexer #(.select(1), .width(32), .disabled("Z"), .enable("false")) multiplexer_15 (
    .in0(register_4_q), .in1({32{1'b0}}), .out(multiplexer_15_out), .sel(csrrci));
  D_Flip_Flop #(.trigger("high"), .Pre_Clr_Positions("LEGACY"), .NegatePresetClear("false"), .enable("true"), .NewFFLayout("false")) d_ff_1 (.Q(d_ff_1_q));  // open: clk, D, Qn, preset, en, reset
  // Probe on 13'hc
  or or_13 (or_13_out, and_4_out, and_5_out, and_3_out);
  RAM ram_1 (
    .Mode(sb), .\字节地址 (alu_1_result[11:0]), .Din(MDin), .CLK(CLK), .str(MemWrite), .id(not_5_out),
    .Dout(ram_1_dout));
  Register #(.width(32), .trigger("rising"), .Select("low")) register_5 (
    .D(multiplexer_12_out), .en(ss), .Q(LedData), .clk(CLK));  // open: clr
  Register #(.width(32), .trigger("rising"), .Select("low")) register_6 (
    .D(multiplexer_15_out), .en(\堆栈 ), .Q(register_6_q), .clk(CLK));  // open: clr
  Comparator #(.width(13), .mode("twosComplement")) comparator_8 (
    .a(CNT_num), .b(13'hc), .eq(comparator_8_eq), .lt(comparator_8_lt));  // open: gt
  Clock #(.highDuration(1), .lowDuration(1)) clock_1 (.out(clock_1_out));
  Multiplexer #(.select(1), .width(32), .disabled("Z"), .enable("false")) multiplexer_16 (
    .in0(alu_1_result), .in1(ram_1_dout), .out(multiplexer_16_out), .sel(\单周期硬布线控制器_1_memtoreg ));
  Counter #(.width(13), .max('h1fff), .ongoal("stay"), .trigger("rising"), .behavior("old")) counter_1 (
    .count(comparator_8_lt), .Q(CNT_num), .clk(clock_1_out));  // open: load, D, carry, clr, preset
  nand nand_1 (nand_1_out, d_ff_1_q, comparator_8_eq);
  assign CLK = nand_1_out ? clock_1_out : 1'bz;  // Controlled_Buffer controlled_buffer_1
  Pull_Resistor #(.pull(1)) pull_resistor_4 (.node(CLK));
  or or_14 (or_14_out, Go, not_6_out);
  not not_6 (not_6_out, halt);
  Counter #(.width(16), .max('hffff), .ongoal("wrap"), .trigger("rising"), .behavior("new")) counter_2 (
    .count(or_14_out), .Q(\总周期数 ), .clk(CLK));  // open: load, D, carry, clr, preset, down

  // Notes on the sheet:
  //   中断源
  //   中断等待指示
  //   总复位信号应将除ROM以外所有存储组件全部清零
  //   多级中断测试信号模拟器
  //   数码管输出
  //   数码管输出应该用寄存器锁存，否则显示数据只能一闪而过
  //   指令探针
  //   指令存储器
  //   指令字
  //   contents of rom_1 (hex, n*v repeats v):
  //   7d000113 100413 1f41993 41f9d993 433 c00913 800b13 140413 f47413 800293 100313 499993 89e9b3 1300533
  //   2200893 73 406282b3 fe0294e3 140413 f00f93 1f47433 1c41413 800293 100313 49d993 89e9b3 1300533
  //   2200893 73 406282b3 fe0294e3 1c45413 406b0b33 b0463 f95ff06f 2b3 fff2c293 1029293 fff2e293 500533
  //   2200893 73 f5dff06f 1112023 410113 a12023 410113 812023 410113 1312023 410113 1412023 410113 1512023
  //   410113 1612023 410113 40e073 100b13 300a13 100a93 1600433 441413 14469b3 1300533 2200893 73 fe0416e3
  //   415a0a33 fe0a10e3 40f073 ffc10113 12b03 ffc10113 12a83 ffc10113 12a03 ffc10113 12983 ffc10113 12403
  //   ffc10113 12503 ffc10113 12883 200073 1112023 410113 a12023 410113 812023 410113 1312023 410113
  //   1412023 410113 1512023 410113 1612023 410113 40e073 200b13 300a13 100a93 1600433 441413 14469b3
  //   1300533 2200893 73 fe0416e3 415a0a33 fe0a10e3 40f073 ffc10113 12b03 ffc10113 12a83 ffc10113 12a03
  //   ffc10113 12983 ffc10113 12403 ffc10113 12503 ffc10113 12883 200073 1112023 410113 a12023 410113
  //   812023 410113 1312023 410113 1412023 410113 1512023 410113 1612023 410113 40e073 300b13 300a13
  //   100a93 1600433 441413 14469b3 1300533 2200893 73 fe0416e3 415a0a33 fe0a10e3 40f073 ffc10113 12b03
  //   ffc10113 12a83 ffc10113 12a03 ffc10113 12983 ffc10113 12403 ffc10113 12503 ffc10113 12883 200073
  //   JAL
  //   JALR
  //   URET
  //   Beq
  //   Bne
  //   AluOP
  //   AluSrcB
  //   RegWrite
  //   MemToReg
  //   MemWrite
  //   为方便自动评测，需要输出PC，IR，寄存器堆写如数据RDin
  //   RAM写使能MemWrite、RAM写入数据MDin等信号
  //   数据存储器
  //   控制位
  //   暂停节拍，不能为0
  //   戳工具置1进入计数暂停模式，ctrl+k时钟自动运行到对应节拍暂停
  //   ctrl+k关闭时钟连续运行，将控制位置零，进入单步调试模式调试
  //   可计数暂停的时钟源
endmodule

module \封装正确性测试  (
);

  wire IR1, IR2, IR3, MemW, RegW;
  wire [31:0] EX_PC, ID_PC, IF_PC, IR, LED, MDin, MDinr, MEM_PC, PC, RDin, RDinr, WB_PC;

  \单周期RISC_V  \u_单周期risc_v_1  (
    .IR1(IR1), .IR2(IR2), .IR3(IR3), .RegWrite(RegW), .MemWrite(MemW), .PC(PC), .IR(IR), .RDin(RDin),
    .MDin(MDin), .LedData(LED));
  \气泡流水线  \u_气泡流水线_1  (
    .RegWrite(RegW), .MemWrite(MemW), .IF_PC(IF_PC), .ID_PC(ID_PC), .EX_PC(EX_PC), .M_PC(MEM_PC),
    .WB_PC(WB_PC), .RDin(RDinr), .MDin(MDinr), .LedData(LED));
  \单周期_单级中断  \u_单周期_单级中断_1  (
    .IR1(IR1), .IR2(IR2), .IR3(IR3), .RegWrite(RegW), .MemWrite(MemW), .PC(PC), .IR(IR), .RDin(RDin),
    .MDin(MDin), .LedData(LED));
  \理想流水线  \u_理想流水线_1  (
    .RegWrite(RegW), .MemWrite(MemW), .IF_PC(IF_PC), .ID_PC(ID_PC), .EX_PC(EX_PC), .M_PC(MEM_PC),
    .WB_PC(WB_PC), .RDin(RDinr), .MDin(MDinr), .LedData(LED));
  \重定向流水线  \u_重定向流水线_1  (
    .RegWrite(RegW), .MemWrite(MemW), .IF_PC(IF_PC), .ID_PC(ID_PC), .EX_PC(EX_PC), .M_PC(MEM_PC),
    .WB_PC(WB_PC), .RDin(RDinr), .MDin(MDinr), .LedData(LED));
  \单周期_多级中断  \u_单周期_多级中断_1  (
    .IR1(IR1), .IR2(IR2), .IR3(IR3), .RegWrite(RegW), .MemWrite(MemW), .PC(PC), .IR(IR), .RDin(RDin),
    .MDin(MDin), .LedData(LED));

  // Notes on the sheet:
  //   单周期封装测试
  //   气泡流水封装测试
  //   单周期+单级中断封装测试
  //   请检查上面封装有无位宽不匹配，引脚标签是否和连接的标签相对应，否则无法在educoder平台上正确测试
  //   理想流水封装测试
  //   重定向流水封装测试
  //   单周期+多级中断封装测试
endmodule

module IF_ID (
  input  [31:0] IRin,
  input  [31:0] PCin,
  input  clk,
  output [31:0] IRout,
  output [31:0] PCout
);

  Register #(.width(32), .trigger("rising"), .Select("low")) register_1 (
    .D(IRin), .Q(IRout), .clk(clk));  // open: en, clr
  Register #(.width(32), .trigger("rising"), .Select("low")) register_2 (
    .D(PCin), .Q(PCout), .clk(clk));  // open: en, clr
endmodule

module ID_EX (
  input  [6:0] signal,
  input  ecall,
  input  [2:0] JJU,
  input  [3:0] AluOp,
  input  [31:0] R1,
  input  [31:0] R2,
  input  [31:0] I_S_imm,
  input  [31:0] B_imm,
  input  [31:0] J_imm,
  input  [31:0] PCin,
  input  [4:0] WriteReg_num,
  input  sb,
  input  CLK,
  output [6:0] signalout,
  output ecallout,
  output [2:0] JJUout,
  output [3:0] AluOpout,
  output [31:0] R1_2,
  output [31:0] R2_2,
  output [31:0] I_S_imm_2,
  output [31:0] B_imm_2,
  output [31:0] J_imm_2,
  output [31:0] PCout,
  output [4:0] WriteReg_num_2,
  output sb_2
);

  Register #(.width(7), .trigger("rising"), .Select("low")) register_1 (
    .D(signal), .Q(signalout), .clk(CLK));  // open: en, clr
  Register #(.width(1), .trigger("rising"), .Select("low")) register_2 (
    .D(ecall), .Q(ecallout), .clk(CLK));  // open: en, clr
  Register #(.width(3), .trigger("rising"), .Select("low")) register_3 (
    .D(JJU), .Q(JJUout), .clk(CLK));  // open: en, clr
  Register #(.width(4), .trigger("rising"), .Select("low")) register_4 (
    .D(AluOp), .Q(AluOpout), .clk(CLK));  // open: en, clr
  Register #(.width(32), .trigger("rising"), .Select("low")) register_5 (.D(R1), .Q(R1_2), .clk(CLK));  // open: en, clr
  Register #(.width(32), .trigger("rising"), .Select("low")) register_6 (.D(R2), .Q(R2_2), .clk(CLK));  // open: en, clr
  Register #(.width(32), .trigger("rising"), .Select("low")) register_7 (
    .D(I_S_imm), .Q(I_S_imm_2), .clk(CLK));  // open: en, clr
  Register #(.width(32), .trigger("rising"), .Select("low")) register_8 (
    .D(B_imm), .Q(B_imm_2), .clk(CLK));  // open: en, clr
  Register #(.width(32), .trigger("rising"), .Select("low")) register_9 (
    .D(J_imm), .Q(J_imm_2), .clk(CLK));  // open: en, clr
  Register #(.width(32), .trigger("rising"), .Select("low")) register_10 (
    .D(PCin), .Q(PCout), .clk(CLK));  // open: en, clr
  Register #(.width(5), .trigger("rising"), .Select("low")) register_11 (
    .D(WriteReg_num), .Q(WriteReg_num_2), .clk(CLK));  // open: en, clr
  Register #(.width(1), .trigger("rising"), .Select("low")) register_12 (.D(sb), .Q(sb_2), .clk(CLK));  // open: en, clr
endmodule

module EX_MEM (
  input  JALin,
  input  JALRin,
  input  RegWrite,
  input  MemToReg,
  input  sb,
  input  MemWrite,
  input  [31:0] Write_Data,
  input  [31:0] ALU_Result,
  input  [4:0] WriteReg_num,
  input  [31:0] PCin,
  input  haltin,
  input  CLK,
  output JALout,
  output JALRout,
  output RegWrite_2,
  output MemToReg_2,
  output sb_2,
  output MemWrite_2,
  output [31:0] Write_Data_2,
  output [31:0] ALU_Result_2,
  output [4:0] WriteReg_num_2,
  output [31:0] PCout,
  output haltout
);

  Register #(.width(1), .trigger("rising"), .Select("low")) register_1 (
    .D(JALin), .Q(JALout), .clk(CLK));  // open: en, clr
  Register #(.width(1), .trigger("rising"), .Select("low")) register_2 (
    .D(JALRin), .Q(JALRout), .clk(CLK));  // open: en, clr
  Register #(.width(1), .trigger("rising"), .Select("low")) register_3 (
    .D(RegWrite), .Q(RegWrite_2), .clk(CLK));  // open: en, clr
  Register #(.width(1), .trigger("rising"), .Select("low")) register_4 (
    .D(MemToReg), .Q(MemToReg_2), .clk(CLK));  // open: en, clr
  Register #(.width(1), .trigger("rising"), .Select("low")) register_5 (.D(sb), .Q(sb_2), .clk(CLK));  // open: en, clr
  Register #(.width(1), .trigger("rising"), .Select("low")) register_6 (
    .D(MemWrite), .Q(MemWrite_2), .clk(CLK));  // open: en, clr
  Register #(.width(32), .trigger("rising"), .Select("low")) register_7 (
    .D(Write_Data), .Q(Write_Data_2), .clk(CLK));  // open: en, clr
  Register #(.width(32), .trigger("rising"), .Select("low")) register_8 (
    .D(ALU_Result), .Q(ALU_Result_2), .clk(CLK));  // open: en, clr
  Register #(.width(5), .trigger("rising"), .Select("low")) register_9 (
    .D(WriteReg_num), .Q(WriteReg_num_2), .clk(CLK));  // open: en, clr
  Register #(.width(32), .trigger("rising"), .Select("low")) register_10 (
    .D(PCin), .Q(PCout), .clk(CLK));  // open: en, clr
  Register #(.width(1), .trigger("rising"), .Select("low")) register_11 (
    .D(haltin), .Q(haltout), .clk(CLK));  // open: en, clr
endmodule

module MEM_WB (
  input  halt,
  input  JAL,
  input  JALR,
  input  RegWrite,
  input  MemToReg,
  input  [31:0] ALU_Result,
  input  [31:0] MemData,
  input  [4:0] WriteReg_num,
  input  [31:0] PC,
  input  CLK,
  output haltout,
  output JALout,
  output JALRout,
  output RegWrite_2,
  output MemToReg_2,
  output [31:0] ALU_Result_2,
  output [31:0] MemData_2,
  output [4:0] WriteReg_num_2,
  output [31:0] PCout
);

  Register #(.width(1), .trigger("rising"), .Select("low")) register_1 (
    .D(halt), .Q(haltout), .clk(CLK));  // open: en, clr
  Register #(.width(1), .trigger("rising"), .Select("low")) register_2 (
    .D(JAL), .Q(JALout), .clk(CLK));  // open: en, clr
  Register #(.width(1), .trigger("rising"), .Select("low")) register_3 (
    .D(JALR), .Q(JALRout), .clk(CLK));  // open: en, clr
  Register #(.width(1), .trigger("rising"), .Select("low")) register_4 (
    .D(RegWrite), .Q(RegWrite_2), .clk(CLK));  // open: en, clr
  Register #(.width(1), .trigger("rising"), .Select("low")) register_5 (
    .D(MemToReg), .Q(MemToReg_2), .clk(CLK));  // open: en, clr
  Register #(.width(32), .trigger("rising"), .Select("low")) register_6 (
    .D(ALU_Result), .Q(ALU_Result_2), .clk(CLK));  // open: en, clr
  Register #(.width(32), .trigger("rising"), .Select("low")) register_7 (
    .D(MemData), .Q(MemData_2), .clk(CLK));  // open: en, clr
  Register #(.width(5), .trigger("rising"), .Select("low")) register_8 (
    .D(WriteReg_num), .Q(WriteReg_num_2), .clk(CLK));  // open: en, clr
  Register #(.width(32), .trigger("rising"), .Select("low")) register_9 (
    .D(PC), .Q(PCout), .clk(CLK));  // open: en, clr
endmodule

module IF_ID2 (
  input  [31:0] IRin,
  input  [31:0] PCin,
  input  clk,
  input  bubble,
  input  stop,
  output [31:0] IRout,
  output [31:0] PCout
);

  wire [31:0] multiplexer_1_out, multiplexer_2_out;

  Pull_Resistor #(.pull(0)) pull_resistor_1 (.node(bubble));
  Multiplexer #(.select(1), .width(32), .disabled("Z"), .enable("false")) multiplexer_1 (
    .in0(IRin), .in1({32{1'b0}}), .out(multiplexer_1_out), .sel(bubble));
  Multiplexer #(.select(1), .width(32), .disabled("Z"), .enable("false")) multiplexer_2 (
    .in0(PCin), .in1({32{1'b0}}), .out(multiplexer_2_out), .sel(bubble));
  Register #(.width(32), .trigger("rising"), .Select("low")) register_1 (
    .D(multiplexer_1_out), .en(stop), .Q(IRout), .clk(clk));  // open: clr
  Register #(.width(32), .trigger("rising"), .Select("low")) register_2 (
    .D(multiplexer_2_out), .en(stop), .Q(PCout), .clk(clk));  // open: clr
  Pull_Resistor #(.pull(0)) pull_resistor_2 (.node(stop));
endmodule

module ID_EX2 (
  input  [6:0] signal,
  input  ecall,
  input  [2:0] JJU,
  input  [3:0] AluOp,
  input  [31:0] R1,
  input  [31:0] R2,
  input  [31:0] I_S_imm,
  input  [31:0] B_imm,
  input  [31:0] J_imm,
  input  [31:0] PCin,
  input  [4:0] WriteReg_num,
  input  CLK,
  input  sb,
  input  bubble,
  input  stop,
  output [6:0] signalout,
  output ecallout,
  output [2:0] JJUout,
  output [3:0] AluOpout,
  output [31:0] R1_2,
  output [31:0] R2_2,
  output [31:0] I_S_imm_2,
  output [31:0] B_imm_2,
  output [31:0] J_imm_2,
  output [31:0] PCout,
  output [4:0] WriteReg_num_2,
  output sb_2
);

  wire multiplexer_2_out, multiplexer_12_out;
  wire [2:0] multiplexer_3_out;
  wire [3:0] multiplexer_4_out;
  wire [4:0] multiplexer_11_out;
  wire [6:0] multiplexer_1_out;
  wire [31:0] multiplexer_5_out, multiplexer_6_out, multiplexer_7_out, multiplexer_8_out, multiplexer_9_out,
       multiplexer_10_out;

  Multiplexer #(.select(1), .width(7), .disabled("Z"), .enable("false")) multiplexer_1 (
    .in0(signal), .in1({7{1'b0}}), .out(multiplexer_1_out), .sel(bubble));
  Multiplexer #(.select(1), .width(1), .disabled("Z"), .enable("false")) multiplexer_2 (
    .in0(ecall), .in1(1'b0), .out(multiplexer_2_out), .sel(bubble));
  Multiplexer #(.select(1), .width(3), .disabled("Z"), .enable("false")) multiplexer_3 (
    .in0(JJU), .in1(3'b000), .out(multiplexer_3_out), .sel(bubble));
  Multiplexer #(.select(1), .width(4), .disabled("Z"), .enable("false")) multiplexer_4 (
    .in0(AluOp), .in1(4'b0000), .out(multiplexer_4_out), .sel(bubble));
  Multiplexer #(.select(1), .width(32), .disabled("Z"), .enable("false")) multiplexer_5 (
    .in0(R1), .in1({32{1'b0}}), .out(multiplexer_5_out), .sel(bubble));
  Multiplexer #(.select(1), .width(32), .disabled("Z"), .enable("false")) multiplexer_6 (
    .in0(R2), .in1({32{1'b0}}), .out(multiplexer_6_out), .sel(bubble));
  Multiplexer #(.select(1), .width(32), .disabled("Z"), .enable("false")) multiplexer_7 (
    .in0(I_S_imm), .in1({32{1'b0}}), .out(multiplexer_7_out), .sel(bubble));
  Multiplexer #(.select(1), .width(32), .disabled("Z"), .enable("false")) multiplexer_8 (
    .in0(B_imm), .in1({32{1'b0}}), .out(multiplexer_8_out), .sel(bubble));
  Multiplexer #(.select(1), .width(32), .disabled("Z"), .enable("false")) multiplexer_9 (
    .in0(J_imm), .in1({32{1'b0}}), .out(multiplexer_9_out), .sel(bubble));
  Multiplexer #(.select(1), .width(32), .disabled("Z"), .enable("false")) multiplexer_10 (
    .in0(PCin), .in1({32{1'b0}}), .out(multiplexer_10_out), .sel(bubble));
  Multiplexer #(.select(1), .width(5), .disabled("Z"), .enable("false")) multiplexer_11 (
    .in0(WriteReg_num), .in1({5{1'b0}}), .out(multiplexer_11_out), .sel(bubble));
  Multiplexer #(.select(1), .width(1), .disabled("Z"), .enable("false")) multiplexer_12 (
    .in0(sb), .in1(1'b0), .out(multiplexer_12_out), .sel(bubble));
  Pull_Resistor #(.pull(0)) pull_resistor_1 (.node(bubble));
  Register #(.width(7), .trigger("rising"), .Select("low")) register_1 (
    .D(multiplexer_1_out), .en(stop), .Q(signalout), .clk(CLK));  // open: clr
  Register #(.width(1), .trigger("rising"), .Select("low")) register_2 (
    .D(multiplexer_2_out), .en(stop), .Q(ecallout), .clk(CLK));  // open: clr
  Register #(.width(3), .trigger("rising"), .Select("low")) register_3 (
    .D(multiplexer_3_out), .en(stop), .Q(JJUout), .clk(CLK));  // open: clr
  Register #(.width(4), .trigger("rising"), .Select("low")) register_4 (
    .D(multiplexer_4_out), .en(stop), .Q(AluOpout), .clk(CLK));  // open: clr
  Register #(.width(32), .trigger("rising"), .Select("low")) register_5 (
    .D(multiplexer_5_out), .en(stop), .Q(R1_2), .clk(CLK));  // open: clr
  Register #(.width(32), .trigger("rising"), .Select("low")) register_6 (
    .D(multiplexer_6_out), .en(stop), .Q(R2_2), .clk(CLK));  // open: clr
  Register #(.width(32), .trigger("rising"), .Select("low")) register_7 (
    .D(multiplexer_7_out), .en(stop), .Q(I_S_imm_2), .clk(CLK));  // open: clr
  Register #(.width(32), .trigger("rising"), .Select("low")) register_8 (
    .D(multiplexer_8_out), .en(stop), .Q(B_imm_2), .clk(CLK));  // open: clr
  Register #(.width(32), .trigger("rising"), .Select("low")) register_9 (
    .D(multiplexer_9_out), .en(stop), .Q(J_imm_2), .clk(CLK));  // open: clr
  Register #(.width(32), .trigger("rising"), .Select("low")) register_10 (
    .D(multiplexer_10_out), .en(stop), .Q(PCout), .clk(CLK));  // open: clr
  Register #(.width(5), .trigger("rising"), .Select("low")) register_11 (
    .D(multiplexer_11_out), .en(stop), .Q(WriteReg_num_2), .clk(CLK));  // open: clr
  Register #(.width(1), .trigger("rising"), .Select("low")) register_12 (
    .D(multiplexer_12_out), .en(stop), .Q(sb_2), .clk(CLK));  // open: clr
  Pull_Resistor #(.pull(0)) pull_resistor_2 (.node(stop));
endmodule

module EX_MEM2 (
  input  JALin,
  input  JALRin,
  input  RegWrite,
  input  MemToReg,
  input  MemWrite,
  input  [31:0] Write_Data,
  input  [31:0] ALU_Result,
  input  sb,
  input  [4:0] WriteReg_num,
  input  [31:0] PCin,
  input  haltin,
  input  CLK,
  input  bubble,
  input  stop,
  output JALout,
  output JALRout,
  output RegWrite_2,
  output MemToReg_2,
  output MemWrite_2,
  output [31:0] Write_Data_2,
  output [31:0] ALU_Result_2,
  output sb_2,
  output [4:0] WriteReg_num_2,
  output [31:0] PCout,
  output haltout
);

  wire multiplexer_1_out, multiplexer_2_out, multiplexer_3_out, multiplexer_4_out, multiplexer_5_out,
       multiplexer_6_out, multiplexer_11_out;
  wire [4:0] multiplexer_9_out;
  wire [31:0] multiplexer_7_out, multiplexer_8_out, multiplexer_10_out;

  Pull_Resistor #(.pull(0)) pull_resistor_1 (.node(bubble));
  Multiplexer #(.select(1), .width(1), .disabled("Z"), .enable("false")) multiplexer_1 (
    .in0(sb), .in1(1'b0), .out(multiplexer_1_out), .sel(bubble));
  Multiplexer #(.select(1), .width(1), .disabled("Z"), .enable("false")) multiplexer_2 (
    .in0(JALin), .in1(1'b0), .out(multiplexer_2_out), .sel(bubble));
  Multiplexer #(.select(1), .width(1), .disabled("Z"), .enable("false")) multiplexer_3 (
    .in0(JALRin), .in1(1'b0), .out(multiplexer_3_out), .sel(bubble));
  Multiplexer #(.select(1), .width(1), .disabled("Z"), .enable("false")) multiplexer_4 (
    .in0(RegWrite), .in1(1'b0), .out(multiplexer_4_out), .sel(bubble));
  Multiplexer #(.select(1), .width(1), .disabled("Z"), .enable("false")) multiplexer_5 (
    .in0(MemToReg), .in1(1'b0), .out(multiplexer_5_out), .sel(bubble));
  Multiplexer #(.select(1), .width(1), .disabled("Z"), .enable("false")) multiplexer_6 (
    .in0(MemWrite), .in1(1'b0), .out(multiplexer_6_out), .sel(bubble));
  Multiplexer #(.select(1), .width(32), .disabled("Z"), .enable("false")) multiplexer_7 (
    .in0(Write_Data), .in1({32{1'b0}}), .out(multiplexer_7_out), .sel(bubble));
  Multiplexer #(.select(1), .width(32), .disabled("Z"), .enable("false")) multiplexer_8 (
    .in0(ALU_Result), .in1({32{1'b0}}), .out(multiplexer_8_out), .sel(bubble));
  Multiplexer #(.select(1), .width(5), .disabled("Z"), .enable("false")) multiplexer_9 (
    .in0(WriteReg_num), .in1({5{1'b0}}), .out(multiplexer_9_out), .sel(bubble));
  Multiplexer #(.select(1), .width(32), .disabled("Z"), .enable("false")) multiplexer_10 (
    .in0(PCin), .in1({32{1'b0}}), .out(multiplexer_10_out), .sel(bubble));
  Multiplexer #(.select(1), .width(1), .disabled("Z"), .enable("false")) multiplexer_11 (
    .in0(haltin), .in1(1'b0), .out(multiplexer_11_out), .sel(bubble));
  Pull_Resistor #(.pull(0)) pull_resistor_2 (.node(stop));
  Register #(.width(1), .trigger("rising"), .Select("low")) register_1 (
    .D(multiplexer_1_out), .en(stop), .Q(sb_2), .clk(CLK));  // open: clr
  Register #(.width(1), .trigger("rising"), .Select("low")) register_2 (
    .D(multiplexer_2_out), .en(stop), .Q(JALout), .clk(CLK));  // open: clr
  Register #(.width(1), .trigger("rising"), .Select("low")) register_3 (
    .D(multiplexer_3_out), .en(stop), .Q(JALRout), .clk(CLK));  // open: clr
  Register #(.width(1), .trigger("rising"), .Select("low")) register_4 (
    .D(multiplexer_4_out), .en(stop), .Q(RegWrite_2), .clk(CLK));  // open: clr
  Register #(.width(1), .trigger("rising"), .Select("low")) register_5 (
    .D(multiplexer_5_out), .en(stop), .Q(MemToReg_2), .clk(CLK));  // open: clr
  Register #(.width(1), .trigger("rising"), .Select("low")) register_6 (
    .D(multiplexer_6_out), .en(stop), .Q(MemWrite_2), .clk(CLK));  // open: clr
  Register #(.width(32), .trigger("rising"), .Select("low")) register_7 (
    .D(multiplexer_7_out), .en(stop), .Q(Write_Data_2), .clk(CLK));  // open: clr
  Register #(.width(32), .trigger("rising"), .Select("low")) register_8 (
    .D(multiplexer_8_out), .en(stop), .Q(ALU_Result_2), .clk(CLK));  // open: clr
  Register #(.width(5), .trigger("rising"), .Select("low")) register_9 (
    .D(multiplexer_9_out), .en(stop), .Q(WriteReg_num_2), .clk(CLK));  // open: clr
  Register #(.width(32), .trigger("rising"), .Select("low")) register_10 (
    .D(multiplexer_10_out), .en(stop), .Q(PCout), .clk(CLK));  // open: clr
  Register #(.width(1), .trigger("rising"), .Select("low")) register_11 (
    .D(multiplexer_11_out), .en(stop), .Q(haltout), .clk(CLK));  // open: clr
endmodule

module MEM_WB2 (
  input  halt,
  input  JAL,
  input  JALR,
  input  RegWrite,
  input  MemToReg,
  input  [31:0] ALU_Result,
  input  [31:0] MemData,
  input  [4:0] WriteReg_num,
  input  [31:0] PC,
  input  CLK,
  input  bubble,
  input  stop,
  output haltout,
  output JALout,
  output JALRout,
  output RegWrite_2,
  output MemToReg_2,
  output [31:0] ALU_Result_2,
  output [31:0] MemData_2,
  output [4:0] WriteReg_num_2,
  output [31:0] PCout
);

  wire multiplexer_1_out, multiplexer_2_out, multiplexer_3_out, multiplexer_4_out, multiplexer_5_out;
  wire [4:0] multiplexer_8_out;
  wire [31:0] multiplexer_6_out, multiplexer_7_out, multiplexer_9_out;

  Multiplexer #(.select(1), .width(1), .disabled("Z"), .enable("false")) multiplexer_1 (
    .in0(halt), .in1(1'b0), .out(multiplexer_1_out), .sel(bubble));
  Multiplexer #(.select(1), .width(1), .disabled("Z"), .enable("false")) multiplexer_2 (
    .in0(JAL), .in1(1'b0), .out(multiplexer_2_out), .sel(bubble));
  Multiplexer #(.select(1), .width(1), .disabled("Z"), .enable("false")) multiplexer_3 (
    .in0(JALR), .in1(1'b0), .out(multiplexer_3_out), .sel(bubble));
  Multiplexer #(.select(1), .width(1), .disabled("Z"), .enable("false")) multiplexer_4 (
    .in0(RegWrite), .in1(1'b0), .out(multiplexer_4_out), .sel(bubble));
  Multiplexer #(.select(1), .width(1), .disabled("Z"), .enable("false")) multiplexer_5 (
    .in0(MemToReg), .in1(1'b0), .out(multiplexer_5_out), .sel(bubble));
  Multiplexer #(.select(1), .width(32), .disabled("Z"), .enable("false")) multiplexer_6 (
    .in0(ALU_Result), .in1({32{1'b0}}), .out(multiplexer_6_out), .sel(bubble));
  Multiplexer #(.select(1), .width(32), .disabled("Z"), .enable("false")) multiplexer_7 (
    .in0(MemData), .in1({32{1'b0}}), .out(multiplexer_7_out), .sel(bubble));
  Multiplexer #(.select(1), .width(5), .disabled("Z"), .enable("false")) multiplexer_8 (
    .in0(WriteReg_num), .in1({5{1'b0}}), .out(multiplexer_8_out), .sel(bubble));
  Multiplexer #(.select(1), .width(32), .disabled("Z"), .enable("false")) multiplexer_9 (
    .in0(PC), .in1({32{1'b0}}), .out(multiplexer_9_out), .sel(bubble));
  Pull_Resistor #(.pull(0)) pull_resistor_1 (.node(bubble));
  Register #(.width(1), .trigger("rising"), .Select("low")) register_1 (
    .D(multiplexer_1_out), .en(stop), .Q(haltout), .clk(CLK));  // open: clr
  Register #(.width(1), .trigger("rising"), .Select("low")) register_2 (
    .D(multiplexer_2_out), .en(stop), .Q(JALout), .clk(CLK));  // open: clr
  Register #(.width(1), .trigger("rising"), .Select("low")) register_3 (
    .D(multiplexer_3_out), .en(stop), .Q(JALRout), .clk(CLK));  // open: clr
  Register #(.width(1), .trigger("rising"), .Select("low")) register_4 (
    .D(multiplexer_4_out), .en(stop), .Q(RegWrite_2), .clk(CLK));  // open: clr
  Register #(.width(1), .trigger("rising"), .Select("low")) register_5 (
    .D(multiplexer_5_out), .en(stop), .Q(MemToReg_2), .clk(CLK));  // open: clr
  Register #(.width(32), .trigger("rising"), .Select("low")) register_6 (
    .D(multiplexer_6_out), .en(stop), .Q(ALU_Result_2), .clk(CLK));  // open: clr
  Register #(.width(32), .trigger("rising"), .Select("low")) register_7 (
    .D(multiplexer_7_out), .en(stop), .Q(MemData_2), .clk(CLK));  // open: clr
  Register #(.width(5), .trigger("rising"), .Select("low")) register_8 (
    .D(multiplexer_8_out), .en(stop), .Q(WriteReg_num_2), .clk(CLK));  // open: clr
  Register #(.width(32), .trigger("rising"), .Select("low")) register_9 (
    .D(multiplexer_9_out), .en(stop), .Q(PCout), .clk(CLK));  // open: clr
  Pull_Resistor #(.pull(0)) pull_resistor_2 (.node(stop));
endmodule

module DataHazzard (
  input  RsUsed,
  input  RtUsed,
  input  EXRW,
  input  MEMRW,
  input  [4:0] rs,
  input  [4:0] rt,
  input  [4:0] exw,
  input  [4:0] memw,
  output DH
);

  wire and_1_out, and_2_out, and_3_out, and_4_out, comparator_1_eq, comparator_2_eq, comparator_3_eq,
       comparator_4_eq, comparator_5_eq, comparator_6_eq, not_1_out, not_2_out;

  Comparator #(.width(5), .mode("twosComplement")) comparator_1 (
    .a(rs), .b({5{1'b0}}), .eq(comparator_1_eq));  // open: gt, lt
  Comparator #(.width(5), .mode("twosComplement")) comparator_2 (
    .a({5{1'b0}}), .b(rt), .eq(comparator_2_eq));  // open: gt, lt
  Comparator #(.width(5), .mode("twosComplement")) comparator_3 (
    .a(rs), .b(exw), .eq(comparator_3_eq));  // open: gt, lt
  Comparator #(.width(5), .mode("twosComplement")) comparator_4 (
    .a(rs), .b(memw), .eq(comparator_4_eq));  // open: gt, lt
  Comparator #(.width(5), .mode("twosComplement")) comparator_5 (
    .a(rt), .b(exw), .eq(comparator_5_eq));  // open: gt, lt
  Comparator #(.width(5), .mode("twosComplement")) comparator_6 (
    .a(rt), .b(memw), .eq(comparator_6_eq));  // open: gt, lt
  not not_1 (not_1_out, comparator_1_eq);
  not not_2 (not_2_out, comparator_2_eq);
  and and_1 (and_1_out, RsUsed, not_1_out, comparator_3_eq, EXRW);
  and and_2 (and_2_out, EXRW, RtUsed, not_2_out, comparator_5_eq);
  and and_3 (and_3_out, not_1_out, MEMRW, RsUsed, comparator_4_eq);
  and and_4 (and_4_out, MEMRW, comparator_6_eq, not_2_out, RtUsed);
  or or_1 (DH, and_1_out, and_2_out, and_3_out, and_4_out);
endmodule

module ID_EX3 (
  input  sb,
  input  [6:0] signal,
  input  ecall,
  input  [2:0] JJU,
  input  [3:0] AluOp,
  input  [31:0] R1,
  input  [31:0] R2,
  input  [31:0] I_S_imm,
  input  [31:0] B_imm,
  input  [31:0] J_imm,
  input  [31:0] PCin,
  input  [4:0] WriteReg_num,
  input  [1:0] RsForward,
  input  [1:0] RtForward,
  input  CLK,
  input  bubble,
  input  stop,
  output sb_2,
  output [6:0] signalout,
  output ecallout,
  output [2:0] JJUout,
  output [3:0] AluOpout,
  output [31:0] R1_2,
  output [31:0] R2_2,
  output [31:0] I_S_imm_2,
  output [31:0] B_imm_2,
  output [31:0] J_imm_2,
  output [31:0] PCout,
  output [4:0] WriteReg_num_2,
  output [1:0] RsForward_2,
  output [1:0] RtForward_2
);

  wire multiplexer_1_out, multiplexer_3_out;
  wire [1:0] multiplexer_13_out, multiplexer_14_out;
  wire [2:0] multiplexer_4_out;
  wire [3:0] multiplexer_5_out;
  wire [4:0] multiplexer_12_out;
  wire [6:0] multiplexer_2_out;
  wire [31:0] multiplexer_6_out, multiplexer_7_out, multiplexer_8_out, multiplexer_9_out, multiplexer_10_out,
       multiplexer_11_out;

  Multiplexer #(.select(1), .width(1), .disabled("Z"), .enable("false")) multiplexer_1 (
    .in0(sb), .in1(1'b0), .out(multiplexer_1_out), .sel(bubble));
  Multiplexer #(.select(1), .width(7), .disabled("Z"), .enable("false")) multiplexer_2 (
    .in0(signal), .in1({7{1'b0}}), .out(multiplexer_2_out), .sel(bubble));
  Multiplexer #(.select(1), .width(1), .disabled("Z"), .enable("false")) multiplexer_3 (
    .in0(ecall), .in1(1'b0), .out(multiplexer_3_out), .sel(bubble));
  Multiplexer #(.select(1), .width(3), .disabled("Z"), .enable("false")) multiplexer_4 (
    .in0(JJU), .in1(3'b000), .out(multiplexer_4_out), .sel(bubble));
  Multiplexer #(.select(1), .width(4), .disabled("Z"), .enable("false")) multiplexer_5 (
    .in0(AluOp), .in1(4'b0000), .out(multiplexer_5_out), .sel(bubble));
  Multiplexer #(.select(1), .width(32), .disabled("Z"), .enable("false")) multiplexer_6 (
    .in0(R1), .in1({32{1'b0}}), .out(multiplexer_6_out), .sel(bubble));
  Multiplexer #(.select(1), .width(32), .disabled("Z"), .enable("false")) multiplexer_7 (
    .in0(R2), .in1({32{1'b0}}), .out(multiplexer_7_out), .sel(bubble));
  Multiplexer #(.select(1), .width(32), .disabled("Z"), .enable("false")) multiplexer_8 (
    .in0(I_S_imm), .in1({32{1'b0}}), .out(multiplexer_8_out), .sel(bubble));
  Multiplexer #(.select(1), .width(32), .disabled("Z"), .enable("false")) multiplexer_9 (
    .in0(B_imm), .in1({32{1'b0}}), .out(multiplexer_9_out), .sel(bubble));
  Multiplexer #(.select(1), .width(32), .disabled("Z"), .enable("false")) multiplexer_10 (
    .in0(J_imm), .in1({32{1'b0}}), .out(multiplexer_10_out), .sel(bubble));
  Multiplexer #(.select(1), .width(32), .disabled("Z"), .enable("false")) multiplexer_11 (
    .in0(PCin), .in1({32{1'b0}}), .out(multiplexer_11_out), .sel(bubble));
  Multiplexer #(.select(1), .width(5), .disabled("Z"), .enable("false")) multiplexer_12 (
    .in0(WriteReg_num), .in1({5{1'b0}}), .out(multiplexer_12_out), .sel(bubble));
  Multiplexer #(.select(1), .width(2), .disabled("Z"), .enable("false")) multiplexer_13 (
    .in0(RsForward), .in1(2'b00), .out(multiplexer_13_out), .sel(bubble));
  Multiplexer #(.select(1), .width(2), .disabled("Z"), .enable("false")) multiplexer_14 (
    .in0(RtForward), .in1(2'b00), .out(multiplexer_14_out), .sel(bubble));
  Pull_Resistor #(.pull(0)) pull_resistor_1 (.node(bubble));
  Register #(.width(1), .trigger("rising"), .Select("low")) register_1 (
    .D(multiplexer_1_out), .en(stop), .Q(sb_2), .clk(CLK));  // open: clr
  Register #(.width(7), .trigger("rising"), .Select("low")) register_2 (
    .D(multiplexer_2_out), .en(stop), .Q(signalout), .clk(CLK));  // open: clr
  Register #(.width(1), .trigger("rising"), .Select("low")) register_3 (
    .D(multiplexer_3_out), .en(stop), .Q(ecallout), .clk(CLK));  // open: clr
  Register #(.width(3), .trigger("rising"), .Select("low")) register_4 (
    .D(multiplexer_4_out), .en(stop), .Q(JJUout), .clk(CLK));  // open: clr
  Register #(.width(4), .trigger("rising"), .Select("low")) register_5 (
    .D(multiplexer_5_out), .en(stop), .Q(AluOpout), .clk(CLK));  // open: clr
  Register #(.width(32), .trigger("rising"), .Select("low")) register_6 (
    .D(multiplexer_6_out), .en(stop), .Q(R1_2), .clk(CLK));  // open: clr
  Register #(.width(32), .trigger("rising"), .Select("low")) register_7 (
    .D(multiplexer_7_out), .en(stop), .Q(R2_2), .clk(CLK));  // open: clr
  Register #(.width(32), .trigger("rising"), .Select("low")) register_8 (
    .D(multiplexer_8_out), .en(stop), .Q(I_S_imm_2), .clk(CLK));  // open: clr
  Register #(.width(32), .trigger("rising"), .Select("low")) register_9 (
    .D(multiplexer_9_out), .en(stop), .Q(B_imm_2), .clk(CLK));  // open: clr
  Register #(.width(32), .trigger("rising"), .Select("low")) register_10 (
    .D(multiplexer_10_out), .en(stop), .Q(J_imm_2), .clk(CLK));  // open: clr
  Register #(.width(32), .trigger("rising"), .Select("low")) register_11 (
    .D(multiplexer_11_out), .en(stop), .Q(PCout), .clk(CLK));  // open: clr
  Register #(.width(5), .trigger("rising"), .Select("low")) register_12 (
    .D(multiplexer_12_out), .en(stop), .Q(WriteReg_num_2), .clk(CLK));  // open: clr
  Register #(.width(2), .trigger("rising"), .Select("low")) register_13 (
    .D(multiplexer_13_out), .en(stop), .Q(RsForward_2), .clk(CLK));  // open: clr
  Register #(.width(2), .trigger("rising"), .Select("low")) register_14 (
    .D(multiplexer_14_out), .en(stop), .Q(RtForward_2), .clk(CLK));  // open: clr
  Pull_Resistor #(.pull(0)) pull_resistor_2 (.node(stop));
endmodule

module RAM (
  input  Mode,
  input  [11:0] \字节地址 ,
  input  [31:0] Din,
  input  CLK,
  input  id,
  input  str,
  output [31:0] Dout
);

  wire _0, _1, and_1_out, and_2_out, and_3_out, and_4_out, and_5_out, and_6_out, and_7_out, and_8_out,
       comparator_1_eq, comparator_2_eq, comparator_3_eq, comparator_4_eq, W0, W1, W2, W3;
  wire [7:0] byte0, byte1, byte2, byte3, d0, d1, d2, d3, multiplexer_5_out;
  wire [31:0] bit_extender_1_out;

  and and_1 (and_1_out, W0, str);
  RAM_part #(.addrWidth(10), .dataWidth(8), .bus("separate"), .Select("high")) ram_1 (
    .addr(\字节地址 [11:2]), .din(d0), .data(byte0), .str(and_1_out), .sel(1'b1), .clk(CLK), .ld(id));  // open: clr
  Multiplexer #(.select(1), .width(8), .disabled("Z"), .enable("false")) multiplexer_1 (
    .in0(Din[7:0]), .in1(Din[7:0]), .out(d0), .sel(Mode));
  Multiplexer #(.select(1), .width(8), .disabled("Z"), .enable("false")) multiplexer_2 (
    .in0(Din[23:16]), .in1(Din[7:0]), .out(d2), .sel(Mode));
  and and_2 (and_2_out, W1, str);
  RAM_part #(.addrWidth(10), .dataWidth(8), .bus("separate"), .Select("high")) ram_2 (
    .addr(\字节地址 [11:2]), .din(d1), .data(byte1), .str(and_2_out), .sel(1'b1), .clk(CLK), .ld(id));  // open: clr
  and and_3 (and_3_out, W2, str);
  Multiplexer #(.select(1), .width(8), .disabled("Z"), .enable("false")) multiplexer_3 (
    .in0(Din[15:8]), .in1(Din[7:0]), .out(d1), .sel(Mode));
  Multiplexer #(.select(1), .width(8), .disabled("Z"), .enable("false")) multiplexer_4 (
    .in0(Din[31:24]), .in1(Din[7:0]), .out(d3), .sel(Mode));
  RAM_part #(.addrWidth(10), .dataWidth(8), .bus("separate"), .Select("high")) ram_3 (
    .addr(\字节地址 [11:2]), .din(d2), .data(byte2), .str(and_3_out), .sel(1'b1), .clk(CLK), .ld(id));  // open: clr
  and and_4 (and_4_out, W3, str);
  Demultiplexer #(.select(1), .width(1), .tristate("false"), .disabled("Z"), .enable("false")) demultiplexer_1 (
    .out0(_0), .out1(_1), .in(1'b1), .sel(Mode));
  RAM_part #(.addrWidth(10), .dataWidth(8), .bus("separate"), .Select("high")) ram_4 (
    .addr(\字节地址 [11:2]), .din(d3), .data(byte3), .str(and_4_out), .sel(1'b1), .clk(CLK), .ld(id));  // open: clr
  Comparator #(.width(2), .mode("twosComplement")) comparator_1 (
    .a(\字节地址 [1:0]), .b(2'b00), .eq(comparator_1_eq));  // open: gt, lt
  Comparator #(.width(2), .mode("twosComplement")) comparator_2 (
    .a(\字节地址 [1:0]), .b(2'b10), .eq(comparator_2_eq));  // open: gt, lt
  Multiplexer #(.select(2), .width(8), .disabled("Z"), .enable("false")) multiplexer_5 (
    .in0(byte0), .in1(byte1), .in2(byte2), .in3(byte3), .out(multiplexer_5_out), .sel(\字节地址 [1:0]));
  and and_5 (and_5_out, _1, comparator_1_eq);
  and and_6 (and_6_out, _1, comparator_2_eq);
  assign bit_extender_1_out = {{24{1'b0}}, multiplexer_5_out};  // Bit_Extender bit_extender_1
  or or_1 (W0, _0, and_5_out);
  or or_2 (W2, _0, and_6_out);
  Multiplexer #(.select(1), .width(32), .disabled("Z"), .enable("false")) multiplexer_6 (
    .in0({byte3, byte2, byte1, byte0}), .in1(bit_extender_1_out), .out(Dout), .sel(Mode));
  Comparator #(.width(2), .mode("twosComplement")) comparator_3 (
    .a(\字节地址 [1:0]), .b(2'b01), .eq(comparator_3_eq));  // open: gt, lt
  Comparator #(.width(2), .mode("twosComplement")) comparator_4 (
    .a(\字节地址 [1:0]), .b(2'b11), .eq(comparator_4_eq));  // open: gt, lt
  or or_3 (W1, _0, and_7_out);
  and and_7 (and_7_out, _1, comparator_3_eq);
  or or_4 (W3, _0, and_8_out);
  and and_8 (and_8_out, _1, comparator_4_eq);

  // Notes on the sheet:
  //   输入引脚区
endmodule

module \中断响应  (
  input  clk,
  input  \_1号 ,
  input  next,
  input  [1:0] nextid,
  input  \_2号 ,
  input  \_3号 ,
  input  \开中断 ,
  input  \关中断 ,
  output \中断响应 
);

  wire and_1_out, and_2_out, and_3_out, and_4_out, c0, c1, c2, c3, d_ff_1_q, d_ff_2_q, d_ff_3_q, d_ff_4_q,
       IR1_2_q, IR1_q, IR2_q, multiplexer_1_out, not_1_out, or_1_out, or_2_out, or_3_out, or_4_out;

  Multiplexer #(.select(1), .width(1), .disabled("Z"), .enable("false")) multiplexer_1 (
    .in0(d_ff_4_q), .in1(1'b0), .out(multiplexer_1_out), .sel(\开中断 ));
  D_Flip_Flop #(.trigger("rising"), .Pre_Clr_Positions("LEGACY"), .NegatePresetClear("false"), .enable("true"), .NewFFLayout("false")) d_ff_1 (
    .clk(\_1号 ), .D(1'b1), .Q(d_ff_1_q), .reset(IR1_q));  // open: Qn, preset, en
  D_Flip_Flop #(.trigger("rising"), .Pre_Clr_Positions("LEGACY"), .NegatePresetClear("false"), .enable("true"), .NewFFLayout("false")) d_ff_2 (
    .clk(\_2号 ), .D(1'b1), .Q(d_ff_2_q), .reset(IR2_q));  // open: Qn, preset, en
  D_Flip_Flop #(.trigger("rising"), .Pre_Clr_Positions("LEGACY"), .NegatePresetClear("false"), .enable("true"), .NewFFLayout("false")) d_ff_3 (
    .clk(\_3号 ), .D(1'b1), .Q(d_ff_3_q), .reset(IR1_2_q));  // open: Qn, preset, en
  D_Flip_Flop #(.trigger("rising"), .Pre_Clr_Positions("LEGACY"), .NegatePresetClear("false"), .enable("true"), .NewFFLayout("false")) d_ff_4 (
    .clk(clk), .D(multiplexer_1_out), .Q(d_ff_4_q), .preset(\关中断 ), .en(1'b1));  // open: Qn, reset
  or or_1 (or_1_out, d_ff_1_q, IR1_q);
  or or_2 (or_2_out, d_ff_2_q, IR2_q);
  or or_3 (or_3_out, d_ff_3_q, IR1_2_q);
  not not_1 (not_1_out, d_ff_4_q);
  and and_1 (and_1_out, or_1_out, ~c1);  // AND_Gate
  and and_2 (and_2_out, or_2_out, ~c2);  // AND_Gate
  and and_3 (and_3_out, or_3_out, ~c3);  // AND_Gate
  D_Flip_Flop #(.trigger("rising"), .Pre_Clr_Positions("LEGACY"), .NegatePresetClear("false"), .enable("true"), .NewFFLayout("false")) IR1 (
    .clk(clk), .D(and_1_out), .Q(IR1_q));  // open: Qn, preset, en, reset
  D_Flip_Flop #(.trigger("rising"), .Pre_Clr_Positions("LEGACY"), .NegatePresetClear("false"), .enable("true"), .NewFFLayout("false")) IR2 (
    .clk(clk), .D(and_2_out), .Q(IR2_q));  // open: Qn, preset, en, reset
  D_Flip_Flop #(.trigger("rising"), .Pre_Clr_Positions("LEGACY"), .NegatePresetClear("false"), .enable("true"), .NewFFLayout("false")) IR1_2 (
    .clk(clk), .D(and_3_out), .Q(IR1_2_q));  // open: Qn, preset, en, reset
  or or_4 (or_4_out, IR1_q, IR2_q, IR1_2_q);
  Decoder #(.select(2), .tristate("false"), .disabled(0), .enable("true")) decoder_1 (
    .out0(c0), .out1(c1), .out2(c2), .out3(c3), .sel(nextid), .en(next));
  and and_4 (and_4_out, or_4_out, not_1_out);
  D_Flip_Flop #(.trigger("rising"), .Pre_Clr_Positions("LEGACY"), .NegatePresetClear("false"), .enable("true"), .NewFFLayout("false")) IR1_3 (
    .clk(clk), .D(1'b0), .Q(\中断响应 ), .preset(and_4_out));  // open: Qn, en, reset
endmodule

module \中断多级  (
  input  clk,
  input  \_1号 ,
  input  clear,
  input  \_2号 ,
  input  \_3号 ,
  output _1ing,
  output [1:0] ingid,
  output _2ing,
  output [31:0] address,
  output _3ing
);

  wire and_1_out, and_2_out, and_3_out, c0, c1, c2, c3, d_ff_1_q, d_ff_2_q, d_ff_3_q, IR1_q, IR2_q, IR3_q,
       or_4_out, or_5_out, or_6_out;

  or or_1 (_1ing, IR1_q, d_ff_1_q);
  or or_2 (_2ing, IR2_q, d_ff_2_q);
  or or_3 (_3ing, IR3_q, d_ff_3_q);
  D_Flip_Flop #(.trigger("rising"), .Pre_Clr_Positions("LEGACY"), .NegatePresetClear("false"), .enable("true"), .NewFFLayout("false")) d_ff_1 (
    .clk(\_1号 ), .D(1'b1), .Q(d_ff_1_q), .reset(IR1_q));  // open: Qn, preset, en
  D_Flip_Flop #(.trigger("rising"), .Pre_Clr_Positions("LEGACY"), .NegatePresetClear("false"), .enable("true"), .NewFFLayout("false")) d_ff_2 (
    .clk(\_2号 ), .D(1'b1), .Q(d_ff_2_q), .reset(IR2_q));  // open: Qn, preset, en
  D_Flip_Flop #(.trigger("rising"), .Pre_Clr_Positions("LEGACY"), .NegatePresetClear("false"), .enable("true"), .NewFFLayout("false")) d_ff_3 (
    .clk(\_3号 ), .D(1'b1), .Q(d_ff_3_q), .reset(IR3_q));  // open: Qn, preset, en
  or or_4 (or_4_out, d_ff_1_q, IR1_q);
  or or_5 (or_5_out, d_ff_2_q, IR2_q);
  or or_6 (or_6_out, d_ff_3_q, IR3_q);
  and and_1 (and_1_out, or_4_out, ~c1);  // AND_Gate
  and and_2 (and_2_out, or_5_out, ~c2);  // AND_Gate
  and and_3 (and_3_out, or_6_out, ~c3);  // AND_Gate
  D_Flip_Flop #(.trigger("rising"), .Pre_Clr_Positions("LEGACY"), .NegatePresetClear("false"), .enable("true"), .NewFFLayout("false")) IR1 (
    .clk(clk), .D(and_1_out), .Q(IR1_q));  // open: Qn, preset, en, reset
  D_Flip_Flop #(.trigger("rising"), .Pre_Clr_Positions("LEGACY"), .NegatePresetClear("false"), .enable("true"), .NewFFLayout("false")) IR2 (
    .clk(clk), .D(and_2_out), .Q(IR2_q));  // open: Qn, preset, en, reset
  D_Flip_Flop #(.trigger("rising"), .Pre_Clr_Positions("LEGACY"), .NegatePresetClear("false"), .enable("true"), .NewFFLayout("false")) IR3 (
    .clk(clk), .D(and_3_out), .Q(IR3_q));  // open: Qn, preset, en, reset
  Priority_Encoder #(.select(2), .disabled("Z")) priority_encoder_1 (
    .in0(1'b1), .in1(IR1_q), .in2(IR2_q), .in3(IR3_q), .out(ingid));  // open: gs, en_out, en_in
  Multiplexer #(.select(2), .width(32), .disabled("Z"), .enable("false")) multiplexer_1 (
    .in1(32'h30ac), .in2(32'h3158), .in3(32'h3204), .out(address), .sel(ingid));  // open: in0
  Decoder #(.select(2), .tristate("false"), .disabled(0), .enable("true")) decoder_1 (
    .out0(c0), .out1(c1), .out2(c2), .out3(c3), .sel(ingid), .en(clear));

  // Notes on the sheet:
  //   Reset 
  //   Reset 
  //   Reset 
endmodule

module \中断响应多级  (
  input  clk,
  input  \_1号 ,
  input  next,
  input  [1:0] nextid,
  input  \_2号 ,
  input  \_3号 ,
  input  equal,
  input  \开中断 ,
  input  \关中断 ,
  output \中断响应 
);

  wire and_1_out, and_2_out, and_3_out, and_4_out, c0, c1, c2, c3, d_ff_1_q, d_ff_2_q, d_ff_3_q, d_ff_4_q,
       IR1_2_q, IR1_3_q, IR1_q, IR2_q, multiplexer_1_out, not_1_out, or_1_out, or_2_out, or_3_out, or_4_out;

  Multiplexer #(.select(1), .width(1), .disabled("Z"), .enable("false")) multiplexer_1 (
    .in0(d_ff_4_q), .in1(1'b0), .out(multiplexer_1_out), .sel(\开中断 ));
  D_Flip_Flop #(.trigger("rising"), .Pre_Clr_Positions("LEGACY"), .NegatePresetClear("false"), .enable("true"), .NewFFLayout("false")) d_ff_1 (
    .clk(\_1号 ), .D(1'b1), .Q(d_ff_1_q), .reset(IR1_q));  // open: Qn, preset, en
  D_Flip_Flop #(.trigger("rising"), .Pre_Clr_Positions("LEGACY"), .NegatePresetClear("false"), .enable("true"), .NewFFLayout("false")) d_ff_2 (
    .clk(\_2号 ), .D(1'b1), .Q(d_ff_2_q), .reset(IR2_q));  // open: Qn, preset, en
  D_Flip_Flop #(.trigger("rising"), .Pre_Clr_Positions("LEGACY"), .NegatePresetClear("false"), .enable("true"), .NewFFLayout("false")) d_ff_3 (
    .clk(\_3号 ), .D(1'b1), .Q(d_ff_3_q), .reset(IR1_2_q));  // open: Qn, preset, en
  D_Flip_Flop #(.trigger("rising"), .Pre_Clr_Positions("LEGACY"), .NegatePresetClear("false"), .enable("true"), .NewFFLayout("false")) d_ff_4 (
    .clk(clk), .D(multiplexer_1_out), .Q(d_ff_4_q), .preset(\关中断 ), .en(1'b1));  // open: Qn, reset
  or or_1 (or_1_out, d_ff_1_q, IR1_q);
  or or_2 (or_2_out, d_ff_2_q, IR2_q);
  or or_3 (or_3_out, d_ff_3_q, IR1_2_q);
  not not_1 (not_1_out, d_ff_4_q);
  and and_1 (and_1_out, or_1_out, ~c1);  // AND_Gate
  and and_2 (and_2_out, or_2_out, ~c2);  // AND_Gate
  and and_3 (and_3_out, or_3_out, ~c3);  // AND_Gate
  D_Flip_Flop #(.trigger("rising"), .Pre_Clr_Positions("LEGACY"), .NegatePresetClear("false"), .enable("true"), .NewFFLayout("false")) IR1 (
    .clk(clk), .D(and_1_out), .Q(IR1_q));  // open: Qn, preset, en, reset
  D_Flip_Flop #(.trigger("rising"), .Pre_Clr_Positions("LEGACY"), .NegatePresetClear("false"), .enable("true"), .NewFFLayout("false")) IR2 (
    .clk(clk), .D(and_2_out), .Q(IR2_q));  // open: Qn, preset, en, reset
  D_Flip_Flop #(.trigger("rising"), .Pre_Clr_Positions("LEGACY"), .NegatePresetClear("false"), .enable("true"), .NewFFLayout("false")) IR1_2 (
    .clk(clk), .D(and_3_out), .Q(IR1_2_q));  // open: Qn, preset, en, reset
  or or_4 (or_4_out, IR1_q, IR2_q, IR1_2_q);
  Decoder #(.select(2), .tristate("false"), .disabled(0), .enable("true")) decoder_1 (
    .out0(c0), .out1(c1), .out2(c2), .out3(c3), .sel(nextid), .en(next));
  and and_4 (and_4_out, or_4_out, not_1_out);
  Multiplexer #(.select(1), .width(1), .disabled("Z"), .enable("false")) multiplexer_2 (
    .in0(1'b0), .in1(IR1_3_q), .out(\中断响应 ), .sel(equal));
  D_Flip_Flop #(.trigger("rising"), .Pre_Clr_Positions("LEGACY"), .NegatePresetClear("false"), .enable("true"), .NewFFLayout("false")) IR1_3 (
    .clk(clk), .D(1'b0), .Q(IR1_3_q), .preset(and_4_out));  // open: Qn, en, reset
endmodule

module \流水线中断  (
  output RegWrite,
  output MemWrite,
  output [31:0] IF_PC,
  output [31:0] ID_PC,
  output [31:0] EX_PC,
  output [31:0] M_PC,
  output [31:0] WB_PC,
  output [31:0] RDin,
  output [31:0] MDin,
  output [31:0] LedData
);

  wire alu_1_p2, alu_1_p6, and_1_out, and_2_out, and_5_out, and_6_out, and_7_out, and_8_out, and_9_out,
       and_10_out, and_11_out, and_12_out, and_13_out, branchtaken, CLK, clock_1_out, comparator_1_eq,
       comparator_1_lt, comparator_2_eq, comparator_3_eq, comparator_4_eq, comparator_5_eq, comparator_6_eq,
       comparator_7_eq, comparator_8_eq, comparator_9_eq, comparator_10_eq, comparator_11_eq,
       comparator_12_eq, comparator_13_eq, comparator_14_eq, d_ff_1_q, ecall, ecall2, ex_blt,
       ex_mem2_1_jalout, ex_mem2_1_jalrout, ex_mem2_1_memtoreg_2, EX_MemToReg, EX_RegWrite, ex_sb, Go, H,
       halt, halt1, halt2, id_sb, id_Uret, IR1, IR2, IR3, jAL, JALR, JJ, loaduse, MEM_RegWrite, mem_sb,
       mem_wb2_1_jalout, mem_wb2_1_jalrout, mem_wb2_1_memtoreg_2, nand_1_out, not_1_out, not_2_out,
       not_3_out, not_4_out, not_5_out, not_6_out, not_7_out, not_8_out, not_10_out, not_11_out, not_12_out,
       not_13_out, not_14_out, not_15_out, or_2_out, or_3_out, or_4_out, or_5_out, RST, RsUsed, RtUsed, s,
       ss, W1, W2, W3, \中断响应 ;
  wire [1:0] ex_RsF, ex_RtF, id, multiplexer_16_out, multiplexer_17_out, register_1_q, RsForward, RtForward;
  wire [1:1] JJUin;
  wire [2:0] JJUout;
  wire [3:0] id_ex3_1_aluopout, \单周期硬布线控制器_1_alu_op ;
  wire [4:0] EXW, MEMW, rs, rt, W_F;
  wire [6:0] signalin;
  wire [6:1] signalout;
  wire [11:0] multiplexer_6_out;
  wire [12:0] CNT_num;
  wire [15:0] \LoadUse次数 , \总周期数 , \插入气泡数 , \无条件分支数 , \条件分支成功数 ;
  wire [31:0] adder_1_out, adder_2_out, alu_1_p7, bit_extender_1_out, bit_extender_2_out, bit_extender_3_out,
       EX_IR, id_ex3_1_b_imm_2, id_ex3_1_i_s_imm_2, id_ex3_1_j_imm_2, ID_IR, IF_IR, intPC, IR, mem_a, MEM_IR,
       mem_wb2_1_alu_result_2, mem_wb2_1_memdata_2, multiplexer_2_out, multiplexer_9_out, multiplexer_10_out,
       multiplexer_11_out, multiplexer_13_out, PC_F, PC_q, PCN, R1, R2, R11, R22, ram_1_dout,
       \regifile_下降沿_1_r1 , \regifile_下降沿_1_r2 , rom_1_data, shifter_1_out, wb_a, WB_IR, \断点 ;

  Button \u_总复位  (.out(RST));
  Button _1 (.out(IR1));
  Button _2 (.out(IR2));
  Button _3 (.out(IR3));
  // Probe on \总周期数 
  // Probe on \总周期数 
  Counter #(.width(16), .max('hffff), .ongoal("wrap"), .trigger("rising"), .behavior("new")) counter_1 (
    .Q(\总周期数 ), .clk(CLK));  // open: load, D, count, carry, clr, preset, down
  Multiplexer #(.select(1), .width(32), .disabled("Z"), .enable("false")) multiplexer_1 (
    .in0(adder_1_out), .in1(multiplexer_13_out), .out(PCN), .sel(branchtaken));
  Button \u_继续运行  (.out(Go));
  LED #(.active("true")) led_1 (.in(W1));
  LED #(.active("true")) led_2 (.in(W2));
  LED #(.active("true")) led_3 (.in(W3));
  or or_1 (branchtaken, JJUout[0], JALR, or_5_out);
  Multiplexer #(.select(1), .width(32), .disabled("Z"), .enable("false")) multiplexer_2 (
    .in0(PCN), .in1(\断点 ), .out(multiplexer_2_out), .sel(\中断响应 ));
  and and_1 (and_1_out, not_1_out, H);
  not not_1 (not_1_out, loaduse);
  Hex_Digit_Display hex_digit_display_1 (.value(LedData[31:28]));  // open: dp
  // Probe on IF_PC[19:0]
  // RiscV_Probe riscv_probe_1: pin names not known; wires that end beside it: IF_IR
  Register #(.width(32), .trigger("rising"), .Select("low")) PC (
    .D(multiplexer_2_out), .en(and_1_out), .Q(PC_q), .clk(CLK), .clr(RST));
  Adder #(.width(32)) adder_1 (.a(IF_PC), .b(32'h4), .out(adder_1_out));  // open: cin, cout
  Hex_Digit_Display hex_digit_display_2 (.value(LedData[23:20]));  // open: dp
  Hex_Digit_Display hex_digit_display_3 (.value(LedData[27:24]));  // open: dp
  // Probe on ID_PC[19:0]
  // RiscV_Probe riscv_probe_2: pin names not known; wires that end beside it: ID_IR
  Multiplexer #(.select(1), .width(32), .disabled("Z"), .enable("false")) multiplexer_3 (
    .in0(PC_q), .in1(intPC), .out(IF_PC), .sel(id_Uret));
  or or_2 (or_2_out, JJUout[2], \中断响应 );
  Hex_Digit_Display hex_digit_display_4 (.value(LedData[19:16]));  // open: dp
  Hex_Digit_Display hex_digit_display_5 (.value(LedData[15:12]));  // open: dp
  not not_2 (not_2_out, loaduse);
  Register #(.width(2), .trigger("falling"), .Select("low")) register_1 (
    .D(id), .Q(register_1_q), .clk(or_2_out));  // open: en, clr
  Hex_Digit_Display hex_digit_display_6 (.value(LedData[11:8]));  // open: dp
  Hex_Digit_Display hex_digit_display_7 (.value(LedData[7:4]));  // open: dp
  // Probe on EX_PC[19:0]
  // RiscV_Probe riscv_probe_3: pin names not known; wires that end beside it: EX_IR
  // RiscV_Probe riscv_probe_4: pin names not known; wires that end beside it: IF_PC[11:2], IR
  ROM #(.addrWidth(10), .dataWidth(32), .Select("high")) rom_1 (.addr(IF_PC[11:2]), .data(rom_1_data));
  and and_2 (and_2_out, not_2_out, H);
  or or_3 (or_3_out, branchtaken, \中断响应 );
  \中断响应流水线  \u_中断响应流水线_1  (
    .clk(CLK), .\_1号 (IR1), .next(\中断响应 ), .nextid(id), .\_2号 (IR2), .\_3号 (IR3), .EX_PC(EX_PC),
    .\中断响应 (\中断响应 ), .\开中断 (JJUout[2]), .\关中断 (\中断响应 ));
  \中断  \u_中断_1  (
    .ingid(id), .\_1号 (IR1), .\_2号 (IR2), .\_3号 (IR3), ._1ing(W1), ._2ing(W2), ._3ing(W3), .address(\断点 ),
    .clear(JJUout[2]), .clrid(register_1_q), .clk(CLK));
  Hex_Digit_Display hex_digit_display_8 (.value(LedData[3:0]));  // open: dp
  IF_ID2 if_id2_1 (
    .IRin(rom_1_data), .PCin(IF_PC), .clk(CLK), .bubble(or_3_out), .stop(and_2_out), .IRout(IR), .PCout(ID_PC));
  // Probe on \总周期数 
  // Probe on M_PC[19:0]
  // RiscV_Probe riscv_probe_5: pin names not known; wires that end beside it: MEM_IR
  // Probe on \总周期数 
  // Probe on \无条件分支数 
  // Probe on \条件分支成功数 
  // Probe on \插入气泡数 
  // Probe on \LoadUse次数 
  \单周期硬布线控制器  \u_单周期硬布线控制器_1  (
    .Funct({IR[30], IR[25], IR[14:12]}), .OP(IR[6:2]), .ALU_OP(\单周期硬布线控制器_1_alu_op ), .MemToReg(signalin[3]),
    .MemWrite(signalin[2]), .ALU_SRC(signalin[1]), .RegWrite(signalin[0]), .ecall(ecall), .S_type(s),
    .Jalr(JJUin[1]), .Beq(signalin[6]), .JAL(jAL), .Bne(signalin[4]), .in_3(IR[21]), .uret(id_Uret),
    .blt(signalin[5]), .sb(id_sb));  // open: csrrsi, csrrci
  // Probe on IF_PC[11:0]
  // Probe on WB_PC[19:0]
  // RiscV_Probe riscv_probe_6: pin names not known; wires that end beside it: WB_IR
  Multiplexer #(.select(1), .width(5), .disabled("Z"), .enable("false")) multiplexer_4 (
    .in0(IR[19:15]), .in1(5'b10001), .out(rs), .sel(ecall));
  Multiplexer #(.select(1), .width(5), .disabled("Z"), .enable("false")) multiplexer_5 (
    .in0(IR[24:20]), .in1(5'b01010), .out(rt), .sel(ecall));
  Multiplexer #(.select(1), .width(12), .disabled("Z"), .enable("false")) multiplexer_6 (
    .in0(IR[31:20]), .in1({IR[31:25], IR[11:7]}), .out(multiplexer_6_out), .sel(s));
  assign bit_extender_1_out = {{20{IR[31]}}, {IR[31], IR[7], IR[30:25], IR[11:8]}};  // Bit_Extender bit_extender_1
  assign bit_extender_2_out = {{12{IR[31]}}, {IR[31], IR[19:12], IR[20], IR[30:21]}};  // Bit_Extender bit_extender_2
  Multiplexer #(.select(1), .width(32), .disabled("Z"), .enable("false")) multiplexer_7 (
    .in0(wb_a), .in1(PC_F), .out(RDin), .sel(JJ));
  // Probe on EX_PC[11:0]
  // Probe on ID_PC[11:0]
  \Regifile_下降沿  \regifile_下降沿_1  (
    .Din(RDin), .Clk(CLK), .R1(\regifile_下降沿_1_r1 ), .R2(\regifile_下降沿_1_r2 ), .WE(RegWrite), .W_num(W_F),
    .R1_num(rs), .R2_num(rt));
  assign bit_extender_3_out = {{20{multiplexer_6_out[11]}}, multiplexer_6_out};  // Bit_Extender bit_extender_3
  Register #(.width(32), .trigger("rising"), .Select("low")) register_2 (
    .D(EX_PC), .en(\中断响应 ), .Q(intPC), .clk(CLK));  // open: clr
  // Probe on M_PC[11:0]
  D_Flip_Flop #(.trigger("high"), .Pre_Clr_Positions("LEGACY"), .NegatePresetClear("false"), .enable("true"), .NewFFLayout("false")) d_ff_1 (.Q(d_ff_1_q));  // open: clk, D, Qn, preset, en, reset
  // Probe on 13'hc
  // Probe on WB_PC[11:0]
  Comparator #(.width(13), .mode("twosComplement")) comparator_1 (
    .a(CNT_num), .b(13'hc), .eq(comparator_1_eq), .lt(comparator_1_lt));  // open: gt
  Clock #(.highDuration(1), .lowDuration(1)) clock_1 (.out(clock_1_out));
  or or_4 (or_4_out, loaduse, \中断响应 , branchtaken);
  nand nand_1 (nand_1_out, d_ff_1_q, comparator_1_eq);
  Counter #(.width(13), .max('h1fff), .ongoal("stay"), .trigger("rising"), .behavior("old")) counter_2 (
    .count(comparator_1_lt), .Q(CNT_num), .clk(clock_1_out));  // open: load, D, carry, clr, preset
  ID_EX3 id_ex3_1 (
    .signal(signalin), .ecall(ecall), .JJU({id_Uret, JJUin[1], jAL}), .AluOp(\单周期硬布线控制器_1_alu_op ),
    .R1(\regifile_下降沿_1_r1 ), .R2(\regifile_下降沿_1_r2 ), .I_S_imm(bit_extender_3_out),
    .B_imm(bit_extender_1_out), .J_imm(bit_extender_2_out), .PCin(ID_PC), .WriteReg_num(IR[11:7]),
    .RsForward(RsForward), .RtForward(RtForward), .CLK(CLK), .bubble(or_4_out), .stop(H),
    .signalout({signalout[6], ex_blt, signalout[4], EX_MemToReg, signalout[2:1], EX_RegWrite}),
    .ecallout(ecall2), .JJUout({JJUout[2], JALR, JJUout[0]}), .AluOpout(id_ex3_1_aluopout), .R1_2(R1),
    .R2_2(R2), .I_S_imm_2(id_ex3_1_i_s_imm_2), .B_imm_2(id_ex3_1_b_imm_2), .J_imm_2(id_ex3_1_j_imm_2),
    .PCout(EX_PC), .WriteReg_num_2(EXW), .RsForward_2(ex_RsF), .RtForward_2(ex_RtF), .sb(id_sb), .sb_2(ex_sb));
  Multiplexer #(.select(2), .width(32), .disabled("Z"), .enable("false")) multiplexer_8 (
    .in0(R1), .in1(wb_a), .in2(mem_a), .out(R11), .sel(ex_RsF));  // open: in3
  assign CLK = nand_1_out ? clock_1_out : 1'bz;  // Controlled_Buffer controlled_buffer_1
  Multiplexer #(.select(1), .width(32), .disabled("Z"), .enable("false")) multiplexer_9 (
    .in0(id_ex3_1_j_imm_2), .in1(id_ex3_1_b_imm_2), .out(multiplexer_9_out), .sel(or_5_out));
  Pull_Resistor #(.pull(1)) pull_resistor_1 (.node(CLK));
  Multiplexer #(.select(1), .width(32), .disabled("Z"), .enable("false")) multiplexer_10 (
    .in0(R22), .in1(id_ex3_1_i_s_imm_2), .out(multiplexer_10_out), .sel(signalout[1]));
  Multiplexer #(.select(1), .width(32), .disabled("Z"), .enable("false")) multiplexer_11 (
    .in0(LedData), .in1(R22), .out(multiplexer_11_out), .sel(ss));
  Comparator #(.width(32), .mode("twosComplement")) comparator_2 (
    .a(32'h22), .b(R11), .eq(comparator_2_eq));  // open: gt, lt
  and and_3 (ss, comparator_2_eq, ecall2);
  not not_3 (not_3_out, comparator_2_eq);
  and and_4 (halt, not_3_out, ecall2);
  not not_4 (not_4_out, alu_1_p6);
  // ALU alu_1: pin names not known; wires that end beside it: R11, alu_1_p2, multiplexer_10_out, alu_1_p2, id_ex3_1_aluopout, alu_1_p6, alu_1_p7
  Shifter #(.width(32), .shift("ll")) shifter_1 (.in(multiplexer_9_out), .\dist (5'b00001), .out(shifter_1_out));
  Multiplexer #(.select(2), .width(32), .disabled("Z"), .enable("false")) multiplexer_12 (
    .in0(R2), .in1(wb_a), .in2(mem_a), .out(R22), .sel(ex_RtF));  // open: in3
  and and_5 (and_5_out, signalout[4], not_4_out);
  and and_6 (and_6_out, signalout[6], alu_1_p6);
  Adder #(.width(32)) adder_2 (.a(shifter_1_out), .b(EX_PC), .out(adder_2_out));  // open: cin, cout
  or or_5 (or_5_out, and_5_out, and_6_out);
  EX_MEM2 ex_mem2_1 (
    .JALin(JJUout[0]), .JALRin(JALR), .RegWrite(EX_RegWrite), .MemToReg(EX_MemToReg),
    .MemWrite(signalout[2]), .Write_Data(R22), .ALU_Result(alu_1_p7), .WriteReg_num(EXW), .PCin(EX_PC),
    .haltin(halt), .CLK(CLK), .bubble(\中断响应 ), .stop(H), .JALout(ex_mem2_1_jalout),
    .JALRout(ex_mem2_1_jalrout), .RegWrite_2(MEM_RegWrite), .MemToReg_2(ex_mem2_1_memtoreg_2),
    .MemWrite_2(MemWrite), .Write_Data_2(MDin), .ALU_Result_2(mem_a), .WriteReg_num_2(MEMW), .PCout(M_PC),
    .haltout(halt1), .sb(ex_sb), .sb_2(mem_sb));
  Multiplexer #(.select(1), .width(32), .disabled("Z"), .enable("false")) multiplexer_13 (
    .in0(adder_2_out), .in1(alu_1_p7), .out(multiplexer_13_out), .sel(JALR));
  Register #(.width(32), .trigger("rising"), .Select("low")) register_3 (
    .D(multiplexer_11_out), .en(ss), .Q(LedData), .clk(CLK));  // open: clr
  RAM ram_1 (
    .Mode(mem_sb), .\字节地址 (mem_a[11:0]), .Din(MDin), .CLK(CLK), .str(MemWrite), .id(not_5_out),
    .Dout(ram_1_dout));
  not not_5 (not_5_out, MemWrite);
  MEM_WB2 mem_wb2_1 (
    .halt(halt1), .JAL(ex_mem2_1_jalout), .JALR(ex_mem2_1_jalrout), .RegWrite(MEM_RegWrite),
    .MemToReg(ex_mem2_1_memtoreg_2), .ALU_Result(mem_a), .MemData(ram_1_dout), .WriteReg_num(MEMW),
    .PC(M_PC), .CLK(CLK), .bubble(1'b0), .stop(H), .haltout(halt2), .JALout(mem_wb2_1_jalout),
    .JALRout(mem_wb2_1_jalrout), .RegWrite_2(RegWrite), .MemToReg_2(mem_wb2_1_memtoreg_2),
    .ALU_Result_2(mem_wb2_1_alu_result_2), .MemData_2(mem_wb2_1_memdata_2), .WriteReg_num_2(W_F),
    .PCout(WB_PC));
  Multiplexer #(.select(1), .width(32), .disabled("Z"), .enable("false")) multiplexer_14 (
    .in0(mem_wb2_1_alu_result_2), .in1(mem_wb2_1_memdata_2), .out(wb_a), .sel(mem_wb2_1_memtoreg_2));
  or or_6 (JJ, mem_wb2_1_jalout, mem_wb2_1_jalrout);
  Adder #(.width(32)) adder_3 (.a(WB_PC), .b(32'h4), .out(PC_F));  // open: cin, cout
  Comparator #(.width(5), .mode("twosComplement")) comparator_3 (
    .a(rs), .b({5{1'b0}}), .eq(comparator_3_eq));  // open: gt, lt
  not not_6 (not_6_out, comparator_3_eq);
  Comparator #(.width(5), .mode("twosComplement")) comparator_4 (
    .a(rs), .b(EXW), .eq(comparator_4_eq));  // open: gt, lt
  not not_7 (not_7_out, comparator_5_eq);
  Comparator #(.width(5), .mode("twosComplement")) comparator_5 (
    .a(rs), .b({5{1'b0}}), .eq(comparator_5_eq));  // open: gt, lt
  Comparator #(.width(5), .mode("twosComplement")) comparator_6 (
    .a(rs), .b(MEMW), .eq(comparator_6_eq));  // open: gt, lt
  or or_7 (H, not_8_out, Go);
  not not_8 (not_8_out, halt2);
  and and_7 (and_7_out, EX_RegWrite, RsUsed, not_6_out, comparator_4_eq);
  and and_8 (and_8_out, MEM_RegWrite, RsUsed, not_7_out, comparator_6_eq);
  not not_9 (RsUsed, jAL);
  Multiplexer #(.select(1), .width(2), .disabled("Z"), .enable("false")) multiplexer_15 (
    .in0(multiplexer_16_out), .in1(2'b10), .out(RsForward), .sel(and_7_out));
  Multiplexer #(.select(1), .width(2), .disabled("Z"), .enable("false")) multiplexer_16 (
    .in0(2'b00), .in1(2'b01), .out(multiplexer_16_out), .sel(and_8_out));
  not not_10 (not_10_out, signalin[1]);
  and and_9 (and_9_out, not_10_out, not_11_out);
  not not_11 (not_11_out, jAL);
  or or_8 (RtUsed, s, and_9_out);
  Comparator #(.width(5), .mode("twosComplement")) comparator_7 (
    .a(rs), .b({5{1'b0}}), .eq(comparator_7_eq));  // open: gt, lt
  Comparator #(.width(5), .mode("twosComplement")) comparator_8 (
    .a(rs), .b(EXW), .eq(comparator_8_eq));  // open: gt, lt
  Comparator #(.width(5), .mode("twosComplement")) comparator_9 (
    .a(rt), .b({5{1'b0}}), .eq(comparator_9_eq));  // open: gt, lt
  Comparator #(.width(5), .mode("twosComplement")) comparator_10 (
    .a(EXW), .b(rt), .eq(comparator_10_eq));  // open: gt, lt
  not not_12 (not_12_out, comparator_7_eq);
  not not_13 (not_13_out, comparator_9_eq);
  and and_10 (and_10_out, EX_MemToReg, RsUsed, not_12_out, comparator_8_eq);
  and and_11 (and_11_out, EX_MemToReg, not_13_out, comparator_10_eq, RtUsed);
  or or_9 (loaduse, and_10_out, and_11_out);
  Comparator #(.width(5), .mode("twosComplement")) comparator_11 (
    .a(rt), .b({5{1'b0}}), .eq(comparator_11_eq));  // open: gt, lt
  not not_14 (not_14_out, comparator_11_eq);
  Comparator #(.width(5), .mode("twosComplement")) comparator_12 (
    .a(rt), .b(EXW), .eq(comparator_12_eq));  // open: gt, lt
  not not_15 (not_15_out, comparator_13_eq);
  Comparator #(.width(5), .mode("twosComplement")) comparator_13 (
    .a(rt), .b({5{1'b0}}), .eq(comparator_13_eq));  // open: gt, lt
  Comparator #(.width(5), .mode("twosComplement")) comparator_14 (
    .a(rt), .b(MEMW), .eq(comparator_14_eq));  // open: gt, lt
  and and_12 (and_12_out, EX_RegWrite, RtUsed, not_14_out, comparator_12_eq);
  and and_13 (and_13_out, MEM_RegWrite, RtUsed, not_15_out, comparator_14_eq);
  Multiplexer #(.select(1), .width(2), .disabled("Z"), .enable("false")) multiplexer_17 (
    .in0(2'b00), .in1(2'b01), .out(multiplexer_17_out), .sel(and_13_out));
  Multiplexer #(.select(1), .width(2), .disabled("Z"), .enable("false")) multiplexer_18 (
    .in0(multiplexer_17_out), .in1(2'b10), .out(RtForward), .sel(and_12_out));

  // Other names for the same wires on the sheet: W_num[4:0] = IR[11:7]; JJUin (some bits) = {id_Uret, jAL};
  //   JJUout[1] = JALR; Uret = JJUout[2]; MEM_PC[31:0] = M_PC; PC[31:0] = IF_PC; src = signalin[1];
  //   signalout (some bits) = {ex_blt, EX_MemToReg, EX_RegWrite}

  // Notes on the sheet:
  //   中断源
  //   时空图监测，可删除
  //   中断等待指示
  //   数码管输出
  //   指令探针
  //   指令存储器
  //   contents of rom_1 (hex, n*v repeats v):
  //   7d000113 100413 1f41993 41f9d993 433 c00913 800b13 140413 f47413 800293 100313 499993 89e9b3 1300533
  //   2200893 73 406282b3 fe0294e3 140413 f00f93 1f47433 1c41413 800293 100313 49d993 89e9b3 1300533
  //   2200893 73 406282b3 fe0294e3 1c45413 406b0b33 b0463 f95ff06f 2b3 fff2c293 1029293 fff2e293 500533
  //   2200893 73 f5dff06f 1112023 410113 a12023 410113 812023 410113 1312023 410113 1412023 410113 1512023
  //   410113 1612023 410113 100b13 300a13 100a93 1600433 441413 14469b3 1300533 2200893 73 fe0416e3
  //   415a0a33 fe0a10e3 ffc10113 12b03 ffc10113 12a83 ffc10113 12a03 ffc10113 12983 ffc10113 12403
  //   ffc10113 12503 ffc10113 12883 200073 1112023 410113 a12023 410113 812023 410113 1312023 410113
  //   1412023 410113 1512023 410113 1612023 410113 200b13 300a13 100a93 1600433 441413 14469b3 1300533
  //   2200893 73 fe0416e3 415a0a33 fe0a10e3 ffc10113 12b03 ffc10113 12a83 ffc10113 12a03 ffc10113 12983
  //   ffc10113 12403 ffc10113 12503 ffc10113 12883 200073 1112023 410113 a12023 410113 812023 410113
  //   1312023 410113 1412023 410113 1512023 410113 1612023 410113 300b13 300a13 100a93 1600433 441413
  //   14469b3 1300533 2200893 73 fe0416e3 415a0a33 fe0a10e3 ffc10113 12b03 ffc10113 12a83 ffc10113 12a03
  //   ffc10113 12983 ffc10113 12403 ffc10113 12503 ffc10113 12883 200073
  //   JAL
  //   JALR
  //   Beq
  //   Bne
  //   URET
  //   MemToReg
  //   MemWrite
  //   AluOP
  //   AluSrcB
  //   RegWrite
  //   控制位
  //   流水调试日志用
  //   暂停节拍，不能为0
  //   可计数暂停的时钟源
  //   为方便自动评测，需要输出流水线各段保存的PC值，注意是PC不是PC+4，另外ID段寄存器写入信息，Mem段内存写入信息也要输出
  //   数据存储器
endmodule

module \中断响应流水线  (
  input  clk,
  input  \_1号 ,
  input  next,
  input  [1:0] nextid,
  input  \_2号 ,
  input  \_3号 ,
  input  [31:0] EX_PC,
  input  \开中断 ,
  input  \关中断 ,
  output \中断响应 
);

  wire and_1_out, and_2_out, and_3_out, and_4_out, and_5_out, c0, c1, c2, c3, comparator_1_eq, d_ff_1_q,
       d_ff_2_q, d_ff_3_q, d_ff_4_q, IR1_2_q, IR1_3_q, IR1_q, IR2_q, multiplexer_1_out, not_1_out, not_2_out,
       or_1_out, or_2_out, or_3_out, or_4_out;

  Multiplexer #(.select(1), .width(1), .disabled("Z"), .enable("false")) multiplexer_1 (
    .in0(d_ff_4_q), .in1(1'b0), .out(multiplexer_1_out), .sel(\开中断 ));
  D_Flip_Flop #(.trigger("rising"), .Pre_Clr_Positions("LEGACY"), .NegatePresetClear("false"), .enable("true"), .NewFFLayout("false")) d_ff_1 (
    .clk(\_1号 ), .D(1'b1), .Q(d_ff_1_q), .reset(IR1_q));  // open: Qn, preset, en
  D_Flip_Flop #(.trigger("rising"), .Pre_Clr_Positions("LEGACY"), .NegatePresetClear("false"), .enable("true"), .NewFFLayout("false")) d_ff_2 (
    .clk(\_2号 ), .D(1'b1), .Q(d_ff_2_q), .reset(IR2_q));  // open: Qn, preset, en
  D_Flip_Flop #(.trigger("rising"), .Pre_Clr_Positions("LEGACY"), .NegatePresetClear("false"), .enable("true"), .NewFFLayout("false")) d_ff_3 (
    .clk(\_3号 ), .D(1'b1), .Q(d_ff_3_q), .reset(IR1_2_q));  // open: Qn, preset, en
  D_Flip_Flop #(.trigger("rising"), .Pre_Clr_Positions("LEGACY"), .NegatePresetClear("false"), .enable("true"), .NewFFLayout("false")) d_ff_4 (
    .clk(clk), .D(multiplexer_1_out), .Q(d_ff_4_q), .preset(\关中断 ), .en(1'b1));  // open: Qn, reset
  or or_1 (or_1_out, d_ff_1_q, IR1_q);
  or or_2 (or_2_out, d_ff_2_q, IR2_q);
  or or_3 (or_3_out, d_ff_3_q, IR1_2_q);
  not not_1 (not_1_out, d_ff_4_q);
  and and_1 (and_1_out, or_1_out, ~c1);  // AND_Gate
  and and_2 (and_2_out, or_2_out, ~c2);  // AND_Gate
  and and_3 (and_3_out, or_3_out, ~c3);  // AND_Gate
  D_Flip_Flop #(.trigger("rising"), .Pre_Clr_Positions("LEGACY"), .NegatePresetClear("false"), .enable("true"), .NewFFLayout("false")) IR1 (
    .clk(clk), .D(and_1_out), .Q(IR1_q));  // open: Qn, preset, en, reset
  D_Flip_Flop #(.trigger("rising"), .Pre_Clr_Positions("LEGACY"), .NegatePresetClear("false"), .enable("true"), .NewFFLayout("false")) IR2 (
    .clk(clk), .D(and_2_out), .Q(IR2_q));  // open: Qn, preset, en, reset
  D_Flip_Flop #(.trigger("rising"), .Pre_Clr_Positions("LEGACY"), .NegatePresetClear("false"), .enable("true"), .NewFFLayout("false")) IR1_2 (
    .clk(clk), .D(and_3_out), .Q(IR1_2_q));  // open: Qn, preset, en, reset
  or or_4 (or_4_out, IR1_q, IR2_q, IR1_2_q);
  and and_4 (and_4_out, or_4_out, not_1_out);
  Decoder #(.select(2), .tristate("false"), .disabled(0), .enable("true")) decoder_1 (
    .out0(c0), .out1(c1), .out2(c2), .out3(c3), .sel(nextid), .en(next));
  D_Flip_Flop #(.trigger("rising"), .Pre_Clr_Positions("LEGACY"), .NegatePresetClear("false"), .enable("true"), .NewFFLayout("false")) IR1_3 (
    .clk(clk), .D(1'b0), .Q(IR1_3_q), .preset(and_4_out), .reset(\中断响应 ));  // open: Qn, en
  Comparator #(.width(32), .mode("twosComplement")) comparator_1 (
    .a(EX_PC), .b({32{1'b0}}), .eq(comparator_1_eq));  // open: gt, lt
  and and_5 (and_5_out, IR1_3_q, not_2_out);
  not not_2 (not_2_out, comparator_1_eq);
  D_Flip_Flop #(.trigger("rising"), .Pre_Clr_Positions("LEGACY"), .NegatePresetClear("false"), .enable("true"), .NewFFLayout("false")) IR1_4 (
    .clk(clk), .D(1'b0), .Q(\中断响应 ), .preset(and_5_out));  // open: Qn, en, reset

  // Notes on the sheet:
  //   中断信号采样参考电路
endmodule
module BTB (
  input  [31:0] PC,
  input  [31:0] EX_PC,
  input  [31:0] EX_BranchAddr,
  input  EX_Branch,
  input  EX_Branched,
  input  in_6,
  output ID_PredictJump,
  output [31:0] BTB_JumpAddr
);

  wire and_17_out, and_26_out, and_27_out, and_28_out, and_29_out, and_30_out, and_31_out, and_32_out,
       and_33_out, comparator_1_eq, comparator_2_eq, comparator_3_eq, comparator_4_eq, comparator_5_eq,
       comparator_6_eq, comparator_7_eq, comparator_8_eq, comparator_9_eq, comparator_10_eq,
       comparator_11_eq, comparator_12_eq, comparator_13_eq, comparator_14_eq, comparator_15_eq,
       comparator_16_eq, d_ff_1_q, d_ff_2_q, d_ff_3_q, d_ff_4_q, d_ff_5_q, d_ff_6_q, d_ff_7_q, d_ff_8_q,
       decoder_1_out0, decoder_1_out1, decoder_1_out2, decoder_1_out3, decoder_1_out4, decoder_1_out5,
       decoder_1_out6, decoder_1_out7, decoder_2_out0, decoder_2_out1, decoder_2_out2, decoder_2_out3,
       decoder_2_out4, decoder_2_out5, decoder_2_out6, decoder_2_out7, EX_Hit, EX_Miss, L0, L1, L2, L3, L4,
       L5, L6, L7, M0, M1, M2, M3, M4, M5, M6, M7, not_1_out, not_2_out, not_3_out, not_4_out, not_5_out,
       not_6_out, not_7_out, not_8_out, or_1_out, or_2_out, or_3_out, or_4_out, or_5_out, or_6_out, or_7_out,
       or_8_out, or_10_out, or_11_out, or_12_out, or_13_out, or_14_out, or_15_out, or_16_out, or_17_out,
       priority_encoder_1_gs, v0, v1, v2, v3, v4, v5, v6, v7, write0, write1, write2, write3, write4, write5,
       write6, write7;
  wire [0:0] controlled_buffer_9_out, controlled_buffer_10_out, controlled_buffer_11_out,
       controlled_buffer_12_out, controlled_buffer_13_out, controlled_buffer_14_out,
       controlled_buffer_15_out, controlled_buffer_16_out;
  wire [1:0] fsm_1_nextlow, fsm_2_nextlow, fsm_3_nextlow, fsm_4_nextlow, fsm_5_nextlow, fsm_6_nextlow,
       fsm_7_nextlow, fsm_8_nextlow, predict0, predict1, predict2, predict3, predict4, predict5, predict6,
       predict7;
  wire [2:0] max_1_max_num, max_2_max_num, max_3_max_num, max_4_max_num, max_5_max_num, max_6_max_num,
       max_7_max_num, priority_encoder_1_out;
  wire [15:0] c0, c1, c2, c3, c4, c5, c6, c7, max_1_max, max_2_max, max_3_max, max_4_max, max_5_max,
       max_6_max;
  wire [31:0] register_17_q, register_18_q, register_19_q, register_20_q, register_21_q, register_22_q,
       register_23_q, register_24_q, tag0, tag1, tag2, tag3, tag4, tag5, tag6, tag7;

  LED #(.active("true")) led_1 (.in(v0));
  Register #(.width(1), .trigger("rising"), .Select("low")) register_1 (
    .D(1'b1), .en(write0), .Q(v0), .clk(in_6));  // open: clr
  LED #(.active("true")) led_2 (.in(v1));
  Register #(.width(1), .trigger("rising"), .Select("low")) register_2 (
    .D(1'b1), .en(write1), .Q(v1), .clk(in_6));  // open: clr
  LED #(.active("true")) led_3 (.in(v2));
  Register #(.width(1), .trigger("rising"), .Select("low")) register_3 (
    .D(1'b1), .en(write2), .Q(v2), .clk(in_6));  // open: clr
  LED #(.active("true")) led_4 (.in(v3));
  Register #(.width(1), .trigger("rising"), .Select("low")) register_4 (
    .D(1'b1), .en(write3), .Q(v3), .clk(in_6));  // open: clr
  LED #(.active("true")) led_5 (.in(v4));
  Register #(.width(1), .trigger("rising"), .Select("low")) register_5 (
    .D(1'b1), .en(write4), .Q(v4), .clk(in_6));  // open: clr
  LED #(.active("true")) led_6 (.in(v5));
  Register #(.width(1), .trigger("rising"), .Select("low")) register_6 (
    .D(1'b1), .en(write5), .Q(v5), .clk(in_6));  // open: clr
  LED #(.active("true")) led_7 (.in(v6));
  Register #(.width(1), .trigger("rising"), .Select("low")) register_7 (
    .D(1'b1), .en(write6), .Q(v6), .clk(in_6));  // open: clr
  Register #(.width(1), .trigger("rising"), .Select("low")) register_8 (
    .D(1'b1), .en(write7), .Q(v7), .clk(in_6));  // open: clr
  LED #(.active("true")) led_8 (.in(v7));
  // Probe on tag0
  Register #(.width(32), .trigger("rising"), .Select("low")) register_9 (
    .D(EX_PC), .en(write0), .Q(tag0), .clk(in_6));  // open: clr
  // Probe on tag1
  Register #(.width(32), .trigger("rising"), .Select("low")) register_10 (
    .D(EX_PC), .en(write1), .Q(tag1), .clk(in_6));  // open: clr
  // Probe on tag2
  Register #(.width(32), .trigger("rising"), .Select("low")) register_11 (
    .D(EX_PC), .en(write2), .Q(tag2), .clk(in_6));  // open: clr
  // Probe on tag3
  Register #(.width(32), .trigger("rising"), .Select("low")) register_12 (
    .D(EX_PC), .en(write3), .Q(tag3), .clk(in_6));  // open: clr
  // Probe on tag4
  Register #(.width(32), .trigger("rising"), .Select("low")) register_13 (
    .D(EX_PC), .en(write4), .Q(tag4), .clk(in_6));  // open: clr
  // Probe on tag5
  Register #(.width(32), .trigger("rising"), .Select("low")) register_14 (
    .D(EX_PC), .en(write5), .Q(tag5), .clk(in_6));  // open: clr
  Register #(.width(32), .trigger("rising"), .Select("low")) register_15 (
    .D(EX_PC), .en(write6), .Q(tag6), .clk(in_6));  // open: clr
  // Probe on tag7
  Register #(.width(32), .trigger("rising"), .Select("low")) register_16 (
    .D(EX_PC), .en(write7), .Q(tag7), .clk(in_6));  // open: clr
  // Probe on tag6
  Counter #(.width(16), .max('hffff), .ongoal("wrap"), .trigger("rising"), .behavior("new")) counter_1 (
    .Q(c0), .clk(in_6), .clr(d_ff_3_q));  // open: load, D, count, carry, preset, down
  or or_1 (or_1_out, write0, L0);
  Counter #(.width(16), .max('hffff), .ongoal("wrap"), .trigger("rising"), .behavior("new")) counter_2 (
    .Q(c1), .clk(in_6), .clr(d_ff_4_q));  // open: load, D, count, carry, preset, down
  or or_2 (or_2_out, write1, L1);
  Counter #(.width(16), .max('hffff), .ongoal("wrap"), .trigger("rising"), .behavior("new")) counter_3 (
    .Q(c2), .clk(in_6), .clr(d_ff_5_q));  // open: load, D, count, carry, preset, down
  or or_3 (or_3_out, write2, L2);
  Counter #(.width(16), .max('hffff), .ongoal("wrap"), .trigger("rising"), .behavior("new")) counter_4 (
    .Q(c3), .clk(in_6), .clr(d_ff_6_q));  // open: load, D, count, carry, preset, down
  or or_4 (or_4_out, write3, L3);
  Counter #(.width(16), .max('hffff), .ongoal("wrap"), .trigger("rising"), .behavior("new")) counter_5 (
    .Q(c4), .clk(in_6), .clr(d_ff_1_q));  // open: load, D, count, carry, preset, down
  D_Flip_Flop #(.trigger("rising"), .Pre_Clr_Positions("ABOVE_BELOW"), .NegatePresetClear("false"), .enable("false"), .NewFFLayout("false")) d_ff_1 (
    .clk(in_6), .D(or_5_out), .Q(d_ff_1_q));  // open: Qn, preset, reset
  or or_5 (or_5_out, write4, L4);
  Counter #(.width(16), .max('hffff), .ongoal("wrap"), .trigger("rising"), .behavior("new")) counter_6 (
    .Q(c5), .clk(in_6), .clr(d_ff_7_q));  // open: load, D, count, carry, preset, down
  or or_6 (or_6_out, write5, L5);
  Counter #(.width(16), .max('hffff), .ongoal("wrap"), .trigger("rising"), .behavior("new")) counter_7 (
    .Q(c6), .clk(in_6), .clr(d_ff_8_q));  // open: load, D, count, carry, preset, down
  or or_7 (or_7_out, write6, L6);
  Counter #(.width(16), .max('hffff), .ongoal("wrap"), .trigger("rising"), .behavior("new")) counter_8 (
    .Q(c7), .clk(in_6), .clr(d_ff_2_q));  // open: load, D, count, carry, preset, down
  D_Flip_Flop #(.trigger("rising"), .Pre_Clr_Positions("LEGACY"), .NegatePresetClear("false"), .enable("true"), .NewFFLayout("false")) d_ff_2 (
    .clk(in_6), .D(or_8_out), .Q(d_ff_2_q));  // open: Qn, preset, en, reset
  or or_8 (or_8_out, write7, L7);
  D_Flip_Flop #(.trigger("rising"), .Pre_Clr_Positions("ABOVE_BELOW"), .NegatePresetClear("false"), .enable("false"), .NewFFLayout("false")) d_ff_3 (
    .clk(in_6), .D(or_1_out), .Q(d_ff_3_q));  // open: Qn, preset, reset
  D_Flip_Flop #(.trigger("rising"), .Pre_Clr_Positions("ABOVE_BELOW"), .NegatePresetClear("false"), .enable("false"), .NewFFLayout("false")) d_ff_4 (
    .clk(in_6), .D(or_2_out), .Q(d_ff_4_q));  // open: Qn, preset, reset
  D_Flip_Flop #(.trigger("rising"), .Pre_Clr_Positions("ABOVE_BELOW"), .NegatePresetClear("false"), .enable("false"), .NewFFLayout("false")) d_ff_5 (
    .clk(in_6), .D(or_3_out), .Q(d_ff_5_q));  // open: Qn, preset, reset
  D_Flip_Flop #(.trigger("rising"), .Pre_Clr_Positions("ABOVE_BELOW"), .NegatePresetClear("false"), .enable("false"), .NewFFLayout("false")) d_ff_6 (
    .clk(in_6), .D(or_4_out), .Q(d_ff_6_q));  // open: Qn, preset, reset
  D_Flip_Flop #(.trigger("rising"), .Pre_Clr_Positions("ABOVE_BELOW"), .NegatePresetClear("false"), .enable("false"), .NewFFLayout("false")) d_ff_7 (
    .clk(in_6), .D(or_6_out), .Q(d_ff_7_q));  // open: Qn, preset, reset
  D_Flip_Flop #(.trigger("rising"), .Pre_Clr_Positions("LEGACY"), .NegatePresetClear("false"), .enable("true"), .NewFFLayout("false")) d_ff_8 (
    .clk(in_6), .D(or_7_out), .Q(d_ff_8_q));  // open: Qn, preset, en, reset
  Register #(.width(32), .trigger("rising"), .Select("low")) register_17 (
    .D(EX_BranchAddr), .en(write0), .Q(register_17_q), .clk(in_6));  // open: clr
  Register #(.width(32), .trigger("rising"), .Select("low")) register_18 (
    .D(EX_BranchAddr), .en(write1), .Q(register_18_q), .clk(in_6));  // open: clr
  Register #(.width(32), .trigger("rising"), .Select("low")) register_19 (
    .D(EX_BranchAddr), .en(write2), .Q(register_19_q), .clk(in_6));  // open: clr
  Register #(.width(32), .trigger("rising"), .Select("low")) register_20 (
    .D(EX_BranchAddr), .en(write3), .Q(register_20_q), .clk(in_6));  // open: clr
  Register #(.width(32), .trigger("rising"), .Select("low")) register_21 (
    .D(EX_BranchAddr), .en(write4), .Q(register_21_q), .clk(in_6));  // open: clr
  Register #(.width(32), .trigger("rising"), .Select("low")) register_22 (
    .D(EX_BranchAddr), .en(write5), .Q(register_22_q), .clk(in_6));  // open: clr
  Register #(.width(32), .trigger("rising"), .Select("low")) register_23 (
    .D(EX_BranchAddr), .en(write6), .Q(register_23_q), .clk(in_6));  // open: clr
  Register #(.width(32), .trigger("rising"), .Select("low")) register_24 (
    .D(EX_BranchAddr), .en(write7), .Q(register_24_q), .clk(in_6));  // open: clr
  assign BTB_JumpAddr = L0 ? register_17_q : 32'bz;  // Controlled_Buffer controlled_buffer_1
  assign BTB_JumpAddr = L1 ? register_18_q : 32'bz;  // Controlled_Buffer controlled_buffer_2
  assign BTB_JumpAddr = L2 ? register_19_q : 32'bz;  // Controlled_Buffer controlled_buffer_3
  assign BTB_JumpAddr = L3 ? register_20_q : 32'bz;  // Controlled_Buffer controlled_buffer_4
  assign BTB_JumpAddr = L4 ? register_21_q : 32'bz;  // Controlled_Buffer controlled_buffer_5
  assign BTB_JumpAddr = L5 ? register_22_q : 32'bz;  // Controlled_Buffer controlled_buffer_6
  assign BTB_JumpAddr = L6 ? register_23_q : 32'bz;  // Controlled_Buffer controlled_buffer_7
  assign BTB_JumpAddr = L7 ? register_24_q : 32'bz;  // Controlled_Buffer controlled_buffer_8
  Comparator #(.width(32), .mode("twosComplement")) comparator_1 (
    .a(tag0), .b(PC), .eq(comparator_1_eq));  // open: gt, lt
  Comparator #(.width(32), .mode("twosComplement")) comparator_2 (
    .a(tag1), .b(PC), .eq(comparator_2_eq));  // open: gt, lt
  Comparator #(.width(32), .mode("twosComplement")) comparator_3 (
    .a(tag2), .b(PC), .eq(comparator_3_eq));  // open: gt, lt
  Comparator #(.width(32), .mode("twosComplement")) comparator_4 (
    .a(tag3), .b(PC), .eq(comparator_4_eq));  // open: gt, lt
  Comparator #(.width(32), .mode("twosComplement")) comparator_5 (
    .a(tag4), .b(PC), .eq(comparator_5_eq));  // open: gt, lt
  Comparator #(.width(32), .mode("twosComplement")) comparator_6 (
    .a(tag5), .b(PC), .eq(comparator_6_eq));  // open: gt, lt
  Comparator #(.width(32), .mode("twosComplement")) comparator_7 (
    .a(tag6), .b(PC), .eq(comparator_7_eq));  // open: gt, lt
  Comparator #(.width(32), .mode("twosComplement")) comparator_8 (
    .a(tag7), .b(PC), .eq(comparator_8_eq));  // open: gt, lt
  and and_1 (L0, v0, comparator_1_eq);
  and and_2 (L1, v1, comparator_2_eq);
  and and_3 (L2, v2, comparator_3_eq);
  and and_4 (L3, v3, comparator_4_eq);
  and and_5 (L4, v4, comparator_5_eq);
  and and_6 (L5, v5, comparator_6_eq);
  and and_7 (L6, v6, comparator_7_eq);
  and and_8 (L7, v7, comparator_8_eq);
  Comparator #(.width(32), .mode("twosComplement")) comparator_9 (
    .a(tag0), .b(EX_PC), .eq(comparator_9_eq));  // open: gt, lt
  Comparator #(.width(32), .mode("twosComplement")) comparator_10 (
    .a(tag1), .b(EX_PC), .eq(comparator_10_eq));  // open: gt, lt
  Comparator #(.width(32), .mode("twosComplement")) comparator_11 (
    .a(tag2), .b(EX_PC), .eq(comparator_11_eq));  // open: gt, lt
  Comparator #(.width(32), .mode("twosComplement")) comparator_12 (
    .a(tag3), .b(EX_PC), .eq(comparator_12_eq));  // open: gt, lt
  Comparator #(.width(32), .mode("twosComplement")) comparator_13 (
    .a(tag4), .b(EX_PC), .eq(comparator_13_eq));  // open: gt, lt
  Comparator #(.width(32), .mode("twosComplement")) comparator_14 (
    .a(tag5), .b(EX_PC), .eq(comparator_14_eq));  // open: gt, lt
  Comparator #(.width(32), .mode("twosComplement")) comparator_15 (
    .a(tag6), .b(EX_PC), .eq(comparator_15_eq));  // open: gt, lt
  Comparator #(.width(32), .mode("twosComplement")) comparator_16 (
    .a(tag7), .b(EX_PC), .eq(comparator_16_eq));  // open: gt, lt
  and and_9 (M0, v0, comparator_9_eq);
  and and_10 (M1, v1, comparator_10_eq);
  and and_11 (M2, v2, comparator_11_eq);
  and and_12 (M3, v3, comparator_12_eq);
  and and_13 (M4, v4, comparator_13_eq);
  and and_14 (M5, v5, comparator_14_eq);
  and and_15 (M6, v6, comparator_15_eq);
  and and_16 (M7, v7, comparator_16_eq);
  not not_1 (not_1_out, v0);
  not not_2 (not_2_out, v1);
  not not_3 (not_3_out, v2);
  not not_4 (not_4_out, v3);
  not not_5 (not_5_out, v4);
  not not_6 (not_6_out, v5);
  not not_7 (not_7_out, v6);
  not not_8 (not_8_out, v7);
  MAX max_1 (.Y(c1), .X(c0), .Y_num(3'b001), .X_num(3'b000), .MAX(max_1_max), .Max_num(max_1_max_num));
  MAX max_2 (.Y(c3), .X(c2), .Y_num(3'b011), .X_num(3'b010), .MAX(max_2_max), .Max_num(max_2_max_num));
  MAX max_3 (.Y(c5), .X(c4), .Y_num(3'b101), .X_num(3'b100), .MAX(max_3_max), .Max_num(max_3_max_num));
  MAX max_4 (.Y(c7), .X(c6), .Y_num(3'b111), .X_num(3'b110), .MAX(max_4_max), .Max_num(max_4_max_num));
  or or_9 (EX_Hit, M0, M1, M2, M3, M4, M5, M6, M7);
  not not_9 (EX_Miss, EX_Hit);
  Priority_Encoder #(.select(3), .disabled("Z")) priority_encoder_1 (
    .in0(not_1_out), .in1(not_2_out), .in2(not_3_out), .in3(not_4_out), .in4(not_5_out), .in5(not_6_out),
    .in6(not_7_out), .in7(not_8_out), .out(priority_encoder_1_out), .gs(priority_encoder_1_gs));  // open: en_out, en_in
  MAX max_5 (
    .Y(max_2_max), .X(max_1_max), .Y_num(max_2_max_num), .X_num(max_1_max_num), .MAX(max_5_max),
    .Max_num(max_5_max_num));
  MAX max_6 (
    .Y(max_4_max), .X(max_3_max), .Y_num(max_4_max_num), .X_num(max_3_max_num), .MAX(max_6_max),
    .Max_num(max_6_max_num));
  and and_17 (and_17_out, v0, v1, v2, v3, v4, v5, v6, v7);
  Decoder #(.select(3), .tristate("false"), .disabled(0), .enable("true")) decoder_1 (
    .out0(decoder_1_out0), .out1(decoder_1_out1), .out2(decoder_1_out2), .out3(decoder_1_out3),
    .out4(decoder_1_out4), .out5(decoder_1_out5), .out6(decoder_1_out6), .out7(decoder_1_out7),
    .sel(priority_encoder_1_out), .en(priority_encoder_1_gs));
  Decoder #(.select(3), .tristate("false"), .disabled(0), .enable("true")) decoder_2 (
    .out0(decoder_2_out0), .out1(decoder_2_out1), .out2(decoder_2_out2), .out3(decoder_2_out3),
    .out4(decoder_2_out4), .out5(decoder_2_out5), .out6(decoder_2_out6), .out7(decoder_2_out7),
    .sel(max_7_max_num), .en(and_17_out));
  MAX max_7 (
    .Y(max_6_max), .X(max_5_max), .Y_num(max_6_max_num), .X_num(max_5_max_num), .Max_num(max_7_max_num));  // open: MAX
  or or_10 (or_10_out, decoder_1_out0, decoder_2_out0);
  or or_11 (or_11_out, decoder_1_out1, decoder_2_out1);
  or or_12 (or_12_out, decoder_1_out2, decoder_2_out2);
  or or_13 (or_13_out, decoder_1_out3, decoder_2_out3);
  or or_14 (or_14_out, decoder_1_out4, decoder_2_out4);
  or or_15 (or_15_out, decoder_1_out5, decoder_2_out5);
  or or_16 (or_16_out, decoder_1_out6, decoder_2_out6);
  or or_17 (or_17_out, decoder_1_out7, decoder_2_out7);
  and and_18 (write0, or_10_out, EX_Miss, EX_Branch);
  and and_19 (write1, or_11_out, EX_Miss, EX_Branch);
  and and_20 (write2, or_12_out, EX_Miss, EX_Branch);
  and and_21 (write3, or_13_out, EX_Miss, EX_Branch);
  and and_22 (write4, or_14_out, EX_Miss, EX_Branch);
  and and_23 (write5, or_15_out, EX_Miss, EX_Branch);
  and and_24 (write6, or_16_out, EX_Miss, EX_Branch);
  and and_25 (write7, or_17_out, EX_Miss, EX_Branch);
  assign {ID_PredictJump, controlled_buffer_9_out[0]} = L0 ? predict0 : 2'bz;  // Controlled_Buffer controlled_buffer_9
  assign {ID_PredictJump, controlled_buffer_10_out[0]} = L1 ? predict1 : 2'bz;  // Controlled_Buffer controlled_buffer_10
  assign {ID_PredictJump, controlled_buffer_11_out[0]} = L2 ? predict2 : 2'bz;  // Controlled_Buffer controlled_buffer_11
  assign {ID_PredictJump, controlled_buffer_12_out[0]} = L3 ? predict3 : 2'bz;  // Controlled_Buffer controlled_buffer_12
  assign {ID_PredictJump, controlled_buffer_13_out[0]} = L4 ? predict4 : 2'bz;  // Controlled_Buffer controlled_buffer_13
  assign {ID_PredictJump, controlled_buffer_14_out[0]} = L5 ? predict5 : 2'bz;  // Controlled_Buffer controlled_buffer_14
  assign {ID_PredictJump, controlled_buffer_15_out[0]} = L6 ? predict6 : 2'bz;  // Controlled_Buffer controlled_buffer_15
  assign {ID_PredictJump, controlled_buffer_16_out[0]} = L7 ? predict7 : 2'bz;  // Controlled_Buffer controlled_buffer_16
  Pull_Resistor #(.pull(0)) pull_resistor_1 (.node(ID_PredictJump));
  FSM fsm_1 (
    .high(predict0[1]), .low(predict0[0]), .jump(EX_Branched), .NextHigh(fsm_1_nextlow[1]),
    .NextLow(fsm_1_nextlow[0]));
  FSM fsm_2 (
    .high(predict1[1]), .low(predict1[0]), .jump(EX_Branched), .NextHigh(fsm_2_nextlow[1]),
    .NextLow(fsm_2_nextlow[0]));
  FSM fsm_3 (
    .high(predict2[1]), .low(predict2[0]), .jump(EX_Branched), .NextHigh(fsm_3_nextlow[1]),
    .NextLow(fsm_3_nextlow[0]));
  FSM fsm_4 (
    .high(predict3[1]), .low(predict3[0]), .jump(EX_Branched), .NextHigh(fsm_4_nextlow[1]),
    .NextLow(fsm_4_nextlow[0]));
  FSM fsm_5 (
    .high(predict4[1]), .low(predict4[0]), .jump(EX_Branched), .NextHigh(fsm_5_nextlow[1]),
    .NextLow(fsm_5_nextlow[0]));
  FSM fsm_6 (
    .high(predict5[1]), .low(predict5[0]), .jump(EX_Branched), .NextHigh(fsm_6_nextlow[1]),
    .NextLow(fsm_6_nextlow[0]));
  FSM fsm_7 (
    .high(predict6[1]), .low(predict6[0]), .jump(EX_Branched), .NextHigh(fsm_7_nextlow[1]),
    .NextLow(fsm_7_nextlow[0]));
  FSM fsm_8 (
    .high(predict7[1]), .low(predict7[0]), .jump(EX_Branched), .NextHigh(fsm_8_nextlow[1]),
    .NextLow(fsm_8_nextlow[0]));
  and and_26 (and_26_out, EX_Branch, M0);
  Register #(.width(2), .trigger("rising"), .Select("low")) register_25 (
    .D(fsm_1_nextlow), .en(and_26_out), .Q(predict0), .clk(in_6));  // open: clr
  and and_27 (and_27_out, EX_Branch, M1);
  Register #(.width(2), .trigger("rising"), .Select("low")) register_26 (
    .D(fsm_2_nextlow), .en(and_27_out), .Q(predict1), .clk(in_6));  // open: clr
  and and_28 (and_28_out, EX_Branch, M2);
  Register #(.width(2), .trigger("rising"), .Select("low")) register_27 (
    .D(fsm_3_nextlow), .en(and_28_out), .Q(predict2), .clk(in_6));  // open: clr
  and and_29 (and_29_out, EX_Branch, M3);
  Register #(.width(2), .trigger("rising"), .Select("low")) register_28 (
    .D(fsm_4_nextlow), .en(and_29_out), .Q(predict3), .clk(in_6));  // open: clr
  and and_30 (and_30_out, EX_Branch, M4);
  Register #(.width(2), .trigger("rising"), .Select("low")) register_29 (
    .D(fsm_5_nextlow), .en(and_30_out), .Q(predict4), .clk(in_6));  // open: clr
  and and_31 (and_31_out, EX_Branch, M5);
  Register #(.width(2), .trigger("rising"), .Select("low")) register_30 (
    .D(fsm_6_nextlow), .en(and_31_out), .Q(predict5), .clk(in_6));  // open: clr
  and and_32 (and_32_out, EX_Branch, M6);
  Register #(.width(2), .trigger("rising"), .Select("low")) register_31 (
    .D(fsm_7_nextlow), .en(and_32_out), .Q(predict6), .clk(in_6));  // open: clr
  and and_33 (and_33_out, EX_Branch, M7);
  Register #(.width(2), .trigger("rising"), .Select("low")) register_32 (
    .D(fsm_8_nextlow), .en(and_33_out), .Q(predict7), .clk(in_6));  // open: clr

  // Other names for the same wires on the sheet: CLK = in_6; Tag[31:0] = EX_PC

  // Notes on the sheet:
  //   EX写入逻辑
  //   历史预测位
  //   与PC比较数据命中  选择L而不是M
  //   EX.PC如果数据命中，需要根据EX.Branched的值依据预测位状态机更新分支预测历史位的值
endmodule

module FSM (
  input  high,
  input  low,
  input  jump,
  output NextHigh,
  output NextLow
);

  wire and_1_out, and_2_out, and_3_out, and_4_out, not_1_out, not_2_out, not_3_out, not_4_out, not_5_out;

  not not_1 (not_1_out, low);
  not not_2 (not_2_out, high);
  not not_3 (not_3_out, low);
  not not_4 (not_4_out, low);
  not not_5 (not_5_out, jump);
  and and_1 (and_1_out, low, jump);
  and and_2 (and_2_out, high, not_1_out);
  and and_3 (and_3_out, not_2_out, not_3_out, jump);
  and and_4 (and_4_out, high, not_4_out, not_5_out);
  or or_1 (NextHigh, and_1_out, and_2_out);
  or or_2 (NextLow, and_3_out, and_4_out);
endmodule

module MAX (
  input  [15:0] Y,
  input  [15:0] X,
  input  [2:0] Y_num,
  input  [2:0] X_num,
  output [15:0] MAX,
  output [2:0] Max_num
);

  wire comparator_1_eq, comparator_1_gt, or_1_out;

  Comparator #(.width(16), .mode("unsigned")) comparator_1 (
    .a(X), .b(Y), .gt(comparator_1_gt), .eq(comparator_1_eq));  // open: lt
  Multiplexer #(.select(1), .width(16), .disabled("Z"), .enable("false")) multiplexer_1 (
    .in0(Y), .in1(X), .out(MAX), .sel(or_1_out));
  or or_1 (or_1_out, comparator_1_gt, comparator_1_eq);
  Multiplexer #(.select(1), .width(3), .disabled("Z"), .enable("false")) multiplexer_2 (
    .in0(Y_num), .in1(X_num), .out(Max_num), .sel(or_1_out));

  // Notes on the sheet:
  //   输出两个输入中的较大值，并输出较大值的3位编号
endmodule

module \重定向分支预测  (
  output RegWrite,
  output MemWrite,
  output [31:0] IF_PC,
  output [31:0] ID_PC,
  output [31:0] EX_PC,
  output [31:0] M_PC,
  output [31:0] WB_PC,
  output [31:0] RDin,
  output [31:0] MDin,
  output [31:0] LedData
);

  wire alu_1_p2, alu_1_p6, alu_1_p7, and_1_out, and_5_out, and_6_out, and_7_out, and_8_out, and_9_out,
       and_10_out, and_11_out, and_12_out, and_13_out, and_14_out, branch, branchtaken, CLK, clock_1_out,
       comparator_1_eq, comparator_1_lt, comparator_2_eq, comparator_3_eq, comparator_4_eq, comparator_5_eq,
       comparator_6_eq, comparator_7_eq, comparator_8_eq, comparator_9_eq, comparator_10_eq,
       comparator_11_eq, comparator_12_eq, comparator_13_eq, comparator_14_eq, comparator_15_eq, d_ff_1_q,
       ecall, ecall2, EX_beq, EX_blt, EX_bne, EX_jal, EX_jalr, ex_mem2_1_jalout, ex_mem2_1_jalrout,
       ex_mem2_1_memtoreg_2, EX_MemToReg, EX_PredictJump, EX_RegWrite, ex_sb, Go, H, halt, halt1, halt2,
       ID_bubble, ID_PredictJump, id_sb, IF_bubble, IF_PredictJump, IF_stop, IR1, IR2, IR3, jAL, JJ, loaduse,
       MEM_RegWrite, mem_sb, mem_wb2_1_jalout, mem_wb2_1_jalrout, mem_wb2_1_memtoreg_2, multiplexer_3_out,
       multiplexer_4_out, nand_1_out, not_1_out, not_2_out, not_3_out, not_5_out, not_6_out, not_7_out,
       not_8_out, not_9_out, not_10_out, not_11_out, not_12_out, not_14_out, not_15_out, not_16_out,
       not_17_out, or_4_out, RST, RsUsed, RtUsed, s, ss, W1, W2, W3;
  wire [1:0] ex_RsF, ex_RtF, multiplexer_17_out, multiplexer_19_out, RsForward, RtForward;
  wire [2:1] JJUin, signalout;
  wire [2:2] JJUout;
  wire [3:0] id_ex3_1_aluopout, \单周期硬布线控制器_1_alu_op ;
  wire [4:0] EXW, MEMW, rs, rt, W_F;
  wire [6:0] signalin;
  wire [11:0] multiplexer_7_out;
  wire [12:0] CNT_num;
  wire [15:0] \LoadUse次数 , \总周期数 , \插入气泡数 , \无条件分支数 , \条件分支成功数 ;
  wire [31:0] adder_3_out, alu_1_p8, bit_extender_1_out, bit_extender_2_out, bit_extender_3_out,
       btb_1_btb_jumpaddr, EX_BranchAddr, EX_IR, EX_PC_4, id_ex3_1_b_imm_2, id_ex3_1_i_s_imm_2,
       id_ex3_1_j_imm_2, ID_IR, IF_IR, IF_PC_4, IR, mem_a, MEM_IR, mem_wb2_1_alu_result_2,
       mem_wb2_1_memdata_2, multiplexer_1_out, multiplexer_2_out, multiplexer_11_out, multiplexer_12_out,
       multiplexer_13_out, PC_F, PredictAddr, R1, R2, R11, R22, ram_1_dout, \regifile_下降沿_1_r1 ,
       \regifile_下降沿_1_r2 , rom_1_data, shifter_1_out, wb_a, WB_IR;

  Button \u_总复位  (.out(RST));
  Button _1 (.out(IR1));
  Button _2 (.out(IR2));
  Button _3 (.out(IR3));
  // Probe on \总周期数 
  // Probe on \总周期数 
  Button \u_继续运行  (.out(Go));
  LED #(.active("true")) led_1 (.in(W1));
  LED #(.active("true")) led_2 (.in(W2));
  LED #(.active("true")) led_3 (.in(W3));
  not not_1 (not_1_out, halt2);
  or or_1 (branchtaken, EX_jal, EX_jalr, or_4_out);
  Multiplexer #(.select(1), .width(32), .disabled("Z"), .enable("false")) multiplexer_1 (
    .in0(EX_PC_4), .in1(EX_BranchAddr), .out(multiplexer_1_out), .sel(branchtaken));
  Multiplexer #(.select(1), .width(32), .disabled("Z"), .enable("false")) multiplexer_2 (
    .in0(PredictAddr), .in1(multiplexer_1_out), .out(multiplexer_2_out), .sel(IF_bubble));
  not not_2 (not_2_out, loaduse);
  Hex_Digit_Display hex_digit_display_1 (.value(LedData[31:28]));  // open: dp
  // Probe on IF_PC[19:0]
  // RiscV_Probe riscv_probe_1: pin names not known; wires that end beside it: IF_IR
  Counter #(.width(16), .max('hffff), .ongoal("wrap"), .trigger("rising"), .behavior("new")) counter_1 (
    .count(not_1_out), .Q(\总周期数 ), .clk(CLK));  // open: load, D, carry, clr, preset, down
  Register #(.width(32), .trigger("rising"), .Select("low")) PC (
    .D(multiplexer_2_out), .en(and_1_out), .Q(IF_PC), .clk(CLK), .clr(RST));
  and and_1 (and_1_out, not_2_out, H);
  Adder #(.width(32)) adder_1 (.a(IF_PC), .b(32'h4), .out(IF_PC_4));  // open: cin, cout
  Hex_Digit_Display hex_digit_display_2 (.value(LedData[27:24]));  // open: dp
  Hex_Digit_Display hex_digit_display_3 (.value(LedData[23:20]));  // open: dp
  // Probe on ID_PC[19:0]
  // RiscV_Probe riscv_probe_2: pin names not known; wires that end beside it: ID_IR
  Hex_Digit_Display hex_digit_display_4 (.value(LedData[15:12]));  // open: dp
  Hex_Digit_Display hex_digit_display_5 (.value(LedData[19:16]));  // open: dp
  not not_3 (not_3_out, loaduse);
  Adder #(.width(32)) adder_2 (.a(EX_PC), .b(32'h4), .out(EX_PC_4));  // open: cin, cout
  Multiplexer #(.select(1), .width(1), .disabled("Z"), .enable("false")) multiplexer_3 (
    .in0(IF_PredictJump), .in1(1'b0), .out(multiplexer_3_out), .sel(IF_bubble));
  Multiplexer #(.select(1), .width(1), .disabled("Z"), .enable("false")) multiplexer_4 (
    .in0(ID_PredictJump), .in1(1'b0), .out(multiplexer_4_out), .sel(ID_bubble));
  Hex_Digit_Display hex_digit_display_6 (.value(LedData[11:8]));  // open: dp
  Hex_Digit_Display hex_digit_display_7 (.value(LedData[7:4]));  // open: dp
  // Probe on EX_PC[19:0]
  // RiscV_Probe riscv_probe_3: pin names not known; wires that end beside it: EX_IR
  // RiscV_Probe riscv_probe_4: pin names not known; wires that end beside it: IF_PC[11:2], IR
  ROM #(.addrWidth(10), .dataWidth(32), .Select("high")) rom_1 (.addr(IF_PC[11:2]), .data(rom_1_data));
  and and_2 (IF_stop, not_3_out, H);
  Register #(.width(1), .trigger("rising"), .Select("low")) register_1 (
    .D(multiplexer_3_out), .en(IF_stop), .Q(ID_PredictJump), .clk(CLK));  // open: clr
  Register #(.width(1), .trigger("rising"), .Select("low")) register_2 (
    .D(multiplexer_4_out), .en(H), .Q(EX_PredictJump), .clk(CLK));  // open: clr
  Hex_Digit_Display hex_digit_display_8 (.value(LedData[3:0]));  // open: dp
  IF_ID2 if_id2_1 (
    .IRin(rom_1_data), .PCin(IF_PC), .clk(CLK), .bubble(IF_bubble), .stop(IF_stop), .IRout(IR), .PCout(ID_PC));
  or or_2 (branch, EX_jalr, EX_jal, EX_beq, EX_bne, EX_blt);
  // Probe on \总周期数 
  // Probe on M_PC[19:0]
  // RiscV_Probe riscv_probe_5: pin names not known; wires that end beside it: MEM_IR
  // Probe on \总周期数 
  // Probe on \无条件分支数 
  // Probe on \条件分支成功数 
  // Probe on \插入气泡数 
  // Probe on \LoadUse次数 
  \单周期硬布线控制器  \u_单周期硬布线控制器_1  (
    .Funct({IR[30], IR[25], IR[14:12]}), .OP(IR[6:2]), .ALU_OP(\单周期硬布线控制器_1_alu_op ), .MemToReg(signalin[3]),
    .MemWrite(signalin[2]), .ALU_SRC(signalin[1]), .RegWrite(signalin[0]), .ecall(ecall), .S_type(s),
    .Jalr(JJUin[1]), .Beq(signalin[6]), .JAL(jAL), .Bne(signalin[4]), .in_3(IR[21]), .uret(JJUin[2]),
    .blt(signalin[5]), .sb(id_sb));  // open: csrrsi, csrrci
  // Probe on IF_PC[11:0]
  // Probe on WB_PC[19:0]
  // RiscV_Probe riscv_probe_6: pin names not known; wires that end beside it: WB_IR
  Multiplexer #(.select(1), .width(5), .disabled("Z"), .enable("false")) multiplexer_5 (
    .in0(IR[19:15]), .in1(5'b10001), .out(rs), .sel(ecall));
  Multiplexer #(.select(1), .width(5), .disabled("Z"), .enable("false")) multiplexer_6 (
    .in0(IR[24:20]), .in1(5'b01010), .out(rt), .sel(ecall));
  Multiplexer #(.select(1), .width(12), .disabled("Z"), .enable("false")) multiplexer_7 (
    .in0(IR[31:20]), .in1({IR[31:25], IR[11:7]}), .out(multiplexer_7_out), .sel(s));
  assign bit_extender_1_out = {{20{IR[31]}}, {IR[31], IR[7], IR[30:25], IR[11:8]}};  // Bit_Extender bit_extender_1
  assign bit_extender_2_out = {{12{IR[31]}}, {IR[31], IR[19:12], IR[20], IR[30:21]}};  // Bit_Extender bit_extender_2
  Multiplexer #(.select(1), .width(32), .disabled("Z"), .enable("false")) multiplexer_8 (
    .in0(wb_a), .in1(PC_F), .out(RDin), .sel(JJ));
  // Probe on EX_PC[11:0]
  // Probe on ID_PC[11:0]
  \Regifile_下降沿  \regifile_下降沿_1  (
    .Din(RDin), .Clk(CLK), .R1(\regifile_下降沿_1_r1 ), .R2(\regifile_下降沿_1_r2 ), .WE(RegWrite), .W_num(W_F),
    .R1_num(rs), .R2_num(rt));
  assign bit_extender_3_out = {{20{multiplexer_7_out[11]}}, multiplexer_7_out};  // Bit_Extender bit_extender_3
  // Probe on M_PC[11:0]
  D_Flip_Flop #(.trigger("high"), .Pre_Clr_Positions("LEGACY"), .NegatePresetClear("false"), .enable("true"), .NewFFLayout("false")) d_ff_1 (.Q(d_ff_1_q));  // open: clk, D, Qn, preset, en, reset
  // Probe on 13'hc
  BTB btb_1 (
    .PC(IF_PC), .EX_PC(EX_PC), .EX_BranchAddr(EX_BranchAddr), .EX_Branch(branch), .EX_Branched(branchtaken),
    .in_6(CLK), .ID_PredictJump(IF_PredictJump), .BTB_JumpAddr(btb_1_btb_jumpaddr));
  // Probe on WB_PC[11:0]
  Comparator #(.width(13), .mode("twosComplement")) comparator_1 (
    .a(CNT_num), .b(13'hc), .eq(comparator_1_eq), .lt(comparator_1_lt));  // open: gt
  Clock #(.highDuration(1), .lowDuration(1)) clock_1 (.out(clock_1_out));
  or or_3 (ID_bubble, loaduse, IF_bubble);
  not not_4 (IF_bubble, comparator_2_eq);
  Comparator #(.width(1), .mode("twosComplement")) comparator_2 (
    .a(branchtaken), .b(EX_PredictJump), .eq(comparator_2_eq));  // open: gt, lt
  nand nand_1 (nand_1_out, d_ff_1_q, comparator_1_eq);
  Counter #(.width(13), .max('h1fff), .ongoal("stay"), .trigger("rising"), .behavior("old")) counter_2 (
    .count(comparator_1_lt), .Q(CNT_num), .clk(clock_1_out));  // open: load, D, carry, clr, preset
  ID_EX3 id_ex3_1 (
    .signal(signalin), .ecall(ecall), .JJU({JJUin, jAL}), .AluOp(\单周期硬布线控制器_1_alu_op ),
    .R1(\regifile_下降沿_1_r1 ), .R2(\regifile_下降沿_1_r2 ), .I_S_imm(bit_extender_3_out),
    .B_imm(bit_extender_1_out), .J_imm(bit_extender_2_out), .PCin(ID_PC), .WriteReg_num(IR[11:7]),
    .RsForward(RsForward), .RtForward(RtForward), .CLK(CLK), .bubble(ID_bubble), .stop(H),
    .signalout({EX_beq, EX_blt, EX_bne, EX_MemToReg, signalout, EX_RegWrite}), .ecallout(ecall2),
    .JJUout({JJUout[2], EX_jalr, EX_jal}), .AluOpout(id_ex3_1_aluopout), .R1_2(R1), .R2_2(R2),
    .I_S_imm_2(id_ex3_1_i_s_imm_2), .B_imm_2(id_ex3_1_b_imm_2), .J_imm_2(id_ex3_1_j_imm_2), .PCout(EX_PC),
    .WriteReg_num_2(EXW), .RsForward_2(ex_RsF), .RtForward_2(ex_RtF), .sb(id_sb), .sb_2(ex_sb));
  Multiplexer #(.select(2), .width(32), .disabled("Z"), .enable("false")) multiplexer_9 (
    .in0(R1), .in1(wb_a), .in2(mem_a), .out(R11), .sel(ex_RsF));  // open: in3
  Multiplexer #(.select(1), .width(32), .disabled("Z"), .enable("false")) multiplexer_10 (
    .in0(IF_PC_4), .in1(btb_1_btb_jumpaddr), .out(PredictAddr), .sel(IF_PredictJump));
  assign CLK = nand_1_out ? clock_1_out : 1'bz;  // Controlled_Buffer controlled_buffer_1
  Multiplexer #(.select(1), .width(32), .disabled("Z"), .enable("false")) multiplexer_11 (
    .in0(id_ex3_1_j_imm_2), .in1(id_ex3_1_b_imm_2), .out(multiplexer_11_out), .sel(or_4_out));
  Pull_Resistor #(.pull(1)) pull_resistor_1 (.node(CLK));
  Multiplexer #(.select(1), .width(32), .disabled("Z"), .enable("false")) multiplexer_12 (
    .in0(R22), .in1(id_ex3_1_i_s_imm_2), .out(multiplexer_12_out), .sel(signalout[1]));
  Multiplexer #(.select(1), .width(32), .disabled("Z"), .enable("false")) multiplexer_13 (
    .in0(LedData), .in1(R22), .out(multiplexer_13_out), .sel(ss));
  Comparator #(.width(32), .mode("twosComplement")) comparator_3 (
    .a(32'h22), .b(R11), .eq(comparator_3_eq));  // open: gt, lt
  and and_3 (ss, comparator_3_eq, ecall2);
  not not_5 (not_5_out, comparator_3_eq);
  and and_4 (halt, not_5_out, ecall2);
  not not_6 (not_6_out, alu_1_p6);
  // ALU alu_1: pin names not known; wires that end beside it: R11, alu_1_p2, multiplexer_12_out, alu_1_p2, id_ex3_1_aluopout, alu_1_p6, alu_1_p7, alu_1_p8
  Shifter #(.width(32), .shift("ll")) shifter_1 (.in(multiplexer_11_out), .\dist (5'b00001), .out(shifter_1_out));
  Multiplexer #(.select(2), .width(32), .disabled("Z"), .enable("false")) multiplexer_14 (
    .in0(R2), .in1(wb_a), .in2(mem_a), .out(R22), .sel(ex_RtF));  // open: in3
  Comparator #(.width(5), .mode("twosComplement")) comparator_4 (
    .a(rs), .b({5{1'b0}}), .eq(comparator_4_eq));  // open: gt, lt
  not not_7 (not_7_out, comparator_4_eq);
  Comparator #(.width(5), .mode("twosComplement")) comparator_5 (
    .a(rs), .b(EXW), .eq(comparator_5_eq));  // open: gt, lt
  not not_8 (not_8_out, comparator_6_eq);
  Comparator #(.width(5), .mode("twosComplement")) comparator_6 (
    .a(rs), .b({5{1'b0}}), .eq(comparator_6_eq));  // open: gt, lt
  Comparator #(.width(5), .mode("twosComplement")) comparator_7 (
    .a(rs), .b(MEMW), .eq(comparator_7_eq));  // open: gt, lt
  and and_5 (and_5_out, EX_blt, alu_1_p7);
  and and_6 (and_6_out, EX_bne, not_6_out);
  and and_7 (and_7_out, EX_beq, alu_1_p6);
  Adder #(.width(32)) adder_3 (.a(shifter_1_out), .b(EX_PC), .out(adder_3_out));  // open: cin, cout
  or or_4 (or_4_out, and_6_out, and_5_out, and_7_out);
  EX_MEM2 ex_mem2_1 (
    .JALin(EX_jal), .JALRin(EX_jalr), .RegWrite(EX_RegWrite), .MemToReg(EX_MemToReg),
    .MemWrite(signalout[2]), .Write_Data(R22), .ALU_Result(alu_1_p8), .WriteReg_num(EXW), .PCin(EX_PC),
    .haltin(halt), .CLK(CLK), .bubble(1'b0), .stop(H), .JALout(ex_mem2_1_jalout),
    .JALRout(ex_mem2_1_jalrout), .RegWrite_2(MEM_RegWrite), .MemToReg_2(ex_mem2_1_memtoreg_2),
    .MemWrite_2(MemWrite), .Write_Data_2(MDin), .ALU_Result_2(mem_a), .WriteReg_num_2(MEMW), .PCout(M_PC),
    .haltout(halt1), .sb(ex_sb), .sb_2(mem_sb));
  Multiplexer #(.select(1), .width(32), .disabled("Z"), .enable("false")) multiplexer_15 (
    .in0(adder_3_out), .in1(alu_1_p8), .out(EX_BranchAddr), .sel(EX_jalr));
  and and_8 (and_8_out, EX_RegWrite, RsUsed, not_7_out, comparator_5_eq);
  and and_9 (and_9_out, MEM_RegWrite, RsUsed, not_8_out, comparator_7_eq);
  Register #(.width(32), .trigger("rising"), .Select("low")) register_3 (
    .D(multiplexer_13_out), .en(ss), .Q(LedData), .clk(CLK));  // open: clr
  Multiplexer #(.select(1), .width(2), .disabled("Z"), .enable("false")) multiplexer_16 (
    .in0(multiplexer_17_out), .in1(2'b10), .out(RsForward), .sel(and_8_out));
  Multiplexer #(.select(1), .width(2), .disabled("Z"), .enable("false")) multiplexer_17 (
    .in0(2'b00), .in1(2'b01), .out(multiplexer_17_out), .sel(and_9_out));
  RAM ram_1 (
    .Mode(mem_sb), .\字节地址 (mem_a[11:0]), .Din(MDin), .CLK(CLK), .str(MemWrite), .id(not_9_out),
    .Dout(ram_1_dout));
  not not_9 (not_9_out, MemWrite);
  MEM_WB2 mem_wb2_1 (
    .halt(halt1), .JAL(ex_mem2_1_jalout), .JALR(ex_mem2_1_jalrout), .RegWrite(MEM_RegWrite),
    .MemToReg(ex_mem2_1_memtoreg_2), .ALU_Result(mem_a), .MemData(ram_1_dout), .WriteReg_num(MEMW),
    .PC(M_PC), .CLK(CLK), .bubble(1'b0), .stop(H), .haltout(halt2), .JALout(mem_wb2_1_jalout),
    .JALRout(mem_wb2_1_jalrout), .RegWrite_2(RegWrite), .MemToReg_2(mem_wb2_1_memtoreg_2),
    .ALU_Result_2(mem_wb2_1_alu_result_2), .MemData_2(mem_wb2_1_memdata_2), .WriteReg_num_2(W_F),
    .PCout(WB_PC));
  Multiplexer #(.select(1), .width(32), .disabled("Z"), .enable("false")) multiplexer_18 (
    .in0(mem_wb2_1_alu_result_2), .in1(mem_wb2_1_memdata_2), .out(wb_a), .sel(mem_wb2_1_memtoreg_2));
  Comparator #(.width(5), .mode("twosComplement")) comparator_8 (
    .a(rt), .b({5{1'b0}}), .eq(comparator_8_eq));  // open: gt, lt
  not not_10 (not_10_out, comparator_8_eq);
  Comparator #(.width(5), .mode("twosComplement")) comparator_9 (
    .a(rt), .b(EXW), .eq(comparator_9_eq));  // open: gt, lt
  not not_11 (not_11_out, comparator_10_eq);
  Comparator #(.width(5), .mode("twosComplement")) comparator_10 (
    .a(rt), .b({5{1'b0}}), .eq(comparator_10_eq));  // open: gt, lt
  Comparator #(.width(5), .mode("twosComplement")) comparator_11 (
    .a(rt), .b(MEMW), .eq(comparator_11_eq));  // open: gt, lt
  or or_5 (JJ, mem_wb2_1_jalout, mem_wb2_1_jalrout);
  Adder #(.width(32)) adder_4 (.a(WB_PC), .b(32'h4), .out(PC_F));  // open: cin, cout
  or or_6 (H, not_12_out, Go);
  not not_12 (not_12_out, halt2);
  and and_10 (and_10_out, EX_RegWrite, RtUsed, not_10_out, comparator_9_eq);
  and and_11 (and_11_out, MEM_RegWrite, RtUsed, not_11_out, comparator_11_eq);
  Multiplexer #(.select(1), .width(2), .disabled("Z"), .enable("false")) multiplexer_19 (
    .in0(2'b00), .in1(2'b01), .out(multiplexer_19_out), .sel(and_11_out));
  Multiplexer #(.select(1), .width(2), .disabled("Z"), .enable("false")) multiplexer_20 (
    .in0(multiplexer_19_out), .in1(2'b10), .out(RtForward), .sel(and_10_out));
  not not_13 (RsUsed, jAL);
  not not_14 (not_14_out, signalin[1]);
  and and_12 (and_12_out, not_14_out, not_15_out);
  not not_15 (not_15_out, jAL);
  or or_7 (RtUsed, s, and_12_out);
  Comparator #(.width(5), .mode("twosComplement")) comparator_12 (
    .a(rs), .b({5{1'b0}}), .eq(comparator_12_eq));  // open: gt, lt
  Comparator #(.width(5), .mode("twosComplement")) comparator_13 (
    .a(rs), .b(EXW), .eq(comparator_13_eq));  // open: gt, lt
  Comparator #(.width(5), .mode("twosComplement")) comparator_14 (
    .a(rt), .b({5{1'b0}}), .eq(comparator_14_eq));  // open: gt, lt
  Comparator #(.width(5), .mode("twosComplement")) comparator_15 (
    .a(EXW), .b(rt), .eq(comparator_15_eq));  // open: gt, lt
  not not_16 (not_16_out, comparator_12_eq);
  not not_17 (not_17_out, comparator_14_eq);
  and and_13 (and_13_out, EX_MemToReg, RsUsed, not_16_out, comparator_13_eq);
  and and_14 (and_14_out, EX_MemToReg, not_17_out, comparator_15_eq, RtUsed);
  or or_8 (loaduse, and_13_out, and_14_out);

  // Other names for the same wires on the sheet: W_num[4:0] = IR[11:7]; ID_stop = H; JJUin[0] = jAL;
  //   JJUout[1:0] = {EX_jalr, EX_jal}; JALR = EX_jalr; MEM_PC[31:0] = M_PC; PC[31:0] = IF_PC;
  //   Predicterror = IF_bubble; src = signalin[1];
  //   signalout (some bits) = {EX_beq, EX_blt, EX_bne, EX_MemToReg, EX_RegWrite}; 跳转addr[31:0] = EX_BranchAddr

  // Notes on the sheet:
  //   中断源
  //   时空图监测，可删除
  //   中断等待指示
  //   数码管输出
  //   指令探针
  //   指令存储器
  //   contents of rom_1 (hex, n*v repeats v):
  //   100493 100006f 100493 200913 300993 100006f 100493 200913 300993 100006f 100493 200913 300993
  //   100006f 100493 200913 300993 3ac000ef 100413 100493 1f49493 900533 2200893 73 24d493 48463 fedff06f
  //   900533 2200893 73 100493 249493 900533 2200893 73 48463 fedff06f 100493 1f49493 900533 2200893 73
  //   4034d493 900533 2200893 73 4044d493 900533 2200893 73 4044d493 900533 2200893 73 4044d493 900533
  //   2200893 73 4044d493 900533 2200893 73 4044d493 900533 2200893 73 4044d493 900533 2200893 73 4044d493
  //   900533 2200893 73 100413 1f41993 41f9d993 433 c00913 300b13 140413 f47413 800293 100313 499993
  //   89e9b3 1300533 2200893 73 406282b3 fe0294e3 140413 f00f93 1f47433 1c41413 800293 100313 49d993
  //   89e9b3 1300533 2200893 73 406282b3 fe0294e3 1c45413 406b0b33 b0463 f95ff06f 2b3 fff2c293 829293
  //   ff2e293 500533 2200893 73 fff00413 493 84a023 140413 448493 84a023 140413 448493 84a023 140413
  //   448493 84a023 140413 448493 84a023 140413 448493 84a023 140413 448493 84a023 140413 448493 84a023
  //   140413 448493 84a023 140413 448493 84a023 140413 448493 84a023 140413 448493 84a023 140413 448493
  //   84a023 140413 448493 84a023 140413 448493 84a023 140413 448493 84a023 140413 448493 140413 433
  //   3c00493 42983 4aa03 149a2b3 28663 134a023 1442023 ffc48493 fe9412e3 800533 2200893 73 440413 3c00493
  //   fc9416e3 3200893 73 100293 300313 800493 849493 7648493 1449493 900533 2200893 73 800e13 54d4b3
  //   64d4b3 900533 2200893 73 fffe0e13 fe0e14e3 a00893 73 fff00293 7700493 849493 7748493 900533 2200893
  //   73 1000e13 54c4b3 900533 2200893 73 fffe0e13 fe0e16e3 a00893 73 313 2000e13 493 100913 930023 900533
  //   2200893 73 12484b3 130313 fffe0e13 fe0e12e3 800e13 313 32483 900533 2200893 73 430313 fffe0e13
  //   fe0e14e3 a00893 73 ff100493 900533 2200893 73 148493 fe04c8e3 a00893 73 a00893 73 413 140413 800533
  //   2200893 73 240413 800533 2200893 73 340413 800533 2200893 73 440413 800533 2200893 73 540413 800533
  //   2200893 73 640413 800533 2200893 73 740413 800533 2200893 73 840413 800533 2200893 2200893 73 8067
  //   JAL
  //   JALR
  //   Beq
  //   Bne
  //   URET
  //   MemToReg
  //   MemWrite
  //   AluOP
  //   AluSrcB
  //   RegWrite
  //   控制位
  //   流水调试日志用
  //   暂停节拍，不能为0
  //   可计数暂停的时钟源
  //   为方便自动评测，需要输出流水线各段保存的PC值，注意是PC不是PC+4，另外ID段寄存器写入信息，Mem段内存写入信息也要输出
  //   数据存储器
endmodule

// Regifile
module \Regifile_下降沿  (
  input  [31:0] Din,
  input  Clk,
  input  WE,
  input  [4:0] R1_num,
  input  [4:0] W_num,
  input  [4:0] R2_num,
  output [31:0] R1,
  output [31:0] R2
);

  // RegisterFile registerfile_1: pin names not known; wires that end beside it: Din, Clk, WE, W_num, R1_num, R2_num, R1, R2
endmodule
