// Logisim project 走迷宫.circ as structural Verilog: 15 circuits, main circuit ◇单周期RISC-V
module \单周期RISC_V  (
  input  IR1,
  input  IR2,
  input  IR3,
  input  IR4,
  input  IR5,
  input  IR6,
  input  RST,
  input  CLK,
  output ecall,
  output [9:0] ADDR,
  output [4:0] W_num,
  output MemWrite,
  output [31:0] RDin,
  output [31:0] v0,
  output [31:0] MDin,
  output RegWrite
);

  wire ALU, ALU_t, ALU_t_t, and_2_out, and_3_out, and_4_out, and_5_out, and_6_out, and_7_out, and_8_out,
       and_9_out, and_10_out, and_11_out, and_13_out, and_14_out, Beq, BGE, Bne, clear1, clear2, clear3,
       clear4, clear5, clear6, clock_1_out, comparator_1_eq, comparator_2_eq, comparator_3_eq,
       comparator_3_lt, controlled_buffer_1_out, CSRRCI, CSRRSI, d_ff_1_q, d_ff_2_q, d_ff_3_q, d_ff_4_q,
       d_ff_5_q, d_ff_6_q, d_ff_8_q, Go, halt, IE, INT, INTRequest, IR1_q, IR1_t, IR2_q, IR2_t, IR3_q, IR3_t,
       IR4_q, IR4_t, IR5_q, IR5_t, IR6_q, IR6_t, IRA, IRB, IRC, IRD, IRE, IRF, JAL, JALR, LUI, mips_ram_1_p7,
       nand_1_out, not_1_out, not_2_out, or_7_out, or_8_out, or_9_out, or_10_out, or_11_out, or_12_out,
       or_13_out, SH, SLTIU, URET, W1, W2, W3, W4, W5, W6, \单周期硬布线控制器_1_alu_src , \单周期硬布线控制器_1_s_type ;
  wire [1:0] priority_encoder_1_out, \单周期硬布线控制器_1_memtoreg ;
  wire [2:0] INTnum, register_1_q;
  wire [3:0] mips_ram_1_p4, \单周期硬布线控制器_1_alu_op ;
  wire [3:1] multiplexer_15_out;
  wire [4:0] multiplexer_4_out, multiplexer_5_out;
  wire [11:0] multiplexer_8_out;
  wire [12:0] CNT_num;
  wire [15:0] \总周期数 ;
  wire [31:0] ALUresult, and_1_out, B_ADD, bit_extender_1_out, bit_extender_2_out, bit_extender_3_out,
       INT_PC, IR, JAL_ADD, LedData, mips_ram_1_p8, multiplexer_2_out, multiplexer_3_out, multiplexer_7_out,
       multiplexer_9_out, multiplexer_11_out, multiplexer_13_out, PC, PC_4, regifile_1_r2, RET_PC, Scene,
       shifter_1_out, shifter_2_out, shifter_3_out;

  Button \u_继续运行  (.out(Go));
  Button _1 (.out(IRA));
  Button _2 (.out(IRB));
  Button _3 (.out(IRC));
  Button _4 (.out(IRD));
  Button _5 (.out(IRE));
  Button _6 (.out(IRF));
  LED #(.active("true")) led_1 (.in(W1));
  LED #(.active("true")) led_2 (.in(W2));
  LED #(.active("true")) led_3 (.in(W3));
  LED #(.active("true")) led_4 (.in(W4));
  LED #(.active("true")) led_5 (.in(W5));
  LED #(.active("true")) led_6 (.in(W6));
  Hex_Digit_Display hex_digit_display_1 (.value(LedData[31:28]));  // open: dp
  Hex_Digit_Display hex_digit_display_2 (.value(LedData[23:20]));  // open: dp
  Hex_Digit_Display hex_digit_display_3 (.value(LedData[27:24]));  // open: dp
  assign and_1_out = 32'hfffffffe & {ALUresult[31:12], ADDR, ALUresult[1:0]};  // AND_Gate and_1, 32 bits wide
  or or_1 (W1, IR1_q, d_ff_1_q);
  or or_2 (W2, IR2_q, d_ff_2_q);
  or or_3 (W3, IR3_q, d_ff_3_q);
  or or_4 (W4, IR4_q, d_ff_4_q);
  or or_5 (W5, IR5_q, d_ff_5_q);
  or or_6 (W6, IR6_q, d_ff_6_q);
  Hex_Digit_Display hex_digit_display_4 (.value(LedData[19:16]));  // open: dp
  Hex_Digit_Display hex_digit_display_5 (.value(LedData[15:12]));  // open: dp
  Multiplexer #(.select(2), .width(32), .disabled("Z"), .enable("false")) multiplexer_1 (
    .in0(PC_4), .in1(and_1_out), .in2(JAL_ADD), .in3(B_ADD), .out(Scene), .sel(priority_encoder_1_out));
  D_Flip_Flop #(.trigger("rising"), .Pre_Clr_Positions("LEGACY"), .NegatePresetClear("false"), .enable("true"), .NewFFLayout("false")) d_ff_1 (
    .clk(IR1_t), .D(1'b1), .Q(d_ff_1_q), .reset(IR1_q));  // open: Qn, preset, en
  D_Flip_Flop #(.trigger("rising"), .Pre_Clr_Positions("LEGACY"), .NegatePresetClear("false"), .enable("true"), .NewFFLayout("false")) d_ff_2 (
    .clk(IR2_t), .D(1'b1), .Q(d_ff_2_q), .reset(IR2_q));  // open: Qn, preset, en
  D_Flip_Flop #(.trigger("rising"), .Pre_Clr_Positions("LEGACY"), .NegatePresetClear("false"), .enable("true"), .NewFFLayout("false")) d_ff_3 (
    .clk(IR3_t), .D(1'b1), .Q(d_ff_3_q), .reset(IR3_q));  // open: Qn, preset, en
  D_Flip_Flop #(.trigger("rising"), .Pre_Clr_Positions("LEGACY"), .NegatePresetClear("false"), .enable("true"), .NewFFLayout("false")) d_ff_4 (
    .clk(IR4_t), .D(1'b1), .Q(d_ff_4_q), .reset(IR4_q));  // open: Qn, preset, en
  D_Flip_Flop #(.trigger("rising"), .Pre_Clr_Positions("LEGACY"), .NegatePresetClear("false"), .enable("true"), .NewFFLayout("false")) d_ff_5 (
    .clk(IR5_t), .D(1'b1), .Q(d_ff_5_q), .reset(IR5_q));  // open: Qn, preset, en
  D_Flip_Flop #(.trigger("rising"), .Pre_Clr_Positions("LEGACY"), .NegatePresetClear("false"), .enable("true"), .NewFFLayout("false")) d_ff_6 (
    .clk(IR6_t), .D(1'b1), .Q(d_ff_6_q), .reset(IR6_q));  // open: Qn, preset, en
  Hex_Digit_Display hex_digit_display_6 (.value(LedData[11:8]));  // open: dp
  Hex_Digit_Display hex_digit_display_7 (.value(LedData[7:4]));  // open: dp
  // Probe on \总周期数 
  Multiplexer #(.select(1), .width(32), .disabled("Z"), .enable("false")) multiplexer_2 (
    .in0(Scene), .in1(RET_PC), .out(multiplexer_2_out), .sel(URET));
  or or_7 (or_7_out, d_ff_1_q, IR1_q);
  or or_8 (or_8_out, d_ff_2_q, IR2_q);
  or or_9 (or_9_out, d_ff_3_q, IR3_q);
  or or_10 (or_10_out, d_ff_4_q, IR4_q);
  or or_11 (or_11_out, d_ff_5_q, IR5_q);
  or or_12 (or_12_out, d_ff_6_q, IR6_q);
  Hex_Digit_Display hex_digit_display_8 (.value(LedData[3:0]));  // open: dp
  Priority_Encoder #(.select(2), .disabled(0)) priority_encoder_1 (
    .in0(1'b1), .in1(JALR), .in2(JAL), .in3(or_13_out), .out(priority_encoder_1_out));  // open: gs, en_out, en_in
  Multiplexer #(.select(1), .width(32), .disabled("Z"), .enable("false")) multiplexer_3 (
    .in0(multiplexer_2_out), .in1(INT_PC), .out(multiplexer_3_out), .sel(INT));
  not not_1 (not_1_out, halt);
  and and_2 (and_2_out, or_7_out, ~clear1);  // AND_Gate
  and and_3 (and_3_out, or_8_out, ~clear2);  // AND_Gate
  and and_4 (and_4_out, or_9_out, ~clear3);  // AND_Gate
  and and_5 (and_5_out, or_10_out, ~clear4);  // AND_Gate
  and and_6 (and_6_out, or_11_out, ~clear5);  // AND_Gate
  and and_7 (and_7_out, or_12_out, ~clear6);  // AND_Gate
  // Probe on PC
  or or_13 (or_13_out, and_8_out, and_9_out, and_10_out);
  Register #(.width(32), .trigger("rising"), .Select("low")) u_PC (
    .D(multiplexer_3_out), .en(not_1_out), .Q(PC), .clk(CLK), .clr(RST));
  D_Flip_Flop #(.trigger("rising"), .Pre_Clr_Positions("LEGACY"), .NegatePresetClear("false"), .enable("true"), .NewFFLayout("false")) u_IR1 (
    .clk(CLK), .D(and_2_out), .Q(IR1_q));  // open: Qn, preset, en, reset
  D_Flip_Flop #(.trigger("rising"), .Pre_Clr_Positions("LEGACY"), .NegatePresetClear("false"), .enable("true"), .NewFFLayout("false")) u_IR2 (
    .clk(CLK), .D(and_3_out), .Q(IR2_q));  // open: Qn, preset, en, reset
  D_Flip_Flop #(.trigger("rising"), .Pre_Clr_Positions("LEGACY"), .NegatePresetClear("false"), .enable("true"), .NewFFLayout("false")) u_IR3 (
    .clk(CLK), .D(and_4_out), .Q(IR3_q));  // open: Qn, preset, en, reset
  D_Flip_Flop #(.trigger("rising"), .Pre_Clr_Positions("LEGACY"), .NegatePresetClear("false"), .enable("true"), .NewFFLayout("false")) u_IR4 (
    .clk(CLK), .D(and_5_out), .Q(IR4_q));  // open: Qn, preset, en, reset
  D_Flip_Flop #(.trigger("rising"), .Pre_Clr_Positions("LEGACY"), .NegatePresetClear("false"), .enable("true"), .NewFFLayout("false")) u_IR5 (
    .clk(CLK), .D(and_6_out), .Q(IR5_q));  // open: Qn, preset, en, reset
  D_Flip_Flop #(.trigger("rising"), .Pre_Clr_Positions("LEGACY"), .NegatePresetClear("false"), .enable("true"), .NewFFLayout("false")) u_IR6 (
    .clk(CLK), .D(and_7_out), .Q(IR6_q));  // open: Qn, preset, en, reset
  and and_8 (and_8_out, Beq, ALU_t);
  and and_9 (and_9_out, ~ALU_t, Bne);  // AND_Gate
  and and_10 (and_10_out, BGE, ALU_t_t);
  Adder #(.width(32)) adder_1 (.a(PC), .b(32'h4), .out(PC_4), .cin(1'b0));  // open: cout
  // Probe on {IR[31:12], W_num, IR[6:0]}
  // RiscV_Probe riscv_probe_1: pin names not known; wires that end beside it: 1'b1, {IR[31:12], W_num, IR[6:0]}
  // Probe on RegWrite
  ROM #(.addrWidth(10), .dataWidth(32), .Select("high")) rom_1 (.addr(PC[11:2]), .data({IR[31:12], W_num, IR[6:0]}));
  Priority_Encoder #(.select(3), .disabled("Z")) priority_encoder_2 (
    .in0(IR1_q), .in1(IR2_q), .in2(IR3_q), .in3(IR4_q), .in4(IR5_q), .in5(IR6_q), .out(INTnum),
    .gs(INTRequest));  // open: in6, in7, en_out, en_in
  // Probe on RDin
  \单周期硬布线控制器  \u_单周期硬布线控制器_1  (
    .Funct({IR[30], IR[25], IR[14:12]}), .OP(IR[6:2]), .ALU_OP(\单周期硬布线控制器_1_alu_op ),
    .MemToReg(\单周期硬布线控制器_1_memtoreg [0]), .MemWrite(MemWrite), .ALU_SRC(\单周期硬布线控制器_1_alu_src ),
    .RegWrite(RegWrite), .ecall(ecall), .S_type(\单周期硬布线控制器_1_s_type ), .Jalr(JALR), .Beq(Beq), .JAL(JAL),
    .Bne(Bne), .in_3(IR[21]), .uret(URET), .SLTIU(SLTIU), .SH(SH), .BGE(BGE), .CSRRSI(CSRRSI),
    .CSRRCI(CSRRCI), .LUI(LUI));  // open: SRL, rs1_used, rs2_used
  Multiplexer #(.select(1), .width(5), .disabled("Z"), .enable("false")) multiplexer_4 (
    .in0(IR[19:15]), .in1(5'b10001), .out(multiplexer_4_out), .sel(ecall));
  Multiplexer #(.select(1), .width(5), .disabled("Z"), .enable("false")) multiplexer_5 (
    .in0(IR[24:20]), .in1(5'b01010), .out(multiplexer_5_out), .sel(ecall));
  assign bit_extender_1_out = {{20{IR[31]}}, {IR[31], W_num[0], IR[30:25], W_num[4:1]}};  // Bit_Extender bit_extender_1
  assign bit_extender_2_out = {{12{IR[31]}}, {IR[31], IR[19:12], IR[20], IR[30:21]}};  // Bit_Extender bit_extender_2
  Multiplexer #(.select(1), .width(32), .disabled("Z"), .enable("false")) multiplexer_6 (
    .in0(multiplexer_9_out), .in1(multiplexer_7_out), .out(RDin), .sel(SLTIU));
  Multiplexer #(.select(1), .width(32), .disabled("Z"), .enable("false")) multiplexer_7 (
    .in0({32{1'b0}}), .in1(32'h1), .out(multiplexer_7_out), .sel(ALU));
  // Probe on MemWrite
  assign bit_extender_3_out = {{20{multiplexer_8_out[11]}}, multiplexer_8_out};  // Bit_Extender bit_extender_3
  Multiplexer #(.select(1), .width(12), .disabled("Z"), .enable("false")) multiplexer_8 (
    .in0(IR[31:20]), .in1({IR[31:25], W_num}), .out(multiplexer_8_out), .sel(\单周期硬布线控制器_1_s_type ));
  Shifter #(.width(32), .shift("ll")) shifter_1 (.in(bit_extender_1_out), .\dist (5'b00001), .out(shifter_1_out));
  Shifter #(.width(32), .shift("ll")) shifter_2 (.in(bit_extender_2_out), .\dist (5'b00001), .out(shifter_2_out));
  // Probe on MDin
  Counter #(.width(16), .max('hffff), .ongoal("wrap"), .trigger("rising"), .behavior("new")) counter_1 (
    .count(not_2_out), .Q(\总周期数 ), .clk(CLK));  // open: load, D, carry, clr, preset, down
  not not_2 (not_2_out, halt);
  Regifile regifile_1 (
    .Din(RDin), .Clk(CLK), .R1(v0), .R2(regifile_1_r2), .WE(RegWrite), .W_num(W_num),
    .R1_num(multiplexer_4_out), .R2_num(multiplexer_5_out));
  Adder #(.width(32)) adder_2 (.a(PC), .b(shifter_1_out), .out(B_ADD), .cin(1'b0));  // open: cout
  Adder #(.width(32)) adder_3 (.a(PC), .b(shifter_2_out), .out(JAL_ADD), .cin(1'b0));  // open: cout
  Multiplexer #(.select(1), .width(32), .disabled("Z"), .enable("false")) multiplexer_9 (
    .in0(multiplexer_13_out), .in1({IR[31:12], {12{1'b0}}}), .out(multiplexer_9_out), .sel(LUI));
  and and_11 (and_11_out, INTRequest, ~URET);  // AND_Gate
  Register #(.width(3), .trigger("rising"), .Select("low")) register_1 (
    .D(INTnum), .en(INT), .Q(register_1_q), .clk(CLK));  // open: clr
  D_Flip_Flop #(.trigger("rising"), .Pre_Clr_Positions("LEGACY"), .NegatePresetClear("false"), .enable("true"), .NewFFLayout("false")) d_ff_7 (
    .clk(CLK), .D(and_11_out), .Q(IE));  // open: Qn, preset, en, reset
  Register #(.width(32), .trigger("rising"), .Select("low")) register_2 (
    .D(Scene), .en(INT), .Q(RET_PC), .clk(CLK));  // open: clr
  Multiplexer #(.select(3), .width(32), .disabled("Z"), .enable("false")) multiplexer_10 (
    .in0(32'h3438), .in1(32'h33d4), .in2(32'h3328), .in3(32'h3380), .in4(32'h3004), .in5(32'h3198),
    .out(INT_PC), .sel(INTnum));  // open: in6, in7
  and and_12 (INT, INTRequest, ~IE);  // AND_Gate
  Demultiplexer #(.select(3), .width(1), .tristate("false"), .disabled("Z"), .enable("false")) demultiplexer_1 (
    .out0(clear1), .out1(clear2), .out2(clear3), .out3(clear4), .out4(clear5), .out5(clear6), .in(URET),
    .sel(register_1_q));  // open: out6, out7
  // Probe on LedData
  Multiplexer #(.select(1), .width(32), .disabled("Z"), .enable("false")) multiplexer_11 (
    .in0(regifile_1_r2), .in1(bit_extender_3_out), .out(multiplexer_11_out), .sel(\单周期硬布线控制器_1_alu_src ));
  ALU alu_1 (
    .X(v0), .Y(multiplexer_11_out), .AluOP(\单周期硬布线控制器_1_alu_op ), .Equal(ALU_t),
    .Result({ALUresult[31:12], ADDR, ALUresult[1:0]}), .out_4(ALU_t_t), .out_6(ALU));  // open: Result_2
  Comparator #(.width(32), .mode("twosComplement")) comparator_1 (
    .a(v0), .b(32'h22), .eq(comparator_1_eq));  // open: gt, lt
  Comparator #(.width(32), .mode("twosComplement")) comparator_2 (
    .a(v0), .b(32'h64), .eq(comparator_2_eq));  // open: gt, lt
  D_Flip_Flop #(.trigger("high"), .Pre_Clr_Positions("LEGACY"), .NegatePresetClear("false"), .enable("true"), .NewFFLayout("false")) d_ff_8 (.Q(d_ff_8_q));  // open: clk, D, Qn, preset, en, reset
  // Probe on 13'h30
  // Probe on \单周期硬布线控制器_1_alu_op 
  and and_13 (and_13_out, ~comparator_1_eq, ~comparator_2_eq);  // AND_Gate
  Register #(.width(32), .trigger("rising"), .Select("low")) PC_2 (
    .D(regifile_1_r2), .en(and_14_out), .Q(LedData), .clk(CLK));  // open: clr
  and and_14 (and_14_out, comparator_1_eq, ecall);
  Comparator #(.width(13), .mode("twosComplement")) comparator_3 (
    .a(CNT_num), .b(13'h30), .eq(comparator_3_eq), .lt(comparator_3_lt));  // open: gt
  Clock #(.highDuration(1), .lowDuration(1)) clock_1 (.out(clock_1_out));
  D_Flip_Flop #(.trigger("falling"), .Pre_Clr_Positions("ABOVE_BELOW"), .NegatePresetClear("false"), .enable("true"), .NewFFLayout("true")) d_ff_9 (
    .clk(CLK), .D(and_13_out), .Q(halt), .en(ecall), .reset(Go));  // open: Qn, preset
  Counter #(.width(13), .max('h1fff), .ongoal("stay"), .trigger("rising"), .behavior("old")) counter_2 (
    .count(comparator_3_lt), .Q(CNT_num), .clk(clock_1_out));  // open: load, D, carry, clr, preset
  nand nand_1 (nand_1_out, d_ff_8_q, comparator_3_eq);
  assign controlled_buffer_1_out = nand_1_out ? clock_1_out : 1'bz;  // Controlled_Buffer controlled_buffer_1
  Pull_Resistor #(.pull(1)) pull_resistor_1 (.node(controlled_buffer_1_out));
  // MIPS_RAM mips_ram_1: pin names not known; wires that end beside it: ADDR, MDin, MemWrite, mips_ram_1_p4, CLK, 1'b1, mips_ram_1_p7, mips_ram_1_p8
  Button button_1 (.out(mips_ram_1_p7));
  Multiplexer #(.select(1), .width(32), .disabled("Z"), .enable("false")) multiplexer_12 (
    .in0(regifile_1_r2), .in1(shifter_3_out), .out(MDin), .sel(ALUresult[1]));
  Shifter #(.width(32), .shift("ll")) shifter_3 (.in(regifile_1_r2), .\dist (5'b10000), .out(shifter_3_out));
  or or_14 (IR1_t, IR1, IRA);
  or or_15 (IR4_t, IR4, IRD);
  or or_16 (\单周期硬布线控制器_1_memtoreg [1], JAL, JALR);
  Multiplexer #(.select(2), .width(32), .disabled("Z"), .enable("false")) multiplexer_13 (
    .in0({ALUresult[31:12], ADDR, ALUresult[1:0]}), .in1(mips_ram_1_p8), .in2(PC_4),
    .out(multiplexer_13_out), .sel(\单周期硬布线控制器_1_memtoreg ));  // open: in3
  Multiplexer #(.select(1), .width(4), .disabled("Z"), .enable("false")) multiplexer_14 (
    .in0(4'b1111), .in1({{2{multiplexer_15_out[3]}}, {2{multiplexer_15_out[1]}}}), .out(mips_ram_1_p4),
    .sel(SH));
  Multiplexer #(.select(1), .width(1), .disabled("Z"), .enable("false")) multiplexer_15 (
    .in0(1'b1), .in1(1'b0), .out(multiplexer_15_out[1]), .sel(ALUresult[1]));
  Multiplexer #(.select(1), .width(1), .disabled("Z"), .enable("false")) multiplexer_16 (
    .in0(1'b0), .in1(1'b1), .out(multiplexer_15_out[3]), .sel(ALUresult[1]));
  or or_17 (IR2_t, IR2, IRB);
  or or_18 (IR5_t, IR5, IRE);
  or or_19 (IR3_t, IR3, IRC);
  or or_20 (IR6_t, IR6, IRF);

  // Other names for the same wires on the sheet: IR[11:7] = W_num;
  //   JALR_ADD[31:0] = {ALUresult[31:12], ADDR, ALUresult[1:0]}; ALUresult[11:2] = ADDR

  // Notes on the sheet:
  //   中断源
  //   CPU主体
  //   中断相关
  //   中断等待指示
  //   数码管输出应该用寄存器锁存，否则显示数据只能一闪而过
  //   Reset 
  //   Reset 
  //   Reset 
  //   Reset 
  //   Reset 
  //   Reset 
  //   指令探针
  //   指令存储器
  //   rs1
  //   rs2
  //   指令字
  //   contents of rom_1 (hex, n*v repeats v):
  //   4a40006f 18039863 40c37 1c0c13 1802023 40c37 40c0c13 1802223 3fe50c37 fffc0c13 1802423 240c37 4c0c13
  //   1802623 240c37 4c0c13 1802823 3aa80c37 924c0c13 1802a23 aa00c37 124c0c13 1802c23 aa00c37 124c0c13
  //   1802e23 fac00c37 f24c0c13 3802023 2820c37 24c0c13 3802223 3aa60c37 24c0c13 3802423 2efa8c37 fe4c0c13
  //   3802623 20120c37 20c0c13 3802823 2ff20c37 20c0c13 3802a23 24440c37 f3fc0c13 3802c23 21120c37 20c0c13
  //   3802e23 27f20c37 20c0c13 5802023 24128c37 f24c0c13 5802223 20120c37 124c0c13 5802423 20f20c37
  //   124c0c13 5802623 3c840c37 f24c0c13 5802823 4820c37 4c0c13 5802a23 4920c37 4c0c13 5802c23 e4928c37
  //   ffcc0c13 5802e23 24904c37 c0c13 7802023 24904c37 c0c13 7802223 249fdc37 fffc0c13 7802423 4800c37
  //   c0c13 7802623 4800c37 c0c13 7802823 fd000c37 fcfc0c13 7802a23 800c37 c0c13 7802c23 800c37 c0c13
  //   7802e23 2200893 73 100393 200073 18039663 100c13 1802023 6efd8c37 ffcc0c13 1802223 11008c37 2c0c13
  //   1802423 d35f2c37 fdac0c13 1802623 14802c37 22c0c13 1802823 527fcc37 72ac0c13 1802a23 48801c37
  //   8aac0c13 1802c23 447dfc37 28cc0c13 1802e23 52800c37 252c0c13 3802023 249fec37 c2ac0c13 3802223
  //   50a02c37 2a2c0c13 3802423 3c993c37 aacc0c13 3802623 4282bc37 aa0c0c13 3802823 527abc37 91ac0c13
  //   3802a23 a8841c37 822c0c13 3802c23 72d0c37 4a4c0c13 3802e23 40222c37 24ac0c13 5802023 535a5c37
  //   98ac0c13 5802223 54849c37 22c0c13 5802423 5562bc37 bdcc0c13 5802623 55480c37 402c0c13 5802823
  //   5152bc37 972c0c13 5802a23 2e251c37 484c0c13 5802c23 40922c37 2b8c0c13 5802e23 39294c37 484c0c13
  //   7802023 4a25c37 112c0c13 7802223 d6989c37 2aac0c13 7802423 12831c37 442c0c13 7802623 727c7c37
  //   95cc0c13 7802823 a008c37 110c0c13 7802a23 e9ff2c37 ee4c0c13 7802c23 8006c37 2c0c13 7802e23 2200893
  //   73 100393 200073 4038a63 1f00c13 17828463 100493 928933 12499b3 231a13 a2a83 13afb33 140b1663 9282b3
  //   13aeab3 19d993 13acab3 15a2023 2200893 73 1f00b93 1728463 200073 25730463 200073 4038863 10028a63
  //   100493 40928933 12499b3 231a13 a2a83 13afb33 e0b1c63 409282b3 13aeab3 199993 13acab3 15a2023 2200893
  //   73 1f00b93 1728463 200073 1f730a63 200073 6038063 1f00c13 b830e63 100493 28933 12499b3 930bb3 2b9a13
  //   a2a83 13afb33 80b1e63 930333 13aeab3 15a2023 ffca0a13 a2a83 13acab3 15a2023 2200893 73 1f00b93
  //   1728463 200073 19730863 200073 4038e63 4030e63 100493 28933 12499b3 40930bb3 2b9a13 a2a83 13afb33
  //   20b1e63 40930333 13aeab3 15a2023 4a0a13 a2a83 13acab3 15a2023 2200893 73 1f00b93 1728463 200073
  //   13730863 200073 6400893 73 200073 293 313 557c37 700c0c13 1802023 554c37 200c0c13 1802223 757c37
  //   200c0c13 1802423 551c37 200c0c13 1802623 577c37 200c0c13 1802823 11088c37 cf8c0c13 1802e23 1b141c37
  //   880c0c13 3802023 153e1c37 f8c0c13 3802223 11222c37 80c0c13 3802423 11228c37 cf8c0c13 3802623 60e5c37
  //   ea0c0c13 3802c23 208bc37 8a0c0c13 3802e23 20efc37 e40c0c13 5802023 208ac37 240c0c13 5802223 74ebc37
  //   e40c0c13 5802423 70a5c37 ec0c0c13 5802a23 10abc37 aa0c0c13 5802c23 70efc37 ea0c0c13 5802e23 40abc37
  //   ca0c0c13 7802023 74abc37 ac0c0c13 7802223 2200893 73 393 5*13 fedff06f 100e13 75777c37 772c0c13
  //   3802a23 45445c37 442c0c13 3802c23 75447c37 772c0c13 3802e23 15444c37 110c0c13 5802023 77777c37
  //   772c0c13 5802223 2200893 73 fa1ff06f
  //   rd
  //   imm-i
  //   rd
  //   imm-j
  //   beq/bne
  //   jal
  //   MemToReg
  //   MemWrite
  //   AluOP
  //   AluSrcB
  //   RegWrite
  //   S_type
  //   为方便自动评测，需要输出PC，IR，寄存器堆写如数据RDin
  //   SignImm
  //   RAM写使能MemWrite、RAM写入数据MDin等信号
  //   控制位
  //   暂停节拍，不能为0
  //   戳工具置1进入计数暂停模式，ctrl+k时钟自动运行到对应节拍暂停
  //   ctrl+k关闭时钟连续运行，将控制位置零，进入单步调试模式调试
  //   用这个时钟源需要去掉电路中的其他时钟源
  //   数据存储器
  //   可计数暂停的时钟源
endmodule

// 单周期硬布线控制器
module \单周期硬布线控制器  (
  input  [4:0] OP,
  input  [4:0] Funct,
  input  in_3,
  output [3:0] ALU_OP,
  output uret,
  output MemToReg,
  output ecall,
  output MemWrite,
  output ALU_SRC,
  output RegWrite,
  output S_type,
  output Beq,
  output Bne,
  output Jalr,
  output JAL,
  output SRL,
  output SLTIU,
  output SH,
  output BGE,
  output rs1_used,
  output rs2_used,
  output CSRRSI,
  output CSRRCI,
  output LUI
);

  wire \控制信号自动生成_1_ecall ;

  \运算控制器自动生成  \u_运算控制器自动生成_1  (
    .OP2(OP[0]), .OP3(OP[1]), .OP4(OP[2]), .OP5(OP[3]), .OP6(OP[4]), .F12(Funct[0]), .F13(Funct[1]),
    .F14(Funct[2]), .F25(Funct[3]), .F30(Funct[4]), .S0(ALU_OP[0]), .S1(ALU_OP[1]), .S2(ALU_OP[2]),
    .S3(ALU_OP[3]));
  \控制信号自动生成  \u_控制信号自动生成_1  (
    .OP2(OP[0]), .OP3(OP[1]), .MemToReg(MemToReg), .OP4(OP[2]), .OP5(OP[3]), .OP6(OP[4]), .F12(Funct[0]),
    .F13(Funct[1]), .F14(Funct[2]), .MemWrite(MemWrite), .F25(Funct[3]), .F30(Funct[4]), .LUI(LUI),
    .ALU_SRC(ALU_SRC), .RegWrite(RegWrite), .ecall(\控制信号自动生成_1_ecall ), .S_Type(S_type), .BEQ(Beq),
    .BNE(Bne), .JALR(Jalr), .JAL(JAL), .SRL(SRL), .SLTIU(SLTIU), .SH(SH), .BGE(BGE), .rs1_used(rs1_used),
    .rs2_used(rs2_used), .CSRRSI(CSRRSI), .CSRRCI(CSRRCI));
  and and_1 (uret, in_3, \控制信号自动生成_1_ecall );
  and and_2 (ecall, ~in_3, \控制信号自动生成_1_ecall );  // AND_Gate

  // Other names for the same wires on the sheet: IR21 = in_3; OP_CODE[4:0] = OP

  // Notes on the sheet:
  //   运算器控制器，根据指令生成运算器功能选择信号
  //   控制信号生成，产生数据通路需要的其他控制信号
endmodule

// 运算器控制器
module \运算控制器自动生成  (
  input  OP2,
  input  OP3,
  input  OP4,
  input  OP5,
  input  OP6,
  input  F12,
  input  F13,
  input  F14,
  input  F25,
  input  F30,
  output S0,
  output S1,
  output S2,
  output S3
);

  wire and_1_out, and_2_out, and_3_out, and_4_out, and_5_out, and_6_out, and_7_out, and_8_out, and_9_out,
       and_10_out, and_11_out, and_12_out, and_13_out, and_14_out, and_15_out, and_16_out, and_17_out,
       and_18_out, and_19_out, and_20_out, and_21_out, and_22_out, and_23_out, and_24_out, and_25_out,
       and_26_out, and_27_out, and_28_out, and_29_out, and_30_out, and_31_out, and_32_out, and_33_out,
       and_34_out, and_35_out, and_36_out, and_37_out, and_38_out, and_39_out, and_40_out, and_41_out,
       and_42_out, and_43_out, and_44_out, not_1_out, not_2_out, not_3_out, not_4_out, not_5_out, not_6_out,
       not_7_out, not_8_out, not_9_out, not_10_out, not_11_out, not_12_out, not_13_out, not_14_out,
       not_15_out, not_16_out, not_17_out, not_18_out, not_19_out, not_20_out, not_21_out, not_22_out,
       not_23_out, not_24_out, not_25_out, not_26_out, not_27_out, not_28_out, not_29_out, not_30_out,
       not_31_out, not_32_out, not_33_out, not_34_out, not_35_out, not_36_out, not_37_out, not_38_out,
       not_39_out, not_40_out, not_41_out, not_42_out, not_43_out, not_44_out, not_45_out, not_46_out,
       not_47_out, not_48_out, not_49_out, not_50_out, not_51_out, not_52_out, not_53_out, not_54_out,
       not_55_out, not_56_out, not_57_out, not_58_out, not_59_out, not_60_out, not_61_out, not_62_out,
       not_63_out, not_64_out, not_65_out, not_66_out, not_67_out, not_68_out, not_69_out, not_70_out,
       not_71_out, not_72_out, not_73_out, not_74_out, not_75_out, not_76_out, not_77_out, not_78_out,
       not_79_out, not_80_out, not_81_out, not_82_out, not_83_out, not_84_out, not_85_out, not_86_out,
       not_87_out, not_88_out, not_89_out, not_90_out, not_91_out, not_92_out, not_93_out, not_94_out,
       not_95_out, not_96_out, not_97_out, not_98_out, not_99_out, not_100_out, not_101_out, not_102_out,
       not_103_out, not_104_out, not_105_out, not_106_out, not_107_out, not_108_out, not_109_out,
       not_110_out, not_111_out, not_112_out, not_113_out, not_114_out, not_115_out, not_116_out,
       not_117_out, not_118_out, not_119_out, not_120_out, not_121_out, not_122_out, not_123_out,
       not_124_out, not_125_out, not_126_out, not_127_out, not_128_out, not_129_out, not_130_out,
       not_131_out, not_132_out, not_133_out, not_134_out, not_135_out, not_136_out, not_137_out,
       not_138_out, not_139_out, not_140_out, not_141_out, not_142_out, not_143_out, not_144_out,
       not_145_out, not_146_out, not_147_out, not_148_out, not_149_out, not_150_out, not_151_out,
       not_152_out, not_153_out, not_154_out, not_155_out, not_156_out, not_157_out, not_158_out,
       not_159_out, not_160_out, not_161_out, not_162_out, not_163_out, not_164_out, not_165_out,
       not_166_out, not_167_out, not_168_out, not_169_out, not_170_out, not_171_out, not_172_out,
       not_173_out, not_174_out, not_175_out, not_176_out, not_177_out, not_178_out, not_179_out,
       not_180_out, not_181_out, not_182_out, not_183_out, not_184_out, not_185_out, not_186_out,
       not_187_out, not_188_out, not_189_out, not_190_out, not_191_out, not_192_out, not_193_out,
       not_194_out, not_195_out, not_196_out, not_197_out, not_198_out, not_199_out, not_200_out,
       not_201_out, not_202_out, not_203_out, not_204_out, not_205_out, not_206_out, not_207_out,
       not_208_out, not_209_out, not_210_out, not_211_out, not_212_out, not_213_out, not_214_out,
       not_215_out, not_216_out, not_217_out, not_218_out, not_219_out, not_220_out, not_221_out,
       not_222_out, not_223_out, not_224_out, not_225_out, not_226_out, not_227_out, not_228_out,
       not_229_out, not_230_out, not_231_out, not_232_out, not_233_out, not_234_out, not_235_out,
       not_236_out, not_237_out, not_238_out, not_239_out, not_240_out, not_241_out, not_242_out,
       not_243_out, not_244_out, not_245_out, not_246_out, not_247_out, not_248_out, not_249_out,
       not_250_out, not_251_out, not_252_out, not_253_out, not_254_out, not_255_out, not_256_out,
       not_257_out, not_258_out;

  not not_1 (not_1_out, F30);
  not not_2 (not_2_out, F25);
  not not_3 (not_3_out, F14);
  not not_4 (not_4_out, F13);
  not not_5 (not_5_out, F12);
  not not_6 (not_6_out, OP6);
  not not_7 (not_7_out, OP3);
  not not_8 (not_8_out, OP2);
  not not_9 (not_9_out, F30);
  not not_10 (not_10_out, F25);
  not not_11 (not_11_out, OP6);
  not not_12 (not_12_out, OP3);
  not not_13 (not_13_out, OP2);
  not not_14 (not_14_out, F30);
  not not_15 (not_15_out, F25);
  not not_16 (not_16_out, F14);
  not not_17 (not_17_out, F12);
  not not_18 (not_18_out, OP6);
  not not_19 (not_19_out, OP3);
  not not_20 (not_20_out, OP2);
  not not_21 (not_21_out, F14);
  not not_22 (not_22_out, F13);
  not not_23 (not_23_out, F12);
  not not_24 (not_24_out, OP6);
  not not_25 (not_25_out, OP5);
  not not_26 (not_26_out, OP3);
  not not_27 (not_27_out, OP2);
  not not_28 (not_28_out, OP6);
  not not_29 (not_29_out, OP5);
  not not_30 (not_30_out, OP3);
  not not_31 (not_31_out, OP2);
  not not_32 (not_32_out, F13);
  not not_33 (not_33_out, F12);
  not not_34 (not_34_out, OP6);
  not not_35 (not_35_out, OP5);
  not not_36 (not_36_out, OP3);
  not not_37 (not_37_out, OP2);
  not not_38 (not_38_out, F14);
  not not_39 (not_39_out, F12);
  not not_40 (not_40_out, OP6);
  not not_41 (not_41_out, OP5);
  not not_42 (not_42_out, OP3);
  not not_43 (not_43_out, OP2);
  not not_44 (not_44_out, F25);
  not not_45 (not_45_out, F13);
  not not_46 (not_46_out, OP6);
  not not_47 (not_47_out, OP5);
  not not_48 (not_48_out, OP3);
  not not_49 (not_49_out, OP2);
  not not_50 (not_50_out, F14);
  not not_51 (not_51_out, F12);
  not not_52 (not_52_out, OP6);
  not not_53 (not_53_out, OP5);
  not not_54 (not_54_out, OP4);
  not not_55 (not_55_out, OP3);
  not not_56 (not_56_out, OP2);
  not not_57 (not_57_out, F14);
  not not_58 (not_58_out, F12);
  not not_59 (not_59_out, OP6);
  not not_60 (not_60_out, OP4);
  not not_61 (not_61_out, OP3);
  not not_62 (not_62_out, OP2);
  not not_63 (not_63_out, F14);
  not not_64 (not_64_out, F13);
  not not_65 (not_65_out, F12);
  not not_66 (not_66_out, OP4);
  not not_67 (not_67_out, OP3);
  not not_68 (not_68_out, F13);
  not not_69 (not_69_out, OP4);
  not not_70 (not_70_out, OP3);
  not not_71 (not_71_out, OP2);
  not not_72 (not_72_out, F30);
  not not_73 (not_73_out, F25);
  not not_74 (not_74_out, F13);
  not not_75 (not_75_out, F12);
  not not_76 (not_76_out, OP6);
  not not_77 (not_77_out, OP3);
  not not_78 (not_78_out, OP2);
  not not_79 (not_79_out, F25);
  not not_80 (not_80_out, F14);
  not not_81 (not_81_out, F13);
  not not_82 (not_82_out, F12);
  not not_83 (not_83_out, OP6);
  not not_84 (not_84_out, OP3);
  not not_85 (not_85_out, OP2);
  not not_86 (not_86_out, F30);
  not not_87 (not_87_out, F25);
  not not_88 (not_88_out, OP6);
  not not_89 (not_89_out, OP3);
  not not_90 (not_90_out, OP2);
  not not_91 (not_91_out, F30);
  not not_92 (not_92_out, F25);
  not not_93 (not_93_out, F14);
  not not_94 (not_94_out, F12);
  not not_95 (not_95_out, OP6);
  not not_96 (not_96_out, OP3);
  not not_97 (not_97_out, OP2);
  not not_98 (not_98_out, OP6);
  not not_99 (not_99_out, OP5);
  not not_100 (not_100_out, OP3);
  not not_101 (not_101_out, OP2);
  not not_102 (not_102_out, F14);
  not not_103 (not_103_out, F12);
  not not_104 (not_104_out, OP6);
  not not_105 (not_105_out, OP5);
  not not_106 (not_106_out, OP3);
  not not_107 (not_107_out, OP2);
  not not_108 (not_108_out, F30);
  not not_109 (not_109_out, F25);
  not not_110 (not_110_out, F13);
  not not_111 (not_111_out, OP6);
  not not_112 (not_112_out, OP5);
  not not_113 (not_113_out, OP3);
  not not_114 (not_114_out, OP2);
  not not_115 (not_115_out, F14);
  not not_116 (not_116_out, F13);
  not not_117 (not_117_out, F12);
  not not_118 (not_118_out, OP4);
  not not_119 (not_119_out, OP3);
  not not_120 (not_120_out, OP2);
  not not_121 (not_121_out, F14);
  not not_122 (not_122_out, F13);
  not not_123 (not_123_out, OP4);
  not not_124 (not_124_out, OP3);
  not not_125 (not_125_out, OP2);
  not not_126 (not_126_out, F30);
  not not_127 (not_127_out, F25);
  not not_128 (not_128_out, F13);
  not not_129 (not_129_out, OP6);
  not not_130 (not_130_out, OP3);
  not not_131 (not_131_out, OP2);
  not not_132 (not_132_out, F13);
  not not_133 (not_133_out, OP4);
  not not_134 (not_134_out, OP3);
  not not_135 (not_135_out, OP2);
  not not_136 (not_136_out, F30);
  not not_137 (not_137_out, F25);
  not not_138 (not_138_out, F14);
  not not_139 (not_139_out, F13);
  not not_140 (not_140_out, F12);
  not not_141 (not_141_out, OP6);
  not not_142 (not_142_out, OP3);
  not not_143 (not_143_out, OP2);
  not not_144 (not_144_out, F25);
  not not_145 (not_145_out, F14);
  not not_146 (not_146_out, F13);
  not not_147 (not_147_out, F12);
  not not_148 (not_148_out, OP6);
  not not_149 (not_149_out, OP3);
  not not_150 (not_150_out, OP2);
  not not_151 (not_151_out, F30);
  not not_152 (not_152_out, F25);
  not not_153 (not_153_out, OP6);
  not not_154 (not_154_out, OP3);
  not not_155 (not_155_out, OP2);
  not not_156 (not_156_out, F30);
  not not_157 (not_157_out, F25);
  not not_158 (not_158_out, F14);
  not not_159 (not_159_out, OP6);
  not not_160 (not_160_out, OP3);
  not not_161 (not_161_out, OP2);
  not not_162 (not_162_out, F14);
  not not_163 (not_163_out, F13);
  not not_164 (not_164_out, F12);
  not not_165 (not_165_out, OP6);
  not not_166 (not_166_out, OP5);
  not not_167 (not_167_out, OP3);
  not not_168 (not_168_out, OP2);
  not not_169 (not_169_out, OP6);
  not not_170 (not_170_out, OP5);
  not not_171 (not_171_out, OP3);
  not not_172 (not_172_out, OP2);
  not not_173 (not_173_out, F14);
  not not_174 (not_174_out, F12);
  not not_175 (not_175_out, OP6);
  not not_176 (not_176_out, OP5);
  not not_177 (not_177_out, OP4);
  not not_178 (not_178_out, OP3);
  not not_179 (not_179_out, OP2);
  not not_180 (not_180_out, F14);
  not not_181 (not_181_out, F12);
  not not_182 (not_182_out, OP6);
  not not_183 (not_183_out, OP4);
  not not_184 (not_184_out, OP3);
  not not_185 (not_185_out, OP2);
  not not_186 (not_186_out, F14);
  not not_187 (not_187_out, F13);
  not not_188 (not_188_out, F12);
  not not_189 (not_189_out, OP4);
  not not_190 (not_190_out, OP3);
  not not_191 (not_191_out, OP2);
  not not_192 (not_192_out, F14);
  not not_193 (not_193_out, F13);
  not not_194 (not_194_out, OP4);
  not not_195 (not_195_out, OP3);
  not not_196 (not_196_out, OP2);
  not not_197 (not_197_out, F14);
  not not_198 (not_198_out, F13);
  not not_199 (not_199_out, F12);
  not not_200 (not_200_out, OP4);
  not not_201 (not_201_out, OP3);
  not not_202 (not_202_out, F14);
  not not_203 (not_203_out, OP6);
  not not_204 (not_204_out, OP5);
  not not_205 (not_205_out, OP3);
  not not_206 (not_206_out, OP2);
  not not_207 (not_207_out, F30);
  not not_208 (not_208_out, F25);
  not not_209 (not_209_out, F12);
  not not_210 (not_210_out, OP6);
  not not_211 (not_211_out, OP3);
  not not_212 (not_212_out, OP2);
  not not_213 (not_213_out, F30);
  not not_214 (not_214_out, F25);
  not not_215 (not_215_out, F14);
  not not_216 (not_216_out, F12);
  not not_217 (not_217_out, OP6);
  not not_218 (not_218_out, OP3);
  not not_219 (not_219_out, OP2);
  not not_220 (not_220_out, F30);
  not not_221 (not_221_out, F25);
  not not_222 (not_222_out, F14);
  not not_223 (not_223_out, OP6);
  not not_224 (not_224_out, OP3);
  not not_225 (not_225_out, OP2);
  not not_226 (not_226_out, F12);
  not not_227 (not_227_out, OP6);
  not not_228 (not_228_out, OP5);
  not not_229 (not_229_out, OP3);
  not not_230 (not_230_out, OP2);
  not not_231 (not_231_out, F13);
  not not_232 (not_232_out, F12);
  not not_233 (not_233_out, OP6);
  not not_234 (not_234_out, OP5);
  not not_235 (not_235_out, OP3);
  not not_236 (not_236_out, OP2);
  not not_237 (not_237_out, F14);
  not not_238 (not_238_out, F12);
  not not_239 (not_239_out, OP6);
  not not_240 (not_240_out, OP5);
  not not_241 (not_241_out, OP3);
  not not_242 (not_242_out, OP2);
  not not_243 (not_243_out, F14);
  not not_244 (not_244_out, OP6);
  not not_245 (not_245_out, OP5);
  not not_246 (not_246_out, OP3);
  not not_247 (not_247_out, OP2);
  not not_248 (not_248_out, F13);
  not not_249 (not_249_out, OP4);
  not not_250 (not_250_out, OP3);
  not not_251 (not_251_out, OP2);
  not not_252 (not_252_out, F30);
  not not_253 (not_253_out, F25);
  not not_254 (not_254_out, F13);
  not not_255 (not_255_out, F12);
  not not_256 (not_256_out, OP6);
  not not_257 (not_257_out, OP3);
  not not_258 (not_258_out, OP2);
  and and_1 (and_1_out, not_1_out, not_2_out, not_3_out, not_4_out, not_5_out, not_6_out, OP5, OP4, not_7_out, not_8_out);
  and and_2 (and_2_out, not_9_out, not_10_out, F14, F13, F12, not_11_out, OP5, OP4, not_12_out, not_13_out);
  and and_3 (and_3_out, not_14_out, not_15_out, not_16_out, F13, not_17_out, not_18_out, OP5, OP4, not_19_out, not_20_out);
  and and_4 (and_4_out, not_21_out, not_22_out, not_23_out, not_24_out, not_25_out, OP4, not_26_out, not_27_out);
  and and_5 (and_5_out, F14, F13, F12, not_28_out, not_29_out, OP4, not_30_out, not_31_out);
  and and_6 (and_6_out, F14, not_32_out, not_33_out, not_34_out, not_35_out, OP4, not_36_out, not_37_out);
  and and_7 (and_7_out, not_38_out, F13, not_39_out, not_40_out, not_41_out, OP4, not_42_out, not_43_out);
  and and_8 (and_8_out, F30, not_44_out, F14, not_45_out, F12, not_46_out, not_47_out, OP4, not_48_out, not_49_out);
  and and_9 (and_9_out, not_50_out, F13, not_51_out, not_52_out, not_53_out, not_54_out, not_55_out, not_56_out);
  and and_10 (and_10_out, not_57_out, F13, not_58_out, not_59_out, OP5, not_60_out, not_61_out, not_62_out);
  and and_11 (and_11_out, not_63_out, not_64_out, not_65_out, OP6, OP5, not_66_out, not_67_out, OP2);
  and and_12 (and_12_out, F14, not_68_out, F12, OP6, OP5, not_69_out, not_70_out, not_71_out);
  and and_13 (and_13_out, not_72_out, not_73_out, F14, not_74_out, not_75_out, not_76_out, OP5, OP4, not_77_out, not_78_out);
  and and_14 (and_14_out, F30, not_79_out, not_80_out, not_81_out, not_82_out, not_83_out, OP5, OP4, not_84_out, not_85_out);
  and and_15 (and_15_out, not_86_out, not_87_out, F14, F13, F12, not_88_out, OP5, OP4, not_89_out, not_90_out);
  and and_16 (and_16_out, not_91_out, not_92_out, not_93_out, F13, not_94_out, not_95_out, OP5, OP4, not_96_out, not_97_out);
  and and_17 (and_17_out, F14, F13, F12, not_98_out, not_99_out, OP4, not_100_out, not_101_out);
  and and_18 (and_18_out, not_102_out, F13, not_103_out, not_104_out, not_105_out, OP4, not_106_out, not_107_out);
  and and_19 (and_19_out, not_108_out, not_109_out, F14, not_110_out, F12, not_111_out, not_112_out, OP4, not_113_out, not_114_out);
  and and_20 (and_20_out, not_115_out, not_116_out, not_117_out, OP6, OP5, not_118_out, not_119_out, not_120_out);
  and and_21 (and_21_out, not_121_out, not_122_out, F12, OP6, OP5, not_123_out, not_124_out, not_125_out);
  and and_22 (and_22_out, not_126_out, not_127_out, F14, not_128_out, F12, not_129_out, OP5, OP4, not_130_out, not_131_out);
  and and_23 (and_23_out, F14, not_132_out, F12, OP6, OP5, not_133_out, not_134_out, not_135_out);
  and and_24 (and_24_out, not_136_out, not_137_out, not_138_out, not_139_out, not_140_out, not_141_out, OP5, OP4, not_142_out, not_143_out);
  and and_25 (and_25_out, F30, not_144_out, not_145_out, not_146_out, not_147_out, not_148_out, OP5, OP4, not_149_out, not_150_out);
  and and_26 (and_26_out, not_151_out, not_152_out, F14, F13, F12, not_153_out, OP5, OP4, not_154_out, not_155_out);
  and and_27 (and_27_out, not_156_out, not_157_out, not_158_out, F13, F12, not_159_out, OP5, OP4, not_160_out, not_161_out);
  and and_28 (and_28_out, not_162_out, not_163_out, not_164_out, not_165_out, not_166_out, OP4, not_167_out, not_168_out);
  and and_29 (and_29_out, F14, F13, F12, not_169_out, not_170_out, OP4, not_171_out, not_172_out);
  and and_30 (and_30_out, not_173_out, F13, not_174_out, not_175_out, not_176_out, not_177_out, not_178_out, not_179_out);
  and and_31 (and_31_out, not_180_out, F13, not_181_out, not_182_out, OP5, not_183_out, not_184_out, not_185_out);
  and and_32 (and_32_out, not_186_out, not_187_out, not_188_out, OP6, OP5, not_189_out, not_190_out, not_191_out);
  and and_33 (and_33_out, not_192_out, not_193_out, F12, OP6, OP5, not_194_out, not_195_out, not_196_out);
  and and_34 (and_34_out, not_197_out, not_198_out, not_199_out, OP6, OP5, not_200_out, not_201_out, OP2);
  and and_35 (and_35_out, not_202_out, F13, F12, not_203_out, not_204_out, OP4, not_205_out, not_206_out);
  and and_36 (and_36_out, not_207_out, not_208_out, F14, F13, not_209_out, not_210_out, OP5, OP4, not_211_out, not_212_out);
  and and_37 (and_37_out, not_213_out, not_214_out, not_215_out, F13, not_216_out, not_217_out, OP5, OP4, not_218_out, not_219_out);
  and and_38 (and_38_out, not_220_out, not_221_out, not_222_out, F13, F12, not_223_out, OP5, OP4, not_224_out, not_225_out);
  and and_39 (and_39_out, F14, F13, not_226_out, not_227_out, not_228_out, OP4, not_229_out, not_230_out);
  and and_40 (and_40_out, F14, not_231_out, not_232_out, not_233_out, not_234_out, OP4, not_235_out, not_236_out);
  and and_41 (and_41_out, not_237_out, F13, not_238_out, not_239_out, not_240_out, OP4, not_241_out, not_242_out);
  and and_42 (and_42_out, not_243_out, F13, F12, not_244_out, not_245_out, OP4, not_246_out, not_247_out);
  and and_43 (and_43_out, F14, not_248_out, F12, OP6, OP5, not_249_out, not_250_out, not_251_out);
  and and_44 (and_44_out, not_252_out, not_253_out, F14, not_254_out, not_255_out, not_256_out, OP5, OP4, not_257_out, not_258_out);
  or or_1 (S0, and_1_out, and_2_out, and_3_out, and_4_out, and_5_out, and_6_out, and_7_out, and_8_out, and_9_out, and_10_out, and_11_out, and_12_out, and_13_out);
  or or_2 (S1, and_14_out, and_15_out, and_16_out, and_17_out, and_18_out, and_19_out, and_20_out, and_21_out, and_22_out, and_23_out);
  or or_3 (S2, and_24_out, and_25_out, and_26_out, and_27_out, and_28_out, and_29_out, and_30_out, and_31_out, and_32_out, and_33_out, and_34_out, and_35_out);
  or or_4 (S3, and_36_out, and_37_out, and_38_out, and_39_out, and_40_out, and_41_out, and_42_out, and_43_out, and_44_out);
endmodule

// 控制信号生成
module \控制信号自动生成  (
  input  OP2,
  input  OP3,
  input  OP4,
  input  OP5,
  input  OP6,
  input  F12,
  input  F13,
  input  F14,
  input  F25,
  input  F30,
  output MemToReg,
  output MemWrite,
  output LUI,
  output ALU_SRC,
  output RegWrite,
  output ecall,
  output S_Type,
  output BEQ,
  output BNE,
  output JALR,
  output JAL,
  output SRL,
  output SLTIU,
  output SH,
  output BGE,
  output rs1_used,
  output rs2_used,
  output CSRRSI,
  output CSRRCI
);

  wire and_2_out, and_3_out, and_5_out, and_6_out, and_7_out, and_8_out, and_9_out, and_10_out, and_11_out,
       and_12_out, and_13_out, and_14_out, and_15_out, and_16_out, and_17_out, and_18_out, and_19_out,
       and_20_out, and_21_out, and_22_out, and_23_out, and_24_out, and_25_out, and_26_out, and_27_out,
       and_28_out, and_29_out, and_30_out, and_31_out, and_32_out, and_33_out, and_34_out, and_35_out,
       and_36_out, and_37_out, and_38_out, and_39_out, and_41_out, and_42_out, and_51_out, and_52_out,
       and_53_out, and_54_out, and_55_out, and_56_out, and_57_out, and_58_out, and_59_out, and_60_out,
       and_61_out, and_62_out, and_63_out, and_64_out, and_65_out, and_66_out, and_67_out, and_68_out,
       and_69_out, and_70_out, and_71_out, and_72_out, and_73_out, and_74_out, and_75_out, and_76_out,
       and_77_out, and_78_out, and_79_out, and_80_out, and_81_out, and_82_out, and_83_out, and_84_out,
       and_85_out, and_86_out, and_87_out, and_88_out, and_89_out, and_90_out, and_91_out, not_1_out,
       not_2_out, not_3_out, not_4_out, not_5_out, not_6_out, not_7_out, not_8_out, not_9_out, not_10_out,
       not_11_out, not_12_out, not_13_out, not_14_out, not_15_out, not_16_out, not_17_out, not_18_out,
       not_19_out, not_20_out, not_21_out, not_22_out, not_23_out, not_24_out, not_25_out, not_26_out,
       not_27_out, not_28_out, not_29_out, not_30_out, not_31_out, not_32_out, not_33_out, not_34_out,
       not_35_out, not_36_out, not_37_out, not_38_out, not_39_out, not_40_out, not_41_out, not_42_out,
       not_43_out, not_44_out, not_45_out, not_46_out, not_47_out, not_48_out, not_49_out, not_50_out,
       not_51_out, not_52_out, not_53_out, not_54_out, not_55_out, not_56_out, not_57_out, not_58_out,
       not_59_out, not_60_out, not_61_out, not_62_out, not_63_out, not_64_out, not_65_out, not_66_out,
       not_67_out, not_68_out, not_69_out, not_70_out, not_71_out, not_72_out, not_73_out, not_74_out,
       not_75_out, not_76_out, not_77_out, not_78_out, not_79_out, not_80_out, not_81_out, not_82_out,
       not_83_out, not_84_out, not_85_out, not_86_out, not_87_out, not_88_out, not_89_out, not_90_out,
       not_91_out, not_92_out, not_93_out, not_94_out, not_95_out, not_96_out, not_97_out, not_98_out,
       not_99_out, not_100_out, not_101_out, not_102_out, not_103_out, not_104_out, not_105_out, not_106_out,
       not_107_out, not_108_out, not_109_out, not_110_out, not_111_out, not_112_out, not_113_out,
       not_114_out, not_115_out, not_116_out, not_117_out, not_118_out, not_119_out, not_120_out,
       not_121_out, not_122_out, not_123_out, not_124_out, not_125_out, not_126_out, not_127_out,
       not_128_out, not_129_out, not_130_out, not_131_out, not_132_out, not_133_out, not_134_out,
       not_135_out, not_136_out, not_137_out, not_138_out, not_139_out, not_140_out, not_141_out,
       not_142_out, not_143_out, not_144_out, not_145_out, not_146_out, not_147_out, not_148_out,
       not_149_out, not_150_out, not_151_out, not_152_out, not_153_out, not_154_out, not_155_out,
       not_156_out, not_157_out, not_158_out, not_159_out, not_160_out, not_161_out, not_162_out,
       not_163_out, not_164_out, not_165_out, not_166_out, not_167_out, not_168_out, not_169_out,
       not_170_out, not_171_out, not_172_out, not_173_out, not_174_out, not_175_out, not_176_out,
       not_177_out, not_178_out, not_179_out, not_180_out, not_181_out, not_182_out, not_183_out,
       not_184_out, not_185_out, not_186_out, not_187_out, not_188_out, not_189_out, not_190_out,
       not_191_out, not_192_out, not_193_out, not_194_out, not_195_out, not_196_out, not_197_out,
       not_198_out, not_199_out, not_200_out, not_201_out, not_202_out, not_203_out, not_204_out,
       not_205_out, not_206_out, not_207_out, not_208_out, not_209_out, not_210_out, not_211_out,
       not_212_out, not_213_out, not_214_out, not_215_out, not_216_out, not_217_out, not_218_out,
       not_219_out, not_220_out, not_221_out, not_222_out, not_223_out, not_224_out, not_225_out,
       not_226_out, not_227_out, not_228_out, not_229_out, not_230_out, not_231_out, not_232_out,
       not_233_out, not_234_out, not_235_out, not_236_out, not_237_out, not_238_out, not_239_out,
       not_240_out, not_241_out, not_242_out, not_243_out, not_244_out, not_245_out, not_246_out,
       not_247_out, not_248_out, not_249_out, not_250_out, not_251_out, not_252_out, not_253_out,
       not_254_out, not_255_out, not_256_out, not_257_out, not_258_out, not_259_out, not_260_out,
       not_261_out, not_262_out, not_263_out, not_264_out, not_265_out, not_266_out, not_267_out,
       not_268_out, not_269_out, not_270_out, not_271_out, not_272_out, not_273_out, not_274_out,
       not_275_out, not_276_out, not_277_out, not_278_out, not_279_out, not_280_out, not_281_out,
       not_282_out, not_283_out, not_284_out, not_285_out, not_286_out, not_287_out, not_288_out,
       not_289_out, not_290_out, not_291_out, not_292_out, not_293_out, not_294_out, not_295_out,
       not_296_out, not_297_out, not_298_out, not_299_out, not_300_out, not_301_out, not_302_out,
       not_303_out, not_304_out, not_305_out, not_306_out, not_307_out, not_308_out, not_309_out,
       not_310_out, not_311_out, not_312_out, not_313_out, not_314_out, not_315_out, not_316_out,
       not_317_out, not_318_out, not_319_out, not_320_out, not_321_out, not_322_out, not_323_out,
       not_324_out, not_325_out, not_326_out, not_327_out, not_328_out, not_329_out, not_330_out,
       not_331_out, not_332_out, not_333_out, not_334_out, not_335_out, not_336_out, not_337_out,
       not_338_out, not_339_out, not_340_out, not_341_out, not_342_out, not_343_out, not_344_out,
       not_345_out, not_346_out, not_347_out, not_348_out, not_349_out, not_350_out, not_351_out,
       not_352_out, not_353_out, not_354_out, not_355_out, not_356_out, not_357_out, not_358_out,
       not_359_out, not_360_out, not_361_out, not_362_out, not_363_out, not_364_out, not_365_out,
       not_366_out, not_367_out, not_368_out, not_369_out, not_370_out, not_371_out, not_372_out,
       not_373_out, not_374_out, not_375_out, not_376_out, not_377_out, not_378_out, not_379_out,
       not_380_out, not_381_out, not_382_out, not_383_out, not_384_out, not_385_out, not_386_out,
       not_387_out, not_388_out, not_389_out, not_390_out, not_391_out, not_392_out, not_393_out,
       not_394_out, not_395_out, not_396_out, not_397_out, not_398_out, not_399_out, not_400_out,
       not_401_out, not_402_out, not_403_out, not_404_out, not_405_out, not_406_out, not_407_out,
       not_408_out, not_409_out, not_410_out, not_411_out, not_412_out, not_413_out, not_414_out,
       not_415_out, not_416_out, not_417_out, not_418_out, not_419_out, not_420_out, not_421_out,
       not_422_out, not_423_out, not_424_out, not_425_out, not_426_out, not_427_out, not_428_out,
       not_429_out, not_430_out, not_431_out, not_432_out, not_433_out, not_434_out, not_435_out,
       not_436_out, not_437_out, not_438_out, not_439_out, not_440_out, not_441_out, not_442_out,
       not_443_out, not_444_out, not_445_out, not_446_out, not_447_out, not_448_out, not_449_out,
       not_450_out, not_451_out, not_452_out, not_453_out, not_454_out, not_455_out, not_456_out,
       not_457_out, not_458_out, not_459_out, not_460_out, not_461_out, not_462_out, not_463_out,
       not_464_out, not_465_out, not_466_out, not_467_out, not_468_out, not_469_out, not_470_out,
       not_471_out, not_472_out, not_473_out, not_474_out, not_475_out, not_476_out, not_477_out,
       not_478_out, not_479_out, not_480_out, not_481_out, not_482_out, not_483_out, not_484_out,
       not_485_out, not_486_out, not_487_out, not_488_out, not_489_out, not_490_out, not_491_out,
       not_492_out, not_493_out, not_494_out, not_495_out, not_496_out, not_497_out, not_498_out,
       not_499_out, not_500_out, not_501_out, not_502_out, not_503_out, not_504_out, not_505_out,
       not_506_out, not_507_out, not_508_out, not_509_out, not_510_out, not_511_out, not_512_out,
       not_513_out, not_514_out, not_515_out, not_516_out, not_517_out, not_518_out, not_519_out,
       not_520_out, not_521_out, not_522_out, not_523_out, not_524_out, not_525_out, not_526_out,
       not_527_out, not_528_out, not_529_out, not_530_out, not_531_out, not_532_out;

  not not_1 (not_1_out, F14);
  not not_2 (not_2_out, F12);
  not not_3 (not_3_out, OP6);
  not not_4 (not_4_out, OP5);
  not not_5 (not_5_out, OP4);
  not not_6 (not_6_out, OP3);
  not not_7 (not_7_out, OP2);
  not not_8 (not_8_out, F14);
  not not_9 (not_9_out, F12);
  not not_10 (not_10_out, OP6);
  not not_11 (not_11_out, OP4);
  not not_12 (not_12_out, OP3);
  not not_13 (not_13_out, OP2);
  not not_14 (not_14_out, F14);
  not not_15 (not_15_out, F13);
  not not_16 (not_16_out, OP6);
  not not_17 (not_17_out, OP4);
  not not_18 (not_18_out, OP3);
  not not_19 (not_19_out, OP2);
  not not_20 (not_20_out, OP6);
  not not_21 (not_21_out, OP3);
  not not_22 (not_22_out, F14);
  not not_23 (not_23_out, F13);
  not not_24 (not_24_out, F12);
  not not_25 (not_25_out, OP6);
  not not_26 (not_26_out, OP5);
  not not_27 (not_27_out, OP3);
  not not_28 (not_28_out, OP2);
  not not_29 (not_29_out, OP6);
  not not_30 (not_30_out, OP5);
  not not_31 (not_31_out, OP3);
  not not_32 (not_32_out, OP2);
  not not_33 (not_33_out, F12);
  not not_34 (not_34_out, OP6);
  not not_35 (not_35_out, OP5);
  not not_36 (not_36_out, OP3);
  not not_37 (not_37_out, OP2);
  not not_38 (not_38_out, F13);
  not not_39 (not_39_out, F12);
  not not_40 (not_40_out, OP6);
  not not_41 (not_41_out, OP5);
  not not_42 (not_42_out, OP3);
  not not_43 (not_43_out, OP2);
  not not_44 (not_44_out, F14);
  not not_45 (not_45_out, F12);
  not not_46 (not_46_out, OP6);
  not not_47 (not_47_out, OP5);
  not not_48 (not_48_out, OP3);
  not not_49 (not_49_out, OP2);
  not not_50 (not_50_out, F30);
  not not_51 (not_51_out, F25);
  not not_52 (not_52_out, F14);
  not not_53 (not_53_out, F13);
  not not_54 (not_54_out, OP6);
  not not_55 (not_55_out, OP5);
  not not_56 (not_56_out, OP3);
  not not_57 (not_57_out, OP2);
  not not_58 (not_58_out, F30);
  not not_59 (not_59_out, F25);
  not not_60 (not_60_out, F13);
  not not_61 (not_61_out, OP6);
  not not_62 (not_62_out, OP5);
  not not_63 (not_63_out, OP3);
  not not_64 (not_64_out, OP2);
  not not_65 (not_65_out, F25);
  not not_66 (not_66_out, F13);
  not not_67 (not_67_out, OP6);
  not not_68 (not_68_out, OP5);
  not not_69 (not_69_out, OP3);
  not not_70 (not_70_out, OP2);
  not not_71 (not_71_out, F14);
  not not_72 (not_72_out, F12);
  not not_73 (not_73_out, OP6);
  not not_74 (not_74_out, OP5);
  not not_75 (not_75_out, OP4);
  not not_76 (not_76_out, OP3);
  not not_77 (not_77_out, OP2);
  not not_78 (not_78_out, F14);
  not not_79 (not_79_out, F12);
  not not_80 (not_80_out, OP6);
  not not_81 (not_81_out, OP4);
  not not_82 (not_82_out, OP3);
  not not_83 (not_83_out, OP2);
  not not_84 (not_84_out, F14);
  not not_85 (not_85_out, F13);
  not not_86 (not_86_out, F12);
  not not_87 (not_87_out, OP4);
  not not_88 (not_88_out, OP3);
  not not_89 (not_89_out, F14);
  not not_90 (not_90_out, OP6);
  not not_91 (not_91_out, OP5);
  not not_92 (not_92_out, OP3);
  not not_93 (not_93_out, OP2);
  not not_94 (not_94_out, F14);
  not not_95 (not_95_out, F13);
  not not_96 (not_96_out, OP6);
  not not_97 (not_97_out, OP4);
  not not_98 (not_98_out, OP3);
  not not_99 (not_99_out, OP2);
  not not_100 (not_100_out, F30);
  not not_101 (not_101_out, F25);
  not not_102 (not_102_out, F14);
  not not_103 (not_103_out, F13);
  not not_104 (not_104_out, F12);
  not not_105 (not_105_out, OP6);
  not not_106 (not_106_out, OP3);
  not not_107 (not_107_out, OP2);
  not not_108 (not_108_out, F25);
  not not_109 (not_109_out, F14);
  not not_110 (not_110_out, F13);
  not not_111 (not_111_out, F12);
  not not_112 (not_112_out, OP6);
  not not_113 (not_113_out, OP3);
  not not_114 (not_114_out, OP2);
  not not_115 (not_115_out, F30);
  not not_116 (not_116_out, F25);
  not not_117 (not_117_out, OP6);
  not not_118 (not_118_out, OP3);
  not not_119 (not_119_out, OP2);
  not not_120 (not_120_out, F30);
  not not_121 (not_121_out, F25);
  not not_122 (not_122_out, F12);
  not not_123 (not_123_out, OP6);
  not not_124 (not_124_out, OP3);
  not not_125 (not_125_out, OP2);
  not not_126 (not_126_out, F30);
  not not_127 (not_127_out, F25);
  not not_128 (not_128_out, F14);
  not not_129 (not_129_out, F12);
  not not_130 (not_130_out, OP6);
  not not_131 (not_131_out, OP3);
  not not_132 (not_132_out, OP2);
  not not_133 (not_133_out, F30);
  not not_134 (not_134_out, F25);
  not not_135 (not_135_out, F14);
  not not_136 (not_136_out, OP6);
  not not_137 (not_137_out, OP3);
  not not_138 (not_138_out, OP2);
  not not_139 (not_139_out, F14);
  not not_140 (not_140_out, F13);
  not not_141 (not_141_out, F12);
  not not_142 (not_142_out, OP6);
  not not_143 (not_143_out, OP5);
  not not_144 (not_144_out, OP3);
  not not_145 (not_145_out, OP2);
  not not_146 (not_146_out, OP6);
  not not_147 (not_147_out, OP5);
  not not_148 (not_148_out, OP3);
  not not_149 (not_149_out, OP2);
  not not_150 (not_150_out, F12);
  not not_151 (not_151_out, OP6);
  not not_152 (not_152_out, OP5);
  not not_153 (not_153_out, OP3);
  not not_154 (not_154_out, OP2);
  not not_155 (not_155_out, F13);
  not not_156 (not_156_out, F12);
  not not_157 (not_157_out, OP6);
  not not_158 (not_158_out, OP5);
  not not_159 (not_159_out, OP3);
  not not_160 (not_160_out, OP2);
  not not_161 (not_161_out, F14);
  not not_162 (not_162_out, F12);
  not not_163 (not_163_out, OP6);
  not not_164 (not_164_out, OP5);
  not not_165 (not_165_out, OP3);
  not not_166 (not_166_out, OP2);
  not not_167 (not_167_out, F30);
  not not_168 (not_168_out, F25);
  not not_169 (not_169_out, F14);
  not not_170 (not_170_out, F13);
  not not_171 (not_171_out, OP6);
  not not_172 (not_172_out, OP5);
  not not_173 (not_173_out, OP3);
  not not_174 (not_174_out, OP2);
  not not_175 (not_175_out, F30);
  not not_176 (not_176_out, F25);
  not not_177 (not_177_out, F13);
  not not_178 (not_178_out, OP6);
  not not_179 (not_179_out, OP5);
  not not_180 (not_180_out, OP3);
  not not_181 (not_181_out, OP2);
  not not_182 (not_182_out, F25);
  not not_183 (not_183_out, F13);
  not not_184 (not_184_out, OP6);
  not not_185 (not_185_out, OP5);
  not not_186 (not_186_out, OP3);
  not not_187 (not_187_out, OP2);
  not not_188 (not_188_out, F14);
  not not_189 (not_189_out, F12);
  not not_190 (not_190_out, OP6);
  not not_191 (not_191_out, OP5);
  not not_192 (not_192_out, OP4);
  not not_193 (not_193_out, OP3);
  not not_194 (not_194_out, OP2);
  not not_195 (not_195_out, OP4);
  not not_196 (not_196_out, F14);
  not not_197 (not_197_out, F13);
  not not_198 (not_198_out, F12);
  not not_199 (not_199_out, OP4);
  not not_200 (not_200_out, OP3);
  not not_201 (not_201_out, F30);
  not not_202 (not_202_out, F25);
  not not_203 (not_203_out, F13);
  not not_204 (not_204_out, OP6);
  not not_205 (not_205_out, OP3);
  not not_206 (not_206_out, OP2);
  not not_207 (not_207_out, F14);
  not not_208 (not_208_out, OP6);
  not not_209 (not_209_out, OP5);
  not not_210 (not_210_out, OP3);
  not not_211 (not_211_out, OP2);
  not not_212 (not_212_out, OP6);
  not not_213 (not_213_out, OP3);
  not not_214 (not_214_out, F30);
  not not_215 (not_215_out, F25);
  not not_216 (not_216_out, F14);
  not not_217 (not_217_out, F13);
  not not_218 (not_218_out, OP6);
  not not_219 (not_219_out, OP3);
  not not_220 (not_220_out, OP2);
  not not_221 (not_221_out, F30);
  not not_222 (not_222_out, F25);
  not not_223 (not_223_out, F13);
  not not_224 (not_224_out, F12);
  not not_225 (not_225_out, OP6);
  not not_226 (not_226_out, OP3);
  not not_227 (not_227_out, OP2);
  not not_228 (not_228_out, F30);
  not not_229 (not_229_out, F25);
  not not_230 (not_230_out, F14);
  not not_231 (not_231_out, F13);
  not not_232 (not_232_out, F12);
  not not_233 (not_233_out, OP3);
  not not_234 (not_234_out, OP2);
  not not_235 (not_235_out, F14);
  not not_236 (not_236_out, F12);
  not not_237 (not_237_out, OP6);
  not not_238 (not_238_out, OP4);
  not not_239 (not_239_out, OP3);
  not not_240 (not_240_out, OP2);
  not not_241 (not_241_out, F14);
  not not_242 (not_242_out, F13);
  not not_243 (not_243_out, OP6);
  not not_244 (not_244_out, OP4);
  not not_245 (not_245_out, OP3);
  not not_246 (not_246_out, OP2);
  not not_247 (not_247_out, F14);
  not not_248 (not_248_out, F13);
  not not_249 (not_249_out, F12);
  not not_250 (not_250_out, OP4);
  not not_251 (not_251_out, OP3);
  not not_252 (not_252_out, OP2);
  not not_253 (not_253_out, F14);
  not not_254 (not_254_out, F13);
  not not_255 (not_255_out, OP4);
  not not_256 (not_256_out, OP3);
  not not_257 (not_257_out, OP2);
  not not_258 (not_258_out, F14);
  not not_259 (not_259_out, F13);
  not not_260 (not_260_out, F12);
  not not_261 (not_261_out, OP4);
  not not_262 (not_262_out, OP3);
  not not_263 (not_263_out, OP4);
  not not_264 (not_264_out, F30);
  not not_265 (not_265_out, F25);
  not not_266 (not_266_out, F13);
  not not_267 (not_267_out, OP6);
  not not_268 (not_268_out, OP3);
  not not_269 (not_269_out, OP2);
  not not_270 (not_270_out, F14);
  not not_271 (not_271_out, OP6);
  not not_272 (not_272_out, OP5);
  not not_273 (not_273_out, OP3);
  not not_274 (not_274_out, OP2);
  not not_275 (not_275_out, F14);
  not not_276 (not_276_out, F13);
  not not_277 (not_277_out, OP6);
  not not_278 (not_278_out, OP4);
  not not_279 (not_279_out, OP3);
  not not_280 (not_280_out, OP2);
  not not_281 (not_281_out, F13);
  not not_282 (not_282_out, OP4);
  not not_283 (not_283_out, OP3);
  not not_284 (not_284_out, OP2);
  not not_285 (not_285_out, F30);
  not not_286 (not_286_out, F25);
  not not_287 (not_287_out, F14);
  not not_288 (not_288_out, F13);
  not not_289 (not_289_out, F12);
  not not_290 (not_290_out, OP6);
  not not_291 (not_291_out, OP3);
  not not_292 (not_292_out, OP2);
  not not_293 (not_293_out, F25);
  not not_294 (not_294_out, F14);
  not not_295 (not_295_out, F13);
  not not_296 (not_296_out, F12);
  not not_297 (not_297_out, OP6);
  not not_298 (not_298_out, OP3);
  not not_299 (not_299_out, OP2);
  not not_300 (not_300_out, F30);
  not not_301 (not_301_out, F25);
  not not_302 (not_302_out, OP6);
  not not_303 (not_303_out, OP3);
  not not_304 (not_304_out, OP2);
  not not_305 (not_305_out, F30);
  not not_306 (not_306_out, F25);
  not not_307 (not_307_out, F12);
  not not_308 (not_308_out, OP6);
  not not_309 (not_309_out, OP3);
  not not_310 (not_310_out, OP2);
  not not_311 (not_311_out, F30);
  not not_312 (not_312_out, F25);
  not not_313 (not_313_out, F14);
  not not_314 (not_314_out, F12);
  not not_315 (not_315_out, OP6);
  not not_316 (not_316_out, OP3);
  not not_317 (not_317_out, OP2);
  not not_318 (not_318_out, F30);
  not not_319 (not_319_out, F25);
  not not_320 (not_320_out, F14);
  not not_321 (not_321_out, OP6);
  not not_322 (not_322_out, OP3);
  not not_323 (not_323_out, OP2);
  not not_324 (not_324_out, F14);
  not not_325 (not_325_out, F13);
  not not_326 (not_326_out, F12);
  not not_327 (not_327_out, OP6);
  not not_328 (not_328_out, OP5);
  not not_329 (not_329_out, OP3);
  not not_330 (not_330_out, OP2);
  not not_331 (not_331_out, OP6);
  not not_332 (not_332_out, OP5);
  not not_333 (not_333_out, OP3);
  not not_334 (not_334_out, OP2);
  not not_335 (not_335_out, F12);
  not not_336 (not_336_out, OP6);
  not not_337 (not_337_out, OP5);
  not not_338 (not_338_out, OP3);
  not not_339 (not_339_out, OP2);
  not not_340 (not_340_out, F13);
  not not_341 (not_341_out, F12);
  not not_342 (not_342_out, OP6);
  not not_343 (not_343_out, OP5);
  not not_344 (not_344_out, OP3);
  not not_345 (not_345_out, OP2);
  not not_346 (not_346_out, F14);
  not not_347 (not_347_out, F12);
  not not_348 (not_348_out, OP6);
  not not_349 (not_349_out, OP5);
  not not_350 (not_350_out, OP3);
  not not_351 (not_351_out, OP2);
  not not_352 (not_352_out, F30);
  not not_353 (not_353_out, F25);
  not not_354 (not_354_out, F14);
  not not_355 (not_355_out, F13);
  not not_356 (not_356_out, OP6);
  not not_357 (not_357_out, OP5);
  not not_358 (not_358_out, OP3);
  not not_359 (not_359_out, OP2);
  not not_360 (not_360_out, F30);
  not not_361 (not_361_out, F25);
  not not_362 (not_362_out, F13);
  not not_363 (not_363_out, OP6);
  not not_364 (not_364_out, OP5);
  not not_365 (not_365_out, OP3);
  not not_366 (not_366_out, OP2);
  not not_367 (not_367_out, F25);
  not not_368 (not_368_out, F13);
  not not_369 (not_369_out, OP6);
  not not_370 (not_370_out, OP5);
  not not_371 (not_371_out, OP3);
  not not_372 (not_372_out, OP2);
  not not_373 (not_373_out, F14);
  not not_374 (not_374_out, F12);
  not not_375 (not_375_out, OP6);
  not not_376 (not_376_out, OP5);
  not not_377 (not_377_out, OP4);
  not not_378 (not_378_out, OP3);
  not not_379 (not_379_out, OP2);
  not not_380 (not_380_out, F14);
  not not_381 (not_381_out, F12);
  not not_382 (not_382_out, OP6);
  not not_383 (not_383_out, OP4);
  not not_384 (not_384_out, OP3);
  not not_385 (not_385_out, OP2);
  not not_386 (not_386_out, F14);
  not not_387 (not_387_out, F13);
  not not_388 (not_388_out, F12);
  not not_389 (not_389_out, OP4);
  not not_390 (not_390_out, OP3);
  not not_391 (not_391_out, OP2);
  not not_392 (not_392_out, F14);
  not not_393 (not_393_out, F13);
  not not_394 (not_394_out, OP4);
  not not_395 (not_395_out, OP3);
  not not_396 (not_396_out, OP2);
  not not_397 (not_397_out, F14);
  not not_398 (not_398_out, F13);
  not not_399 (not_399_out, F12);
  not not_400 (not_400_out, OP4);
  not not_401 (not_401_out, OP3);
  not not_402 (not_402_out, F12);
  not not_403 (not_403_out, OP3);
  not not_404 (not_404_out, OP2);
  not not_405 (not_405_out, OP3);
  not not_406 (not_406_out, OP2);
  not not_407 (not_407_out, F30);
  not not_408 (not_408_out, F25);
  not not_409 (not_409_out, F13);
  not not_410 (not_410_out, OP6);
  not not_411 (not_411_out, OP3);
  not not_412 (not_412_out, OP2);
  not not_413 (not_413_out, F14);
  not not_414 (not_414_out, OP6);
  not not_415 (not_415_out, OP5);
  not not_416 (not_416_out, OP3);
  not not_417 (not_417_out, OP2);
  not not_418 (not_418_out, F14);
  not not_419 (not_419_out, F13);
  not not_420 (not_420_out, OP6);
  not not_421 (not_421_out, OP4);
  not not_422 (not_422_out, OP3);
  not not_423 (not_423_out, OP2);
  not not_424 (not_424_out, F13);
  not not_425 (not_425_out, OP4);
  not not_426 (not_426_out, OP3);
  not not_427 (not_427_out, OP2);
  not not_428 (not_428_out, F30);
  not not_429 (not_429_out, F25);
  not not_430 (not_430_out, F14);
  not not_431 (not_431_out, F13);
  not not_432 (not_432_out, OP6);
  not not_433 (not_433_out, OP3);
  not not_434 (not_434_out, OP2);
  not not_435 (not_435_out, F30);
  not not_436 (not_436_out, F25);
  not not_437 (not_437_out, F13);
  not not_438 (not_438_out, F12);
  not not_439 (not_439_out, OP6);
  not not_440 (not_440_out, OP3);
  not not_441 (not_441_out, OP2);
  not not_442 (not_442_out, F30);
  not not_443 (not_443_out, F25);
  not not_444 (not_444_out, F14);
  not not_445 (not_445_out, F13);
  not not_446 (not_446_out, F12);
  not not_447 (not_447_out, OP6);
  not not_448 (not_448_out, OP3);
  not not_449 (not_449_out, OP2);
  not not_450 (not_450_out, F25);
  not not_451 (not_451_out, F14);
  not not_452 (not_452_out, F13);
  not not_453 (not_453_out, F12);
  not not_454 (not_454_out, OP6);
  not not_455 (not_455_out, OP3);
  not not_456 (not_456_out, OP2);
  not not_457 (not_457_out, F30);
  not not_458 (not_458_out, F25);
  not not_459 (not_459_out, OP6);
  not not_460 (not_460_out, OP3);
  not not_461 (not_461_out, OP2);
  not not_462 (not_462_out, F30);
  not not_463 (not_463_out, F25);
  not not_464 (not_464_out, F12);
  not not_465 (not_465_out, OP6);
  not not_466 (not_466_out, OP3);
  not not_467 (not_467_out, OP2);
  not not_468 (not_468_out, F30);
  not not_469 (not_469_out, F25);
  not not_470 (not_470_out, F14);
  not not_471 (not_471_out, F12);
  not not_472 (not_472_out, OP6);
  not not_473 (not_473_out, OP3);
  not not_474 (not_474_out, OP2);
  not not_475 (not_475_out, F30);
  not not_476 (not_476_out, F25);
  not not_477 (not_477_out, F14);
  not not_478 (not_478_out, OP6);
  not not_479 (not_479_out, OP3);
  not not_480 (not_480_out, OP2);
  not not_481 (not_481_out, F14);
  not not_482 (not_482_out, F12);
  not not_483 (not_483_out, OP6);
  not not_484 (not_484_out, OP4);
  not not_485 (not_485_out, OP3);
  not not_486 (not_486_out, OP2);
  not not_487 (not_487_out, F14);
  not not_488 (not_488_out, F13);
  not not_489 (not_489_out, F12);
  not not_490 (not_490_out, OP4);
  not not_491 (not_491_out, OP3);
  not not_492 (not_492_out, OP2);
  not not_493 (not_493_out, F14);
  not not_494 (not_494_out, F13);
  not not_495 (not_495_out, OP4);
  not not_496 (not_496_out, OP3);
  not not_497 (not_497_out, OP2);
  not not_498 (not_498_out, F30);
  not not_499 (not_499_out, F25);
  not not_500 (not_500_out, F13);
  not not_501 (not_501_out, OP6);
  not not_502 (not_502_out, OP3);
  not not_503 (not_503_out, OP2);
  not not_504 (not_504_out, F14);
  not not_505 (not_505_out, F13);
  not not_506 (not_506_out, OP6);
  not not_507 (not_507_out, OP4);
  not not_508 (not_508_out, OP3);
  not not_509 (not_509_out, OP2);
  not not_510 (not_510_out, F13);
  not not_511 (not_511_out, OP4);
  not not_512 (not_512_out, OP3);
  not not_513 (not_513_out, OP2);
  not not_514 (not_514_out, F30);
  not not_515 (not_515_out, F25);
  not not_516 (not_516_out, F14);
  not not_517 (not_517_out, F13);
  not not_518 (not_518_out, OP6);
  not not_519 (not_519_out, OP3);
  not not_520 (not_520_out, OP2);
  not not_521 (not_521_out, F30);
  not not_522 (not_522_out, F25);
  not not_523 (not_523_out, F13);
  not not_524 (not_524_out, F12);
  not not_525 (not_525_out, OP6);
  not not_526 (not_526_out, OP3);
  not not_527 (not_527_out, OP2);
  not not_528 (not_528_out, F12);
  not not_529 (not_529_out, OP3);
  not not_530 (not_530_out, OP2);
  not not_531 (not_531_out, OP3);
  not not_532 (not_532_out, OP2);
  and and_1 (MemToReg, not_1_out, F13, not_2_out, not_3_out, not_4_out, not_5_out, not_6_out, not_7_out);
  and and_2 (and_2_out, not_8_out, F13, not_9_out, not_10_out, OP5, not_11_out, not_12_out, not_13_out);
  and and_3 (and_3_out, not_14_out, not_15_out, F12, not_16_out, OP5, not_17_out, not_18_out, not_19_out);
  and and_4 (LUI, not_20_out, OP5, OP4, not_21_out, OP2);
  and and_5 (and_5_out, not_22_out, not_23_out, not_24_out, not_25_out, not_26_out, OP4, not_27_out, not_28_out);
  and and_6 (and_6_out, F14, F13, F12, not_29_out, not_30_out, OP4, not_31_out, not_32_out);
  and and_7 (and_7_out, F14, F13, not_33_out, not_34_out, not_35_out, OP4, not_36_out, not_37_out);
  and and_8 (and_8_out, F14, not_38_out, not_39_out, not_40_out, not_41_out, OP4, not_42_out, not_43_out);
  and and_9 (and_9_out, not_44_out, F13, not_45_out, not_46_out, not_47_out, OP4, not_48_out, not_49_out);
  and and_10 (and_10_out, not_50_out, not_51_out, not_52_out, not_53_out, F12, not_54_out, not_55_out, OP4, not_56_out, not_57_out);
  and and_11 (and_11_out, not_58_out, not_59_out, F14, not_60_out, F12, not_61_out, not_62_out, OP4, not_63_out, not_64_out);
  and and_12 (and_12_out, F30, not_65_out, F14, not_66_out, F12, not_67_out, not_68_out, OP4, not_69_out, not_70_out);
  and and_13 (and_13_out, not_71_out, F13, not_72_out, not_73_out, not_74_out, not_75_out, not_76_out, not_77_out);
  and and_14 (and_14_out, not_78_out, F13, not_79_out, not_80_out, OP5, not_81_out, not_82_out, not_83_out);
  and and_15 (and_15_out, not_84_out, not_85_out, not_86_out, OP6, OP5, not_87_out, not_88_out, OP2);
  and and_16 (and_16_out, not_89_out, F13, F12, not_90_out, not_91_out, OP4, not_92_out, not_93_out);
  and and_17 (and_17_out, not_94_out, not_95_out, F12, not_96_out, OP5, not_97_out, not_98_out, not_99_out);
  and and_18 (and_18_out, not_100_out, not_101_out, not_102_out, not_103_out, not_104_out, not_105_out, OP5, OP4, not_106_out, not_107_out);
  and and_19 (and_19_out, F30, not_108_out, not_109_out, not_110_out, not_111_out, not_112_out, OP5, OP4, not_113_out, not_114_out);
  and and_20 (and_20_out, not_115_out, not_116_out, F14, F13, F12, not_117_out, OP5, OP4, not_118_out, not_119_out);
  and and_21 (and_21_out, not_120_out, not_121_out, F14, F13, not_122_out, not_123_out, OP5, OP4, not_124_out, not_125_out);
  and and_22 (and_22_out, not_126_out, not_127_out, not_128_out, F13, not_129_out, not_130_out, OP5, OP4, not_131_out, not_132_out);
  and and_23 (and_23_out, not_133_out, not_134_out, not_135_out, F13, F12, not_136_out, OP5, OP4, not_137_out, not_138_out);
  and and_24 (and_24_out, not_139_out, not_140_out, not_141_out, not_142_out, not_143_out, OP4, not_144_out, not_145_out);
  and and_25 (and_25_out, F14, F13, F12, not_146_out, not_147_out, OP4, not_148_out, not_149_out);
  and and_26 (and_26_out, F14, F13, not_150_out, not_151_out, not_152_out, OP4, not_153_out, not_154_out);
  and and_27 (and_27_out, F14, not_155_out, not_156_out, not_157_out, not_158_out, OP4, not_159_out, not_160_out);
  and and_28 (and_28_out, not_161_out, F13, not_162_out, not_163_out, not_164_out, OP4, not_165_out, not_166_out);
  and and_29 (and_29_out, not_167_out, not_168_out, not_169_out, not_170_out, F12, not_171_out, not_172_out, OP4, not_173_out, not_174_out);
  and and_30 (and_30_out, not_175_out, not_176_out, F14, not_177_out, F12, not_178_out, not_179_out, OP4, not_180_out, not_181_out);
  and and_31 (and_31_out, F30, not_182_out, F14, not_183_out, F12, not_184_out, not_185_out, OP4, not_186_out, not_187_out);
  and and_32 (and_32_out, not_188_out, F13, not_189_out, not_190_out, not_191_out, not_192_out, not_193_out, not_194_out);
  and and_33 (and_33_out, OP6, OP5, not_195_out, OP3, OP2);
  and and_34 (and_34_out, not_196_out, not_197_out, not_198_out, OP6, OP5, not_199_out, not_200_out, OP2);
  and and_35 (and_35_out, not_201_out, not_202_out, F14, not_203_out, F12, not_204_out, OP5, OP4, not_205_out, not_206_out);
  and and_36 (and_36_out, not_207_out, F13, F12, not_208_out, not_209_out, OP4, not_210_out, not_211_out);
  and and_37 (and_37_out, not_212_out, OP5, OP4, not_213_out, OP2);
  and and_38 (and_38_out, not_214_out, not_215_out, not_216_out, not_217_out, F12, not_218_out, OP5, OP4, not_219_out, not_220_out);
  and and_39 (and_39_out, not_221_out, not_222_out, F14, not_223_out, not_224_out, not_225_out, OP5, OP4, not_226_out, not_227_out);
  and and_40 (ecall, not_228_out, not_229_out, not_230_out, not_231_out, not_232_out, OP6, OP5, OP4, not_233_out, not_234_out);
  and and_41 (and_41_out, not_235_out, F13, not_236_out, not_237_out, OP5, not_238_out, not_239_out, not_240_out);
  and and_42 (and_42_out, not_241_out, not_242_out, F12, not_243_out, OP5, not_244_out, not_245_out, not_246_out);
  and and_43 (BEQ, not_247_out, not_248_out, not_249_out, OP6, OP5, not_250_out, not_251_out, not_252_out);
  and and_44 (BNE, not_253_out, not_254_out, F12, OP6, OP5, not_255_out, not_256_out, not_257_out);
  and and_45 (JALR, not_258_out, not_259_out, not_260_out, OP6, OP5, not_261_out, not_262_out, OP2);
  and and_46 (JAL, OP6, OP5, not_263_out, OP3, OP2);
  and and_47 (SRL, not_264_out, not_265_out, F14, not_266_out, F12, not_267_out, OP5, OP4, not_268_out, not_269_out);
  and and_48 (SLTIU, not_270_out, F13, F12, not_271_out, not_272_out, OP4, not_273_out, not_274_out);
  and and_49 (SH, not_275_out, not_276_out, F12, not_277_out, OP5, not_278_out, not_279_out, not_280_out);
  and and_50 (BGE, F14, not_281_out, F12, OP6, OP5, not_282_out, not_283_out, not_284_out);
  and and_51 (and_51_out, not_285_out, not_286_out, not_287_out, not_288_out, not_289_out, not_290_out, OP5, OP4, not_291_out, not_292_out);
  and and_52 (and_52_out, F30, not_293_out, not_294_out, not_295_out, not_296_out, not_297_out, OP5, OP4, not_298_out, not_299_out);
  and and_53 (and_53_out, not_300_out, not_301_out, F14, F13, F12, not_302_out, OP5, OP4, not_303_out, not_304_out);
  and and_54 (and_54_out, not_305_out, not_306_out, F14, F13, not_307_out, not_308_out, OP5, OP4, not_309_out, not_310_out);
  and and_55 (and_55_out, not_311_out, not_312_out, not_313_out, F13, not_314_out, not_315_out, OP5, OP4, not_316_out, not_317_out);
  and and_56 (and_56_out, not_318_out, not_319_out, not_320_out, F13, F12, not_321_out, OP5, OP4, not_322_out, not_323_out);
  and and_57 (and_57_out, not_324_out, not_325_out, not_326_out, not_327_out, not_328_out, OP4, not_329_out, not_330_out);
  and and_58 (and_58_out, F14, F13, F12, not_331_out, not_332_out, OP4, not_333_out, not_334_out);
  and and_59 (and_59_out, F14, F13, not_335_out, not_336_out, not_337_out, OP4, not_338_out, not_339_out);
  and and_60 (and_60_out, F14, not_340_out, not_341_out, not_342_out, not_343_out, OP4, not_344_out, not_345_out);
  and and_61 (and_61_out, not_346_out, F13, not_347_out, not_348_out, not_349_out, OP4, not_350_out, not_351_out);
  and and_62 (and_62_out, not_352_out, not_353_out, not_354_out, not_355_out, F12, not_356_out, not_357_out, OP4, not_358_out, not_359_out);
  and and_63 (and_63_out, not_360_out, not_361_out, F14, not_362_out, F12, not_363_out, not_364_out, OP4, not_365_out, not_366_out);
  and and_64 (and_64_out, F30, not_367_out, F14, not_368_out, F12, not_369_out, not_370_out, OP4, not_371_out, not_372_out);
  and and_65 (and_65_out, not_373_out, F13, not_374_out, not_375_out, not_376_out, not_377_out, not_378_out, not_379_out);
  and and_66 (and_66_out, not_380_out, F13, not_381_out, not_382_out, OP5, not_383_out, not_384_out, not_385_out);
  and and_67 (and_67_out, not_386_out, not_387_out, not_388_out, OP6, OP5, not_389_out, not_390_out, not_391_out);
  and and_68 (and_68_out, not_392_out, not_393_out, F12, OP6, OP5, not_394_out, not_395_out, not_396_out);
  and and_69 (and_69_out, not_397_out, not_398_out, not_399_out, OP6, OP5, not_400_out, not_401_out, OP2);
  and and_70 (and_70_out, F14, F13, not_402_out, OP6, OP5, OP4, not_403_out, not_404_out);
  and and_71 (and_71_out, F14, F13, F12, OP6, OP5, OP4, not_405_out, not_406_out);
  and and_72 (and_72_out, not_407_out, not_408_out, F14, not_409_out, F12, not_410_out, OP5, OP4, not_411_out, not_412_out);
  and and_73 (and_73_out, not_413_out, F13, F12, not_414_out, not_415_out, OP4, not_416_out, not_417_out);
  and and_74 (and_74_out, not_418_out, not_419_out, F12, not_420_out, OP5, not_421_out, not_422_out, not_423_out);
  and and_75 (and_75_out, F14, not_424_out, F12, OP6, OP5, not_425_out, not_426_out, not_427_out);
  and and_76 (and_76_out, not_428_out, not_429_out, not_430_out, not_431_out, F12, not_432_out, OP5, OP4, not_433_out, not_434_out);
  and and_77 (and_77_out, not_435_out, not_436_out, F14, not_437_out, not_438_out, not_439_out, OP5, OP4, not_440_out, not_441_out);
  and and_78 (and_78_out, not_442_out, not_443_out, not_444_out, not_445_out, not_446_out, not_447_out, OP5, OP4, not_448_out, not_449_out);
  and and_79 (and_79_out, F30, not_450_out, not_451_out, not_452_out, not_453_out, not_454_out, OP5, OP4, not_455_out, not_456_out);
  and and_80 (and_80_out, not_457_out, not_458_out, F14, F13, F12, not_459_out, OP5, OP4, not_460_out, not_461_out);
  and and_81 (and_81_out, not_462_out, not_463_out, F14, F13, not_464_out, not_465_out, OP5, OP4, not_466_out, not_467_out);
  and and_82 (and_82_out, not_468_out, not_469_out, not_470_out, F13, not_471_out, not_472_out, OP5, OP4, not_473_out, not_474_out);
  and and_83 (and_83_out, not_475_out, not_476_out, not_477_out, F13, F12, not_478_out, OP5, OP4, not_479_out, not_480_out);
  and and_84 (and_84_out, not_481_out, F13, not_482_out, not_483_out, OP5, not_484_out, not_485_out, not_486_out);
  and and_85 (and_85_out, not_487_out, not_488_out, not_489_out, OP6, OP5, not_490_out, not_491_out, not_492_out);
  and and_86 (and_86_out, not_493_out, not_494_out, F12, OP6, OP5, not_495_out, not_496_out, not_497_out);
  and and_87 (and_87_out, not_498_out, not_499_out, F14, not_500_out, F12, not_501_out, OP5, OP4, not_502_out, not_503_out);
  and and_88 (and_88_out, not_504_out, not_505_out, F12, not_506_out, OP5, not_507_out, not_508_out, not_509_out);
  and and_89 (and_89_out, F14, not_510_out, F12, OP6, OP5, not_511_out, not_512_out, not_513_out);
  and and_90 (and_90_out, not_514_out, not_515_out, not_516_out, not_517_out, F12, not_518_out, OP5, OP4, not_519_out, not_520_out);
  and and_91 (and_91_out, not_521_out, not_522_out, F14, not_523_out, not_524_out, not_525_out, OP5, OP4, not_526_out, not_527_out);
  and and_92 (CSRRSI, F14, F13, not_528_out, OP6, OP5, OP4, not_529_out, not_530_out);
  and and_93 (CSRRCI, F14, F13, F12, OP6, OP5, OP4, not_531_out, not_532_out);
  or or_1 (MemWrite, and_2_out, and_3_out);
  or or_2 (S_Type, and_41_out, and_42_out);
  or or_3 (ALU_SRC, and_5_out, and_6_out, and_7_out, and_8_out, and_9_out, and_10_out, and_11_out, and_12_out, and_13_out, and_14_out, and_15_out, and_16_out, and_17_out);
  or or_4 (rs2_used, and_78_out, and_79_out, and_80_out, and_81_out, and_82_out, and_83_out, and_84_out, and_85_out, and_86_out, and_87_out, and_88_out, and_89_out, and_90_out, and_91_out);
  or or_5 (RegWrite, and_18_out, and_19_out, and_20_out, and_21_out, and_22_out, and_23_out, and_24_out, and_25_out, and_26_out, and_27_out, and_28_out, and_29_out, and_30_out, and_31_out, and_32_out, and_33_out, and_34_out, and_35_out, and_36_out, and_37_out, and_38_out, and_39_out);
  or or_6 (rs1_used, and_51_out, and_52_out, and_53_out, and_54_out, and_55_out, and_56_out, and_57_out, and_58_out, and_59_out, and_60_out, and_61_out, and_62_out, and_63_out, and_64_out, and_65_out, and_66_out, and_67_out, and_68_out, and_69_out, and_70_out, and_71_out, and_72_out, and_73_out, and_74_out, and_75_out, and_76_out, and_77_out);
endmodule

// ALU
module ALU (
  input  [31:0] X,
  input  [31:0] Y,
  input  [3:0] AluOP,
  output out_4,
  output Equal,
  output out_6,
  output [31:0] Result,
  output [31:0] Result_2
);

  wire [0:0] comparator_1_lt, comparator_2_lt;
  wire [31:0] adder_1_out, AND_out, divider_1_out, divider_1_rem, multiplier_1_cout, multiplier_1_out,
       NOR_out, OR_out, shifter_1_out, shifter_2_out, shifter_3_out, subtractor_1_out, XOR_out;

  assign AND_out = X & Y;  // AND_Gate AND, 32 bits wide
  assign OR_out = X | Y;  // OR_Gate OR, 32 bits wide
  Shifter #(.width(32), .shift("ll")) shifter_1 (.in(X), .\dist (Y[4:0]), .out(shifter_1_out));
  Shifter #(.width(32), .shift("ar")) shifter_2 (.in(X), .\dist (Y[4:0]), .out(shifter_2_out));
  Shifter #(.width(32), .shift("lr")) shifter_3 (.in(X), .\dist (Y[4:0]), .out(shifter_3_out));
  Multiplier #(.width(32)) multiplier_1 (.a(X), .b(Y), .out(multiplier_1_out), .cout(multiplier_1_cout));  // open: cin
  Divider #(.width(32)) divider_1 (.a(X), .b(Y), .out(divider_1_out), .rem(divider_1_rem));  // open: upper
  Adder #(.width(32)) adder_1 (.a(X), .b(Y), .out(adder_1_out));  // open: cin, cout
  Subtractor #(.width(32)) subtractor_1 (.a(X), .b(Y), .out(subtractor_1_out));  // open: bin, bout
  assign XOR_out = X ^ Y;  // XOR_Gate XOR, 32 bits wide
  assign NOR_out = ~(X | Y);  // NOR_Gate NOR, 32 bits wide
  Comparator #(.width(32), .mode("twosComplement")) comparator_1 (
    .a(X), .b(Y), .eq(Equal), .lt(comparator_1_lt[0]));  // open: gt
  Comparator #(.width(32), .mode("unsigned")) comparator_2 (.a(X), .b(Y), .lt(comparator_2_lt[0]));  // open: gt, eq
  Multiplexer #(.select(4), .width(32), .disabled("Z"), .enable("false")) multiplexer_1 (
    .in0(shifter_1_out), .in1(shifter_2_out), .in2(shifter_3_out), .in3(multiplier_1_out),
    .in4(divider_1_out), .in5(adder_1_out), .in6(subtractor_1_out), .in7(AND_out), .in8(OR_out),
    .in9(XOR_out), .in10(NOR_out), .in11({{31{1'b0}}, comparator_1_lt[0]}),
    .in12({{31{1'b0}}, comparator_2_lt[0]}), .in13({32{1'b0}}), .in14({32{1'b0}}), .in15({32{1'b0}}),
    .out(Result), .sel(AluOP));
  Multiplexer #(.select(4), .width(32), .disabled("Z"), .enable("false")) multiplexer_2 (
    .in0({32{1'b0}}), .in1({32{1'b0}}), .in2({32{1'b0}}), .in3(multiplier_1_cout), .in4(divider_1_rem),
    .in5({32{1'b0}}), .in6({32{1'b0}}), .in7({32{1'b0}}), .in8({32{1'b0}}), .in9({32{1'b0}}),
    .in10({32{1'b0}}), .in11({32{1'b0}}), .in12({32{1'b0}}), .in13({32{1'b0}}), .in14({32{1'b0}}),
    .in15({32{1'b0}}), .out(Result_2), .sel(AluOP));
  Multiplexer #(.select(4), .width(1), .disabled("Z"), .enable("false")) multiplexer_3 (
    .in0(1'b0), .in1(1'b0), .in2(1'b0), .in3(1'b0), .in4(1'b0), .in5(1'b0), .in6(1'b0), .in7(1'b0),
    .in8(1'b0), .in9(1'b0), .in10(1'b0), .in11(comparator_1_lt[0]), .in12(comparator_2_lt[0]), .in13(1'b0),
    .in14(1'b0), .in15(1'b0), .out(out_6), .sel(AluOP));
  not not_1 (out_4, out_6);

  // Other names for the same wires on the sheet: Result2[31:0] = Result_2; S[3:0] = AluOP; tunnel = out_6;
  //   tunnel_t = out_4

  // Notes on the sheet:
  //   不要改变此引脚区域内容，也不要改变ALU封装形式
  //   输入引脚
  //   输出引脚
endmodule

module Regifile (
  input  [31:0] Din,
  input  Clk,
  input  WE,
  input  [4:0] R1_num,
  input  [4:0] W_num,
  input  [4:0] R2_num,
  output [31:0] R1,
  output [31:0] R2
);

  // RegisterFile registerfile_1: pin names not known; wires that end beside it: Din, Clk, WE, W_num, R1_num, R2_num, R1, R2
endmodule

module \点阵显示寄存器堆  (
  input  \写使能 ,
  input  [31:0] _1,
  input  [31:0] _2,
  input  [31:0] _3,
  input  [31:0] _4,
  input  [31:0] _5,
  input  [31:0] _6,
  input  [31:0] _7,
  input  [31:0] _8,
  input  [31:0] _9,
  input  [31:0] _10,
  input  [31:0] _11,
  input  [31:0] _12,
  input  [31:0] _13,
  input  [31:0] _14,
  input  [31:0] _15,
  input  [31:0] _16,
  input  [31:0] _17,
  input  [31:0] _18,
  input  [31:0] _19,
  input  [31:0] _20,
  input  [31:0] _21,
  input  [31:0] _22,
  input  [31:0] _23,
  input  [31:0] _24,
  input  [31:0] _25,
  input  [31:0] _26,
  input  [31:0] _27,
  input  [31:0] _28,
  input  [31:0] _29,
  input  [31:0] _30,
  input  [31:0] _31,
  input  [31:0] _32,
  input  CLK,
  input  RST,
  output [31:0] _1_2,
  output [31:0] _2_2,
  output [31:0] _3_2,
  output [31:0] _4_2,
  output [31:0] _5_2,
  output [31:0] _6_2,
  output [31:0] _7_2,
  output [31:0] _8_2,
  output [31:0] _9_2,
  output [31:0] _10_2,
  output [31:0] _11_2,
  output [31:0] _12_2,
  output [31:0] _13_2,
  output [31:0] _14_2,
  output [31:0] _15_2,
  output [31:0] _16_2,
  output [31:0] _17_2,
  output [31:0] _18_2,
  output [31:0] _19_2,
  output [31:0] _20_2,
  output [31:0] _21_2,
  output [31:0] _22_2,
  output [31:0] _23_2,
  output [31:0] _24_2,
  output [31:0] _25_2,
  output [31:0] _26_2,
  output [31:0] _27_2,
  output [31:0] _28_2,
  output [31:0] _29_2,
  output [31:0] _30_2,
  output [31:0] _31_2,
  output [31:0] _32_2
);

  Register #(.width(32), .trigger("rising"), .Select("low")) register_1 (
    .D(_1), .en(\写使能 ), .Q(_1_2), .clk(CLK), .clr(RST));
  Register #(.width(32), .trigger("rising"), .Select("low")) register_2 (
    .D(_5), .en(\写使能 ), .Q(_5_2), .clk(CLK), .clr(RST));
  Register #(.width(32), .trigger("rising"), .Select("low")) register_3 (
    .D(_9), .en(\写使能 ), .Q(_9_2), .clk(CLK), .clr(RST));
  Register #(.width(32), .trigger("rising"), .Select("low")) register_4 (
    .D(_13), .en(\写使能 ), .Q(_13_2), .clk(CLK), .clr(RST));
  Register #(.width(32), .trigger("rising"), .Select("low")) register_5 (
    .D(_17), .en(\写使能 ), .Q(_17_2), .clk(CLK), .clr(RST));
  Register #(.width(32), .trigger("rising"), .Select("low")) register_6 (
    .D(_21), .en(\写使能 ), .Q(_21_2), .clk(CLK), .clr(RST));
  Register #(.width(32), .trigger("rising"), .Select("low")) register_7 (
    .D(_25), .en(\写使能 ), .Q(_25_2), .clk(CLK), .clr(RST));
  Register #(.width(32), .trigger("rising"), .Select("low")) register_8 (
    .D(_29), .en(\写使能 ), .Q(_29_2), .clk(CLK), .clr(RST));
  Register #(.width(32), .trigger("rising"), .Select("low")) register_9 (
    .D(_2), .en(\写使能 ), .Q(_2_2), .clk(CLK), .clr(RST));
  Register #(.width(32), .trigger("rising"), .Select("low")) register_10 (
    .D(_6), .en(\写使能 ), .Q(_6_2), .clk(CLK), .clr(RST));
  Register #(.width(32), .trigger("rising"), .Select("low")) register_11 (
    .D(_10), .en(\写使能 ), .Q(_10_2), .clk(CLK), .clr(RST));
  Register #(.width(32), .trigger("rising"), .Select("low")) register_12 (
    .D(_14), .en(\写使能 ), .Q(_14_2), .clk(CLK), .clr(RST));
  Register #(.width(32), .trigger("rising"), .Select("low")) register_13 (
    .D(_18), .en(\写使能 ), .Q(_18_2), .clk(CLK), .clr(RST));
  Register #(.width(32), .trigger("rising"), .Select("low")) register_14 (
    .D(_22), .en(\写使能 ), .Q(_22_2), .clk(CLK), .clr(RST));
  Register #(.width(32), .trigger("rising"), .Select("low")) register_15 (
    .D(_26), .en(\写使能 ), .Q(_26_2), .clk(CLK), .clr(RST));
  Register #(.width(32), .trigger("rising"), .Select("low")) register_16 (
    .D(_30), .en(\写使能 ), .Q(_30_2), .clk(CLK), .clr(RST));
  Register #(.width(32), .trigger("rising"), .Select("low")) register_17 (
    .D(_3), .en(\写使能 ), .Q(_3_2), .clk(CLK), .clr(RST));
  Register #(.width(32), .trigger("rising"), .Select("low")) register_18 (
    .D(_7), .en(\写使能 ), .Q(_7_2), .clk(CLK), .clr(RST));
  Register #(.width(32), .trigger("rising"), .Select("low")) register_19 (
    .D(_11), .en(\写使能 ), .Q(_11_2), .clk(CLK), .clr(RST));
  Register #(.width(32), .trigger("rising"), .Select("low")) register_20 (
    .D(_15), .en(\写使能 ), .Q(_15_2), .clk(CLK), .clr(RST));
  Register #(.width(32), .trigger("rising"), .Select("low")) register_21 (
    .D(_19), .en(\写使能 ), .Q(_19_2), .clk(CLK), .clr(RST));
  Register #(.width(32), .trigger("rising"), .Select("low")) register_22 (
    .D(_23), .en(\写使能 ), .Q(_23_2), .clk(CLK), .clr(RST));
  Register #(.width(32), .trigger("rising"), .Select("low")) register_23 (
    .D(_27), .en(\写使能 ), .Q(_27_2), .clk(CLK), .clr(RST));
  Register #(.width(32), .trigger("rising"), .Select("low")) register_24 (
    .D(_31), .en(\写使能 ), .Q(_31_2), .clk(CLK), .clr(RST));
  Register #(.width(32), .trigger("rising"), .Select("low")) register_25 (
    .D(_4), .en(\写使能 ), .Q(_4_2), .clk(CLK), .clr(RST));
  Register #(.width(32), .trigger("rising"), .Select("low")) register_26 (
    .D(_8), .en(\写使能 ), .Q(_8_2), .clk(CLK), .clr(RST));
  Register #(.width(32), .trigger("rising"), .Select("low")) register_27 (
    .D(_12), .en(\写使能 ), .Q(_12_2), .clk(CLK), .clr(RST));
  Register #(.width(32), .trigger("rising"), .Select("low")) register_28 (
    .D(_16), .en(\写使能 ), .Q(_16_2), .clk(CLK), .clr(RST));
  Register #(.width(32), .trigger("rising"), .Select("low")) register_29 (
    .D(_20), .en(\写使能 ), .Q(_20_2), .clk(CLK), .clr(RST));
  Register #(.width(32), .trigger("rising"), .Select("low")) register_30 (
    .D(_24), .en(\写使能 ), .Q(_24_2), .clk(CLK), .clr(RST));
  Register #(.width(32), .trigger("rising"), .Select("low")) register_31 (
    .D(_28), .en(\写使能 ), .Q(_28_2), .clk(CLK), .clr(RST));
  Register #(.width(32), .trigger("rising"), .Select("low")) register_32 (
    .D(_32), .en(\写使能 ), .Q(_32_2), .clk(CLK), .clr(RST));
endmodule

module \地图备份寄存器堆  (
  input  \写使能 ,
  input  [9:0] Addr,
  input  CLK,
  input  RST,
  input  [31:0] Data,
  output [31:0] \行1 ,
  output [31:0] \行9 ,
  output [31:0] \行17 ,
  output [31:0] \行25 ,
  output [31:0] \行2 ,
  output [31:0] \行10 ,
  output [31:0] \行18 ,
  output [31:0] \行26 ,
  output [31:0] \行3 ,
  output [31:0] \行11 ,
  output [31:0] \行19 ,
  output [31:0] \行27 ,
  output [31:0] \行4 ,
  output [31:0] \行12 ,
  output [31:0] \行20 ,
  output [31:0] \行28 ,
  output [31:0] \行5 ,
  output [31:0] \行13 ,
  output [31:0] \行21 ,
  output [31:0] \行29 ,
  output [31:0] \行6 ,
  output [31:0] \行14 ,
  output [31:0] \行22 ,
  output [31:0] \行30 ,
  output [31:0] \行7 ,
  output [31:0] \行15 ,
  output [31:0] \行23 ,
  output [31:0] \行31 ,
  output [31:0] \行8 ,
  output [31:0] \行16 ,
  output [31:0] \行24 ,
  output [31:0] \行32 
);

  wire and_1_out, and_2_out, and_3_out, and_4_out, and_5_out, and_6_out, and_7_out, and_8_out, and_9_out,
       and_10_out, and_11_out, and_12_out, and_13_out, and_14_out, and_15_out, and_16_out, and_17_out,
       and_18_out, and_19_out, and_20_out, and_21_out, and_22_out, and_23_out, and_24_out, and_25_out,
       and_26_out, and_27_out, and_28_out, and_29_out, and_30_out, and_31_out, and_32_out, \行1_t , \行2_t ,
       \行3_t , \行4_t , \行5_t , \行6_t , \行7_t , \行8_t , \行9_t , \行10_t , \行11_t , \行12_t , \行13_t , \行14_t ,
       \行15_t , \行16_t , \行17_t , \行18_t , \行19_t , \行20_t , \行21_t , \行22_t , \行23_t , \行24_t , \行25_t ,
       \行26_t , \行27_t , \行28_t , \行29_t , \行30_t , \行31_t , \行32_t ;

  and and_1 (and_1_out, \写使能 , \行1_t );
  and and_2 (and_2_out, \写使能 , \行2_t );
  and and_3 (and_3_out, \写使能 , \行3_t );
  and and_4 (and_4_out, \写使能 , \行4_t );
  and and_5 (and_5_out, \写使能 , \行5_t );
  and and_6 (and_6_out, \写使能 , \行6_t );
  and and_7 (and_7_out, \写使能 , \行7_t );
  and and_8 (and_8_out, \写使能 , \行8_t );
  Register #(.width(32), .trigger("rising"), .Select("low")) register_1 (
    .D(Data), .en(and_1_out), .Q(\行1 ), .clk(CLK), .clr(RST));
  Register #(.width(32), .trigger("rising"), .Select("low")) register_2 (
    .D(Data), .en(and_2_out), .Q(\行2 ), .clk(CLK), .clr(RST));
  Register #(.width(32), .trigger("rising"), .Select("low")) register_3 (
    .D(Data), .en(and_3_out), .Q(\行3 ), .clk(CLK), .clr(RST));
  Register #(.width(32), .trigger("rising"), .Select("low")) register_4 (
    .D(Data), .en(and_4_out), .Q(\行4 ), .clk(CLK), .clr(RST));
  Register #(.width(32), .trigger("rising"), .Select("low")) register_5 (
    .D(Data), .en(and_5_out), .Q(\行5 ), .clk(CLK), .clr(RST));
  Register #(.width(32), .trigger("rising"), .Select("low")) register_6 (
    .D(Data), .en(and_6_out), .Q(\行6 ), .clk(CLK), .clr(RST));
  Register #(.width(32), .trigger("rising"), .Select("low")) register_7 (
    .D(Data), .en(and_7_out), .Q(\行7 ), .clk(CLK), .clr(RST));
  Register #(.width(32), .trigger("rising"), .Select("low")) register_8 (
    .D(Data), .en(and_8_out), .Q(\行8 ), .clk(CLK), .clr(RST));
  and and_9 (and_9_out, \写使能 , \行9_t );
  and and_10 (and_10_out, \写使能 , \行10_t );
  and and_11 (and_11_out, \写使能 , \行11_t );
  and and_12 (and_12_out, \写使能 , \行12_t );
  and and_13 (and_13_out, \写使能 , \行13_t );
  and and_14 (and_14_out, \写使能 , \行14_t );
  and and_15 (and_15_out, \写使能 , \行15_t );
  and and_16 (and_16_out, \写使能 , \行16_t );
  Register #(.width(32), .trigger("rising"), .Select("low")) register_9 (
    .D(Data), .en(and_9_out), .Q(\行9 ), .clk(CLK), .clr(RST));
  Register #(.width(32), .trigger("rising"), .Select("low")) register_10 (
    .D(Data), .en(and_10_out), .Q(\行10 ), .clk(CLK), .clr(RST));
  Register #(.width(32), .trigger("rising"), .Select("low")) register_11 (
    .D(Data), .en(and_11_out), .Q(\行11 ), .clk(CLK), .clr(RST));
  Register #(.width(32), .trigger("rising"), .Select("low")) register_12 (
    .D(Data), .en(and_12_out), .Q(\行12 ), .clk(CLK), .clr(RST));
  Register #(.width(32), .trigger("rising"), .Select("low")) register_13 (
    .D(Data), .en(and_13_out), .Q(\行13 ), .clk(CLK), .clr(RST));
  Register #(.width(32), .trigger("rising"), .Select("low")) register_14 (
    .D(Data), .en(and_14_out), .Q(\行14 ), .clk(CLK), .clr(RST));
  Register #(.width(32), .trigger("rising"), .Select("low")) register_15 (
    .D(Data), .en(and_15_out), .Q(\行15 ), .clk(CLK), .clr(RST));
  Register #(.width(32), .trigger("rising"), .Select("low")) register_16 (
    .D(Data), .en(and_16_out), .Q(\行16 ), .clk(CLK), .clr(RST));
  and and_17 (and_17_out, \写使能 , \行17_t );
  and and_18 (and_18_out, \写使能 , \行18_t );
  and and_19 (and_19_out, \写使能 , \行19_t );
  and and_20 (and_20_out, \写使能 , \行20_t );
  and and_21 (and_21_out, \写使能 , \行21_t );
  and and_22 (and_22_out, \写使能 , \行22_t );
  and and_23 (and_23_out, \写使能 , \行23_t );
  and and_24 (and_24_out, \写使能 , \行24_t );
  Register #(.width(32), .trigger("rising"), .Select("low")) register_17 (
    .D(Data), .en(and_17_out), .Q(\行17 ), .clk(CLK), .clr(RST));
  Register #(.width(32), .trigger("rising"), .Select("low")) register_18 (
    .D(Data), .en(and_18_out), .Q(\行18 ), .clk(CLK), .clr(RST));
  Register #(.width(32), .trigger("rising"), .Select("low")) register_19 (
    .D(Data), .en(and_19_out), .Q(\行19 ), .clk(CLK), .clr(RST));
  Register #(.width(32), .trigger("rising"), .Select("low")) register_20 (
    .D(Data), .en(and_20_out), .Q(\行20 ), .clk(CLK), .clr(RST));
  Register #(.width(32), .trigger("rising"), .Select("low")) register_21 (
    .D(Data), .en(and_21_out), .Q(\行21 ), .clk(CLK), .clr(RST));
  Register #(.width(32), .trigger("rising"), .Select("low")) register_22 (
    .D(Data), .en(and_22_out), .Q(\行22 ), .clk(CLK), .clr(RST));
  Register #(.width(32), .trigger("rising"), .Select("low")) register_23 (
    .D(Data), .en(and_23_out), .Q(\行23 ), .clk(CLK), .clr(RST));
  Register #(.width(32), .trigger("rising"), .Select("low")) register_24 (
    .D(Data), .en(and_24_out), .Q(\行24 ), .clk(CLK), .clr(RST));
  and and_25 (and_25_out, \写使能 , \行25_t );
  and and_26 (and_26_out, \写使能 , \行26_t );
  and and_27 (and_27_out, \写使能 , \行27_t );
  and and_28 (and_28_out, \写使能 , \行28_t );
  and and_29 (and_29_out, \写使能 , \行29_t );
  and and_30 (and_30_out, \写使能 , \行30_t );
  and and_31 (and_31_out, \写使能 , \行31_t );
  and and_32 (and_32_out, \写使能 , \行32_t );
  Register #(.width(32), .trigger("rising"), .Select("low")) register_25 (
    .D(Data), .en(and_25_out), .Q(\行25 ), .clk(CLK), .clr(RST));
  Register #(.width(32), .trigger("rising"), .Select("low")) register_26 (
    .D(Data), .en(and_26_out), .Q(\行26 ), .clk(CLK), .clr(RST));
  Register #(.width(32), .trigger("rising"), .Select("low")) register_27 (
    .D(Data), .en(and_27_out), .Q(\行27 ), .clk(CLK), .clr(RST));
  Register #(.width(32), .trigger("rising"), .Select("low")) register_28 (
    .D(Data), .en(and_28_out), .Q(\行28 ), .clk(CLK), .clr(RST));
  Register #(.width(32), .trigger("rising"), .Select("low")) register_29 (
    .D(Data), .en(and_29_out), .Q(\行29 ), .clk(CLK), .clr(RST));
  Register #(.width(32), .trigger("rising"), .Select("low")) register_30 (
    .D(Data), .en(and_30_out), .Q(\行30 ), .clk(CLK), .clr(RST));
  Register #(.width(32), .trigger("rising"), .Select("low")) register_31 (
    .D(Data), .en(and_31_out), .Q(\行31 ), .clk(CLK), .clr(RST));
  Register #(.width(32), .trigger("rising"), .Select("low")) register_32 (
    .D(Data), .en(and_32_out), .Q(\行32 ), .clk(CLK), .clr(RST));
  Demultiplexer #(.select(5), .width(1), .tristate("false"), .disabled("Z"), .enable("false")) demultiplexer_1 (
    .out0(\行1_t ), .out1(\行2_t ), .out2(\行3_t ), .out3(\行4_t ), .out4(\行5_t ), .out5(\行6_t ), .out6(\行7_t ),
    .out7(\行8_t ), .out8(\行9_t ), .out9(\行10_t ), .out10(\行11_t ), .out11(\行12_t ), .out12(\行13_t ),
    .out13(\行14_t ), .out14(\行15_t ), .out15(\行16_t ), .out16(\行17_t ), .out17(\行18_t ), .out18(\行19_t ),
    .out19(\行20_t ), .out20(\行21_t ), .out21(\行22_t ), .out22(\行23_t ), .out23(\行24_t ), .out24(\行25_t ),
    .out25(\行26_t ), .out26(\行27_t ), .out27(\行28_t ), .out28(\行29_t ), .out29(\行30_t ), .out30(\行31_t ),
    .out31(\行32_t ), .in(1'b1), .sel(Addr[4:0]));
endmodule

module \报警器  (
  input  [31:0] v0,
  input  ecall,
  input  CLK,
  input  RST,
  output Warning
);

  wire and_1_out, comparator_1_eq, register_1_q, register_2_q, register_3_q, register_4_q, register_5_q,
       register_6_q, register_7_q, register_8_q, register_9_q, register_10_q, register_11_q, register_12_q,
       register_13_q, register_14_q, register_15_q, register_16_q;

  Comparator #(.width(32), .mode("twosComplement")) comparator_1 (
    .a(v0), .b(32'h64), .eq(comparator_1_eq));  // open: gt, lt
  and and_1 (and_1_out, comparator_1_eq, ecall);
  Register #(.width(1), .trigger("rising"), .Select("low")) register_1 (
    .D(and_1_out), .Q(register_1_q), .clk(CLK), .clr(RST));  // open: en
  Register #(.width(1), .trigger("rising"), .Select("low")) register_2 (
    .D(register_1_q), .Q(register_2_q), .clk(CLK), .clr(RST));  // open: en
  Register #(.width(1), .trigger("rising"), .Select("low")) register_3 (
    .D(register_2_q), .Q(register_3_q), .clk(CLK), .clr(RST));  // open: en
  Register #(.width(1), .trigger("rising"), .Select("low")) register_4 (
    .D(register_3_q), .Q(register_4_q), .clk(CLK), .clr(RST));  // open: en
  Register #(.width(1), .trigger("rising"), .Select("low")) register_5 (
    .D(register_4_q), .Q(register_5_q), .clk(CLK), .clr(RST));  // open: en
  Register #(.width(1), .trigger("rising"), .Select("low")) register_6 (
    .D(register_5_q), .Q(register_6_q), .clk(CLK), .clr(RST));  // open: en
  Register #(.width(1), .trigger("rising"), .Select("low")) register_7 (
    .D(register_6_q), .Q(register_7_q), .clk(CLK), .clr(RST));  // open: en
  Register #(.width(1), .trigger("rising"), .Select("low")) register_8 (
    .D(register_7_q), .Q(register_8_q), .clk(CLK), .clr(RST));  // open: en
  Register #(.width(1), .trigger("rising"), .Select("low")) register_9 (
    .D(register_8_q), .Q(register_9_q), .clk(CLK), .clr(RST));  // open: en
  Register #(.width(1), .trigger("rising"), .Select("low")) register_10 (
    .D(register_9_q), .Q(register_10_q), .clk(CLK), .clr(RST));  // open: en
  Register #(.width(1), .trigger("rising"), .Select("low")) register_11 (
    .D(register_10_q), .Q(register_11_q), .clk(CLK), .clr(RST));  // open: en
  Register #(.width(1), .trigger("rising"), .Select("low")) register_12 (
    .D(register_11_q), .Q(register_12_q), .clk(CLK), .clr(RST));  // open: en
  Register #(.width(1), .trigger("rising"), .Select("low")) register_13 (
    .D(register_12_q), .Q(register_13_q), .clk(CLK), .clr(RST));  // open: en
  Register #(.width(1), .trigger("rising"), .Select("low")) register_14 (
    .D(register_13_q), .Q(register_14_q), .clk(CLK), .clr(RST));  // open: en
  Register #(.width(1), .trigger("rising"), .Select("low")) register_15 (
    .D(register_14_q), .Q(register_15_q), .clk(CLK), .clr(RST));  // open: en
  Register #(.width(1), .trigger("rising"), .Select("low")) register_16 (
    .D(register_15_q), .Q(register_16_q), .clk(CLK), .clr(RST));  // open: en
  or or_1 (Warning, register_1_q, register_2_q, register_3_q, register_4_q, register_5_q, register_6_q, register_7_q, register_8_q, register_9_q, register_10_q, register_11_q, register_12_q, register_13_q, register_14_q, register_15_q, register_16_q);
endmodule
module \地图点阵显示电路  (
  input  [31:0] a7,
  input  ecall,
  input  MemWrite,
  input  [9:0] ADDR,
  input  [31:0] MDin,
  input  CLK,
  input  RST,
  output [31:0] \行1 ,
  output [31:0] \行2 ,
  output [31:0] \行3 ,
  output [31:0] \行4 ,
  output [31:0] \行5 ,
  output [31:0] \行6 ,
  output [31:0] \行7 ,
  output [31:0] \行8 ,
  output [31:0] \行9 ,
  output [31:0] \行10 ,
  output [31:0] \行11 ,
  output [31:0] \行12 ,
  output [31:0] \行13 ,
  output [31:0] \行14 ,
  output [31:0] \行15 ,
  output [31:0] \行16 ,
  output [31:0] \行17 ,
  output [31:0] \行18 ,
  output [31:0] \行19 ,
  output [31:0] \行20 ,
  output [31:0] \行21 ,
  output [31:0] \行22 ,
  output [31:0] \行23 ,
  output [31:0] \行24 ,
  output [31:0] \行25 ,
  output [31:0] \行26 ,
  output [31:0] \行27 ,
  output [31:0] \行28 ,
  output [31:0] \行29 ,
  output [31:0] \行30 ,
  output [31:0] \行31 ,
  output [31:0] \行32 
);

  wire and_1_out, and_2_out, comparator_1_eq, comparator_2_gt;
  wire [31:0] \地图备份寄存器堆_1_行1 , \地图备份寄存器堆_1_行2 , \地图备份寄存器堆_1_行3 , \地图备份寄存器堆_1_行4 , \地图备份寄存器堆_1_行5 ,
       \地图备份寄存器堆_1_行6 , \地图备份寄存器堆_1_行7 , \地图备份寄存器堆_1_行8 , \地图备份寄存器堆_1_行9 , \地图备份寄存器堆_1_行10 ,
       \地图备份寄存器堆_1_行11 , \地图备份寄存器堆_1_行12 , \地图备份寄存器堆_1_行13 , \地图备份寄存器堆_1_行14 , \地图备份寄存器堆_1_行15 ,
       \地图备份寄存器堆_1_行16 , \地图备份寄存器堆_1_行17 , \地图备份寄存器堆_1_行18 , \地图备份寄存器堆_1_行19 , \地图备份寄存器堆_1_行20 ,
       \地图备份寄存器堆_1_行21 , \地图备份寄存器堆_1_行22 , \地图备份寄存器堆_1_行23 , \地图备份寄存器堆_1_行24 , \地图备份寄存器堆_1_行25 ,
       \地图备份寄存器堆_1_行26 , \地图备份寄存器堆_1_行27 , \地图备份寄存器堆_1_行28 , \地图备份寄存器堆_1_行29 , \地图备份寄存器堆_1_行30 ,
       \地图备份寄存器堆_1_行31 , \地图备份寄存器堆_1_行32 ;

  Comparator #(.width(32), .mode("twosComplement")) comparator_1 (
    .a(a7), .b(32'h22), .eq(comparator_1_eq));  // open: gt, lt
  and and_1 (and_1_out, MemWrite, comparator_2_gt);
  Comparator #(.width(10), .mode("twosComplement")) comparator_2 (
    .a(10'h20), .b(ADDR), .gt(comparator_2_gt));  // open: eq, lt
  and and_2 (and_2_out, comparator_1_eq, ecall);
  \地图备份寄存器堆  \u_地图备份寄存器堆_1  (
    .\写使能 (and_1_out), .Addr(ADDR), .CLK(CLK), .Data(MDin), .\行1 (\地图备份寄存器堆_1_行1 ), .\行9 (\地图备份寄存器堆_1_行9 ),
    .\行17 (\地图备份寄存器堆_1_行17 ), .\行25 (\地图备份寄存器堆_1_行25 ), .\行2 (\地图备份寄存器堆_1_行2 ), .\行10 (\地图备份寄存器堆_1_行10 ),
    .\行18 (\地图备份寄存器堆_1_行18 ), .\行26 (\地图备份寄存器堆_1_行26 ), .\行3 (\地图备份寄存器堆_1_行3 ), .\行11 (\地图备份寄存器堆_1_行11 ),
    .\行19 (\地图备份寄存器堆_1_行19 ), .\行27 (\地图备份寄存器堆_1_行27 ), .\行4 (\地图备份寄存器堆_1_行4 ), .\行12 (\地图备份寄存器堆_1_行12 ),
    .\行20 (\地图备份寄存器堆_1_行20 ), .\行28 (\地图备份寄存器堆_1_行28 ), .\行5 (\地图备份寄存器堆_1_行5 ), .\行13 (\地图备份寄存器堆_1_行13 ),
    .\行21 (\地图备份寄存器堆_1_行21 ), .\行29 (\地图备份寄存器堆_1_行29 ), .\行6 (\地图备份寄存器堆_1_行6 ), .\行14 (\地图备份寄存器堆_1_行14 ),
    .\行22 (\地图备份寄存器堆_1_行22 ), .\行30 (\地图备份寄存器堆_1_行30 ), .\行7 (\地图备份寄存器堆_1_行7 ), .\行15 (\地图备份寄存器堆_1_行15 ),
    .\行23 (\地图备份寄存器堆_1_行23 ), .\行31 (\地图备份寄存器堆_1_行31 ), .\行8 (\地图备份寄存器堆_1_行8 ), .\行16 (\地图备份寄存器堆_1_行16 ),
    .\行24 (\地图备份寄存器堆_1_行24 ), .\行32 (\地图备份寄存器堆_1_行32 ), .RST(RST));
  \点阵显示寄存器堆  \u_点阵显示寄存器堆_1  (
    .\写使能 (and_2_out), ._1(\地图备份寄存器堆_1_行1 ), ._2(\地图备份寄存器堆_1_行2 ), ._3(\地图备份寄存器堆_1_行3 ),
    ._4(\地图备份寄存器堆_1_行4 ), ._5(\地图备份寄存器堆_1_行5 ), ._6(\地图备份寄存器堆_1_行6 ), ._7(\地图备份寄存器堆_1_行7 ),
    ._8(\地图备份寄存器堆_1_行8 ), ._9(\地图备份寄存器堆_1_行9 ), ._10(\地图备份寄存器堆_1_行10 ), ._11(\地图备份寄存器堆_1_行11 ),
    ._12(\地图备份寄存器堆_1_行12 ), ._13(\地图备份寄存器堆_1_行13 ), ._14(\地图备份寄存器堆_1_行14 ), ._15(\地图备份寄存器堆_1_行15 ),
    ._16(\地图备份寄存器堆_1_行16 ), ._17(\地图备份寄存器堆_1_行17 ), ._18(\地图备份寄存器堆_1_行18 ), ._19(\地图备份寄存器堆_1_行19 ),
    ._20(\地图备份寄存器堆_1_行20 ), ._21(\地图备份寄存器堆_1_行21 ), ._22(\地图备份寄存器堆_1_行22 ), ._23(\地图备份寄存器堆_1_行23 ),
    ._24(\地图备份寄存器堆_1_行24 ), ._25(\地图备份寄存器堆_1_行25 ), ._26(\地图备份寄存器堆_1_行26 ), ._27(\地图备份寄存器堆_1_行27 ),
    ._28(\地图备份寄存器堆_1_行28 ), ._29(\地图备份寄存器堆_1_行29 ), ._30(\地图备份寄存器堆_1_行30 ), ._31(\地图备份寄存器堆_1_行31 ),
    ._32(\地图备份寄存器堆_1_行32 ), .CLK(CLK), ._1_2(\行1 ), ._2_2(\行2 ), ._3_2(\行3 ), ._4_2(\行4 ), ._5_2(\行5 ),
    ._6_2(\行6 ), ._7_2(\行7 ), ._8_2(\行8 ), ._9_2(\行9 ), ._10_2(\行10 ), ._11_2(\行11 ), ._12_2(\行12 ),
    ._13_2(\行13 ), ._14_2(\行14 ), ._15_2(\行15 ), ._16_2(\行16 ), ._17_2(\行17 ), ._18_2(\行18 ), ._19_2(\行19 ),
    ._20_2(\行20 ), ._21_2(\行21 ), ._22_2(\行22 ), ._23_2(\行23 ), ._24_2(\行24 ), ._25_2(\行25 ), ._26_2(\行26 ),
    ._27_2(\行27 ), ._28_2(\行28 ), ._29_2(\行29 ), ._30_2(\行30 ), ._31_2(\行31 ), ._32_2(\行32 ), .RST(RST));
endmodule

module \判断通关电路  (
  input  [31:0] RDin,
  input  [4:0] W_num,
  input  RegWrite,
  input  CLK,
  input  RST,
  output Success
);

  wire and_1_out, comparator_1_eq;
  wire [31:1] s3_q;

  Comparator #(.width(5), .mode("unsigned")) comparator_1 (
    .a(W_num), .b(5'b11100), .eq(comparator_1_eq));  // open: gt, lt
  and and_1 (and_1_out, comparator_1_eq, RegWrite);
  Register #(.width(32), .trigger("rising"), .Select("low")) s3 (
    .D(RDin), .en(and_1_out), .Q({s3_q, Success}), .clk(CLK), .clr(RST));
endmodule

module \键盘解析电路  (
  input  [6:0] \键盘输入 ,
  input  CLK,
  input  RST,
  output UP_W,
  output Down_S,
  output Left_A,
  output Right_D,
  output Rst_2,
  output easy,
  output hard
);

  wire comparator_1_eq, comparator_2_eq, comparator_3_eq, comparator_4_eq, comparator_5_eq, comparator_6_eq,
       comparator_7_eq;

  Comparator #(.width(7), .mode("twosComplement")) comparator_1 (
    .a(\键盘输入 ), .b(7'b1110111), .eq(comparator_1_eq));  // open: gt, lt
  Comparator #(.width(7), .mode("twosComplement")) comparator_2 (
    .a(\键盘输入 ), .b(7'b1110011), .eq(comparator_2_eq));  // open: gt, lt
  Comparator #(.width(7), .mode("twosComplement")) comparator_3 (
    .a(\键盘输入 ), .b(7'b1100001), .eq(comparator_3_eq));  // open: gt, lt
  Comparator #(.width(7), .mode("twosComplement")) comparator_4 (
    .a(\键盘输入 ), .b(7'b1100100), .eq(comparator_4_eq));  // open: gt, lt
  Comparator #(.width(7), .mode("twosComplement")) comparator_5 (
    .a(\键盘输入 ), .b(7'b1110010), .eq(comparator_5_eq));  // open: gt, lt
  Comparator #(.width(7), .mode("twosComplement")) comparator_6 (
    .a(\键盘输入 ), .b(7'b1100101), .eq(comparator_6_eq));  // open: gt, lt
  Comparator #(.width(7), .mode("twosComplement")) comparator_7 (
    .a(\键盘输入 ), .b(7'b1101000), .eq(comparator_7_eq));  // open: gt, lt
  Register #(.width(1), .trigger("rising"), .Select("low")) register_1 (
    .D(comparator_1_eq), .Q(UP_W), .clk(CLK), .clr(RST));  // open: en
  Register #(.width(1), .trigger("rising"), .Select("low")) register_2 (
    .D(comparator_2_eq), .Q(Down_S), .clk(CLK), .clr(RST));  // open: en
  Register #(.width(1), .trigger("rising"), .Select("low")) register_3 (
    .D(comparator_3_eq), .Q(Left_A), .clk(CLK), .clr(RST));  // open: en
  Register #(.width(1), .trigger("rising"), .Select("low")) register_4 (
    .D(comparator_4_eq), .Q(Right_D), .clk(CLK), .clr(RST));  // open: en
  Register #(.width(1), .trigger("rising"), .Select("low")) register_5 (
    .D(comparator_5_eq), .Q(Rst_2), .clk(CLK), .clr(RST));  // open: en
  Register #(.width(1), .trigger("rising"), .Select("low")) register_6 (
    .D(comparator_6_eq), .Q(easy), .clk(CLK), .clr(RST));  // open: en
  Register #(.width(1), .trigger("rising"), .Select("low")) register_7 (
    .D(comparator_7_eq), .Q(hard), .clk(CLK), .clr(RST));  // open: en
endmodule

module \频率转换器  (
  input  [15:0] \延缓倍数 ,
  input  \原CLK ,
  input  RST,
  output \后CLK 
);

  wire comparator_1_eq, comparator_2_eq, comparator_2_gt, or_1_out;
  wire [15:0] counter_1_q, shifter_1_out;

  Shifter #(.width(16), .shift("lr")) shifter_1 (.in(\延缓倍数 ), .\dist (4'b0001), .out(shifter_1_out));
  Counter #(.width(16), .max('hffff), .ongoal("wrap"), .trigger("rising"), .behavior("new")) counter_1 (
    .load(comparator_1_eq), .D({16{1'b0}}), .Q(counter_1_q), .clk(\原CLK ), .clr(RST));  // open: count, carry, preset, down
  Comparator #(.width(16), .mode("unsigned")) comparator_1 (
    .a(\延缓倍数 ), .b(counter_1_q), .eq(comparator_1_eq));  // open: gt, lt
  Comparator #(.width(16), .mode("unsigned")) comparator_2 (
    .a(shifter_1_out), .b(counter_1_q), .gt(comparator_2_gt), .eq(comparator_2_eq));  // open: lt
  or or_1 (or_1_out, comparator_2_gt, comparator_2_eq);
  Multiplexer #(.select(1), .width(1), .disabled("Z"), .enable("false")) multiplexer_1 (
    .in0(1'b1), .in1(1'b0), .out(\后CLK ), .sel(or_1_out));
endmodule

module \游戏界面  (
);

  wire A, CLK, D, Easy, Hard, RST, S, Success, W, Warning, \单周期risc_v_1_ecall , \单周期risc_v_1_memwrite ,
       \单周期risc_v_1_regwrite ;
  wire [4:0] \单周期risc_v_1_w_num ;
  wire [6:0] keyboard_1_data;
  wire [9:0] \单周期risc_v_1_addr ;
  wire [31:0] \单周期risc_v_1_mdin , \单周期risc_v_1_rdin , \单周期risc_v_1_v0 , \地图点阵显示电路_1_行1 , \地图点阵显示电路_1_行2 ,
       \地图点阵显示电路_1_行3 , \地图点阵显示电路_1_行4 , \地图点阵显示电路_1_行5 , \地图点阵显示电路_1_行6 , \地图点阵显示电路_1_行7 , \地图点阵显示电路_1_行8 ,
       \地图点阵显示电路_1_行9 , \地图点阵显示电路_1_行10 , \地图点阵显示电路_1_行11 , \地图点阵显示电路_1_行12 , \地图点阵显示电路_1_行13 ,
       \地图点阵显示电路_1_行14 , \地图点阵显示电路_1_行15 , \地图点阵显示电路_1_行16 , \地图点阵显示电路_1_行17 , \地图点阵显示电路_1_行18 ,
       \地图点阵显示电路_1_行19 , \地图点阵显示电路_1_行20 , \地图点阵显示电路_1_行21 , \地图点阵显示电路_1_行22 , \地图点阵显示电路_1_行23 ,
       \地图点阵显示电路_1_行24 , \地图点阵显示电路_1_行25 , \地图点阵显示电路_1_行26 , \地图点阵显示电路_1_行27 , \地图点阵显示电路_1_行28 ,
       \地图点阵显示电路_1_行29 , \地图点阵显示电路_1_行30 , \地图点阵显示电路_1_行31 , \地图点阵显示电路_1_行32 ;

  \单周期RISC_V  \u_单周期risc_v_1  (
    .IR1(W), .IR2(S), .IR3(A), .IR4(D), .IR5(Easy), .IR6(Hard), .RST(RST), .CLK(CLK),
    .ecall(\单周期risc_v_1_ecall ), .v0(\单周期risc_v_1_v0 ), .ADDR(\单周期risc_v_1_addr ), .MDin(\单周期risc_v_1_mdin ),
    .W_num(\单周期risc_v_1_w_num ), .MemWrite(\单周期risc_v_1_memwrite ), .RegWrite(\单周期risc_v_1_regwrite ),
    .RDin(\单周期risc_v_1_rdin ));
  Clock #(.highDuration(1), .lowDuration(1)) u_CLK (.out(CLK));
  \地图点阵显示电路  \u_地图点阵显示电路_1  (
    .a7(\单周期risc_v_1_v0 ), .ecall(\单周期risc_v_1_ecall ), .MemWrite(\单周期risc_v_1_memwrite ),
    .ADDR(\单周期risc_v_1_addr ), .MDin(\单周期risc_v_1_mdin ), .CLK(CLK), .RST(RST), .\行1 (\地图点阵显示电路_1_行1 ),
    .\行2 (\地图点阵显示电路_1_行2 ), .\行3 (\地图点阵显示电路_1_行3 ), .\行4 (\地图点阵显示电路_1_行4 ), .\行5 (\地图点阵显示电路_1_行5 ),
    .\行6 (\地图点阵显示电路_1_行6 ), .\行7 (\地图点阵显示电路_1_行7 ), .\行8 (\地图点阵显示电路_1_行8 ), .\行9 (\地图点阵显示电路_1_行9 ),
    .\行10 (\地图点阵显示电路_1_行10 ), .\行11 (\地图点阵显示电路_1_行11 ), .\行12 (\地图点阵显示电路_1_行12 ), .\行13 (\地图点阵显示电路_1_行13 ),
    .\行14 (\地图点阵显示电路_1_行14 ), .\行15 (\地图点阵显示电路_1_行15 ), .\行16 (\地图点阵显示电路_1_行16 ), .\行17 (\地图点阵显示电路_1_行17 ),
    .\行18 (\地图点阵显示电路_1_行18 ), .\行19 (\地图点阵显示电路_1_行19 ), .\行20 (\地图点阵显示电路_1_行20 ), .\行21 (\地图点阵显示电路_1_行21 ),
    .\行22 (\地图点阵显示电路_1_行22 ), .\行23 (\地图点阵显示电路_1_行23 ), .\行24 (\地图点阵显示电路_1_行24 ), .\行25 (\地图点阵显示电路_1_行25 ),
    .\行26 (\地图点阵显示电路_1_行26 ), .\行27 (\地图点阵显示电路_1_行27 ), .\行28 (\地图点阵显示电路_1_行28 ), .\行29 (\地图点阵显示电路_1_行29 ),
    .\行30 (\地图点阵显示电路_1_行30 ), .\行31 (\地图点阵显示电路_1_行31 ), .\行32 (\地图点阵显示电路_1_行32 ));
  \判断通关电路  \u_判断通关电路_1  (
    .RDin(\单周期risc_v_1_rdin ), .W_num(\单周期risc_v_1_w_num ), .RegWrite(\单周期risc_v_1_regwrite ), .CLK(CLK),
    .RST(RST), .Success(Success));
  \报警器  \u_报警器_1  (.v0(\单周期risc_v_1_v0 ), .ecall(\单周期risc_v_1_ecall ), .CLK(CLK), .RST(RST), .Warning(Warning));
  DotMatrix #(.inputtype("row"), .matrixcols(32), .matrixrows(32), .persist(0), .dotshape("square")) dotmatrix_1 (
    .row0(\地图点阵显示电路_1_行1 ), .row1(\地图点阵显示电路_1_行2 ), .row2(\地图点阵显示电路_1_行3 ), .row3(\地图点阵显示电路_1_行4 ),
    .row4(\地图点阵显示电路_1_行5 ), .row5(\地图点阵显示电路_1_行6 ), .row6(\地图点阵显示电路_1_行7 ), .row7(\地图点阵显示电路_1_行8 ),
    .row8(\地图点阵显示电路_1_行9 ), .row9(\地图点阵显示电路_1_行10 ), .row10(\地图点阵显示电路_1_行11 ), .row11(\地图点阵显示电路_1_行12 ),
    .row12(\地图点阵显示电路_1_行13 ), .row13(\地图点阵显示电路_1_行14 ), .row14(\地图点阵显示电路_1_行15 ), .row15(\地图点阵显示电路_1_行16 ),
    .row16(\地图点阵显示电路_1_行17 ), .row17(\地图点阵显示电路_1_行18 ), .row18(\地图点阵显示电路_1_行19 ), .row19(\地图点阵显示电路_1_行20 ),
    .row20(\地图点阵显示电路_1_行21 ), .row21(\地图点阵显示电路_1_行22 ), .row22(\地图点阵显示电路_1_行23 ), .row23(\地图点阵显示电路_1_行24 ),
    .row24(\地图点阵显示电路_1_行25 ), .row25(\地图点阵显示电路_1_行26 ), .row26(\地图点阵显示电路_1_行27 ), .row27(\地图点阵显示电路_1_行28 ),
    .row28(\地图点阵显示电路_1_行29 ), .row29(\地图点阵显示电路_1_行30 ), .row30(\地图点阵显示电路_1_行31 ), .row31(\地图点阵显示电路_1_行32 ));
  Keyboard #(.Char_bit_width(7), .buflen(32), .trigger("rising")) keyboard_1 (
    .clk(CLK), .re(1'b1), .clr(RST), .data(keyboard_1_data));  // open: avail
  \键盘解析电路  \u_键盘解析电路_1  (
    .UP_W(W), .Down_S(S), .Left_A(A), .Right_D(D), .\键盘输入 (keyboard_1_data), .CLK(CLK), .RST(RST),
    .Rst_2(RST), .easy(Easy), .hard(Hard));
  LED #(.active("true")) led_1 (.in(Warning));
  // Buzzer #(.freq_measure("Hz"), .vol_width(1)) 警告: pin names not known; wires that end beside it: 14'hfff, Warning, Warning

  // Notes on the sheet:
  //   click here!
endmodule

module \音乐播放器  (
  input  [15:0] \频率延缓倍数 ,
  input  CLK,
  input  play,
  input  RST,
  output [13:0] out_5,
  output Enable,
  output \音量 ,
  output [13:0] out_8
);

  wire Now_CLK;
  wire [31:0] adder_1_out, PC_q;
  wire [31:14] \主_data , \伴奏_data ;

  Register #(.width(32), .trigger("rising"), .Select("low")) PC (
    .D(adder_1_out), .en(play), .Q(PC_q), .clk(Now_CLK), .clr(RST));
  \频率转换器  \u_频率转换器_1  (.\延缓倍数 (\频率延缓倍数 ), .\原CLK (CLK), .RST(RST), .\后CLK (Now_CLK));
  Adder #(.width(32)) adder_1 (.a(PC_q), .b(32'h4), .out(adder_1_out), .cout(RST));  // open: cin
  ROM #(.addrWidth(10), .dataWidth(32), .Select("high")) \u_主  (.addr(PC_q[11:2]), .data({\主_data , out_5}));
  ROM #(.addrWidth(10), .dataWidth(32), .Select("high")) \u_伴奏  (.addr(PC_q[11:2]), .data({\伴奏_data , out_8}));

  assign Enable = play;
  assign \音量  = play;

  // Notes on the sheet:
  //   建议频率:转换后：16Hz
  //   contents of 主 (hex, n*v repeats v):
  //   20b 20b 20b 0 20b 20b 20b 0 310 310 310 0 310 310 310 0 370 370 370 0 370 370 370 0 310 310 310 5*0
  //   2ba 2ba 2ba 0 2ba 2ba 2ba 0 293 293 293 0 293 293 293 0 24b 24b 24b 0 24b 24b 24b 0 20b 20b 20b 5*0
  //   310 310 310 0 310 310 310 0 2ba 2ba 2ba 0 2ba 2ba 2ba 0 293 293 293 0 293 293 293 0 24b 24b 24b 5*0
  //   310 310 310 0 310 310 310 0 2ba 2ba 2ba 0 2ba 2ba 2ba 0 293 293 293 0 293 293 293 0 24b 24b 24b 5*0
  //   20b 20b 20b 0 20b 20b 20b 0 310 310 310 0 310 310 310 0 370 370 370 0 370 370 370 0 310 310 310 5*0
  //   2ba 2ba 2ba 0 2ba 2ba 2ba 0 293 293 293 0 293 293 293 0 24b 24b 24b 0 24b 24b 24b 0 20b 20b 20b
  //   contents of 伴奏 (hex, n*v repeats v):
  //   106 106 188 188 14a 14a 188 188 106 106 188 188 14a 14a 188 188 106 106 1b8 1b8 15d 15d 1b8 1b8 106
  //   106 188 188 14a 14a 188 188 e9 e9 188 188 126 126 188 188 106 106 188 188 14a 14a 188 188 e9 e9 188
  //   188 126 126 188 188 106 106 188 188 14a 14a 188 188 106 106 188 188 14a 14a 188 188 e9 e9 188 188
  //   126 126 188 188 106 106 188 188 14a 14a 188 188 e9 e9 188 188 126 126 188 188 106 106 188 188 14a
  //   14a 188 188 e9 e9 188 188 126 126 188 188 106 106 188 188 14a 14a 188 188 e9 e9 188 188 126 126 188
  //   188 106 106 188 188 14a 14a 188 188 106 106 188 188 14a 14a 188 188 106 106 1b8 1b8 15d 15d 1b8 1b8
  //   106 106 188 188 14a 14a 188 188 e9 e9 188 188 126 126 188 188 106 106 188 188 14a 14a 188 188 e9 e9
  //   188 188 126 126 188 188 106 106 188 188 14a 14a 188 188
  //   小星星变奏曲-前奏
endmodule
